// Logisim project dhb-cpu24-2-29-版本1.circ as structural Verilog: 24 circuits, main circuit ◇单周期MIPS
module \单周期MIPS  (
  input  IR1,
  input  IR2,
  input  IR3,
  output RegWrite,
  output MemWrite,
  output [31:0] PC,
  output [31:0] IR,
  output [31:0] RDin,
  output [31:0] MDin,
  output [31:0] LedData
);

  wire and_1_out, and_2_out, and_3_out, CLK, display, Go, IR1_t, IR2_t, IR3_t, IRA, IRB, IRC,
       mips_alu_1_equal, not_1_out, not_2_out, not_3_out, not_4_out, not_5_out, not_6_out, SB, SignedExt,
       Stop, VAR, W1, W2, W3, \单周期硬布线控制器_1_alu_src , \单周期硬布线控制器_1_beq , \单周期硬布线控制器_1_bltz ,
       \单周期硬布线控制器_1_bne , \单周期硬布线控制器_1_jal , \单周期硬布线控制器_1_jr , \单周期硬布线控制器_1_memtoreg , \单周期硬布线控制器_1_regdst ,
       \单周期硬布线控制器_1_syscall ;
  wire [1:0] \单周期硬布线控制器_1_jmp ;
  wire [3:0] adder_1_out_2, \单周期硬布线控制器_1_alu_op ;
  wire [4:0] mips_regifile_1_r1, multiplexer_3_out, multiplexer_4_out, multiplexer_5_out, multiplexer_6_out,
       multiplexer_10_out;
  wire [7:0] mips_regifile_1_r2;
  wire [15:0] \总周期数 ;
  wire [27:0] adder_1_out;
  wire [31:0] adder_2_out, adder_3_out, bit_extender_1_out, bit_extender_2_out, controlled_buffer_1_out,
       mips_alu_1_result, multiplexer_1_out, multiplexer_2_out, multiplexer_8_out, multiplexer_9_out,
       multiplexer_12_out, ram_1_data, sb_1_out_4, shifter_1_out;
  wire [31:5] mips_regifile_1_r1_2;
  wire [31:8] mips_regifile_1_r2_2;

  Clock #(.highDuration(1), .lowDuration(1)) clock_1 (.out(CLK));
  Button _1 (.out(IRA));
  Button _2 (.out(IRB));
  Button _3 (.out(IRC));
  not not_1 (not_1_out, \单周期硬布线控制器_1_jr );
  Multiplexer #(.select(1), .width(32), .disabled("Z"), .enable("false")) multiplexer_1 (
    .in0({mips_regifile_1_r1_2, mips_regifile_1_r1}), .in1({adder_1_out_2, IR[25:0], 2'b00}),
    .out(multiplexer_1_out), .sel(not_1_out));
  Button \u_继续运行  (.out(Go));
  LED #(.active("true")) led_1 (.in(W1));
  LED #(.active("true")) led_2 (.in(W2));
  LED #(.active("true")) led_3 (.in(W3));
  Multiplexer #(.select(2), .width(32), .disabled("Z"), .enable("false")) multiplexer_2 (
    .in0({adder_1_out_2, adder_1_out}), .in1(multiplexer_1_out), .in2(adder_3_out), .out(multiplexer_2_out),
    .sel(\单周期硬布线控制器_1_jmp ));  // open: in3
  not not_2 (not_2_out, Stop);
  Hex_Digit_Display hex_digit_display_1 (.value(LedData[31:28]));  // open: dp
  Register #(.width(32), .trigger("rising"), .Select("low")) u_PC (
    .D(multiplexer_2_out), .en(not_2_out), .Q(PC), .clk(CLK));  // open: clr
  Hex_Digit_Display hex_digit_display_2 (.value(LedData[23:20]));  // open: dp
  Hex_Digit_Display hex_digit_display_3 (.value(LedData[27:24]));  // open: dp
  Adder #(.width(32)) adder_1 (.a(PC), .b(32'h4), .out({adder_1_out_2, adder_1_out}));  // open: cin, cout
  Hex_Digit_Display hex_digit_display_4 (.value(LedData[15:12]));  // open: dp
  Hex_Digit_Display hex_digit_display_5 (.value(LedData[19:16]));  // open: dp
  not not_3 (not_3_out, Stop);
  Counter #(.width(16), .max('hffff), .ongoal("stay"), .trigger("rising"), .behavior("new")) counter_1 (
    .count(not_3_out), .Q(\总周期数 ), .clk(CLK));  // open: load, D, carry, clr, preset, down
  Hex_Digit_Display hex_digit_display_6 (.value(LedData[7:4]));  // open: dp
  Hex_Digit_Display hex_digit_display_7 (.value(LedData[11:8]));  // open: dp
  // Probe on \总周期数 
  ROM #(.addrWidth(10), .dataWidth(32), .Select("high")) rom_1 (.addr(PC[11:2]), .data(IR));
  Hex_Digit_Display hex_digit_display_8 (.value(LedData[3:0]));  // open: dp
  \单周期硬布线控制器  \u_单周期硬布线控制器_1  (
    .Func(IR[5:0]), .OP(IR[31:26]), .ALU_OP(\单周期硬布线控制器_1_alu_op ), .MemToReg(\单周期硬布线控制器_1_memtoreg ),
    .MemWrite(MemWrite), .ALU_SRC(\单周期硬布线控制器_1_alu_src ), .RegWrite(RegWrite),
    .SysCALL(\单周期硬布线控制器_1_syscall ), .SignedExt(SignedExt), .RegDst(\单周期硬布线控制器_1_regdst ),
    .JR(\单周期硬布线控制器_1_jr ), .JMP(\单周期硬布线控制器_1_jmp [0]), .Beq(\单周期硬布线控制器_1_beq ), .JAL(\单周期硬布线控制器_1_jal ),
    .Bne(\单周期硬布线控制器_1_bne ), .SB(SB), .BLTZ(\单周期硬布线控制器_1_bltz ), .VAR(VAR));  // open: ERET, MT_MF, MFC0, MTC0
  Multiplexer #(.select(1), .width(5), .disabled("Z"), .enable("false")) multiplexer_3 (
    .in0(IR[25:21]), .in1(5'b00010), .out(multiplexer_3_out), .sel(\单周期硬布线控制器_1_syscall ));
  Multiplexer #(.select(1), .width(5), .disabled("Z"), .enable("false")) multiplexer_4 (
    .in0(IR[20:16]), .in1(5'b00100), .out(multiplexer_4_out), .sel(\单周期硬布线控制器_1_syscall ));
  or or_1 (IR1_t, IR1, IRA);
  Multiplexer #(.select(1), .width(5), .disabled("Z"), .enable("false")) multiplexer_5 (
    .in0(multiplexer_4_out), .in1(IR[15:11]), .out(multiplexer_5_out), .sel(\单周期硬布线控制器_1_regdst ));
  Adder #(.width(32)) adder_2 (.a(PC), .b(32'h4), .out(adder_2_out));  // open: cin, cout
  or or_2 (IR2_t, IR2, IRB);
  Multiplexer #(.select(1), .width(5), .disabled("Z"), .enable("false")) multiplexer_6 (
    .in0(multiplexer_5_out), .in1({5{1'b1}}), .out(multiplexer_6_out), .sel(\单周期硬布线控制器_1_jal ));
  Multiplexer #(.select(1), .width(32), .disabled("Z"), .enable("false")) multiplexer_7 (
    .in0(multiplexer_12_out), .in1(adder_2_out), .out(RDin), .sel(\单周期硬布线控制器_1_jal ));
  MIPS_Regifile mips_regifile_1 (
    .Din(RDin), .Clk(CLK), .R1({mips_regifile_1_r1_2, mips_regifile_1_r1}),
    .R2({mips_regifile_1_r2_2, mips_regifile_1_r2}), .WE(RegWrite), .W_num(multiplexer_6_out),
    .R1_num(multiplexer_3_out), .R2_num(multiplexer_4_out));
  or or_3 (IR3_t, IR3, IRC);
  assign controlled_buffer_1_out = display ? {mips_regifile_1_r2_2, mips_regifile_1_r2} : 32'bz;  // Controlled_Buffer controlled_buffer_1
  assign bit_extender_1_out = {{16{1'b0}}, IR[15:0]};  // Bit_Extender bit_extender_1
  assign bit_extender_2_out = {{16{IR[15]}}, IR[15:0]};  // Bit_Extender bit_extender_2
  not not_4 (not_4_out, display);
  Comparator #(.width(32), .mode("twosComplement")) comparator_1 (
    .a(32'h22), .b({mips_regifile_1_r1_2, mips_regifile_1_r1}), .eq(display));  // open: gt, lt
  Register #(.width(32), .trigger("rising"), .Select("low")) register_1 (
    .D(controlled_buffer_1_out), .Q(LedData), .clk(CLK));  // open: en, clr
  Multiplexer #(.select(1), .width(32), .disabled("Z"), .enable("false")) multiplexer_8 (
    .in0(bit_extender_1_out), .in1(bit_extender_2_out), .out(multiplexer_8_out), .sel(SignedExt));
  Shifter #(.width(32), .shift("ll")) shifter_1 (.in(bit_extender_2_out), .\dist (5'b00010), .out(shifter_1_out));
  or or_4 (\单周期硬布线控制器_1_jmp [1], and_3_out, and_2_out, and_1_out);
  D_Flip_Flop #(.trigger("rising"), .Pre_Clr_Positions("ABOVE_BELOW"), .NegatePresetClear("false"), .enable("true"), .NewFFLayout("true")) d_ff_1 (
    .clk(CLK), .D(not_4_out), .Q(Stop), .en(\单周期硬布线控制器_1_syscall ), .reset(Go));  // open: Qn, preset
  Multiplexer #(.select(1), .width(32), .disabled("Z"), .enable("false")) multiplexer_9 (
    .in0({mips_regifile_1_r2_2, mips_regifile_1_r2}), .in1(multiplexer_8_out), .out(multiplexer_9_out),
    .sel(\单周期硬布线控制器_1_alu_src ));
  Adder #(.width(32)) adder_3 (
    .a(shifter_1_out), .b({adder_1_out_2, adder_1_out}), .out(adder_3_out));  // open: cin, cout
  and and_1 (and_1_out, \单周期硬布线控制器_1_beq , mips_alu_1_equal);
  Multiplexer #(.select(1), .width(5), .disabled("Z"), .enable("false")) multiplexer_10 (
    .in0(IR[10:6]), .in1(mips_regifile_1_r1), .out(multiplexer_10_out), .sel(VAR));
  and and_2 (and_2_out, \单周期硬布线控制器_1_bltz , mips_alu_1_result[0]);
  and and_3 (and_3_out, \单周期硬布线控制器_1_bne , not_5_out);
  not not_5 (not_5_out, mips_alu_1_equal);
  MIPS_ALU mips_alu_1 (
    .X({mips_regifile_1_r1_2, mips_regifile_1_r1}), .Y(multiplexer_9_out), .AluOP(\单周期硬布线控制器_1_alu_op ),
    .Equal(mips_alu_1_equal), .Result(mips_alu_1_result), .shamt(multiplexer_10_out));  // open: Result_2
  SB sb_1 (.\原数据 (ram_1_data), .addr(mips_alu_1_result[1:0]), .data(mips_regifile_1_r2), .out_4(sb_1_out_4));
  not not_6 (not_6_out, SB);
  RAM #(.addrWidth(10), .dataWidth(32), .bus("separate"), .Select("high")) ram_1 (
    .addr(mips_alu_1_result[11:2]), .din(MDin), .data(ram_1_data), .str(MemWrite), .clk(CLK));  // open: sel, ld, clr
  Multiplexer #(.select(1), .width(32), .disabled("Z"), .enable("false")) multiplexer_11 (
    .in0(sb_1_out_4), .in1({mips_regifile_1_r2_2, mips_regifile_1_r2}), .out(MDin), .sel(not_6_out));
  Multiplexer #(.select(1), .width(32), .disabled("Z"), .enable("false")) multiplexer_12 (
    .in0(mips_alu_1_result), .in1(ram_1_data), .out(multiplexer_12_out), .sel(\单周期硬布线控制器_1_memtoreg ));

  // Notes on the sheet:
  //   中断源
  //   PC = R[rs]
  //   中断等待指示
  //   总复位信号应将除ROM以外所有存储组件全部清零
  //   PC = JumpAddr
  //   数码管输出
  //   指令存储器
  //   Address
  //   数码管输出应该用寄存器锁存，否则显示数据只能一闪而过
  //   指令字
  //   contents of rom_1 (hex, n*v repeats v):
  //   20110001 8000c05 20110001 20120002 20130003 8000c09 20110001 20120002 20130003 8000c0d 20110001
  //   20120002 20130003 8000c11 20110001 20120002 20130003 c000cb8 20100001 20110001 118fc0 112020
  //   20020022 c 118882 12200001 8000c15 112020 20020022 c 20110001 118880 112020 20020022 c 12200001
  //   8000c1f 20110001 118fc0 112020 20020022 c 1188c3 112020 20020022 c 118903 112020 20020022 c 118903
  //   112020 20020022 c 118903 112020 20020022 c 118903 112020 20020022 c 118903 112020 20020022 c 118903
  //   112020 20020022 c 118903 112020 20020022 c 20100001 109fc0 139fc3 8021 2012000c 24160003 26100001
  //   3210000f 20080008 20090001 139900 2709825 132020 20020022 c 1094022 1500fff9 22100001 2018000f
  //   2188024 108700 20080008 20090001 139902 2709825 132021 20020022 c 1094022 1500fff9 108702 2c9b022
  //   12c00001 8000c50 4020 1084027 84400 3508ffff 82021 20020022 c 2010ffff 20110000 ae300000 22100001
  //   22310004 ae300000 22100001 22310004 ae300000 22100001 22310004 ae300000 22100001 22310004 ae300000
  //   22100001 22310004 ae300000 22100001 22310004 ae300000 22100001 22310004 ae300000 22100001 22310004
  //   ae300000 22100001 22310004 ae300000 22100001 22310004 ae300000 22100001 22310004 ae300000 22100001
  //   22310004 ae300000 22100001 22310004 ae300000 22100001 22310004 ae300000 22100001 22310004 ae300000
  //   22100001 22310004 22100001 8020 2011003c 8e130000 8e340000 274402a 11000002 ae330000 ae140000
  //   2231fffc 1611fff8 102020 20020022 c 22100004 2011003c 1611fff2 20020032 c 20100000 22100001 102020
  //   20020022 c 22100002 102020 20020022 c 22100003 102020 20020022 c 22100004 102020 20020022 c 22100005
  //   102020 20020022 c 22100006 102020 20020022 c 22100007 102020 20020022 c 22100008 102020 20020022
  //   20020022 c 3e00008
  //   OP
  //   Func
  //   rs
  //   rt
  //   rd
  //   imm
  //   shmat
  //   BLTZ
  //   JMP
  //   Beq
  //   JR
  //   Bne
  //   OP
  //   JAL
  //   Func
  //   Syscall
  //   $v0
  //   $a0
  //   MemToReg
  //   MemWrite
  //   AluOP
  //   AluSrcB
  //   RegWrite
  //   RegDst
  //   为方便自动评测，需要输出PC，IR，寄存器堆写如数据RDin
  //   RAM写使能MemWrite、RAM写入数据MDin等信号
endmodule

// 单周期硬布线控制器
module \单周期硬布线控制器  (
  input  [5:0] OP,
  input  [5:0] Func,
  input  [4:0] MT_MF,
  output [3:0] ALU_OP,
  output MemToReg,
  output MemWrite,
  output ALU_SRC,
  output RegWrite,
  output SysCALL,
  output SignedExt,
  output RegDst,
  output Beq,
  output Bne,
  output JR,
  output JMP,
  output JAL,
  output SB,
  output BLTZ,
  output VAR,
  output ERET,
  output MFC0,
  output MTC0
);

  \运算控制器自动生成  \u_运算控制器自动生成_1  (
    .OP0(OP[0]), .OP1(OP[1]), .OP2(OP[2]), .OP3(OP[3]), .OP4(OP[4]), .OP5(OP[5]), .F0(Func[0]), .F1(Func[1]),
    .F2(Func[2]), .F3(Func[3]), .F4(Func[4]), .F5(Func[5]), .S0(ALU_OP[0]), .S1(ALU_OP[1]), .S2(ALU_OP[2]),
    .S3(ALU_OP[3]));
  \控制信号自动生成  \u_控制信号自动生成_1  (
    .OP0(OP[0]), .OP1(OP[1]), .OP2(OP[2]), .OP3(OP[3]), .OP4(OP[4]), .OP5(OP[5]), .F0(Func[0]), .F1(Func[1]),
    .F2(Func[2]), .F3(Func[3]), .F4(Func[4]), .F5(Func[5]), .MT_MF(MT_MF), .MemToReg(MemToReg),
    .MemWrite(MemWrite), .ALU_SRC(ALU_SRC), .RegWrite(RegWrite), .SysCALL(SysCALL), .SignedExt(SignedExt),
    .RegDst(RegDst), .BEQ(Beq), .BNE(Bne), .JR(JR), .JUMP(JMP), .JAL(JAL), .SB(SB), .BLTZ(BLTZ),
    .VARIABLE(VAR), .ERET(ERET), .MFC0(MFC0), .MTC0(MTC0));

  // Other names for the same wires on the sheet: OP_CODE[5:0] = OP

  // Notes on the sheet:
  //   运算器控制器，根据指令生成运算器功能选择信号
  //   控制信号生成，产生数据通路需要的其他控制信号
endmodule

// 运算器控制器
module \运算控制器自动生成  (
  input  OP0,
  input  OP1,
  input  OP2,
  input  OP3,
  input  OP4,
  input  OP5,
  input  F0,
  input  F1,
  input  F2,
  input  F3,
  input  F4,
  input  F5,
  output S0,
  output S1,
  output S2,
  output S3
);

  wire and_1_out, and_2_out, and_3_out, and_4_out, and_5_out, and_6_out, and_7_out, and_8_out, and_9_out,
       and_10_out, and_11_out, and_12_out, and_13_out, and_14_out, and_15_out, and_16_out, and_17_out,
       and_18_out, and_19_out, and_20_out, and_21_out, and_22_out, and_23_out, and_24_out, and_25_out,
       and_26_out, and_27_out, and_28_out, and_29_out, and_30_out, and_31_out, and_32_out, and_33_out,
       and_34_out, and_35_out, and_36_out, and_37_out, and_38_out, and_39_out, and_40_out, and_41_out,
       and_42_out, and_43_out, not_1_out, not_2_out, not_3_out, not_4_out, not_5_out, not_6_out, not_7_out,
       not_8_out, not_9_out, not_10_out, not_11_out, not_12_out, not_13_out, not_14_out, not_15_out,
       not_16_out, not_17_out, not_18_out, not_19_out, not_20_out, not_21_out, not_22_out, not_23_out,
       not_24_out, not_25_out, not_26_out, not_27_out, not_28_out, not_29_out, not_30_out, not_31_out,
       not_32_out, not_33_out, not_34_out, not_35_out, not_36_out, not_37_out, not_38_out, not_39_out,
       not_40_out, not_41_out, not_42_out, not_43_out, not_44_out, not_45_out, not_46_out, not_47_out,
       not_48_out, not_49_out, not_50_out, not_51_out, not_52_out, not_53_out, not_54_out, not_55_out,
       not_56_out, not_57_out, not_58_out, not_59_out, not_60_out, not_61_out, not_62_out, not_63_out,
       not_64_out, not_65_out, not_66_out, not_67_out, not_68_out, not_69_out, not_70_out, not_71_out,
       not_72_out, not_73_out, not_74_out, not_75_out, not_76_out, not_77_out, not_78_out, not_79_out,
       not_80_out, not_81_out, not_82_out, not_83_out, not_84_out, not_85_out, not_86_out, not_87_out,
       not_88_out, not_89_out, not_90_out, not_91_out, not_92_out, not_93_out, not_94_out, not_95_out,
       not_96_out, not_97_out, not_98_out, not_99_out, not_100_out, not_101_out, not_102_out, not_103_out,
       not_104_out, not_105_out, not_106_out, not_107_out, not_108_out, not_109_out, not_110_out,
       not_111_out, not_112_out, not_113_out, not_114_out, not_115_out, not_116_out, not_117_out,
       not_118_out, not_119_out, not_120_out, not_121_out, not_122_out, not_123_out, not_124_out,
       not_125_out, not_126_out, not_127_out, not_128_out, not_129_out, not_130_out, not_131_out,
       not_132_out, not_133_out, not_134_out, not_135_out, not_136_out, not_137_out, not_138_out,
       not_139_out, not_140_out, not_141_out, not_142_out, not_143_out, not_144_out, not_145_out,
       not_146_out, not_147_out, not_148_out, not_149_out, not_150_out, not_151_out, not_152_out,
       not_153_out, not_154_out, not_155_out, not_156_out, not_157_out, not_158_out, not_159_out,
       not_160_out, not_161_out, not_162_out, not_163_out, not_164_out, not_165_out, not_166_out,
       not_167_out, not_168_out, not_169_out, not_170_out, not_171_out, not_172_out, not_173_out,
       not_174_out, not_175_out, not_176_out, not_177_out, not_178_out, not_179_out, not_180_out,
       not_181_out, not_182_out, not_183_out, not_184_out, not_185_out, not_186_out, not_187_out,
       not_188_out, not_189_out, not_190_out, not_191_out, not_192_out, not_193_out, not_194_out,
       not_195_out, not_196_out, not_197_out, not_198_out, not_199_out, not_200_out, not_201_out,
       not_202_out, not_203_out, not_204_out, not_205_out, not_206_out, not_207_out, not_208_out,
       not_209_out, not_210_out, not_211_out, not_212_out, not_213_out, not_214_out, not_215_out,
       not_216_out, not_217_out, not_218_out, not_219_out, not_220_out, not_221_out, not_222_out,
       not_223_out, not_224_out, not_225_out, not_226_out, not_227_out, not_228_out, not_229_out,
       not_230_out, not_231_out, not_232_out, not_233_out, not_234_out, not_235_out, not_236_out,
       not_237_out, not_238_out, not_239_out, not_240_out, not_241_out, not_242_out, not_243_out,
       not_244_out, not_245_out, not_246_out, not_247_out, not_248_out, not_249_out, not_250_out,
       not_251_out, not_252_out, not_253_out, not_254_out, not_255_out, not_256_out, not_257_out,
       not_258_out, not_259_out, not_260_out, not_261_out, not_262_out, not_263_out, not_264_out,
       not_265_out, not_266_out, not_267_out, not_268_out, not_269_out, not_270_out, not_271_out,
       not_272_out, not_273_out, not_274_out, not_275_out, not_276_out, not_277_out, not_278_out,
       not_279_out, not_280_out, not_281_out, not_282_out, not_283_out, not_284_out, not_285_out, not_286_out;

  not not_1 (not_1_out, OP5);
  not not_2 (not_2_out, OP4);
  not not_3 (not_3_out, OP3);
  not not_4 (not_4_out, OP2);
  not not_5 (not_5_out, OP1);
  not not_6 (not_6_out, OP0);
  not not_7 (not_7_out, F5);
  not not_8 (not_8_out, F4);
  not not_9 (not_9_out, F3);
  not not_10 (not_10_out, F2);
  not not_11 (not_11_out, OP5);
  not not_12 (not_12_out, OP4);
  not not_13 (not_13_out, OP3);
  not not_14 (not_14_out, OP2);
  not not_15 (not_15_out, OP1);
  not not_16 (not_16_out, OP0);
  not not_17 (not_17_out, F4);
  not not_18 (not_18_out, F3);
  not not_19 (not_19_out, F2);
  not not_20 (not_20_out, F1);
  not not_21 (not_21_out, F0);
  not not_22 (not_22_out, OP5);
  not not_23 (not_23_out, OP4);
  not not_24 (not_24_out, OP3);
  not not_25 (not_25_out, OP2);
  not not_26 (not_26_out, OP1);
  not not_27 (not_27_out, OP0);
  not not_28 (not_28_out, F4);
  not not_29 (not_29_out, F3);
  not not_30 (not_30_out, F2);
  not not_31 (not_31_out, F1);
  not not_32 (not_32_out, OP5);
  not not_33 (not_33_out, OP4);
  not not_34 (not_34_out, OP3);
  not not_35 (not_35_out, OP2);
  not not_36 (not_36_out, OP1);
  not not_37 (not_37_out, OP0);
  not not_38 (not_38_out, F4);
  not not_39 (not_39_out, F3);
  not not_40 (not_40_out, F1);
  not not_41 (not_41_out, F0);
  not not_42 (not_42_out, OP5);
  not not_43 (not_43_out, OP4);
  not not_44 (not_44_out, OP3);
  not not_45 (not_45_out, OP2);
  not not_46 (not_46_out, OP1);
  not not_47 (not_47_out, OP0);
  not not_48 (not_48_out, F4);
  not not_49 (not_49_out, F2);
  not not_50 (not_50_out, F0);
  not not_51 (not_51_out, OP5);
  not not_52 (not_52_out, OP4);
  not not_53 (not_53_out, OP3);
  not not_54 (not_54_out, OP2);
  not not_55 (not_55_out, OP5);
  not not_56 (not_56_out, OP4);
  not not_57 (not_57_out, OP2);
  not not_58 (not_58_out, OP1);
  not not_59 (not_59_out, OP0);
  not not_60 (not_60_out, OP5);
  not not_61 (not_61_out, OP4);
  not not_62 (not_62_out, OP1);
  not not_63 (not_63_out, OP0);
  not not_64 (not_64_out, OP5);
  not not_65 (not_65_out, OP4);
  not not_66 (not_66_out, OP2);
  not not_67 (not_67_out, OP1);
  not not_68 (not_68_out, OP5);
  not not_69 (not_69_out, OP4);
  not not_70 (not_70_out, OP2);
  not not_71 (not_71_out, OP0);
  not not_72 (not_72_out, OP4);
  not not_73 (not_73_out, OP3);
  not not_74 (not_74_out, OP2);
  not not_75 (not_75_out, OP4);
  not not_76 (not_76_out, OP2);
  not not_77 (not_77_out, OP5);
  not not_78 (not_78_out, OP4);
  not not_79 (not_79_out, OP3);
  not not_80 (not_80_out, OP2);
  not not_81 (not_81_out, OP1);
  not not_82 (not_82_out, OP0);
  not not_83 (not_83_out, F5);
  not not_84 (not_84_out, F4);
  not not_85 (not_85_out, F3);
  not not_86 (not_86_out, OP4);
  not not_87 (not_87_out, OP2);
  not not_88 (not_88_out, OP1);
  not not_89 (not_89_out, OP0);
  not not_90 (not_90_out, OP5);
  not not_91 (not_91_out, OP4);
  not not_92 (not_92_out, OP3);
  not not_93 (not_93_out, OP2);
  not not_94 (not_94_out, OP1);
  not not_95 (not_95_out, OP5);
  not not_96 (not_96_out, OP4);
  not not_97 (not_97_out, OP3);
  not not_98 (not_98_out, OP2);
  not not_99 (not_99_out, OP1);
  not not_100 (not_100_out, OP0);
  not not_101 (not_101_out, F5);
  not not_102 (not_102_out, F4);
  not not_103 (not_103_out, F3);
  not not_104 (not_104_out, F2);
  not not_105 (not_105_out, F0);
  not not_106 (not_106_out, OP5);
  not not_107 (not_107_out, OP4);
  not not_108 (not_108_out, OP3);
  not not_109 (not_109_out, OP2);
  not not_110 (not_110_out, OP1);
  not not_111 (not_111_out, OP0);
  not not_112 (not_112_out, F4);
  not not_113 (not_113_out, F3);
  not not_114 (not_114_out, F2);
  not not_115 (not_115_out, F0);
  not not_116 (not_116_out, OP5);
  not not_117 (not_117_out, OP4);
  not not_118 (not_118_out, OP3);
  not not_119 (not_119_out, OP2);
  not not_120 (not_120_out, OP1);
  not not_121 (not_121_out, OP0);
  not not_122 (not_122_out, F4);
  not not_123 (not_123_out, F3);
  not not_124 (not_124_out, F1);
  not not_125 (not_125_out, F0);
  not not_126 (not_126_out, OP5);
  not not_127 (not_127_out, OP4);
  not not_128 (not_128_out, OP3);
  not not_129 (not_129_out, OP2);
  not not_130 (not_130_out, OP1);
  not not_131 (not_131_out, OP0);
  not not_132 (not_132_out, F4);
  not not_133 (not_133_out, F3);
  not not_134 (not_134_out, OP5);
  not not_135 (not_135_out, OP4);
  not not_136 (not_136_out, OP3);
  not not_137 (not_137_out, OP2);
  not not_138 (not_138_out, OP1);
  not not_139 (not_139_out, OP0);
  not not_140 (not_140_out, F4);
  not not_141 (not_141_out, F2);
  not not_142 (not_142_out, F0);
  not not_143 (not_143_out, OP5);
  not not_144 (not_144_out, OP4);
  not not_145 (not_145_out, OP1);
  not not_146 (not_146_out, OP0);
  not not_147 (not_147_out, OP5);
  not not_148 (not_148_out, OP4);
  not not_149 (not_149_out, OP2);
  not not_150 (not_150_out, OP0);
  not not_151 (not_151_out, OP5);
  not not_152 (not_152_out, OP4);
  not not_153 (not_153_out, OP3);
  not not_154 (not_154_out, OP2);
  not not_155 (not_155_out, OP1);
  not not_156 (not_156_out, OP0);
  not not_157 (not_157_out, F5);
  not not_158 (not_158_out, F4);
  not not_159 (not_159_out, F3);
  not not_160 (not_160_out, F0);
  not not_161 (not_161_out, OP5);
  not not_162 (not_162_out, OP4);
  not not_163 (not_163_out, OP3);
  not not_164 (not_164_out, OP2);
  not not_165 (not_165_out, OP1);
  not not_166 (not_166_out, OP0);
  not not_167 (not_167_out, F4);
  not not_168 (not_168_out, F3);
  not not_169 (not_169_out, F2);
  not not_170 (not_170_out, F1);
  not not_171 (not_171_out, F0);
  not not_172 (not_172_out, OP5);
  not not_173 (not_173_out, OP4);
  not not_174 (not_174_out, OP3);
  not not_175 (not_175_out, OP2);
  not not_176 (not_176_out, OP1);
  not not_177 (not_177_out, OP0);
  not not_178 (not_178_out, F4);
  not not_179 (not_179_out, F3);
  not not_180 (not_180_out, F2);
  not not_181 (not_181_out, F1);
  not not_182 (not_182_out, OP5);
  not not_183 (not_183_out, OP4);
  not not_184 (not_184_out, OP3);
  not not_185 (not_185_out, OP2);
  not not_186 (not_186_out, OP1);
  not not_187 (not_187_out, OP0);
  not not_188 (not_188_out, F4);
  not not_189 (not_189_out, F3);
  not not_190 (not_190_out, F2);
  not not_191 (not_191_out, F0);
  not not_192 (not_192_out, OP5);
  not not_193 (not_193_out, OP4);
  not not_194 (not_194_out, OP3);
  not not_195 (not_195_out, OP2);
  not not_196 (not_196_out, OP1);
  not not_197 (not_197_out, OP0);
  not not_198 (not_198_out, F4);
  not not_199 (not_199_out, F3);
  not not_200 (not_200_out, F1);
  not not_201 (not_201_out, F0);
  not not_202 (not_202_out, OP5);
  not not_203 (not_203_out, OP4);
  not not_204 (not_204_out, OP3);
  not not_205 (not_205_out, OP2);
  not not_206 (not_206_out, OP1);
  not not_207 (not_207_out, OP0);
  not not_208 (not_208_out, F4);
  not not_209 (not_209_out, F2);
  not not_210 (not_210_out, OP5);
  not not_211 (not_211_out, OP4);
  not not_212 (not_212_out, OP3);
  not not_213 (not_213_out, OP2);
  not not_214 (not_214_out, OP5);
  not not_215 (not_215_out, OP4);
  not not_216 (not_216_out, OP2);
  not not_217 (not_217_out, OP1);
  not not_218 (not_218_out, OP0);
  not not_219 (not_219_out, OP5);
  not not_220 (not_220_out, OP4);
  not not_221 (not_221_out, OP1);
  not not_222 (not_222_out, OP0);
  not not_223 (not_223_out, OP5);
  not not_224 (not_224_out, OP4);
  not not_225 (not_225_out, OP2);
  not not_226 (not_226_out, OP1);
  not not_227 (not_227_out, OP4);
  not not_228 (not_228_out, OP3);
  not not_229 (not_229_out, OP2);
  not not_230 (not_230_out, OP4);
  not not_231 (not_231_out, OP2);
  not not_232 (not_232_out, OP4);
  not not_233 (not_233_out, OP2);
  not not_234 (not_234_out, OP1);
  not not_235 (not_235_out, OP0);
  not not_236 (not_236_out, OP5);
  not not_237 (not_237_out, OP4);
  not not_238 (not_238_out, OP3);
  not not_239 (not_239_out, OP2);
  not not_240 (not_240_out, OP1);
  not not_241 (not_241_out, OP5);
  not not_242 (not_242_out, OP4);
  not not_243 (not_243_out, OP3);
  not not_244 (not_244_out, OP2);
  not not_245 (not_245_out, OP1);
  not not_246 (not_246_out, OP0);
  not not_247 (not_247_out, F4);
  not not_248 (not_248_out, F3);
  not not_249 (not_249_out, F1);
  not not_250 (not_250_out, OP5);
  not not_251 (not_251_out, OP4);
  not not_252 (not_252_out, OP3);
  not not_253 (not_253_out, OP2);
  not not_254 (not_254_out, OP1);
  not not_255 (not_255_out, OP0);
  not not_256 (not_256_out, F4);
  not not_257 (not_257_out, F3);
  not not_258 (not_258_out, OP5);
  not not_259 (not_259_out, OP4);
  not not_260 (not_260_out, OP3);
  not not_261 (not_261_out, OP2);
  not not_262 (not_262_out, OP1);
  not not_263 (not_263_out, OP0);
  not not_264 (not_264_out, F4);
  not not_265 (not_265_out, F2);
  not not_266 (not_266_out, F0);
  not not_267 (not_267_out, OP5);
  not not_268 (not_268_out, OP4);
  not not_269 (not_269_out, OP3);
  not not_270 (not_270_out, OP2);
  not not_271 (not_271_out, OP1);
  not not_272 (not_272_out, OP0);
  not not_273 (not_273_out, F4);
  not not_274 (not_274_out, F2);
  not not_275 (not_275_out, OP5);
  not not_276 (not_276_out, OP4);
  not not_277 (not_277_out, OP2);
  not not_278 (not_278_out, OP0);
  not not_279 (not_279_out, OP5);
  not not_280 (not_280_out, OP4);
  not not_281 (not_281_out, OP1);
  not not_282 (not_282_out, OP5);
  not not_283 (not_283_out, OP4);
  not not_284 (not_284_out, OP3);
  not not_285 (not_285_out, OP2);
  not not_286 (not_286_out, OP1);
  and and_1 (and_1_out, not_1_out, not_2_out, not_3_out, not_4_out, not_5_out, not_6_out, not_7_out, not_8_out, not_9_out, not_10_out, F1, F0);
  and and_2 (and_2_out, not_11_out, not_12_out, not_13_out, not_14_out, not_15_out, not_16_out, F5, not_17_out, not_18_out, not_19_out, not_20_out, not_21_out);
  and and_3 (and_3_out, not_22_out, not_23_out, not_24_out, not_25_out, not_26_out, not_27_out, F5, not_28_out, not_29_out, not_30_out, not_31_out, F0);
  and and_4 (and_4_out, not_32_out, not_33_out, not_34_out, not_35_out, not_36_out, not_37_out, F5, not_38_out, not_39_out, F2, not_40_out, not_41_out);
  and and_5 (and_5_out, not_42_out, not_43_out, not_44_out, not_45_out, not_46_out, not_47_out, F5, not_48_out, F3, not_49_out, F1, not_50_out);
  and and_6 (and_6_out, not_51_out, not_52_out, not_53_out, not_54_out, OP1, OP0);
  and and_7 (and_7_out, not_55_out, not_56_out, OP3, not_57_out, not_58_out, not_59_out);
  and and_8 (and_8_out, not_60_out, not_61_out, OP3, OP2, not_62_out, not_63_out);
  and and_9 (and_9_out, not_64_out, not_65_out, OP3, not_66_out, not_67_out, OP0);
  and and_10 (and_10_out, not_68_out, not_69_out, OP3, not_70_out, OP1, not_71_out);
  and and_11 (and_11_out, OP5, not_72_out, not_73_out, not_74_out, OP1, OP0);
  and and_12 (and_12_out, OP5, not_75_out, OP3, not_76_out, OP1, OP0);
  and and_13 (and_13_out, not_77_out, not_78_out, not_79_out, not_80_out, not_81_out, not_82_out, not_83_out, not_84_out, not_85_out, F2, F1, F0);
  and and_14 (and_14_out, OP5, not_86_out, OP3, not_87_out, not_88_out, not_89_out);
  and and_15 (and_15_out, not_90_out, not_91_out, not_92_out, not_93_out, not_94_out, OP0);
  and and_16 (and_16_out, not_95_out, not_96_out, not_97_out, not_98_out, not_99_out, not_100_out, not_101_out, not_102_out, not_103_out, not_104_out, F1, not_105_out);
  and and_17 (and_17_out, not_106_out, not_107_out, not_108_out, not_109_out, not_110_out, not_111_out, F5, not_112_out, not_113_out, not_114_out, F1, not_115_out);
  and and_18 (and_18_out, not_116_out, not_117_out, not_118_out, not_119_out, not_120_out, not_121_out, F5, not_122_out, not_123_out, F2, not_124_out, not_125_out);
  and and_19 (and_19_out, not_126_out, not_127_out, not_128_out, not_129_out, not_130_out, not_131_out, F5, not_132_out, not_133_out, F2, F1, F0);
  and and_20 (and_20_out, not_134_out, not_135_out, not_136_out, not_137_out, not_138_out, not_139_out, F5, not_140_out, F3, not_141_out, F1, not_142_out);
  and and_21 (and_21_out, not_143_out, not_144_out, OP3, OP2, not_145_out, not_146_out);
  and and_22 (and_22_out, not_147_out, not_148_out, OP3, not_149_out, OP1, not_150_out);
  and and_23 (and_23_out, not_151_out, not_152_out, not_153_out, not_154_out, not_155_out, not_156_out, not_157_out, not_158_out, not_159_out, F2, F1, not_160_out);
  and and_24 (and_24_out, not_161_out, not_162_out, not_163_out, not_164_out, not_165_out, not_166_out, F5, not_167_out, not_168_out, not_169_out, not_170_out, not_171_out);
  and and_25 (and_25_out, not_172_out, not_173_out, not_174_out, not_175_out, not_176_out, not_177_out, F5, not_178_out, not_179_out, not_180_out, not_181_out, F0);
  and and_26 (and_26_out, not_182_out, not_183_out, not_184_out, not_185_out, not_186_out, not_187_out, F5, not_188_out, not_189_out, not_190_out, F1, not_191_out);
  and and_27 (and_27_out, not_192_out, not_193_out, not_194_out, not_195_out, not_196_out, not_197_out, F5, not_198_out, not_199_out, F2, not_200_out, not_201_out);
  and and_28 (and_28_out, not_202_out, not_203_out, not_204_out, not_205_out, not_206_out, not_207_out, F5, not_208_out, F3, not_209_out, F1, F0);
  and and_29 (and_29_out, not_210_out, not_211_out, not_212_out, not_213_out, OP1, OP0);
  and and_30 (and_30_out, not_214_out, not_215_out, OP3, not_216_out, not_217_out, not_218_out);
  and and_31 (and_31_out, not_219_out, not_220_out, OP3, OP2, not_221_out, not_222_out);
  and and_32 (and_32_out, not_223_out, not_224_out, OP3, not_225_out, not_226_out, OP0);
  and and_33 (and_33_out, OP5, not_227_out, not_228_out, not_229_out, OP1, OP0);
  and and_34 (and_34_out, OP5, not_230_out, OP3, not_231_out, OP1, OP0);
  and and_35 (and_35_out, OP5, not_232_out, OP3, not_233_out, not_234_out, not_235_out);
  and and_36 (and_36_out, not_236_out, not_237_out, not_238_out, not_239_out, not_240_out, OP0);
  and and_37 (and_37_out, not_241_out, not_242_out, not_243_out, not_244_out, not_245_out, not_246_out, F5, not_247_out, not_248_out, F2, not_249_out, F0);
  and and_38 (and_38_out, not_250_out, not_251_out, not_252_out, not_253_out, not_254_out, not_255_out, F5, not_256_out, not_257_out, F2, F1, F0);
  and and_39 (and_39_out, not_258_out, not_259_out, not_260_out, not_261_out, not_262_out, not_263_out, F5, not_264_out, F3, not_265_out, F1, not_266_out);
  and and_40 (and_40_out, not_267_out, not_268_out, not_269_out, not_270_out, not_271_out, not_272_out, F5, not_273_out, F3, not_274_out, F1, F0);
  and and_41 (and_41_out, not_275_out, not_276_out, OP3, not_277_out, OP1, not_278_out);
  and and_42 (and_42_out, not_279_out, not_280_out, OP3, OP2, not_281_out, OP0);
  and and_43 (and_43_out, not_282_out, not_283_out, not_284_out, not_285_out, not_286_out, OP0);
  or or_1 (S1, and_16_out, and_17_out, and_18_out, and_19_out, and_20_out, and_21_out, and_22_out, and_23_out);
  or or_2 (S3, and_37_out, and_38_out, and_39_out, and_40_out, and_41_out, and_42_out, and_43_out);
  or or_3 (S0, and_1_out, and_2_out, and_3_out, and_4_out, and_5_out, and_6_out, and_7_out, and_8_out, and_9_out, and_10_out, and_11_out, and_12_out, and_13_out, and_14_out, and_15_out);
  or or_4 (S2, and_24_out, and_25_out, and_26_out, and_27_out, and_28_out, and_29_out, and_30_out, and_31_out, and_32_out, and_33_out, and_34_out, and_35_out, and_36_out);
endmodule

// 控制信号生成
module \控制信号自动生成  (
  input  OP0,
  input  OP1,
  input  OP2,
  input  OP3,
  input  OP4,
  input  OP5,
  input  F0,
  input  F1,
  input  F2,
  input  F3,
  input  F4,
  input  F5,
  input  [4:0] MT_MF,
  output MemToReg,
  output MemWrite,
  output ALU_SRC,
  output RegWrite,
  output SysCALL,
  output SignedExt,
  output RegDst,
  output BEQ,
  output BNE,
  output JR,
  output JUMP,
  output JAL,
  output SB,
  output BLTZ,
  output VARIABLE,
  output ERET,
  output MFC0,
  output MTC0
);

  wire and_2_out, and_3_out, and_4_out, and_5_out, and_6_out, and_7_out, and_8_out, and_9_out, and_10_out,
       and_11_out, and_12_out, and_13_out, and_14_out, and_15_out, and_16_out, and_17_out, and_18_out,
       and_19_out, and_20_out, and_21_out, and_22_out, and_23_out, and_24_out, and_25_out, and_26_out,
       and_29_out, and_30_out, not_1_out, not_2_out, not_3_out, not_4_out, not_5_out, not_6_out, not_7_out,
       not_8_out, not_9_out, not_10_out, not_11_out, not_12_out, not_13_out, not_14_out, not_15_out,
       not_16_out, not_17_out, not_18_out, not_19_out, not_20_out, not_21_out, not_22_out, not_23_out,
       not_24_out, not_25_out, not_26_out, not_27_out, not_28_out, not_29_out, not_30_out, not_31_out,
       not_32_out, not_33_out, not_34_out, not_35_out, not_36_out, not_37_out, not_38_out, not_39_out,
       not_40_out, not_41_out, not_42_out, not_43_out, not_44_out, not_45_out, not_46_out, not_47_out,
       not_48_out, not_49_out, not_50_out, not_51_out, not_52_out, not_53_out, not_54_out, not_55_out,
       not_56_out, not_57_out, not_58_out, not_59_out, not_60_out, not_61_out, not_62_out, not_63_out,
       not_64_out, not_65_out, not_66_out, not_67_out, not_68_out, not_69_out, not_70_out, not_71_out,
       not_72_out, not_73_out, not_74_out, not_75_out, not_76_out, not_77_out, not_78_out, not_79_out,
       not_80_out, not_81_out, not_82_out, not_83_out, not_84_out, not_85_out, not_86_out, not_87_out,
       not_88_out, not_89_out, not_90_out, not_91_out, not_92_out, not_93_out, not_94_out, not_95_out,
       not_96_out, not_97_out, not_98_out, not_99_out, not_100_out, not_101_out, not_102_out, not_103_out,
       not_104_out, not_105_out, not_106_out, not_107_out, not_108_out, not_109_out, not_110_out,
       not_111_out, not_112_out, not_113_out, not_114_out, not_115_out, not_116_out, not_117_out,
       not_118_out, not_119_out, not_120_out, not_121_out, not_122_out, not_123_out, not_124_out,
       not_125_out, not_126_out, not_127_out, not_128_out, not_129_out, not_130_out, not_131_out,
       not_132_out, not_133_out, not_134_out, not_135_out, not_136_out, not_137_out, not_138_out,
       not_139_out, not_140_out, not_141_out, not_142_out, not_143_out, not_144_out, not_145_out,
       not_146_out, not_147_out, not_148_out, not_149_out, not_150_out, not_151_out, not_152_out,
       not_153_out, not_154_out, not_155_out, not_156_out, not_157_out, not_158_out, not_159_out,
       not_160_out, not_161_out, not_162_out, not_163_out, not_164_out, not_165_out, not_166_out,
       not_167_out, not_168_out, not_169_out, not_170_out, not_171_out, not_172_out, not_173_out,
       not_174_out, not_175_out, not_176_out, not_177_out, not_178_out, not_179_out, not_180_out,
       not_181_out, not_182_out, not_183_out, not_184_out, not_185_out, not_186_out, not_187_out,
       not_188_out, not_189_out, not_190_out, not_191_out, not_192_out, not_193_out, not_194_out,
       not_195_out, not_196_out, not_197_out, not_198_out, not_199_out, not_200_out, not_201_out,
       not_202_out, not_203_out, not_204_out, not_205_out, not_206_out, not_207_out, not_208_out,
       not_209_out, not_210_out, not_211_out, not_212_out, not_213_out, not_214_out, not_215_out,
       not_216_out, not_217_out, not_218_out, not_219_out, not_220_out, not_221_out, not_222_out,
       not_223_out, not_224_out, not_225_out, not_226_out, not_227_out, not_228_out, not_229_out,
       not_230_out, not_231_out, not_232_out, not_233_out, not_234_out, not_235_out, not_236_out,
       not_237_out, not_238_out;

  not not_1 (not_1_out, OP2);
  not not_2 (not_2_out, OP3);
  not not_3 (not_3_out, OP4);
  not not_4 (not_4_out, OP0);
  not not_5 (not_5_out, OP1);
  not not_6 (not_6_out, OP2);
  not not_7 (not_7_out, OP4);
  not not_8 (not_8_out, OP2);
  not not_9 (not_9_out, OP4);
  not not_10 (not_10_out, OP0);
  not not_11 (not_11_out, OP1);
  not not_12 (not_12_out, OP2);
  not not_13 (not_13_out, OP4);
  not not_14 (not_14_out, OP0);
  not not_15 (not_15_out, OP2);
  not not_16 (not_16_out, OP4);
  not not_17 (not_17_out, OP5);
  not not_18 (not_18_out, OP1);
  not not_19 (not_19_out, OP4);
  not not_20 (not_20_out, OP5);
  not not_21 (not_21_out, OP2);
  not not_22 (not_22_out, OP4);
  not not_23 (not_23_out, OP0);
  not not_24 (not_24_out, OP1);
  not not_25 (not_25_out, OP2);
  not not_26 (not_26_out, OP4);
  not not_27 (not_27_out, OP5);
  not not_28 (not_28_out, F0);
  not not_29 (not_29_out, F2);
  not not_30 (not_30_out, F3);
  not not_31 (not_31_out, F4);
  not not_32 (not_32_out, OP0);
  not not_33 (not_33_out, OP1);
  not not_34 (not_34_out, OP2);
  not not_35 (not_35_out, OP4);
  not not_36 (not_36_out, OP5);
  not not_37 (not_37_out, F1);
  not not_38 (not_38_out, F3);
  not not_39 (not_39_out, F4);
  not not_40 (not_40_out, OP0);
  not not_41 (not_41_out, OP1);
  not not_42 (not_42_out, OP2);
  not not_43 (not_43_out, OP4);
  not not_44 (not_44_out, OP5);
  not not_45 (not_45_out, F3);
  not not_46 (not_46_out, F4);
  not not_47 (not_47_out, F5);
  not not_48 (not_48_out, OP0);
  not not_49 (not_49_out, OP1);
  not not_50 (not_50_out, OP2);
  not not_51 (not_51_out, OP4);
  not not_52 (not_52_out, OP5);
  not not_53 (not_53_out, F2);
  not not_54 (not_54_out, F4);
  not not_55 (not_55_out, OP0);
  not not_56 (not_56_out, OP1);
  not not_57 (not_57_out, OP2);
  not not_58 (not_58_out, OP4);
  not not_59 (not_59_out, OP5);
  not not_60 (not_60_out, F3);
  not not_61 (not_61_out, F4);
  not not_62 (not_62_out, OP0);
  not not_63 (not_63_out, OP2);
  not not_64 (not_64_out, OP4);
  not not_65 (not_65_out, OP5);
  not not_66 (not_66_out, OP1);
  not not_67 (not_67_out, OP4);
  not not_68 (not_68_out, OP5);
  not not_69 (not_69_out, OP2);
  not not_70 (not_70_out, OP3);
  not not_71 (not_71_out, OP4);
  not not_72 (not_72_out, OP0);
  not not_73 (not_73_out, OP1);
  not not_74 (not_74_out, OP2);
  not not_75 (not_75_out, OP3);
  not not_76 (not_76_out, OP4);
  not not_77 (not_77_out, OP5);
  not not_78 (not_78_out, F0);
  not not_79 (not_79_out, F1);
  not not_80 (not_80_out, F4);
  not not_81 (not_81_out, F5);
  not not_82 (not_82_out, OP0);
  not not_83 (not_83_out, OP1);
  not not_84 (not_84_out, OP2);
  not not_85 (not_85_out, OP4);
  not not_86 (not_86_out, OP0);
  not not_87 (not_87_out, OP2);
  not not_88 (not_88_out, OP4);
  not not_89 (not_89_out, OP5);
  not not_90 (not_90_out, OP1);
  not not_91 (not_91_out, OP3);
  not not_92 (not_92_out, OP4);
  not not_93 (not_93_out, OP5);
  not not_94 (not_94_out, OP1);
  not not_95 (not_95_out, OP2);
  not not_96 (not_96_out, OP4);
  not not_97 (not_97_out, OP5);
  not not_98 (not_98_out, OP2);
  not not_99 (not_99_out, OP4);
  not not_100 (not_100_out, OP0);
  not not_101 (not_101_out, OP1);
  not not_102 (not_102_out, OP2);
  not not_103 (not_103_out, OP3);
  not not_104 (not_104_out, OP4);
  not not_105 (not_105_out, OP5);
  not not_106 (not_106_out, F0);
  not not_107 (not_107_out, F1);
  not not_108 (not_108_out, F2);
  not not_109 (not_109_out, F4);
  not not_110 (not_110_out, F5);
  not not_111 (not_111_out, OP0);
  not not_112 (not_112_out, OP1);
  not not_113 (not_113_out, OP2);
  not not_114 (not_114_out, OP3);
  not not_115 (not_115_out, OP4);
  not not_116 (not_116_out, OP5);
  not not_117 (not_117_out, F0);
  not not_118 (not_118_out, F2);
  not not_119 (not_119_out, F3);
  not not_120 (not_120_out, F4);
  not not_121 (not_121_out, OP0);
  not not_122 (not_122_out, OP1);
  not not_123 (not_123_out, OP2);
  not not_124 (not_124_out, OP3);
  not not_125 (not_125_out, OP4);
  not not_126 (not_126_out, OP5);
  not not_127 (not_127_out, F1);
  not not_128 (not_128_out, F3);
  not not_129 (not_129_out, F4);
  not not_130 (not_130_out, OP0);
  not not_131 (not_131_out, OP1);
  not not_132 (not_132_out, OP2);
  not not_133 (not_133_out, OP3);
  not not_134 (not_134_out, OP4);
  not not_135 (not_135_out, OP5);
  not not_136 (not_136_out, F3);
  not not_137 (not_137_out, F4);
  not not_138 (not_138_out, F5);
  not not_139 (not_139_out, OP0);
  not not_140 (not_140_out, OP1);
  not not_141 (not_141_out, OP2);
  not not_142 (not_142_out, OP3);
  not not_143 (not_143_out, OP4);
  not not_144 (not_144_out, OP5);
  not not_145 (not_145_out, F2);
  not not_146 (not_146_out, F4);
  not not_147 (not_147_out, OP0);
  not not_148 (not_148_out, OP1);
  not not_149 (not_149_out, OP2);
  not not_150 (not_150_out, OP3);
  not not_151 (not_151_out, OP4);
  not not_152 (not_152_out, OP5);
  not not_153 (not_153_out, F3);
  not not_154 (not_154_out, F4);
  not not_155 (not_155_out, OP0);
  not not_156 (not_156_out, OP1);
  not not_157 (not_157_out, OP3);
  not not_158 (not_158_out, OP4);
  not not_159 (not_159_out, OP5);
  not not_160 (not_160_out, OP1);
  not not_161 (not_161_out, OP3);
  not not_162 (not_162_out, OP4);
  not not_163 (not_163_out, OP5);
  not not_164 (not_164_out, OP0);
  not not_165 (not_165_out, OP1);
  not not_166 (not_166_out, OP2);
  not not_167 (not_167_out, OP3);
  not not_168 (not_168_out, OP4);
  not not_169 (not_169_out, OP5);
  not not_170 (not_170_out, F0);
  not not_171 (not_171_out, F1);
  not not_172 (not_172_out, F2);
  not not_173 (not_173_out, F4);
  not not_174 (not_174_out, F5);
  not not_175 (not_175_out, OP0);
  not not_176 (not_176_out, OP2);
  not not_177 (not_177_out, OP3);
  not not_178 (not_178_out, OP4);
  not not_179 (not_179_out, OP5);
  not not_180 (not_180_out, F0);
  not not_181 (not_181_out, F1);
  not not_182 (not_182_out, F2);
  not not_183 (not_183_out, F4);
  not not_184 (not_184_out, F5);
  not not_185 (not_185_out, OP2);
  not not_186 (not_186_out, OP3);
  not not_187 (not_187_out, OP4);
  not not_188 (not_188_out, OP5);
  not not_189 (not_189_out, OP2);
  not not_190 (not_190_out, OP3);
  not not_191 (not_191_out, OP4);
  not not_192 (not_192_out, OP5);
  not not_193 (not_193_out, OP0);
  not not_194 (not_194_out, OP1);
  not not_195 (not_195_out, OP2);
  not not_196 (not_196_out, OP4);
  not not_197 (not_197_out, OP1);
  not not_198 (not_198_out, OP2);
  not not_199 (not_199_out, OP3);
  not not_200 (not_200_out, OP4);
  not not_201 (not_201_out, OP5);
  not not_202 (not_202_out, OP0);
  not not_203 (not_203_out, OP1);
  not not_204 (not_204_out, OP2);
  not not_205 (not_205_out, OP3);
  not not_206 (not_206_out, OP4);
  not not_207 (not_207_out, OP5);
  not not_208 (not_208_out, F3);
  not not_209 (not_209_out, F4);
  not not_210 (not_210_out, F5);
  not not_211 (not_211_out, OP5);
  not not_212 (not_212_out, OP3);
  not not_213 (not_213_out, OP2);
  not not_214 (not_214_out, OP1);
  not not_215 (not_215_out, OP0);
  not not_216 (not_216_out, F5);
  not not_217 (not_217_out, F2);
  not not_218 (not_218_out, F1);
  not not_219 (not_219_out, F0);
  not not_220 (not_220_out, OP5);
  not not_221 (not_221_out, OP3);
  not not_222 (not_222_out, OP2);
  not not_223 (not_223_out, OP1);
  not not_224 (not_224_out, OP0);
  not not_225 (not_225_out, MT_MF[0]);
  not not_226 (not_226_out, MT_MF[1]);
  not not_227 (not_227_out, MT_MF[2]);
  not not_228 (not_228_out, MT_MF[3]);
  not not_229 (not_229_out, MT_MF[4]);
  not not_230 (not_230_out, OP5);
  not not_231 (not_231_out, OP3);
  not not_232 (not_232_out, OP2);
  not not_233 (not_233_out, OP1);
  not not_234 (not_234_out, OP0);
  not not_235 (not_235_out, MT_MF[0]);
  not not_236 (not_236_out, MT_MF[1]);
  not not_237 (not_237_out, MT_MF[3]);
  not not_238 (not_238_out, MT_MF[4]);
  and and_1 (MemToReg, OP0, OP1, not_1_out, not_2_out, not_3_out, OP5);
  and and_2 (and_2_out, not_4_out, not_5_out, not_6_out, OP3, not_7_out, OP5);
  and and_3 (and_3_out, OP0, OP1, not_8_out, OP3, not_9_out, OP5);
  and and_4 (and_4_out, not_10_out, not_11_out, not_12_out, OP3, not_13_out);
  and and_5 (and_5_out, not_14_out, not_15_out, OP3, not_16_out, not_17_out);
  and and_6 (and_6_out, not_18_out, OP3, not_19_out, not_20_out);
  and and_7 (and_7_out, OP0, OP1, not_21_out, not_22_out, OP5);
  and and_8 (and_8_out, not_23_out, not_24_out, not_25_out, not_26_out, not_27_out, not_28_out, not_29_out, not_30_out, not_31_out);
  and and_9 (and_9_out, not_32_out, not_33_out, not_34_out, not_35_out, not_36_out, not_37_out, not_38_out, not_39_out, F5);
  and and_10 (and_10_out, not_40_out, not_41_out, not_42_out, not_43_out, not_44_out, F1, not_45_out, not_46_out, not_47_out);
  and and_11 (and_11_out, not_48_out, not_49_out, not_50_out, not_51_out, not_52_out, F1, not_53_out, F3, not_54_out, F5);
  and and_12 (and_12_out, not_55_out, not_56_out, not_57_out, not_58_out, not_59_out, F0, F1, F2, not_60_out, not_61_out);
  and and_13 (and_13_out, not_62_out, not_63_out, OP3, not_64_out, not_65_out);
  and and_14 (and_14_out, not_66_out, OP3, not_67_out, not_68_out);
  and and_15 (and_15_out, OP0, OP1, not_69_out, not_70_out, not_71_out);
  and and_16 (and_16_out, not_82_out, not_83_out, not_84_out, OP3, not_85_out);
  and and_17 (and_17_out, not_86_out, not_87_out, OP3, not_88_out, not_89_out);
  and and_18 (and_18_out, not_90_out, OP2, not_91_out, not_92_out, not_93_out);
  and and_19 (and_19_out, OP0, not_94_out, not_95_out, not_96_out, not_97_out);
  and and_20 (and_20_out, OP0, OP1, not_98_out, not_99_out, OP5);
  and and_21 (and_21_out, not_100_out, not_101_out, not_102_out, not_103_out, not_104_out, not_105_out, not_106_out, not_107_out, not_108_out, not_109_out, not_110_out);
  and and_22 (and_22_out, not_111_out, not_112_out, not_113_out, not_114_out, not_115_out, not_116_out, not_117_out, not_118_out, not_119_out, not_120_out);
  and and_23 (and_23_out, not_121_out, not_122_out, not_123_out, not_124_out, not_125_out, not_126_out, not_127_out, not_128_out, not_129_out, F5);
  and and_24 (and_24_out, not_130_out, not_131_out, not_132_out, not_133_out, not_134_out, not_135_out, F1, not_136_out, not_137_out, not_138_out);
  and and_25 (and_25_out, not_139_out, not_140_out, not_141_out, not_142_out, not_143_out, not_144_out, F1, not_145_out, F3, not_146_out, F5);
  and and_26 (and_26_out, not_147_out, not_148_out, not_149_out, not_150_out, not_151_out, not_152_out, F0, F1, F2, not_153_out, not_154_out);
  and and_27 (BEQ, not_155_out, not_156_out, OP2, not_157_out, not_158_out, not_159_out);
  and and_28 (BNE, OP0, not_160_out, OP2, not_161_out, not_162_out, not_163_out);
  and and_29 (and_29_out, not_175_out, not_176_out, not_177_out, not_178_out, not_179_out, not_180_out, not_181_out, not_182_out, F3, not_183_out, not_184_out);
  and and_30 (and_30_out, OP1, not_185_out, not_186_out, not_187_out, not_188_out);
  and and_31 (JAL, OP0, OP1, not_189_out, not_190_out, not_191_out, not_192_out);
  and and_32 (SB, not_193_out, not_194_out, not_195_out, OP3, not_196_out, OP5);
  and and_33 (BLTZ, OP0, not_197_out, not_198_out, not_199_out, not_200_out, not_201_out);
  and and_34 (VARIABLE, not_202_out, not_203_out, not_204_out, not_205_out, not_206_out, not_207_out, F1, F2, not_208_out, not_209_out, not_210_out);
  or or_1 (MemWrite, and_2_out, and_3_out);
  or or_2 (ALU_SRC, and_4_out, and_5_out, and_6_out, and_7_out);
  and and_35 (SysCALL, not_72_out, not_73_out, not_74_out, not_75_out, not_76_out, not_77_out, not_78_out, not_79_out, F2, F3, not_80_out, not_81_out);
  or or_3 (SignedExt, and_16_out, and_17_out, and_18_out, and_19_out, and_20_out);
  and and_36 (JR, not_164_out, not_165_out, not_166_out, not_167_out, not_168_out, not_169_out, not_170_out, not_171_out, not_172_out, F3, not_173_out, not_174_out);
  or or_4 (JUMP, and_29_out, and_30_out);
  and and_37 (ERET, not_211_out, OP4, not_212_out, not_213_out, not_214_out, not_215_out, not_216_out, F4, F3, not_217_out, not_218_out, not_219_out);
  and and_38 (MFC0, not_220_out, OP4, not_221_out, not_222_out, not_223_out, not_224_out, not_225_out, not_226_out, not_227_out, not_228_out, not_229_out);
  and and_39 (MTC0, not_230_out, OP4, not_231_out, not_232_out, not_233_out, not_234_out, not_235_out, not_236_out, MT_MF[2], not_237_out, not_238_out);
  or or_5 (RegWrite, and_8_out, and_9_out, and_10_out, and_11_out, and_12_out, and_13_out, and_14_out, and_15_out);
  or or_6 (RegDst, and_21_out, and_22_out, and_23_out, and_24_out, and_25_out, and_26_out);
endmodule

// ALU
module MIPS_ALU (
  input  [4:0] shamt,
  input  [31:0] X,
  input  [31:0] Y,
  input  [3:0] AluOP,
  output Equal,
  output [31:0] Result,
  output [31:0] Result_2
);

  wire [0:0] comparator_1_lt, comparator_2_lt;
  wire [31:0] adder_1_out, AND_out, divider_1_out, divider_1_rem, multiplier_1_cout, multiplier_1_out,
       NOR_out, OR_out, shifter_1_out, shifter_2_out, shifter_3_out, subtractor_1_out, XOR_out;

  assign AND_out = X & Y;  // AND_Gate AND, 32 bits wide
  assign OR_out = X | Y;  // OR_Gate OR, 32 bits wide
  Shifter #(.width(32), .shift("ll")) shifter_1 (.in(Y), .\dist (shamt), .out(shifter_1_out));
  Shifter #(.width(32), .shift("ar")) shifter_2 (.in(Y), .\dist (shamt), .out(shifter_2_out));
  Shifter #(.width(32), .shift("lr")) shifter_3 (.in(Y), .\dist (shamt), .out(shifter_3_out));
  Multiplier #(.width(32)) multiplier_1 (.a(X), .b(Y), .out(multiplier_1_out), .cout(multiplier_1_cout));  // open: cin
  Divider #(.width(32)) divider_1 (.a(X), .b(Y), .out(divider_1_out), .rem(divider_1_rem));  // open: upper
  Adder #(.width(32)) adder_1 (.a(X), .b(Y), .out(adder_1_out));  // open: cin, cout
  Subtractor #(.width(32)) subtractor_1 (.a(X), .b(Y), .out(subtractor_1_out));  // open: bin, bout
  assign XOR_out = X ^ Y;  // XOR_Gate XOR, 32 bits wide
  assign NOR_out = ~(X | Y);  // NOR_Gate NOR, 32 bits wide
  Comparator #(.width(32), .mode("twosComplement")) comparator_1 (
    .a(X), .b(Y), .eq(Equal), .lt(comparator_1_lt[0]));  // open: gt
  Comparator #(.width(32), .mode("unsigned")) comparator_2 (.a(X), .b(Y), .lt(comparator_2_lt[0]));  // open: gt, eq
  Multiplexer #(.select(4), .width(32), .disabled("Z"), .enable("false")) multiplexer_1 (
    .in0(shifter_1_out), .in1(shifter_2_out), .in2(shifter_3_out), .in3(multiplier_1_out),
    .in4(divider_1_out), .in5(adder_1_out), .in6(subtractor_1_out), .in7(AND_out), .in8(OR_out),
    .in9(XOR_out), .in10(NOR_out), .in11({{31{1'b0}}, comparator_1_lt[0]}),
    .in12({{31{1'b0}}, comparator_2_lt[0]}), .in13({{31{1'b0}}, X[31]}), .in14({32{1'b0}}),
    .in15({32{1'b0}}), .out(Result), .sel(AluOP));
  Multiplexer #(.select(4), .width(32), .disabled("Z"), .enable("false")) multiplexer_2 (
    .in0({32{1'b0}}), .in1({32{1'b0}}), .in2({32{1'b0}}), .in3(multiplier_1_cout), .in4(divider_1_rem),
    .in5({32{1'b0}}), .in6({32{1'b0}}), .in7({32{1'b0}}), .in8({32{1'b0}}), .in9({32{1'b0}}),
    .in10({32{1'b0}}), .in11({32{1'b0}}), .in12({32{1'b0}}), .in13({32{1'b0}}), .in14({32{1'b0}}),
    .in15({32{1'b0}}), .out(Result_2), .sel(AluOP));

  // Other names for the same wires on the sheet: Result2[31:0] = Result_2; S[3:0] = AluOP

  // Notes on the sheet:
  //   不要改变此引脚区域内容，也不要改变ALU封装形式
  //   输入引脚
  //   输出引脚
endmodule

module MIPS_Regifile (
  input  [31:0] Din,
  input  Clk,
  input  WE,
  input  [4:0] R1_num,
  input  [4:0] W_num,
  input  [4:0] R2_num,
  output [31:0] R1,
  output [31:0] R2
);

  // RegisterFile registerfile_1: pin names not known; wires that end beside it: Din, Clk, WE, W_num, R1_num, R2_num, R1, R2
endmodule

module \理想流水线  (
  output RegWrite,
  output MemWrite,
  output [31:0] IF_PC,
  output [31:0] ID_PC,
  output [31:0] EX_PC,
  output [31:0] M_PC,
  output [31:0] WB_PC,
  output [31:0] RDin,
  output [31:0] MDin,
  output [31:0] LedData
);

  wire CLK, d_ff_1_q, display, ex_mem_1_regwrite_2, ex_mem_1_wb_2, Go, id_ex_1_mem_2, id_ex_1_regwrite_2,
       id_ex_1_srcb_2, id_ex_1_syscall_2, id_ex_1_wb_2, IR1, IR2, IR3, mem_wb_1_wb_2, mips_probe_5_p1,
       mips_probe_5_p2, mips_probe_5_p4, mips_probe_5_p5, mips_probe_5_p6, not_1_out, not_2_out, RST,
       SignedExt, Stop, W1, W2, W3, \单周期硬布线控制器_1_alu_src , \单周期硬布线控制器_1_jal , \单周期硬布线控制器_1_memtoreg ,
       \单周期硬布线控制器_1_memwrite , \单周期硬布线控制器_1_regdst , \单周期硬布线控制器_1_regwrite , \单周期硬布线控制器_1_syscall ;
  wire [3:0] id_ex_1_aluop_2, \单周期硬布线控制器_1_alu_op ;
  wire [4:0] ex_mem_1_writereg_num_2, id_ex_1_writereg_num_2, mem_wb_1_writereg_num_2, multiplexer_1_out,
       multiplexer_2_out, multiplexer_3_out;
  wire [15:0] \LoadUse次数 , \总周期数 , \插入气泡数 , \无条件分支数 , \条件分支成功数 ;
  wire [31:0] a0, adder_1_out, bit_extender_1_out, bit_extender_2_out, controlled_buffer_1_out, EX_IR,
       ex_mem_1_aluresult_2, ex_mem_1_ir_2, id_ex_1_a_2, id_ex_1_imm_2, id_ex_1_ir_2, ID_IR, if_id_1_ir_2,
       IF_IR, MEM_IR, mem_wb_1_aluresult_2, mem_wb_1_ir_2, mem_wb_1_md_2, mips_alu_1_result,
       mips_regifile_1_r1, mips_regifile_1_r2, multiplexer_4_out, multiplexer_5_out, ram_1_data, rom_1_data,
       WB_IR;

  Button \u_总复位  (.out(RST));
  Button _1 (.out(IR1));
  Button _2 (.out(IR2));
  Button _3 (.out(IR3));
  // Probe on \总周期数 
  // Probe on \总周期数 
  Button \u_继续运行  (.out(Go));
  LED #(.active("true")) led_1 (.in(W1));
  LED #(.active("true")) led_2 (.in(W2));
  LED #(.active("true")) led_3 (.in(W3));
  Hex_Digit_Display hex_digit_display_1 (.value(LedData[31:28]));  // open: dp
  // Probe on IF_PC[19:0]
  // Mips_Probe mips_probe_1: pin names not known; wires that end beside it: IF_IR
  not not_1 (not_1_out, Stop);
  Hex_Digit_Display hex_digit_display_2 (.value(LedData[23:20]));  // open: dp
  Hex_Digit_Display hex_digit_display_3 (.value(LedData[27:24]));  // open: dp
  // Probe on ID_PC[19:0]
  // Mips_Probe mips_probe_2: pin names not known; wires that end beside it: ID_IR
  assign controlled_buffer_1_out = display ? a0 : 32'bz;  // Controlled_Buffer controlled_buffer_1
  Register #(.width(32), .trigger("rising"), .Select("low")) PC (
    .D(adder_1_out), .en(not_1_out), .Q(IF_PC), .clk(CLK));  // open: clr
  Hex_Digit_Display hex_digit_display_4 (.value(LedData[15:12]));  // open: dp
  Hex_Digit_Display hex_digit_display_5 (.value(LedData[19:16]));  // open: dp
  Register #(.width(32), .trigger("rising"), .Select("low")) register_1 (
    .D(controlled_buffer_1_out), .Q(LedData), .clk(CLK));  // open: en, clr
  Counter #(.width(16), .max('hffff), .ongoal("wrap"), .trigger("rising"), .behavior("new")) counter_1 (
    .count(not_1_out), .Q(\总周期数 ), .clk(CLK));  // open: load, D, carry, clr, preset, down
  Hex_Digit_Display hex_digit_display_6 (.value(LedData[11:8]));  // open: dp
  Hex_Digit_Display hex_digit_display_7 (.value(LedData[7:4]));  // open: dp
  Clock #(.highDuration(1), .lowDuration(1)) clock_1 (.out(CLK));
  // Probe on EX_PC[19:0]
  // Mips_Probe mips_probe_3: pin names not known; wires that end beside it: EX_IR
  Adder #(.width(32)) adder_1 (.a(32'h4), .b(IF_PC), .out(adder_1_out));  // open: cin, cout
  Hex_Digit_Display hex_digit_display_8 (.value(LedData[3:0]));  // open: dp
  ROM #(.addrWidth(10), .dataWidth(32), .Select("high")) rom_1 (.addr(IF_PC[11:2]), .data(rom_1_data));
  // Probe on \总周期数 
  // Probe on M_PC[19:0]
  // Mips_Probe mips_probe_4: pin names not known; wires that end beside it: MEM_IR
  IF_ID if_id_1 (.IR(rom_1_data), .PC(IF_PC), .IR_2(if_id_1_ir_2), .PC_2(ID_PC), .CLK(CLK));  // open: clr, EN
  // Probe on \总周期数 
  // Probe on \无条件分支数 
  // Probe on \条件分支成功数 
  // Probe on \插入气泡数 
  // Probe on \LoadUse次数 
  // Probe on IF_PC[11:0]
  // Probe on WB_PC[19:0]
  // Mips_Probe mips_probe_5: pin names not known; wires that end beside it: mips_probe_5_p1, mips_probe_5_p2, WB_IR, mips_probe_5_p4, mips_probe_5_p5, mips_probe_5_p6
  \单周期硬布线控制器  \u_单周期硬布线控制器_1  (
    .Func(if_id_1_ir_2[5:0]), .OP(if_id_1_ir_2[31:26]), .ALU_OP(\单周期硬布线控制器_1_alu_op ),
    .MemToReg(\单周期硬布线控制器_1_memtoreg ), .MemWrite(\单周期硬布线控制器_1_memwrite ), .ALU_SRC(\单周期硬布线控制器_1_alu_src ),
    .RegWrite(\单周期硬布线控制器_1_regwrite ), .SysCALL(\单周期硬布线控制器_1_syscall ), .SignedExt(SignedExt),
    .RegDst(\单周期硬布线控制器_1_regdst ), .JR(mips_probe_5_p2), .JMP(mips_probe_5_p1), .Beq(mips_probe_5_p5),
    .JAL(\单周期硬布线控制器_1_jal ), .Bne(mips_probe_5_p6), .BLTZ(mips_probe_5_p4));  // open: SB, VAR, ERET, MT_MF, MFC0, MTC0
  Multiplexer #(.select(1), .width(5), .disabled("Z"), .enable("false")) multiplexer_1 (
    .in0(if_id_1_ir_2[25:21]), .in1(5'b00010), .out(multiplexer_1_out), .sel(\单周期硬布线控制器_1_syscall ));
  Multiplexer #(.select(1), .width(5), .disabled("Z"), .enable("false")) multiplexer_2 (
    .in0(if_id_1_ir_2[20:16]), .in1(5'b00100), .out(multiplexer_2_out), .sel(\单周期硬布线控制器_1_syscall ));
  // Probe on EX_PC[11:0]
  // Probe on ID_PC[11:0]
  Multiplexer #(.select(1), .width(5), .disabled("Z"), .enable("false")) multiplexer_3 (
    .in0(multiplexer_2_out), .in1(if_id_1_ir_2[15:11]), .out(multiplexer_3_out), .sel(\单周期硬布线控制器_1_regdst ));
  // Probe on M_PC[11:0]
  assign bit_extender_1_out = {{16{1'b0}}, if_id_1_ir_2[15:0]};  // Bit_Extender bit_extender_1
  assign bit_extender_2_out = {{16{if_id_1_ir_2[15]}}, if_id_1_ir_2[15:0]};  // Bit_Extender bit_extender_2
  // Probe on WB_PC[11:0]
  ID_EX id_ex_1 (
    .WB(\单周期硬布线控制器_1_memtoreg ), .MEM(\单周期硬布线控制器_1_memwrite ), .AluOp(\单周期硬布线控制器_1_alu_op ),
    .SrcB(\单周期硬布线控制器_1_alu_src ), .RegWrite(\单周期硬布线控制器_1_regwrite ), .WriteReg_num(multiplexer_3_out),
    .Syscall(\单周期硬布线控制器_1_syscall ), .A(mips_regifile_1_r1), .B(mips_regifile_1_r2), .IMM(multiplexer_4_out),
    .IR(if_id_1_ir_2), .PC(ID_PC), .WB_2(id_ex_1_wb_2), .MEM_2(id_ex_1_mem_2), .AluOp_2(id_ex_1_aluop_2),
    .SrcB_2(id_ex_1_srcb_2), .RegWrite_2(id_ex_1_regwrite_2), .WriteReg_num_2(id_ex_1_writereg_num_2),
    .Syscall_2(id_ex_1_syscall_2), .A_2(id_ex_1_a_2), .B_2(a0), .IMM_2(id_ex_1_imm_2), .IR_2(id_ex_1_ir_2),
    .PC_2(EX_PC), .CLK(CLK));  // open: JR, JMP, BLTZ, Beq, Bne, JAL, SB, VAR, JR_2, JMP_2, BLTZ_2, Beq_2, Bne_2, JAL_2, SB_2, VAR_2, clr, EN
  MIPS_Regifile mips_regifile_1 (
    .Din(RDin), .Clk(CLK), .R1(mips_regifile_1_r1), .R2(mips_regifile_1_r2), .WE(RegWrite),
    .W_num(mem_wb_1_writereg_num_2), .R1_num(multiplexer_1_out), .R2_num(multiplexer_2_out));
  Multiplexer #(.select(1), .width(32), .disabled("Z"), .enable("false")) multiplexer_4 (
    .in0(bit_extender_1_out), .in1(bit_extender_2_out), .out(multiplexer_4_out), .sel(SignedExt));
  Comparator #(.width(32), .mode("twosComplement")) comparator_1 (
    .a(32'h22), .b(id_ex_1_a_2), .eq(display));  // open: gt, lt
  not not_2 (not_2_out, display);
  D_Flip_Flop #(.trigger("rising"), .Pre_Clr_Positions("ABOVE_BELOW"), .NegatePresetClear("false"), .enable("true"), .NewFFLayout("true")) d_ff_1 (
    .clk(CLK), .D(not_2_out), .Q(d_ff_1_q), .en(id_ex_1_syscall_2), .reset(Go));  // open: Qn, preset
  Multiplexer #(.select(1), .width(32), .disabled("Z"), .enable("false")) multiplexer_5 (
    .in0(a0), .in1(id_ex_1_imm_2), .out(multiplexer_5_out), .sel(id_ex_1_srcb_2));
  EX_MEM ex_mem_1 (
    .WB(id_ex_1_wb_2), .MEM(id_ex_1_mem_2), .RegWrite(id_ex_1_regwrite_2),
    .WriteReg_num(id_ex_1_writereg_num_2), .AluResult(mips_alu_1_result), .B(a0), .IR(id_ex_1_ir_2),
    .PC(EX_PC), .WB_2(ex_mem_1_wb_2), .MEM_2(MemWrite), .RegWrite_2(ex_mem_1_regwrite_2),
    .WriteReg_num_2(ex_mem_1_writereg_num_2), .AluResult_2(ex_mem_1_aluresult_2), .B_2(MDin),
    .IR_2(ex_mem_1_ir_2), .PC_2(M_PC), .CLK(CLK), .stop(d_ff_1_q), .stop_2(Stop));  // open: JAL, SB, JAL_2, SB_2, clr, EN
  MIPS_ALU mips_alu_1 (
    .X(id_ex_1_a_2), .Y(multiplexer_5_out), .AluOP(id_ex_1_aluop_2), .Result(mips_alu_1_result),
    .shamt(id_ex_1_ir_2[10:6]));  // open: Equal, Result_2
  RAM #(.addrWidth(10), .dataWidth(32), .bus("separate"), .Select("high")) ram_1 (
    .addr(ex_mem_1_aluresult_2[11:2]), .din(MDin), .data(ram_1_data), .str(MemWrite), .clk(CLK));  // open: sel, ld, clr
  MEM_WB mem_wb_1 (
    .WB(ex_mem_1_wb_2), .RegWrite(ex_mem_1_regwrite_2), .WriteReg_num(ex_mem_1_writereg_num_2),
    .AluResult(ex_mem_1_aluresult_2), .IR(ex_mem_1_ir_2), .PC(M_PC), .WB_2(mem_wb_1_wb_2),
    .RegWrite_2(RegWrite), .WriteReg_num_2(mem_wb_1_writereg_num_2), .AluResult_2(mem_wb_1_aluresult_2),
    .IR_2(mem_wb_1_ir_2), .PC_2(WB_PC), .CLK(CLK), .MD(ram_1_data), .MD_2(mem_wb_1_md_2));  // open: JAL, JAL_2, clr, EN
  Multiplexer #(.select(1), .width(32), .disabled("Z"), .enable("false")) multiplexer_6 (
    .in0(mem_wb_1_aluresult_2), .in1(mem_wb_1_md_2), .out(RDin), .sel(mem_wb_1_wb_2));

  // Other names for the same wires on the sheet: MEM_PC[31:0] = M_PC

  // Notes on the sheet:
  //   中断源
  //   时空图监测，可删除
  //   中断等待指示
  //   数码管输出
  //   contents of rom_1 (hex, n*v repeats v):
  //   20100000 20110000 20120000 20130000 36100000 36310001 36520002 36730003 ae100000 ae110004 ae120008
  //   ae13000c 2002000a 20110000 20120000 20130000 c
  //   rd
  //   rs
  //   rt
  //   JMP
  //   JR
  //   OP
  //   OP
  //   Func
  //   Func
  //   $v0
  //   $a0
  //   imm
  //   BLTZ
  //   Beq
  //   Bne
  //   MemToReg
  //   MemWrite
  //   AluOP
  //   AluSrcB
  //   RegWrite
  //   JAL
  //   RegDst
  //   流水调试日志用
  //   为方便自动评测，需要输出流水线各段保存的PC值，注意是PC不是PC+4，另外ID段寄存器写入信息，Mem段内存写入信息也要输出
endmodule

module \气泡流水线  (
  output RegWrite,
  output MemWrite,
  output [31:0] IF_PC,
  output [31:0] ID_PC,
  output [31:0] EX_PC,
  output [31:0] M_PC,
  output [31:0] WB_PC,
  output [31:0] RDin,
  output [31:0] MDin,
  output [31:0] LedData
);

  wire and_1_out, and_2_out, and_3_out, and_4_out, and_5_out, and_6_out, and_7_out, CLK, CLR, d_ff_1_q,
       display, EX, ex_mem_1_jal_2, ex_mem_1_regwrite_2, ex_mem_1_sb_2, ex_mem_1_wb_2, Go, id_ex_1_beq_2,
       id_ex_1_bltz_2, id_ex_1_bne_2, id_ex_1_jal_2, id_ex_1_jr_2, id_ex_1_mem_2, id_ex_1_regwrite_2,
       id_ex_1_sb_2, id_ex_1_srcb_2, id_ex_1_syscall_2, id_ex_1_var_2, id_ex_1_wb_2, IR1, IR2, IR3, JUMP,
       MEM, mem_wb_1_jal_2, mem_wb_1_wb_2, mips_alu_1_equal, mips_probe_6_p2, mips_probe_8_p2, not_1_out,
       not_2_out, not_3_out, not_4_out, not_5_out, not_6_out, not_7_out, not_8_out, or_1_out, or_4_out,
       register_2_q, register_3_q, RST, SB, SignedExt, Stop, VAR, W1, W2, W3, \单周期硬布线控制器_1_alu_src ,
       \单周期硬布线控制器_1_beq , \单周期硬布线控制器_1_bltz , \单周期硬布线控制器_1_bne , \单周期硬布线控制器_1_jal , \单周期硬布线控制器_1_jmp ,
       \单周期硬布线控制器_1_jr , \单周期硬布线控制器_1_memtoreg , \单周期硬布线控制器_1_memwrite , \单周期硬布线控制器_1_regdst ,
       \单周期硬布线控制器_1_regwrite , \单周期硬布线控制器_1_syscall , \源寄存器使用情况_1_r1_used , \源寄存器使用情况_1_r2_used ;
  wire [1:0] id_ex_1_jmp_2;
  wire [3:0] id_ex_1_aluop_2, \单周期硬布线控制器_1_alu_op ;
  wire [4:0] ex_mem_1_writereg_num_2, id_ex_1_writereg_num_2, multiplexer_3_out, multiplexer_4_out,
       multiplexer_5_out, multiplexer_7_out, multiplexer_8_out, W_num;
  wire [15:0] \LoadUse次数 , \总周期数 , \插入气泡数 , \无条件分支数 , \条件分支成功数 ;
  wire [31:0] a0, adder_1_out, adder_2_out, adder_3_out, adder_4_out, bit_extender_1_out, bit_extender_2_out,
       controlled_buffer_1_out, EX_IR, ex_mem_1_aluresult_2, ex_mem_1_b_2, ex_mem_1_ir_2, id_ex_1_imm_2,
       id_ex_1_ir_2, ID_IR, if_id_1_ir_2, IF_IR, MEM_IR, mem_wb_1_aluresult_2, mem_wb_1_md_2,
       mips_alu_1_result, mips_probe_4_p1, mips_regifile_1_r1, mips_regifile_1_r2, multiplexer_1_out,
       multiplexer_2_out, multiplexer_6_out, multiplexer_9_out, multiplexer_11_out, R_rs, ram_1_data,
       sb_1_out_4, shifter_1_out, WB_IR;

  Button \u_总复位  (.out(RST));
  Button _1 (.out(IR1));
  Button _2 (.out(IR2));
  Button _3 (.out(IR3));
  // Probe on \总周期数 
  // Probe on \总周期数 
  Button \u_继续运行  (.out(Go));
  LED #(.active("true")) led_1 (.in(W1));
  LED #(.active("true")) led_2 (.in(W2));
  LED #(.active("true")) led_3 (.in(W3));
  not not_1 (not_1_out, id_ex_1_jr_2);
  Multiplexer #(.select(1), .width(32), .disabled("Z"), .enable("false")) multiplexer_1 (
    .in0(R_rs), .in1({adder_2_out[31:28], id_ex_1_ir_2[25:0], 2'b00}), .out(multiplexer_1_out),
    .sel(not_1_out));
  Hex_Digit_Display hex_digit_display_1 (.value(LedData[31:28]));  // open: dp
  // Probe on IF_PC[19:0]
  // Mips_Probe mips_probe_1: pin names not known; wires that end beside it: IF_IR
  Multiplexer #(.select(2), .width(32), .disabled("Z"), .enable("false")) multiplexer_2 (
    .in0(adder_1_out), .in1(multiplexer_1_out), .in2(adder_3_out), .out(multiplexer_2_out),
    .sel(id_ex_1_jmp_2));  // open: in3
  Hex_Digit_Display hex_digit_display_2 (.value(LedData[23:20]));  // open: dp
  Hex_Digit_Display hex_digit_display_3 (.value(LedData[27:24]));  // open: dp
  // Probe on ID_PC[19:0]
  // Mips_Probe mips_probe_2: pin names not known; wires that end beside it: ID_IR
  not not_2 (not_2_out, Stop);
  Counter #(.width(16), .max('hffff), .ongoal("wrap"), .trigger("rising"), .behavior("new")) counter_1 (
    .count(not_2_out), .Q(\总周期数 ), .clk(CLK));  // open: load, D, carry, clr, preset, down
  and and_1 (and_1_out, ~Stop, ~EX, ~MEM);  // AND_Gate
  Hex_Digit_Display hex_digit_display_4 (.value(LedData[15:12]));  // open: dp
  Hex_Digit_Display hex_digit_display_5 (.value(LedData[19:16]));  // open: dp
  assign controlled_buffer_1_out = display ? a0 : 32'bz;  // Controlled_Buffer controlled_buffer_1
  Register #(.width(32), .trigger("rising"), .Select("low")) PC (
    .D(multiplexer_2_out), .en(and_1_out), .Q(IF_PC), .clk(CLK));  // open: clr
  Hex_Digit_Display hex_digit_display_6 (.value(LedData[11:8]));  // open: dp
  Hex_Digit_Display hex_digit_display_7 (.value(LedData[7:4]));  // open: dp
  Clock #(.highDuration(1), .lowDuration(1)) clock_1 (.out(CLK));
  // Probe on EX_PC[19:0]
  // Mips_Probe mips_probe_3: pin names not known; wires that end beside it: EX_IR
  Register #(.width(32), .trigger("rising"), .Select("low")) register_1 (
    .D(controlled_buffer_1_out), .Q(LedData), .clk(CLK));  // open: en, clr
  Hex_Digit_Display hex_digit_display_8 (.value(LedData[3:0]));  // open: dp
  // Mips_Probe mips_probe_4: pin names not known; wires that end beside it: mips_probe_4_p1
  ROM #(.addrWidth(10), .dataWidth(32), .Select("high")) rom_1 (.addr(IF_PC[11:2]), .data(mips_probe_4_p1));
  Adder #(.width(32)) adder_1 (.a(32'h4), .b(IF_PC), .out(adder_1_out));  // open: cin, cout
  and and_2 (and_2_out, JUMP, CLK);
  // Probe on \总周期数 
  // Probe on M_PC[19:0]
  // Mips_Probe mips_probe_5: pin names not known; wires that end beside it: MEM_IR
  // Probe on \总周期数 
  // Probe on \无条件分支数 
  // Probe on \条件分支成功数 
  // Probe on \插入气泡数 
  // Probe on \LoadUse次数 
  IF_ID if_id_1 (
    .IR(mips_probe_4_p1), .PC(IF_PC), .IR_2(if_id_1_ir_2), .PC_2(ID_PC), .CLK(CLK), .clr(and_2_out),
    .EN(and_3_out));
  and and_3 (and_3_out, ~EX, ~Stop, ~MEM);  // AND_Gate
  // Probe on IF_PC[11:0]
  // Probe on WB_PC[19:0]
  // Mips_Probe mips_probe_6: pin names not known; wires that end beside it: WB_IR, mips_probe_6_p2
  // Mips_Probe mips_probe_7: pin names not known; wires that end beside it: if_id_1_ir_2, if_id_1_ir_2[25:21]
  // Probe on ID_PC[11:0]
  // Probe on EX_PC[11:0]
  \单周期硬布线控制器  \u_单周期硬布线控制器_1  (
    .Func(if_id_1_ir_2[5:0]), .OP(if_id_1_ir_2[31:26]), .ALU_OP(\单周期硬布线控制器_1_alu_op ),
    .MemToReg(\单周期硬布线控制器_1_memtoreg ), .MemWrite(\单周期硬布线控制器_1_memwrite ), .ALU_SRC(\单周期硬布线控制器_1_alu_src ),
    .RegWrite(\单周期硬布线控制器_1_regwrite ), .SysCALL(\单周期硬布线控制器_1_syscall ), .SignedExt(SignedExt),
    .RegDst(\单周期硬布线控制器_1_regdst ), .JR(\单周期硬布线控制器_1_jr ), .JMP(\单周期硬布线控制器_1_jmp ), .Beq(\单周期硬布线控制器_1_beq ),
    .JAL(\单周期硬布线控制器_1_jal ), .Bne(\单周期硬布线控制器_1_bne ), .SB(SB), .BLTZ(\单周期硬布线控制器_1_bltz ), .VAR(VAR));  // open: ERET, MT_MF, MFC0, MTC0
  Multiplexer #(.select(1), .width(5), .disabled("Z"), .enable("false")) multiplexer_3 (
    .in0(if_id_1_ir_2[25:21]), .in1(5'b00010), .out(multiplexer_3_out), .sel(\单周期硬布线控制器_1_syscall ));
  Multiplexer #(.select(1), .width(5), .disabled("Z"), .enable("false")) multiplexer_4 (
    .in0(if_id_1_ir_2[20:16]), .in1(5'b00100), .out(multiplexer_4_out), .sel(\单周期硬布线控制器_1_syscall ));
  // Probe on M_PC[11:0]
  \源寄存器使用情况  \u_源寄存器使用情况_1  (
    .OP0(if_id_1_ir_2[26]), .OP1(if_id_1_ir_2[27]), .OP2(if_id_1_ir_2[28]), .OP3(if_id_1_ir_2[29]),
    .OP4(if_id_1_ir_2[30]), .OP5(if_id_1_ir_2[31]), .F0(if_id_1_ir_2[0]), .F1(if_id_1_ir_2[1]),
    .F2(if_id_1_ir_2[2]), .F3(if_id_1_ir_2[3]), .F4(if_id_1_ir_2[4]), .F5(if_id_1_ir_2[5]),
    .R1_used(\源寄存器使用情况_1_r1_used ), .R2_used(\源寄存器使用情况_1_r2_used ));
  // Probe on WB_PC[11:0]
  Register #(.width(1), .trigger("rising"), .Select("low")) register_2 (
    .D(MEM), .Q(register_2_q), .clk(CLK), .clr(CLR));  // open: en
  Register #(.width(1), .trigger("rising"), .Select("low")) register_3 (
    .D(EX), .Q(register_3_q), .clk(CLK), .clr(CLR));  // open: en
  Multiplexer #(.select(1), .width(5), .disabled("Z"), .enable("false")) multiplexer_5 (
    .in0(multiplexer_4_out), .in1(if_id_1_ir_2[15:11]), .out(multiplexer_5_out), .sel(\单周期硬布线控制器_1_regdst ));
  MIPS_Regifile mips_regifile_1 (
    .Din(RDin), .Clk(CLK), .R1(mips_regifile_1_r1), .R2(mips_regifile_1_r2), .WE(RegWrite), .W_num(W_num),
    .R1_num(multiplexer_3_out), .R2_num(multiplexer_4_out));
  assign bit_extender_1_out = {{16{1'b0}}, if_id_1_ir_2[15:0]};  // Bit_Extender bit_extender_1
  Multiplexer #(.select(1), .width(32), .disabled("Z"), .enable("false")) multiplexer_6 (
    .in0(bit_extender_1_out), .in1(bit_extender_2_out), .out(multiplexer_6_out), .sel(SignedExt));
  assign bit_extender_2_out = {{16{if_id_1_ir_2[15]}}, if_id_1_ir_2[15:0]};  // Bit_Extender bit_extender_2
  or or_1 (or_1_out, EX, MEM, and_2_out);
  \数据相关检测  \u_数据相关检测_1  (
    .R1_num(multiplexer_3_out), .EX_WriteReg_num(id_ex_1_writereg_num_2),
    .MEM_WriteReg_num(ex_mem_1_writereg_num_2), .R2_num(multiplexer_4_out), .EX(EX), .MEM(MEM),
    .R1_used(\源寄存器使用情况_1_r1_used ), .R2_used(\源寄存器使用情况_1_r2_used ), .EX_RegWrite(id_ex_1_regwrite_2),
    .MEM_RegWrite(ex_mem_1_regwrite_2));
  ID_EX id_ex_1 (
    .JR(\单周期硬布线控制器_1_jr ), .JMP(\单周期硬布线控制器_1_jmp ), .BLTZ(\单周期硬布线控制器_1_bltz ), .Beq(\单周期硬布线控制器_1_beq ),
    .Bne(\单周期硬布线控制器_1_bne ), .WB(\单周期硬布线控制器_1_memtoreg ), .MEM(\单周期硬布线控制器_1_memwrite ),
    .AluOp(\单周期硬布线控制器_1_alu_op ), .SrcB(\单周期硬布线控制器_1_alu_src ), .RegWrite(\单周期硬布线控制器_1_regwrite ),
    .JAL(\单周期硬布线控制器_1_jal ), .WriteReg_num(multiplexer_7_out), .Syscall(\单周期硬布线控制器_1_syscall ),
    .A(mips_regifile_1_r1), .B(mips_regifile_1_r2), .IMM(multiplexer_6_out), .SB(SB), .VAR(VAR),
    .IR(if_id_1_ir_2), .PC(ID_PC), .JR_2(id_ex_1_jr_2), .JMP_2(id_ex_1_jmp_2[0]), .BLTZ_2(id_ex_1_bltz_2),
    .Beq_2(id_ex_1_beq_2), .Bne_2(id_ex_1_bne_2), .WB_2(id_ex_1_wb_2), .MEM_2(id_ex_1_mem_2),
    .AluOp_2(id_ex_1_aluop_2), .SrcB_2(id_ex_1_srcb_2), .RegWrite_2(id_ex_1_regwrite_2),
    .JAL_2(id_ex_1_jal_2), .WriteReg_num_2(id_ex_1_writereg_num_2), .Syscall_2(id_ex_1_syscall_2),
    .A_2(R_rs), .B_2(a0), .IMM_2(id_ex_1_imm_2), .SB_2(id_ex_1_sb_2), .VAR_2(id_ex_1_var_2),
    .IR_2(id_ex_1_ir_2), .PC_2(EX_PC), .CLK(CLK), .clr(CLR), .EN(not_4_out));
  Multiplexer #(.select(1), .width(5), .disabled("Z"), .enable("false")) multiplexer_7 (
    .in0(multiplexer_5_out), .in1({5{1'b1}}), .out(multiplexer_7_out), .sel(\单周期硬布线控制器_1_jal ));
  or or_2 (CLR, register_2_q, register_3_q, and_2_out);
  and and_4 (and_4_out, id_ex_1_bltz_2, mips_alu_1_result[0]);
  and and_5 (and_5_out, id_ex_1_beq_2, mips_alu_1_equal);
  and and_6 (and_6_out, id_ex_1_bne_2, ~mips_alu_1_equal);  // AND_Gate
  and and_7 (and_7_out, or_1_out, ~Stop);  // AND_Gate
  Counter #(.width(16), .max('hffff), .ongoal("wrap"), .trigger("rising"), .behavior("new")) counter_2 (
    .count(and_7_out), .Q(\插入气泡数 ), .clk(CLK));  // open: load, D, carry, clr, preset, down
  or or_3 (id_ex_1_jmp_2[1], and_4_out, and_5_out, and_6_out);
  not not_3 (not_3_out, display);
  Comparator #(.width(32), .mode("twosComplement")) comparator_1 (.a(32'h22), .b(R_rs), .eq(display));  // open: gt, lt
  not not_4 (not_4_out, Stop);
  or or_4 (or_4_out, id_ex_1_jmp_2[0], id_ex_1_jmp_2[1]);
  Counter #(.width(16), .max('hffff), .ongoal("wrap"), .trigger("rising"), .behavior("new")) counter_3 (
    .count(id_ex_1_jmp_2[1]), .Q(\条件分支成功数 ), .clk(CLK));  // open: load, D, carry, clr, preset, down
  D_Flip_Flop #(.trigger("rising"), .Pre_Clr_Positions("ABOVE_BELOW"), .NegatePresetClear("false"), .enable("true"), .NewFFLayout("true")) d_ff_1 (
    .clk(CLK), .D(not_3_out), .Q(d_ff_1_q), .en(id_ex_1_syscall_2), .reset(Go));  // open: Qn, preset
  Multiplexer #(.select(1), .width(5), .disabled("Z"), .enable("false")) multiplexer_8 (
    .in0(R_rs[4:0]), .in1(id_ex_1_ir_2[10:6]), .out(multiplexer_8_out), .sel(not_5_out));
  not not_5 (not_5_out, id_ex_1_var_2);
  // Mips_Probe mips_probe_8: pin names not known; wires that end beside it: mips_regifile_1_r1, mips_probe_8_p2, mips_probe_8_p2, id_ex_1_ir_2
  Adder #(.width(32)) adder_2 (.a(32'h4), .b(EX_PC), .out(adder_2_out));  // open: cin, cout
  Shifter #(.width(32), .shift("ll")) shifter_1 (.in(id_ex_1_imm_2), .\dist (5'b00010), .out(shifter_1_out));
  Register #(.width(1), .trigger("rising"), .Select("low")) \u_跳转  (
    .D(or_4_out), .Q(JUMP), .clk(CLK), .clr(CLR));  // open: en
  Counter #(.width(16), .max('hffff), .ongoal("wrap"), .trigger("rising"), .behavior("new")) counter_4 (
    .count(id_ex_1_jmp_2[0]), .Q(\无条件分支数 ), .clk(CLK));  // open: load, D, carry, clr, preset, down
  Multiplexer #(.select(1), .width(32), .disabled("Z"), .enable("false")) multiplexer_9 (
    .in0(a0), .in1(id_ex_1_imm_2), .out(multiplexer_9_out), .sel(id_ex_1_srcb_2));
  Adder #(.width(32)) adder_3 (.a(shifter_1_out), .b(adder_2_out), .out(adder_3_out));  // open: cin, cout
  MIPS_ALU mips_alu_1 (
    .X(R_rs), .Y(multiplexer_9_out), .AluOP(id_ex_1_aluop_2), .Equal(mips_alu_1_equal),
    .Result(mips_alu_1_result), .shamt(multiplexer_8_out));  // open: Result_2
  EX_MEM ex_mem_1 (
    .WB(id_ex_1_wb_2), .MEM(id_ex_1_mem_2), .RegWrite(id_ex_1_regwrite_2), .JAL(id_ex_1_jal_2),
    .WriteReg_num(id_ex_1_writereg_num_2), .AluResult(mips_alu_1_result), .B(a0), .SB(id_ex_1_sb_2),
    .IR(id_ex_1_ir_2), .PC(EX_PC), .WB_2(ex_mem_1_wb_2), .MEM_2(MemWrite), .RegWrite_2(ex_mem_1_regwrite_2),
    .JAL_2(ex_mem_1_jal_2), .WriteReg_num_2(ex_mem_1_writereg_num_2), .AluResult_2(ex_mem_1_aluresult_2),
    .B_2(ex_mem_1_b_2), .SB_2(ex_mem_1_sb_2), .IR_2(ex_mem_1_ir_2), .PC_2(M_PC), .CLK(CLK), .EN(not_6_out),
    .stop(d_ff_1_q), .stop_2(Stop));  // open: clr
  // Mips_Probe mips_probe_9: pin names not known; wires that end beside it: ex_mem_1_ir_2
  not not_6 (not_6_out, Stop);
  SB sb_1 (.\原数据 (ram_1_data), .addr(ex_mem_1_aluresult_2[1:0]), .data(ex_mem_1_b_2[7:0]), .out_4(sb_1_out_4));
  Multiplexer #(.select(1), .width(32), .disabled("Z"), .enable("false")) multiplexer_10 (
    .in0(sb_1_out_4), .in1(ex_mem_1_b_2), .out(MDin), .sel(not_7_out));
  not not_7 (not_7_out, ex_mem_1_sb_2);
  RAM #(.addrWidth(10), .dataWidth(32), .bus("separate"), .Select("high")) ram_1 (
    .addr(ex_mem_1_aluresult_2[11:2]), .din(MDin), .data(ram_1_data), .str(MemWrite), .clk(CLK));  // open: sel, ld, clr
  MEM_WB mem_wb_1 (
    .WB(ex_mem_1_wb_2), .RegWrite(ex_mem_1_regwrite_2), .JAL(ex_mem_1_jal_2),
    .WriteReg_num(ex_mem_1_writereg_num_2), .AluResult(ex_mem_1_aluresult_2), .IR(ex_mem_1_ir_2), .PC(M_PC),
    .WB_2(mem_wb_1_wb_2), .RegWrite_2(RegWrite), .JAL_2(mem_wb_1_jal_2), .WriteReg_num_2(W_num),
    .AluResult_2(mem_wb_1_aluresult_2), .PC_2(WB_PC), .CLK(CLK), .MD(ram_1_data), .MD_2(mem_wb_1_md_2),
    .EN(not_8_out));  // open: IR_2, clr
  not not_8 (not_8_out, Stop);
  Multiplexer #(.select(1), .width(32), .disabled("Z"), .enable("false")) multiplexer_11 (
    .in0(mem_wb_1_aluresult_2), .in1(mem_wb_1_md_2), .out(multiplexer_11_out), .sel(mem_wb_1_wb_2));
  Adder #(.width(32)) adder_4 (.a(32'h4), .b(WB_PC), .out(adder_4_out));  // open: cin, cout
  Multiplexer #(.select(1), .width(32), .disabled("Z"), .enable("false")) multiplexer_12 (
    .in0(multiplexer_11_out), .in1(adder_4_out), .out(RDin), .sel(mem_wb_1_jal_2));

  // Other names for the same wires on the sheet: MEM_PC[31:0] = M_PC

  // Notes on the sheet:
  //   中断源
  //   时空图监测，可删除
  //   中断等待指示
  //   数码管输出
  //   PC = JumpAddr
  //   contents of rom_1 (hex, n*v repeats v):
  //   20110001 8000c05 20110001 20120002 20130003 8000c09 20110001 20120002 20130003 8000c0d 20110001
  //   20120002 20130003 8000c11 20110001 20120002 20130003 c000cb8 20100001 20110001 118fc0 112020
  //   20020022 c 118882 12200001 8000c15 112020 20020022 c 20110001 118880 112020 20020022 c 12200001
  //   8000c1f 20110001 118fc0 112020 20020022 c 1188c3 112020 20020022 c 118903 112020 20020022 c 118903
  //   112020 20020022 c 118903 112020 20020022 c 118903 112020 20020022 c 118903 112020 20020022 c 118903
  //   112020 20020022 c 118903 112020 20020022 c 20100001 109fc0 139fc3 8021 2012000c 24160003 26100001
  //   3210000f 20080008 20090001 139900 2709825 132020 20020022 c 1094022 1500fff9 22100001 2018000f
  //   2188024 108700 20080008 20090001 139902 2709825 132021 20020022 c 1094022 1500fff9 108702 2c9b022
  //   12c00001 8000c50 4020 1084027 84400 3508ffff 82021 20020022 c 2010ffff 20110000 ae300000 22100001
  //   22310004 ae300000 22100001 22310004 ae300000 22100001 22310004 ae300000 22100001 22310004 ae300000
  //   22100001 22310004 ae300000 22100001 22310004 ae300000 22100001 22310004 ae300000 22100001 22310004
  //   ae300000 22100001 22310004 ae300000 22100001 22310004 ae300000 22100001 22310004 ae300000 22100001
  //   22310004 ae300000 22100001 22310004 ae300000 22100001 22310004 ae300000 22100001 22310004 ae300000
  //   22100001 22310004 22100001 8020 2011003c 8e130000 8e340000 274402a 11000002 ae330000 ae140000
  //   2231fffc 1611fff8 102020 20020022 c 22100004 2011003c 1611fff2 20020032 c 20100000 22100001 102020
  //   20020022 c 22100002 102020 20020022 c 22100003 102020 20020022 c 22100004 102020 20020022 c 22100005
  //   102020 20020022 c 22100006 102020 20020022 c 22100007 102020 20020022 c 22100008 102020 20020022
  //   20020022 c 3e00008
  //   JMP
  //   JR
  //   OP
  //   OP
  //   Func
  //   Func
  //   rd
  //   rs
  //   $v0
  //   rt
  //   $a0
  //   imm
  //   BLTZ
  //   Beq
  //   Bne
  //   MemToReg
  //   MemWrite
  //   AluOP
  //   AluSrcB
  //   RegWrite
  //   JAL
  //   RegDst
  //   流水调试日志用
  //   Address
  //   为方便自动评测，需要输出流水线各段保存的PC值，注意是PC不是PC+4，另外ID段寄存器写入信息，Mem段内存写入信息也要输出
endmodule

module \重定向流水线  (
  output RegWrite,
  output MemWrite,
  output [31:0] IF_PC,
  output [31:0] ID_PC,
  output [31:0] EX_PC,
  output [31:0] M_PC,
  output [31:0] WB_PC,
  output [31:0] RDin,
  output [31:0] MDin,
  output [31:0] LedData
);

  wire and_1_out, and_2_out, and_3_out, and_5_out, and_6_out, and_7_out, CLK, CLR, comparator_1_eq, d_ff_1_q,
       display, EX, ex_mem_1_jal_2, ex_mem_1_regwrite_2, ex_mem_1_sb_2, ex_mem_1_wb_2, Go, id_ex_1_beq_2,
       id_ex_1_bltz_2, id_ex_1_bne_2, id_ex_1_jal_2, id_ex_1_jr_2, id_ex_1_mem_2, id_ex_1_regwrite_2,
       id_ex_1_sb_2, id_ex_1_srcb_2, id_ex_1_syscall_2, id_ex_1_var_2, id_ex_1_wb_2, IR1, IR2, IR3, JUMP,
       LoadUse, mem_wb_1_jal_2, mem_wb_1_wb_2, mips_alu_1_equal, not_1_out, not_2_out, not_3_out, not_4_out,
       not_5_out, not_6_out, not_7_out, not_8_out, or_1_out, or_5_out, register_2_q, RST, SB, SignedExt,
       Stop, VAR, W1, W2, W3, \单周期硬布线控制器_1_alu_src , \单周期硬布线控制器_1_beq , \单周期硬布线控制器_1_bltz ,
       \单周期硬布线控制器_1_bne , \单周期硬布线控制器_1_jal , \单周期硬布线控制器_1_jmp , \单周期硬布线控制器_1_jr , \单周期硬布线控制器_1_memtoreg ,
       \单周期硬布线控制器_1_memwrite , \单周期硬布线控制器_1_regdst , \单周期硬布线控制器_1_regwrite , \单周期硬布线控制器_1_syscall ,
       \源寄存器使用情况_1_r1_used , \源寄存器使用情况_1_r2_used ;
  wire [1:0] id_ex_1_jmp_2, R1, R2;
  wire [3:0] forward_1_forward, id_ex_1_aluop_2, \单周期硬布线控制器_1_alu_op ;
  wire [4:0] ex_mem_1_writereg_num_2, id_ex_1_writereg_num_2, multiplexer_3_out, multiplexer_4_out,
       multiplexer_5_out, multiplexer_7_out, multiplexer_8_out, W_num;
  wire [15:0] \LoadUse次数 , \总周期数 , \插入气泡数 , \无条件分支数 , \条件分支成功数 ;
  wire [31:0] a0, adder_1_out, adder_2_out, adder_3_out, adder_4_out, bit_extender_1_out, bit_extender_2_out,
       EX_IR, ex_mem_1_aluresult_2, ex_mem_1_b_2, ex_mem_1_ir_2, id_ex_1_b_2, id_ex_1_imm_2, id_ex_1_ir_2,
       ID_IR, if_id_1_ir_2, IF_IR, MEM_IR, mem_wb_1_aluresult_2, mem_wb_1_md_2, mips_alu_1_result,
       mips_probe_9_p2, mips_regifile_1_r1, mips_regifile_1_r2, multiplexer_1_out, multiplexer_2_out,
       multiplexer_6_out, multiplexer_9_out, multiplexer_11_out, multiplexer_13_out, R_rs, ram_1_data,
       rom_1_data, sb_1_out_4, shifter_1_out, WB_IR;

  Button \u_总复位  (.out(RST));
  Button _1 (.out(IR1));
  Button _2 (.out(IR2));
  Button _3 (.out(IR3));
  // Probe on \总周期数 
  // Probe on \总周期数 
  Button \u_继续运行  (.out(Go));
  LED #(.active("true")) led_1 (.in(W1));
  LED #(.active("true")) led_2 (.in(W2));
  LED #(.active("true")) led_3 (.in(W3));
  not not_1 (not_1_out, id_ex_1_jr_2);
  Multiplexer #(.select(1), .width(32), .disabled("Z"), .enable("false")) multiplexer_1 (
    .in0(R_rs), .in1({adder_2_out[31:28], id_ex_1_ir_2[25:0], 2'b00}), .out(multiplexer_1_out),
    .sel(not_1_out));
  Hex_Digit_Display hex_digit_display_1 (.value(LedData[31:28]));  // open: dp
  // Probe on IF_PC[19:0]
  // Mips_Probe mips_probe_1: pin names not known; wires that end beside it: IF_IR
  Multiplexer #(.select(2), .width(32), .disabled("Z"), .enable("false")) multiplexer_2 (
    .in0(adder_1_out), .in1(multiplexer_1_out), .in2(adder_3_out), .out(multiplexer_2_out),
    .sel(id_ex_1_jmp_2));  // open: in3
  Hex_Digit_Display hex_digit_display_2 (.value(LedData[27:24]));  // open: dp
  Hex_Digit_Display hex_digit_display_3 (.value(LedData[23:20]));  // open: dp
  // Probe on ID_PC[19:0]
  // Mips_Probe mips_probe_2: pin names not known; wires that end beside it: ID_IR
  not not_2 (not_2_out, Stop);
  Counter #(.width(16), .max('hffff), .ongoal("wrap"), .trigger("rising"), .behavior("new")) counter_1 (
    .count(not_2_out), .Q(\总周期数 ), .clk(CLK));  // open: load, D, carry, clr, preset, down
  and and_1 (and_1_out, ~Stop, ~LoadUse);  // AND_Gate
  Hex_Digit_Display hex_digit_display_4 (.value(LedData[15:12]));  // open: dp
  Hex_Digit_Display hex_digit_display_5 (.value(LedData[19:16]));  // open: dp
  Register #(.width(32), .trigger("rising"), .Select("low")) PC (
    .D(multiplexer_2_out), .en(and_1_out), .Q(IF_PC), .clk(CLK));  // open: clr
  Hex_Digit_Display hex_digit_display_6 (.value(LedData[11:8]));  // open: dp
  Hex_Digit_Display hex_digit_display_7 (.value(LedData[7:4]));  // open: dp
  Clock #(.highDuration(1), .lowDuration(1)) clock_1 (.out(CLK));
  // Probe on EX_PC[19:0]
  // Mips_Probe mips_probe_3: pin names not known; wires that end beside it: EX_IR
  Register #(.width(32), .trigger("rising"), .Select("low")) register_1 (
    .D(a0), .en(display), .Q(LedData), .clk(CLK));  // open: clr
  Hex_Digit_Display hex_digit_display_8 (.value(LedData[3:0]));  // open: dp
  ROM #(.addrWidth(10), .dataWidth(32), .Select("high")) rom_1 (.addr(IF_PC[11:2]), .data(rom_1_data));
  Adder #(.width(32)) adder_1 (.a(32'h4), .b(IF_PC), .out(adder_1_out));  // open: cin, cout
  and and_2 (and_2_out, JUMP, CLK);
  // Probe on \总周期数 
  // Probe on M_PC[19:0]
  // Mips_Probe mips_probe_4: pin names not known; wires that end beside it: MEM_IR
  // Mips_Probe mips_probe_5: pin names not known; wires that end beside it: rom_1_data
  // Probe on \总周期数 
  // Probe on \无条件分支数 
  // Probe on \条件分支成功数 
  // Probe on \插入气泡数 
  // Probe on \LoadUse次数 
  IF_ID if_id_1 (
    .IR(rom_1_data), .PC(IF_PC), .IR_2(if_id_1_ir_2), .PC_2(ID_PC), .CLK(CLK), .clr(and_2_out), .EN(and_3_out));
  // Probe on IF_PC[11:0]
  // Probe on WB_PC[19:0]
  // Mips_Probe mips_probe_6: pin names not known; wires that end beside it: WB_IR
  // Mips_Probe mips_probe_7: pin names not known; wires that end beside it: if_id_1_ir_2, if_id_1_ir_2[25:21]
  and and_3 (and_3_out, ~LoadUse, ~Stop);  // AND_Gate
  // Probe on ID_PC[11:0]
  // Probe on EX_PC[11:0]
  \单周期硬布线控制器  \u_单周期硬布线控制器_1  (
    .Func(if_id_1_ir_2[5:0]), .OP(if_id_1_ir_2[31:26]), .ALU_OP(\单周期硬布线控制器_1_alu_op ),
    .MemToReg(\单周期硬布线控制器_1_memtoreg ), .MemWrite(\单周期硬布线控制器_1_memwrite ), .ALU_SRC(\单周期硬布线控制器_1_alu_src ),
    .RegWrite(\单周期硬布线控制器_1_regwrite ), .SysCALL(\单周期硬布线控制器_1_syscall ), .SignedExt(SignedExt),
    .RegDst(\单周期硬布线控制器_1_regdst ), .JR(\单周期硬布线控制器_1_jr ), .JMP(\单周期硬布线控制器_1_jmp ), .Beq(\单周期硬布线控制器_1_beq ),
    .JAL(\单周期硬布线控制器_1_jal ), .Bne(\单周期硬布线控制器_1_bne ), .SB(SB), .BLTZ(\单周期硬布线控制器_1_bltz ), .VAR(VAR));  // open: ERET, MT_MF, MFC0, MTC0
  Multiplexer #(.select(1), .width(5), .disabled("Z"), .enable("false")) multiplexer_3 (
    .in0(if_id_1_ir_2[25:21]), .in1(5'b00010), .out(multiplexer_3_out), .sel(\单周期硬布线控制器_1_syscall ));
  Multiplexer #(.select(1), .width(5), .disabled("Z"), .enable("false")) multiplexer_4 (
    .in0(if_id_1_ir_2[20:16]), .in1(5'b00100), .out(multiplexer_4_out), .sel(\单周期硬布线控制器_1_syscall ));
  Comparator #(.width(6), .mode("twosComplement")) comparator_1 (
    .a(id_ex_1_ir_2[31:26]), .b(6'b100011), .eq(comparator_1_eq));  // open: gt, lt
  // Probe on M_PC[11:0]
  \源寄存器使用情况  \u_源寄存器使用情况_1  (
    .OP0(if_id_1_ir_2[26]), .OP1(if_id_1_ir_2[27]), .OP2(if_id_1_ir_2[28]), .OP3(if_id_1_ir_2[29]),
    .OP4(if_id_1_ir_2[30]), .OP5(if_id_1_ir_2[31]), .F0(if_id_1_ir_2[0]), .F1(if_id_1_ir_2[1]),
    .F2(if_id_1_ir_2[2]), .F3(if_id_1_ir_2[3]), .F4(if_id_1_ir_2[4]), .F5(if_id_1_ir_2[5]),
    .R1_used(\源寄存器使用情况_1_r1_used ), .R2_used(\源寄存器使用情况_1_r2_used ));
  and and_4 (LoadUse, comparator_1_eq, EX);
  // Probe on WB_PC[11:0]
  Counter #(.width(16), .max('hffff), .ongoal("wrap"), .trigger("rising"), .behavior("new")) counter_2 (
    .count(LoadUse), .Q(\LoadUse次数 ), .clk(CLK));  // open: load, D, carry, clr, preset, down
  Register #(.width(1), .trigger("rising"), .Select("low")) register_2 (
    .D(LoadUse), .Q(register_2_q), .clk(CLK), .clr(CLR));  // open: en
  forward forward_1 (
    .R1_num(multiplexer_3_out), .EX_WriteReg_num(id_ex_1_writereg_num_2),
    .MEM_WriteReg_num(ex_mem_1_writereg_num_2), .R2_num(multiplexer_4_out), .forward(forward_1_forward),
    .R1_used(\源寄存器使用情况_1_r1_used ), .R2_used(\源寄存器使用情况_1_r2_used ), .EX_RegWrite(id_ex_1_regwrite_2),
    .MEM_RegWrite(ex_mem_1_regwrite_2));
  Multiplexer #(.select(1), .width(5), .disabled("Z"), .enable("false")) multiplexer_5 (
    .in0(multiplexer_4_out), .in1(if_id_1_ir_2[15:11]), .out(multiplexer_5_out), .sel(\单周期硬布线控制器_1_regdst ));
  MIPS_Regifile mips_regifile_1 (
    .Din(RDin), .Clk(CLK), .R1(mips_regifile_1_r1), .R2(mips_regifile_1_r2), .WE(RegWrite), .W_num(W_num),
    .R1_num(multiplexer_3_out), .R2_num(multiplexer_4_out));
  assign bit_extender_1_out = {{16{1'b0}}, if_id_1_ir_2[15:0]};  // Bit_Extender bit_extender_1
  Multiplexer #(.select(1), .width(32), .disabled("Z"), .enable("false")) multiplexer_6 (
    .in0(bit_extender_1_out), .in1(bit_extender_2_out), .out(multiplexer_6_out), .sel(SignedExt));
  assign bit_extender_2_out = {{16{if_id_1_ir_2[15]}}, if_id_1_ir_2[15:0]};  // Bit_Extender bit_extender_2
  or or_1 (or_1_out, LoadUse, CLR);
  or or_2 (CLR, register_2_q, and_2_out);
  ID_EX id_ex_1 (
    .JR(\单周期硬布线控制器_1_jr ), .JMP(\单周期硬布线控制器_1_jmp ), .BLTZ(\单周期硬布线控制器_1_bltz ), .Beq(\单周期硬布线控制器_1_beq ),
    .Bne(\单周期硬布线控制器_1_bne ), .WB(\单周期硬布线控制器_1_memtoreg ), .MEM(\单周期硬布线控制器_1_memwrite ),
    .AluOp(\单周期硬布线控制器_1_alu_op ), .SrcB(\单周期硬布线控制器_1_alu_src ), .RegWrite(\单周期硬布线控制器_1_regwrite ),
    .JAL(\单周期硬布线控制器_1_jal ), .WriteReg_num(multiplexer_7_out), .Syscall(\单周期硬布线控制器_1_syscall ),
    .A(mips_regifile_1_r1), .B(mips_regifile_1_r2), .IMM(multiplexer_6_out), .SB(SB), .VAR(VAR),
    .IR(if_id_1_ir_2), .PC(ID_PC), .JR_2(id_ex_1_jr_2), .JMP_2(id_ex_1_jmp_2[0]), .BLTZ_2(id_ex_1_bltz_2),
    .Beq_2(id_ex_1_beq_2), .Bne_2(id_ex_1_bne_2), .WB_2(id_ex_1_wb_2), .MEM_2(id_ex_1_mem_2),
    .AluOp_2(id_ex_1_aluop_2), .SrcB_2(id_ex_1_srcb_2), .RegWrite_2(id_ex_1_regwrite_2),
    .JAL_2(id_ex_1_jal_2), .WriteReg_num_2(id_ex_1_writereg_num_2), .Syscall_2(id_ex_1_syscall_2),
    .A_2(R_rs), .B_2(id_ex_1_b_2), .IMM_2(id_ex_1_imm_2), .SB_2(id_ex_1_sb_2), .VAR_2(id_ex_1_var_2),
    .IR_2(id_ex_1_ir_2), .PC_2(EX_PC), .CLK(CLK), .clr(CLR), .EN(not_4_out));
  Multiplexer #(.select(1), .width(5), .disabled("Z"), .enable("false")) multiplexer_7 (
    .in0(multiplexer_5_out), .in1({5{1'b1}}), .out(multiplexer_7_out), .sel(\单周期硬布线控制器_1_jal ));
  Register #(.width(4), .trigger("rising"), .Select("low")) register_3 (
    .D(forward_1_forward), .Q({R2, R1}), .clk(CLK), .clr(CLR));  // open: en
  and and_5 (and_5_out, id_ex_1_bltz_2, mips_alu_1_result[0]);
  and and_6 (and_6_out, id_ex_1_beq_2, mips_alu_1_equal);
  and and_7 (and_7_out, id_ex_1_bne_2, ~mips_alu_1_equal);  // AND_Gate
  Comparator #(.width(32), .mode("twosComplement")) comparator_2 (
    .a(32'h22), .b(multiplexer_9_out), .eq(display));  // open: gt, lt
  or or_3 (id_ex_1_jmp_2[1], and_5_out, and_6_out, and_7_out);
  D_Flip_Flop #(.trigger("rising"), .Pre_Clr_Positions("ABOVE_BELOW"), .NegatePresetClear("false"), .enable("true"), .NewFFLayout("true")) d_ff_1 (
    .clk(CLK), .D(not_3_out), .Q(d_ff_1_q), .en(id_ex_1_syscall_2), .reset(Go));  // open: Qn, preset
  not not_3 (not_3_out, display);
  not not_4 (not_4_out, Stop);
  Counter #(.width(16), .max('hffff), .ongoal("wrap"), .trigger("rising"), .behavior("new")) counter_3 (
    .count(or_1_out), .Q(\插入气泡数 ), .clk(CLK));  // open: load, D, carry, clr, preset, down
  or or_4 (EX, forward_1_forward[0], forward_1_forward[2]);
  or or_5 (or_5_out, id_ex_1_jmp_2[0], id_ex_1_jmp_2[1]);
  Counter #(.width(16), .max('hffff), .ongoal("wrap"), .trigger("rising"), .behavior("new")) counter_4 (
    .count(id_ex_1_jmp_2[1]), .Q(\条件分支成功数 ), .clk(CLK));  // open: load, D, carry, clr, preset, down
  Multiplexer #(.select(1), .width(5), .disabled("Z"), .enable("false")) multiplexer_8 (
    .in0(R_rs[4:0]), .in1(id_ex_1_ir_2[10:6]), .out(multiplexer_8_out), .sel(not_5_out));
  not not_5 (not_5_out, id_ex_1_var_2);
  Shifter #(.width(32), .shift("ll")) shifter_1 (.in(id_ex_1_imm_2), .\dist (5'b00010), .out(shifter_1_out));
  Register #(.width(1), .trigger("rising"), .Select("low")) \u_跳转  (
    .D(or_5_out), .Q(JUMP), .clk(CLK), .clr(CLR));  // open: en
  Counter #(.width(16), .max('hffff), .ongoal("wrap"), .trigger("rising"), .behavior("new")) counter_5 (
    .count(id_ex_1_jmp_2[0]), .Q(\无条件分支数 ), .clk(CLK));  // open: load, D, carry, clr, preset, down
  Multiplexer #(.select(2), .width(32), .disabled("Z"), .enable("false")) multiplexer_9 (
    .in0(R_rs), .in1(ex_mem_1_aluresult_2), .in2(RDin), .in3(ex_mem_1_aluresult_2), .out(multiplexer_9_out),
    .sel(R1));
  Multiplexer #(.select(2), .width(32), .disabled("Z"), .enable("false")) multiplexer_10 (
    .in0(id_ex_1_b_2), .in1(ex_mem_1_aluresult_2), .in2(RDin), .in3(ex_mem_1_aluresult_2), .out(a0), .sel(R2));
  Adder #(.width(32)) adder_2 (.a(EX_PC), .b(32'h4), .out(adder_2_out));  // open: cin, cout
  Multiplexer #(.select(1), .width(32), .disabled("Z"), .enable("false")) multiplexer_11 (
    .in0(a0), .in1(id_ex_1_imm_2), .out(multiplexer_11_out), .sel(id_ex_1_srcb_2));
  // Mips_Probe mips_probe_8: pin names not known; wires that end beside it: not_3_out, id_ex_1_ir_2
  Adder #(.width(32)) adder_3 (.a(shifter_1_out), .b(adder_2_out), .out(adder_3_out));  // open: cin, cout
  MIPS_ALU mips_alu_1 (
    .X(multiplexer_9_out), .Y(multiplexer_11_out), .AluOP(id_ex_1_aluop_2), .Equal(mips_alu_1_equal),
    .Result(mips_alu_1_result), .shamt(multiplexer_8_out));  // open: Result_2
  EX_MEM ex_mem_1 (
    .WB(id_ex_1_wb_2), .MEM(id_ex_1_mem_2), .RegWrite(id_ex_1_regwrite_2), .JAL(id_ex_1_jal_2),
    .WriteReg_num(id_ex_1_writereg_num_2), .AluResult(mips_alu_1_result), .B(a0), .SB(id_ex_1_sb_2),
    .IR(id_ex_1_ir_2), .PC(EX_PC), .WB_2(ex_mem_1_wb_2), .MEM_2(MemWrite), .RegWrite_2(ex_mem_1_regwrite_2),
    .JAL_2(ex_mem_1_jal_2), .WriteReg_num_2(ex_mem_1_writereg_num_2), .AluResult_2(ex_mem_1_aluresult_2),
    .B_2(ex_mem_1_b_2), .SB_2(ex_mem_1_sb_2), .IR_2(ex_mem_1_ir_2), .PC_2(M_PC), .CLK(CLK), .EN(not_6_out),
    .stop(d_ff_1_q), .stop_2(Stop));  // open: clr
  not not_6 (not_6_out, Stop);
  SB sb_1 (.\原数据 (ram_1_data), .addr(ex_mem_1_aluresult_2[1:0]), .data(ex_mem_1_b_2[7:0]), .out_4(sb_1_out_4));
  Multiplexer #(.select(1), .width(32), .disabled("Z"), .enable("false")) multiplexer_12 (
    .in0(sb_1_out_4), .in1(ex_mem_1_b_2), .out(MDin), .sel(not_7_out));
  not not_7 (not_7_out, ex_mem_1_sb_2);
  RAM #(.addrWidth(10), .dataWidth(32), .bus("separate"), .Select("high")) ram_1 (
    .addr(ex_mem_1_aluresult_2[11:2]), .din(MDin), .data(ram_1_data), .str(MemWrite), .clk(CLK));  // open: sel, ld, clr
  // Mips_Probe mips_probe_9: pin names not known; wires that end beside it: ex_mem_1_ir_2, mips_probe_9_p2
  MEM_WB mem_wb_1 (
    .WB(ex_mem_1_wb_2), .RegWrite(ex_mem_1_regwrite_2), .JAL(ex_mem_1_jal_2),
    .WriteReg_num(ex_mem_1_writereg_num_2), .AluResult(ex_mem_1_aluresult_2), .IR(ex_mem_1_ir_2), .PC(M_PC),
    .WB_2(mem_wb_1_wb_2), .RegWrite_2(RegWrite), .JAL_2(mem_wb_1_jal_2), .WriteReg_num_2(W_num),
    .AluResult_2(mem_wb_1_aluresult_2), .IR_2(mips_probe_9_p2), .PC_2(WB_PC), .CLK(CLK), .MD(ram_1_data),
    .MD_2(mem_wb_1_md_2), .EN(not_8_out));  // open: clr
  not not_8 (not_8_out, Stop);
  Multiplexer #(.select(1), .width(32), .disabled("Z"), .enable("false")) multiplexer_13 (
    .in0(mem_wb_1_aluresult_2), .in1(mem_wb_1_md_2), .out(multiplexer_13_out), .sel(mem_wb_1_wb_2));
  Adder #(.width(32)) adder_4 (.a(32'h4), .b(WB_PC), .out(adder_4_out));  // open: cin, cout
  Multiplexer #(.select(1), .width(32), .disabled("Z"), .enable("false")) multiplexer_14 (
    .in0(multiplexer_13_out), .in1(adder_4_out), .out(RDin), .sel(mem_wb_1_jal_2));

  // Other names for the same wires on the sheet: MEM_PC[31:0] = M_PC

  // Notes on the sheet:
  //   中断源
  //   时空图监测，可删除
  //   中断等待指示
  //   总复位信号应将除ROM以外所有存储组件全部清零
  //   数码管输出
  //   数码管输出应该用寄存器锁存，否则显示数据只能一闪而过
  //   PC = JumpAddr
  //   contents of rom_1 (hex, n*v repeats v):
  //   20110001 8000c05 20110001 20120002 20130003 8000c09 20110001 20120002 20130003 8000c0d 20110001
  //   20120002 20130003 8000c11 20110001 20120002 20130003 c000cb8 20100001 20110001 118fc0 112020
  //   20020022 c 118882 12200001 8000c15 112020 20020022 c 20110001 118880 112020 20020022 c 12200001
  //   8000c1f 20110001 118fc0 112020 20020022 c 1188c3 112020 20020022 c 118903 112020 20020022 c 118903
  //   112020 20020022 c 118903 112020 20020022 c 118903 112020 20020022 c 118903 112020 20020022 c 118903
  //   112020 20020022 c 118903 112020 20020022 c 20100001 109fc0 139fc3 8021 2012000c 24160003 26100001
  //   3210000f 20080008 20090001 139900 2709825 132020 20020022 c 1094022 1500fff9 22100001 2018000f
  //   2188024 108700 20080008 20090001 139902 2709825 132021 20020022 c 1094022 1500fff9 108702 2c9b022
  //   12c00001 8000c50 4020 1084027 84400 3508ffff 82021 20020022 c 2010ffff 20110000 ae300000 22100001
  //   22310004 ae300000 22100001 22310004 ae300000 22100001 22310004 ae300000 22100001 22310004 ae300000
  //   22100001 22310004 ae300000 22100001 22310004 ae300000 22100001 22310004 ae300000 22100001 22310004
  //   ae300000 22100001 22310004 ae300000 22100001 22310004 ae300000 22100001 22310004 ae300000 22100001
  //   22310004 ae300000 22100001 22310004 ae300000 22100001 22310004 ae300000 22100001 22310004 ae300000
  //   22100001 22310004 22100001 8020 2011003c 8e130000 8e340000 274402a 11000002 ae330000 ae140000
  //   2231fffc 1611fff8 102020 20020022 c 22100004 2011003c 1611fff2 20020032 c 20100000 22100001 102020
  //   20020022 c 22100002 102020 20020022 c 22100003 102020 20020022 c 22100004 102020 20020022 c 22100005
  //   102020 20020022 c 22100006 102020 20020022 c 22100007 102020 20020022 c 22100008 102020 20020022
  //   20020022 c 3e00008
  //   Address
  //   JMP
  //   JR
  //   OP
  //   OP
  //   Func
  //   Func
  //   rd
  //   rs
  //   rt
  //   $v0
  //   $a0
  //   imm
  //   BLTZ
  //   Beq
  //   Bne
  //   MemToReg
  //   MemWrite
  //   AluOP
  //   AluSrcB
  //   RegWrite
  //   JAL
  //   RegDst
  //   流水调试日志用
  //   为方便自动评测，需要输出流水线各段保存的PC值，注意是PC不是PC+4，另外ID段寄存器写入信息，Mem段内存写入信息也要输出
endmodule

module \中断按键参考电路  (
  input  \同步清零信号 ,
  output \与中断屏蔽位与 
);

  wire \_1号中断_out , and_1_out, clock_1_out, d_ff_1_q, or_1_out, or_2_out;

  Clock #(.highDuration(1), .lowDuration(1)) clock_1 (.out(clock_1_out));
  Button \_1号中断  (.out(\_1号中断_out ));
  LED #(.active("true")) \_1号中断等待指示灯  (.in(or_1_out));
  or or_1 (or_1_out, \与中断屏蔽位与 , d_ff_1_q);
  D_Flip_Flop #(.trigger("rising"), .Pre_Clr_Positions("LEGACY"), .NegatePresetClear("false"), .enable("true"), .NewFFLayout("false")) d_ff_1 (
    .clk(\_1号中断_out ), .D(1'b1), .Q(d_ff_1_q), .reset(\与中断屏蔽位与 ));  // open: Qn, preset, en
  or or_2 (or_2_out, d_ff_1_q, \与中断屏蔽位与 );
  and and_1 (and_1_out, or_2_out, ~\同步清零信号 );  // AND_Gate
  D_Flip_Flop #(.trigger("rising"), .Pre_Clr_Positions("LEGACY"), .NegatePresetClear("false"), .enable("true"), .NewFFLayout("false")) IR1 (
    .clk(clock_1_out), .D(and_1_out), .Q(\与中断屏蔽位与 ));  // open: Qn, preset, en, reset

  // Notes on the sheet:
  //   中断信号采样参考电路
  //   Reset 
endmodule
module \单周期MIPS_单级中断  (
  input  IR1,
  input  IR2,
  input  IR3,
  output RegWrite,
  output MemWrite,
  output [31:0] PC,
  output [31:0] IR,
  output [31:0] RDin,
  output [31:0] MDin,
  output [31:0] LedData
);

  wire and_1_out, and_2_out, and_3_out, and_4_out, CLK, display, Go, \IE非_q , IR1_t, IR2_t, IR3_t, IRA, IRB,
       IRC, mips_alu_1_equal, not_1_out, not_2_out, not_3_out, not_4_out, not_5_out, not_6_out, SB,
       SignedExt, Stop, VAR, W1, W2, W3, \单周期硬布线控制器_1_alu_src , \单周期硬布线控制器_1_beq , \单周期硬布线控制器_1_bltz ,
       \单周期硬布线控制器_1_bne , \单周期硬布线控制器_1_eret , \单周期硬布线控制器_1_jal , \单周期硬布线控制器_1_jr , \单周期硬布线控制器_1_memtoreg ,
       \单周期硬布线控制器_1_regdst , \单周期硬布线控制器_1_syscall , \单重中断_1_ir , \单重中断_1_out_12 ;
  wire [1:0] mips_alu_1_result, \单周期硬布线控制器_1_jmp , \单重中断_1_out_9 , \当前中断请求_q ;
  wire [3:0] adder_1_out_2, \单周期硬布线控制器_1_alu_op ;
  wire [4:0] multiplexer_6_out, multiplexer_7_out, multiplexer_8_out, multiplexer_9_out, multiplexer_13_out;
  wire [9:0] mips_alu_1_result_2;
  wire [15:0] \总周期数 ;
  wire [27:0] adder_1_out;
  wire [31:0] a0, adder_2_out, adder_3_out, bit_extender_1_out, bit_extender_2_out, controlled_buffer_1_out,
       EPC, mips_regifile_1_r1, multiplexer_1_out, multiplexer_2_out, multiplexer_3_out, multiplexer_4_out,
       multiplexer_5_out, multiplexer_11_out, multiplexer_12_out, multiplexer_15_out, ram_1_data, sb_1_out_4,
       shifter_1_out;
  wire [31:12] mips_alu_1_result_3;

  Clock #(.highDuration(1), .lowDuration(1)) clock_1 (.out(CLK));
  Button _1 (.out(IRA));
  Button _2 (.out(IRB));
  Button _3 (.out(IRC));
  Button \u_继续运行  (.out(Go));
  LED #(.active("true")) led_1 (.in(W1));
  LED #(.active("true")) led_2 (.in(W2));
  LED #(.active("true")) led_3 (.in(W3));
  not not_1 (not_1_out, \单周期硬布线控制器_1_jr );
  Multiplexer #(.select(1), .width(32), .disabled("Z"), .enable("false")) multiplexer_1 (
    .in0(mips_regifile_1_r1), .in1({adder_1_out_2, IR[25:0], 2'b00}), .out(multiplexer_1_out), .sel(not_1_out));
  Hex_Digit_Display hex_digit_display_1 (.value(LedData[31:28]));  // open: dp
  Multiplexer #(.select(2), .width(32), .disabled("Z"), .enable("false")) multiplexer_2 (
    .in0({adder_1_out_2, adder_1_out}), .in1(multiplexer_1_out), .in2(adder_3_out), .out(multiplexer_2_out),
    .sel(\单周期硬布线控制器_1_jmp ));  // open: in3
  Multiplexer #(.select(2), .width(32), .disabled("Z"), .enable("false")) multiplexer_3 (
    .in1(32'h30ac), .in2(32'h3150), .in3(32'h31f4), .out(multiplexer_3_out), .sel(\单重中断_1_out_9 ));  // open: in0
  Hex_Digit_Display hex_digit_display_2 (.value(LedData[23:20]));  // open: dp
  Hex_Digit_Display hex_digit_display_3 (.value(LedData[27:24]));  // open: dp
  Multiplexer #(.select(1), .width(32), .disabled("Z"), .enable("false")) multiplexer_4 (
    .in0(multiplexer_2_out), .in1(multiplexer_3_out), .out(multiplexer_4_out), .sel(\单重中断_1_out_12 ));
  Hex_Digit_Display hex_digit_display_4 (.value(LedData[15:12]));  // open: dp
  Hex_Digit_Display hex_digit_display_5 (.value(LedData[19:16]));  // open: dp
  Multiplexer #(.select(1), .width(32), .disabled("Z"), .enable("false")) multiplexer_5 (
    .in0(multiplexer_4_out), .in1(EPC), .out(multiplexer_5_out), .sel(\单周期硬布线控制器_1_eret ));
  not not_2 (not_2_out, Stop);
  Hex_Digit_Display hex_digit_display_6 (.value(LedData[7:4]));  // open: dp
  Hex_Digit_Display hex_digit_display_7 (.value(LedData[11:8]));  // open: dp
  // Probe on \总周期数 
  // Probe on \总周期数 
  Counter #(.width(16), .max('hffff), .ongoal("stay"), .trigger("rising"), .behavior("new")) counter_1 (
    .count(not_2_out), .Q(\总周期数 ), .clk(CLK));  // open: load, D, carry, clr, preset, down
  Register #(.width(32), .trigger("rising"), .Select("low")) u_PC (
    .D(multiplexer_5_out), .en(not_2_out), .Q(PC), .clk(CLK));  // open: clr
  Adder #(.width(32)) adder_1 (.a(PC), .b(32'h4), .out({adder_1_out_2, adder_1_out}));  // open: cin, cout
  Hex_Digit_Display hex_digit_display_8 (.value(LedData[3:0]));  // open: dp
  \单重中断  \u_单重中断_1  (
    .\_1号中断 (IR1_t), .\_2号中断 (IR2_t), .\_3号中断 (IR3_t), .\_1号中断等待指示灯 (W1), .\_1号中断等待指示灯_2 (W2),
    .\_3号中断等待指示灯 (W3), .IR(\单重中断_1_ir ), .out_9(\单重中断_1_out_9 ), .CLK(CLK), .out_12(\单重中断_1_out_12 ),
    .in_4(\当前中断请求_q ), .ERET(\单周期硬布线控制器_1_eret ), .IE(not_3_out));
  // Probe on PC
  // Mips_Probe mips_probe_1: pin names not known; wires that end beside it: IR
  ROM #(.addrWidth(10), .dataWidth(32), .Select("high")) rom_1 (.addr(PC[11:2]), .data(IR));
  or or_1 (IR1_t, IR1, IRA);
  // Mips_Probe mips_probe_2: pin names not known; wires that end beside it: IR
  Register #(.width(2), .trigger("rising"), .Select("low")) \u_当前中断请求  (
    .D(\单重中断_1_out_9 ), .en(and_1_out), .Q(\当前中断请求_q ), .clk(CLK), .clr(\单周期硬布线控制器_1_eret ));
  Register #(.width(1), .trigger("rising"), .Select("low")) \IE非  (
    .D(\单重中断_1_ir ), .en(not_3_out), .Q(\IE非_q ), .clk(CLK), .clr(\单周期硬布线控制器_1_eret ));
  or or_2 (IR2_t, IR2, IRB);
  and and_1 (and_1_out, ~\当前中断请求_q [0], ~\当前中断请求_q [1]);  // AND_Gate
  not not_3 (not_3_out, \IE非_q );
  \单周期硬布线控制器  \u_单周期硬布线控制器_1  (
    .Func(IR[5:0]), .OP(IR[31:26]), .ALU_OP(\单周期硬布线控制器_1_alu_op ), .MemToReg(\单周期硬布线控制器_1_memtoreg ),
    .MemWrite(MemWrite), .ALU_SRC(\单周期硬布线控制器_1_alu_src ), .RegWrite(RegWrite),
    .SysCALL(\单周期硬布线控制器_1_syscall ), .SignedExt(SignedExt), .RegDst(\单周期硬布线控制器_1_regdst ),
    .JR(\单周期硬布线控制器_1_jr ), .JMP(\单周期硬布线控制器_1_jmp [0]), .Beq(\单周期硬布线控制器_1_beq ), .JAL(\单周期硬布线控制器_1_jal ),
    .Bne(\单周期硬布线控制器_1_bne ), .SB(SB), .BLTZ(\单周期硬布线控制器_1_bltz ), .VAR(VAR), .ERET(\单周期硬布线控制器_1_eret ));  // open: MT_MF, MFC0, MTC0
  Multiplexer #(.select(1), .width(5), .disabled("Z"), .enable("false")) multiplexer_6 (
    .in0(IR[25:21]), .in1(5'b00010), .out(multiplexer_6_out), .sel(\单周期硬布线控制器_1_syscall ));
  Multiplexer #(.select(1), .width(5), .disabled("Z"), .enable("false")) multiplexer_7 (
    .in0(IR[20:16]), .in1(5'b00100), .out(multiplexer_7_out), .sel(\单周期硬布线控制器_1_syscall ));
  Adder #(.width(32)) adder_2 (.a(PC), .b(32'h4), .out(adder_2_out));  // open: cin, cout
  or or_3 (IR3_t, IR3, IRC);
  Register #(.width(32), .trigger("rising"), .Select("low")) u_EPC (
    .D(multiplexer_2_out), .Q(EPC), .clk(\IE非_q ));  // open: en, clr
  Multiplexer #(.select(1), .width(5), .disabled("Z"), .enable("false")) multiplexer_8 (
    .in0(multiplexer_7_out), .in1(IR[15:11]), .out(multiplexer_8_out), .sel(\单周期硬布线控制器_1_regdst ));
  Multiplexer #(.select(1), .width(5), .disabled("Z"), .enable("false")) multiplexer_9 (
    .in0(multiplexer_8_out), .in1({5{1'b1}}), .out(multiplexer_9_out), .sel(\单周期硬布线控制器_1_jal ));
  Multiplexer #(.select(1), .width(32), .disabled("Z"), .enable("false")) multiplexer_10 (
    .in0(multiplexer_15_out), .in1(adder_2_out), .out(RDin), .sel(\单周期硬布线控制器_1_jal ));
  Register #(.width(32), .trigger("rising"), .Select("low")) register_1 (
    .D(controlled_buffer_1_out), .Q(LedData), .clk(CLK));  // open: en, clr
  assign controlled_buffer_1_out = display ? a0 : 32'bz;  // Controlled_Buffer controlled_buffer_1
  MIPS_Regifile mips_regifile_1 (
    .Din(RDin), .Clk(CLK), .R1(mips_regifile_1_r1), .R2(a0), .WE(RegWrite), .W_num(multiplexer_9_out),
    .R1_num(multiplexer_6_out), .R2_num(multiplexer_7_out));
  not not_4 (not_4_out, display);
  assign bit_extender_1_out = {{16{1'b0}}, IR[15:0]};  // Bit_Extender bit_extender_1
  Multiplexer #(.select(1), .width(32), .disabled("Z"), .enable("false")) multiplexer_11 (
    .in0(bit_extender_1_out), .in1(bit_extender_2_out), .out(multiplexer_11_out), .sel(SignedExt));
  assign bit_extender_2_out = {{16{IR[15]}}, IR[15:0]};  // Bit_Extender bit_extender_2
  or or_4 (\单周期硬布线控制器_1_jmp [1], and_4_out, and_3_out, and_2_out);
  D_Flip_Flop #(.trigger("rising"), .Pre_Clr_Positions("ABOVE_BELOW"), .NegatePresetClear("false"), .enable("true"), .NewFFLayout("true")) d_ff_1 (
    .clk(CLK), .D(not_4_out), .Q(Stop), .en(\单周期硬布线控制器_1_syscall ), .reset(Go));  // open: Qn, preset
  Comparator #(.width(32), .mode("twosComplement")) comparator_1 (
    .a(32'h22), .b(mips_regifile_1_r1), .eq(display));  // open: gt, lt
  Shifter #(.width(32), .shift("ll")) shifter_1 (.in(bit_extender_2_out), .\dist (5'b00010), .out(shifter_1_out));
  Multiplexer #(.select(1), .width(32), .disabled("Z"), .enable("false")) multiplexer_12 (
    .in0(a0), .in1(multiplexer_11_out), .out(multiplexer_12_out), .sel(\单周期硬布线控制器_1_alu_src ));
  Adder #(.width(32)) adder_3 (
    .a(shifter_1_out), .b({adder_1_out_2, adder_1_out}), .out(adder_3_out));  // open: cin, cout
  and and_2 (and_2_out, \单周期硬布线控制器_1_beq , mips_alu_1_equal);
  Multiplexer #(.select(1), .width(5), .disabled("Z"), .enable("false")) multiplexer_13 (
    .in0(IR[10:6]), .in1(mips_regifile_1_r1[4:0]), .out(multiplexer_13_out), .sel(VAR));
  and and_3 (and_3_out, \单周期硬布线控制器_1_bltz , mips_alu_1_result[0]);
  and and_4 (and_4_out, \单周期硬布线控制器_1_bne , not_5_out);
  not not_5 (not_5_out, mips_alu_1_equal);
  MIPS_ALU mips_alu_1 (
    .X(mips_regifile_1_r1), .Y(multiplexer_12_out), .AluOP(\单周期硬布线控制器_1_alu_op ), .Equal(mips_alu_1_equal),
    .Result({mips_alu_1_result_3, mips_alu_1_result_2, mips_alu_1_result}), .shamt(multiplexer_13_out));  // open: Result_2
  SB sb_1 (.\原数据 (ram_1_data), .addr(mips_alu_1_result), .data(a0[7:0]), .out_4(sb_1_out_4));
  not not_6 (not_6_out, SB);
  RAM #(.addrWidth(10), .dataWidth(32), .bus("separate"), .Select("high")) ram_1 (
    .addr(mips_alu_1_result_2), .din(MDin), .data(ram_1_data), .str(MemWrite), .clk(CLK));  // open: sel, ld, clr
  Multiplexer #(.select(1), .width(32), .disabled("Z"), .enable("false")) multiplexer_14 (
    .in0(sb_1_out_4), .in1(a0), .out(MDin), .sel(not_6_out));
  Multiplexer #(.select(1), .width(32), .disabled("Z"), .enable("false")) multiplexer_15 (
    .in0({mips_alu_1_result_3, mips_alu_1_result_2, mips_alu_1_result}), .in1(ram_1_data),
    .out(multiplexer_15_out), .sel(\单周期硬布线控制器_1_memtoreg ));

  // Notes on the sheet:
  //   中断源
  //   中断等待指示
  //   总复位信号应将除ROM以外所有存储组件全部清零
  //   PC = JumpAddr
  //   PC = R[rs]
  //   数码管输出
  //   指令存储器
  //   contents of rom_1 (hex, n*v repeats v):
  //   201d07d0 20100001 109fc0 139fc3 8021 2012000c 24160008 26100001 3210000f 20080008 20090001 139900
  //   2709825 132020 20020022 c 1094022 1500fff9 22100001 2018000f 2188024 108700 20080008 20090001 139902
  //   2709825 132021 20020022 c 1094022 1500fff9 108702 2c9b022 12c00001 8000c07 4020 1084027 84400
  //   3508ffff 82021 20020022 c 8000c01 afa20000 23bd0004 afa40000 23bd0004 afb00000 23bd0004 afb30000
  //   23bd0004 afb40000 23bd0004 afb50000 23bd0004 afb60000 23bd0004 20160001 20140003 20150001 168020
  //   108100 2149825 132020 20020022 c 1600fffa 295a022 1680fff7 23bdfffc 8fb60000 23bdfffc 8fb50000
  //   23bdfffc 8fb40000 23bdfffc 8fb30000 23bdfffc 8fb00000 23bdfffc 8fa40000 23bdfffc 8fa20000 42000018
  //   afa20000 23bd0004 afa40000 23bd0004 afb00000 23bd0004 afb30000 23bd0004 afb40000 23bd0004 afb50000
  //   23bd0004 afb60000 23bd0004 20160002 20140003 20150001 168020 108100 2149825 132020 20020022 c
  //   1600fffa 295a022 1680fff7 23bdfffc 8fb60000 23bdfffc 8fb50000 23bdfffc 8fb40000 23bdfffc 8fb30000
  //   23bdfffc 8fb00000 23bdfffc 8fa40000 23bdfffc 8fa20000 42000018 afa20000 23bd0004 afa40000 23bd0004
  //   afb00000 23bd0004 afb30000 23bd0004 afb40000 23bd0004 afb50000 23bd0004 afb60000 23bd0004 20160003
  //   20140003 20150001 168020 108100 2149825 132020 20020022 c 1600fffa 295a022 1680fff7 23bdfffc
  //   8fb60000 23bdfffc 8fb50000 23bdfffc 8fb40000 23bdfffc 8fb30000 23bdfffc 8fb00000 23bdfffc 8fa40000
  //   23bdfffc 8fa20000 42000018
  //   Address
  //   OP
  //   Func
  //   rs
  //   指令字
  //   rt
  //   rd
  //   imm
  //   shmat
  //   JMP
  //   JR
  //   OP
  //   Func
  //   $v0
  //   $a0
  //   BLTZ
  //   Beq
  //   Bne
  //   MemToReg
  //   MemWrite
  //   AluOP
  //   AluSrcB
  //   RegWrite
  //   JAL
  //   RegDst
  //   Syscall
  //   为方便自动评测，需要输出PC，IR，寄存器堆写如数据RDin
  //   RAM写使能MemWrite、RAM写入数据MDin等信号
endmodule

module \单周期MIPS_多级中断  (
  input  IR1,
  input  IR2,
  input  IR3,
  output RegWrite,
  output MemWrite,
  output [31:0] PC,
  output [31:0] IR,
  output [31:0] RDin,
  output [31:0] MDin,
  output [31:0] LedData
);

  wire and_1_out, and_2_out, and_3_out, and_4_out, and_5_out, and_6_out, and_7_out, and_8_out, and_9_out,
       and_10_out, and_11_out, and_12_out, CLK, comparator_2_gt, comparator_3_eq, comparator_4_eq,
       comparator_5_eq, display, Go, IR1_t, IR2_t, IR3_t, IRA, IRB, IRC, MFC0, mips_alu_1_equal, MTC0,
       multiplexer_14_out, multiplexer_16_out, not_1_out, not_2_out, not_3_out, not_4_out, not_5_out,
       not_6_out, not_7_out, not_8_out, not_9_out, not_10_out, not_11_out, or_6_out, or_7_out, SB, SignedExt,
       Stop, VAR, W1, W2, W3, \单周期硬布线控制器_1_alu_src , \单周期硬布线控制器_1_beq , \单周期硬布线控制器_1_bltz ,
       \单周期硬布线控制器_1_bne , \单周期硬布线控制器_1_eret , \单周期硬布线控制器_1_jal , \单周期硬布线控制器_1_jr , \单周期硬布线控制器_1_memtoreg ,
       \单周期硬布线控制器_1_regdst , \单周期硬布线控制器_1_regwrite , \单周期硬布线控制器_1_syscall , \多中断_1_out_12 ;
  wire [0:0] \多中断_1_ir ;
  wire [1:0] IRT, multiplexer_21_out, Status_2_q, Status_3_q, Status_4_q, \单周期硬布线控制器_1_jmp , \多中断_1_out_9 ;
  wire [3:0] \单周期硬布线控制器_1_alu_op ;
  wire [4:0] mips_regifile_1_r1, multiplexer_6_out, multiplexer_7_out, multiplexer_8_out, multiplexer_9_out,
       multiplexer_10_out, multiplexer_19_out;
  wire [15:0] \总周期数 ;
  wire [31:0] adder_1_out, adder_2_out, adder_3_out, bit_extender_1_out, bit_extender_2_out,
       controlled_buffer_1_out, EPC, mips_alu_1_result, multiplexer_1_out, multiplexer_2_out,
       multiplexer_3_out, multiplexer_4_out, multiplexer_5_out, multiplexer_11_out, multiplexer_13_out,
       multiplexer_15_out, multiplexer_17_out, multiplexer_18_out, multiplexer_23_out, R2, ram_1_data,
       sb_1_out_4, shifter_1_out, Status_q;
  wire [31:5] mips_regifile_1_r1_2;

  Clock #(.highDuration(1), .lowDuration(1)) clock_1 (.out(CLK));
  Button _1 (.out(IRA));
  Button _2 (.out(IRB));
  Button _3 (.out(IRC));
  Button \u_继续运行  (.out(Go));
  LED #(.active("true")) led_1 (.in(W1));
  LED #(.active("true")) led_2 (.in(W2));
  LED #(.active("true")) led_3 (.in(W3));
  not not_1 (not_1_out, \单周期硬布线控制器_1_jr );
  Multiplexer #(.select(1), .width(32), .disabled("Z"), .enable("false")) multiplexer_1 (
    .in0({mips_regifile_1_r1_2, mips_regifile_1_r1}), .in1({adder_1_out[31:28], IR[25:0], 2'b00}),
    .out(multiplexer_1_out), .sel(not_1_out));
  Hex_Digit_Display hex_digit_display_1 (.value(LedData[31:28]));  // open: dp
  Multiplexer #(.select(2), .width(32), .disabled("Z"), .enable("false")) multiplexer_2 (
    .in0(adder_1_out), .in1(multiplexer_1_out), .in2(adder_3_out), .out(multiplexer_2_out),
    .sel(\单周期硬布线控制器_1_jmp ));  // open: in3
  Multiplexer #(.select(2), .width(32), .disabled("Z"), .enable("false")) multiplexer_3 (
    .in1(32'h30ac), .in2(32'h3174), .in3(32'h323c), .out(multiplexer_3_out), .sel(IRT));  // open: in0
  Hex_Digit_Display hex_digit_display_2 (.value(LedData[23:20]));  // open: dp
  Hex_Digit_Display hex_digit_display_3 (.value(LedData[27:24]));  // open: dp
  Multiplexer #(.select(1), .width(32), .disabled("Z"), .enable("false")) multiplexer_4 (
    .in0(multiplexer_2_out), .in1(multiplexer_3_out), .out(multiplexer_4_out), .sel(\多中断_1_out_12 ));
  Hex_Digit_Display hex_digit_display_4 (.value(LedData[19:16]));  // open: dp
  Hex_Digit_Display hex_digit_display_5 (.value(LedData[15:12]));  // open: dp
  Multiplexer #(.select(1), .width(32), .disabled("Z"), .enable("false")) multiplexer_5 (
    .in0(multiplexer_4_out), .in1(EPC), .out(multiplexer_5_out), .sel(\单周期硬布线控制器_1_eret ));
  not not_2 (not_2_out, Stop);
  Hex_Digit_Display hex_digit_display_6 (.value(LedData[7:4]));  // open: dp
  Hex_Digit_Display hex_digit_display_7 (.value(LedData[11:8]));  // open: dp
  // Probe on \总周期数 
  // Probe on \总周期数 
  Counter #(.width(16), .max('hffff), .ongoal("stay"), .trigger("rising"), .behavior("new")) counter_1 (
    .count(not_2_out), .Q(\总周期数 ), .clk(CLK));  // open: load, D, carry, clr, preset, down
  Register #(.width(32), .trigger("rising"), .Select("low")) u_PC (
    .D(multiplexer_5_out), .en(not_2_out), .Q(PC), .clk(CLK));  // open: clr
  Hex_Digit_Display hex_digit_display_8 (.value(LedData[3:0]));  // open: dp
  assign controlled_buffer_1_out = display ? R2 : 32'bz;  // Controlled_Buffer controlled_buffer_1
  Adder #(.width(32)) adder_1 (.a(PC), .b(32'h4), .out(adder_1_out));  // open: cin, cout
  // Probe on PC
  Register #(.width(32), .trigger("rising"), .Select("low")) register_1 (
    .D(controlled_buffer_1_out), .Q(LedData), .clk(CLK));  // open: en, clr
  ROM #(.addrWidth(10), .dataWidth(32), .Select("high")) rom_1 (.addr(PC[11:2]), .data(IR));
  or or_1 (IR1_t, IR1, IRA);
  // Mips_Probe mips_probe_1: pin names not known; wires that end beside it: IR
  or or_2 (IR2_t, IR2, IRB);
  \单周期硬布线控制器  \u_单周期硬布线控制器_1  (
    .Func(IR[5:0]), .OP(IR[31:26]), .ALU_OP(\单周期硬布线控制器_1_alu_op ), .MemToReg(\单周期硬布线控制器_1_memtoreg ),
    .MemWrite(MemWrite), .ALU_SRC(\单周期硬布线控制器_1_alu_src ), .RegWrite(\单周期硬布线控制器_1_regwrite ),
    .SysCALL(\单周期硬布线控制器_1_syscall ), .SignedExt(SignedExt), .RegDst(\单周期硬布线控制器_1_regdst ),
    .JR(\单周期硬布线控制器_1_jr ), .JMP(\单周期硬布线控制器_1_jmp [0]), .Beq(\单周期硬布线控制器_1_beq ), .JAL(\单周期硬布线控制器_1_jal ),
    .Bne(\单周期硬布线控制器_1_bne ), .SB(SB), .BLTZ(\单周期硬布线控制器_1_bltz ), .VAR(VAR), .ERET(\单周期硬布线控制器_1_eret ),
    .MT_MF(IR[25:21]), .MFC0(MFC0), .MTC0(MTC0));
  Multiplexer #(.select(1), .width(5), .disabled("Z"), .enable("false")) multiplexer_6 (
    .in0(IR[25:21]), .in1(5'b00010), .out(multiplexer_6_out), .sel(\单周期硬布线控制器_1_syscall ));
  Multiplexer #(.select(1), .width(5), .disabled("Z"), .enable("false")) multiplexer_7 (
    .in0(IR[20:16]), .in1(5'b00100), .out(multiplexer_7_out), .sel(\单周期硬布线控制器_1_syscall ));
  or or_3 (IR3_t, IR3, IRC);
  not not_3 (not_3_out, IR[11]);
  not not_4 (not_4_out, IR[12]);
  not not_5 (not_5_out, IR[15]);
  not not_6 (not_6_out, IR[11]);
  not not_7 (not_7_out, IR[15]);
  Multiplexer #(.select(1), .width(5), .disabled("Z"), .enable("false")) multiplexer_8 (
    .in0(multiplexer_7_out), .in1(IR[15:11]), .out(multiplexer_8_out), .sel(\单周期硬布线控制器_1_regdst ));
  Adder #(.width(32)) adder_2 (.a(PC), .b(32'h4), .out(adder_2_out));  // open: cin, cout
  and and_1 (and_1_out, not_3_out, not_4_out, IR[13], IR[14], not_5_out);
  and and_2 (and_2_out, not_6_out, IR[12], IR[13], IR[14], not_7_out);
  Multiplexer #(.select(1), .width(5), .disabled("Z"), .enable("false")) multiplexer_9 (
    .in0(multiplexer_8_out), .in1({5{1'b1}}), .out(multiplexer_9_out), .sel(\单周期硬布线控制器_1_jal ));
  Multiplexer #(.select(1), .width(5), .disabled("Z"), .enable("false")) multiplexer_10 (
    .in0(multiplexer_9_out), .in1(multiplexer_7_out), .out(multiplexer_10_out), .sel(MFC0));
  Multiplexer #(.select(1), .width(32), .disabled("Z"), .enable("false")) multiplexer_11 (
    .in0(multiplexer_23_out), .in1(adder_2_out), .out(multiplexer_11_out), .sel(\单周期硬布线控制器_1_jal ));
  Multiplexer #(.select(1), .width(32), .disabled("Z"), .enable("false")) multiplexer_12 (
    .in0(multiplexer_11_out), .in1(EPC), .out(RDin), .sel(MFC0));
  and and_3 (and_3_out, and_1_out, MTC0);
  and and_4 (and_4_out, and_2_out, MTC0);
  or or_4 (RegWrite, \单周期硬布线控制器_1_regwrite , MFC0);
  Multiplexer #(.select(1), .width(32), .disabled("Z"), .enable("false")) multiplexer_13 (
    .in0({{31{1'b0}}, \多中断_1_ir [0]}), .in1(R2), .out(multiplexer_13_out), .sel(and_1_out));
  Multiplexer #(.select(1), .width(1), .disabled("Z"), .enable("false")) multiplexer_14 (
    .in0(\多中断_1_out_12 ), .in1(and_3_out), .out(multiplexer_14_out), .sel(and_1_out));
  Multiplexer #(.select(1), .width(32), .disabled("Z"), .enable("false")) multiplexer_15 (
    .in0(multiplexer_2_out), .in1(R2), .out(multiplexer_15_out), .sel(and_2_out));
  Multiplexer #(.select(1), .width(1), .disabled("Z"), .enable("false")) multiplexer_16 (
    .in0(\多中断_1_out_12 ), .in1(and_4_out), .out(multiplexer_16_out), .sel(and_2_out));
  MIPS_Regifile mips_regifile_1 (
    .Din(RDin), .Clk(CLK), .R1({mips_regifile_1_r1_2, mips_regifile_1_r1}), .R2(R2), .WE(RegWrite),
    .W_num(multiplexer_10_out), .R1_num(multiplexer_6_out), .R2_num(multiplexer_7_out));
  Register #(.width(32), .trigger("rising"), .Select("low")) Status (
    .D(multiplexer_13_out), .en(multiplexer_14_out), .Q(Status_q), .clk(CLK), .clr(\单周期硬布线控制器_1_eret ));
  Register #(.width(32), .trigger("rising"), .Select("low")) u_EPC (
    .D(multiplexer_15_out), .en(multiplexer_16_out), .Q(EPC), .clk(CLK));  // open: clr
  assign bit_extender_1_out = {{16{1'b0}}, IR[15:0]};  // Bit_Extender bit_extender_1
  assign bit_extender_2_out = {{16{IR[15]}}, IR[15:0]};  // Bit_Extender bit_extender_2
  not not_8 (not_8_out, Status_q[0]);
  D_Flip_Flop #(.trigger("rising"), .Pre_Clr_Positions("ABOVE_BELOW"), .NegatePresetClear("false"), .enable("true"), .NewFFLayout("true")) d_ff_1 (
    .clk(CLK), .D(not_9_out), .Q(Stop), .en(\单周期硬布线控制器_1_syscall ), .reset(Go));  // open: Qn, preset
  not not_9 (not_9_out, display);
  Comparator #(.width(32), .mode("twosComplement")) comparator_1 (
    .a(32'h22), .b({mips_regifile_1_r1_2, mips_regifile_1_r1}), .eq(display));  // open: gt, lt
  Multiplexer #(.select(1), .width(32), .disabled("Z"), .enable("false")) multiplexer_17 (
    .in0(bit_extender_1_out), .in1(bit_extender_2_out), .out(multiplexer_17_out), .sel(SignedExt));
  Shifter #(.width(32), .shift("ll")) shifter_1 (.in(bit_extender_2_out), .\dist (5'b00010), .out(shifter_1_out));
  \多中断  \u_多中断_1  (
    .CLK(CLK), .\_1号中断 (IR1_t), .\_1号中断等待指示灯 (W1), .\_2号中断 (IR2_t), .\_2号中断等待指示灯 (W2), .\_3号中断 (IR3_t),
    .\_3号中断等待指示灯 (W3), .out_9(\多中断_1_out_9 ), .IR(\多中断_1_ir [0]), .out_12(\多中断_1_out_12 ), .IE(not_8_out),
    .ERET(\单周期硬布线控制器_1_eret ), .in_4(Status_2_q));
  or or_5 (\单周期硬布线控制器_1_jmp [1], and_6_out, and_9_out, and_5_out);
  Multiplexer #(.select(1), .width(32), .disabled("Z"), .enable("false")) multiplexer_18 (
    .in0(R2), .in1(multiplexer_17_out), .out(multiplexer_18_out), .sel(\单周期硬布线控制器_1_alu_src ));
  Adder #(.width(32)) adder_3 (.a(shifter_1_out), .b(adder_1_out), .out(adder_3_out));  // open: cin, cout
  and and_5 (and_5_out, \单周期硬布线控制器_1_beq , mips_alu_1_equal);
  and and_6 (and_6_out, \单周期硬布线控制器_1_bne , not_10_out);
  MIPS_ALU mips_alu_1 (
    .X({mips_regifile_1_r1_2, mips_regifile_1_r1}), .Y(multiplexer_18_out), .AluOP(\单周期硬布线控制器_1_alu_op ),
    .Equal(mips_alu_1_equal), .Result(mips_alu_1_result), .shamt(multiplexer_19_out));  // open: Result_2
  Multiplexer #(.select(1), .width(5), .disabled("Z"), .enable("false")) multiplexer_19 (
    .in0(IR[10:6]), .in1(mips_regifile_1_r1), .out(multiplexer_19_out), .sel(VAR));
  and and_7 (and_7_out, not_8_out, or_7_out);
  and and_8 (and_8_out, not_8_out, comparator_2_gt);
  and and_9 (and_9_out, \单周期硬布线控制器_1_bltz , mips_alu_1_result[0]);
  not not_10 (not_10_out, mips_alu_1_equal);
  Multiplexer #(.select(1), .width(2), .disabled("Z"), .enable("false")) multiplexer_20 (
    .in0(Status_3_q), .in1(multiplexer_21_out), .out(IRT), .sel(and_11_out));
  Multiplexer #(.select(1), .width(2), .disabled("Z"), .enable("false")) multiplexer_21 (
    .in0(Status_4_q), .in1(\多中断_1_out_9 ), .out(multiplexer_21_out), .sel(and_12_out));
  SB sb_1 (.\原数据 (ram_1_data), .addr(mips_alu_1_result[1:0]), .data(R2[7:0]), .out_4(sb_1_out_4));
  Multiplexer #(.select(1), .width(32), .disabled("Z"), .enable("false")) multiplexer_22 (
    .in0(sb_1_out_4), .in1(R2), .out(MDin), .sel(not_11_out));
  not not_11 (not_11_out, SB);
  Register #(.width(2), .trigger("rising"), .Select("low")) Status_2 (
    .D(IRT), .en(or_6_out), .Q(Status_2_q), .clk(CLK), .clr(and_10_out));
  or or_6 (or_6_out, and_7_out, \单周期硬布线控制器_1_eret );
  and and_10 (and_10_out, \单周期硬布线控制器_1_eret , and_12_out, and_11_out);
  RAM #(.addrWidth(10), .dataWidth(32), .bus("separate"), .Select("high")) ram_1 (
    .addr(mips_alu_1_result[11:2]), .din(MDin), .data(ram_1_data), .str(MemWrite), .clk(CLK));  // open: sel, ld, clr
  Register #(.width(2), .trigger("rising"), .Select("low")) Status_3 (
    .D(Status_2_q), .en(and_8_out), .Q(Status_3_q), .clk(CLK), .clr(comparator_4_eq));
  Multiplexer #(.select(1), .width(32), .disabled("Z"), .enable("false")) multiplexer_23 (
    .in0(mips_alu_1_result), .in1(ram_1_data), .out(multiplexer_23_out), .sel(\单周期硬布线控制器_1_memtoreg ));
  and and_11 (and_11_out, ~Status_3_q[1], ~Status_3_q[0]);  // AND_Gate
  Comparator #(.width(2), .mode("unsigned")) comparator_2 (
    .a(IRT), .b(Status_2_q), .gt(comparator_2_gt));  // open: eq, lt
  Comparator #(.width(2), .mode("unsigned")) comparator_3 (
    .a(Status_2_q), .b(2'b00), .eq(comparator_3_eq));  // open: gt, lt
  Register #(.width(2), .trigger("rising"), .Select("low")) Status_4 (
    .D(Status_3_q), .en(and_8_out), .Q(Status_4_q), .clk(CLK), .clr(comparator_5_eq));
  and and_12 (and_12_out, ~Status_4_q[1], ~Status_4_q[0]);  // AND_Gate
  or or_7 (or_7_out, comparator_2_gt, comparator_3_eq);
  Comparator #(.width(2), .mode("unsigned")) comparator_4 (
    .a(Status_3_q), .b(Status_2_q), .eq(comparator_4_eq));  // open: gt, lt
  Comparator #(.width(2), .mode("unsigned")) comparator_5 (
    .a(Status_4_q), .b(Status_2_q), .eq(comparator_5_eq));  // open: gt, lt

  // Notes on the sheet:
  //   中断源
  //   中断等待指示
  //   总复位信号应将除ROM以外所有存储组件全部清零
  //   PC = R[rs]
  //   PC = JumpAddr
  //   数码管输出
  //   数码管输出应该用寄存器锁存，否则显示数据只能一闪而过
  //   指令存储器
  //   contents of rom_1 (hex, n*v repeats v):
  //   201d07d0 20100001 109fc0 139fc3 8021 2012000c 24160008 26100001 3210000f 20080008 20090001 139900
  //   2709825 132020 20020022 c 1094022 1500fff9 22100001 2018000f 2188024 108700 20080008 20090001 139902
  //   2709825 132021 20020022 c 1094022 1500fff9 108702 2c9b022 12c00001 8000c07 4020 1084027 84400
  //   3508ffff 82021 20020022 c 8000c01 afa20000 23bd0004 afa40000 23bd0004 afb00000 23bd0004 afb30000
  //   23bd0004 afb40000 23bd0004 afb50000 23bd0004 afb60000 23bd0004 40167000 afb60000 23bd0004 40806000
  //   20160001 20140003 20150001 168020 108100 2149825 132020 20020022 c 1600fffa 295a022 1680fff7
  //   20160001 40966000 23bdfffc 8fb60000 40967000 23bdfffc 8fb60000 23bdfffc 8fb50000 23bdfffc 8fb40000
  //   23bdfffc 8fb30000 23bdfffc 8fb00000 23bdfffc 8fa40000 23bdfffc 8fa20000 42000018 afa20000 23bd0004
  //   afa40000 23bd0004 afb00000 23bd0004 afb30000 23bd0004 afb40000 23bd0004 afb50000 23bd0004 afb60000
  //   23bd0004 40167000 afb60000 23bd0004 40806000 20160002 20140003 20150001 168020 108100 2149825 132020
  //   20020022 c 1600fffa 295a022 1680fff7 20160001 40966000 23bdfffc 8fb60000 40967000 23bdfffc 8fb60000
  //   23bdfffc 8fb50000 23bdfffc 8fb40000 23bdfffc 8fb30000 23bdfffc 8fb00000 23bdfffc 8fa40000 23bdfffc
  //   8fa20000 42000018 afa20000 23bd0004 afa40000 23bd0004 afb00000 23bd0004 afb30000 23bd0004 afb40000
  //   23bd0004 afb50000 23bd0004 afb60000 23bd0004 40167000 afb60000 23bd0004 40806000 20160003 20140003
  //   20150001 168020 108100 2149825 132020 20020022 c 1600fffa 295a022 1680fff7 20160001 40966000
  //   23bdfffc 8fb60000 40967000 23bdfffc 8fb60000 23bdfffc 8fb50000 23bdfffc 8fb40000 23bdfffc 8fb30000
  //   23bdfffc 8fb00000 23bdfffc 8fa40000 23bdfffc 8fa20000 42000018
  //   Address
  //   rd
  //   OP
  //   Func
  //   rs
  //   指令字
  //   rt
  //   rd
  //   imm
  //   shmat
  //   JMP
  //   JR
  //   OP
  //   Func
  //   $v0
  //   $a0
  //   PC = R[rs]
  //   BLTZ
  //   Beq
  //   Bne
  //   MemToReg
  //   MemWrite
  //   AluOP
  //   AluSrcB
  //   RegWrite
  //   JAL
  //   RegDst
  //   Syscall
  //   为方便自动评测，需要输出PC，IR，寄存器堆写如数据RDin
  //   RAM写使能MemWrite、RAM写入数据MDin等信号
endmodule

module \封装正确性测试  (
);

  wire IR1, IR2, IR3, MemW, RegW;
  wire [31:0] EX_PC, ID_PC, IF_PC, IR, LED, MDin, MDinr, MEM_PC, PC, RDin, RDinr, WB_PC;

  \单周期MIPS  \u_单周期mips_1  (
    .RegWrite(RegW), .MemWrite(MemW), .PC(PC), .IR(IR), .RDin(RDin), .MDin(MDin), .LedData(LED));  // open: IR1, IR2, IR3
  \气泡流水线  \u_气泡流水线_1  (
    .RegWrite(RegW), .MemWrite(MemW), .IF_PC(IF_PC), .ID_PC(ID_PC), .EX_PC(EX_PC), .M_PC(MEM_PC),
    .WB_PC(WB_PC), .RDin(RDinr), .MDin(MDinr), .LedData(LED));
  \单周期MIPS_单级中断  \u_单周期mips_单级中断_1  (
    .IR1(IR1), .IR2(IR2), .IR3(IR3), .RegWrite(RegW), .MemWrite(MemW), .PC(PC), .IR(IR), .RDin(RDin),
    .MDin(MDin), .LedData(LED));
  \理想流水线  \u_理想流水线_1  (
    .RegWrite(RegW), .MemWrite(MemW), .IF_PC(IF_PC), .ID_PC(ID_PC), .EX_PC(EX_PC), .M_PC(MEM_PC),
    .WB_PC(WB_PC), .RDin(RDinr), .MDin(MDinr), .LedData(LED));
  \气泡流水线  \u_气泡流水线_2  (
    .RegWrite(RegW), .MemWrite(MemW), .IF_PC(IF_PC), .ID_PC(ID_PC), .EX_PC(EX_PC), .M_PC(MEM_PC),
    .WB_PC(WB_PC), .RDin(RDinr), .MDin(MDinr), .LedData(LED));
  \单周期MIPS_多级中断  \u_单周期mips_多级中断_1  (
    .IR1(IR1), .IR2(IR2), .IR3(IR3), .RegWrite(RegW), .MemWrite(MemW), .PC(PC), .IR(IR), .RDin(RDin),
    .MDin(MDin), .LedData(LED));

  // Notes on the sheet:
  //   单周期封装测试
  //   气泡流水封装测试
  //   单周期+单级中断封装测试
  //   请检查上面封装有无位宽不匹配，引脚标签是否和连接的标签相对应，否则无法在educoder平台上正确测试
  //   理想流水封装测试
  //   重定向流水封装测试
  //   单周期+多级中断封装测试
endmodule

module SB (
  input  [31:0] \原数据 ,
  input  [1:0] addr,
  input  [7:0] data,
  output [31:0] out_4
);

  wire [4:0] shifter_2_out, shifter_4_out;
  wire [31:0] and_1_out, not_1_out, shifter_1_out, shifter_3_out;

  Shifter #(.width(32), .shift("ll")) shifter_1 (.in(32'hff), .\dist (shifter_2_out), .out(shifter_1_out));
  Shifter #(.width(5), .shift("ll")) shifter_2 (.in({3'b000, addr}), .\dist (3'b011), .out(shifter_2_out));
  Shifter #(.width(32), .shift("ll")) shifter_3 (.in({{24{1'b0}}, data}), .\dist (shifter_4_out), .out(shifter_3_out));
  Shifter #(.width(5), .shift("ll")) shifter_4 (.in({3'b000, addr}), .\dist (3'b011), .out(shifter_4_out));
  assign not_1_out = ~shifter_1_out;  // NOT_Gate not_1, 32 bits wide
  assign and_1_out = \原数据  & not_1_out;  // AND_Gate and_1, 32 bits wide
  assign out_4 = and_1_out | shifter_3_out;  // OR_Gate or_1, 32 bits wide
endmodule

module \源寄存器使用情况  (
  input  OP0,
  input  OP1,
  input  OP2,
  input  OP3,
  input  OP4,
  input  OP5,
  input  F0,
  input  F1,
  input  F2,
  input  F3,
  input  F4,
  input  F5,
  output R1_used,
  output R2_used
);

  wire and_1_out, and_2_out, and_3_out, and_4_out, and_5_out, and_6_out, and_7_out, and_8_out, and_9_out,
       and_10_out, and_11_out, and_12_out, and_13_out, and_14_out, and_15_out, and_16_out, and_17_out,
       and_18_out, and_19_out, and_20_out, and_21_out, and_22_out, and_23_out, and_24_out, and_25_out,
       and_26_out, and_27_out, and_28_out, and_29_out, not_1_out, not_2_out, not_3_out, not_4_out, not_5_out,
       not_6_out, not_7_out, not_8_out, not_9_out, not_10_out, not_11_out, not_12_out, not_13_out,
       not_14_out, not_15_out, not_16_out, not_17_out, not_18_out, not_19_out, not_20_out, not_21_out,
       not_22_out, not_23_out, not_24_out, not_25_out, not_26_out, not_27_out, not_28_out, not_29_out,
       not_30_out, not_31_out, not_32_out, not_33_out, not_34_out, not_35_out, not_36_out, not_37_out,
       not_38_out, not_39_out, not_40_out, not_41_out, not_42_out, not_43_out, not_44_out, not_45_out,
       not_46_out, not_47_out, not_48_out, not_49_out, not_50_out, not_51_out, not_52_out, not_53_out,
       not_54_out, not_55_out, not_56_out, not_57_out, not_58_out, not_59_out, not_60_out, not_61_out,
       not_62_out, not_63_out, not_64_out, not_65_out, not_66_out, not_67_out, not_68_out, not_69_out,
       not_70_out, not_71_out, not_72_out, not_73_out, not_74_out, not_75_out, not_76_out, not_77_out,
       not_78_out, not_79_out, not_80_out, not_81_out, not_82_out, not_83_out, not_84_out, not_85_out,
       not_86_out, not_87_out, not_88_out, not_89_out, not_90_out, not_91_out, not_92_out, not_93_out,
       not_94_out, not_95_out, not_96_out, not_97_out, not_98_out, not_99_out, not_100_out, not_101_out,
       not_102_out, not_103_out, not_104_out, not_105_out, not_106_out, not_107_out, not_108_out,
       not_109_out, not_110_out, not_111_out, not_112_out, not_113_out, not_114_out, not_115_out,
       not_116_out, not_117_out, not_118_out, not_119_out, not_120_out, not_121_out, not_122_out,
       not_123_out, not_124_out, not_125_out, not_126_out, not_127_out, not_128_out, not_129_out,
       not_130_out, not_131_out, not_132_out, not_133_out, not_134_out, not_135_out, not_136_out,
       not_137_out, not_138_out, not_139_out, not_140_out, not_141_out, not_142_out, not_143_out,
       not_144_out, not_145_out, not_146_out, not_147_out, not_148_out, not_149_out, not_150_out,
       not_151_out, not_152_out, not_153_out, not_154_out, not_155_out, not_156_out, not_157_out,
       not_158_out, not_159_out, not_160_out, not_161_out, not_162_out, not_163_out, not_164_out,
       not_165_out, not_166_out, not_167_out, not_168_out, not_169_out, not_170_out, not_171_out,
       not_172_out, not_173_out, not_174_out, not_175_out, not_176_out, not_177_out, not_178_out,
       not_179_out, not_180_out, not_181_out, not_182_out, not_183_out, not_184_out, not_185_out,
       not_186_out, not_187_out, not_188_out, not_189_out, not_190_out, not_191_out, not_192_out,
       not_193_out, not_194_out, not_195_out, not_196_out, not_197_out, not_198_out, not_199_out,
       not_200_out, not_201_out, not_202_out, not_203_out, not_204_out;

  not not_1 (not_1_out, OP1);
  not not_2 (not_2_out, OP4);
  not not_3 (not_3_out, OP5);
  not not_4 (not_4_out, F0);
  not not_5 (not_5_out, F2);
  not not_6 (not_6_out, F3);
  not not_7 (not_7_out, F4);
  not not_8 (not_8_out, OP1);
  not not_9 (not_9_out, OP4);
  not not_10 (not_10_out, OP5);
  not not_11 (not_11_out, F1);
  not not_12 (not_12_out, F3);
  not not_13 (not_13_out, F4);
  not not_14 (not_14_out, OP1);
  not not_15 (not_15_out, OP4);
  not not_16 (not_16_out, OP5);
  not not_17 (not_17_out, F0);
  not not_18 (not_18_out, F1);
  not not_19 (not_19_out, F4);
  not not_20 (not_20_out, F5);
  not not_21 (not_21_out, OP1);
  not not_22 (not_22_out, OP4);
  not not_23 (not_23_out, OP5);
  not not_24 (not_24_out, F3);
  not not_25 (not_25_out, F4);
  not not_26 (not_26_out, F5);
  not not_27 (not_27_out, OP1);
  not not_28 (not_28_out, OP4);
  not not_29 (not_29_out, OP5);
  not not_30 (not_30_out, F2);
  not not_31 (not_31_out, F4);
  not not_32 (not_32_out, OP1);
  not not_33 (not_33_out, OP4);
  not not_34 (not_34_out, OP5);
  not not_35 (not_35_out, F3);
  not not_36 (not_36_out, F4);
  not not_37 (not_37_out, OP0);
  not not_38 (not_38_out, OP1);
  not not_39 (not_39_out, OP2);
  not not_40 (not_40_out, OP4);
  not not_41 (not_41_out, OP0);
  not not_42 (not_42_out, OP2);
  not not_43 (not_43_out, OP4);
  not not_44 (not_44_out, OP5);
  not not_45 (not_45_out, OP1);
  not not_46 (not_46_out, OP4);
  not not_47 (not_47_out, OP5);
  not not_48 (not_48_out, OP1);
  not not_49 (not_49_out, OP4);
  not not_50 (not_50_out, OP5);
  not not_51 (not_51_out, OP2);
  not not_52 (not_52_out, OP4);
  not not_53 (not_53_out, OP5);
  not not_54 (not_54_out, OP4);
  not not_55 (not_55_out, OP3);
  not not_56 (not_56_out, OP2);
  not not_57 (not_57_out, OP1);
  not not_58 (not_58_out, OP0);
  not not_59 (not_59_out, F5);
  not not_60 (not_60_out, F4);
  not not_61 (not_61_out, F3);
  not not_62 (not_62_out, F2);
  not not_63 (not_63_out, F1);
  not not_64 (not_64_out, F0);
  not not_65 (not_65_out, OP5);
  not not_66 (not_66_out, OP4);
  not not_67 (not_67_out, OP3);
  not not_68 (not_68_out, OP2);
  not not_69 (not_69_out, OP1);
  not not_70 (not_70_out, OP0);
  not not_71 (not_71_out, F5);
  not not_72 (not_72_out, F4);
  not not_73 (not_73_out, F3);
  not not_74 (not_74_out, F2);
  not not_75 (not_75_out, OP5);
  not not_76 (not_76_out, OP4);
  not not_77 (not_77_out, OP3);
  not not_78 (not_78_out, OP2);
  not not_79 (not_79_out, OP1);
  not not_80 (not_80_out, OP0);
  not not_81 (not_81_out, F5);
  not not_82 (not_82_out, F4);
  not not_83 (not_83_out, F3);
  not not_84 (not_84_out, F2);
  not not_85 (not_85_out, F0);
  not not_86 (not_86_out, OP5);
  not not_87 (not_87_out, OP4);
  not not_88 (not_88_out, OP3);
  not not_89 (not_89_out, OP2);
  not not_90 (not_90_out, OP1);
  not not_91 (not_91_out, OP0);
  not not_92 (not_92_out, F4);
  not not_93 (not_93_out, F3);
  not not_94 (not_94_out, F2);
  not not_95 (not_95_out, F1);
  not not_96 (not_96_out, F0);
  not not_97 (not_97_out, OP5);
  not not_98 (not_98_out, OP4);
  not not_99 (not_99_out, OP3);
  not not_100 (not_100_out, OP2);
  not not_101 (not_101_out, OP1);
  not not_102 (not_102_out, OP0);
  not not_103 (not_103_out, F4);
  not not_104 (not_104_out, F3);
  not not_105 (not_105_out, F2);
  not not_106 (not_106_out, F1);
  not not_107 (not_107_out, OP5);
  not not_108 (not_108_out, OP4);
  not not_109 (not_109_out, OP3);
  not not_110 (not_110_out, OP2);
  not not_111 (not_111_out, OP1);
  not not_112 (not_112_out, OP0);
  not not_113 (not_113_out, F4);
  not not_114 (not_114_out, F3);
  not not_115 (not_115_out, F2);
  not not_116 (not_116_out, F0);
  not not_117 (not_117_out, OP5);
  not not_118 (not_118_out, OP4);
  not not_119 (not_119_out, OP3);
  not not_120 (not_120_out, OP2);
  not not_121 (not_121_out, OP1);
  not not_122 (not_122_out, OP0);
  not not_123 (not_123_out, F4);
  not not_124 (not_124_out, F3);
  not not_125 (not_125_out, F1);
  not not_126 (not_126_out, F0);
  not not_127 (not_127_out, OP5);
  not not_128 (not_128_out, OP4);
  not not_129 (not_129_out, OP3);
  not not_130 (not_130_out, OP2);
  not not_131 (not_131_out, OP1);
  not not_132 (not_132_out, OP0);
  not not_133 (not_133_out, F4);
  not not_134 (not_134_out, F3);
  not not_135 (not_135_out, F1);
  not not_136 (not_136_out, OP5);
  not not_137 (not_137_out, OP4);
  not not_138 (not_138_out, OP3);
  not not_139 (not_139_out, OP2);
  not not_140 (not_140_out, OP1);
  not not_141 (not_141_out, OP0);
  not not_142 (not_142_out, F4);
  not not_143 (not_143_out, F3);
  not not_144 (not_144_out, OP5);
  not not_145 (not_145_out, OP4);
  not not_146 (not_146_out, OP3);
  not not_147 (not_147_out, OP2);
  not not_148 (not_148_out, OP1);
  not not_149 (not_149_out, OP0);
  not not_150 (not_150_out, F4);
  not not_151 (not_151_out, F2);
  not not_152 (not_152_out, F0);
  not not_153 (not_153_out, OP5);
  not not_154 (not_154_out, OP4);
  not not_155 (not_155_out, OP3);
  not not_156 (not_156_out, OP2);
  not not_157 (not_157_out, OP1);
  not not_158 (not_158_out, OP0);
  not not_159 (not_159_out, F4);
  not not_160 (not_160_out, F2);
  not not_161 (not_161_out, OP5);
  not not_162 (not_162_out, OP4);
  not not_163 (not_163_out, OP3);
  not not_164 (not_164_out, OP2);
  not not_165 (not_165_out, OP1);
  not not_166 (not_166_out, OP0);
  not not_167 (not_167_out, F5);
  not not_168 (not_168_out, F4);
  not not_169 (not_169_out, F1);
  not not_170 (not_170_out, F0);
  not not_171 (not_171_out, OP5);
  not not_172 (not_172_out, OP4);
  not not_173 (not_173_out, OP3);
  not not_174 (not_174_out, OP1);
  not not_175 (not_175_out, OP0);
  not not_176 (not_176_out, OP5);
  not not_177 (not_177_out, OP4);
  not not_178 (not_178_out, OP3);
  not not_179 (not_179_out, OP1);
  not not_180 (not_180_out, OP4);
  not not_181 (not_181_out, OP2);
  not not_182 (not_182_out, OP5);
  not not_183 (not_183_out, OP4);
  not not_184 (not_184_out, OP3);
  not not_185 (not_185_out, OP2);
  not not_186 (not_186_out, OP1);
  not not_187 (not_187_out, OP0);
  not not_188 (not_188_out, F5);
  not not_189 (not_189_out, F4);
  not not_190 (not_190_out, F3);
  not not_191 (not_191_out, F0);
  not not_192 (not_192_out, OP5);
  not not_193 (not_193_out, OP4);
  not not_194 (not_194_out, OP3);
  not not_195 (not_195_out, OP2);
  not not_196 (not_196_out, OP1);
  not not_197 (not_197_out, OP0);
  not not_198 (not_198_out, F5);
  not not_199 (not_199_out, F4);
  not not_200 (not_200_out, F3);
  not not_201 (not_201_out, OP4);
  not not_202 (not_202_out, OP2);
  not not_203 (not_203_out, OP1);
  not not_204 (not_204_out, OP0);
  and and_1 (and_1_out, not_1_out, not_2_out, not_3_out, not_4_out, not_5_out, not_6_out, not_7_out);
  and and_2 (and_2_out, not_8_out, not_9_out, not_10_out, not_11_out, not_12_out, not_13_out, F5);
  and and_3 (and_3_out, not_14_out, not_15_out, not_16_out, not_17_out, not_18_out, F3, not_19_out, not_20_out);
  and and_4 (and_4_out, not_21_out, not_22_out, not_23_out, F1, not_24_out, not_25_out, not_26_out);
  and and_5 (and_5_out, not_27_out, not_28_out, not_29_out, F1, not_30_out, F3, not_31_out, F5);
  and and_6 (and_6_out, not_32_out, not_33_out, not_34_out, F0, F1, F2, not_35_out, not_36_out);
  and and_7 (and_7_out, not_37_out, not_38_out, not_39_out, OP3, not_40_out);
  and and_8 (and_8_out, not_41_out, not_42_out, OP3, not_43_out, not_44_out);
  and and_9 (and_9_out, not_45_out, OP2, not_46_out, not_47_out);
  and and_10 (and_10_out, OP0, not_48_out, not_49_out, not_50_out);
  and and_11 (and_11_out, OP0, OP1, not_51_out, not_52_out, OP5);
  and and_12 (and_12_out, not_53_out, not_54_out, not_55_out, not_56_out, not_57_out, not_58_out, not_59_out, not_60_out, not_61_out, not_62_out, not_63_out, not_64_out);
  and and_13 (and_13_out, not_65_out, not_66_out, not_67_out, not_68_out, not_69_out, not_70_out, not_71_out, not_72_out, not_73_out, not_74_out, F1, F0);
  and and_14 (and_14_out, not_75_out, not_76_out, not_77_out, not_78_out, not_79_out, not_80_out, not_81_out, not_82_out, not_83_out, not_84_out, F1, not_85_out);
  and and_15 (and_15_out, not_86_out, not_87_out, not_88_out, not_89_out, not_90_out, not_91_out, F5, not_92_out, not_93_out, not_94_out, not_95_out, not_96_out);
  and and_16 (and_16_out, not_97_out, not_98_out, not_99_out, not_100_out, not_101_out, not_102_out, F5, not_103_out, not_104_out, not_105_out, not_106_out, F0);
  and and_17 (and_17_out, not_107_out, not_108_out, not_109_out, not_110_out, not_111_out, not_112_out, F5, not_113_out, not_114_out, not_115_out, F1, not_116_out);
  and and_18 (and_18_out, not_117_out, not_118_out, not_119_out, not_120_out, not_121_out, not_122_out, F5, not_123_out, not_124_out, F2, not_125_out, not_126_out);
  and and_19 (and_19_out, not_127_out, not_128_out, not_129_out, not_130_out, not_131_out, not_132_out, F5, not_133_out, not_134_out, F2, not_135_out, F0);
  and and_20 (and_20_out, not_136_out, not_137_out, not_138_out, not_139_out, not_140_out, not_141_out, F5, not_142_out, not_143_out, F2, F1, F0);
  and and_21 (and_21_out, not_144_out, not_145_out, not_146_out, not_147_out, not_148_out, not_149_out, F5, not_150_out, F3, not_151_out, F1, not_152_out);
  and and_22 (and_22_out, not_153_out, not_154_out, not_155_out, not_156_out, not_157_out, not_158_out, F5, not_159_out, F3, not_160_out, F1, F0);
  and and_23 (and_23_out, not_161_out, not_162_out, not_163_out, not_164_out, not_165_out, not_166_out, not_167_out, not_168_out, F3, F2, not_169_out, not_170_out);
  and and_24 (and_24_out, not_171_out, not_172_out, not_173_out, OP2, not_174_out, not_175_out);
  and and_25 (and_25_out, not_176_out, not_177_out, not_178_out, OP2, not_179_out, OP0);
  and and_26 (and_26_out, OP5, not_180_out, OP3, not_181_out, OP1, OP0);
  and and_27 (and_27_out, not_182_out, not_183_out, not_184_out, not_185_out, not_186_out, not_187_out, not_188_out, not_189_out, not_190_out, F2, F1, not_191_out);
  and and_28 (and_28_out, not_192_out, not_193_out, not_194_out, not_195_out, not_196_out, not_197_out, not_198_out, not_199_out, not_200_out, F2, F1, F0);
  and and_29 (and_29_out, OP5, not_201_out, OP3, not_202_out, not_203_out, not_204_out);
  or or_1 (R1_used, and_1_out, and_2_out, and_3_out, and_4_out, and_5_out, and_6_out, and_7_out, and_8_out, and_9_out, and_10_out, and_11_out);
  or or_2 (R2_used, and_12_out, and_13_out, and_14_out, and_15_out, and_16_out, and_17_out, and_18_out, and_19_out, and_20_out, and_21_out, and_22_out, and_23_out, and_24_out, and_25_out, and_26_out, and_27_out, and_28_out, and_29_out);
endmodule

module \数据相关检测  (
  input  R1_used,
  input  R2_used,
  input  EX_RegWrite,
  input  MEM_RegWrite,
  input  [4:0] R1_num,
  input  [4:0] EX_WriteReg_num,
  input  [4:0] MEM_WriteReg_num,
  input  [4:0] R2_num,
  output EX,
  output MEM
);

  wire and_1_out, and_2_out, and_3_out, and_4_out, comparator_1_eq, comparator_2_eq, comparator_3_eq,
       comparator_4_eq, comparator_5_eq, comparator_6_eq;

  Comparator #(.width(5), .mode("twosComplement")) comparator_1 (
    .a({5{1'b0}}), .b(R1_num), .eq(comparator_1_eq));  // open: gt, lt
  Comparator #(.width(5), .mode("twosComplement")) comparator_2 (
    .a(R1_num), .b(EX_WriteReg_num), .eq(comparator_2_eq));  // open: gt, lt
  Comparator #(.width(5), .mode("twosComplement")) comparator_3 (
    .a(R1_num), .b(MEM_WriteReg_num), .eq(comparator_3_eq));  // open: gt, lt
  Comparator #(.width(5), .mode("twosComplement")) comparator_4 (
    .a(R2_num), .b(EX_WriteReg_num), .eq(comparator_4_eq));  // open: gt, lt
  Comparator #(.width(5), .mode("twosComplement")) comparator_5 (
    .a(R2_num), .b(MEM_WriteReg_num), .eq(comparator_5_eq));  // open: gt, lt
  Comparator #(.width(5), .mode("twosComplement")) comparator_6 (
    .a(R2_num), .b({5{1'b0}}), .eq(comparator_6_eq));  // open: gt, lt
  and and_1 (and_1_out, ~comparator_1_eq, EX_RegWrite, comparator_2_eq, R1_used);  // AND_Gate
  and and_2 (and_2_out, ~comparator_1_eq, MEM_RegWrite, comparator_3_eq, R1_used);  // AND_Gate
  and and_3 (and_3_out, R2_used, EX_RegWrite, comparator_4_eq, ~comparator_6_eq);  // AND_Gate
  and and_4 (and_4_out, R2_used, MEM_RegWrite, comparator_5_eq, ~comparator_6_eq);  // AND_Gate
  or or_1 (EX, and_1_out, and_3_out);
  or or_2 (MEM, and_2_out, and_4_out);
endmodule

module IF_ID (
  input  [31:0] IR,
  input  [31:0] PC,
  input  EN,
  input  CLK,
  input  clr,
  output [31:0] IR_2,
  output [31:0] PC_2
);

  Register #(.width(32), .trigger("rising"), .Select("low")) u_IR (.D(IR), .en(EN), .Q(IR_2), .clk(CLK), .clr(clr));
  Register #(.width(32), .trigger("rising"), .Select("low")) u_PC (.D(PC), .en(EN), .Q(PC_2), .clk(CLK), .clr(clr));
endmodule

module ID_EX (
  input  JR,
  input  JMP,
  input  BLTZ,
  input  Beq,
  input  Bne,
  input  WB,
  input  MEM,
  input  [3:0] AluOp,
  input  SrcB,
  input  RegWrite,
  input  JAL,
  input  [4:0] WriteReg_num,
  input  Syscall,
  input  [31:0] A,
  input  [31:0] B,
  input  [31:0] IMM,
  input  SB,
  input  VAR,
  input  [31:0] IR,
  input  [31:0] PC,
  input  EN,
  input  CLK,
  input  clr,
  output JR_2,
  output JMP_2,
  output BLTZ_2,
  output Beq_2,
  output Bne_2,
  output WB_2,
  output MEM_2,
  output [3:0] AluOp_2,
  output SrcB_2,
  output RegWrite_2,
  output JAL_2,
  output [4:0] WriteReg_num_2,
  output Syscall_2,
  output [31:0] A_2,
  output [31:0] B_2,
  output [31:0] IMM_2,
  output SB_2,
  output VAR_2,
  output [31:0] IR_2,
  output [31:0] PC_2
);

  Register #(.width(1), .trigger("rising"), .Select("low")) u_JR (.D(JR), .en(EN), .Q(JR_2), .clk(CLK), .clr(clr));
  Register #(.width(1), .trigger("rising"), .Select("low")) u_JMP (.D(JMP), .en(EN), .Q(JMP_2), .clk(CLK), .clr(clr));
  Register #(.width(1), .trigger("rising"), .Select("low")) u_BLTZ (
    .D(BLTZ), .en(EN), .Q(BLTZ_2), .clk(CLK), .clr(clr));
  Register #(.width(1), .trigger("rising"), .Select("low")) u_Beq (.D(Beq), .en(EN), .Q(Beq_2), .clk(CLK), .clr(clr));
  Register #(.width(1), .trigger("rising"), .Select("low")) u_Bne (.D(Bne), .en(EN), .Q(Bne_2), .clk(CLK), .clr(clr));
  Register #(.width(1), .trigger("rising"), .Select("low")) u_WB (.D(WB), .en(EN), .Q(WB_2), .clk(CLK), .clr(clr));
  Register #(.width(1), .trigger("rising"), .Select("low")) u_MEM (.D(MEM), .en(EN), .Q(MEM_2), .clk(CLK), .clr(clr));
  Register #(.width(4), .trigger("rising"), .Select("low")) u_AluOp (
    .D(AluOp), .en(EN), .Q(AluOp_2), .clk(CLK), .clr(clr));
  Register #(.width(1), .trigger("rising"), .Select("low")) u_SrcB (
    .D(SrcB), .en(EN), .Q(SrcB_2), .clk(CLK), .clr(clr));
  Register #(.width(1), .trigger("rising"), .Select("low")) u_Regwrite (
    .D(RegWrite), .en(EN), .Q(RegWrite_2), .clk(CLK), .clr(clr));
  Register #(.width(1), .trigger("rising"), .Select("low")) u_JAL (.D(JAL), .en(EN), .Q(JAL_2), .clk(CLK), .clr(clr));
  Register #(.width(5), .trigger("rising"), .Select("low")) u_WriteReg_num (
    .D(WriteReg_num), .en(EN), .Q(WriteReg_num_2), .clk(CLK), .clr(clr));
  Register #(.width(1), .trigger("rising"), .Select("low")) u_Syscall (
    .D(Syscall), .en(EN), .Q(Syscall_2), .clk(CLK), .clr(clr));
  Register #(.width(32), .trigger("rising"), .Select("low")) u_A (.D(A), .en(EN), .Q(A_2), .clk(CLK), .clr(clr));
  Register #(.width(32), .trigger("rising"), .Select("low")) u_B (.D(B), .en(EN), .Q(B_2), .clk(CLK), .clr(clr));
  Register #(.width(32), .trigger("rising"), .Select("low")) u_IMM (.D(IMM), .en(EN), .Q(IMM_2), .clk(CLK), .clr(clr));
  Register #(.width(1), .trigger("rising"), .Select("low")) u_SB (.D(SB), .en(EN), .Q(SB_2), .clk(CLK), .clr(clr));
  Register #(.width(1), .trigger("rising"), .Select("low")) u_VAR (.D(VAR), .en(EN), .Q(VAR_2), .clk(CLK), .clr(clr));
  Register #(.width(32), .trigger("rising"), .Select("low")) u_IR (.D(IR), .en(EN), .Q(IR_2), .clk(CLK), .clr(clr));
  Register #(.width(32), .trigger("rising"), .Select("low")) u_PC (.D(PC), .en(EN), .Q(PC_2), .clk(CLK), .clr(clr));
endmodule

module EX_MEM (
  input  WB,
  input  MEM,
  input  RegWrite,
  input  JAL,
  input  [4:0] WriteReg_num,
  input  stop,
  input  [31:0] AluResult,
  input  [31:0] B,
  input  SB,
  input  [31:0] IR,
  input  [31:0] PC,
  input  EN,
  input  CLK,
  input  clr,
  output WB_2,
  output MEM_2,
  output RegWrite_2,
  output JAL_2,
  output [4:0] WriteReg_num_2,
  output stop_2,
  output [31:0] AluResult_2,
  output [31:0] B_2,
  output SB_2,
  output [31:0] IR_2,
  output [31:0] PC_2
);

  Register #(.width(1), .trigger("rising"), .Select("low")) u_WB (.D(WB), .en(EN), .Q(WB_2), .clk(CLK), .clr(clr));
  Register #(.width(1), .trigger("rising"), .Select("low")) u_MEM (.D(MEM), .en(EN), .Q(MEM_2), .clk(CLK), .clr(clr));
  Register #(.width(1), .trigger("rising"), .Select("low")) u_Regwrite (
    .D(RegWrite), .en(EN), .Q(RegWrite_2), .clk(CLK), .clr(clr));
  Register #(.width(1), .trigger("rising"), .Select("low")) u_JAL (.D(JAL), .en(EN), .Q(JAL_2), .clk(CLK), .clr(clr));
  Register #(.width(5), .trigger("rising"), .Select("low")) u_WriteReg_num (
    .D(WriteReg_num), .en(EN), .Q(WriteReg_num_2), .clk(CLK));  // open: clr
  Register #(.width(1), .trigger("rising"), .Select("low")) register_1 (
    .D(stop), .en(EN), .Q(stop_2), .clk(CLK));  // open: clr
  Register #(.width(32), .trigger("rising"), .Select("low")) u_AluResult (
    .D(AluResult), .en(EN), .Q(AluResult_2), .clk(CLK), .clr(clr));
  Register #(.width(32), .trigger("rising"), .Select("low")) u_B (.D(B), .en(EN), .Q(B_2), .clk(CLK), .clr(clr));
  Register #(.width(1), .trigger("rising"), .Select("low")) u_SB (.D(SB), .en(EN), .Q(SB_2), .clk(CLK), .clr(clr));
  Register #(.width(32), .trigger("rising"), .Select("low")) u_IR (.D(IR), .en(EN), .Q(IR_2), .clk(CLK), .clr(clr));
  Register #(.width(32), .trigger("rising"), .Select("low")) u_PC (.D(PC), .en(EN), .Q(PC_2), .clk(CLK), .clr(clr));
endmodule

module MEM_WB (
  input  WB,
  input  RegWrite,
  input  JAL,
  input  [4:0] WriteReg_num,
  input  [31:0] MD,
  input  [31:0] AluResult,
  input  [31:0] IR,
  input  [31:0] PC,
  input  EN,
  input  CLK,
  input  clr,
  output WB_2,
  output RegWrite_2,
  output JAL_2,
  output [4:0] WriteReg_num_2,
  output [31:0] MD_2,
  output [31:0] AluResult_2,
  output [31:0] IR_2,
  output [31:0] PC_2
);

  Register #(.width(1), .trigger("rising"), .Select("low")) u_WB (.D(WB), .en(EN), .Q(WB_2), .clk(CLK), .clr(clr));
  Register #(.width(1), .trigger("rising"), .Select("low")) u_Regwrite (
    .D(RegWrite), .en(EN), .Q(RegWrite_2), .clk(CLK), .clr(clr));
  Register #(.width(1), .trigger("rising"), .Select("low")) u_JAL (.D(JAL), .en(EN), .Q(JAL_2), .clk(CLK), .clr(clr));
  Register #(.width(5), .trigger("rising"), .Select("low")) u_WriteReg_num (
    .D(WriteReg_num), .en(EN), .Q(WriteReg_num_2), .clk(CLK));  // open: clr
  Register #(.width(32), .trigger("rising"), .Select("low")) u_MD (.D(MD), .en(EN), .Q(MD_2), .clk(CLK), .clr(clr));
  Register #(.width(32), .trigger("rising"), .Select("low")) u_AluResult (
    .D(AluResult), .en(EN), .Q(AluResult_2), .clk(CLK), .clr(clr));
  Register #(.width(32), .trigger("rising"), .Select("low")) u_IR (.D(IR), .en(EN), .Q(IR_2), .clk(CLK), .clr(clr));
  Register #(.width(32), .trigger("rising"), .Select("low")) u_PC (.D(PC), .en(EN), .Q(PC_2), .clk(CLK), .clr(clr));
endmodule

module forward (
  input  R1_used,
  input  R2_used,
  input  EX_RegWrite,
  input  MEM_RegWrite,
  input  [4:0] R1_num,
  input  [4:0] EX_WriteReg_num,
  input  [4:0] MEM_WriteReg_num,
  input  [4:0] R2_num,
  output [3:0] forward
);

  wire comparator_1_eq, comparator_2_eq, comparator_3_eq, comparator_4_eq, comparator_5_eq, comparator_6_eq;

  Comparator #(.width(5), .mode("twosComplement")) comparator_1 (
    .a({5{1'b0}}), .b(R1_num), .eq(comparator_1_eq));  // open: gt, lt
  Comparator #(.width(5), .mode("twosComplement")) comparator_2 (
    .a(R1_num), .b(EX_WriteReg_num), .eq(comparator_2_eq));  // open: gt, lt
  Comparator #(.width(5), .mode("twosComplement")) comparator_3 (
    .a(R1_num), .b(MEM_WriteReg_num), .eq(comparator_3_eq));  // open: gt, lt
  Comparator #(.width(5), .mode("twosComplement")) comparator_4 (
    .a(R2_num), .b(EX_WriteReg_num), .eq(comparator_4_eq));  // open: gt, lt
  Comparator #(.width(5), .mode("twosComplement")) comparator_5 (
    .a(R2_num), .b(MEM_WriteReg_num), .eq(comparator_5_eq));  // open: gt, lt
  Comparator #(.width(5), .mode("twosComplement")) comparator_6 (
    .a(R2_num), .b({5{1'b0}}), .eq(comparator_6_eq));  // open: gt, lt
  and and_1 (forward[0], ~comparator_1_eq, EX_RegWrite, comparator_2_eq, R1_used);  // AND_Gate
  and and_2 (forward[1], ~comparator_1_eq, MEM_RegWrite, comparator_3_eq, R1_used);  // AND_Gate
  and and_3 (forward[2], R2_used, EX_RegWrite, comparator_4_eq, ~comparator_6_eq);  // AND_Gate
  and and_4 (forward[3], R2_used, MEM_RegWrite, comparator_5_eq, ~comparator_6_eq);  // AND_Gate
endmodule

module \单重中断  (
  input  CLK,
  input  \_1号中断 ,
  input  \_2号中断 ,
  input  [1:0] in_4,
  input  \_3号中断 ,
  input  IE,
  input  ERET,
  output \_1号中断等待指示灯 ,
  output [1:0] out_9,
  output IR,
  output \_1号中断等待指示灯_2 ,
  output out_12,
  output \_3号中断等待指示灯 
);

  wire and_1_out, and_2_out, and_3_out, and_4_out, and_5_out, and_6_out, and_7_out, and_8_out, and_9_out,
       d_ff_1_q, d_ff_2_q, d_ff_3_q, IR1_q, IR2_q, IR3_q, or_4_out, or_5_out, or_6_out;
  wire [1:0] multiplexer_2_out;
  wire [2:0] multiplexer_1_out;

  or or_1 (\_1号中断等待指示灯 , IR1_q, d_ff_1_q);
  or or_2 (\_1号中断等待指示灯_2 , IR2_q, d_ff_2_q);
  or or_3 (\_3号中断等待指示灯 , IR3_q, d_ff_3_q);
  D_Flip_Flop #(.trigger("rising"), .Pre_Clr_Positions("LEGACY"), .NegatePresetClear("false"), .enable("true"), .NewFFLayout("false")) d_ff_1 (
    .clk(\_1号中断 ), .D(1'b1), .Q(d_ff_1_q), .reset(IR1_q));  // open: Qn, preset, en
  D_Flip_Flop #(.trigger("rising"), .Pre_Clr_Positions("LEGACY"), .NegatePresetClear("false"), .enable("true"), .NewFFLayout("false")) d_ff_2 (
    .clk(\_2号中断 ), .D(1'b1), .Q(d_ff_2_q), .reset(IR2_q));  // open: Qn, preset, en
  D_Flip_Flop #(.trigger("rising"), .Pre_Clr_Positions("LEGACY"), .NegatePresetClear("false"), .enable("true"), .NewFFLayout("false")) d_ff_3 (
    .clk(\_3号中断 ), .D(1'b1), .Q(d_ff_3_q), .reset(IR3_q));  // open: Qn, preset, en
  or or_4 (or_4_out, d_ff_1_q, IR1_q);
  or or_5 (or_5_out, d_ff_2_q, IR2_q);
  or or_6 (or_6_out, d_ff_3_q, IR3_q);
  and and_1 (and_1_out, or_4_out, ~multiplexer_1_out[0]);  // AND_Gate
  and and_2 (and_2_out, IE, ~and_3_out);  // AND_Gate
  and and_3 (and_3_out, ERET, IR1_q);
  and and_4 (and_4_out, or_5_out, ~multiplexer_1_out[1]);  // AND_Gate
  and and_5 (and_5_out, IE, ~and_6_out);  // AND_Gate
  and and_6 (and_6_out, ERET, IR2_q);
  and and_7 (and_7_out, or_6_out, ~multiplexer_1_out[2]);  // AND_Gate
  and and_8 (and_8_out, IE, ~and_9_out);  // AND_Gate
  and and_9 (and_9_out, IR3_q, ERET);
  D_Flip_Flop #(.trigger("rising"), .Pre_Clr_Positions("LEGACY"), .NegatePresetClear("false"), .enable("true"), .NewFFLayout("false")) IR1 (
    .clk(CLK), .D(and_1_out), .Q(IR1_q), .en(and_2_out));  // open: Qn, preset, reset
  D_Flip_Flop #(.trigger("rising"), .Pre_Clr_Positions("LEGACY"), .NegatePresetClear("false"), .enable("true"), .NewFFLayout("false")) IR2 (
    .clk(CLK), .D(and_4_out), .Q(IR2_q), .en(and_5_out));  // open: Qn, preset, reset
  D_Flip_Flop #(.trigger("rising"), .Pre_Clr_Positions("LEGACY"), .NegatePresetClear("false"), .enable("true"), .NewFFLayout("false")) IR3 (
    .clk(CLK), .D(and_7_out), .Q(IR3_q), .en(and_8_out));  // open: Qn, preset, reset
  Multiplexer #(.select(2), .width(3), .disabled(0), .enable("false")) multiplexer_1 (
    .in0(3'b000), .in1(3'b001), .in2(3'b010), .in3(3'b100), .out(multiplexer_1_out), .sel(out_9));
  Priority_Encoder #(.select(2), .disabled(0)) priority_encoder_1 (
    .in0(1'b1), .in1(IR1_q), .in2(IR2_q), .in3(IR3_q), .out(out_9));  // open: gs, en_out, en_in
  or or_7 (IR, IR3_q, IR2_q, IR1_q);
  Multiplexer #(.select(1), .width(2), .disabled("Z"), .enable("false")) multiplexer_2 (
    .in0(in_4), .in1(out_9), .out(multiplexer_2_out), .sel(and_8_out));
  Multiplexer #(.select(2), .width(1), .disabled("Z"), .enable("false")) multiplexer_3 (
    .in0(1'b0), .in1(IR1_q), .in2(IR2_q), .in3(IR3_q), .out(out_12), .sel(multiplexer_2_out));

  // Notes on the sheet:
  //   中断信号采样参考电路
  //   Reset 
  //   Reset 
  //   Reset 
endmodule

module MTC (
  input  [31:0] R2,
  input  MTC0,
  input  [4:0] Rd,
  input  CLK,
  output [31:0] Status,
  output [31:0] EPC
);

  wire and_1_out, and_2_out, and_3_out, and_4_out, not_1_out, not_2_out, not_3_out, not_4_out, not_5_out;

  not not_1 (not_1_out, Rd[0]);
  not not_2 (not_2_out, Rd[3]);
  not not_3 (not_3_out, Rd[4]);
  not not_4 (not_4_out, Rd[0]);
  not not_5 (not_5_out, Rd[4]);
  and and_1 (and_1_out, not_1_out, Rd[1], Rd[2], not_2_out, not_3_out);
  and and_2 (and_2_out, not_4_out, Rd[1], Rd[2], Rd[3], not_5_out);
  and and_3 (and_3_out, MTC0, and_1_out);
  and and_4 (and_4_out, MTC0, and_2_out);
  Register #(.width(32), .trigger("rising"), .Select("low")) u_Status (
    .D(R2), .en(and_3_out), .Q(Status), .clk(CLK));  // open: clr
  Register #(.width(32), .trigger("rising"), .Select("low")) u_EPC (
    .D(R2), .en(and_4_out), .Q(EPC), .clk(CLK));  // open: clr
endmodule

module \多中断  (
  input  CLK,
  input  \_1号中断 ,
  input  \_2号中断 ,
  input  [1:0] in_4,
  input  \_3号中断 ,
  input  IE,
  input  ERET,
  output \_1号中断等待指示灯 ,
  output [1:0] out_9,
  output IR,
  output \_2号中断等待指示灯 ,
  output out_12,
  output \_3号中断等待指示灯 
);

  wire and_1_out, and_2_out, and_3_out, and_4_out, and_5_out, comparator_1_gt, d_ff_1_q, d_ff_2_q, d_ff_3_q,
       IR1_q, IR2_q, IR3_q, not_1_out, or_4_out, or_5_out, or_6_out, or_7_out, or_8_out, or_9_out;
  wire [1:0] multiplexer_2_out;
  wire [2:0] multiplexer_1_out;

  or or_1 (\_1号中断等待指示灯 , IR1_q, d_ff_1_q);
  or or_2 (\_2号中断等待指示灯 , IR2_q, d_ff_2_q);
  or or_3 (\_3号中断等待指示灯 , IR3_q, d_ff_3_q);
  D_Flip_Flop #(.trigger("rising"), .Pre_Clr_Positions("LEGACY"), .NegatePresetClear("false"), .enable("true"), .NewFFLayout("false")) d_ff_1 (
    .clk(\_1号中断 ), .D(1'b1), .Q(d_ff_1_q), .reset(IR1_q));  // open: Qn, preset, en
  D_Flip_Flop #(.trigger("rising"), .Pre_Clr_Positions("LEGACY"), .NegatePresetClear("false"), .enable("true"), .NewFFLayout("false")) d_ff_2 (
    .clk(\_2号中断 ), .D(1'b1), .Q(d_ff_2_q), .reset(IR2_q));  // open: Qn, preset, en
  D_Flip_Flop #(.trigger("rising"), .Pre_Clr_Positions("LEGACY"), .NegatePresetClear("false"), .enable("true"), .NewFFLayout("false")) d_ff_3 (
    .clk(\_3号中断 ), .D(1'b1), .Q(d_ff_3_q), .reset(IR3_q));  // open: Qn, preset, en
  or or_4 (or_4_out, d_ff_1_q, IR1_q);
  or or_5 (or_5_out, d_ff_2_q, IR2_q);
  or or_6 (or_6_out, d_ff_3_q, IR3_q);
  and and_1 (and_1_out, or_4_out, ~multiplexer_1_out[0]);  // AND_Gate
  or or_7 (or_7_out, d_ff_1_q, and_4_out);
  and and_2 (and_2_out, or_5_out, ~multiplexer_1_out[1]);  // AND_Gate
  or or_8 (or_8_out, d_ff_2_q, and_4_out);
  and and_3 (and_3_out, or_6_out, ~multiplexer_1_out[2]);  // AND_Gate
  or or_9 (or_9_out, d_ff_3_q, and_4_out);
  D_Flip_Flop #(.trigger("rising"), .Pre_Clr_Positions("LEGACY"), .NegatePresetClear("false"), .enable("true"), .NewFFLayout("false")) IR1 (
    .clk(CLK), .D(and_1_out), .Q(IR1_q), .en(or_7_out));  // open: Qn, preset, reset
  D_Flip_Flop #(.trigger("rising"), .Pre_Clr_Positions("LEGACY"), .NegatePresetClear("false"), .enable("true"), .NewFFLayout("false")) IR2 (
    .clk(CLK), .D(and_2_out), .Q(IR2_q), .en(or_8_out));  // open: Qn, preset, reset
  D_Flip_Flop #(.trigger("rising"), .Pre_Clr_Positions("LEGACY"), .NegatePresetClear("false"), .enable("true"), .NewFFLayout("false")) IR3 (
    .clk(CLK), .D(and_3_out), .Q(IR3_q), .en(or_9_out));  // open: Qn, preset, reset
  and and_4 (and_4_out, and_5_out, ~ERET);  // AND_Gate
  and and_5 (and_5_out, IE, not_1_out);
  Multiplexer #(.select(2), .width(3), .disabled(0), .enable("false")) multiplexer_1 (
    .in0(3'b000), .in1(3'b001), .in2(3'b010), .in3(3'b100), .out(multiplexer_1_out), .sel(out_9));
  Priority_Encoder #(.select(2), .disabled(0)) priority_encoder_1 (
    .in0(1'b1), .in1(IR1_q), .in2(IR2_q), .in3(IR3_q), .out(out_9));  // open: gs, en_out, en_in
  or or_10 (IR, IR3_q, IR2_q, IR1_q);
  Multiplexer #(.select(1), .width(2), .disabled("Z"), .enable("false")) multiplexer_2 (
    .in0(in_4), .in1(out_9), .out(multiplexer_2_out), .sel(and_5_out));
  Multiplexer #(.select(2), .width(1), .disabled("Z"), .enable("false")) multiplexer_3 (
    .in0(1'b0), .in1(IR1_q), .in2(IR2_q), .in3(IR3_q), .out(out_12), .sel(multiplexer_2_out));
  not not_1 (not_1_out, comparator_1_gt);
  Comparator #(.width(2), .mode("unsigned")) comparator_1 (.a(in_4), .b(out_9), .gt(comparator_1_gt));  // open: eq, lt

  // Notes on the sheet:
  //   中断信号采样参考电路
  //   Reset 
  //   Reset 
  //   Reset 
endmodule
