// Logisim project dhb-cpu24_backup-版本4.circ as structural Verilog: 18 circuits, main circuit ◇单周期MIPS
module \单周期MIPS  (
  output RegWrite,
  output MemWrite,
  output [31:0] PC,
  output [31:0] IR,
  output [31:0] RDin,
  output [31:0] MDin
);

  wire and_1_out, Branch, CLK, comparator_1_eq, Go, halt, IR1, IR2, IR3, mips_ram_adapter_1_clk_2,
       mips_ram_adapter_1_str, not_1_out, not_2_out, or_3_out, SignedExt, Syscall, W1, W2, W3,
       \单周期硬布线控制器_1_alu_src , \单周期硬布线控制器_1_jal , \单周期硬布线控制器_1_jmp , \单周期硬布线控制器_1_jr , \单周期硬布线控制器_1_memtoreg ,
       \单周期硬布线控制器_1_regdst ;
  wire [1:0] or_2_out;
  wire [2:0] \单周期硬布线控制器_1_memcontrol ;
  wire [4:0] multiplexer_2_out, multiplexer_4_out, multiplexer_5_out, multiplexer_6_out;
  wire [6:0] \单周期硬布线控制器_1_alu_op ;
  wire [9:0] mips_ram_adapter_1_a;
  wire [15:0] \总周期数 ;
  wire [31:0] adder_1_out, adder_2_out, bit_extender_1_out, bit_extender_2_out, LedData, mips_alu_1_result,
       mips_ram_adapter_1_dataout, mips_ram_adapter_1_din, multiplexer_1_out, multiplexer_7_out,
       multiplexer_8_out, multiplexer_9_out, ram_1_data, shifter_1_out, v0;

  Clock #(.highDuration(1), .lowDuration(1)) clock_1 (.out(CLK));
  Button _1 (.out(IR1));
  Button _2 (.out(IR2));
  Button _3 (.out(IR3));
  Button \u_继续运行  (.out(Go));
  LED #(.active("true")) led_1 (.in(W1));
  LED #(.active("true")) led_2 (.in(W2));
  LED #(.active("true")) led_3 (.in(W3));
  Register #(.width(32), .trigger("rising"), .Select("low")) u_PC (
    .D(multiplexer_1_out), .en(not_1_out), .Q(PC), .clk(CLK));  // open: clr
  Multiplexer #(.select(2), .width(32), .disabled("Z"), .enable("false")) multiplexer_1 (
    .in0(adder_1_out), .in1(multiplexer_9_out), .in2(adder_2_out), .in3({PC[31:28], IR[25:0], 2'b00}),
    .out(multiplexer_1_out), .sel(or_2_out));
  not not_1 (not_1_out, halt);
  not not_2 (not_2_out, halt);
  Hex_Digit_Display hex_digit_display_1 (.value(LedData[31:28]));  // open: dp
  or or_1 (or_2_out[1], Branch, or_3_out);
  or or_2 (or_2_out[0], \单周期硬布线控制器_1_jr , or_3_out);
  Counter #(.width(16), .max('hffff), .ongoal("stay"), .trigger("rising"), .behavior("old")) \u_总周期数  (
    .count(not_2_out), .Q(\总周期数 ), .clk(CLK));  // open: load, D, carry, clr, preset
  Hex_Digit_Display hex_digit_display_2 (.value(LedData[27:24]));  // open: dp
  Hex_Digit_Display hex_digit_display_3 (.value(LedData[23:20]));  // open: dp
  or or_3 (or_3_out, \单周期硬布线控制器_1_jmp , \单周期硬布线控制器_1_jal );
  Adder #(.width(32)) adder_1 (.a(PC), .b(32'h4), .out(adder_1_out));  // open: cin, cout
  Hex_Digit_Display hex_digit_display_4 (.value(LedData[19:16]));  // open: dp
  Hex_Digit_Display hex_digit_display_5 (.value(LedData[15:12]));  // open: dp
  ROM #(.addrWidth(10), .dataWidth(32), .Select("high")) rom_1 (.addr(PC[11:2]), .data(IR));
  Adder #(.width(32)) adder_2 (.a(adder_1_out), .b(shifter_1_out), .out(adder_2_out));  // open: cin, cout
  Hex_Digit_Display hex_digit_display_6 (.value(LedData[7:4]));  // open: dp
  Hex_Digit_Display hex_digit_display_7 (.value(LedData[11:8]));  // open: dp
  // Probe on \总周期数 
  Comparator #(.width(32), .mode("unsigned")) comparator_1 (.a(v0), .b(32'ha), .eq(comparator_1_eq));  // open: gt, lt
  Hex_Digit_Display hex_digit_display_8 (.value(LedData[3:0]));  // open: dp
  Multiplexer #(.select(1), .width(5), .disabled("Z"), .enable("false")) multiplexer_2 (
    .in0(IR[20:16]), .in1(IR[15:11]), .out(multiplexer_2_out), .sel(\单周期硬布线控制器_1_regdst ));
  Multiplexer #(.select(1), .width(32), .disabled("Z"), .enable("false")) multiplexer_3 (
    .in0(multiplexer_9_out), .in1(adder_1_out), .out(RDin), .sel(\单周期硬布线控制器_1_jal ));
  assign bit_extender_1_out = {{16{1'b0}}, IR[15:0]};  // Bit_Extender bit_extender_1
  assign bit_extender_2_out = {{16{IR[15]}}, IR[15:0]};  // Bit_Extender bit_extender_2
  and and_1 (and_1_out, ~comparator_1_eq, Syscall);  // AND_Gate
  Register #(.width(32), .trigger("rising"), .Select("low")) register_1 (
    .D(MDin), .en(and_1_out), .Q(LedData), .clk(CLK));  // open: clr
  \单周期硬布线控制器  \u_单周期硬布线控制器_1  (
    .IR(IR), .ALU_OP(\单周期硬布线控制器_1_alu_op ), .MemToReg(\单周期硬布线控制器_1_memtoreg ),
    .MemControl({MemWrite, \单周期硬布线控制器_1_memcontrol }), .ALU_SRC(\单周期硬布线控制器_1_alu_src ), .RegWrite(RegWrite),
    .SysCALL(Syscall), .SignedExt(SignedExt), .RegDst(\单周期硬布线控制器_1_regdst ), .JR(\单周期硬布线控制器_1_jr ),
    .JMP(\单周期硬布线控制器_1_jmp ), .JAL(\单周期硬布线控制器_1_jal ));  // open: R1_Used, R2_Used
  Multiplexer #(.select(1), .width(5), .disabled("Z"), .enable("false")) multiplexer_4 (
    .in0(IR[25:21]), .in1(5'b00010), .out(multiplexer_4_out), .sel(Syscall));
  Multiplexer #(.select(1), .width(5), .disabled("Z"), .enable("false")) multiplexer_5 (
    .in0(IR[20:16]), .in1(5'b00100), .out(multiplexer_5_out), .sel(Syscall));
  Multiplexer #(.select(1), .width(5), .disabled("Z"), .enable("false")) multiplexer_6 (
    .in0(multiplexer_2_out), .in1({5{1'b1}}), .out(multiplexer_6_out), .sel(\单周期硬布线控制器_1_jal ));
  Multiplexer #(.select(1), .width(32), .disabled("Z"), .enable("false")) multiplexer_7 (
    .in0(bit_extender_1_out), .in1(bit_extender_2_out), .out(multiplexer_7_out), .sel(SignedExt));
  and and_2 (halt, comparator_1_eq, Syscall);
  MIPS_Regifile mips_regifile_1 (
    .Din(RDin), .Clk(CLK), .R1(v0), .R2(MDin), .WE(RegWrite), .W_num(multiplexer_6_out),
    .R1_num(multiplexer_4_out), .R2_num(multiplexer_5_out));
  Multiplexer #(.select(1), .width(32), .disabled("Z"), .enable("false")) multiplexer_8 (
    .in0(MDin), .in1(multiplexer_7_out), .out(multiplexer_8_out), .sel(\单周期硬布线控制器_1_alu_src ));
  Shifter #(.width(32), .shift("ll")) shifter_1 (.in(multiplexer_7_out), .\dist (5'b00010), .out(shifter_1_out));
  MIPS_ALU mips_alu_1 (
    .X(v0), .Y(multiplexer_8_out), .AluOP(\单周期硬布线控制器_1_alu_op ), .Branch(Branch), .Result(mips_alu_1_result),
    .shamt(IR[10:6]));  // open: Result_2
  MIPS_Ram_Adapter mips_ram_adapter_1 (
    .Addr(mips_alu_1_result), .DataIn(MDin), .dout(ram_1_data), .CLK(CLK),
    .CONTROL({MemWrite, \单周期硬布线控制器_1_memcontrol }), .A(mips_ram_adapter_1_a), .din(mips_ram_adapter_1_din),
    .DataOut(mips_ram_adapter_1_dataout), .clk_2(mips_ram_adapter_1_clk_2), .str(mips_ram_adapter_1_str));
  RAM #(.addrWidth(10), .dataWidth(32), .bus("separate"), .Select("high")) ram_1 (
    .addr(mips_ram_adapter_1_a), .din(mips_ram_adapter_1_din), .data(ram_1_data),
    .str(mips_ram_adapter_1_str), .clk(mips_ram_adapter_1_clk_2));  // open: sel, ld, clr
  Multiplexer #(.select(1), .width(32), .disabled("Z"), .enable("false")) multiplexer_9 (
    .in0(mips_alu_1_result), .in1(mips_ram_adapter_1_dataout), .out(multiplexer_9_out),
    .sel(\单周期硬布线控制器_1_memtoreg ));

  // Other names for the same wires on the sheet: a0[31:0] = MDin

  // Notes on the sheet:
  //   中断源
  //   PC+4
  //   JR
  //   J/JAL
  //   PC计数器
  //   中断等待指示
  //   总复位信号应将除ROM以外所有存储组件全部清零
  //   BEQ/BNE
  //   指令存储器
  //   PC+4
  //   数码管输出
  //   指令字
  //   contents of rom_1 (hex, n*v repeats v):
  //   20110001 8000c05 20110001 20120002 20130003 8000c09 20110001 20120002 20130003 8000c0d 20110001
  //   20120002 20130003 8000c11 20110001 20120002 20130003 c000cb8 20100001 20110001 118fc0 112020
  //   20020022 c 118882 12200001 8000c15 112020 20020022 c 20110001 118880 112020 20020022 c 12200001
  //   8000c1f 20110001 118fc0 112020 20020022 c 1188c3 112020 20020022 c 118903 112020 20020022 c 118903
  //   112020 20020022 c 118903 112020 20020022 c 118903 112020 20020022 c 118903 112020 20020022 c 118903
  //   112020 20020022 c 118903 112020 20020022 c 20100001 109fc0 139fc3 8021 2012000c 24160003 26100001
  //   3210000f 20080008 20090001 139900 2709825 132020 20020022 c 1094022 1500fff9 22100001 2018000f
  //   2188024 108700 20080008 20090001 139902 2709825 132021 20020022 c 1094022 1500fff9 108702 2c9b022
  //   12c00001 8000c50 4020 1084027 84400 3508ffff 82021 20020022 c 2010ffff 20110000 ae300000 22100001
  //   22310004 ae300000 22100001 22310004 ae300000 22100001 22310004 ae300000 22100001 22310004 ae300000
  //   22100001 22310004 ae300000 22100001 22310004 ae300000 22100001 22310004 ae300000 22100001 22310004
  //   ae300000 22100001 22310004 ae300000 22100001 22310004 ae300000 22100001 22310004 ae300000 22100001
  //   22310004 ae300000 22100001 22310004 ae300000 22100001 22310004 ae300000 22100001 22310004 ae300000
  //   22100001 22310004 22100001 8020 2011003c 8e130000 8e340000 274402a 11000002 ae330000 ae140000
  //   2231fffc 1611fff8 102020 20020022 c 22100004 2011003c 1611fff2 2002000a c 20100000 22100001 102020
  //   20020022 c 22100002 102020 20020022 c 22100003 102020 20020022 c 22100004 102020 20020022 c 22100005
  //   102020 20020022 c 22100006 102020 20020022 c 22100007 102020 20020022 c 22100008 102020 20020022
  //   20020022 c 3e00008
  //   addr
  //   数码管输出应该用寄存器锁存，否则显示数据只能一闪而过
  //   JMP
  //   JR
  //   IR
  //   rs
  //   rt
  //   rd
  //   imm
  //   shamt
  //   Syscall功能实现
  //   MemToReg
  //   MemControl
  //   AluOP
  //   AluSrcB
  //   RegWrite
  //   JAL
  //   RegDst
  //   Syscall
  //   为方便自动评测，需要输出PC，IR，寄存器文件写入端口RDin，内存写入端口MDin等信号
endmodule

// 单周期硬布线控制器
module \单周期硬布线控制器  (
  input  [31:0] IR,
  output [6:0] ALU_OP,
  output MemToReg,
  output [3:0] MemControl,
  output ALU_SRC,
  output RegWrite,
  output SysCALL,
  output SignedExt,
  output RegDst,
  output JR,
  output JMP,
  output JAL,
  output R1_Used,
  output R2_Used
);

  \运算控制器自动生成  \u_运算控制器自动生成_1  (
    .OP0(IR[26]), .OP1(IR[27]), .OP2(IR[28]), .OP3(IR[29]), .OP4(IR[30]), .OP5(IR[31]), .F0(IR[0]),
    .F1(IR[1]), .F2(IR[2]), .F3(IR[3]), .F4(IR[4]), .F5(IR[5]), .RT0(IR[16]), .S0(ALU_OP[0]), .S1(ALU_OP[1]),
    .S2(ALU_OP[2]), .S3(ALU_OP[3]), .B0(ALU_OP[4]), .B1(ALU_OP[5]), .B2(ALU_OP[6]));
  \控制信号自动生成  \u_控制信号自动生成_1  (
    .OP0(IR[26]), .OP1(IR[27]), .OP2(IR[28]), .OP3(IR[29]), .OP4(IR[30]), .OP5(IR[31]), .F0(IR[0]),
    .F1(IR[1]), .F2(IR[2]), .F3(IR[3]), .F4(IR[4]), .F5(IR[5]), .MemToReg(MemToReg),
    .MemWrite(MemControl[3]), .MemHalf(MemControl[2]), .MemByte(MemControl[1]), .MemUnsigned(MemControl[0]),
    .ALU_SRC(ALU_SRC), .RegWrite(RegWrite), .SysCALL(SysCALL), .SignedExt(SignedExt), .RegDst(RegDst),
    .JR(JR), .JUMP(JMP), .JAL(JAL));
  \源寄存器使用情况  \u_源寄存器使用情况_1  (
    .OP0(IR[26]), .OP1(IR[27]), .OP2(IR[28]), .OP3(IR[29]), .OP4(IR[30]), .OP5(IR[31]), .F0(IR[0]),
    .F1(IR[1]), .F2(IR[2]), .F3(IR[3]), .F4(IR[4]), .F5(IR[5]), .R1_Used(R1_Used), .R2_Used(R2_Used));

  // Notes on the sheet:
  //   OP
  //   rt
  //   Func
  //   运算器控制器，根据指令生成运算器功能选择信号
  //   控制信号生成，产生数据通路需要的其他控制信号
endmodule

// 运算器控制器
module \运算控制器自动生成  (
  input  OP0,
  input  OP1,
  input  OP2,
  input  OP3,
  input  OP4,
  input  OP5,
  input  F0,
  input  F1,
  input  F2,
  input  F3,
  input  F4,
  input  F5,
  input  RT0,
  output S0,
  output S1,
  output S2,
  output S3,
  output B0,
  output B1,
  output B2
);

  wire and_1_out, and_2_out, and_3_out, and_4_out, and_5_out, and_6_out, and_7_out, and_8_out, and_9_out,
       and_10_out, and_11_out, and_12_out, and_13_out, and_14_out, and_15_out, and_16_out, and_17_out,
       and_18_out, and_19_out, and_20_out, and_21_out, and_22_out, and_23_out, and_24_out, and_25_out,
       and_26_out, and_27_out, and_28_out, and_29_out, and_30_out, and_31_out, and_32_out, and_33_out,
       and_34_out, and_35_out, and_36_out, and_37_out, and_38_out, and_39_out, and_40_out, and_41_out,
       not_1_out, not_2_out, not_3_out, not_4_out, not_5_out, not_6_out, not_7_out, not_8_out, not_9_out,
       not_10_out, not_11_out, not_12_out, not_13_out, not_14_out, not_15_out, not_16_out, not_17_out,
       not_18_out, not_19_out, not_20_out, not_21_out, not_22_out, not_23_out, not_24_out, not_25_out,
       not_26_out, not_27_out, not_28_out, not_29_out, not_30_out, not_31_out, not_32_out, not_33_out,
       not_34_out, not_35_out, not_36_out, not_37_out, not_38_out, not_39_out, not_40_out, not_41_out,
       not_42_out, not_43_out, not_44_out, not_45_out, not_46_out, not_47_out, not_48_out, not_49_out,
       not_50_out, not_51_out, not_52_out, not_53_out, not_54_out, not_55_out, not_56_out, not_57_out,
       not_58_out, not_59_out, not_60_out, not_61_out, not_62_out, not_63_out, not_64_out, not_65_out,
       not_66_out, not_67_out, not_68_out, not_69_out, not_70_out, not_71_out, not_72_out, not_73_out,
       not_74_out, not_75_out, not_76_out, not_77_out, not_78_out, not_79_out, not_80_out, not_81_out,
       not_82_out, not_83_out, not_84_out, not_85_out, not_86_out, not_87_out, not_88_out, not_89_out,
       not_90_out, not_91_out, not_92_out, not_93_out, not_94_out, not_95_out, not_96_out, not_97_out,
       not_98_out, not_99_out, not_100_out, not_101_out, not_102_out, not_103_out, not_104_out, not_105_out,
       not_106_out, not_107_out, not_108_out, not_109_out, not_110_out, not_111_out, not_112_out,
       not_113_out, not_114_out, not_115_out, not_116_out, not_117_out, not_118_out, not_119_out,
       not_120_out, not_121_out, not_122_out, not_123_out, not_124_out, not_125_out, not_126_out,
       not_127_out, not_128_out, not_129_out, not_130_out, not_131_out, not_132_out, not_133_out,
       not_134_out, not_135_out, not_136_out, not_137_out, not_138_out, not_139_out, not_140_out,
       not_141_out, not_142_out, not_143_out, not_144_out, not_145_out, not_146_out, not_147_out,
       not_148_out, not_149_out, not_150_out, not_151_out, not_152_out, not_153_out, not_154_out,
       not_155_out, not_156_out, not_157_out, not_158_out, not_159_out, not_160_out, not_161_out,
       not_162_out, not_163_out, not_164_out, not_165_out, not_166_out, not_167_out, not_168_out,
       not_169_out, not_170_out, not_171_out, not_172_out, not_173_out, not_174_out, not_175_out,
       not_176_out, not_177_out, not_178_out, not_179_out, not_180_out, not_181_out, not_182_out,
       not_183_out, not_184_out, not_185_out, not_186_out, not_187_out, not_188_out, not_189_out,
       not_190_out, not_191_out, not_192_out, not_193_out, not_194_out, not_195_out, not_196_out,
       not_197_out, not_198_out, not_199_out, not_200_out, not_201_out, not_202_out, not_203_out,
       not_204_out, not_205_out, not_206_out, not_207_out, not_208_out, not_209_out, not_210_out,
       not_211_out, not_212_out, not_213_out, not_214_out, not_215_out, not_216_out, not_217_out,
       not_218_out, not_219_out, not_220_out, not_221_out, not_222_out, not_223_out, not_224_out,
       not_225_out, not_226_out, not_227_out, not_228_out, not_229_out, not_230_out, not_231_out,
       not_232_out, not_233_out, not_234_out, not_235_out, not_236_out, not_237_out, not_238_out;

  not not_1 (not_1_out, OP0);
  not not_2 (not_2_out, OP1);
  not not_3 (not_3_out, OP2);
  not not_4 (not_4_out, OP4);
  not not_5 (not_5_out, F1);
  not not_6 (not_6_out, F2);
  not not_7 (not_7_out, F3);
  not not_8 (not_8_out, F4);
  not not_9 (not_9_out, OP0);
  not not_10 (not_10_out, OP1);
  not not_11 (not_11_out, OP2);
  not not_12 (not_12_out, OP4);
  not not_13 (not_13_out, F0);
  not not_14 (not_14_out, F3);
  not not_15 (not_15_out, F4);
  not not_16 (not_16_out, OP0);
  not not_17 (not_17_out, OP1);
  not not_18 (not_18_out, OP2);
  not not_19 (not_19_out, OP4);
  not not_20 (not_20_out, F0);
  not not_21 (not_21_out, F2);
  not not_22 (not_22_out, F4);
  not not_23 (not_23_out, OP0);
  not not_24 (not_24_out, OP1);
  not not_25 (not_25_out, OP2);
  not not_26 (not_26_out, OP4);
  not not_27 (not_27_out, F2);
  not not_28 (not_28_out, F3);
  not not_29 (not_29_out, F4);
  not not_30 (not_30_out, F5);
  not not_31 (not_31_out, OP1);
  not not_32 (not_32_out, OP3);
  not not_33 (not_33_out, OP4);
  not not_34 (not_34_out, OP0);
  not not_35 (not_35_out, OP4);
  not not_36 (not_36_out, OP5);
  not not_37 (not_37_out, OP1);
  not not_38 (not_38_out, OP2);
  not not_39 (not_39_out, OP4);
  not not_40 (not_40_out, OP2);
  not not_41 (not_41_out, OP4);
  not not_42 (not_42_out, OP0);
  not not_43 (not_43_out, OP1);
  not not_44 (not_44_out, OP2);
  not not_45 (not_45_out, OP3);
  not not_46 (not_46_out, OP4);
  not not_47 (not_47_out, OP5);
  not not_48 (not_48_out, F0);
  not not_49 (not_49_out, F1);
  not not_50 (not_50_out, F3);
  not not_51 (not_51_out, F4);
  not not_52 (not_52_out, OP0);
  not not_53 (not_53_out, OP1);
  not not_54 (not_54_out, OP2);
  not not_55 (not_55_out, OP3);
  not not_56 (not_56_out, OP4);
  not not_57 (not_57_out, OP5);
  not not_58 (not_58_out, F0);
  not not_59 (not_59_out, F1);
  not not_60 (not_60_out, F4);
  not not_61 (not_61_out, F5);
  not not_62 (not_62_out, OP0);
  not not_63 (not_63_out, OP1);
  not not_64 (not_64_out, OP2);
  not not_65 (not_65_out, OP3);
  not not_66 (not_66_out, OP4);
  not not_67 (not_67_out, OP5);
  not not_68 (not_68_out, F0);
  not not_69 (not_69_out, F3);
  not not_70 (not_70_out, F4);
  not not_71 (not_71_out, F5);
  not not_72 (not_72_out, OP0);
  not not_73 (not_73_out, OP1);
  not not_74 (not_74_out, OP2);
  not not_75 (not_75_out, OP3);
  not not_76 (not_76_out, OP4);
  not not_77 (not_77_out, OP5);
  not not_78 (not_78_out, F0);
  not not_79 (not_79_out, F2);
  not not_80 (not_80_out, F4);
  not not_81 (not_81_out, OP0);
  not not_82 (not_82_out, OP1);
  not not_83 (not_83_out, OP2);
  not not_84 (not_84_out, OP3);
  not not_85 (not_85_out, OP4);
  not not_86 (not_86_out, OP5);
  not not_87 (not_87_out, F2);
  not not_88 (not_88_out, F3);
  not not_89 (not_89_out, F4);
  not not_90 (not_90_out, OP0);
  not not_91 (not_91_out, OP1);
  not not_92 (not_92_out, OP2);
  not not_93 (not_93_out, OP3);
  not not_94 (not_94_out, OP4);
  not not_95 (not_95_out, OP5);
  not not_96 (not_96_out, F3);
  not not_97 (not_97_out, F4);
  not not_98 (not_98_out, OP0);
  not not_99 (not_99_out, OP1);
  not not_100 (not_100_out, OP4);
  not not_101 (not_101_out, OP5);
  not not_102 (not_102_out, OP0);
  not not_103 (not_103_out, OP2);
  not not_104 (not_104_out, OP4);
  not not_105 (not_105_out, OP5);
  not not_106 (not_106_out, OP0);
  not not_107 (not_107_out, OP1);
  not not_108 (not_108_out, OP2);
  not not_109 (not_109_out, OP4);
  not not_110 (not_110_out, F2);
  not not_111 (not_111_out, F3);
  not not_112 (not_112_out, F4);
  not not_113 (not_113_out, OP0);
  not not_114 (not_114_out, OP1);
  not not_115 (not_115_out, OP2);
  not not_116 (not_116_out, OP4);
  not not_117 (not_117_out, F0);
  not not_118 (not_118_out, F1);
  not not_119 (not_119_out, F3);
  not not_120 (not_120_out, F4);
  not not_121 (not_121_out, OP0);
  not not_122 (not_122_out, OP1);
  not not_123 (not_123_out, OP2);
  not not_124 (not_124_out, OP4);
  not not_125 (not_125_out, F0);
  not not_126 (not_126_out, F1);
  not not_127 (not_127_out, F4);
  not not_128 (not_128_out, F5);
  not not_129 (not_129_out, OP0);
  not not_130 (not_130_out, OP1);
  not not_131 (not_131_out, OP2);
  not not_132 (not_132_out, OP4);
  not not_133 (not_133_out, F3);
  not not_134 (not_134_out, F4);
  not not_135 (not_135_out, F5);
  not not_136 (not_136_out, OP0);
  not not_137 (not_137_out, OP1);
  not not_138 (not_138_out, OP2);
  not not_139 (not_139_out, OP4);
  not not_140 (not_140_out, F2);
  not not_141 (not_141_out, F4);
  not not_142 (not_142_out, OP1);
  not not_143 (not_143_out, OP3);
  not not_144 (not_144_out, OP4);
  not not_145 (not_145_out, OP0);
  not not_146 (not_146_out, OP1);
  not not_147 (not_147_out, OP4);
  not not_148 (not_148_out, OP5);
  not not_149 (not_149_out, OP1);
  not not_150 (not_150_out, OP2);
  not not_151 (not_151_out, OP4);
  not not_152 (not_152_out, OP2);
  not not_153 (not_153_out, OP4);
  not not_154 (not_154_out, OP2);
  not not_155 (not_155_out, OP4);
  not not_156 (not_156_out, OP0);
  not not_157 (not_157_out, OP1);
  not not_158 (not_158_out, OP2);
  not not_159 (not_159_out, OP3);
  not not_160 (not_160_out, OP4);
  not not_161 (not_161_out, OP5);
  not not_162 (not_162_out, F0);
  not not_163 (not_163_out, F1);
  not not_164 (not_164_out, F2);
  not not_165 (not_165_out, F4);
  not not_166 (not_166_out, F5);
  not not_167 (not_167_out, OP0);
  not not_168 (not_168_out, OP1);
  not not_169 (not_169_out, OP2);
  not not_170 (not_170_out, OP3);
  not not_171 (not_171_out, OP4);
  not not_172 (not_172_out, OP5);
  not not_173 (not_173_out, F0);
  not not_174 (not_174_out, F3);
  not not_175 (not_175_out, F4);
  not not_176 (not_176_out, F5);
  not not_177 (not_177_out, OP0);
  not not_178 (not_178_out, OP1);
  not not_179 (not_179_out, OP2);
  not not_180 (not_180_out, OP3);
  not not_181 (not_181_out, OP4);
  not not_182 (not_182_out, OP5);
  not not_183 (not_183_out, F2);
  not not_184 (not_184_out, F4);
  not not_185 (not_185_out, OP0);
  not not_186 (not_186_out, OP1);
  not not_187 (not_187_out, OP2);
  not not_188 (not_188_out, OP3);
  not not_189 (not_189_out, OP4);
  not not_190 (not_190_out, OP5);
  not not_191 (not_191_out, F3);
  not not_192 (not_192_out, F4);
  not not_193 (not_193_out, OP0);
  not not_194 (not_194_out, OP1);
  not not_195 (not_195_out, OP2);
  not not_196 (not_196_out, OP3);
  not not_197 (not_197_out, OP4);
  not not_198 (not_198_out, OP5);
  not not_199 (not_199_out, F3);
  not not_200 (not_200_out, F4);
  not not_201 (not_201_out, OP0);
  not not_202 (not_202_out, OP4);
  not not_203 (not_203_out, OP5);
  not not_204 (not_204_out, OP2);
  not not_205 (not_205_out, OP4);
  not not_206 (not_206_out, OP5);
  not not_207 (not_207_out, OP1);
  not not_208 (not_208_out, OP4);
  not not_209 (not_209_out, OP5);
  not not_210 (not_210_out, OP0);
  not not_211 (not_211_out, OP1);
  not not_212 (not_212_out, OP3);
  not not_213 (not_213_out, OP4);
  not not_214 (not_214_out, OP5);
  not not_215 (not_215_out, OP1);
  not not_216 (not_216_out, OP2);
  not not_217 (not_217_out, OP3);
  not not_218 (not_218_out, OP4);
  not not_219 (not_219_out, OP5);
  not not_220 (not_220_out, OP3);
  not not_221 (not_221_out, OP4);
  not not_222 (not_222_out, OP5);
  not not_223 (not_223_out, OP1);
  not not_224 (not_224_out, OP3);
  not not_225 (not_225_out, OP4);
  not not_226 (not_226_out, OP5);
  not not_227 (not_227_out, RT0);
  not not_228 (not_228_out, OP3);
  not not_229 (not_229_out, OP4);
  not not_230 (not_230_out, OP5);
  not not_231 (not_231_out, OP3);
  not not_232 (not_232_out, OP4);
  not not_233 (not_233_out, OP5);
  not not_234 (not_234_out, OP1);
  not not_235 (not_235_out, OP2);
  not not_236 (not_236_out, OP3);
  not not_237 (not_237_out, OP4);
  not not_238 (not_238_out, OP5);
  and and_1 (and_1_out, not_1_out, not_2_out, not_3_out, not_4_out, not_5_out, not_6_out, not_7_out, not_8_out, F5);
  and and_2 (and_2_out, not_9_out, not_10_out, not_11_out, not_12_out, not_13_out, F2, not_14_out, not_15_out);
  and and_3 (and_3_out, not_16_out, not_17_out, not_18_out, not_19_out, not_20_out, F1, not_21_out, F3, not_22_out, F5);
  and and_4 (and_4_out, not_23_out, not_24_out, not_25_out, not_26_out, F0, F1, not_27_out, not_28_out, not_29_out, not_30_out);
  and and_5 (and_5_out, not_31_out, not_32_out, not_33_out, OP5);
  and and_6 (and_6_out, not_34_out, OP3, not_35_out, not_36_out);
  and and_7 (and_7_out, not_37_out, not_38_out, OP3, not_39_out);
  and and_8 (and_8_out, OP0, not_40_out, not_41_out, OP5);
  and and_9 (and_9_out, not_42_out, not_43_out, not_44_out, not_45_out, not_46_out, not_47_out, not_48_out, not_49_out, F2, not_50_out, not_51_out, F5);
  and and_10 (and_10_out, not_52_out, not_53_out, not_54_out, not_55_out, not_56_out, not_57_out, not_58_out, not_59_out, F2, F3, not_60_out, not_61_out);
  and and_11 (and_11_out, not_62_out, not_63_out, not_64_out, not_65_out, not_66_out, not_67_out, not_68_out, F1, not_69_out, not_70_out, not_71_out);
  and and_12 (and_12_out, not_72_out, not_73_out, not_74_out, not_75_out, not_76_out, not_77_out, not_78_out, F1, not_79_out, not_80_out, F5);
  and and_13 (and_13_out, not_81_out, not_82_out, not_83_out, not_84_out, not_85_out, not_86_out, F1, not_87_out, not_88_out, not_89_out, F5);
  and and_14 (and_14_out, not_90_out, not_91_out, not_92_out, not_93_out, not_94_out, not_95_out, F0, F1, F2, not_96_out, not_97_out);
  and and_15 (and_15_out, not_98_out, not_99_out, OP2, OP3, not_100_out, not_101_out);
  and and_16 (and_16_out, not_102_out, OP1, not_103_out, OP3, not_104_out, not_105_out);
  and and_17 (and_17_out, not_106_out, not_107_out, not_108_out, not_109_out, not_110_out, not_111_out, not_112_out, F5);
  and and_18 (and_18_out, not_113_out, not_114_out, not_115_out, not_116_out, not_117_out, not_118_out, F2, not_119_out, not_120_out);
  and and_19 (and_19_out, not_121_out, not_122_out, not_123_out, not_124_out, not_125_out, not_126_out, F2, not_127_out, not_128_out);
  and and_20 (and_20_out, not_129_out, not_130_out, not_131_out, not_132_out, F1, F2, not_133_out, not_134_out, not_135_out);
  and and_21 (and_21_out, not_136_out, not_137_out, not_138_out, not_139_out, F0, F1, not_140_out, not_141_out, F5);
  and and_22 (and_22_out, not_142_out, not_143_out, not_144_out, OP5);
  and and_23 (and_23_out, not_145_out, not_146_out, OP3, not_147_out, not_148_out);
  and and_24 (and_24_out, not_149_out, not_150_out, OP3, not_151_out);
  and and_25 (and_25_out, OP0, not_152_out, not_153_out, OP5);
  and and_26 (and_26_out, OP0, not_154_out, OP3, not_155_out);
  and and_27 (and_27_out, not_156_out, not_157_out, not_158_out, not_159_out, not_160_out, not_161_out, not_162_out, not_163_out, not_164_out, F3, not_165_out, not_166_out);
  and and_28 (and_28_out, not_167_out, not_168_out, not_169_out, not_170_out, not_171_out, not_172_out, not_173_out, F2, not_174_out, not_175_out, not_176_out);
  and and_29 (and_29_out, not_177_out, not_178_out, not_179_out, not_180_out, not_181_out, not_182_out, F1, not_183_out, F3, not_184_out, F5);
  and and_30 (and_30_out, not_185_out, not_186_out, not_187_out, not_188_out, not_189_out, not_190_out, F1, F2, not_191_out, not_192_out);
  and and_31 (and_31_out, not_193_out, not_194_out, not_195_out, not_196_out, not_197_out, not_198_out, F0, F2, not_199_out, not_200_out, F5);
  and and_32 (and_32_out, not_201_out, OP1, OP3, not_202_out, not_203_out);
  and and_33 (and_33_out, OP1, not_204_out, OP3, not_205_out, not_206_out);
  and and_34 (and_34_out, OP0, not_207_out, OP2, OP3, not_208_out, not_209_out);
  and and_35 (and_35_out, not_210_out, not_211_out, OP2, not_212_out, not_213_out, not_214_out);
  and and_36 (and_36_out, OP0, not_215_out, not_216_out, not_217_out, not_218_out, not_219_out, RT0);
  and and_37 (and_37_out, OP0, OP1, OP2, not_220_out, not_221_out, not_222_out);
  and and_38 (and_38_out, OP0, not_223_out, not_224_out, not_225_out, not_226_out, not_227_out);
  and and_39 (and_39_out, OP0, OP2, not_228_out, not_229_out, not_230_out);
  and and_40 (and_40_out, OP1, OP2, not_231_out, not_232_out, not_233_out);
  and and_41 (and_41_out, OP0, not_234_out, not_235_out, not_236_out, not_237_out, not_238_out);
  or or_1 (S0, and_1_out, and_2_out, and_3_out, and_4_out, and_5_out, and_6_out, and_7_out, and_8_out);
  or or_2 (S2, and_17_out, and_18_out, and_19_out, and_20_out, and_21_out, and_22_out, and_23_out, and_24_out, and_25_out, and_26_out);
  or or_3 (B0, and_35_out, and_36_out, and_37_out);
  or or_4 (B1, and_38_out, and_39_out);
  or or_5 (B2, and_40_out, and_41_out);
  or or_6 (S1, and_9_out, and_10_out, and_11_out, and_12_out, and_13_out, and_14_out, and_15_out, and_16_out);
  or or_7 (S3, and_27_out, and_28_out, and_29_out, and_30_out, and_31_out, and_32_out, and_33_out, and_34_out);
endmodule

// 控制信号生成
module \控制信号自动生成  (
  input  OP0,
  input  OP1,
  input  OP2,
  input  OP3,
  input  OP4,
  input  OP5,
  input  F0,
  input  F1,
  input  F2,
  input  F3,
  input  F4,
  input  F5,
  output MemToReg,
  output MemWrite,
  output MemHalf,
  output MemByte,
  output MemUnsigned,
  output ALU_SRC,
  output RegWrite,
  output SysCALL,
  output SignedExt,
  output RegDst,
  output JR,
  output JUMP,
  output JAL
);

  wire and_1_out, and_2_out, and_3_out, and_4_out, and_5_out, and_6_out, and_7_out, and_8_out, and_10_out,
       and_11_out, and_12_out, and_13_out, and_14_out, and_15_out, and_16_out, and_17_out, and_18_out,
       and_19_out, and_20_out, and_21_out, and_22_out, and_23_out, and_24_out, and_26_out, and_27_out,
       and_28_out, and_29_out, and_30_out, and_31_out, and_32_out, and_33_out, and_34_out, and_35_out,
       not_1_out, not_2_out, not_3_out, not_4_out, not_5_out, not_6_out, not_7_out, not_8_out, not_9_out,
       not_10_out, not_11_out, not_12_out, not_13_out, not_14_out, not_15_out, not_16_out, not_17_out,
       not_18_out, not_19_out, not_20_out, not_21_out, not_22_out, not_23_out, not_24_out, not_25_out,
       not_26_out, not_27_out, not_28_out, not_29_out, not_30_out, not_31_out, not_32_out, not_33_out,
       not_34_out, not_35_out, not_36_out, not_37_out, not_38_out, not_39_out, not_40_out, not_41_out,
       not_42_out, not_43_out, not_44_out, not_45_out, not_46_out, not_47_out, not_48_out, not_49_out,
       not_50_out, not_51_out, not_52_out, not_53_out, not_54_out, not_55_out, not_56_out, not_57_out,
       not_58_out, not_59_out, not_60_out, not_61_out, not_62_out, not_63_out, not_64_out, not_65_out,
       not_66_out, not_67_out, not_68_out, not_69_out, not_70_out, not_71_out, not_72_out, not_73_out,
       not_74_out, not_75_out, not_76_out, not_77_out, not_78_out, not_79_out, not_80_out, not_81_out,
       not_82_out, not_83_out, not_84_out, not_85_out, not_86_out, not_87_out, not_88_out, not_89_out,
       not_90_out, not_91_out, not_92_out, not_93_out, not_94_out, not_95_out, not_96_out, not_97_out,
       not_98_out, not_99_out, not_100_out, not_101_out, not_102_out, not_103_out, not_104_out, not_105_out,
       not_106_out, not_107_out, not_108_out, not_109_out, not_110_out, not_111_out, not_112_out,
       not_113_out, not_114_out, not_115_out, not_116_out, not_117_out, not_118_out, not_119_out,
       not_120_out, not_121_out, not_122_out, not_123_out, not_124_out, not_125_out, not_126_out,
       not_127_out, not_128_out, not_129_out, not_130_out, not_131_out, not_132_out, not_133_out,
       not_134_out, not_135_out, not_136_out, not_137_out, not_138_out, not_139_out, not_140_out,
       not_141_out, not_142_out, not_143_out, not_144_out, not_145_out, not_146_out, not_147_out,
       not_148_out, not_149_out, not_150_out, not_151_out, not_152_out, not_153_out, not_154_out,
       not_155_out, not_156_out, not_157_out, not_158_out, not_159_out, not_160_out, not_161_out,
       not_162_out, not_163_out, not_164_out, not_165_out, not_166_out, not_167_out, not_168_out, not_169_out;

  not not_1 (not_1_out, OP1);
  not not_2 (not_2_out, OP3);
  not not_3 (not_3_out, OP4);
  not not_4 (not_4_out, OP2);
  not not_5 (not_5_out, OP3);
  not not_6 (not_6_out, OP4);
  not not_7 (not_7_out, OP1);
  not not_8 (not_8_out, OP2);
  not not_9 (not_9_out, OP4);
  not not_10 (not_10_out, OP2);
  not not_11 (not_11_out, OP4);
  not not_12 (not_12_out, OP1);
  not not_13 (not_13_out, OP2);
  not not_14 (not_14_out, OP4);
  not not_15 (not_15_out, OP1);
  not not_16 (not_16_out, OP3);
  not not_17 (not_17_out, OP4);
  not not_18 (not_18_out, OP0);
  not not_19 (not_19_out, OP1);
  not not_20 (not_20_out, OP2);
  not not_21 (not_21_out, OP4);
  not not_22 (not_22_out, OP0);
  not not_23 (not_23_out, OP1);
  not not_24 (not_24_out, OP3);
  not not_25 (not_25_out, OP4);
  not not_26 (not_26_out, OP1);
  not not_27 (not_27_out, OP3);
  not not_28 (not_28_out, OP4);
  not not_29 (not_29_out, OP1);
  not not_30 (not_30_out, OP3);
  not not_31 (not_31_out, OP4);
  not not_32 (not_32_out, OP0);
  not not_33 (not_33_out, OP4);
  not not_34 (not_34_out, OP5);
  not not_35 (not_35_out, OP1);
  not not_36 (not_36_out, OP2);
  not not_37 (not_37_out, OP4);
  not not_38 (not_38_out, OP1);
  not not_39 (not_39_out, OP4);
  not not_40 (not_40_out, OP5);
  not not_41 (not_41_out, OP2);
  not not_42 (not_42_out, OP4);
  not not_43 (not_43_out, OP5);
  not not_44 (not_44_out, OP2);
  not not_45 (not_45_out, OP4);
  not not_46 (not_46_out, OP0);
  not not_47 (not_47_out, OP1);
  not not_48 (not_48_out, OP2);
  not not_49 (not_49_out, OP3);
  not not_50 (not_50_out, OP4);
  not not_51 (not_51_out, F0);
  not not_52 (not_52_out, F3);
  not not_53 (not_53_out, F4);
  not not_54 (not_54_out, OP0);
  not not_55 (not_55_out, OP1);
  not not_56 (not_56_out, OP2);
  not not_57 (not_57_out, OP3);
  not not_58 (not_58_out, OP4);
  not not_59 (not_59_out, F3);
  not not_60 (not_60_out, F4);
  not not_61 (not_61_out, OP0);
  not not_62 (not_62_out, OP1);
  not not_63 (not_63_out, OP2);
  not not_64 (not_64_out, OP3);
  not not_65 (not_65_out, OP4);
  not not_66 (not_66_out, F3);
  not not_67 (not_67_out, F4);
  not not_68 (not_68_out, OP0);
  not not_69 (not_69_out, OP1);
  not not_70 (not_70_out, OP2);
  not not_71 (not_71_out, OP3);
  not not_72 (not_72_out, OP4);
  not not_73 (not_73_out, F2);
  not not_74 (not_74_out, F4);
  not not_75 (not_75_out, OP1);
  not not_76 (not_76_out, OP3);
  not not_77 (not_77_out, OP4);
  not not_78 (not_78_out, OP0);
  not not_79 (not_79_out, OP4);
  not not_80 (not_80_out, OP5);
  not not_81 (not_81_out, OP1);
  not not_82 (not_82_out, OP4);
  not not_83 (not_83_out, OP5);
  not not_84 (not_84_out, OP2);
  not not_85 (not_85_out, OP3);
  not not_86 (not_86_out, OP4);
  not not_87 (not_87_out, OP2);
  not not_88 (not_88_out, OP4);
  not not_89 (not_89_out, OP5);
  not not_90 (not_90_out, OP0);
  not not_91 (not_91_out, OP1);
  not not_92 (not_92_out, OP2);
  not not_93 (not_93_out, OP3);
  not not_94 (not_94_out, OP4);
  not not_95 (not_95_out, OP5);
  not not_96 (not_96_out, F0);
  not not_97 (not_97_out, F1);
  not not_98 (not_98_out, F4);
  not not_99 (not_99_out, F5);
  not not_100 (not_100_out, OP1);
  not not_101 (not_101_out, OP3);
  not not_102 (not_102_out, OP4);
  not not_103 (not_103_out, OP1);
  not not_104 (not_104_out, OP2);
  not not_105 (not_105_out, OP4);
  not not_106 (not_106_out, OP2);
  not not_107 (not_107_out, OP4);
  not not_108 (not_108_out, OP5);
  not not_109 (not_109_out, OP3);
  not not_110 (not_110_out, OP4);
  not not_111 (not_111_out, OP5);
  not not_112 (not_112_out, OP1);
  not not_113 (not_113_out, OP2);
  not not_114 (not_114_out, OP4);
  not not_115 (not_115_out, OP2);
  not not_116 (not_116_out, OP4);
  not not_117 (not_117_out, OP0);
  not not_118 (not_118_out, OP1);
  not not_119 (not_119_out, OP2);
  not not_120 (not_120_out, OP3);
  not not_121 (not_121_out, OP4);
  not not_122 (not_122_out, OP5);
  not not_123 (not_123_out, F0);
  not not_124 (not_124_out, F3);
  not not_125 (not_125_out, F4);
  not not_126 (not_126_out, OP0);
  not not_127 (not_127_out, OP1);
  not not_128 (not_128_out, OP2);
  not not_129 (not_129_out, OP3);
  not not_130 (not_130_out, OP4);
  not not_131 (not_131_out, OP5);
  not not_132 (not_132_out, F3);
  not not_133 (not_133_out, F4);
  not not_134 (not_134_out, OP0);
  not not_135 (not_135_out, OP1);
  not not_136 (not_136_out, OP2);
  not not_137 (not_137_out, OP3);
  not not_138 (not_138_out, OP4);
  not not_139 (not_139_out, OP5);
  not not_140 (not_140_out, F3);
  not not_141 (not_141_out, F4);
  not not_142 (not_142_out, OP0);
  not not_143 (not_143_out, OP1);
  not not_144 (not_144_out, OP2);
  not not_145 (not_145_out, OP3);
  not not_146 (not_146_out, OP4);
  not not_147 (not_147_out, OP5);
  not not_148 (not_148_out, F2);
  not not_149 (not_149_out, F4);
  not not_150 (not_150_out, OP0);
  not not_151 (not_151_out, OP1);
  not not_152 (not_152_out, OP2);
  not not_153 (not_153_out, OP3);
  not not_154 (not_154_out, OP4);
  not not_155 (not_155_out, OP5);
  not not_156 (not_156_out, F0);
  not not_157 (not_157_out, F1);
  not not_158 (not_158_out, F2);
  not not_159 (not_159_out, F4);
  not not_160 (not_160_out, F5);
  not not_161 (not_161_out, OP0);
  not not_162 (not_162_out, OP2);
  not not_163 (not_163_out, OP3);
  not not_164 (not_164_out, OP4);
  not not_165 (not_165_out, OP5);
  not not_166 (not_166_out, OP2);
  not not_167 (not_167_out, OP3);
  not not_168 (not_168_out, OP4);
  not not_169 (not_169_out, OP5);
  and and_1 (and_1_out, not_1_out, not_2_out, not_3_out, OP5);
  or or_1 (MemToReg, and_1_out, and_2_out);
  and and_2 (and_2_out, OP0, not_4_out, not_5_out, not_6_out, OP5);
  and and_3 (and_3_out, not_7_out, not_8_out, OP3, not_9_out, OP5);
  or or_2 (MemWrite, and_3_out, and_4_out);
  and and_4 (and_4_out, OP0, not_10_out, OP3, not_11_out, OP5);
  and and_5 (and_5_out, OP0, not_12_out, not_13_out, not_14_out, OP5);
  or or_3 (MemHalf, and_5_out, and_6_out);
  and and_6 (and_6_out, OP0, not_15_out, not_16_out, not_17_out, OP5);
  and and_7 (and_7_out, not_18_out, not_19_out, not_20_out, not_21_out, OP5);
  or or_4 (MemByte, and_7_out, and_8_out);
  and and_8 (and_8_out, not_22_out, not_23_out, not_24_out, not_25_out, OP5);
  and and_9 (MemUnsigned, not_26_out, OP2, not_27_out, not_28_out, OP5);
  and and_10 (and_10_out, not_29_out, not_30_out, not_31_out, OP5);
  and and_11 (and_11_out, not_32_out, OP3, not_33_out, not_34_out);
  and and_12 (and_12_out, not_35_out, not_36_out, OP3, not_37_out);
  and and_13 (and_13_out, not_38_out, OP3, not_39_out, not_40_out);
  and and_14 (and_14_out, not_41_out, OP3, not_42_out, not_43_out);
  and and_15 (and_15_out, OP0, not_44_out, not_45_out, OP5);
  and and_16 (and_16_out, not_46_out, not_47_out, not_48_out, not_49_out, not_50_out, not_51_out, not_52_out, not_53_out);
  and and_17 (and_17_out, not_54_out, not_55_out, not_56_out, not_57_out, not_58_out, not_59_out, not_60_out, F5);
  and and_18 (and_18_out, not_61_out, not_62_out, not_63_out, not_64_out, not_65_out, F1, not_66_out, not_67_out);
  and and_19 (and_19_out, not_68_out, not_69_out, not_70_out, not_71_out, not_72_out, F1, not_73_out, not_74_out, F5);
  and and_20 (and_20_out, not_75_out, not_76_out, not_77_out, OP5);
  and and_21 (and_21_out, not_78_out, OP3, not_79_out, not_80_out);
  and and_22 (and_22_out, not_81_out, OP3, not_82_out, not_83_out);
  and and_23 (and_23_out, OP0, not_84_out, not_85_out, not_86_out, OP5);
  and and_24 (and_24_out, OP0, OP1, not_87_out, not_88_out, not_89_out);
  and and_25 (SysCALL, not_90_out, not_91_out, not_92_out, not_93_out, not_94_out, not_95_out, not_96_out, not_97_out, F2, F3, not_98_out, not_99_out);
  and and_26 (and_26_out, not_100_out, not_101_out, not_102_out, OP5);
  and and_27 (and_27_out, not_103_out, not_104_out, OP3, not_105_out);
  and and_28 (and_28_out, not_106_out, OP3, not_107_out, not_108_out);
  and and_29 (and_29_out, OP2, not_109_out, not_110_out, not_111_out);
  and and_30 (and_30_out, OP0, not_112_out, not_113_out, not_114_out);
  and and_31 (and_31_out, OP0, not_115_out, not_116_out, OP5);
  and and_32 (and_32_out, not_117_out, not_118_out, not_119_out, not_120_out, not_121_out, not_122_out, not_123_out, not_124_out, not_125_out);
  and and_33 (and_33_out, not_126_out, not_127_out, not_128_out, not_129_out, not_130_out, not_131_out, not_132_out, not_133_out, F5);
  and and_34 (and_34_out, not_134_out, not_135_out, not_136_out, not_137_out, not_138_out, not_139_out, F1, not_140_out, not_141_out);
  and and_35 (and_35_out, not_142_out, not_143_out, not_144_out, not_145_out, not_146_out, not_147_out, F1, not_148_out, not_149_out, F5);
  and and_36 (JR, not_150_out, not_151_out, not_152_out, not_153_out, not_154_out, not_155_out, not_156_out, not_157_out, not_158_out, F3, not_159_out, not_160_out);
  and and_37 (JUMP, not_161_out, OP1, not_162_out, not_163_out, not_164_out, not_165_out);
  and and_38 (JAL, OP0, OP1, not_166_out, not_167_out, not_168_out, not_169_out);
  or or_5 (ALU_SRC, and_10_out, and_11_out, and_12_out, and_13_out, and_14_out, and_15_out);
  or or_6 (RegWrite, and_16_out, and_17_out, and_18_out, and_19_out, and_20_out, and_21_out, and_22_out, and_23_out, and_24_out);
  or or_7 (SignedExt, and_26_out, and_27_out, and_28_out, and_29_out, and_30_out, and_31_out);
  or or_8 (RegDst, and_32_out, and_33_out, and_34_out, and_35_out);
endmodule

// ALU
module MIPS_ALU (
  input  [4:0] shamt,
  input  [31:0] X,
  input  [31:0] Y,
  input  [6:0] AluOP,
  output Branch,
  output [31:0] Result,
  output [31:0] Result_2
);

  wire and_2_out, comparator_1_eq, not_1_out, not_2_out, or_2_out;
  wire [0:0] comparator_1_lt, comparator_2_lt;
  wire [31:0] adder_1_out, AND_out, divider_1_out, divider_1_rem, multiplier_1_cout, multiplier_1_out,
       NOR_out, OR_out, shifter_1_out, shifter_2_out, shifter_3_out, shifter_4_out, shifter_5_out,
       shifter_6_out, subtractor_1_out, XOR_out;

  assign AND_out = X & Y;  // AND_Gate AND, 32 bits wide
  assign OR_out = X | Y;  // OR_Gate OR, 32 bits wide
  Shifter #(.width(32), .shift("ll")) shifter_1 (.in(Y), .\dist (shamt), .out(shifter_1_out));
  Shifter #(.width(32), .shift("ar")) shifter_2 (.in(Y), .\dist (shamt), .out(shifter_2_out));
  Shifter #(.width(32), .shift("lr")) shifter_3 (.in(Y), .\dist (shamt), .out(shifter_3_out));
  Multiplier #(.width(32)) multiplier_1 (.a(X), .b(Y), .out(multiplier_1_out), .cout(multiplier_1_cout));  // open: cin
  Divider #(.width(32)) divider_1 (.a(X), .b(Y), .out(divider_1_out), .rem(divider_1_rem));  // open: upper
  Adder #(.width(32)) adder_1 (.a(X), .b(Y), .out(adder_1_out));  // open: cin, cout
  Subtractor #(.width(32)) subtractor_1 (.a(X), .b(Y), .out(subtractor_1_out));  // open: bin, bout
  assign XOR_out = X ^ Y;  // XOR_Gate XOR, 32 bits wide
  assign NOR_out = ~(X | Y);  // NOR_Gate NOR, 32 bits wide
  Comparator #(.width(32), .mode("twosComplement")) comparator_1 (
    .a(X), .b(Y), .eq(comparator_1_eq), .lt(comparator_1_lt[0]));  // open: gt
  Comparator #(.width(32), .mode("unsigned")) comparator_2 (.a(X), .b(Y), .lt(comparator_2_lt[0]));  // open: gt, eq
  Shifter #(.width(32), .shift("ll")) shifter_4 (.in(Y), .\dist (X[4:0]), .out(shifter_4_out));
  Shifter #(.width(32), .shift("ar")) shifter_5 (.in(Y), .\dist (X[4:0]), .out(shifter_5_out));
  Shifter #(.width(32), .shift("lr")) shifter_6 (.in(Y), .\dist (X[4:0]), .out(shifter_6_out));
  Multiplexer #(.select(4), .width(32), .disabled("Z"), .enable("false")) multiplexer_1 (
    .in0(shifter_1_out), .in1(shifter_2_out), .in2(shifter_3_out), .in3(multiplier_1_out),
    .in4(divider_1_out), .in5(adder_1_out), .in6(subtractor_1_out), .in7(AND_out), .in8(OR_out),
    .in9(XOR_out), .in10(NOR_out), .in11({{31{1'b0}}, comparator_1_lt[0]}),
    .in12({{31{1'b0}}, comparator_2_lt[0]}), .in13(shifter_4_out), .in14(shifter_5_out),
    .in15(shifter_6_out), .out(Result), .sel(AluOP[3:0]));
  Multiplexer #(.select(4), .width(32), .disabled("Z"), .enable("false")) multiplexer_2 (
    .in0({32{1'b0}}), .in1({32{1'b0}}), .in2({32{1'b0}}), .in3(multiplier_1_cout), .in4(divider_1_rem),
    .in5({32{1'b0}}), .in6({32{1'b0}}), .in7({32{1'b0}}), .in8({32{1'b0}}), .in9({32{1'b0}}),
    .in10({32{1'b0}}), .in11({32{1'b0}}), .in12({32{1'b0}}), .in13({32{1'b0}}), .in14({32{1'b0}}),
    .in15({32{1'b0}}), .out(Result_2), .sel(AluOP[3:0]));
  or or_2 (or_2_out, comparator_1_eq, X[31]);
  not not_1 (not_1_out, X[31]);
  and and_2 (and_2_out, ~X[31], ~comparator_1_eq);  // AND_Gate
  not not_2 (not_2_out, comparator_1_eq);
  Multiplexer #(.select(3), .width(1), .disabled("Z"), .enable("false")) multiplexer_3 (
    .in0(1'b0), .in1(comparator_1_eq), .in2(not_2_out), .in3(1'b0), .in4(or_2_out), .in5(not_1_out),
    .in6(X[31]), .in7(and_2_out), .out(Branch), .sel(AluOP[6:4]));

  // Other names for the same wires on the sheet: ALUOP_t[3:0] = AluOP[3:0]; BRANCHOP[2:0] = AluOP[6:4];
  //   Result2[31:0] = Result_2

  // Notes on the sheet:
  //   不要改变此引脚区域内容，也不要改变ALU封装形式
  //   输入引脚
  //   输出引脚
endmodule

module MIPS_Regifile (
  input  [31:0] Din,
  input  Clk,
  input  WE,
  input  [4:0] R1_num,
  input  [4:0] W_num,
  input  [4:0] R2_num,
  output [31:0] R1,
  output [31:0] R2
);

  // RegisterFile registerfile_1: pin names not known; wires that end beside it: Din, Clk, WE, W_num, R1_num, R2_num, R1, R2
endmodule

module \MIPS_Regifile_下降沿  (
  input  [31:0] Din,
  input  Clk,
  input  WE,
  input  [4:0] R1_num,
  input  [4:0] W_num,
  input  [4:0] R2_num,
  output [31:0] R1,
  output [31:0] R2
);

  // RegisterFile registerfile_1: pin names not known; wires that end beside it: Din, Clk, WE, W_num, R1_num, R2_num, R1, R2
endmodule

module MIPS_Ram_Adapter (
  input  [31:0] DataIn,
  input  [31:0] dout,
  input  [3:0] CONTROL,
  input  [31:0] Addr,
  input  CLK,
  output [31:0] DataOut,
  output [31:0] din,
  output str,
  output [9:0] A,
  output clk_2
);

  wire [7:0] multiplexer_1_out;
  wire [15:0] multiplexer_2_out;
  wire [31:0] bit_extender_1_out, bit_extender_2_out, bit_extender_3_out, bit_extender_4_out,
       multiplexer_4_out, multiplexer_5_out;

  Multiplexer #(.select(2), .width(8), .disabled("Z"), .enable("false")) multiplexer_1 (
    .in0(dout[7:0]), .in1(dout[15:8]), .in2(dout[23:16]), .in3(dout[31:24]), .out(multiplexer_1_out),
    .sel(Addr[1:0]));
  Multiplexer #(.select(1), .width(16), .disabled("Z"), .enable("false")) multiplexer_2 (
    .in0(dout[15:0]), .in1(dout[31:16]), .out(multiplexer_2_out), .sel(Addr[1]));
  assign bit_extender_1_out = {{24{multiplexer_1_out[7]}}, multiplexer_1_out};  // Bit_Extender bit_extender_1
  assign bit_extender_2_out = {{24{1'b0}}, multiplexer_1_out};  // Bit_Extender bit_extender_2
  assign bit_extender_3_out = {{16{multiplexer_2_out[15]}}, multiplexer_2_out};  // Bit_Extender bit_extender_3
  assign bit_extender_4_out = {{16{1'b0}}, multiplexer_2_out};  // Bit_Extender bit_extender_4
  Multiplexer #(.select(3), .width(32), .disabled("Z"), .enable("false")) multiplexer_3 (
    .in0(dout), .in1(dout), .in2(bit_extender_1_out), .in3(bit_extender_2_out), .in4(bit_extender_3_out),
    .in5(bit_extender_4_out), .in6({32{1'b0}}), .in7({32{1'b0}}), .out(DataOut), .sel(CONTROL[2:0]));
  Multiplexer #(.select(2), .width(32), .disabled("Z"), .enable("false")) multiplexer_4 (
    .in0({dout[31:8], DataIn[7:0]}), .in1({dout[31:16], DataIn[7:0], dout[7:0]}),
    .in2({dout[31:24], DataIn[7:0], dout[15:0]}), .in3({DataIn[7:0], dout[23:0]}), .out(multiplexer_4_out),
    .sel(Addr[1:0]));
  Multiplexer #(.select(1), .width(32), .disabled("Z"), .enable("false")) multiplexer_5 (
    .in0({dout[31:16], DataIn[15:0]}), .in1({DataIn[15:0], dout[15:0]}), .out(multiplexer_5_out),
    .sel(Addr[1]));
  Multiplexer #(.select(2), .width(32), .disabled("Z"), .enable("false")) multiplexer_6 (
    .in0(DataIn), .in1(multiplexer_4_out), .in2(multiplexer_5_out), .in3({32{1'b0}}), .out(din),
    .sel(CONTROL[2:1]));

  assign A = Addr[11:2];
  assign clk_2 = CLK;
  assign str = CONTROL[3];
endmodule

module \理想流水线  (
);

  wire and_1_out, CLK, comparator_1_eq, ex_mem_1_jalout, ex_mem_1_memtoregout, ex_mem_1_regwriteout, Go,
       HaltIn, HaltOut, id_ex_1_alusrcbout, id_ex_1_jalout, id_ex_1_memtoregout, id_ex_1_regwriteout,
       \id_ex_1_使能传递端_低电平有效_stall_高电平有效 , \if_id_1_使能传递端_低电平有效_stall_高电平有效 , IR1, IR2, IR3,
       mem_wb_1_memtoregout, mips_ram_adapter_1_clk_2, mips_ram_adapter_1_str, not_1_out, not_2_out,
       RegWrite, RST, SignedExt, Syscall, W1, W2, W3, \单周期硬布线控制器_1_alu_src , \单周期硬布线控制器_1_jal ,
       \单周期硬布线控制器_1_jmp , \单周期硬布线控制器_1_jr , \单周期硬布线控制器_1_memtoreg , \单周期硬布线控制器_1_regdst ,
       \单周期硬布线控制器_1_regwrite ;
  wire [3:0] ex_mem_1_memcontrolout, id_ex_1_memcontrolout, \单周期硬布线控制器_1_memcontrol ;
  wire [4:0] ex_mem_1_w_out, id_ex_1_shamtout, id_ex_1_w_out, multiplexer_2_out, multiplexer_3_out,
       multiplexer_4_out, multiplexer_6_out, W_num;
  wire [6:0] id_ex_1_aluopout, \单周期硬布线控制器_1_alu_op ;
  wire [9:0] mips_ram_adapter_1_a;
  wire [15:0] \LoadUse次数 , \总周期数 , \插入气泡数 , \无条件分支数 , \条件分支成功数 ;
  wire [25:0] if_id_1_irout;
  wire [31:0] a0, adder_1_out, bit_extender_1_out, bit_extender_2_out, Din, ex_mem_1_aluout, ex_mem_1_bout,
       ex_mem_1_irout, ex_mem_1_pc_4out, ex_mem_1_pcout, EX_PC, id_ex_1_aout, id_ex_1_bout, id_ex_1_immout,
       id_ex_1_irout, id_ex_1_pc_4out, ID_PC, if_id_1_pc_4out, IF_PC, LedData, MEM_PC, mem_wb_1_aluout,
       mem_wb_1_memout, mips_alu_1_result, mips_ram_adapter_1_dataout, mips_ram_adapter_1_din,
       multiplexer_1_out, multiplexer_5_out, multiplexer_7_out, multiplexer_8_out, ram_1_data, rom_1_data,
       undriven, undriven_2, undriven_3, v0, WB_PC;
  wire [31:26] if_id_1_irout_2;

  Button \u_总复位  (.out(RST));
  Button _1 (.out(IR1));
  Button _2 (.out(IR2));
  Button _3 (.out(IR3));
  Button \u_继续运行  (.out(Go));
  LED #(.active("true")) led_1 (.in(W1));
  LED #(.active("true")) led_2 (.in(W2));
  LED #(.active("true")) led_3 (.in(W3));
  Multiplexer #(.select(2), .width(32), .disabled("Z"), .enable("false")) multiplexer_1 (
    .in0(adder_1_out), .in1(undriven_3), .in2(undriven_2), .in3(undriven), .out(multiplexer_1_out),
    .sel(2'b00));
  Register #(.width(32), .trigger("rising"), .Select("low")) PC (
    .D(multiplexer_1_out), .en(not_1_out), .Q(IF_PC), .clk(CLK));  // open: clr
  not not_1 (not_1_out, HaltIn);
  not not_2 (not_2_out, HaltOut);
  Hex_Digit_Display hex_digit_display_1 (.value(LedData[31:28]));  // open: dp
  Counter #(.width(16), .max('hffff), .ongoal("stay"), .trigger("rising"), .behavior("old")) \u_总周期数  (
    .count(not_2_out), .Q(\总周期数 ), .clk(CLK));  // open: load, D, carry, clr, preset
  Hex_Digit_Display hex_digit_display_2 (.value(LedData[27:24]));  // open: dp
  Hex_Digit_Display hex_digit_display_3 (.value(LedData[23:20]));  // open: dp
  Adder #(.width(32)) adder_1 (.a(IF_PC), .b(32'h4), .out(adder_1_out));  // open: cin, cout
  Hex_Digit_Display hex_digit_display_4 (.value(LedData[19:16]));  // open: dp
  Hex_Digit_Display hex_digit_display_5 (.value(LedData[15:12]));  // open: dp
  IF_ID if_id_1 (
    .PCin(IF_PC), .IRin(rom_1_data), .CLK(CLK), .PCout(ID_PC), .IRout({if_id_1_irout_2, if_id_1_irout}),
    .\使能端_低电平有效_stall_高电平有效 (HaltIn), .PC_4in(adder_1_out), .PC_4out(if_id_1_pc_4out),
    .\使能传递端_低电平有效_stall_高电平有效 (\if_id_1_使能传递端_低电平有效_stall_高电平有效 ));  // open: 同步清零_气泡_高电平有效
  ROM #(.addrWidth(10), .dataWidth(32), .Select("high")) rom_1 (.addr(IF_PC[11:2]), .data(rom_1_data));
  Hex_Digit_Display hex_digit_display_6 (.value(LedData[7:4]));  // open: dp
  Hex_Digit_Display hex_digit_display_7 (.value(LedData[11:8]));  // open: dp
  Clock #(.highDuration(1), .lowDuration(1)) clock_1 (.out(CLK));
  Hex_Digit_Display hex_digit_display_8 (.value(LedData[3:0]));  // open: dp
  Comparator #(.width(32), .mode("unsigned")) comparator_1 (.a(v0), .b(32'ha), .eq(comparator_1_eq));  // open: gt, lt
  and and_1 (and_1_out, ~comparator_1_eq, Syscall);  // AND_Gate
  \单周期硬布线控制器  \u_单周期硬布线控制器_1  (
    .IR({if_id_1_irout_2, if_id_1_irout}), .ALU_OP(\单周期硬布线控制器_1_alu_op ), .MemToReg(\单周期硬布线控制器_1_memtoreg ),
    .MemControl(\单周期硬布线控制器_1_memcontrol ), .ALU_SRC(\单周期硬布线控制器_1_alu_src ),
    .RegWrite(\单周期硬布线控制器_1_regwrite ), .SysCALL(Syscall), .SignedExt(SignedExt),
    .RegDst(\单周期硬布线控制器_1_regdst ), .JR(\单周期硬布线控制器_1_jr ), .JMP(\单周期硬布线控制器_1_jmp ), .JAL(\单周期硬布线控制器_1_jal ));  // open: R1_Used, R2_Used
  Multiplexer #(.select(1), .width(5), .disabled("Z"), .enable("false")) multiplexer_2 (
    .in0(if_id_1_irout[25:21]), .in1(5'b00010), .out(multiplexer_2_out), .sel(Syscall));
  Multiplexer #(.select(1), .width(5), .disabled("Z"), .enable("false")) multiplexer_3 (
    .in0(if_id_1_irout[20:16]), .in1(5'b00100), .out(multiplexer_3_out), .sel(Syscall));
  assign bit_extender_1_out = {{16{1'b0}}, if_id_1_irout[15:0]};  // Bit_Extender bit_extender_1
  assign bit_extender_2_out = {{16{if_id_1_irout[15]}}, if_id_1_irout[15:0]};  // Bit_Extender bit_extender_2
  Register #(.width(32), .trigger("rising"), .Select("low")) register_1 (
    .D(a0), .en(and_1_out), .Q(LedData), .clk(CLK));  // open: clr
  // Probe on \总周期数 
  // Probe on \无条件分支数 
  // Probe on \条件分支成功数 
  // Probe on \插入气泡数 
  // Probe on \LoadUse次数 
  Multiplexer #(.select(1), .width(5), .disabled("Z"), .enable("false")) multiplexer_4 (
    .in0(if_id_1_irout[20:16]), .in1(if_id_1_irout[15:11]), .out(multiplexer_4_out),
    .sel(\单周期硬布线控制器_1_regdst ));
  Multiplexer #(.select(1), .width(32), .disabled("Z"), .enable("false")) multiplexer_5 (
    .in0(bit_extender_1_out), .in1(bit_extender_2_out), .out(multiplexer_5_out), .sel(SignedExt));
  and and_2 (HaltIn, comparator_1_eq, Syscall);
  // Probe on IF_PC[11:0]
  ID_EX id_ex_1 (
    .PCin(ID_PC), .IRin({if_id_1_irout_2, if_id_1_irout}), .Ain(v0), .Bin(a0), .IMMin(multiplexer_5_out),
    .MEMTOREGin(\单周期硬布线控制器_1_memtoreg ), .MEMCONTROLin(\单周期硬布线控制器_1_memcontrol ),
    .ALUOPin(\单周期硬布线控制器_1_alu_op ), .ALUSRCBin(\单周期硬布线控制器_1_alu_src ), .CLK(CLK), .PCout(EX_PC),
    .IRout(id_ex_1_irout), .Aout(id_ex_1_aout), .Bout(id_ex_1_bout), .IMMout(id_ex_1_immout),
    .MEMTOREGout(id_ex_1_memtoregout), .MEMCONTROLout(id_ex_1_memcontrolout), .ALUOPout(id_ex_1_aluopout),
    .ALUSRCBout(id_ex_1_alusrcbout), .\使能端_低电平有效_stall_高电平有效 (\if_id_1_使能传递端_低电平有效_stall_高电平有效 ),
    .SHAMTin(if_id_1_irout[10:6]), .SHAMTout(id_ex_1_shamtout), .REGWRITEin(\单周期硬布线控制器_1_regwrite ),
    .REGWRITEout(id_ex_1_regwriteout), .W_in(multiplexer_6_out), .W_out(id_ex_1_w_out),
    .JALin(\单周期硬布线控制器_1_jal ), .JALout(id_ex_1_jalout),
    .\使能传递端_低电平有效_stall_高电平有效 (\id_ex_1_使能传递端_低电平有效_stall_高电平有效 ), .PC_4in(if_id_1_pc_4out),
    .PC_4out(id_ex_1_pc_4out));  // open: 同步清零_气泡_高电平有效, R1_SELin, R1_SELout, R2_SELin, R2_SELout
  Multiplexer #(.select(1), .width(5), .disabled("Z"), .enable("false")) multiplexer_6 (
    .in0(multiplexer_4_out), .in1({5{1'b1}}), .out(multiplexer_6_out), .sel(\单周期硬布线控制器_1_jal ));
  \MIPS_Regifile_下降沿  \mips_regifile_下降沿_1  (
    .Din(Din), .Clk(CLK), .R1(v0), .R2(a0), .WE(RegWrite), .W_num(W_num), .R1_num(multiplexer_2_out),
    .R2_num(multiplexer_3_out));
  // Probe on EX_PC[11:0]
  // Probe on ID_PC[11:0]
  // Probe on MEM_PC[11:0]
  Multiplexer #(.select(1), .width(32), .disabled("Z"), .enable("false")) multiplexer_7 (
    .in0(id_ex_1_bout), .in1(id_ex_1_immout), .out(multiplexer_7_out), .sel(id_ex_1_alusrcbout));
  // Probe on WB_PC[11:0]
  EX_MEM ex_mem_1 (
    .PCin(EX_PC), .IRin(id_ex_1_irout), .Bin(id_ex_1_bout), .MEMTOREGin(id_ex_1_memtoregout),
    .MEMCONTROLin(id_ex_1_memcontrolout), .CLK(CLK), .PCout(ex_mem_1_pcout), .IRout(ex_mem_1_irout),
    .Bout(ex_mem_1_bout), .MEMTOREGout(ex_mem_1_memtoregout), .MEMCONTROLout(ex_mem_1_memcontrolout),
    .\使能端_低电平有效_stall_高电平有效 (\id_ex_1_使能传递端_低电平有效_stall_高电平有效 ), .ALUin(mips_alu_1_result),
    .ALUout(ex_mem_1_aluout), .REGWRITEin(id_ex_1_regwriteout), .REGWRITEout(ex_mem_1_regwriteout),
    .W_in(id_ex_1_w_out), .W_out(ex_mem_1_w_out), .JALin(id_ex_1_jalout), .JALout(ex_mem_1_jalout),
    .\使能传递端_低电平有效_stall_高电平有效 (HaltOut), .PC_4in(id_ex_1_pc_4out), .PC_4out(ex_mem_1_pc_4out));  // open: 同步清零_气泡_高电平有效
  MIPS_ALU mips_alu_1 (
    .X(id_ex_1_aout), .Y(multiplexer_7_out), .AluOP(id_ex_1_aluopout), .Result(mips_alu_1_result),
    .shamt(id_ex_1_shamtout));  // open: Branch, Result_2
  Multiplexer #(.select(1), .width(32), .disabled("Z"), .enable("false")) multiplexer_8 (
    .in0(ex_mem_1_aluout), .in1(ex_mem_1_pc_4out), .out(multiplexer_8_out), .sel(ex_mem_1_jalout));
  MIPS_Ram_Adapter mips_ram_adapter_1 (
    .Addr(ex_mem_1_aluout), .DataIn(ex_mem_1_bout), .dout(ram_1_data), .CLK(CLK),
    .CONTROL(ex_mem_1_memcontrolout), .A(mips_ram_adapter_1_a), .din(mips_ram_adapter_1_din),
    .DataOut(mips_ram_adapter_1_dataout), .clk_2(mips_ram_adapter_1_clk_2), .str(mips_ram_adapter_1_str));
  RAM #(.addrWidth(10), .dataWidth(32), .bus("separate"), .Select("high")) ram_1 (
    .addr(mips_ram_adapter_1_a), .din(mips_ram_adapter_1_din), .data(ram_1_data),
    .str(mips_ram_adapter_1_str), .clk(mips_ram_adapter_1_clk_2));  // open: sel, ld, clr
  MEM_WB mem_wb_1 (
    .PCin(MEM_PC), .IRin(ex_mem_1_irout), .ALUin(multiplexer_8_out), .MEMin(mips_ram_adapter_1_dataout),
    .MEMTOREGin(ex_mem_1_memtoregout), .CLK(CLK), .PCout(WB_PC), .ALUout(mem_wb_1_aluout),
    .MEMout(mem_wb_1_memout), .MEMTOREGout(mem_wb_1_memtoregout), .\使能端_低电平有效_stall_高电平有效 (HaltOut),
    .REGWRITEin(ex_mem_1_regwriteout), .REGWRITEout(RegWrite), .W_in(ex_mem_1_w_out), .W_out(W_num));  // open: IRout, 同步清零_气泡_高电平有效, 使能传递端_低电平有效_stall_高电平有效
  Multiplexer #(.select(1), .width(32), .disabled("Z"), .enable("false")) multiplexer_9 (
    .in0(mem_wb_1_aluout), .in1(mem_wb_1_memout), .out(Din), .sel(mem_wb_1_memtoregout));

  // Notes on the sheet:
  //   中断源
  //   PC+4
  //   JR
  //   J/JAL
  //   中断等待指示
  //   BEQ/BNE
  //   PC计数器
  //   指令存储器
  //   数码管输出
  //   contents of rom_1 (hex, n*v repeats v):
  //   20100000 20110001 20120002 20130003 36100000 36310001 36520002 36730003 ae100000 ae110004 ae120008
  //   ae13000c 2002000a 0 0 0 c
  //   PC+4
  //   JMP
  //   JR
  //   IR
  //   rs
  //   指令字
  //   rt
  //   imm
  //   addr
  //   shamt
  //   Syscall功能实现
  //   MemToReg
  //   MemControl
  //   AluOP
  //   AluSrcB
  //   RegWrite
  //   JAL
  //   RegDst
  //   Syscall
  //   rt
  //   rd
  //   流水调试日志用
endmodule

module \气泡流水线  (
  output RegWrite,
  output MemWrite,
  output [31:0] PC,
  output [31:0] IR,
  output [31:0] RDin,
  output [31:0] MDin
);

  wire and_1_out, branch, CLK, Col, comparator_1_eq, EX_Col_R1, EX_Col_R2, ex_mem_1_jalout,
       ex_mem_1_memtoregout, \ex_mem_1_使能传递端_低电平有效_stall_高电平有效 , EX_MemToReg, EX_RegWrite, Go, Halt, HaltOut,
       id_ex_1_alusrcbout, id_ex_1_jalout, \id_ex_1_使能传递端_低电平有效_stall_高电平有效 , IR1, IR2, IR3, JAL, JMP, JR,
       LoadUse, MEM_Col_R1, MEM_Col_R2, MEM_RegWrite, mem_wb_1_memtoregout, mips_ram_adapter_1_clk_2,
       mips_ram_adapter_1_str, nor_1_out, not_1_out, or_1_out, or_2_out, or_5_out, or_6_out, R1_Used,
       R2_Used, SignedExt, Syscall, W1, W2, W3, \单周期硬布线控制器_1_alu_src , \单周期硬布线控制器_1_memtoreg ,
       \单周期硬布线控制器_1_regdst , \单周期硬布线控制器_1_regwrite ;
  wire [1:0] or_4_out;
  wire [2:0] ex_mem_1_memcontrolout;
  wire [3:0] id_ex_1_memcontrolout, \单周期硬布线控制器_1_memcontrol ;
  wire [4:0] EX_W_num, id_ex_1_shamtout, MEM_W_num, multiplexer_5_out, multiplexer_6_out, R1_num, R2_num,
       W_num;
  wire [6:0] id_ex_1_aluopout, \单周期硬布线控制器_1_alu_op ;
  wire [9:0] mips_ram_adapter_1_a;
  wire [15:0] \LoadUse次数 , \总周期数 , \插入气泡数 , \无条件分支数 , \条件分支成功数 ;
  wire [31:0] adder_1_out, bit_extender_1_out, bit_extender_2_out, BRADDR, ex_mem_1_aluout, ex_mem_1_irout,
       ex_mem_1_pc_4out, EX_PC, id_ex_1_aout, id_ex_1_bout, id_ex_1_immout, id_ex_1_irout, id_ex_1_pc_4out,
       ID_PC, if_id_1_pc_4out, LedData, MEM_PC, mem_wb_1_aluout, mem_wb_1_memout, mips_alu_1_result,
       mips_ram_adapter_1_dataout, mips_ram_adapter_1_din, multiplexer_1_out, multiplexer_4_out,
       multiplexer_7_out, multiplexer_8_out, R1, R2, ram_1_data, rom_1_data, shifter_1_out, WB_PC;

  Clock #(.highDuration(1), .lowDuration(1)) clock_1 (.out(CLK));
  Button _1 (.out(IR1));
  Button _2 (.out(IR2));
  Button _3 (.out(IR3));
  Button \u_继续运行  (.out(Go));
  LED #(.active("true")) led_1 (.in(W1));
  LED #(.active("true")) led_2 (.in(W2));
  LED #(.active("true")) led_3 (.in(W3));
  Multiplexer #(.select(2), .width(32), .disabled("Z"), .enable("false")) multiplexer_1 (
    .in0(adder_1_out), .in1(R1), .in2({ID_PC[31:28], IR[25:0], 2'b00}), .in3(BRADDR),
    .out(multiplexer_1_out), .sel(or_4_out));
  nor nor_1 (nor_1_out, Halt, Col);
  not not_1 (not_1_out, HaltOut);
  Hex_Digit_Display hex_digit_display_1 (.value(LedData[31:28]));  // open: dp
  or or_1 (or_1_out, or_4_out[0], or_2_out);
  or or_2 (or_2_out, JMP, JAL);
  or or_3 (or_4_out[1], or_2_out, branch);
  or or_4 (or_4_out[0], branch, JR);
  Register #(.width(32), .trigger("rising"), .Select("low")) u_PC (
    .D(multiplexer_1_out), .en(nor_1_out), .Q(PC), .clk(CLK));  // open: clr
  Counter #(.width(16), .max('hffff), .ongoal("stay"), .trigger("rising"), .behavior("old")) \u_总周期数  (
    .count(not_1_out), .Q(\总周期数 ), .clk(CLK));  // open: load, D, carry, clr, preset
  Hex_Digit_Display hex_digit_display_2 (.value(LedData[27:24]));  // open: dp
  Hex_Digit_Display hex_digit_display_3 (.value(LedData[23:20]));  // open: dp
  Adder #(.width(32)) adder_1 (.a(PC), .b(32'h4), .out(adder_1_out));  // open: cin, cout
  Hex_Digit_Display hex_digit_display_4 (.value(LedData[19:16]));  // open: dp
  Hex_Digit_Display hex_digit_display_5 (.value(LedData[15:12]));  // open: dp
  IF_ID if_id_1 (
    .PCin(PC), .IRin(rom_1_data), .CLK(CLK), .PCout(ID_PC), .IRout(IR), .\同步清零_气泡_高电平有效 (or_1_out),
    .\使能端_低电平有效_stall_高电平有效 (or_5_out), .PC_4in(adder_1_out), .PC_4out(if_id_1_pc_4out));  // open: 使能传递端_低电平有效_stall_高电平有效
  ROM #(.addrWidth(10), .dataWidth(32), .Select("high")) rom_1 (.addr(PC[11:2]), .data(rom_1_data));
  or or_5 (or_5_out, Col, Halt);
  Hex_Digit_Display hex_digit_display_6 (.value(LedData[7:4]));  // open: dp
  Hex_Digit_Display hex_digit_display_7 (.value(LedData[11:8]));  // open: dp
  // Probe on \总周期数 
  Hex_Digit_Display hex_digit_display_8 (.value(LedData[3:0]));  // open: dp
  assign bit_extender_1_out = {{16{1'b0}}, IR[15:0]};  // Bit_Extender bit_extender_1
  assign bit_extender_2_out = {{16{IR[15]}}, IR[15:0]};  // Bit_Extender bit_extender_2
  \数据相关检测  \u_数据相关检测_1  (
    .R1_Used(R1_Used), .R1_num(R1_num), .R2_Used(R2_Used), .R2_num(R2_num), .Collision(Col),
    .EX_RegWrite(EX_RegWrite), .EX_WriteReg_num(EX_W_num), .MEM_RegWrite(MEM_RegWrite),
    .MEM_WriteReg_num(MEM_W_num), .EX_Collision_R1(EX_Col_R1), .EX_Collision_R2(EX_Col_R2),
    .MEM_Collision_R1(MEM_Col_R1), .MEM_Collision_R2(MEM_Col_R2), .LoadUse(LoadUse), .Ex_MemToReg(EX_MemToReg));
  \单周期硬布线控制器  \u_单周期硬布线控制器_1  (
    .IR(IR), .ALU_OP(\单周期硬布线控制器_1_alu_op ), .MemToReg(\单周期硬布线控制器_1_memtoreg ),
    .MemControl(\单周期硬布线控制器_1_memcontrol ), .ALU_SRC(\单周期硬布线控制器_1_alu_src ),
    .RegWrite(\单周期硬布线控制器_1_regwrite ), .SysCALL(Syscall), .SignedExt(SignedExt),
    .RegDst(\单周期硬布线控制器_1_regdst ), .JR(JR), .JMP(JMP), .JAL(JAL), .R1_Used(R1_Used), .R2_Used(R2_Used));
  Multiplexer #(.select(1), .width(5), .disabled("Z"), .enable("false")) multiplexer_2 (
    .in0(IR[25:21]), .in1(5'b00010), .out(R1_num), .sel(Syscall));
  Multiplexer #(.select(1), .width(5), .disabled("Z"), .enable("false")) multiplexer_3 (
    .in0(IR[20:16]), .in1(5'b00100), .out(R2_num), .sel(Syscall));
  Multiplexer #(.select(1), .width(32), .disabled("Z"), .enable("false")) multiplexer_4 (
    .in0(bit_extender_1_out), .in1(bit_extender_2_out), .out(multiplexer_4_out), .sel(SignedExt));
  Multiplexer #(.select(1), .width(5), .disabled("Z"), .enable("false")) multiplexer_5 (
    .in0(IR[20:16]), .in1(IR[15:11]), .out(multiplexer_5_out), .sel(\单周期硬布线控制器_1_regdst ));
  ID_EX id_ex_1 (
    .PCin(ID_PC), .IRin(IR), .Ain(R1), .Bin(R2), .IMMin(multiplexer_4_out),
    .MEMTOREGin(\单周期硬布线控制器_1_memtoreg ), .MEMCONTROLin(\单周期硬布线控制器_1_memcontrol ),
    .ALUOPin(\单周期硬布线控制器_1_alu_op ), .ALUSRCBin(\单周期硬布线控制器_1_alu_src ), .CLK(CLK), .PCout(EX_PC),
    .IRout(id_ex_1_irout), .Aout(id_ex_1_aout), .Bout(id_ex_1_bout), .IMMout(id_ex_1_immout),
    .MEMTOREGout(EX_MemToReg), .MEMCONTROLout(id_ex_1_memcontrolout), .ALUOPout(id_ex_1_aluopout),
    .ALUSRCBout(id_ex_1_alusrcbout), .\同步清零_气泡_高电平有效 (or_6_out), .\使能端_低电平有效_stall_高电平有效 (Halt),
    .SHAMTin(IR[10:6]), .SHAMTout(id_ex_1_shamtout), .REGWRITEin(\单周期硬布线控制器_1_regwrite ),
    .REGWRITEout(EX_RegWrite), .W_in(multiplexer_6_out), .W_out(EX_W_num), .JALin(JAL),
    .JALout(id_ex_1_jalout), .\使能传递端_低电平有效_stall_高电平有效 (\id_ex_1_使能传递端_低电平有效_stall_高电平有效 ),
    .PC_4in(if_id_1_pc_4out), .PC_4out(id_ex_1_pc_4out));  // open: R1_SELin, R1_SELout, R2_SELin, R2_SELout
  Multiplexer #(.select(1), .width(5), .disabled("Z"), .enable("false")) multiplexer_6 (
    .in0(multiplexer_5_out), .in1({5{1'b1}}), .out(multiplexer_6_out), .sel(JAL));
  \MIPS_Regifile_下降沿  \mips_regifile_下降沿_1  (
    .Din(RDin), .Clk(CLK), .R1(R1), .R2(R2), .WE(RegWrite), .W_num(W_num), .R1_num(R1_num), .R2_num(R2_num));
  or or_6 (or_6_out, Col, branch);
  Shifter #(.width(32), .shift("ll")) shifter_1 (.in(id_ex_1_immout), .\dist (5'b00010), .out(shifter_1_out));
  Comparator #(.width(32), .mode("unsigned")) comparator_1 (.a(R1), .b(32'ha), .eq(comparator_1_eq));  // open: gt, lt
  and and_1 (and_1_out, ~comparator_1_eq, Syscall);  // AND_Gate
  Multiplexer #(.select(1), .width(32), .disabled("Z"), .enable("false")) multiplexer_7 (
    .in0(id_ex_1_bout), .in1(id_ex_1_immout), .out(multiplexer_7_out), .sel(id_ex_1_alusrcbout));
  Adder #(.width(32)) adder_2 (.a(id_ex_1_pc_4out), .b(shifter_1_out), .out(BRADDR));  // open: cin, cout
  Register #(.width(32), .trigger("rising"), .Select("low")) register_1 (
    .D(R2), .en(and_1_out), .Q(LedData), .clk(CLK));  // open: clr
  EX_MEM ex_mem_1 (
    .PCin(EX_PC), .IRin(id_ex_1_irout), .Bin(id_ex_1_bout), .MEMTOREGin(EX_MemToReg),
    .MEMCONTROLin(id_ex_1_memcontrolout), .CLK(CLK), .PCout(MEM_PC), .IRout(ex_mem_1_irout), .Bout(MDin),
    .MEMTOREGout(ex_mem_1_memtoregout), .MEMCONTROLout({MemWrite, ex_mem_1_memcontrolout}),
    .\使能端_低电平有效_stall_高电平有效 (\id_ex_1_使能传递端_低电平有效_stall_高电平有效 ), .ALUin(mips_alu_1_result),
    .ALUout(ex_mem_1_aluout), .REGWRITEin(EX_RegWrite), .REGWRITEout(MEM_RegWrite), .W_in(EX_W_num),
    .W_out(MEM_W_num), .JALin(id_ex_1_jalout), .JALout(ex_mem_1_jalout),
    .\使能传递端_低电平有效_stall_高电平有效 (\ex_mem_1_使能传递端_低电平有效_stall_高电平有效 ), .PC_4in(id_ex_1_pc_4out),
    .PC_4out(ex_mem_1_pc_4out));  // open: 同步清零_气泡_高电平有效
  MIPS_ALU mips_alu_1 (
    .X(id_ex_1_aout), .Y(multiplexer_7_out), .AluOP(id_ex_1_aluopout), .Branch(branch),
    .Result(mips_alu_1_result), .shamt(id_ex_1_shamtout));  // open: Result_2
  and and_2 (Halt, comparator_1_eq, Syscall);
  Multiplexer #(.select(1), .width(32), .disabled("Z"), .enable("false")) multiplexer_8 (
    .in0(ex_mem_1_aluout), .in1(ex_mem_1_pc_4out), .out(multiplexer_8_out), .sel(ex_mem_1_jalout));
  MIPS_Ram_Adapter mips_ram_adapter_1 (
    .Addr(ex_mem_1_aluout), .DataIn(MDin), .dout(ram_1_data), .CLK(CLK),
    .CONTROL({MemWrite, ex_mem_1_memcontrolout}), .A(mips_ram_adapter_1_a), .din(mips_ram_adapter_1_din),
    .DataOut(mips_ram_adapter_1_dataout), .clk_2(mips_ram_adapter_1_clk_2), .str(mips_ram_adapter_1_str));
  RAM #(.addrWidth(10), .dataWidth(32), .bus("separate"), .Select("high")) ram_1 (
    .addr(mips_ram_adapter_1_a), .din(mips_ram_adapter_1_din), .data(ram_1_data),
    .str(mips_ram_adapter_1_str), .clk(mips_ram_adapter_1_clk_2));  // open: sel, ld, clr
  MEM_WB mem_wb_1 (
    .PCin(MEM_PC), .IRin(ex_mem_1_irout), .ALUin(multiplexer_8_out), .MEMin(mips_ram_adapter_1_dataout),
    .MEMTOREGin(ex_mem_1_memtoregout), .CLK(CLK), .PCout(WB_PC), .ALUout(mem_wb_1_aluout),
    .MEMout(mem_wb_1_memout), .MEMTOREGout(mem_wb_1_memtoregout),
    .\使能端_低电平有效_stall_高电平有效 (\ex_mem_1_使能传递端_低电平有效_stall_高电平有效 ), .REGWRITEin(MEM_RegWrite),
    .REGWRITEout(RegWrite), .W_in(MEM_W_num), .W_out(W_num), .\使能传递端_低电平有效_stall_高电平有效 (HaltOut));  // open: IRout, 同步清零_气泡_高电平有效
  // Probe on \总周期数 
  // Probe on \无条件分支数 
  // Probe on \条件分支成功数 
  // Probe on \插入气泡数 
  // Probe on \LoadUse次数 
  Multiplexer #(.select(1), .width(32), .disabled("Z"), .enable("false")) multiplexer_9 (
    .in0(mem_wb_1_aluout), .in1(mem_wb_1_memout), .out(RDin), .sel(mem_wb_1_memtoregout));
  // Probe on PC[11:0]
  // Probe on ID_PC[11:0]
  // Probe on EX_PC[11:0]
  // Probe on MEM_PC[11:0]
  // Probe on WB_PC[11:0]

  // Other names for the same wires on the sheet: IF_PC[31:0] = PC; JADDR[25:0] = IR[25:0]

  // Notes on the sheet:
  //   中断源
  //   PC+4
  //   JR
  //   J/JAL
  //   中断等待指示
  //   总复位信号应将除ROM以外所有存储组件全部清零
  //   BEQ/BNE
  //   PC计数器
  //   指令存储器
  //   数码管输出
  //   contents of rom_1 (hex, n*v repeats v):
  //   20100001 201200ff 20110001 20130003 12120004 12100003 20110001 20120002 20130003 102020 20020001 c
  //   16310004 16320003 20110001 20120002 20130003 132020 20020001 c 2002000a c
  //   PC+4
  //   数码管输出应该用寄存器锁存，否则显示数据只能一闪而过
  //   JMP
  //   JR
  //   IR
  //   rs
  //   指令字
  //   rt
  //   addr
  //   imm
  //   shamt
  //   数据相关检测
  //   MemToReg
  //   MemControl
  //   AluOP
  //   AluSrcB
  //   RegWrite
  //   JAL
  //   RegDst
  //   Syscall
  //   rt
  //   rd
  //   Syscall功能实现
  //   v0
  //   为方便自动评测，需要输出PC，IR，寄存器文件写入端口RDin，内存写入端口MDin等信号
  //   a0
  //   流水调试日志用
endmodule

module \重定向流水线  (
  output RegWrite,
  output MemWrite,
  output [31:0] PC,
  output [31:0] IR,
  output [31:0] RDin,
  output [31:0] MDin
);

  wire and_1_out, branch, CLK, Col, comparator_1_eq, ex_mem_1_jalout, ex_mem_1_memtoregout,
       \ex_mem_1_使能传递端_低电平有效_stall_高电平有效 , EX_MemToReg, EX_RegWrite, Go, Halt, HaltOut, id_ex_1_alusrcbout,
       id_ex_1_jalout, \id_ex_1_使能传递端_低电平有效_stall_高电平有效 , IR1, IR2, IR3, JAL, JMP, JR, LoadUse, MEM_RegWrite,
       mem_wb_1_memtoregout, mips_ram_adapter_1_clk_2, mips_ram_adapter_1_str, nor_1_out, not_1_out,
       or_1_out, or_2_out, or_5_out, or_6_out, R1_Used, R2_Used, SignedExt, Syscall, W1, W2, W3,
       \单周期硬布线控制器_1_alu_src , \单周期硬布线控制器_1_memtoreg , \单周期硬布线控制器_1_regdst , \单周期硬布线控制器_1_regwrite ;
  wire [1:0] id_ex_1_r1_selout, id_ex_1_r2_selout, or_4_out, R1_Sel, R2_Sel;
  wire [2:0] ex_mem_1_memcontrolout;
  wire [3:0] id_ex_1_memcontrolout, \单周期硬布线控制器_1_memcontrol ;
  wire [4:0] EX_W_num, id_ex_1_shamtout, MEM_W_num, multiplexer_5_out, multiplexer_6_out, R1_num, R2_num,
       W_num;
  wire [6:0] id_ex_1_aluopout, \单周期硬布线控制器_1_alu_op ;
  wire [9:0] mips_ram_adapter_1_a;
  wire [15:0] \LoadUse次数 , \总周期数 , \插入气泡数 , \无条件分支数 , \条件分支成功数 ;
  wire [31:0] adder_1_out, bit_extender_1_out, bit_extender_2_out, BRADDR, ex_mem_1_aluout, ex_mem_1_irout,
       ex_mem_1_pc_4out, EX_PC, id_ex_1_aout, id_ex_1_bout, id_ex_1_immout, id_ex_1_irout, id_ex_1_pc_4out,
       ID_PC, ID_R1, ID_R2, if_id_1_pc_4out, IF_PC, LedData, MEM_PC, mem_wb_1_aluout, mem_wb_1_memout,
       mips_ram_adapter_1_dataout, mips_ram_adapter_1_din, multiplexer_1_out, multiplexer_4_out,
       multiplexer_9_out, multiplexer_10_out, multiplexer_11_out, R, R1, R2, ram_1_data, RegD, rom_1_data,
       shifter_1_out, WB_PC;

  Clock #(.highDuration(1), .lowDuration(1)) clock_1 (.out(CLK));
  Button _1 (.out(IR1));
  Button _2 (.out(IR2));
  Button _3 (.out(IR3));
  Button \u_继续运行  (.out(Go));
  LED #(.active("true")) led_1 (.in(W1));
  LED #(.active("true")) led_2 (.in(W2));
  LED #(.active("true")) led_3 (.in(W3));
  Multiplexer #(.select(2), .width(32), .disabled("Z"), .enable("false")) multiplexer_1 (
    .in0(adder_1_out), .in1(R1), .in2({ID_PC[31:28], IR[25:0], 2'b00}), .in3(BRADDR),
    .out(multiplexer_1_out), .sel(or_4_out));
  nor nor_1 (nor_1_out, Halt, LoadUse);
  not not_1 (not_1_out, HaltOut);
  Hex_Digit_Display hex_digit_display_1 (.value(LedData[31:28]));  // open: dp
  or or_1 (or_1_out, or_4_out[0], or_2_out);
  or or_2 (or_2_out, JMP, JAL);
  or or_3 (or_4_out[1], or_2_out, branch);
  or or_4 (or_4_out[0], branch, JR);
  Register #(.width(32), .trigger("rising"), .Select("low")) u_PC (
    .D(multiplexer_1_out), .en(nor_1_out), .Q(IF_PC), .clk(CLK));  // open: clr
  Counter #(.width(16), .max('hffff), .ongoal("stay"), .trigger("rising"), .behavior("old")) \u_总周期数  (
    .count(not_1_out), .Q(\总周期数 ), .clk(CLK));  // open: load, D, carry, clr, preset
  Hex_Digit_Display hex_digit_display_2 (.value(LedData[23:20]));  // open: dp
  Hex_Digit_Display hex_digit_display_3 (.value(LedData[27:24]));  // open: dp
  Adder #(.width(32)) adder_1 (.a(IF_PC), .b(32'h4), .out(adder_1_out));  // open: cin, cout
  Hex_Digit_Display hex_digit_display_4 (.value(LedData[19:16]));  // open: dp
  Hex_Digit_Display hex_digit_display_5 (.value(LedData[15:12]));  // open: dp
  IF_ID if_id_1 (
    .PCin(IF_PC), .IRin(rom_1_data), .CLK(CLK), .PCout(ID_PC), .IRout(IR), .\同步清零_气泡_高电平有效 (or_1_out),
    .\使能端_低电平有效_stall_高电平有效 (or_5_out), .PC_4in(adder_1_out), .PC_4out(if_id_1_pc_4out));  // open: 使能传递端_低电平有效_stall_高电平有效
  ROM #(.addrWidth(10), .dataWidth(32), .Select("high")) rom_1 (.addr(IF_PC[11:2]), .data(rom_1_data));
  or or_5 (or_5_out, LoadUse, Halt);
  Hex_Digit_Display hex_digit_display_6 (.value(LedData[7:4]));  // open: dp
  Hex_Digit_Display hex_digit_display_7 (.value(LedData[11:8]));  // open: dp
  // Probe on \总周期数 
  Hex_Digit_Display hex_digit_display_8 (.value(LedData[3:0]));  // open: dp
  assign bit_extender_1_out = {{16{1'b0}}, IR[15:0]};  // Bit_Extender bit_extender_1
  assign bit_extender_2_out = {{16{IR[15]}}, IR[15:0]};  // Bit_Extender bit_extender_2
  \数据相关检测  \u_数据相关检测_1  (
    .R1_Used(R1_Used), .R1_num(R1_num), .R2_Used(R2_Used), .R2_num(R2_num), .Collision(Col),
    .EX_RegWrite(EX_RegWrite), .EX_WriteReg_num(EX_W_num), .MEM_RegWrite(MEM_RegWrite),
    .MEM_WriteReg_num(MEM_W_num), .EX_Collision_R1(R1_Sel[1]), .EX_Collision_R2(R2_Sel[1]),
    .MEM_Collision_R1(R1_Sel[0]), .MEM_Collision_R2(R2_Sel[0]), .LoadUse(LoadUse), .Ex_MemToReg(EX_MemToReg));
  \单周期硬布线控制器  \u_单周期硬布线控制器_1  (
    .IR(IR), .ALU_OP(\单周期硬布线控制器_1_alu_op ), .MemToReg(\单周期硬布线控制器_1_memtoreg ),
    .MemControl(\单周期硬布线控制器_1_memcontrol ), .ALU_SRC(\单周期硬布线控制器_1_alu_src ),
    .RegWrite(\单周期硬布线控制器_1_regwrite ), .SysCALL(Syscall), .SignedExt(SignedExt),
    .RegDst(\单周期硬布线控制器_1_regdst ), .JR(JR), .JMP(JMP), .JAL(JAL), .R1_Used(R1_Used), .R2_Used(R2_Used));
  Multiplexer #(.select(1), .width(5), .disabled("Z"), .enable("false")) multiplexer_2 (
    .in0(IR[25:21]), .in1(5'b00010), .out(R1_num), .sel(Syscall));
  Multiplexer #(.select(1), .width(5), .disabled("Z"), .enable("false")) multiplexer_3 (
    .in0(IR[20:16]), .in1(5'b00100), .out(R2_num), .sel(Syscall));
  Multiplexer #(.select(1), .width(32), .disabled("Z"), .enable("false")) multiplexer_4 (
    .in0(bit_extender_1_out), .in1(bit_extender_2_out), .out(multiplexer_4_out), .sel(SignedExt));
  Multiplexer #(.select(1), .width(5), .disabled("Z"), .enable("false")) multiplexer_5 (
    .in0(IR[20:16]), .in1(IR[15:11]), .out(multiplexer_5_out), .sel(\单周期硬布线控制器_1_regdst ));
  ID_EX id_ex_1 (
    .PCin(ID_PC), .IRin(IR), .Ain(ID_R1), .Bin(ID_R2), .IMMin(multiplexer_4_out),
    .MEMTOREGin(\单周期硬布线控制器_1_memtoreg ), .MEMCONTROLin(\单周期硬布线控制器_1_memcontrol ),
    .ALUOPin(\单周期硬布线控制器_1_alu_op ), .ALUSRCBin(\单周期硬布线控制器_1_alu_src ), .CLK(CLK), .PCout(EX_PC),
    .IRout(id_ex_1_irout), .Aout(id_ex_1_aout), .Bout(id_ex_1_bout), .IMMout(id_ex_1_immout),
    .MEMTOREGout(EX_MemToReg), .MEMCONTROLout(id_ex_1_memcontrolout), .ALUOPout(id_ex_1_aluopout),
    .ALUSRCBout(id_ex_1_alusrcbout), .\同步清零_气泡_高电平有效 (or_6_out), .\使能端_低电平有效_stall_高电平有效 (Halt),
    .SHAMTin(IR[10:6]), .SHAMTout(id_ex_1_shamtout), .REGWRITEin(\单周期硬布线控制器_1_regwrite ),
    .REGWRITEout(EX_RegWrite), .W_in(multiplexer_6_out), .W_out(EX_W_num), .JALin(JAL),
    .JALout(id_ex_1_jalout), .\使能传递端_低电平有效_stall_高电平有效 (\id_ex_1_使能传递端_低电平有效_stall_高电平有效 ),
    .PC_4in(if_id_1_pc_4out), .PC_4out(id_ex_1_pc_4out), .R1_SELin(R1_Sel), .R1_SELout(id_ex_1_r1_selout),
    .R2_SELin(R2_Sel), .R2_SELout(id_ex_1_r2_selout));
  Multiplexer #(.select(1), .width(5), .disabled("Z"), .enable("false")) multiplexer_6 (
    .in0(multiplexer_5_out), .in1({5{1'b1}}), .out(multiplexer_6_out), .sel(JAL));
  \MIPS_Regifile_下降沿  \mips_regifile_下降沿_1  (
    .Din(RDin), .Clk(CLK), .R1(ID_R1), .R2(ID_R2), .WE(RegWrite), .W_num(W_num), .R1_num(R1_num),
    .R2_num(R2_num));
  Multiplexer #(.select(2), .width(32), .disabled("Z"), .enable("false")) multiplexer_7 (
    .in0(ID_R1), .in1(RegD), .in2(R), .in3(R), .out(R1), .sel(R1_Sel));
  Multiplexer #(.select(2), .width(32), .disabled("Z"), .enable("false")) multiplexer_8 (
    .in0(ID_R2), .in1(RegD), .in2(R), .in3(R), .out(R2), .sel(R2_Sel));
  or or_6 (or_6_out, LoadUse, branch);
  Multiplexer #(.select(2), .width(32), .disabled("Z"), .enable("false")) multiplexer_9 (
    .in0(id_ex_1_aout), .in1(RDin), .in2(RegD), .in3(RegD), .out(multiplexer_9_out), .sel(id_ex_1_r1_selout));
  Multiplexer #(.select(2), .width(32), .disabled("Z"), .enable("false")) multiplexer_10 (
    .in0(id_ex_1_bout), .in1(RDin), .in2(RegD), .in3(RegD), .out(multiplexer_10_out), .sel(id_ex_1_r2_selout));
  Shifter #(.width(32), .shift("ll")) shifter_1 (.in(id_ex_1_immout), .\dist (5'b00010), .out(shifter_1_out));
  Multiplexer #(.select(1), .width(32), .disabled("Z"), .enable("false")) multiplexer_11 (
    .in0(multiplexer_10_out), .in1(id_ex_1_immout), .out(multiplexer_11_out), .sel(id_ex_1_alusrcbout));
  Adder #(.width(32)) adder_2 (.a(id_ex_1_pc_4out), .b(shifter_1_out), .out(BRADDR));  // open: cin, cout
  Comparator #(.width(32), .mode("unsigned")) comparator_1 (.a(R1), .b(32'ha), .eq(comparator_1_eq));  // open: gt, lt
  EX_MEM ex_mem_1 (
    .PCin(EX_PC), .IRin(id_ex_1_irout), .Bin(multiplexer_10_out), .MEMTOREGin(EX_MemToReg),
    .MEMCONTROLin(id_ex_1_memcontrolout), .CLK(CLK), .PCout(MEM_PC), .IRout(ex_mem_1_irout), .Bout(MDin),
    .MEMTOREGout(ex_mem_1_memtoregout), .MEMCONTROLout({MemWrite, ex_mem_1_memcontrolout}),
    .\使能端_低电平有效_stall_高电平有效 (\id_ex_1_使能传递端_低电平有效_stall_高电平有效 ), .ALUin(R), .ALUout(ex_mem_1_aluout),
    .REGWRITEin(EX_RegWrite), .REGWRITEout(MEM_RegWrite), .W_in(EX_W_num), .W_out(MEM_W_num),
    .JALin(id_ex_1_jalout), .JALout(ex_mem_1_jalout),
    .\使能传递端_低电平有效_stall_高电平有效 (\ex_mem_1_使能传递端_低电平有效_stall_高电平有效 ), .PC_4in(id_ex_1_pc_4out),
    .PC_4out(ex_mem_1_pc_4out));  // open: 同步清零_气泡_高电平有效
  MIPS_ALU mips_alu_1 (
    .X(multiplexer_9_out), .Y(multiplexer_11_out), .AluOP(id_ex_1_aluopout), .Branch(branch), .Result(R),
    .shamt(id_ex_1_shamtout));  // open: Result_2
  and and_1 (and_1_out, ~comparator_1_eq, Syscall);  // AND_Gate
  Register #(.width(32), .trigger("rising"), .Select("low")) register_1 (
    .D(R2), .en(and_1_out), .Q(LedData), .clk(CLK));  // open: clr
  Multiplexer #(.select(1), .width(32), .disabled("Z"), .enable("false")) multiplexer_12 (
    .in0(ex_mem_1_aluout), .in1(ex_mem_1_pc_4out), .out(RegD), .sel(ex_mem_1_jalout));
  MIPS_Ram_Adapter mips_ram_adapter_1 (
    .Addr(ex_mem_1_aluout), .DataIn(MDin), .dout(ram_1_data), .CLK(CLK),
    .CONTROL({MemWrite, ex_mem_1_memcontrolout}), .A(mips_ram_adapter_1_a), .din(mips_ram_adapter_1_din),
    .DataOut(mips_ram_adapter_1_dataout), .clk_2(mips_ram_adapter_1_clk_2), .str(mips_ram_adapter_1_str));
  and and_2 (Halt, comparator_1_eq, Syscall);
  RAM #(.addrWidth(10), .dataWidth(32), .bus("separate"), .Select("high")) ram_1 (
    .addr(mips_ram_adapter_1_a), .din(mips_ram_adapter_1_din), .data(ram_1_data),
    .str(mips_ram_adapter_1_str), .clk(mips_ram_adapter_1_clk_2));  // open: sel, ld, clr
  // Probe on \总周期数 
  // Probe on \无条件分支数 
  // Probe on \条件分支成功数 
  // Probe on \插入气泡数 
  // Probe on \LoadUse次数 
  MEM_WB mem_wb_1 (
    .PCin(MEM_PC), .IRin(ex_mem_1_irout), .ALUin(RegD), .MEMin(mips_ram_adapter_1_dataout),
    .MEMTOREGin(ex_mem_1_memtoregout), .CLK(CLK), .PCout(WB_PC), .ALUout(mem_wb_1_aluout),
    .MEMout(mem_wb_1_memout), .MEMTOREGout(mem_wb_1_memtoregout),
    .\使能端_低电平有效_stall_高电平有效 (\ex_mem_1_使能传递端_低电平有效_stall_高电平有效 ), .REGWRITEin(MEM_RegWrite),
    .REGWRITEout(RegWrite), .W_in(MEM_W_num), .W_out(W_num), .\使能传递端_低电平有效_stall_高电平有效 (HaltOut));  // open: IRout, 同步清零_气泡_高电平有效
  // Probe on IF_PC[11:0]
  Multiplexer #(.select(1), .width(32), .disabled("Z"), .enable("false")) multiplexer_13 (
    .in0(mem_wb_1_aluout), .in1(mem_wb_1_memout), .out(RDin), .sel(mem_wb_1_memtoregout));
  // Probe on EX_PC[11:0]
  // Probe on ID_PC[11:0]
  // Probe on MEM_PC[11:0]
  // Probe on WB_PC[11:0]

  // Other names for the same wires on the sheet: JADDR[25:0] = IR[25:0]

  // Notes on the sheet:
  //   中断源
  //   PC+4
  //   JR
  //   J/JAL
  //   中断等待指示
  //   总复位信号应将除ROM以外所有存储组件全部清零
  //   BEQ/BNE
  //   PC计数器
  //   指令存储器
  //   数码管输出
  //   contents of rom_1 (hex, n*v repeats v):
  //   20100001 109fc0 139fc3 8021 2012000c 24160003 26100001 3210000f 20080008 20090001 139900 2709825
  //   132020 20020022 c 1094022 1500fff9 22100001 2018000f 2188024 108700 20080008 20090001 139902 2709825
  //   132021 20020022 c 1094022 1500fff9 108702 2c9b022 12c00001 8000c06 4020 1084027 84400 3508ffff
  //   132021 20020022 c 2002000a c
  //   PC+4
  //   数码管输出应该用寄存器锁存，否则显示数据只能一闪而过
  //   IR
  //   rs
  //   指令字
  //   rt
  //   addr
  //   imm
  //   shamt
  //   数据相关检测
  //   JMP
  //   JR
  //   MemToReg
  //   MemControl
  //   AluOP
  //   AluSrcB
  //   RegWrite
  //   JAL
  //   RegDst
  //   Syscall
  //   rt
  //   rd
  //   为方便自动评测，需要输出PC，IR，寄存器文件写入端口RDin，内存写入端口MDin等信号
  //   Syscall功能实现
  //   v0
  //   a0
  //   流水调试日志用
endmodule

module \中断按键参考电路  (
  input  \同步清零信号 ,
  output \与中断屏蔽位与 
);

  wire \_1号中断_out , and_1_out, clock_1_out, d_ff_1_q, or_1_out, or_2_out;

  Clock #(.highDuration(1), .lowDuration(1)) clock_1 (.out(clock_1_out));
  Button \_1号中断  (.out(\_1号中断_out ));
  or or_1 (or_1_out, \与中断屏蔽位与 , d_ff_1_q);
  LED #(.active("true")) \_1号中断等待指示灯  (.in(or_1_out));
  D_Flip_Flop #(.trigger("rising"), .Pre_Clr_Positions("LEGACY"), .NegatePresetClear("false"), .enable("true"), .NewFFLayout("false")) d_ff_1 (
    .clk(\_1号中断_out ), .D(1'b1), .Q(d_ff_1_q), .reset(\与中断屏蔽位与 ));  // open: Qn, preset, en
  or or_2 (or_2_out, d_ff_1_q, \与中断屏蔽位与 );
  and and_1 (and_1_out, or_2_out, ~\同步清零信号 );  // AND_Gate
  D_Flip_Flop #(.trigger("rising"), .Pre_Clr_Positions("LEGACY"), .NegatePresetClear("false"), .enable("true"), .NewFFLayout("false")) IR1 (
    .clk(clock_1_out), .D(and_1_out), .Q(\与中断屏蔽位与 ));  // open: Qn, preset, en, reset

  // Notes on the sheet:
  //   中断信号采样参考电路
  //   Reset 
endmodule

module IF_ID (
  input  [31:0] PCin,
  input  [31:0] IRin,
  input  [31:0] PC_4in,
  input  CLK,
  input  \同步清零_气泡_高电平有效 ,
  input  \使能端_低电平有效_stall_高电平有效 ,
  output [31:0] PCout,
  output [31:0] IRout,
  output [31:0] PC_4out,
  output \使能传递端_低电平有效_stall_高电平有效 
);

  wire not_1_out;
  wire [31:0] multiplexer_1_out, multiplexer_2_out, multiplexer_3_out;

  Multiplexer #(.select(1), .width(32), .disabled("Z"), .enable("false")) multiplexer_1 (
    .in0(PCin), .in1({32{1'b0}}), .out(multiplexer_1_out), .sel(\同步清零_气泡_高电平有效 ));
  Multiplexer #(.select(1), .width(32), .disabled("Z"), .enable("false")) multiplexer_2 (
    .in0(IRin), .in1({32{1'b0}}), .out(multiplexer_2_out), .sel(\同步清零_气泡_高电平有效 ));
  Multiplexer #(.select(1), .width(32), .disabled("Z"), .enable("false")) multiplexer_3 (
    .in0(PC_4in), .in1({32{1'b0}}), .out(multiplexer_3_out), .sel(\同步清零_气泡_高电平有效 ));
  Pull_Resistor #(.pull(0)) pull_resistor_1 (.node(\同步清零_气泡_高电平有效 ));
  not not_1 (not_1_out, \使能端_低电平有效_stall_高电平有效 );
  Register #(.width(32), .trigger("rising"), .Select("low")) register_1 (
    .D(multiplexer_1_out), .en(not_1_out), .Q(PCout), .clk(CLK));  // open: clr
  Register #(.width(32), .trigger("rising"), .Select("low")) register_2 (
    .D(multiplexer_2_out), .en(not_1_out), .Q(IRout), .clk(CLK));  // open: clr
  Register #(.width(32), .trigger("rising"), .Select("low")) register_3 (
    .D(multiplexer_3_out), .en(not_1_out), .Q(PC_4out), .clk(CLK));  // open: clr
  Pull_Resistor #(.pull(0)) pull_resistor_2 (.node(not_1_out));
  Register #(.width(1), .trigger("rising"), .Select("low")) register_4 (
    .D(\使能端_低电平有效_stall_高电平有效 ), .Q(\使能传递端_低电平有效_stall_高电平有效 ), .clk(CLK));  // open: en, clr
endmodule

module ID_EX (
  input  [31:0] PCin,
  input  [31:0] IRin,
  input  [31:0] Ain,
  input  [31:0] Bin,
  input  [31:0] IMMin,
  input  [31:0] PC_4in,
  input  [4:0] SHAMTin,
  input  MEMTOREGin,
  input  [3:0] MEMCONTROLin,
  input  [6:0] ALUOPin,
  input  ALUSRCBin,
  input  REGWRITEin,
  input  [4:0] W_in,
  input  JALin,
  input  [1:0] R1_SELin,
  input  [1:0] R2_SELin,
  input  CLK,
  input  \同步清零_气泡_高电平有效 ,
  input  \使能端_低电平有效_stall_高电平有效 ,
  output [31:0] PCout,
  output [31:0] IRout,
  output [31:0] Aout,
  output [31:0] Bout,
  output [31:0] IMMout,
  output [31:0] PC_4out,
  output [4:0] SHAMTout,
  output MEMTOREGout,
  output [3:0] MEMCONTROLout,
  output [6:0] ALUOPout,
  output ALUSRCBout,
  output REGWRITEout,
  output [4:0] W_out,
  output JALout,
  output [1:0] R1_SELout,
  output [1:0] R2_SELout,
  output \使能传递端_低电平有效_stall_高电平有效 
);

  wire multiplexer_8_out, multiplexer_11_out, multiplexer_12_out, multiplexer_14_out, not_1_out;
  wire [1:0] multiplexer_15_out, multiplexer_16_out;
  wire [3:0] multiplexer_9_out;
  wire [4:0] multiplexer_7_out, multiplexer_13_out;
  wire [6:0] multiplexer_10_out;
  wire [31:0] multiplexer_1_out, multiplexer_2_out, multiplexer_3_out, multiplexer_4_out, multiplexer_5_out,
       multiplexer_6_out;

  Multiplexer #(.select(1), .width(32), .disabled("Z"), .enable("false")) multiplexer_1 (
    .in0(PCin), .in1({32{1'b0}}), .out(multiplexer_1_out), .sel(\同步清零_气泡_高电平有效 ));
  Multiplexer #(.select(1), .width(32), .disabled("Z"), .enable("false")) multiplexer_2 (
    .in0(IRin), .in1({32{1'b0}}), .out(multiplexer_2_out), .sel(\同步清零_气泡_高电平有效 ));
  Multiplexer #(.select(1), .width(32), .disabled("Z"), .enable("false")) multiplexer_3 (
    .in0(Ain), .in1({32{1'b0}}), .out(multiplexer_3_out), .sel(\同步清零_气泡_高电平有效 ));
  Multiplexer #(.select(1), .width(32), .disabled("Z"), .enable("false")) multiplexer_4 (
    .in0(Bin), .in1({32{1'b0}}), .out(multiplexer_4_out), .sel(\同步清零_气泡_高电平有效 ));
  Multiplexer #(.select(1), .width(32), .disabled("Z"), .enable("false")) multiplexer_5 (
    .in0(IMMin), .in1({32{1'b0}}), .out(multiplexer_5_out), .sel(\同步清零_气泡_高电平有效 ));
  Multiplexer #(.select(1), .width(32), .disabled("Z"), .enable("false")) multiplexer_6 (
    .in0(PC_4in), .in1({32{1'b0}}), .out(multiplexer_6_out), .sel(\同步清零_气泡_高电平有效 ));
  Multiplexer #(.select(1), .width(5), .disabled("Z"), .enable("false")) multiplexer_7 (
    .in0(SHAMTin), .in1({5{1'b0}}), .out(multiplexer_7_out), .sel(\同步清零_气泡_高电平有效 ));
  Multiplexer #(.select(1), .width(1), .disabled("Z"), .enable("false")) multiplexer_8 (
    .in0(MEMTOREGin), .in1(1'b0), .out(multiplexer_8_out), .sel(\同步清零_气泡_高电平有效 ));
  Multiplexer #(.select(1), .width(4), .disabled("Z"), .enable("false")) multiplexer_9 (
    .in0(MEMCONTROLin), .in1(4'b0000), .out(multiplexer_9_out), .sel(\同步清零_气泡_高电平有效 ));
  Multiplexer #(.select(1), .width(7), .disabled("Z"), .enable("false")) multiplexer_10 (
    .in0(ALUOPin), .in1({7{1'b0}}), .out(multiplexer_10_out), .sel(\同步清零_气泡_高电平有效 ));
  Multiplexer #(.select(1), .width(1), .disabled("Z"), .enable("false")) multiplexer_11 (
    .in0(ALUSRCBin), .in1(1'b0), .out(multiplexer_11_out), .sel(\同步清零_气泡_高电平有效 ));
  Multiplexer #(.select(1), .width(1), .disabled("Z"), .enable("false")) multiplexer_12 (
    .in0(REGWRITEin), .in1(1'b0), .out(multiplexer_12_out), .sel(\同步清零_气泡_高电平有效 ));
  Multiplexer #(.select(1), .width(5), .disabled("Z"), .enable("false")) multiplexer_13 (
    .in0(W_in), .in1({5{1'b0}}), .out(multiplexer_13_out), .sel(\同步清零_气泡_高电平有效 ));
  Multiplexer #(.select(1), .width(1), .disabled("Z"), .enable("false")) multiplexer_14 (
    .in0(JALin), .in1(1'b0), .out(multiplexer_14_out), .sel(\同步清零_气泡_高电平有效 ));
  Multiplexer #(.select(1), .width(2), .disabled("Z"), .enable("false")) multiplexer_15 (
    .in0(R1_SELin), .in1(2'b00), .out(multiplexer_15_out), .sel(\同步清零_气泡_高电平有效 ));
  Multiplexer #(.select(1), .width(2), .disabled("Z"), .enable("false")) multiplexer_16 (
    .in0(R2_SELin), .in1(2'b00), .out(multiplexer_16_out), .sel(\同步清零_气泡_高电平有效 ));
  Pull_Resistor #(.pull(0)) pull_resistor_1 (.node(\同步清零_气泡_高电平有效 ));
  not not_1 (not_1_out, \使能端_低电平有效_stall_高电平有效 );
  Register #(.width(32), .trigger("rising"), .Select("low")) register_1 (
    .D(multiplexer_1_out), .en(not_1_out), .Q(PCout), .clk(CLK));  // open: clr
  Register #(.width(32), .trigger("rising"), .Select("low")) register_2 (
    .D(multiplexer_2_out), .en(not_1_out), .Q(IRout), .clk(CLK));  // open: clr
  Register #(.width(32), .trigger("rising"), .Select("low")) register_3 (
    .D(multiplexer_3_out), .en(not_1_out), .Q(Aout), .clk(CLK));  // open: clr
  Register #(.width(32), .trigger("rising"), .Select("low")) register_4 (
    .D(multiplexer_4_out), .en(not_1_out), .Q(Bout), .clk(CLK));  // open: clr
  Register #(.width(32), .trigger("rising"), .Select("low")) register_5 (
    .D(multiplexer_5_out), .en(not_1_out), .Q(IMMout), .clk(CLK));  // open: clr
  Register #(.width(32), .trigger("rising"), .Select("low")) register_6 (
    .D(multiplexer_6_out), .en(not_1_out), .Q(PC_4out), .clk(CLK));  // open: clr
  Register #(.width(5), .trigger("rising"), .Select("low")) register_7 (
    .D(multiplexer_7_out), .en(not_1_out), .Q(SHAMTout), .clk(CLK));  // open: clr
  Register #(.width(1), .trigger("rising"), .Select("low")) register_8 (
    .D(multiplexer_8_out), .en(not_1_out), .Q(MEMTOREGout), .clk(CLK));  // open: clr
  Register #(.width(4), .trigger("rising"), .Select("low")) register_9 (
    .D(multiplexer_9_out), .en(not_1_out), .Q(MEMCONTROLout), .clk(CLK));  // open: clr
  Register #(.width(7), .trigger("rising"), .Select("low")) register_10 (
    .D(multiplexer_10_out), .en(not_1_out), .Q(ALUOPout), .clk(CLK));  // open: clr
  Register #(.width(1), .trigger("rising"), .Select("low")) register_11 (
    .D(multiplexer_11_out), .en(not_1_out), .Q(ALUSRCBout), .clk(CLK));  // open: clr
  Register #(.width(1), .trigger("rising"), .Select("low")) register_12 (
    .D(multiplexer_12_out), .en(not_1_out), .Q(REGWRITEout), .clk(CLK));  // open: clr
  Register #(.width(5), .trigger("rising"), .Select("low")) register_13 (
    .D(multiplexer_13_out), .en(not_1_out), .Q(W_out), .clk(CLK));  // open: clr
  Register #(.width(1), .trigger("rising"), .Select("low")) register_14 (
    .D(multiplexer_14_out), .en(not_1_out), .Q(JALout), .clk(CLK));  // open: clr
  Register #(.width(2), .trigger("rising"), .Select("low")) register_15 (
    .D(multiplexer_15_out), .en(not_1_out), .Q(R1_SELout), .clk(CLK));  // open: clr
  Register #(.width(2), .trigger("rising"), .Select("low")) register_16 (
    .D(multiplexer_16_out), .en(not_1_out), .Q(R2_SELout), .clk(CLK));  // open: clr
  Pull_Resistor #(.pull(0)) pull_resistor_2 (.node(not_1_out));
  Register #(.width(1), .trigger("rising"), .Select("low")) register_17 (
    .D(\使能端_低电平有效_stall_高电平有效 ), .Q(\使能传递端_低电平有效_stall_高电平有效 ), .clk(CLK));  // open: en, clr
endmodule

module EX_MEM (
  input  [31:0] PCin,
  input  [31:0] IRin,
  input  [31:0] ALUin,
  input  [31:0] Bin,
  input  [31:0] PC_4in,
  input  MEMTOREGin,
  input  [3:0] MEMCONTROLin,
  input  REGWRITEin,
  input  [4:0] W_in,
  input  JALin,
  input  CLK,
  input  \同步清零_气泡_高电平有效 ,
  input  \使能端_低电平有效_stall_高电平有效 ,
  output [31:0] PCout,
  output [31:0] IRout,
  output [31:0] ALUout,
  output [31:0] Bout,
  output [31:0] PC_4out,
  output MEMTOREGout,
  output [3:0] MEMCONTROLout,
  output REGWRITEout,
  output [4:0] W_out,
  output JALout,
  output \使能传递端_低电平有效_stall_高电平有效 
);

  wire multiplexer_6_out, multiplexer_8_out, multiplexer_10_out, not_1_out;
  wire [3:0] multiplexer_7_out;
  wire [4:0] multiplexer_9_out;
  wire [31:0] multiplexer_1_out, multiplexer_2_out, multiplexer_3_out, multiplexer_4_out, multiplexer_5_out;

  Multiplexer #(.select(1), .width(32), .disabled("Z"), .enable("false")) multiplexer_1 (
    .in0(PCin), .in1({32{1'b0}}), .out(multiplexer_1_out), .sel(\同步清零_气泡_高电平有效 ));
  Multiplexer #(.select(1), .width(32), .disabled("Z"), .enable("false")) multiplexer_2 (
    .in0(IRin), .in1({32{1'b0}}), .out(multiplexer_2_out), .sel(\同步清零_气泡_高电平有效 ));
  Multiplexer #(.select(1), .width(32), .disabled("Z"), .enable("false")) multiplexer_3 (
    .in0(ALUin), .in1({32{1'b0}}), .out(multiplexer_3_out), .sel(\同步清零_气泡_高电平有效 ));
  Multiplexer #(.select(1), .width(32), .disabled("Z"), .enable("false")) multiplexer_4 (
    .in0(Bin), .in1({32{1'b0}}), .out(multiplexer_4_out), .sel(\同步清零_气泡_高电平有效 ));
  Multiplexer #(.select(1), .width(32), .disabled("Z"), .enable("false")) multiplexer_5 (
    .in0(PC_4in), .in1({32{1'b0}}), .out(multiplexer_5_out), .sel(\同步清零_气泡_高电平有效 ));
  Multiplexer #(.select(1), .width(1), .disabled("Z"), .enable("false")) multiplexer_6 (
    .in0(MEMTOREGin), .in1(1'b0), .out(multiplexer_6_out), .sel(\同步清零_气泡_高电平有效 ));
  Multiplexer #(.select(1), .width(4), .disabled("Z"), .enable("false")) multiplexer_7 (
    .in0(MEMCONTROLin), .in1(4'b0000), .out(multiplexer_7_out), .sel(\同步清零_气泡_高电平有效 ));
  Multiplexer #(.select(1), .width(1), .disabled("Z"), .enable("false")) multiplexer_8 (
    .in0(REGWRITEin), .in1(1'b0), .out(multiplexer_8_out), .sel(\同步清零_气泡_高电平有效 ));
  Multiplexer #(.select(1), .width(5), .disabled("Z"), .enable("false")) multiplexer_9 (
    .in0(W_in), .in1({5{1'b0}}), .out(multiplexer_9_out), .sel(\同步清零_气泡_高电平有效 ));
  Multiplexer #(.select(1), .width(1), .disabled("Z"), .enable("false")) multiplexer_10 (
    .in0(JALin), .in1(1'b0), .out(multiplexer_10_out), .sel(\同步清零_气泡_高电平有效 ));
  Pull_Resistor #(.pull(0)) pull_resistor_1 (.node(\同步清零_气泡_高电平有效 ));
  not not_1 (not_1_out, \使能端_低电平有效_stall_高电平有效 );
  Register #(.width(32), .trigger("rising"), .Select("low")) register_1 (
    .D(multiplexer_1_out), .en(not_1_out), .Q(PCout), .clk(CLK));  // open: clr
  Register #(.width(32), .trigger("rising"), .Select("low")) register_2 (
    .D(multiplexer_2_out), .en(not_1_out), .Q(IRout), .clk(CLK));  // open: clr
  Register #(.width(32), .trigger("rising"), .Select("low")) register_3 (
    .D(multiplexer_3_out), .en(not_1_out), .Q(ALUout), .clk(CLK));  // open: clr
  Register #(.width(32), .trigger("rising"), .Select("low")) register_4 (
    .D(multiplexer_4_out), .en(not_1_out), .Q(Bout), .clk(CLK));  // open: clr
  Register #(.width(32), .trigger("rising"), .Select("low")) register_5 (
    .D(multiplexer_5_out), .en(not_1_out), .Q(PC_4out), .clk(CLK));  // open: clr
  Register #(.width(1), .trigger("rising"), .Select("low")) register_6 (
    .D(multiplexer_6_out), .en(not_1_out), .Q(MEMTOREGout), .clk(CLK));  // open: clr
  Register #(.width(4), .trigger("rising"), .Select("low")) register_7 (
    .D(multiplexer_7_out), .en(not_1_out), .Q(MEMCONTROLout), .clk(CLK));  // open: clr
  Register #(.width(1), .trigger("rising"), .Select("low")) register_8 (
    .D(multiplexer_8_out), .en(not_1_out), .Q(REGWRITEout), .clk(CLK));  // open: clr
  Register #(.width(5), .trigger("rising"), .Select("low")) register_9 (
    .D(multiplexer_9_out), .en(not_1_out), .Q(W_out), .clk(CLK));  // open: clr
  Register #(.width(1), .trigger("rising"), .Select("low")) register_10 (
    .D(multiplexer_10_out), .en(not_1_out), .Q(JALout), .clk(CLK));  // open: clr
  Pull_Resistor #(.pull(0)) pull_resistor_2 (.node(not_1_out));
  Register #(.width(1), .trigger("rising"), .Select("low")) register_11 (
    .D(\使能端_低电平有效_stall_高电平有效 ), .Q(\使能传递端_低电平有效_stall_高电平有效 ), .clk(CLK));  // open: en, clr
endmodule

module MEM_WB (
  input  [31:0] PCin,
  input  [31:0] IRin,
  input  [31:0] ALUin,
  input  [31:0] MEMin,
  input  MEMTOREGin,
  input  REGWRITEin,
  input  [4:0] W_in,
  input  CLK,
  input  \同步清零_气泡_高电平有效 ,
  input  \使能端_低电平有效_stall_高电平有效 ,
  output [31:0] PCout,
  output [31:0] IRout,
  output [31:0] ALUout,
  output [31:0] MEMout,
  output MEMTOREGout,
  output REGWRITEout,
  output [4:0] W_out,
  output \使能传递端_低电平有效_stall_高电平有效 
);

  wire multiplexer_5_out, multiplexer_6_out, not_1_out;
  wire [4:0] multiplexer_7_out;
  wire [31:0] multiplexer_1_out, multiplexer_2_out, multiplexer_3_out, multiplexer_4_out;

  Multiplexer #(.select(1), .width(32), .disabled("Z"), .enable("false")) multiplexer_1 (
    .in0(PCin), .in1({32{1'b0}}), .out(multiplexer_1_out), .sel(\同步清零_气泡_高电平有效 ));
  Multiplexer #(.select(1), .width(32), .disabled("Z"), .enable("false")) multiplexer_2 (
    .in0(IRin), .in1({32{1'b0}}), .out(multiplexer_2_out), .sel(\同步清零_气泡_高电平有效 ));
  Multiplexer #(.select(1), .width(32), .disabled("Z"), .enable("false")) multiplexer_3 (
    .in0(ALUin), .in1({32{1'b0}}), .out(multiplexer_3_out), .sel(\同步清零_气泡_高电平有效 ));
  Multiplexer #(.select(1), .width(32), .disabled("Z"), .enable("false")) multiplexer_4 (
    .in0(MEMin), .in1({32{1'b0}}), .out(multiplexer_4_out), .sel(\同步清零_气泡_高电平有效 ));
  Multiplexer #(.select(1), .width(1), .disabled("Z"), .enable("false")) multiplexer_5 (
    .in0(MEMTOREGin), .in1(1'b0), .out(multiplexer_5_out), .sel(\同步清零_气泡_高电平有效 ));
  Multiplexer #(.select(1), .width(1), .disabled("Z"), .enable("false")) multiplexer_6 (
    .in0(REGWRITEin), .in1(1'b0), .out(multiplexer_6_out), .sel(\同步清零_气泡_高电平有效 ));
  Multiplexer #(.select(1), .width(5), .disabled("Z"), .enable("false")) multiplexer_7 (
    .in0(W_in), .in1({5{1'b0}}), .out(multiplexer_7_out), .sel(\同步清零_气泡_高电平有效 ));
  Pull_Resistor #(.pull(0)) pull_resistor_1 (.node(\同步清零_气泡_高电平有效 ));
  not not_1 (not_1_out, \使能端_低电平有效_stall_高电平有效 );
  Register #(.width(32), .trigger("rising"), .Select("low")) register_1 (
    .D(multiplexer_1_out), .en(not_1_out), .Q(PCout), .clk(CLK));  // open: clr
  Register #(.width(32), .trigger("rising"), .Select("low")) register_2 (
    .D(multiplexer_2_out), .en(not_1_out), .Q(IRout), .clk(CLK));  // open: clr
  Register #(.width(32), .trigger("rising"), .Select("low")) register_3 (
    .D(multiplexer_3_out), .en(not_1_out), .Q(ALUout), .clk(CLK));  // open: clr
  Register #(.width(32), .trigger("rising"), .Select("low")) register_4 (
    .D(multiplexer_4_out), .en(not_1_out), .Q(MEMout), .clk(CLK));  // open: clr
  Register #(.width(1), .trigger("rising"), .Select("low")) register_5 (
    .D(multiplexer_5_out), .en(not_1_out), .Q(MEMTOREGout), .clk(CLK));  // open: clr
  Register #(.width(1), .trigger("rising"), .Select("low")) register_6 (
    .D(multiplexer_6_out), .en(not_1_out), .Q(REGWRITEout), .clk(CLK));  // open: clr
  Register #(.width(5), .trigger("rising"), .Select("low")) register_7 (
    .D(multiplexer_7_out), .en(not_1_out), .Q(W_out), .clk(CLK));  // open: clr
  Pull_Resistor #(.pull(0)) pull_resistor_2 (.node(not_1_out));
  Register #(.width(1), .trigger("rising"), .Select("low")) register_8 (
    .D(\使能端_低电平有效_stall_高电平有效 ), .Q(\使能传递端_低电平有效_stall_高电平有效 ), .clk(CLK));  // open: en, clr
endmodule
module \源寄存器使用情况  (
  input  OP0,
  input  OP1,
  input  OP2,
  input  OP3,
  input  OP4,
  input  OP5,
  input  F0,
  input  F1,
  input  F2,
  input  F3,
  input  F4,
  input  F5,
  output R1_Used,
  output R2_Used
);

  wire and_1_out, and_2_out, and_3_out, and_4_out, and_5_out, and_6_out, and_7_out, and_8_out, and_9_out,
       and_10_out, and_11_out, and_12_out, and_13_out, and_14_out, not_1_out, not_2_out, not_3_out,
       not_4_out, not_5_out, not_6_out, not_7_out, not_8_out, not_9_out, not_10_out, not_11_out, not_12_out,
       not_13_out, not_14_out, not_15_out, not_16_out, not_17_out, not_18_out, not_19_out, not_20_out,
       not_21_out, not_22_out, not_23_out, not_24_out, not_25_out, not_26_out, not_27_out, not_28_out,
       not_29_out, not_30_out, not_31_out, not_32_out, not_33_out, not_34_out, not_35_out, not_36_out,
       not_37_out, not_38_out, not_39_out, not_40_out, not_41_out, not_42_out, not_43_out, not_44_out,
       not_45_out, not_46_out, not_47_out, not_48_out, not_49_out, not_50_out, not_51_out, not_52_out,
       not_53_out, not_54_out, not_55_out, not_56_out, not_57_out, not_58_out, not_59_out, not_60_out,
       not_61_out, not_62_out, not_63_out, not_64_out, not_65_out, not_66_out, not_67_out, not_68_out,
       not_69_out, not_70_out, not_71_out, not_72_out, not_73_out, not_74_out, not_75_out, not_76_out,
       not_77_out, not_78_out, not_79_out;

  not not_1 (not_1_out, OP0);
  not not_2 (not_2_out, OP1);
  not not_3 (not_3_out, OP4);
  not not_4 (not_4_out, OP5);
  not not_5 (not_5_out, F0);
  not not_6 (not_6_out, F1);
  not not_7 (not_7_out, F4);
  not not_8 (not_8_out, F5);
  not not_9 (not_9_out, OP0);
  not not_10 (not_10_out, OP1);
  not not_11 (not_11_out, OP4);
  not not_12 (not_12_out, OP5);
  not not_13 (not_13_out, F3);
  not not_14 (not_14_out, F4);
  not not_15 (not_15_out, OP0);
  not not_16 (not_16_out, OP1);
  not not_17 (not_17_out, OP4);
  not not_18 (not_18_out, OP5);
  not not_19 (not_19_out, F3);
  not not_20 (not_20_out, F4);
  not not_21 (not_21_out, OP0);
  not not_22 (not_22_out, OP1);
  not not_23 (not_23_out, OP4);
  not not_24 (not_24_out, OP5);
  not not_25 (not_25_out, F2);
  not not_26 (not_26_out, F4);
  not not_27 (not_27_out, OP0);
  not not_28 (not_28_out, OP4);
  not not_29 (not_29_out, OP5);
  not not_30 (not_30_out, OP2);
  not not_31 (not_31_out, OP4);
  not not_32 (not_32_out, OP5);
  not not_33 (not_33_out, OP1);
  not not_34 (not_34_out, OP4);
  not not_35 (not_35_out, OP5);
  not not_36 (not_36_out, OP2);
  not not_37 (not_37_out, OP4);
  not not_38 (not_38_out, OP0);
  not not_39 (not_39_out, OP1);
  not not_40 (not_40_out, OP3);
  not not_41 (not_41_out, OP4);
  not not_42 (not_42_out, OP5);
  not not_43 (not_43_out, F0);
  not not_44 (not_44_out, F3);
  not not_45 (not_45_out, F4);
  not not_46 (not_46_out, OP0);
  not not_47 (not_47_out, OP1);
  not not_48 (not_48_out, OP3);
  not not_49 (not_49_out, OP4);
  not not_50 (not_50_out, OP5);
  not not_51 (not_51_out, F3);
  not not_52 (not_52_out, F4);
  not not_53 (not_53_out, OP0);
  not not_54 (not_54_out, OP1);
  not not_55 (not_55_out, OP3);
  not not_56 (not_56_out, OP4);
  not not_57 (not_57_out, OP5);
  not not_58 (not_58_out, F0);
  not not_59 (not_59_out, F1);
  not not_60 (not_60_out, F4);
  not not_61 (not_61_out, F5);
  not not_62 (not_62_out, OP0);
  not not_63 (not_63_out, OP1);
  not not_64 (not_64_out, OP3);
  not not_65 (not_65_out, OP4);
  not not_66 (not_66_out, OP5);
  not not_67 (not_67_out, F3);
  not not_68 (not_68_out, F4);
  not not_69 (not_69_out, OP0);
  not not_70 (not_70_out, OP1);
  not not_71 (not_71_out, OP3);
  not not_72 (not_72_out, OP4);
  not not_73 (not_73_out, OP5);
  not not_74 (not_74_out, F2);
  not not_75 (not_75_out, F4);
  not not_76 (not_76_out, OP1);
  not not_77 (not_77_out, OP3);
  not not_78 (not_78_out, OP4);
  not not_79 (not_79_out, OP5);
  and and_1 (and_1_out, not_1_out, not_2_out, not_3_out, not_4_out, not_5_out, not_6_out, not_7_out, not_8_out);
  and and_2 (and_2_out, not_9_out, not_10_out, not_11_out, not_12_out, not_13_out, not_14_out, F5);
  and and_3 (and_3_out, not_15_out, not_16_out, not_17_out, not_18_out, F1, not_19_out, not_20_out);
  and and_4 (and_4_out, not_21_out, not_22_out, not_23_out, not_24_out, F1, not_25_out, not_26_out, F5);
  and and_5 (and_5_out, not_27_out, OP3, not_28_out, not_29_out);
  and and_6 (and_6_out, not_30_out, OP3, not_31_out, not_32_out);
  and and_7 (and_7_out, not_33_out, OP2, not_34_out, not_35_out);
  and and_8 (and_8_out, OP0, OP1, not_36_out, not_37_out, OP5);
  and and_9 (and_9_out, not_38_out, not_39_out, not_40_out, not_41_out, not_42_out, not_43_out, not_44_out, not_45_out);
  and and_10 (and_10_out, not_46_out, not_47_out, not_48_out, not_49_out, not_50_out, not_51_out, not_52_out, F5);
  and and_11 (and_11_out, not_53_out, not_54_out, not_55_out, not_56_out, not_57_out, not_58_out, not_59_out, F2, not_60_out, not_61_out);
  and and_12 (and_12_out, not_62_out, not_63_out, not_64_out, not_65_out, not_66_out, F1, not_67_out, not_68_out);
  and and_13 (and_13_out, not_69_out, not_70_out, not_71_out, not_72_out, not_73_out, F1, not_74_out, not_75_out, F5);
  and and_14 (and_14_out, not_76_out, OP2, not_77_out, not_78_out, not_79_out);
  or or_1 (R1_Used, and_1_out, and_2_out, and_3_out, and_4_out, and_5_out, and_6_out, and_7_out, and_8_out);
  or or_2 (R2_Used, and_9_out, and_10_out, and_11_out, and_12_out, and_13_out, and_14_out);
endmodule

module \数据相关检测  (
  input  EX_RegWrite,
  input  [4:0] EX_WriteReg_num,
  input  MEM_RegWrite,
  input  [4:0] MEM_WriteReg_num,
  input  R1_Used,
  input  [4:0] R1_num,
  input  R2_Used,
  input  [4:0] R2_num,
  input  Ex_MemToReg,
  output Collision,
  output EX_Collision_R1,
  output MEM_Collision_R1,
  output LoadUse,
  output EX_Collision_R2,
  output MEM_Collision_R2
);

  wire comparator_1_eq, comparator_2_eq, comparator_3_eq, comparator_4_eq, comparator_5_eq, comparator_6_eq,
       or_1_out;

  and and_1 (LoadUse, Ex_MemToReg, or_1_out);
  Comparator #(.width(5), .mode("unsigned")) comparator_1 (
    .a(R1_num), .b({5{1'b0}}), .eq(comparator_1_eq));  // open: gt, lt
  Comparator #(.width(5), .mode("unsigned")) comparator_2 (
    .a(R1_num), .b(EX_WriteReg_num), .eq(comparator_2_eq));  // open: gt, lt
  Comparator #(.width(5), .mode("unsigned")) comparator_3 (
    .a(R2_num), .b({5{1'b0}}), .eq(comparator_3_eq));  // open: gt, lt
  Comparator #(.width(5), .mode("unsigned")) comparator_4 (
    .a(R2_num), .b(EX_WriteReg_num), .eq(comparator_4_eq));  // open: gt, lt
  or or_1 (or_1_out, EX_Collision_R1, EX_Collision_R2);
  and and_2 (EX_Collision_R1, comparator_2_eq, ~comparator_1_eq, R1_Used, EX_RegWrite);  // AND_Gate
  and and_3 (EX_Collision_R2, comparator_4_eq, ~comparator_3_eq, R2_Used, EX_RegWrite);  // AND_Gate
  Comparator #(.width(5), .mode("unsigned")) comparator_5 (
    .a(R1_num), .b(MEM_WriteReg_num), .eq(comparator_5_eq));  // open: gt, lt
  Comparator #(.width(5), .mode("unsigned")) comparator_6 (
    .a(R2_num), .b(MEM_WriteReg_num), .eq(comparator_6_eq));  // open: gt, lt
  and and_4 (MEM_Collision_R2, comparator_6_eq, ~comparator_3_eq, R2_Used, MEM_RegWrite);  // AND_Gate
  and and_5 (MEM_Collision_R1, comparator_5_eq, ~comparator_1_eq, R1_Used, MEM_RegWrite);  // AND_Gate
  or or_2 (Collision, MEM_Collision_R1, MEM_Collision_R2, EX_Collision_R1, EX_Collision_R2);
endmodule
