// Logisim project dhb-cpu24_submit_3309id气泡.circ as structural Verilog: 26 circuits, main circuit ◇单周期MIPS
module \单周期MIPS  (
  input  IR1,
  input  IR2,
  input  IR3,
  output RegWrite,
  output MemWrite,
  output [31:0] PC,
  output [31:0] IR,
  output [31:0] RDin,
  output [31:0] MDin,
  output [31:0] LedData
);

  wire A, and_1_out, B, Branch, C, CLK, comparator_1_eq, Go, halt, IR1_t, IR2_t, IR3_t, IRC,
       mips_ram_adapter_1_clk_2, mips_ram_adapter_1_str, nand_1_out, nand_2_out, or_3_out, SignedExt,
       Syscall, \单周期硬布线控制器_1_alu_src , \单周期硬布线控制器_1_jal , \单周期硬布线控制器_1_jmp , \单周期硬布线控制器_1_jr ,
       \单周期硬布线控制器_1_memtoreg , \单周期硬布线控制器_1_regdst ;
  wire [1:0] C0Reg, or_2_out, \中断电路_1_a ;
  wire [2:0] \单周期硬布线控制器_1_memcontrol ;
  wire [3:0] W;
  wire [3:3] IRS;
  wire [4:0] multiplexer_3_out, multiplexer_4_out, multiplexer_6_out, multiplexer_7_out, multiplexer_8_out;
  wire [6:0] \单周期硬布线控制器_1_alu_op ;
  wire [9:0] mips_ram_adapter_1_a;
  wire [15:0] \总周期数 ;
  wire [31:0] adder_1_out, adder_2_out, bit_extender_1_out, bit_extender_2_out, EPC, IRPC, mips_alu_1_result,
       mips_ram_adapter_1_dataout, mips_ram_adapter_1_din, multiplexer_2_out, multiplexer_9_out,
       multiplexer_10_out, multiplexer_11_out, ram_1_data, shifter_1_out, Status, v0;

  Clock #(.highDuration(1), .lowDuration(1)) clock_1 (.out(CLK));
  Button _1 (.out(A));
  Button _2 (.out(B));
  Button _3 (.out(C));
  Button \u_继续运行  (.out(Go));
  LED #(.active("true")) led_1 (.in(W[0]));
  LED #(.active("true")) led_2 (.in(W[1]));
  LED #(.active("true")) led_3 (.in(W[2]));
  Multiplexer #(.select(2), .width(32), .disabled("Z"), .enable("false")) multiplexer_1 (
    .in0(adder_1_out), .in1(multiplexer_11_out), .in2(adder_2_out), .in3({PC[31:28], IR[25:0], 2'b00}),
    .out(EPC), .sel(or_2_out));
  nand nand_1 (nand_1_out, ~IRC, halt);  // NAND_Gate
  Hex_Digit_Display hex_digit_display_1 (.value(LedData[31:28]));  // open: dp
  // Mips_Probe mips_probe_1: pin names not known; wires that end beside it: IR
  Multiplexer #(.select(1), .width(32), .disabled("Z"), .enable("false")) multiplexer_2 (
    .in0(EPC), .in1(IRPC), .out(multiplexer_2_out), .sel(IRC));
  Register #(.width(32), .trigger("rising"), .Select("low")) u_PC (
    .D(multiplexer_2_out), .en(nand_2_out), .Q(PC), .clk(CLK));  // open: clr
  nand nand_2 (nand_2_out, ~IRC, halt);  // NAND_Gate
  Counter #(.width(16), .max('hffff), .ongoal("stay"), .trigger("rising"), .behavior("old")) \u_总周期数  (
    .count(nand_1_out), .Q(\总周期数 ), .clk(CLK));  // open: load, D, carry, clr, preset
  Hex_Digit_Display hex_digit_display_2 (.value(LedData[27:24]));  // open: dp
  Hex_Digit_Display hex_digit_display_3 (.value(LedData[23:20]));  // open: dp
  or or_1 (or_2_out[1], Branch, or_3_out);
  or or_2 (or_2_out[0], \单周期硬布线控制器_1_jr , or_3_out);
  Hex_Digit_Display hex_digit_display_4 (.value(LedData[19:16]));  // open: dp
  Hex_Digit_Display hex_digit_display_5 (.value(LedData[15:12]));  // open: dp
  or or_3 (or_3_out, \单周期硬布线控制器_1_jmp , \单周期硬布线控制器_1_jal );
  Adder #(.width(32)) adder_1 (.a(PC), .b(32'h4), .out(adder_1_out));  // open: cin, cout
  Hex_Digit_Display hex_digit_display_6 (.value(LedData[11:8]));  // open: dp
  Hex_Digit_Display hex_digit_display_7 (.value(LedData[7:4]));  // open: dp
  // Probe on \总周期数 
  ROM #(.addrWidth(10), .dataWidth(32), .Select("high")) rom_1 (.addr(PC[11:2]), .data(IR));
  Adder #(.width(32)) adder_2 (.a(adder_1_out), .b(shifter_1_out), .out(adder_2_out));  // open: cin, cout
  Comparator #(.width(32), .mode("unsigned")) comparator_1 (.a(v0), .b(32'ha), .eq(comparator_1_eq));  // open: gt, lt
  and and_1 (and_1_out, ~comparator_1_eq, Syscall);  // AND_Gate
  Hex_Digit_Display hex_digit_display_8 (.value(LedData[3:0]));  // open: dp
  Register #(.width(32), .trigger("rising"), .Select("low")) register_1 (
    .D(MDin), .en(and_1_out), .Q(LedData), .clk(CLK));  // open: clr
  Multiplexer #(.select(1), .width(5), .disabled("Z"), .enable("false")) multiplexer_3 (
    .in0(IR[15:11]), .in1(IR[20:16]), .out(multiplexer_3_out), .sel(\单周期硬布线控制器_1_regdst ));
  Multiplexer #(.select(1), .width(5), .disabled("Z"), .enable("false")) multiplexer_4 (
    .in0(IR[20:16]), .in1(IR[15:11]), .out(multiplexer_4_out), .sel(\单周期硬布线控制器_1_regdst ));
  Multiplexer #(.select(1), .width(32), .disabled("Z"), .enable("false")) multiplexer_5 (
    .in0(multiplexer_11_out), .in1(adder_1_out), .out(RDin), .sel(\单周期硬布线控制器_1_jal ));
  assign bit_extender_1_out = {{16{1'b0}}, IR[15:0]};  // Bit_Extender bit_extender_1
  assign bit_extender_2_out = {{16{IR[15]}}, IR[15:0]};  // Bit_Extender bit_extender_2
  and and_2 (halt, comparator_1_eq, Syscall);
  or or_4 (IR1_t, IR1, A);
  \单周期硬布线控制器  \u_单周期硬布线控制器_1  (
    .IR(IR), .ALU_OP(\单周期硬布线控制器_1_alu_op ), .MemToReg(\单周期硬布线控制器_1_memtoreg ),
    .MemControl({MemWrite, \单周期硬布线控制器_1_memcontrol }), .ALU_SRC(\单周期硬布线控制器_1_alu_src ), .RegWrite(RegWrite),
    .SysCALL(Syscall), .SignedExt(SignedExt), .RegDst(\单周期硬布线控制器_1_regdst ), .JR(\单周期硬布线控制器_1_jr ),
    .JMP(\单周期硬布线控制器_1_jmp ), .JAL(\单周期硬布线控制器_1_jal ), .C0Reg(C0Reg));  // open: R1_Used, R2_Used
  Multiplexer #(.select(1), .width(5), .disabled("Z"), .enable("false")) multiplexer_6 (
    .in0(IR[25:21]), .in1(5'b00010), .out(multiplexer_6_out), .sel(Syscall));
  Multiplexer #(.select(1), .width(5), .disabled("Z"), .enable("false")) multiplexer_7 (
    .in0(multiplexer_3_out), .in1(5'b00100), .out(multiplexer_7_out), .sel(Syscall));
  Multiplexer #(.select(1), .width(5), .disabled("Z"), .enable("false")) multiplexer_8 (
    .in0(multiplexer_4_out), .in1({5{1'b1}}), .out(multiplexer_8_out), .sel(\单周期硬布线控制器_1_jal ));
  or or_5 (IR2_t, IR2, B);
  Multiplexer #(.select(1), .width(32), .disabled("Z"), .enable("false")) multiplexer_9 (
    .in0(bit_extender_1_out), .in1(bit_extender_2_out), .out(multiplexer_9_out), .sel(SignedExt));
  MIPS_Regifile mips_regifile_1 (
    .Din(RDin), .Clk(CLK), .R1(v0), .R2(MDin), .WE(RegWrite), .W_num(multiplexer_8_out),
    .R1_num(multiplexer_6_out), .R2_num(multiplexer_7_out), .C0Reg(C0Reg), .Status(Status), .EPC(EPC),
    .IR(IRC));
  \中断电路  \u_中断电路_1  (
    .CLK(CLK), .IRout(IRC), .A(\中断电路_1_a ), .IRin({IRS[3], IR3_t, IR2_t, IR1_t}), .Status(Status), .W(W));
  or or_6 (IR3_t, IR3, C);
  Multiplexer #(.select(1), .width(32), .disabled("Z"), .enable("false")) multiplexer_10 (
    .in0(MDin), .in1(multiplexer_9_out), .out(multiplexer_10_out), .sel(\单周期硬布线控制器_1_alu_src ));
  Shifter #(.width(32), .shift("ll")) shifter_1 (.in(multiplexer_9_out), .\dist (5'b00010), .out(shifter_1_out));
  MIPS_ALU mips_alu_1 (
    .X(v0), .Y(multiplexer_10_out), .AluOP(\单周期硬布线控制器_1_alu_op ), .Branch(Branch),
    .Result(mips_alu_1_result), .shamt(IR[10:6]));  // open: Result_2
  ROM #(.addrWidth(2), .dataWidth(32), .Select("low")) rom_2 (.addr(\中断电路_1_a ), .data(IRPC));
  MIPS_Ram_Adapter mips_ram_adapter_1 (
    .Addr(mips_alu_1_result), .DataIn(MDin), .dout(ram_1_data), .CLK(CLK),
    .CONTROL({MemWrite, \单周期硬布线控制器_1_memcontrol }), .A(mips_ram_adapter_1_a), .din(mips_ram_adapter_1_din),
    .DataOut(mips_ram_adapter_1_dataout), .clk_2(mips_ram_adapter_1_clk_2), .str(mips_ram_adapter_1_str));
  RAM #(.addrWidth(10), .dataWidth(32), .bus("separate"), .Select("high")) ram_1 (
    .addr(mips_ram_adapter_1_a), .din(mips_ram_adapter_1_din), .data(ram_1_data),
    .str(mips_ram_adapter_1_str), .clk(mips_ram_adapter_1_clk_2));  // open: sel, ld, clr
  Multiplexer #(.select(1), .width(32), .disabled("Z"), .enable("false")) multiplexer_11 (
    .in0(mips_alu_1_result), .in1(mips_ram_adapter_1_dataout), .out(multiplexer_11_out),
    .sel(\单周期硬布线控制器_1_memtoreg ));

  // Other names for the same wires on the sheet: a0[31:0] = MDin; IRS[2:0] = {IR3_t, IR2_t, IR1_t}

  // Notes on the sheet:
  //   中断源
  //   PC+4
  //   JR
  //   J/JAL
  //   PC计数器
  //   中断等待指示
  //   总复位信号应将除ROM以外所有存储组件全部清零
  //   BEQ/BNE
  //   数码管输出
  //   指令存储器
  //   PC+4
  //   Syscall功能实现
  //   数码管输出应该用寄存器锁存，否则显示数据只能一闪而过
  //   指令字
  //   contents of rom_1 (hex, n*v repeats v):
  //   8000c53 afbf0000 401f7000 afbffffc c000c40 40896000 24110100 24020022 112021 c 20010001 2218822
  //   1620fffb 40806000 c000c4a 8fbffffc 409f7000 8fbf0000 40896000 42000018 afbf0000 401f7000 afbffffc
  //   c000c40 3409fe01 40896000 24110001 24020022 112021 c 0 118840 1620fffb 40806000 c000c4a 8fbffffc
  //   409f7000 8fbf0000 40896000 42000018 afbf0000 401f7000 afbffffc c000c40 3409f801 40896000 20090003
  //   20080001 20100003 108100 2098825 112020 20020022 c 1600fffa 1284822 1520fff7 40806000 c000c4a
  //   8fbffffc 409f7000 8fbf0000 40896000 42000018 afa1fff8 afa2fff4 afa4ffec afa8ffdc afa9ffd8 afb0ffbc
  //   afb1ffb8 2001004c 3a1e822 3e00008 23bd004c 8fa1fff8 8fa2fff4 8fa4ffec 8fa8ffdc 8fa9ffd8 8fb0ffbc
  //   8fb1ffb8 3e00008 341dfffc 3409ff01 40896000 24111234 112021 24020022 c 2402000a c 8000c58
  //   addr
  //   JMP
  //   JR
  //   IR
  //   rs
  //   rt
  //   rd
  //   imm
  //   shamt
  //   MemToReg
  //   MemControl
  //   AluOP
  //   AluSrcB
  //   RegWrite
  //   JAL
  //   RegDst
  //   Syscall
  //   中断相关实现
  //   contents of rom_2 (hex, n*v repeats v):
  //   4 50 a0
  //   为方便自动评测，需要输出PC，IR，寄存器堆写如数据RDin
  //   RAM写使能MemWrite、RAM写入数据MDin等信号
endmodule

// 单周期硬布线控制器
module \单周期硬布线控制器  (
  input  [31:0] IR,
  output [6:0] ALU_OP,
  output MemToReg,
  output [3:0] MemControl,
  output ALU_SRC,
  output RegWrite,
  output SysCALL,
  output SignedExt,
  output RegDst,
  output JR,
  output JMP,
  output JAL,
  output [1:0] C0Reg,
  output R1_Used,
  output R2_Used
);

  \运算控制器自动生成  \u_运算控制器自动生成_1  (
    .OP0(IR[26]), .OP1(IR[27]), .OP2(IR[28]), .OP3(IR[29]), .OP4(IR[30]), .OP5(IR[31]), .F0(IR[0]),
    .F1(IR[1]), .F2(IR[2]), .F3(IR[3]), .F4(IR[4]), .F5(IR[5]), .RT0(IR[16]), .S0(ALU_OP[0]), .S1(ALU_OP[1]),
    .S2(ALU_OP[2]), .S3(ALU_OP[3]), .B0(ALU_OP[4]), .B1(ALU_OP[5]), .B2(ALU_OP[6]));
  \控制信号自动生成  \u_控制信号自动生成_1  (
    .OP0(IR[26]), .OP1(IR[27]), .MemToReg(MemToReg), .OP2(IR[28]), .OP3(IR[29]), .OP4(IR[30]), .OP5(IR[31]),
    .MemWrite(MemControl[3]), .F0(IR[0]), .F1(IR[1]), .F2(IR[2]), .F3(IR[3]), .MemHalf(MemControl[2]),
    .F4(IR[4]), .F5(IR[5]), .RS2(IR[23]), .RS4(IR[25]), .MemByte(MemControl[1]), .MemUnsigned(MemControl[0]),
    .ALU_SRC(ALU_SRC), .RegWrite(RegWrite), .SysCALL(SysCALL), .SignedExt(SignedExt), .RegDst(RegDst),
    .JR(JR), .JUMP(JMP), .JAL(JAL), .C0Reg0(C0Reg[0]), .C0Reg1(C0Reg[1]));
  \源寄存器使用情况  \u_源寄存器使用情况_1  (
    .OP0(IR[26]), .OP1(IR[27]), .OP2(IR[28]), .OP3(IR[29]), .OP4(IR[30]), .OP5(IR[31]), .F0(IR[0]),
    .F1(IR[1]), .F2(IR[2]), .F3(IR[3]), .F4(IR[4]), .F5(IR[5]), .RS2(IR[23]), .RS4(IR[25]),
    .R1_Used(R1_Used), .R2_Used(R2_Used));

  // Notes on the sheet:
  //   OP
  //   rt
  //   Func
  //   rs
  //   rs
  //   运算器控制器，根据指令生成运算器功能选择信号
  //   控制信号生成，产生数据通路需要的其他控制信号
endmodule

// 运算器控制器
module \运算控制器自动生成  (
  input  OP0,
  input  OP1,
  input  OP2,
  input  OP3,
  input  OP4,
  input  OP5,
  input  F0,
  input  F1,
  input  F2,
  input  F3,
  input  F4,
  input  F5,
  input  RT0,
  output S0,
  output S1,
  output S2,
  output S3,
  output B0,
  output B1,
  output B2
);

  wire and_1_out, and_2_out, and_3_out, and_4_out, and_5_out, and_6_out, and_7_out, and_8_out, and_9_out,
       and_10_out, and_11_out, and_12_out, and_13_out, and_14_out, and_15_out, and_16_out, and_17_out,
       and_18_out, and_19_out, and_20_out, and_21_out, and_22_out, and_23_out, and_24_out, and_25_out,
       and_26_out, and_27_out, and_28_out, and_29_out, and_30_out, and_31_out, and_32_out, and_33_out,
       and_34_out, and_35_out, and_36_out, and_37_out, and_38_out, and_39_out, and_40_out, and_41_out,
       and_42_out, and_43_out, and_44_out, not_1_out, not_2_out, not_3_out, not_4_out, not_5_out, not_6_out,
       not_7_out, not_8_out, not_9_out, not_10_out, not_11_out, not_12_out, not_13_out, not_14_out,
       not_15_out, not_16_out, not_17_out, not_18_out, not_19_out, not_20_out, not_21_out, not_22_out,
       not_23_out, not_24_out, not_25_out, not_26_out, not_27_out, not_28_out, not_29_out, not_30_out,
       not_31_out, not_32_out, not_33_out, not_34_out, not_35_out, not_36_out, not_37_out, not_38_out,
       not_39_out, not_40_out, not_41_out, not_42_out, not_43_out, not_44_out, not_45_out, not_46_out,
       not_47_out, not_48_out, not_49_out, not_50_out, not_51_out, not_52_out, not_53_out, not_54_out,
       not_55_out, not_56_out, not_57_out, not_58_out, not_59_out, not_60_out, not_61_out, not_62_out,
       not_63_out, not_64_out, not_65_out, not_66_out, not_67_out, not_68_out, not_69_out, not_70_out,
       not_71_out, not_72_out, not_73_out, not_74_out, not_75_out, not_76_out, not_77_out, not_78_out,
       not_79_out, not_80_out, not_81_out, not_82_out, not_83_out, not_84_out, not_85_out, not_86_out,
       not_87_out, not_88_out, not_89_out, not_90_out, not_91_out, not_92_out, not_93_out, not_94_out,
       not_95_out, not_96_out, not_97_out, not_98_out, not_99_out, not_100_out, not_101_out, not_102_out,
       not_103_out, not_104_out, not_105_out, not_106_out, not_107_out, not_108_out, not_109_out,
       not_110_out, not_111_out, not_112_out, not_113_out, not_114_out, not_115_out, not_116_out,
       not_117_out, not_118_out, not_119_out, not_120_out, not_121_out, not_122_out, not_123_out,
       not_124_out, not_125_out, not_126_out, not_127_out, not_128_out, not_129_out, not_130_out,
       not_131_out, not_132_out, not_133_out, not_134_out, not_135_out, not_136_out, not_137_out,
       not_138_out, not_139_out, not_140_out, not_141_out, not_142_out, not_143_out, not_144_out,
       not_145_out, not_146_out, not_147_out, not_148_out, not_149_out, not_150_out, not_151_out,
       not_152_out, not_153_out, not_154_out, not_155_out, not_156_out, not_157_out, not_158_out,
       not_159_out, not_160_out, not_161_out, not_162_out, not_163_out, not_164_out, not_165_out,
       not_166_out, not_167_out, not_168_out, not_169_out, not_170_out, not_171_out, not_172_out,
       not_173_out, not_174_out, not_175_out, not_176_out, not_177_out, not_178_out, not_179_out,
       not_180_out, not_181_out, not_182_out, not_183_out, not_184_out, not_185_out, not_186_out,
       not_187_out, not_188_out, not_189_out, not_190_out, not_191_out, not_192_out, not_193_out,
       not_194_out, not_195_out, not_196_out, not_197_out, not_198_out, not_199_out, not_200_out,
       not_201_out, not_202_out, not_203_out, not_204_out, not_205_out, not_206_out, not_207_out,
       not_208_out, not_209_out, not_210_out, not_211_out, not_212_out, not_213_out, not_214_out,
       not_215_out, not_216_out, not_217_out, not_218_out, not_219_out, not_220_out, not_221_out,
       not_222_out, not_223_out, not_224_out, not_225_out, not_226_out, not_227_out, not_228_out,
       not_229_out, not_230_out, not_231_out, not_232_out, not_233_out, not_234_out, not_235_out,
       not_236_out, not_237_out, not_238_out, not_239_out, not_240_out, not_241_out, not_242_out,
       not_243_out, not_244_out, not_245_out, not_246_out, not_247_out, not_248_out, not_249_out,
       not_250_out, not_251_out, not_252_out, not_253_out, not_254_out, not_255_out, not_256_out;

  not not_1 (not_1_out, OP0);
  not not_2 (not_2_out, OP1);
  not not_3 (not_3_out, OP2);
  not not_4 (not_4_out, OP4);
  not not_5 (not_5_out, F1);
  not not_6 (not_6_out, F2);
  not not_7 (not_7_out, F3);
  not not_8 (not_8_out, F4);
  not not_9 (not_9_out, OP0);
  not not_10 (not_10_out, OP1);
  not not_11 (not_11_out, OP2);
  not not_12 (not_12_out, OP4);
  not not_13 (not_13_out, F0);
  not not_14 (not_14_out, F3);
  not not_15 (not_15_out, F4);
  not not_16 (not_16_out, OP0);
  not not_17 (not_17_out, OP1);
  not not_18 (not_18_out, OP2);
  not not_19 (not_19_out, OP4);
  not not_20 (not_20_out, F0);
  not not_21 (not_21_out, F2);
  not not_22 (not_22_out, F4);
  not not_23 (not_23_out, OP0);
  not not_24 (not_24_out, OP1);
  not not_25 (not_25_out, OP2);
  not not_26 (not_26_out, OP4);
  not not_27 (not_27_out, F2);
  not not_28 (not_28_out, F3);
  not not_29 (not_29_out, F4);
  not not_30 (not_30_out, F5);
  not not_31 (not_31_out, OP1);
  not not_32 (not_32_out, OP3);
  not not_33 (not_33_out, OP4);
  not not_34 (not_34_out, OP0);
  not not_35 (not_35_out, OP1);
  not not_36 (not_36_out, OP2);
  not not_37 (not_37_out, OP3);
  not not_38 (not_38_out, OP5);
  not not_39 (not_39_out, OP0);
  not not_40 (not_40_out, OP4);
  not not_41 (not_41_out, OP5);
  not not_42 (not_42_out, OP1);
  not not_43 (not_43_out, OP2);
  not not_44 (not_44_out, OP4);
  not not_45 (not_45_out, OP2);
  not not_46 (not_46_out, OP4);
  not not_47 (not_47_out, OP0);
  not not_48 (not_48_out, OP1);
  not not_49 (not_49_out, OP2);
  not not_50 (not_50_out, OP3);
  not not_51 (not_51_out, OP4);
  not not_52 (not_52_out, OP5);
  not not_53 (not_53_out, F0);
  not not_54 (not_54_out, F1);
  not not_55 (not_55_out, F3);
  not not_56 (not_56_out, F4);
  not not_57 (not_57_out, OP0);
  not not_58 (not_58_out, OP1);
  not not_59 (not_59_out, OP2);
  not not_60 (not_60_out, OP3);
  not not_61 (not_61_out, OP4);
  not not_62 (not_62_out, OP5);
  not not_63 (not_63_out, F0);
  not not_64 (not_64_out, F1);
  not not_65 (not_65_out, F4);
  not not_66 (not_66_out, F5);
  not not_67 (not_67_out, OP0);
  not not_68 (not_68_out, OP1);
  not not_69 (not_69_out, OP2);
  not not_70 (not_70_out, OP3);
  not not_71 (not_71_out, OP4);
  not not_72 (not_72_out, OP5);
  not not_73 (not_73_out, F0);
  not not_74 (not_74_out, F3);
  not not_75 (not_75_out, F4);
  not not_76 (not_76_out, F5);
  not not_77 (not_77_out, OP0);
  not not_78 (not_78_out, OP1);
  not not_79 (not_79_out, OP2);
  not not_80 (not_80_out, OP3);
  not not_81 (not_81_out, OP4);
  not not_82 (not_82_out, OP5);
  not not_83 (not_83_out, F0);
  not not_84 (not_84_out, F2);
  not not_85 (not_85_out, F4);
  not not_86 (not_86_out, OP0);
  not not_87 (not_87_out, OP1);
  not not_88 (not_88_out, OP2);
  not not_89 (not_89_out, OP3);
  not not_90 (not_90_out, OP4);
  not not_91 (not_91_out, OP5);
  not not_92 (not_92_out, F2);
  not not_93 (not_93_out, F3);
  not not_94 (not_94_out, F4);
  not not_95 (not_95_out, OP0);
  not not_96 (not_96_out, OP1);
  not not_97 (not_97_out, OP2);
  not not_98 (not_98_out, OP3);
  not not_99 (not_99_out, OP4);
  not not_100 (not_100_out, OP5);
  not not_101 (not_101_out, F3);
  not not_102 (not_102_out, F4);
  not not_103 (not_103_out, OP0);
  not not_104 (not_104_out, OP1);
  not not_105 (not_105_out, OP4);
  not not_106 (not_106_out, OP5);
  not not_107 (not_107_out, OP0);
  not not_108 (not_108_out, OP2);
  not not_109 (not_109_out, OP4);
  not not_110 (not_110_out, OP5);
  not not_111 (not_111_out, OP0);
  not not_112 (not_112_out, OP1);
  not not_113 (not_113_out, OP2);
  not not_114 (not_114_out, OP4);
  not not_115 (not_115_out, F2);
  not not_116 (not_116_out, F3);
  not not_117 (not_117_out, F4);
  not not_118 (not_118_out, OP0);
  not not_119 (not_119_out, OP1);
  not not_120 (not_120_out, OP2);
  not not_121 (not_121_out, OP4);
  not not_122 (not_122_out, F0);
  not not_123 (not_123_out, F1);
  not not_124 (not_124_out, F3);
  not not_125 (not_125_out, F4);
  not not_126 (not_126_out, OP0);
  not not_127 (not_127_out, OP1);
  not not_128 (not_128_out, OP2);
  not not_129 (not_129_out, OP4);
  not not_130 (not_130_out, F0);
  not not_131 (not_131_out, F1);
  not not_132 (not_132_out, F4);
  not not_133 (not_133_out, F5);
  not not_134 (not_134_out, OP0);
  not not_135 (not_135_out, OP1);
  not not_136 (not_136_out, OP2);
  not not_137 (not_137_out, OP4);
  not not_138 (not_138_out, F0);
  not not_139 (not_139_out, F3);
  not not_140 (not_140_out, F4);
  not not_141 (not_141_out, F5);
  not not_142 (not_142_out, OP0);
  not not_143 (not_143_out, OP1);
  not not_144 (not_144_out, OP2);
  not not_145 (not_145_out, OP4);
  not not_146 (not_146_out, F3);
  not not_147 (not_147_out, F4);
  not not_148 (not_148_out, F5);
  not not_149 (not_149_out, OP0);
  not not_150 (not_150_out, OP1);
  not not_151 (not_151_out, OP2);
  not not_152 (not_152_out, OP4);
  not not_153 (not_153_out, F2);
  not not_154 (not_154_out, F4);
  not not_155 (not_155_out, OP1);
  not not_156 (not_156_out, OP2);
  not not_157 (not_157_out, OP4);
  not not_158 (not_158_out, OP1);
  not not_159 (not_159_out, OP3);
  not not_160 (not_160_out, OP4);
  not not_161 (not_161_out, OP0);
  not not_162 (not_162_out, OP1);
  not not_163 (not_163_out, OP2);
  not not_164 (not_164_out, OP3);
  not not_165 (not_165_out, OP5);
  not not_166 (not_166_out, OP0);
  not not_167 (not_167_out, OP1);
  not not_168 (not_168_out, OP4);
  not not_169 (not_169_out, OP5);
  not not_170 (not_170_out, OP2);
  not not_171 (not_171_out, OP4);
  not not_172 (not_172_out, OP2);
  not not_173 (not_173_out, OP4);
  not not_174 (not_174_out, OP0);
  not not_175 (not_175_out, OP1);
  not not_176 (not_176_out, OP2);
  not not_177 (not_177_out, OP3);
  not not_178 (not_178_out, OP4);
  not not_179 (not_179_out, OP5);
  not not_180 (not_180_out, F0);
  not not_181 (not_181_out, F1);
  not not_182 (not_182_out, F2);
  not not_183 (not_183_out, F4);
  not not_184 (not_184_out, F5);
  not not_185 (not_185_out, OP0);
  not not_186 (not_186_out, OP1);
  not not_187 (not_187_out, OP2);
  not not_188 (not_188_out, OP3);
  not not_189 (not_189_out, OP4);
  not not_190 (not_190_out, OP5);
  not not_191 (not_191_out, F0);
  not not_192 (not_192_out, F3);
  not not_193 (not_193_out, F4);
  not not_194 (not_194_out, F5);
  not not_195 (not_195_out, OP0);
  not not_196 (not_196_out, OP1);
  not not_197 (not_197_out, OP2);
  not not_198 (not_198_out, OP3);
  not not_199 (not_199_out, OP4);
  not not_200 (not_200_out, OP5);
  not not_201 (not_201_out, F2);
  not not_202 (not_202_out, F4);
  not not_203 (not_203_out, OP0);
  not not_204 (not_204_out, OP1);
  not not_205 (not_205_out, OP2);
  not not_206 (not_206_out, OP3);
  not not_207 (not_207_out, OP4);
  not not_208 (not_208_out, OP5);
  not not_209 (not_209_out, F3);
  not not_210 (not_210_out, F4);
  not not_211 (not_211_out, OP0);
  not not_212 (not_212_out, OP1);
  not not_213 (not_213_out, OP2);
  not not_214 (not_214_out, OP3);
  not not_215 (not_215_out, OP4);
  not not_216 (not_216_out, OP5);
  not not_217 (not_217_out, F3);
  not not_218 (not_218_out, F4);
  not not_219 (not_219_out, OP0);
  not not_220 (not_220_out, OP4);
  not not_221 (not_221_out, OP5);
  not not_222 (not_222_out, OP2);
  not not_223 (not_223_out, OP4);
  not not_224 (not_224_out, OP5);
  not not_225 (not_225_out, OP1);
  not not_226 (not_226_out, OP4);
  not not_227 (not_227_out, OP5);
  not not_228 (not_228_out, OP0);
  not not_229 (not_229_out, OP1);
  not not_230 (not_230_out, OP3);
  not not_231 (not_231_out, OP4);
  not not_232 (not_232_out, OP5);
  not not_233 (not_233_out, OP1);
  not not_234 (not_234_out, OP2);
  not not_235 (not_235_out, OP3);
  not not_236 (not_236_out, OP4);
  not not_237 (not_237_out, OP5);
  not not_238 (not_238_out, OP3);
  not not_239 (not_239_out, OP4);
  not not_240 (not_240_out, OP5);
  not not_241 (not_241_out, OP1);
  not not_242 (not_242_out, OP3);
  not not_243 (not_243_out, OP4);
  not not_244 (not_244_out, OP5);
  not not_245 (not_245_out, RT0);
  not not_246 (not_246_out, OP3);
  not not_247 (not_247_out, OP4);
  not not_248 (not_248_out, OP5);
  not not_249 (not_249_out, OP3);
  not not_250 (not_250_out, OP4);
  not not_251 (not_251_out, OP5);
  not not_252 (not_252_out, OP1);
  not not_253 (not_253_out, OP2);
  not not_254 (not_254_out, OP3);
  not not_255 (not_255_out, OP4);
  not not_256 (not_256_out, OP5);
  and and_1 (and_1_out, not_1_out, not_2_out, not_3_out, not_4_out, not_5_out, not_6_out, not_7_out, not_8_out, F5);
  and and_2 (and_2_out, not_9_out, not_10_out, not_11_out, not_12_out, not_13_out, F2, not_14_out, not_15_out);
  and and_3 (and_3_out, not_16_out, not_17_out, not_18_out, not_19_out, not_20_out, F1, not_21_out, F3, not_22_out, F5);
  and and_4 (and_4_out, not_23_out, not_24_out, not_25_out, not_26_out, F0, F1, not_27_out, not_28_out, not_29_out, not_30_out);
  and and_5 (and_5_out, not_31_out, not_32_out, not_33_out, OP5);
  and and_6 (and_6_out, not_34_out, not_35_out, not_36_out, not_37_out, OP4, not_38_out);
  and and_7 (and_7_out, not_39_out, OP3, not_40_out, not_41_out);
  and and_8 (and_8_out, not_42_out, not_43_out, OP3, not_44_out);
  and and_9 (and_9_out, OP0, not_45_out, not_46_out, OP5);
  and and_10 (and_10_out, not_47_out, not_48_out, not_49_out, not_50_out, not_51_out, not_52_out, not_53_out, not_54_out, F2, not_55_out, not_56_out, F5);
  and and_11 (and_11_out, not_57_out, not_58_out, not_59_out, not_60_out, not_61_out, not_62_out, not_63_out, not_64_out, F2, F3, not_65_out, not_66_out);
  and and_12 (and_12_out, not_67_out, not_68_out, not_69_out, not_70_out, not_71_out, not_72_out, not_73_out, F1, not_74_out, not_75_out, not_76_out);
  and and_13 (and_13_out, not_77_out, not_78_out, not_79_out, not_80_out, not_81_out, not_82_out, not_83_out, F1, not_84_out, not_85_out, F5);
  and and_14 (and_14_out, not_86_out, not_87_out, not_88_out, not_89_out, not_90_out, not_91_out, F1, not_92_out, not_93_out, not_94_out, F5);
  and and_15 (and_15_out, not_95_out, not_96_out, not_97_out, not_98_out, not_99_out, not_100_out, F0, F1, F2, not_101_out, not_102_out);
  and and_16 (and_16_out, not_103_out, not_104_out, OP2, OP3, not_105_out, not_106_out);
  and and_17 (and_17_out, not_107_out, OP1, not_108_out, OP3, not_109_out, not_110_out);
  and and_18 (and_18_out, not_111_out, not_112_out, not_113_out, not_114_out, not_115_out, not_116_out, not_117_out, F5);
  and and_19 (and_19_out, not_118_out, not_119_out, not_120_out, not_121_out, not_122_out, not_123_out, F2, not_124_out, not_125_out);
  and and_20 (and_20_out, not_126_out, not_127_out, not_128_out, not_129_out, not_130_out, not_131_out, F2, not_132_out, not_133_out);
  and and_21 (and_21_out, not_134_out, not_135_out, not_136_out, not_137_out, not_138_out, F2, not_139_out, not_140_out, not_141_out);
  and and_22 (and_22_out, not_142_out, not_143_out, not_144_out, not_145_out, F1, F2, not_146_out, not_147_out, not_148_out);
  and and_23 (and_23_out, not_149_out, not_150_out, not_151_out, not_152_out, F0, F1, not_153_out, not_154_out, F5);
  and and_24 (and_24_out, not_155_out, not_156_out, not_157_out, OP5);
  and and_25 (and_25_out, not_158_out, not_159_out, not_160_out, OP5);
  and and_26 (and_26_out, not_161_out, not_162_out, not_163_out, not_164_out, OP4, not_165_out);
  and and_27 (and_27_out, not_166_out, not_167_out, OP3, not_168_out, not_169_out);
  and and_28 (and_28_out, OP0, not_170_out, not_171_out, OP5);
  and and_29 (and_29_out, OP0, not_172_out, OP3, not_173_out);
  and and_30 (and_30_out, not_174_out, not_175_out, not_176_out, not_177_out, not_178_out, not_179_out, not_180_out, not_181_out, not_182_out, F3, not_183_out, not_184_out);
  and and_31 (and_31_out, not_185_out, not_186_out, not_187_out, not_188_out, not_189_out, not_190_out, not_191_out, F2, not_192_out, not_193_out, not_194_out);
  and and_32 (and_32_out, not_195_out, not_196_out, not_197_out, not_198_out, not_199_out, not_200_out, F1, not_201_out, F3, not_202_out, F5);
  and and_33 (and_33_out, not_203_out, not_204_out, not_205_out, not_206_out, not_207_out, not_208_out, F1, F2, not_209_out, not_210_out);
  and and_34 (and_34_out, not_211_out, not_212_out, not_213_out, not_214_out, not_215_out, not_216_out, F0, F2, not_217_out, not_218_out, F5);
  and and_35 (and_35_out, not_219_out, OP1, OP3, not_220_out, not_221_out);
  and and_36 (and_36_out, OP1, not_222_out, OP3, not_223_out, not_224_out);
  and and_37 (and_37_out, OP0, not_225_out, OP2, OP3, not_226_out, not_227_out);
  and and_38 (and_38_out, not_228_out, not_229_out, OP2, not_230_out, not_231_out, not_232_out);
  and and_39 (and_39_out, OP0, not_233_out, not_234_out, not_235_out, not_236_out, not_237_out, RT0);
  and and_40 (and_40_out, OP0, OP1, OP2, not_238_out, not_239_out, not_240_out);
  and and_41 (and_41_out, OP0, not_241_out, not_242_out, not_243_out, not_244_out, not_245_out);
  and and_42 (and_42_out, OP0, OP2, not_246_out, not_247_out, not_248_out);
  and and_43 (and_43_out, OP1, OP2, not_249_out, not_250_out, not_251_out);
  and and_44 (and_44_out, OP0, not_252_out, not_253_out, not_254_out, not_255_out, not_256_out);
  or or_1 (S0, and_1_out, and_2_out, and_3_out, and_4_out, and_5_out, and_6_out, and_7_out, and_8_out, and_9_out);
  or or_2 (B0, and_38_out, and_39_out, and_40_out);
  or or_3 (B1, and_41_out, and_42_out);
  or or_4 (B2, and_43_out, and_44_out);
  or or_5 (S1, and_10_out, and_11_out, and_12_out, and_13_out, and_14_out, and_15_out, and_16_out, and_17_out);
  or or_6 (S2, and_18_out, and_19_out, and_20_out, and_21_out, and_22_out, and_23_out, and_24_out, and_25_out, and_26_out, and_27_out, and_28_out, and_29_out);
  or or_7 (S3, and_30_out, and_31_out, and_32_out, and_33_out, and_34_out, and_35_out, and_36_out, and_37_out);
endmodule

// 控制信号生成
module \控制信号自动生成  (
  input  OP0,
  input  OP1,
  input  OP2,
  input  OP3,
  input  OP4,
  input  OP5,
  input  F0,
  input  F1,
  input  F2,
  input  F3,
  input  F4,
  input  F5,
  input  RS2,
  input  RS4,
  output MemToReg,
  output MemWrite,
  output MemHalf,
  output MemByte,
  output MemUnsigned,
  output ALU_SRC,
  output RegWrite,
  output SysCALL,
  output SignedExt,
  output RegDst,
  output JR,
  output JUMP,
  output JAL,
  output C0Reg0,
  output C0Reg1
);

  wire and_1_out, and_2_out, and_3_out, and_4_out, and_5_out, and_6_out, and_7_out, and_8_out, and_10_out,
       and_11_out, and_12_out, and_13_out, and_14_out, and_15_out, and_16_out, and_17_out, and_18_out,
       and_19_out, and_20_out, and_21_out, and_22_out, and_23_out, and_24_out, and_25_out, and_26_out,
       and_27_out, and_28_out, and_29_out, and_30_out, and_31_out, and_32_out, and_33_out, and_34_out,
       and_35_out, and_36_out, and_37_out, and_38_out, and_39_out, and_40_out, and_41_out, and_42_out,
       and_46_out, and_47_out, and_48_out, and_49_out, and_50_out, and_51_out, not_1_out, not_2_out,
       not_3_out, not_4_out, not_5_out, not_6_out, not_7_out, not_8_out, not_9_out, not_10_out, not_11_out,
       not_12_out, not_13_out, not_14_out, not_15_out, not_16_out, not_17_out, not_18_out, not_19_out,
       not_20_out, not_21_out, not_22_out, not_23_out, not_24_out, not_25_out, not_26_out, not_27_out,
       not_28_out, not_29_out, not_30_out, not_31_out, not_32_out, not_33_out, not_34_out, not_35_out,
       not_36_out, not_37_out, not_38_out, not_39_out, not_40_out, not_41_out, not_42_out, not_43_out,
       not_44_out, not_45_out, not_46_out, not_47_out, not_48_out, not_49_out, not_50_out, not_51_out,
       not_52_out, not_53_out, not_54_out, not_55_out, not_56_out, not_57_out, not_58_out, not_59_out,
       not_60_out, not_61_out, not_62_out, not_63_out, not_64_out, not_65_out, not_66_out, not_67_out,
       not_68_out, not_69_out, not_70_out, not_71_out, not_72_out, not_73_out, not_74_out, not_75_out,
       not_76_out, not_77_out, not_78_out, not_79_out, not_80_out, not_81_out, not_82_out, not_83_out,
       not_84_out, not_85_out, not_86_out, not_87_out, not_88_out, not_89_out, not_90_out, not_91_out,
       not_92_out, not_93_out, not_94_out, not_95_out, not_96_out, not_97_out, not_98_out, not_99_out,
       not_100_out, not_101_out, not_102_out, not_103_out, not_104_out, not_105_out, not_106_out,
       not_107_out, not_108_out, not_109_out, not_110_out, not_111_out, not_112_out, not_113_out,
       not_114_out, not_115_out, not_116_out, not_117_out, not_118_out, not_119_out, not_120_out,
       not_121_out, not_122_out, not_123_out, not_124_out, not_125_out, not_126_out, not_127_out,
       not_128_out, not_129_out, not_130_out, not_131_out, not_132_out, not_133_out, not_134_out,
       not_135_out, not_136_out, not_137_out, not_138_out, not_139_out, not_140_out, not_141_out,
       not_142_out, not_143_out, not_144_out, not_145_out, not_146_out, not_147_out, not_148_out,
       not_149_out, not_150_out, not_151_out, not_152_out, not_153_out, not_154_out, not_155_out,
       not_156_out, not_157_out, not_158_out, not_159_out, not_160_out, not_161_out, not_162_out,
       not_163_out, not_164_out, not_165_out, not_166_out, not_167_out, not_168_out, not_169_out,
       not_170_out, not_171_out, not_172_out, not_173_out, not_174_out, not_175_out, not_176_out,
       not_177_out, not_178_out, not_179_out, not_180_out, not_181_out, not_182_out, not_183_out,
       not_184_out, not_185_out, not_186_out, not_187_out, not_188_out, not_189_out, not_190_out,
       not_191_out, not_192_out, not_193_out, not_194_out, not_195_out, not_196_out, not_197_out,
       not_198_out, not_199_out, not_200_out, not_201_out, not_202_out, not_203_out, not_204_out,
       not_205_out, not_206_out, not_207_out, not_208_out, not_209_out, not_210_out, not_211_out,
       not_212_out, not_213_out, not_214_out, not_215_out, not_216_out, not_217_out, not_218_out,
       not_219_out, not_220_out, not_221_out, not_222_out, not_223_out, not_224_out, not_225_out,
       not_226_out, not_227_out, not_228_out, not_229_out, not_230_out, not_231_out, not_232_out,
       not_233_out, not_234_out, not_235_out, not_236_out, not_237_out, not_238_out;

  not not_1 (not_1_out, OP1);
  not not_2 (not_2_out, OP3);
  not not_3 (not_3_out, OP4);
  not not_4 (not_4_out, OP2);
  not not_5 (not_5_out, OP3);
  not not_6 (not_6_out, OP4);
  not not_7 (not_7_out, OP1);
  not not_8 (not_8_out, OP2);
  not not_9 (not_9_out, OP4);
  not not_10 (not_10_out, OP2);
  not not_11 (not_11_out, OP4);
  not not_12 (not_12_out, OP1);
  not not_13 (not_13_out, OP2);
  not not_14 (not_14_out, OP4);
  not not_15 (not_15_out, OP1);
  not not_16 (not_16_out, OP3);
  not not_17 (not_17_out, OP4);
  not not_18 (not_18_out, OP0);
  not not_19 (not_19_out, OP1);
  not not_20 (not_20_out, OP2);
  not not_21 (not_21_out, OP4);
  not not_22 (not_22_out, OP0);
  not not_23 (not_23_out, OP1);
  not not_24 (not_24_out, OP3);
  not not_25 (not_25_out, OP4);
  not not_26 (not_26_out, OP1);
  not not_27 (not_27_out, OP3);
  not not_28 (not_28_out, OP4);
  not not_29 (not_29_out, OP1);
  not not_30 (not_30_out, OP3);
  not not_31 (not_31_out, OP4);
  not not_32 (not_32_out, OP0);
  not not_33 (not_33_out, OP4);
  not not_34 (not_34_out, OP5);
  not not_35 (not_35_out, OP1);
  not not_36 (not_36_out, OP2);
  not not_37 (not_37_out, OP4);
  not not_38 (not_38_out, OP1);
  not not_39 (not_39_out, OP4);
  not not_40 (not_40_out, OP5);
  not not_41 (not_41_out, OP2);
  not not_42 (not_42_out, OP4);
  not not_43 (not_43_out, OP5);
  not not_44 (not_44_out, OP2);
  not not_45 (not_45_out, OP4);
  not not_46 (not_46_out, OP0);
  not not_47 (not_47_out, OP1);
  not not_48 (not_48_out, OP2);
  not not_49 (not_49_out, OP3);
  not not_50 (not_50_out, OP4);
  not not_51 (not_51_out, F0);
  not not_52 (not_52_out, F3);
  not not_53 (not_53_out, F4);
  not not_54 (not_54_out, OP0);
  not not_55 (not_55_out, OP1);
  not not_56 (not_56_out, OP2);
  not not_57 (not_57_out, OP3);
  not not_58 (not_58_out, OP4);
  not not_59 (not_59_out, F3);
  not not_60 (not_60_out, F4);
  not not_61 (not_61_out, OP0);
  not not_62 (not_62_out, OP1);
  not not_63 (not_63_out, OP2);
  not not_64 (not_64_out, OP3);
  not not_65 (not_65_out, OP4);
  not not_66 (not_66_out, F3);
  not not_67 (not_67_out, F4);
  not not_68 (not_68_out, OP0);
  not not_69 (not_69_out, OP1);
  not not_70 (not_70_out, OP2);
  not not_71 (not_71_out, OP3);
  not not_72 (not_72_out, OP4);
  not not_73 (not_73_out, F2);
  not not_74 (not_74_out, F4);
  not not_75 (not_75_out, OP1);
  not not_76 (not_76_out, OP3);
  not not_77 (not_77_out, OP4);
  not not_78 (not_78_out, OP0);
  not not_79 (not_79_out, OP1);
  not not_80 (not_80_out, OP2);
  not not_81 (not_81_out, OP3);
  not not_82 (not_82_out, OP5);
  not not_83 (not_83_out, RS4);
  not not_84 (not_84_out, OP0);
  not not_85 (not_85_out, OP4);
  not not_86 (not_86_out, OP5);
  not not_87 (not_87_out, OP1);
  not not_88 (not_88_out, OP4);
  not not_89 (not_89_out, OP5);
  not not_90 (not_90_out, OP2);
  not not_91 (not_91_out, OP3);
  not not_92 (not_92_out, OP4);
  not not_93 (not_93_out, OP2);
  not not_94 (not_94_out, OP4);
  not not_95 (not_95_out, OP5);
  not not_96 (not_96_out, OP0);
  not not_97 (not_97_out, OP1);
  not not_98 (not_98_out, OP2);
  not not_99 (not_99_out, OP3);
  not not_100 (not_100_out, OP4);
  not not_101 (not_101_out, OP5);
  not not_102 (not_102_out, F0);
  not not_103 (not_103_out, F1);
  not not_104 (not_104_out, F4);
  not not_105 (not_105_out, F5);
  not not_106 (not_106_out, OP1);
  not not_107 (not_107_out, OP3);
  not not_108 (not_108_out, OP4);
  not not_109 (not_109_out, OP1);
  not not_110 (not_110_out, OP2);
  not not_111 (not_111_out, OP4);
  not not_112 (not_112_out, OP2);
  not not_113 (not_113_out, OP4);
  not not_114 (not_114_out, OP5);
  not not_115 (not_115_out, OP3);
  not not_116 (not_116_out, OP4);
  not not_117 (not_117_out, OP5);
  not not_118 (not_118_out, OP1);
  not not_119 (not_119_out, OP2);
  not not_120 (not_120_out, OP4);
  not not_121 (not_121_out, OP2);
  not not_122 (not_122_out, OP4);
  not not_123 (not_123_out, OP0);
  not not_124 (not_124_out, OP3);
  not not_125 (not_125_out, OP4);
  not not_126 (not_126_out, OP5);
  not not_127 (not_127_out, F0);
  not not_128 (not_128_out, F1);
  not not_129 (not_129_out, F2);
  not not_130 (not_130_out, F4);
  not not_131 (not_131_out, F5);
  not not_132 (not_132_out, OP1);
  not not_133 (not_133_out, OP3);
  not not_134 (not_134_out, OP4);
  not not_135 (not_135_out, OP5);
  not not_136 (not_136_out, F0);
  not not_137 (not_137_out, F3);
  not not_138 (not_138_out, F4);
  not not_139 (not_139_out, OP1);
  not not_140 (not_140_out, OP3);
  not not_141 (not_141_out, OP4);
  not not_142 (not_142_out, OP5);
  not not_143 (not_143_out, F3);
  not not_144 (not_144_out, F4);
  not not_145 (not_145_out, OP1);
  not not_146 (not_146_out, OP3);
  not not_147 (not_147_out, OP4);
  not not_148 (not_148_out, OP5);
  not not_149 (not_149_out, F3);
  not not_150 (not_150_out, F4);
  not not_151 (not_151_out, OP1);
  not not_152 (not_152_out, OP3);
  not not_153 (not_153_out, OP4);
  not not_154 (not_154_out, OP5);
  not not_155 (not_155_out, F2);
  not not_156 (not_156_out, F4);
  not not_157 (not_157_out, OP0);
  not not_158 (not_158_out, OP1);
  not not_159 (not_159_out, OP2);
  not not_160 (not_160_out, OP3);
  not not_161 (not_161_out, OP5);
  not not_162 (not_162_out, RS4);
  not not_163 (not_163_out, OP1);
  not not_164 (not_164_out, OP2);
  not not_165 (not_165_out, OP4);
  not not_166 (not_166_out, OP3);
  not not_167 (not_167_out, OP4);
  not not_168 (not_168_out, OP5);
  not not_169 (not_169_out, OP0);
  not not_170 (not_170_out, OP3);
  not not_171 (not_171_out, OP4);
  not not_172 (not_172_out, OP5);
  not not_173 (not_173_out, OP1);
  not not_174 (not_174_out, OP3);
  not not_175 (not_175_out, OP4);
  not not_176 (not_176_out, OP5);
  not not_177 (not_177_out, OP2);
  not not_178 (not_178_out, OP4);
  not not_179 (not_179_out, OP5);
  not not_180 (not_180_out, OP4);
  not not_181 (not_181_out, OP3);
  not not_182 (not_182_out, OP2);
  not not_183 (not_183_out, OP1);
  not not_184 (not_184_out, OP0);
  not not_185 (not_185_out, F5);
  not not_186 (not_186_out, F4);
  not not_187 (not_187_out, F2);
  not not_188 (not_188_out, F1);
  not not_189 (not_189_out, F0);
  not not_190 (not_190_out, OP5);
  not not_191 (not_191_out, OP3);
  not not_192 (not_192_out, OP2);
  not not_193 (not_193_out, OP1);
  not not_194 (not_194_out, OP0);
  not not_195 (not_195_out, F5);
  not not_196 (not_196_out, F2);
  not not_197 (not_197_out, F1);
  not not_198 (not_198_out, F0);
  not not_199 (not_199_out, OP0);
  not not_200 (not_200_out, OP2);
  not not_201 (not_201_out, OP3);
  not not_202 (not_202_out, OP4);
  not not_203 (not_203_out, OP5);
  not not_204 (not_204_out, OP2);
  not not_205 (not_205_out, OP3);
  not not_206 (not_206_out, OP4);
  not not_207 (not_207_out, OP5);
  not not_208 (not_208_out, OP0);
  not not_209 (not_209_out, OP1);
  not not_210 (not_210_out, OP2);
  not not_211 (not_211_out, OP3);
  not not_212 (not_212_out, OP5);
  not not_213 (not_213_out, RS2);
  not not_214 (not_214_out, RS4);
  not not_215 (not_215_out, OP0);
  not not_216 (not_216_out, OP1);
  not not_217 (not_217_out, OP2);
  not not_218 (not_218_out, OP3);
  not not_219 (not_219_out, OP5);
  not not_220 (not_220_out, F0);
  not not_221 (not_221_out, F1);
  not not_222 (not_222_out, F2);
  not not_223 (not_223_out, F5);
  not not_224 (not_224_out, OP0);
  not not_225 (not_225_out, OP1);
  not not_226 (not_226_out, OP2);
  not not_227 (not_227_out, OP3);
  not not_228 (not_228_out, OP5);
  not not_229 (not_229_out, RS4);
  not not_230 (not_230_out, OP0);
  not not_231 (not_231_out, OP1);
  not not_232 (not_232_out, OP2);
  not not_233 (not_233_out, OP3);
  not not_234 (not_234_out, OP5);
  not not_235 (not_235_out, F0);
  not not_236 (not_236_out, F1);
  not not_237 (not_237_out, F2);
  not not_238 (not_238_out, F5);
  and and_1 (and_1_out, not_1_out, not_2_out, not_3_out, OP5);
  and and_2 (and_2_out, OP0, not_4_out, not_5_out, not_6_out, OP5);
  and and_3 (and_3_out, not_7_out, not_8_out, OP3, not_9_out, OP5);
  and and_4 (and_4_out, OP0, not_10_out, OP3, not_11_out, OP5);
  and and_5 (and_5_out, OP0, not_12_out, not_13_out, not_14_out, OP5);
  and and_6 (and_6_out, OP0, not_15_out, not_16_out, not_17_out, OP5);
  and and_7 (and_7_out, not_18_out, not_19_out, not_20_out, not_21_out, OP5);
  and and_8 (and_8_out, not_22_out, not_23_out, not_24_out, not_25_out, OP5);
  and and_9 (MemUnsigned, not_26_out, OP2, not_27_out, not_28_out, OP5);
  and and_10 (and_10_out, not_29_out, not_30_out, not_31_out, OP5);
  and and_11 (and_11_out, not_32_out, OP3, not_33_out, not_34_out);
  and and_12 (and_12_out, not_35_out, not_36_out, OP3, not_37_out);
  and and_13 (and_13_out, not_38_out, OP3, not_39_out, not_40_out);
  and and_14 (and_14_out, not_41_out, OP3, not_42_out, not_43_out);
  and and_15 (and_15_out, OP0, not_44_out, not_45_out, OP5);
  and and_16 (and_16_out, not_46_out, not_47_out, not_48_out, not_49_out, not_50_out, not_51_out, not_52_out, not_53_out);
  and and_17 (and_17_out, not_54_out, not_55_out, not_56_out, not_57_out, not_58_out, not_59_out, not_60_out, F5);
  and and_18 (and_18_out, not_61_out, not_62_out, not_63_out, not_64_out, not_65_out, F1, not_66_out, not_67_out);
  and and_19 (and_19_out, not_68_out, not_69_out, not_70_out, not_71_out, not_72_out, F1, not_73_out, not_74_out, F5);
  and and_20 (and_20_out, not_75_out, not_76_out, not_77_out, OP5);
  and and_21 (and_21_out, not_78_out, not_79_out, not_80_out, not_81_out, OP4, not_82_out, not_83_out);
  and and_22 (and_22_out, not_84_out, OP3, not_85_out, not_86_out);
  and and_23 (and_23_out, not_87_out, OP3, not_88_out, not_89_out);
  and and_24 (and_24_out, OP0, not_90_out, not_91_out, not_92_out, OP5);
  and and_25 (and_25_out, OP0, OP1, not_93_out, not_94_out, not_95_out);
  and and_26 (and_26_out, not_106_out, not_107_out, not_108_out, OP5);
  and and_27 (and_27_out, not_109_out, not_110_out, OP3, not_111_out);
  and and_28 (and_28_out, not_112_out, OP3, not_113_out, not_114_out);
  and and_29 (and_29_out, OP2, not_115_out, not_116_out, not_117_out);
  and and_30 (and_30_out, OP0, not_118_out, not_119_out, not_120_out);
  and and_31 (and_31_out, OP0, not_121_out, not_122_out, OP5);
  and and_32 (and_32_out, not_123_out, not_124_out, not_125_out, not_126_out, not_127_out, not_128_out, not_129_out, not_130_out, not_131_out);
  and and_33 (and_33_out, not_132_out, not_133_out, not_134_out, not_135_out, not_136_out, not_137_out, not_138_out);
  and and_34 (and_34_out, not_139_out, not_140_out, not_141_out, not_142_out, not_143_out, not_144_out, F5);
  and and_35 (and_35_out, not_145_out, not_146_out, not_147_out, not_148_out, F1, not_149_out, not_150_out);
  and and_36 (and_36_out, not_151_out, not_152_out, not_153_out, not_154_out, F1, not_155_out, not_156_out, F5);
  and and_37 (and_37_out, not_157_out, not_158_out, not_159_out, not_160_out, OP4, not_161_out, RS2, not_162_out);
  and and_38 (and_38_out, not_163_out, not_164_out, OP3, not_165_out, OP5);
  and and_39 (and_39_out, OP2, not_166_out, not_167_out, not_168_out);
  and and_40 (and_40_out, not_169_out, OP1, not_170_out, not_171_out, not_172_out);
  and and_41 (and_41_out, OP0, not_173_out, not_174_out, not_175_out, not_176_out);
  and and_42 (and_42_out, OP0, not_177_out, OP3, not_178_out, OP5);
  and and_43 (JUMP, not_199_out, OP1, not_200_out, not_201_out, not_202_out, not_203_out);
  and and_44 (JAL, OP0, OP1, not_204_out, not_205_out, not_206_out, not_207_out);
  or or_1 (MemToReg, and_1_out, and_2_out);
  or or_2 (MemWrite, and_3_out, and_4_out);
  or or_3 (MemHalf, and_5_out, and_6_out);
  or or_4 (MemByte, and_7_out, and_8_out);
  or or_5 (ALU_SRC, and_10_out, and_11_out, and_12_out, and_13_out, and_14_out, and_15_out);
  and and_45 (SysCALL, not_96_out, not_97_out, not_98_out, not_99_out, not_100_out, not_101_out, not_102_out, not_103_out, F2, F3, not_104_out, not_105_out);
  or or_6 (SignedExt, and_26_out, and_27_out, and_28_out, and_29_out, and_30_out, and_31_out);
  and and_46 (and_46_out, not_179_out, not_180_out, not_181_out, not_182_out, not_183_out, not_184_out, not_185_out, not_186_out, F3, not_187_out, not_188_out, not_189_out);
  or or_7 (JR, and_46_out, and_47_out);
  and and_47 (and_47_out, not_190_out, OP4, not_191_out, not_192_out, not_193_out, not_194_out, not_195_out, F4, F3, not_196_out, not_197_out, not_198_out, RS4);
  and and_48 (and_48_out, not_208_out, not_209_out, not_210_out, not_211_out, OP4, not_212_out, not_213_out, not_214_out);
  or or_8 (C0Reg0, and_48_out, and_49_out);
  and and_49 (and_49_out, not_215_out, not_216_out, not_217_out, not_218_out, OP4, not_219_out, not_220_out, not_221_out, not_222_out, F3, F4, not_223_out, RS4);
  and and_50 (and_50_out, not_224_out, not_225_out, not_226_out, not_227_out, OP4, not_228_out, RS2, not_229_out);
  or or_9 (C0Reg1, and_50_out, and_51_out);
  and and_51 (and_51_out, not_230_out, not_231_out, not_232_out, not_233_out, OP4, not_234_out, not_235_out, not_236_out, not_237_out, F3, F4, not_238_out, RS4);
  or or_10 (RegWrite, and_16_out, and_17_out, and_18_out, and_19_out, and_20_out, and_21_out, and_22_out, and_23_out, and_24_out, and_25_out);
  or or_11 (RegDst, and_32_out, and_33_out, and_34_out, and_35_out, and_36_out, and_37_out, and_38_out, and_39_out, and_40_out, and_41_out, and_42_out);
endmodule

// ALU
module MIPS_ALU (
  input  [4:0] shamt,
  input  [31:0] X,
  input  [31:0] Y,
  input  [6:0] AluOP,
  output Branch,
  output [31:0] Result,
  output [31:0] Result_2
);

  wire and_2_out, comparator_1_eq, not_1_out, not_2_out, or_2_out;
  wire [0:0] comparator_1_lt, comparator_2_lt;
  wire [31:0] adder_1_out, AND_out, divider_1_out, divider_1_rem, multiplier_1_cout, multiplier_1_out,
       NOR_out, OR_out, shifter_1_out, shifter_2_out, shifter_3_out, shifter_4_out, shifter_5_out,
       shifter_6_out, subtractor_1_out, XOR_out;

  assign AND_out = X & Y;  // AND_Gate AND, 32 bits wide
  assign OR_out = X | Y;  // OR_Gate OR, 32 bits wide
  Shifter #(.width(32), .shift("ll")) shifter_1 (.in(Y), .\dist (shamt), .out(shifter_1_out));
  Shifter #(.width(32), .shift("ar")) shifter_2 (.in(Y), .\dist (shamt), .out(shifter_2_out));
  Shifter #(.width(32), .shift("lr")) shifter_3 (.in(Y), .\dist (shamt), .out(shifter_3_out));
  Multiplier #(.width(32)) multiplier_1 (.a(X), .b(Y), .out(multiplier_1_out), .cout(multiplier_1_cout));  // open: cin
  Divider #(.width(32)) divider_1 (.a(X), .b(Y), .out(divider_1_out), .rem(divider_1_rem));  // open: upper
  Adder #(.width(32)) adder_1 (.a(X), .b(Y), .out(adder_1_out));  // open: cin, cout
  Subtractor #(.width(32)) subtractor_1 (.a(X), .b(Y), .out(subtractor_1_out));  // open: bin, bout
  assign XOR_out = X ^ Y;  // XOR_Gate XOR, 32 bits wide
  assign NOR_out = ~(X | Y);  // NOR_Gate NOR, 32 bits wide
  Comparator #(.width(32), .mode("twosComplement")) comparator_1 (
    .a(X), .b(Y), .eq(comparator_1_eq), .lt(comparator_1_lt[0]));  // open: gt
  Comparator #(.width(32), .mode("unsigned")) comparator_2 (.a(X), .b(Y), .lt(comparator_2_lt[0]));  // open: gt, eq
  Shifter #(.width(32), .shift("ll")) shifter_4 (.in(Y), .\dist (X[4:0]), .out(shifter_4_out));
  Shifter #(.width(32), .shift("ar")) shifter_5 (.in(Y), .\dist (X[4:0]), .out(shifter_5_out));
  Shifter #(.width(32), .shift("lr")) shifter_6 (.in(Y), .\dist (X[4:0]), .out(shifter_6_out));
  Multiplexer #(.select(4), .width(32), .disabled("Z"), .enable("false")) multiplexer_1 (
    .in0(shifter_1_out), .in1(shifter_2_out), .in2(shifter_3_out), .in3(multiplier_1_out),
    .in4(divider_1_out), .in5(adder_1_out), .in6(subtractor_1_out), .in7(AND_out), .in8(OR_out),
    .in9(XOR_out), .in10(NOR_out), .in11({{31{1'b0}}, comparator_1_lt[0]}),
    .in12({{31{1'b0}}, comparator_2_lt[0]}), .in13(shifter_4_out), .in14(shifter_5_out),
    .in15(shifter_6_out), .out(Result), .sel(AluOP[3:0]));
  Multiplexer #(.select(4), .width(32), .disabled("Z"), .enable("false")) multiplexer_2 (
    .in0({32{1'b0}}), .in1({32{1'b0}}), .in2({32{1'b0}}), .in3(multiplier_1_cout), .in4(divider_1_rem),
    .in5({32{1'b0}}), .in6({32{1'b0}}), .in7({32{1'b0}}), .in8({32{1'b0}}), .in9({32{1'b0}}),
    .in10({32{1'b0}}), .in11({32{1'b0}}), .in12({32{1'b0}}), .in13({32{1'b0}}), .in14({32{1'b0}}),
    .in15({32{1'b0}}), .out(Result_2), .sel(AluOP[3:0]));
  or or_2 (or_2_out, comparator_1_eq, X[31]);
  not not_1 (not_1_out, X[31]);
  and and_2 (and_2_out, ~X[31], ~comparator_1_eq);  // AND_Gate
  not not_2 (not_2_out, comparator_1_eq);
  Multiplexer #(.select(3), .width(1), .disabled("Z"), .enable("false")) multiplexer_3 (
    .in0(1'b0), .in1(comparator_1_eq), .in2(not_2_out), .in3(1'b0), .in4(or_2_out), .in5(not_1_out),
    .in6(X[31]), .in7(and_2_out), .out(Branch), .sel(AluOP[6:4]));

  // Other names for the same wires on the sheet: ALUOP_t[3:0] = AluOP[3:0]; BRANCHOP[2:0] = AluOP[6:4];
  //   Result2[31:0] = Result_2

  // Notes on the sheet:
  //   不要改变此引脚区域内容，也不要改变ALU封装形式
  //   输入引脚
  //   输出引脚
endmodule

module MIPS_Regifile (
  input  [31:0] Din,
  input  Clk,
  input  [4:0] R1_num,
  input  [4:0] W_num,
  input  [31:0] EPC,
  input  WE,
  input  IR,
  input  [4:0] R2_num,
  input  [1:0] C0Reg,
  output [31:0] R1,
  output [31:0] Status,
  output [31:0] R2
);

  wire and_1_out, decoder_1_out0, decoder_1_out1, demultiplexer_1_out0, demultiplexer_1_out1, or_1_out,
       or_2_out, or_3_out, or_4_out;
  wire [31:0] EPC_q, multiplexer_1_out, multiplexer_2_out, multiplexer_3_out, registerfile_1_p7,
       registerfile_1_p8;

  Decoder #(.select(1), .tristate("false"), .disabled(0), .enable("true")) decoder_1 (
    .out0(decoder_1_out0), .out1(decoder_1_out1), .sel(C0Reg[1]), .en(WE));
  Demultiplexer #(.select(1), .width(1), .tristate("false"), .disabled(0), .enable("false")) demultiplexer_1 (
    .out0(demultiplexer_1_out0), .out1(demultiplexer_1_out1), .in(decoder_1_out1), .sel(W_num[1]));
  Multiplexer #(.select(1), .width(32), .disabled("Z"), .enable("false")) multiplexer_1 (
    .in0(Din), .in1({Status[31:1], 1'b0}), .out(multiplexer_1_out), .sel(IR));
  or or_1 (or_1_out, demultiplexer_1_out0, IR);
  Multiplexer #(.select(1), .width(32), .disabled("Z"), .enable("false")) multiplexer_2 (
    .in0(Din), .in1(EPC), .out(multiplexer_2_out), .sel(IR));
  or or_2 (or_2_out, demultiplexer_1_out1, IR);
  Register #(.width(32), .trigger("rising"), .Select("low")) u_Status (
    .D(multiplexer_1_out), .en(or_1_out), .Q(Status), .clk(Clk));  // open: clr
  Register #(.width(32), .trigger("rising"), .Select("low")) u_EPC (
    .D(multiplexer_2_out), .en(or_2_out), .Q(EPC_q), .clk(Clk));  // open: clr
  // RegisterFile registerfile_1: pin names not known; wires that end beside it: Din, Clk, decoder_1_out0, W_num, R1_num, R2_num, registerfile_1_p7, registerfile_1_p8
  Multiplexer #(.select(1), .width(32), .disabled("Z"), .enable("false")) multiplexer_3 (
    .in0(Status), .in1(EPC_q), .out(multiplexer_3_out), .sel(or_3_out));
  or or_3 (or_3_out, R2_num[1], and_1_out);
  and and_1 (and_1_out, C0Reg[1], C0Reg[0]);
  Multiplexer #(.select(1), .width(32), .disabled("Z"), .enable("false")) multiplexer_4 (
    .in0(registerfile_1_p7), .in1({32{1'b0}}), .out(R1), .sel(or_4_out));
  or or_4 (or_4_out, C0Reg[1], C0Reg[0]);
  Multiplexer #(.select(1), .width(32), .disabled("Z"), .enable("false")) multiplexer_5 (
    .in0(registerfile_1_p8), .in1(multiplexer_3_out), .out(R2), .sel(C0Reg[0]));

  // Notes on the sheet:
  //   GR
  //   CP0
endmodule

module \MIPS_Regifile_下降沿  (
  input  [31:0] Din,
  input  Clk,
  input  WE,
  input  [4:0] R1_num,
  input  [4:0] W_num,
  input  [4:0] R2_num,
  output [31:0] R1,
  output [31:0] R2
);

  // RegisterFile registerfile_1: pin names not known; wires that end beside it: Din, Clk, WE, W_num, R1_num, R2_num, R1, R2
endmodule

module \MIPS_Regifile_下降沿_CP0  (
  input  [31:0] Din,
  input  Clk,
  input  [4:0] R1_num,
  input  [4:0] W_num,
  input  [31:0] EPC,
  input  WE,
  input  C0W,
  input  IR,
  input  [4:0] R2_num,
  input  [1:0] C0Reg,
  output [31:0] R1,
  output [31:0] Status,
  output [31:0] R2
);

  wire decoder_1_out0, decoder_1_out1, demultiplexer_1_out0, demultiplexer_1_out1, or_1_out, or_2_out;
  wire [31:0] EPC_q, multiplexer_1_out, multiplexer_2_out, multiplexer_3_out, registerfile_1_p7,
       registerfile_1_p8, temp_q;

  Register #(.width(32), .trigger("rising"), .Select("low")) temp (.D(EPC), .Q(temp_q), .clk(Clk));  // open: en, clr
  Decoder #(.select(1), .tristate("false"), .disabled(0), .enable("true")) decoder_1 (
    .out0(decoder_1_out0), .out1(decoder_1_out1), .sel(C0W), .en(WE));
  Demultiplexer #(.select(1), .width(1), .tristate("false"), .disabled(0), .enable("false")) demultiplexer_1 (
    .out0(demultiplexer_1_out0), .out1(demultiplexer_1_out1), .in(decoder_1_out1), .sel(W_num[1]));
  Multiplexer #(.select(1), .width(32), .disabled("Z"), .enable("false")) multiplexer_1 (
    .in0(Din), .in1({Status[31:1], 1'b0}), .out(multiplexer_1_out), .sel(IR));
  or or_1 (or_1_out, demultiplexer_1_out0, IR);
  Multiplexer #(.select(1), .width(32), .disabled("Z"), .enable("false")) multiplexer_2 (
    .in0(Din), .in1(temp_q), .out(multiplexer_2_out), .sel(IR));
  or or_2 (or_2_out, demultiplexer_1_out1, IR);
  // RegisterFile registerfile_1: pin names not known; wires that end beside it: Din, Clk, decoder_1_out0, W_num, R1_num, R2_num, registerfile_1_p7, registerfile_1_p8
  Register #(.width(32), .trigger("falling"), .Select("low")) u_Status (
    .D(multiplexer_1_out), .en(or_1_out), .Q(Status), .clk(Clk));  // open: clr
  Register #(.width(32), .trigger("falling"), .Select("low")) u_EPC (
    .D(multiplexer_2_out), .en(or_2_out), .Q(EPC_q), .clk(Clk));  // open: clr
  Multiplexer #(.select(1), .width(32), .disabled("Z"), .enable("false")) multiplexer_3 (
    .in0(Status), .in1(EPC_q), .out(multiplexer_3_out), .sel(R2_num[1]));
  Multiplexer #(.select(2), .width(32), .disabled("Z"), .enable("false")) multiplexer_4 (
    .in0(registerfile_1_p7), .in1({32{1'b0}}), .in2({32{1'b0}}), .in3(EPC_q), .out(R1), .sel(C0Reg));
  Multiplexer #(.select(1), .width(32), .disabled("Z"), .enable("false")) multiplexer_5 (
    .in0(registerfile_1_p8), .in1(multiplexer_3_out), .out(R2), .sel(C0Reg[0]));

  // Notes on the sheet:
  //   GR
  //   CP0
endmodule

module MIPS_Ram_Adapter (
  input  [31:0] DataIn,
  input  [31:0] dout,
  input  [3:0] CONTROL,
  input  [31:0] Addr,
  input  CLK,
  output [31:0] DataOut,
  output [31:0] din,
  output str,
  output [9:0] A,
  output clk_2
);

  wire [7:0] multiplexer_1_out;
  wire [15:0] multiplexer_2_out;
  wire [31:0] bit_extender_1_out, bit_extender_2_out, bit_extender_3_out, bit_extender_4_out,
       multiplexer_4_out, multiplexer_5_out;

  Multiplexer #(.select(2), .width(8), .disabled("Z"), .enable("false")) multiplexer_1 (
    .in0(dout[7:0]), .in1(dout[15:8]), .in2(dout[23:16]), .in3(dout[31:24]), .out(multiplexer_1_out),
    .sel(Addr[1:0]));
  Multiplexer #(.select(1), .width(16), .disabled("Z"), .enable("false")) multiplexer_2 (
    .in0(dout[15:0]), .in1(dout[31:16]), .out(multiplexer_2_out), .sel(Addr[1]));
  assign bit_extender_1_out = {{24{multiplexer_1_out[7]}}, multiplexer_1_out};  // Bit_Extender bit_extender_1
  assign bit_extender_2_out = {{24{1'b0}}, multiplexer_1_out};  // Bit_Extender bit_extender_2
  assign bit_extender_3_out = {{16{multiplexer_2_out[15]}}, multiplexer_2_out};  // Bit_Extender bit_extender_3
  assign bit_extender_4_out = {{16{1'b0}}, multiplexer_2_out};  // Bit_Extender bit_extender_4
  Multiplexer #(.select(3), .width(32), .disabled("Z"), .enable("false")) multiplexer_3 (
    .in0(dout), .in1(dout), .in2(bit_extender_1_out), .in3(bit_extender_2_out), .in4(bit_extender_3_out),
    .in5(bit_extender_4_out), .in6({32{1'b0}}), .in7({32{1'b0}}), .out(DataOut), .sel(CONTROL[2:0]));
  Multiplexer #(.select(2), .width(32), .disabled("Z"), .enable("false")) multiplexer_4 (
    .in0({dout[31:8], DataIn[7:0]}), .in1({dout[31:16], DataIn[7:0], dout[7:0]}),
    .in2({dout[31:24], DataIn[7:0], dout[15:0]}), .in3({DataIn[7:0], dout[23:0]}), .out(multiplexer_4_out),
    .sel(Addr[1:0]));
  Multiplexer #(.select(1), .width(32), .disabled("Z"), .enable("false")) multiplexer_5 (
    .in0({dout[31:16], DataIn[15:0]}), .in1({DataIn[15:0], dout[15:0]}), .out(multiplexer_5_out),
    .sel(Addr[1]));
  Multiplexer #(.select(2), .width(32), .disabled("Z"), .enable("false")) multiplexer_6 (
    .in0(DataIn), .in1(multiplexer_4_out), .in2(multiplexer_5_out), .in3({32{1'b0}}), .out(din),
    .sel(CONTROL[2:1]));

  assign A = Addr[11:2];
  assign clk_2 = CLK;
  assign str = CONTROL[3];
endmodule

module \理想流水线  (
  output RegWrite,
  output MemWrite,
  output [31:0] IF_PC,
  output [31:0] ID_PC,
  output [31:0] EX_PC,
  output [31:0] M_PC,
  output [31:0] WB_PC,
  output [31:0] RDin,
  output [31:0] MDin,
  output [31:0] LedData
);

  wire and_1_out, CLK, comparator_1_eq, ex_mem_1_jalout, ex_mem_1_memtoregout, ex_mem_1_regwriteout,
       \ex_mem_1_使能传递端_低电平有效_stall_高电平有效 , Go, HaltIn, HaltOut, id_ex_1_alusrcbout, id_ex_1_jalout,
       id_ex_1_memtoregout, id_ex_1_regwriteout, \id_ex_1_使能传递端_低电平有效_stall_高电平有效 ,
       \if_id_1_使能传递端_低电平有效_stall_高电平有效 , IR1, IR2, IR3, mem_wb_1_memtoregout, mips_ram_adapter_1_clk_2,
       mips_ram_adapter_1_str, not_1_out, not_2_out, RST, SignedExt, Syscall, W1, W2, W3,
       \单周期硬布线控制器_1_alu_src , \单周期硬布线控制器_1_jal , \单周期硬布线控制器_1_jmp , \单周期硬布线控制器_1_jr , \单周期硬布线控制器_1_memtoreg ,
       \单周期硬布线控制器_1_regdst , \单周期硬布线控制器_1_regwrite ;
  wire [2:0] ex_mem_1_memcontrolout;
  wire [3:0] id_ex_1_memcontrolout, \单周期硬布线控制器_1_memcontrol ;
  wire [4:0] ex_mem_1_w_out, id_ex_1_shamtout, id_ex_1_w_out, multiplexer_2_out, multiplexer_3_out,
       multiplexer_4_out, multiplexer_6_out, W_num;
  wire [6:0] id_ex_1_aluopout, \单周期硬布线控制器_1_alu_op ;
  wire [9:0] mips_ram_adapter_1_a;
  wire [15:0] \总周期数 ;
  wire [25:0] if_id_1_irout;
  wire [31:0] a0, adder_1_out, bit_extender_1_out, bit_extender_2_out, ex_mem_1_aluout, ex_mem_1_irout,
       ex_mem_1_pc_4out, id_ex_1_aout, id_ex_1_bout, id_ex_1_immout, id_ex_1_irout, id_ex_1_pc_4out,
       if_id_1_pc_4out, mem_wb_1_aluout, mem_wb_1_memout, mips_alu_1_result, mips_ram_adapter_1_dataout,
       mips_ram_adapter_1_din, multiplexer_1_out, multiplexer_5_out, multiplexer_7_out, multiplexer_8_out,
       ram_1_data, rom_1_data, undriven, undriven_2, undriven_3, v0;
  wire [31:26] if_id_1_irout_2;

  Button \u_总复位  (.out(RST));
  Button _1 (.out(IR1));
  Button _2 (.out(IR2));
  Button _3 (.out(IR3));
  Button \u_继续运行  (.out(Go));
  LED #(.active("true")) led_1 (.in(W1));
  LED #(.active("true")) led_2 (.in(W2));
  LED #(.active("true")) led_3 (.in(W3));
  Register #(.width(32), .trigger("rising"), .Select("low")) PC (
    .D(multiplexer_1_out), .en(not_1_out), .Q(IF_PC), .clk(CLK));  // open: clr
  Multiplexer #(.select(2), .width(32), .disabled("Z"), .enable("false")) multiplexer_1 (
    .in0(adder_1_out), .in1(undriven_3), .in2(undriven_2), .in3(undriven), .out(multiplexer_1_out),
    .sel(2'b00));
  not not_1 (not_1_out, 1'b0);
  not not_2 (not_2_out, HaltOut);
  Hex_Digit_Display hex_digit_display_1 (.value(LedData[31:28]));  // open: dp
  Counter #(.width(16), .max('hffff), .ongoal("stay"), .trigger("rising"), .behavior("old")) \u_总周期数  (
    .count(not_2_out), .Q(\总周期数 ), .clk(CLK));  // open: load, D, carry, clr, preset
  Hex_Digit_Display hex_digit_display_2 (.value(LedData[27:24]));  // open: dp
  Hex_Digit_Display hex_digit_display_3 (.value(LedData[23:20]));  // open: dp
  Adder #(.width(32)) adder_1 (.a(IF_PC), .b(32'h4), .out(adder_1_out));  // open: cin, cout
  Hex_Digit_Display hex_digit_display_4 (.value(LedData[19:16]));  // open: dp
  Hex_Digit_Display hex_digit_display_5 (.value(LedData[15:12]));  // open: dp
  IF_ID if_id_1 (
    .PCin(IF_PC), .IRin(rom_1_data), .CLK(CLK), .PCout(ID_PC), .IRout({if_id_1_irout_2, if_id_1_irout}),
    .\使能端_低电平有效_stall_高电平有效 (1'b0), .PC_4in(adder_1_out), .PC_4out(if_id_1_pc_4out),
    .\使能传递端_低电平有效_stall_高电平有效 (\if_id_1_使能传递端_低电平有效_stall_高电平有效 ));  // open: 同步清零_气泡_高电平有效, LoadUse
  ROM #(.addrWidth(10), .dataWidth(32), .Select("high")) rom_1 (.addr(IF_PC[11:2]), .data(rom_1_data));
  Hex_Digit_Display hex_digit_display_6 (.value(LedData[7:4]));  // open: dp
  Hex_Digit_Display hex_digit_display_7 (.value(LedData[11:8]));  // open: dp
  Clock #(.highDuration(1), .lowDuration(1)) clock_1 (.out(CLK));
  Hex_Digit_Display hex_digit_display_8 (.value(LedData[3:0]));  // open: dp
  Comparator #(.width(32), .mode("unsigned")) comparator_1 (.a(v0), .b(32'ha), .eq(comparator_1_eq));  // open: gt, lt
  and and_1 (and_1_out, ~comparator_1_eq, Syscall);  // AND_Gate
  \单周期硬布线控制器  \u_单周期硬布线控制器_1  (
    .IR({if_id_1_irout_2, if_id_1_irout}), .ALU_OP(\单周期硬布线控制器_1_alu_op ), .MemToReg(\单周期硬布线控制器_1_memtoreg ),
    .MemControl(\单周期硬布线控制器_1_memcontrol ), .ALU_SRC(\单周期硬布线控制器_1_alu_src ),
    .RegWrite(\单周期硬布线控制器_1_regwrite ), .SysCALL(Syscall), .SignedExt(SignedExt),
    .RegDst(\单周期硬布线控制器_1_regdst ), .JR(\单周期硬布线控制器_1_jr ), .JMP(\单周期硬布线控制器_1_jmp ), .JAL(\单周期硬布线控制器_1_jal ));  // open: R1_Used, R2_Used, C0Reg
  Multiplexer #(.select(1), .width(5), .disabled("Z"), .enable("false")) multiplexer_2 (
    .in0(if_id_1_irout[25:21]), .in1(5'b00010), .out(multiplexer_2_out), .sel(Syscall));
  Multiplexer #(.select(1), .width(5), .disabled("Z"), .enable("false")) multiplexer_3 (
    .in0(if_id_1_irout[20:16]), .in1(5'b00100), .out(multiplexer_3_out), .sel(Syscall));
  assign bit_extender_1_out = {{16{1'b0}}, if_id_1_irout[15:0]};  // Bit_Extender bit_extender_1
  assign bit_extender_2_out = {{16{if_id_1_irout[15]}}, if_id_1_irout[15:0]};  // Bit_Extender bit_extender_2
  Register #(.width(32), .trigger("rising"), .Select("low")) register_1 (
    .D(a0), .en(and_1_out), .Q(LedData), .clk(CLK));  // open: clr
  Multiplexer #(.select(1), .width(5), .disabled("Z"), .enable("false")) multiplexer_4 (
    .in0(if_id_1_irout[20:16]), .in1(if_id_1_irout[15:11]), .out(multiplexer_4_out),
    .sel(\单周期硬布线控制器_1_regdst ));
  Multiplexer #(.select(1), .width(32), .disabled("Z"), .enable("false")) multiplexer_5 (
    .in0(bit_extender_1_out), .in1(bit_extender_2_out), .out(multiplexer_5_out), .sel(SignedExt));
  and and_2 (HaltIn, comparator_1_eq, Syscall);
  ID_EX id_ex_1 (
    .PCin(ID_PC), .IRin({if_id_1_irout_2, if_id_1_irout}), .Ain(v0), .Bin(a0), .IMMin(multiplexer_5_out),
    .MEMTOREGin(\单周期硬布线控制器_1_memtoreg ), .MEMCONTROLin(\单周期硬布线控制器_1_memcontrol ),
    .ALUOPin(\单周期硬布线控制器_1_alu_op ), .ALUSRCBin(\单周期硬布线控制器_1_alu_src ), .CLK(CLK), .PCout(EX_PC),
    .IRout(id_ex_1_irout), .Aout(id_ex_1_aout), .Bout(id_ex_1_bout), .IMMout(id_ex_1_immout),
    .MEMTOREGout(id_ex_1_memtoregout), .MEMCONTROLout(id_ex_1_memcontrolout), .ALUOPout(id_ex_1_aluopout),
    .ALUSRCBout(id_ex_1_alusrcbout), .\使能端_低电平有效_stall_高电平有效 (\if_id_1_使能传递端_低电平有效_stall_高电平有效 ),
    .SHAMTin(if_id_1_irout[10:6]), .SHAMTout(id_ex_1_shamtout), .REGWRITEin(\单周期硬布线控制器_1_regwrite ),
    .REGWRITEout(id_ex_1_regwriteout), .W_in(multiplexer_6_out), .W_out(id_ex_1_w_out),
    .JALin(\单周期硬布线控制器_1_jal ), .JALout(id_ex_1_jalout),
    .\使能传递端_低电平有效_stall_高电平有效 (\id_ex_1_使能传递端_低电平有效_stall_高电平有效 ), .PC_4in(if_id_1_pc_4out),
    .PC_4out(id_ex_1_pc_4out));  // open: 同步清零_气泡_高电平有效, R1_SELin, R1_SELout, R2_SELin, R2_SELout, C0Win, C0Wout, BRPin, BRPout, RSTin, RSTout
  Multiplexer #(.select(1), .width(5), .disabled("Z"), .enable("false")) multiplexer_6 (
    .in0(multiplexer_4_out), .in1({5{1'b1}}), .out(multiplexer_6_out), .sel(\单周期硬布线控制器_1_jal ));
  \MIPS_Regifile_下降沿  \mips_regifile_下降沿_1  (
    .Din(RDin), .Clk(CLK), .R1(v0), .R2(a0), .WE(RegWrite), .W_num(W_num), .R1_num(multiplexer_2_out),
    .R2_num(multiplexer_3_out));
  Multiplexer #(.select(1), .width(32), .disabled("Z"), .enable("false")) multiplexer_7 (
    .in0(id_ex_1_bout), .in1(id_ex_1_immout), .out(multiplexer_7_out), .sel(id_ex_1_alusrcbout));
  EX_MEM ex_mem_1 (
    .PCin(EX_PC), .IRin(id_ex_1_irout), .Bin(id_ex_1_bout), .MEMTOREGin(id_ex_1_memtoregout),
    .MEMCONTROLin(id_ex_1_memcontrolout), .CLK(CLK), .PCout(M_PC), .IRout(ex_mem_1_irout), .Bout(MDin),
    .MEMTOREGout(ex_mem_1_memtoregout), .MEMCONTROLout({MemWrite, ex_mem_1_memcontrolout}),
    .\使能端_低电平有效_stall_高电平有效 (\id_ex_1_使能传递端_低电平有效_stall_高电平有效 ), .ALUin(mips_alu_1_result),
    .ALUout(ex_mem_1_aluout), .REGWRITEin(id_ex_1_regwriteout), .REGWRITEout(ex_mem_1_regwriteout),
    .W_in(id_ex_1_w_out), .W_out(ex_mem_1_w_out), .JALin(id_ex_1_jalout), .JALout(ex_mem_1_jalout),
    .\使能传递端_低电平有效_stall_高电平有效 (\ex_mem_1_使能传递端_低电平有效_stall_高电平有效 ), .PC_4in(id_ex_1_pc_4out),
    .PC_4out(ex_mem_1_pc_4out));  // open: 同步清零_气泡_高电平有效, C0Win, C0Wout
  MIPS_ALU mips_alu_1 (
    .X(id_ex_1_aout), .Y(multiplexer_7_out), .AluOP(id_ex_1_aluopout), .Result(mips_alu_1_result),
    .shamt(id_ex_1_shamtout));  // open: Branch, Result_2
  Multiplexer #(.select(1), .width(32), .disabled("Z"), .enable("false")) multiplexer_8 (
    .in0(ex_mem_1_aluout), .in1(ex_mem_1_pc_4out), .out(multiplexer_8_out), .sel(ex_mem_1_jalout));
  MIPS_Ram_Adapter mips_ram_adapter_1 (
    .Addr(ex_mem_1_aluout), .DataIn(MDin), .dout(ram_1_data), .CLK(CLK),
    .CONTROL({MemWrite, ex_mem_1_memcontrolout}), .A(mips_ram_adapter_1_a), .din(mips_ram_adapter_1_din),
    .DataOut(mips_ram_adapter_1_dataout), .clk_2(mips_ram_adapter_1_clk_2), .str(mips_ram_adapter_1_str));
  RAM #(.addrWidth(10), .dataWidth(32), .bus("separate"), .Select("high")) ram_1 (
    .addr(mips_ram_adapter_1_a), .din(mips_ram_adapter_1_din), .data(ram_1_data),
    .str(mips_ram_adapter_1_str), .clk(mips_ram_adapter_1_clk_2));  // open: sel, ld, clr
  MEM_WB mem_wb_1 (
    .PCin(M_PC), .IRin(ex_mem_1_irout), .ALUin(multiplexer_8_out), .MEMin(mips_ram_adapter_1_dataout),
    .MEMTOREGin(ex_mem_1_memtoregout), .CLK(CLK), .PCout(WB_PC), .ALUout(mem_wb_1_aluout),
    .MEMout(mem_wb_1_memout), .MEMTOREGout(mem_wb_1_memtoregout),
    .\使能端_低电平有效_stall_高电平有效 (\ex_mem_1_使能传递端_低电平有效_stall_高电平有效 ), .REGWRITEin(ex_mem_1_regwriteout),
    .REGWRITEout(RegWrite), .W_in(ex_mem_1_w_out), .W_out(W_num), .\使能传递端_低电平有效_stall_高电平有效 (HaltOut));  // open: IRout, 同步清零_气泡_高电平有效, C0Win, C0Wout
  Multiplexer #(.select(1), .width(32), .disabled("Z"), .enable("false")) multiplexer_9 (
    .in0(mem_wb_1_aluout), .in1(mem_wb_1_memout), .out(RDin), .sel(mem_wb_1_memtoregout));

  // Other names for the same wires on the sheet: Din[31:0] = RDin; MEM_PC[31:0] = M_PC

  // Notes on the sheet:
  //   中断源
  //   PC+4
  //   JR
  //   J/JAL
  //   中断等待指示
  //   BEQ/BNE
  //   PC计数器
  //   指令存储器
  //   数码管输出
  //   contents of rom_1 (hex, n*v repeats v):
  //   20100000 20110000 20120000 20130000 36100000 36310001 36520002 36730003 ae100000 ae110004 ae120008
  //   ae13000c 2002000a 20110000 20120000 20130000 c
  //   PC+4
  //   JMP
  //   JR
  //   IR
  //   rs
  //   指令字
  //   rt
  //   imm
  //   shamt
  //   addr
  //   Syscall功能实现
  //   MemToReg
  //   MemControl
  //   AluOP
  //   AluSrcB
  //   RegWrite
  //   JAL
  //   RegDst
  //   Syscall
  //   rt
  //   rd
  //   为方便自动评测，需要输出流水线各段保存的PC值，注意是PC不是PC+4，另外ID段寄存器写入信息，Mem段内存写入信息也要输出
endmodule

module \气泡流水线  (
  output RegWrite,
  output MemWrite,
  output [31:0] IF_PC,
  output [31:0] ID_PC,
  output [31:0] EX_PC,
  output [31:0] M_PC,
  output [31:0] WB_PC,
  output [31:0] RDin,
  output [31:0] MDin,
  output [31:0] LedData
);

  wire and_1_out, branch, CLK, Col, comparator_1_eq, EX_Col_R1, EX_Col_R2, ex_mem_1_jalout,
       ex_mem_1_memtoregout, \ex_mem_1_使能传递端_低电平有效_stall_高电平有效 , EX_MemToReg, EX_RegWrite, Go, Halt, HaltOut,
       id_ex_1_alusrcbout, id_ex_1_jalout, \id_ex_1_使能传递端_低电平有效_stall_高电平有效 ,
       \if_id_1_使能传递端_低电平有效_stall_高电平有效 , IR1, IR2, IR3, JAL, JMP, JR, LoadUse, MEM_Col_R1, MEM_Col_R2,
       MEM_RegWrite, mem_wb_1_memtoregout, mips_alu_2_branch, mips_ram_adapter_1_clk_2,
       mips_ram_adapter_1_str, nor_1_out, not_1_out, or_1_out, or_2_out, R1_Used, R2_Used, RST, SignedExt,
       Syscall, W1, W2, W3, \单周期硬布线控制器_1_alu_src , \单周期硬布线控制器_1_memtoreg , \单周期硬布线控制器_1_regdst ,
       \单周期硬布线控制器_1_regwrite , \单周期硬布线控制器_1_syscall ;
  wire [1:0] or_4_out;
  wire [2:0] ex_mem_1_memcontrolout;
  wire [3:0] id_ex_1_memcontrolout, \单周期硬布线控制器_1_memcontrol ;
  wire [4:0] EX_W_num, id_ex_1_shamtout, MEM_W_num, multiplexer_5_out, multiplexer_6_out, R1_num, R2_num,
       W_num;
  wire [6:0] id_ex_1_aluopout, \单周期硬布线控制器_1_alu_op ;
  wire [9:0] mips_ram_adapter_1_a;
  wire [15:0] \总周期数 ;
  wire [31:0] adder_1_out, bit_extender_1_out, bit_extender_2_out, BRADDR, ex_mem_1_aluout, ex_mem_1_irout,
       ex_mem_1_pc_4out, id_ex_1_immout, id_ex_1_irout, id_ex_1_pc_4out, ID_R1, if_id_1_pc_4out, IR,
       mem_wb_1_aluout, mem_wb_1_memout, mips_alu_2_result, mips_ram_adapter_1_dataout,
       mips_ram_adapter_1_din, \mips_regifile_下降沿_1_r2 , multiplexer_1_out, multiplexer_4_out,
       multiplexer_7_out, multiplexer_8_out, R1, R2, ram_1_data, rom_1_data, shifter_1_out;

  Button \u_总复位  (.out(RST));
  Button _1 (.out(IR1));
  Button _2 (.out(IR2));
  Button _3 (.out(IR3));
  Button \u_继续运行  (.out(Go));
  LED #(.active("true")) led_1 (.in(W1));
  LED #(.active("true")) led_2 (.in(W2));
  LED #(.active("true")) led_3 (.in(W3));
  or or_1 (or_1_out, or_4_out[0], or_4_out[1]);
  Multiplexer #(.select(2), .width(32), .disabled("Z"), .enable("false")) multiplexer_1 (
    .in0(adder_1_out), .in1(ID_R1), .in2({ID_PC[31:28], IR[25:0], 2'b00}), .in3(BRADDR),
    .out(multiplexer_1_out), .sel(or_4_out));
  nor nor_1 (nor_1_out, 1'b0, Col);
  not not_1 (not_1_out, HaltOut);
  Hex_Digit_Display hex_digit_display_1 (.value(LedData[31:28]));  // open: dp
  or or_2 (or_2_out, JMP, JAL);
  or or_3 (or_4_out[1], or_2_out, branch);
  or or_4 (or_4_out[0], branch, JR);
  Register #(.width(32), .trigger("rising"), .Select("low")) PC (
    .D(multiplexer_1_out), .en(nor_1_out), .Q(IF_PC), .clk(CLK));  // open: clr
  Counter #(.width(16), .max('hffff), .ongoal("stay"), .trigger("rising"), .behavior("old")) \u_总周期数  (
    .count(not_1_out), .Q(\总周期数 ), .clk(CLK));  // open: load, D, carry, clr, preset
  Hex_Digit_Display hex_digit_display_2 (.value(LedData[23:20]));  // open: dp
  Hex_Digit_Display hex_digit_display_3 (.value(LedData[27:24]));  // open: dp
  Adder #(.width(32)) adder_1 (.a(IF_PC), .b(32'h4), .out(adder_1_out));  // open: cin, cout
  Hex_Digit_Display hex_digit_display_4 (.value(LedData[19:16]));  // open: dp
  Hex_Digit_Display hex_digit_display_5 (.value(LedData[15:12]));  // open: dp
  IF_ID if_id_1 (
    .PCin(IF_PC), .IRin(rom_1_data), .CLK(CLK), .PCout(ID_PC), .IRout(IR), .\同步清零_气泡_高电平有效 (or_1_out),
    .\使能端_低电平有效_stall_高电平有效 (1'b0), .PC_4in(adder_1_out), .PC_4out(if_id_1_pc_4out),
    .\使能传递端_低电平有效_stall_高电平有效 (\if_id_1_使能传递端_低电平有效_stall_高电平有效 ), .LoadUse(Col));
  ROM #(.addrWidth(10), .dataWidth(32), .Select("high")) rom_1 (.addr(IF_PC[11:2]), .data(rom_1_data));
  Hex_Digit_Display hex_digit_display_6 (.value(LedData[7:4]));  // open: dp
  Hex_Digit_Display hex_digit_display_7 (.value(LedData[11:8]));  // open: dp
  Clock #(.highDuration(1), .lowDuration(1)) clock_1 (.out(CLK));
  Hex_Digit_Display hex_digit_display_8 (.value(LedData[3:0]));  // open: dp
  assign bit_extender_1_out = {{16{1'b0}}, IR[15:0]};  // Bit_Extender bit_extender_1
  assign bit_extender_2_out = {{16{IR[15]}}, IR[15:0]};  // Bit_Extender bit_extender_2
  \数据相关检测  \u_数据相关检测_1  (
    .R1_Used(R1_Used), .R1_num(R1_num), .R2_Used(R2_Used), .R2_num(R2_num), .Collision(Col),
    .EX_RegWrite(EX_RegWrite), .EX_WriteReg_num(EX_W_num), .MEM_RegWrite(MEM_RegWrite),
    .MEM_WriteReg_num(MEM_W_num), .EX_Collision_R1(EX_Col_R1), .EX_Collision_R2(EX_Col_R2),
    .MEM_Collision_R1(MEM_Col_R1), .MEM_Collision_R2(MEM_Col_R2), .LoadUse(LoadUse), .Ex_MemToReg(EX_MemToReg));
  \单周期硬布线控制器  \u_单周期硬布线控制器_1  (
    .IR(IR), .ALU_OP(\单周期硬布线控制器_1_alu_op ), .MemToReg(\单周期硬布线控制器_1_memtoreg ),
    .MemControl(\单周期硬布线控制器_1_memcontrol ), .ALU_SRC(\单周期硬布线控制器_1_alu_src ),
    .RegWrite(\单周期硬布线控制器_1_regwrite ), .SysCALL(\单周期硬布线控制器_1_syscall ), .SignedExt(SignedExt),
    .RegDst(\单周期硬布线控制器_1_regdst ), .JR(JR), .JMP(JMP), .JAL(JAL), .R1_Used(R1_Used), .R2_Used(R2_Used));  // open: C0Reg
  Multiplexer #(.select(1), .width(5), .disabled("Z"), .enable("false")) multiplexer_2 (
    .in0(IR[25:21]), .in1(5'b00010), .out(R1_num), .sel(\单周期硬布线控制器_1_syscall ));
  Multiplexer #(.select(1), .width(5), .disabled("Z"), .enable("false")) multiplexer_3 (
    .in0(IR[20:16]), .in1(5'b00100), .out(R2_num), .sel(\单周期硬布线控制器_1_syscall ));
  Multiplexer #(.select(1), .width(32), .disabled("Z"), .enable("false")) multiplexer_4 (
    .in0(bit_extender_1_out), .in1(bit_extender_2_out), .out(multiplexer_4_out), .sel(SignedExt));
  Multiplexer #(.select(1), .width(5), .disabled("Z"), .enable("false")) multiplexer_5 (
    .in0(IR[20:16]), .in1(IR[15:11]), .out(multiplexer_5_out), .sel(\单周期硬布线控制器_1_regdst ));
  Multiplexer #(.select(1), .width(5), .disabled("Z"), .enable("false")) multiplexer_6 (
    .in0(multiplexer_5_out), .in1({5{1'b1}}), .out(multiplexer_6_out), .sel(JAL));
  \MIPS_Regifile_下降沿  \mips_regifile_下降沿_1  (
    .Din(RDin), .Clk(CLK), .R1(ID_R1), .R2(\mips_regifile_下降沿_1_r2 ), .WE(RegWrite), .W_num(W_num),
    .R1_num(R1_num), .R2_num(R2_num));
  Adder #(.width(32)) adder_2 (.a(if_id_1_pc_4out), .b(shifter_1_out), .out(BRADDR));  // open: cin, cout
  Shifter #(.width(32), .shift("ll")) shifter_1 (.in(multiplexer_4_out), .\dist (5'b00010), .out(shifter_1_out));
  MIPS_ALU mips_alu_1 (
    .X(ID_R1), .Y(\mips_regifile_下降沿_1_r2 ), .AluOP(\单周期硬布线控制器_1_alu_op ), .Branch(branch));  // open: Result, Result_2, shamt
  Comparator #(.width(32), .mode("unsigned")) comparator_1 (.a(R1), .b(32'h32), .eq(comparator_1_eq));  // open: gt, lt
  and and_1 (and_1_out, ~comparator_1_eq, Syscall);  // AND_Gate
  Register #(.width(32), .trigger("rising"), .Select("low")) register_1 (
    .D(R2), .en(and_1_out), .Q(LedData), .clk(CLK));  // open: clr
  ID_EX id_ex_1 (
    .PCin(ID_PC), .IRin(IR), .Ain(ID_R1), .Bin(\mips_regifile_下降沿_1_r2 ), .IMMin(multiplexer_4_out),
    .MEMTOREGin(\单周期硬布线控制器_1_memtoreg ), .MEMCONTROLin(\单周期硬布线控制器_1_memcontrol ),
    .ALUOPin(\单周期硬布线控制器_1_alu_op ), .ALUSRCBin(\单周期硬布线控制器_1_alu_src ), .CLK(CLK), .PCout(EX_PC),
    .IRout(id_ex_1_irout), .Aout(R1), .Bout(R2), .IMMout(id_ex_1_immout), .MEMTOREGout(EX_MemToReg),
    .MEMCONTROLout(id_ex_1_memcontrolout), .ALUOPout(id_ex_1_aluopout), .ALUSRCBout(id_ex_1_alusrcbout),
    .\同步清零_气泡_高电平有效 (Col), .\使能端_低电平有效_stall_高电平有效 (\if_id_1_使能传递端_低电平有效_stall_高电平有效 ), .SHAMTin(IR[10:6]),
    .SHAMTout(id_ex_1_shamtout), .REGWRITEin(\单周期硬布线控制器_1_regwrite ), .REGWRITEout(EX_RegWrite),
    .W_in(multiplexer_6_out), .W_out(EX_W_num), .JALin(JAL), .JALout(id_ex_1_jalout),
    .\使能传递端_低电平有效_stall_高电平有效 (\id_ex_1_使能传递端_低电平有效_stall_高电平有效 ), .PC_4in(if_id_1_pc_4out),
    .PC_4out(id_ex_1_pc_4out), .RSTin(\单周期硬布线控制器_1_syscall ), .RSTout(Syscall));  // open: R1_SELin, R1_SELout, R2_SELin, R2_SELout, C0Win, C0Wout, BRPin, BRPout
  and and_2 (Halt, comparator_1_eq, Syscall);
  Multiplexer #(.select(1), .width(32), .disabled("Z"), .enable("false")) multiplexer_7 (
    .in0(R2), .in1(id_ex_1_immout), .out(multiplexer_7_out), .sel(id_ex_1_alusrcbout));
  LED #(.active("true")) led_4 (.in(mips_alu_2_branch));
  MIPS_ALU mips_alu_2 (
    .X(R1), .Y(multiplexer_7_out), .AluOP(id_ex_1_aluopout), .Branch(mips_alu_2_branch),
    .Result(mips_alu_2_result), .shamt(id_ex_1_shamtout));  // open: Result_2
  EX_MEM ex_mem_1 (
    .PCin(EX_PC), .IRin(id_ex_1_irout), .Bin(R2), .MEMTOREGin(EX_MemToReg),
    .MEMCONTROLin(id_ex_1_memcontrolout), .CLK(CLK), .PCout(M_PC), .IRout(ex_mem_1_irout), .Bout(MDin),
    .MEMTOREGout(ex_mem_1_memtoregout), .MEMCONTROLout({MemWrite, ex_mem_1_memcontrolout}),
    .\使能端_低电平有效_stall_高电平有效 (\id_ex_1_使能传递端_低电平有效_stall_高电平有效 ), .ALUin(mips_alu_2_result),
    .ALUout(ex_mem_1_aluout), .REGWRITEin(EX_RegWrite), .REGWRITEout(MEM_RegWrite), .W_in(EX_W_num),
    .W_out(MEM_W_num), .JALin(id_ex_1_jalout), .JALout(ex_mem_1_jalout),
    .\使能传递端_低电平有效_stall_高电平有效 (\ex_mem_1_使能传递端_低电平有效_stall_高电平有效 ), .PC_4in(id_ex_1_pc_4out),
    .PC_4out(ex_mem_1_pc_4out));  // open: 同步清零_气泡_高电平有效, C0Win, C0Wout
  Multiplexer #(.select(1), .width(32), .disabled("Z"), .enable("false")) multiplexer_8 (
    .in0(ex_mem_1_aluout), .in1(ex_mem_1_pc_4out), .out(multiplexer_8_out), .sel(ex_mem_1_jalout));
  MIPS_Ram_Adapter mips_ram_adapter_1 (
    .Addr(ex_mem_1_aluout), .DataIn(MDin), .dout(ram_1_data), .CLK(CLK),
    .CONTROL({MemWrite, ex_mem_1_memcontrolout}), .A(mips_ram_adapter_1_a), .din(mips_ram_adapter_1_din),
    .DataOut(mips_ram_adapter_1_dataout), .clk_2(mips_ram_adapter_1_clk_2), .str(mips_ram_adapter_1_str));
  RAM #(.addrWidth(10), .dataWidth(32), .bus("separate"), .Select("high")) ram_1 (
    .addr(mips_ram_adapter_1_a), .din(mips_ram_adapter_1_din), .data(ram_1_data),
    .str(mips_ram_adapter_1_str), .clk(mips_ram_adapter_1_clk_2));  // open: sel, ld, clr
  MEM_WB mem_wb_1 (
    .PCin(M_PC), .IRin(ex_mem_1_irout), .ALUin(multiplexer_8_out), .MEMin(mips_ram_adapter_1_dataout),
    .MEMTOREGin(ex_mem_1_memtoregout), .CLK(CLK), .PCout(WB_PC), .ALUout(mem_wb_1_aluout),
    .MEMout(mem_wb_1_memout), .MEMTOREGout(mem_wb_1_memtoregout),
    .\使能端_低电平有效_stall_高电平有效 (\ex_mem_1_使能传递端_低电平有效_stall_高电平有效 ), .REGWRITEin(MEM_RegWrite),
    .REGWRITEout(RegWrite), .W_in(MEM_W_num), .W_out(W_num), .\使能传递端_低电平有效_stall_高电平有效 (HaltOut));  // open: IRout, 同步清零_气泡_高电平有效, C0Win, C0Wout
  Multiplexer #(.select(1), .width(32), .disabled("Z"), .enable("false")) multiplexer_9 (
    .in0(mem_wb_1_aluout), .in1(mem_wb_1_memout), .out(RDin), .sel(mem_wb_1_memtoregout));

  // Other names for the same wires on the sheet: JADDR[25:0] = IR[25:0]; MEM_PC[31:0] = M_PC

  // Notes on the sheet:
  //   中断源
  //   PC+4
  //   JR
  //   J/JAL
  //   中断等待指示
  //   总复位信号应将除ROM以外所有存储组件全部清零
  //   BEQ/BNE
  //   PC计数器
  //   指令存储器
  //   数码管输出
  //   contents of rom_1 (hex, n*v repeats v):
  //   20110001 8000c05 20110001 20120002 20130003 8000c09 20110001 20120002 20130003 8000c0d 20110001
  //   20120002 20130003 8000c11 20110001 20120002 20130003 c000cb8 20100001 20110001 118fc0 112020
  //   20020022 c 118882 12200001 8000c15 112020 20020022 c 20110001 118880 112020 20020022 c 12200001
  //   8000c1f 20110001 118fc0 112020 20020022 c 1188c3 112020 20020022 c 118903 112020 20020022 c 118903
  //   112020 20020022 c 118903 112020 20020022 c 118903 112020 20020022 c 118903 112020 20020022 c 118903
  //   112020 20020022 c 118903 112020 20020022 c 20100001 109fc0 139fc3 8021 2012000c 24160003 26100001
  //   3210000f 20080008 20090001 139900 2709825 132020 20020022 c 1094022 1500fff9 22100001 2018000f
  //   2188024 108700 20080008 20090001 139902 2709825 132021 20020022 c 1094022 1500fff9 108702 2c9b022
  //   12c00001 8000c50 4020 1084027 84400 3508ffff 82021 20020022 c 2010ffff 20110000 ae300000 22100001
  //   22310004 ae300000 22100001 22310004 ae300000 22100001 22310004 ae300000 22100001 22310004 ae300000
  //   22100001 22310004 ae300000 22100001 22310004 ae300000 22100001 22310004 ae300000 22100001 22310004
  //   ae300000 22100001 22310004 ae300000 22100001 22310004 ae300000 22100001 22310004 ae300000 22100001
  //   22310004 ae300000 22100001 22310004 ae300000 22100001 22310004 ae300000 22100001 22310004 ae300000
  //   22100001 22310004 22100001 8020 2011003c 8e130000 8e340000 274402a 11000002 ae330000 ae140000
  //   2231fffc 1611fff8 102020 20020022 c 22100004 2011003c 1611fff2 20020032 c 20100000 22100001 102020
  //   20020022 c 22100002 102020 20020022 c 22100003 102020 20020022 c 22100004 102020 20020022 c 22100005
  //   102020 20020022 c 22100006 102020 20020022 c 22100007 102020 20020022 c 22100008 102020 20020022
  //   20020022 c 3e00008
  //   PC+4
  //   数码管输出应该用寄存器锁存，否则显示数据只能一闪而过
  //   JMP
  //   JR
  //   IR
  //   rs
  //   rt
  //   addr
  //   imm
  //   shamt
  //   数据相关检测
  //   Syscall
  //   MemToReg
  //   MemControl
  //   AluOP
  //   AluSrcB
  //   RegWrite
  //   JAL
  //   RegDst
  //   rt
  //   rd
  //   Syscall功能实现
  //   v0
  //   a0
  //   为方便自动评测，需要输出流水线各段保存的PC值，注意是PC不是PC+4，另外ID段寄存器写入信息，Mem段内存写入信息也要输出
endmodule

module \重定向流水线  (
  output RegWrite,
  output MemWrite,
  output [31:0] IF_PC,
  output [31:0] ID_PC,
  output [31:0] EX_PC,
  output [31:0] M_PC,
  output [31:0] WB_PC,
  output [31:0] RDin,
  output [31:0] MDin,
  output [31:0] LedData
);

  wire and_1_out, and_2_out, and_3_out, and_5_out, and_6_out, BFail, bht_1_p1, branch, C0W, CLK, Col,
       comparator_1_eq, comparator_2_eq, comparator_3_eq, EX_BRP, EX_ID_RST, EX_Jump, ex_mem_1_c0wout,
       ex_mem_1_jalout, ex_mem_1_memtoregout, \ex_mem_1_使能传递端_低电平有效_stall_高电平有效 , EX_MemToReg, EX_RegWrite,
       EX_RST, Go, Halt, HaltOut, ID_BRP, id_ex_1_alusrcbout, id_ex_1_c0wout, id_ex_1_jalout,
       \id_ex_1_使能传递端_低电平有效_stall_高电平有效 , ID_Jump, ID_RST, \if_id_1_使能传递端_低电平有效_stall_高电平有效 , IR1, IR2, IR3,
       IRC, JAL, JMP, JR, LoadUse, MEM_RegWrite, mem_wb_1_memtoregout, mips_ram_adapter_1_clk_2,
       mips_ram_adapter_1_str, nor_1_out, not_1_out, or_6_out, or_7_out, R1_Used, R2_Used, RST, SignedExt,
       Syscall, W1, W2, W3, \单周期硬布线控制器_1_alu_src , \单周期硬布线控制器_1_memtoreg , \单周期硬布线控制器_1_regdst ,
       \单周期硬布线控制器_1_regwrite ;
  wire [1:0] C0Reg, id_ex_1_r1_selout, id_ex_1_r2_selout, or_2_out, R1_Sel, R2_Sel, \中断电路_下降沿_1_a ;
  wire [2:0] ex_mem_1_memcontrolout;
  wire [3:0] id_ex_1_memcontrolout, IRS, W, \单周期硬布线控制器_1_memcontrol ;
  wire [4:0] EX_W_num, id_ex_1_shamtout, MEM_W_num, multiplexer_8_out, multiplexer_9_out, multiplexer_11_out,
       multiplexer_14_out, R1_num, R2_num, W_num;
  wire [6:0] AluOP, id_ex_1_aluopout;
  wire [9:0] mips_ram_adapter_1_a;
  wire [15:0] \总周期数 ;
  wire [31:0] adder_1_out, bht_1_p2, bit_extender_1_out, bit_extender_2_out, BRADDR, BRPC, EPC,
       ex_mem_1_aluout, ex_mem_1_irout, ex_mem_1_pc_4out, EX_PC_4, id_ex_1_aout, id_ex_1_bout,
       id_ex_1_immout, id_ex_1_irout, ID_R1, ID_R2, if_id_1_pc_4out, IR, IRPC, JPC, mem_wb_1_aluout,
       mem_wb_1_memout, mips_ram_adapter_1_dataout, mips_ram_adapter_1_din, multiplexer_1_out,
       multiplexer_2_out, multiplexer_5_out, multiplexer_6_out, multiplexer_13_out, multiplexer_17_out,
       multiplexer_18_out, multiplexer_19_out, R, R1, R2, ram_1_data, RegD, register_1_q, rom_1_data,
       shifter_1_out, Status;

  Button \u_总复位  (.out(RST));
  Button _1 (.out(IR1));
  Button _2 (.out(IR2));
  Button _3 (.out(IR3));
  Button \u_继续运行  (.out(Go));
  LED #(.active("true")) led_1 (.in(W1));
  LED #(.active("true")) led_2 (.in(W2));
  LED #(.active("true")) led_3 (.in(W3));
  or or_1 (or_2_out[1], and_2_out, EX_RST);
  or or_2 (or_2_out[0], EX_RST, and_3_out);
  Multiplexer #(.select(2), .width(32), .disabled("Z"), .enable("false")) multiplexer_1 (
    .in0(IF_PC), .in1(R1), .in2({ID_PC[31:28], IR[25:0], 2'b00}), .in3(BRPC), .out(multiplexer_1_out),
    .sel(or_2_out));
  Multiplexer #(.select(2), .width(32), .disabled("Z"), .enable("false")) multiplexer_2 (
    .in0(multiplexer_6_out), .in1(R1), .in2({ID_PC[31:28], IR[25:0], 2'b00}), .in3(BRPC),
    .out(multiplexer_2_out), .sel(or_2_out));
  Multiplexer #(.select(1), .width(32), .disabled("Z"), .enable("false")) multiplexer_3 (
    .in0({ID_PC[31:28], IR[25:0], 2'b00}), .in1(R1), .out(JPC), .sel(JR));
  not not_1 (not_1_out, HaltOut);
  Hex_Digit_Display hex_digit_display_1 (.value(LedData[31:28]));  // open: dp
  Multiplexer #(.select(1), .width(32), .disabled("Z"), .enable("false")) multiplexer_4 (
    .in0(multiplexer_1_out), .in1(ID_PC), .out(EPC), .sel(ID_BRP));
  or or_3 (ID_BRP, AluOP[4], AluOP[5], AluOP[6]);
  Multiplexer #(.select(1), .width(32), .disabled("Z"), .enable("false")) multiplexer_5 (
    .in0(multiplexer_2_out), .in1(IRPC), .out(multiplexer_5_out), .sel(IRC));
  nor nor_1 (nor_1_out, LoadUse, and_1_out);
  and and_1 (and_1_out, ~IRC, Halt);  // AND_Gate
  Multiplexer #(.select(1), .width(32), .disabled("Z"), .enable("false")) multiplexer_6 (
    .in0(adder_1_out), .in1(bht_1_p2), .out(multiplexer_6_out), .sel(bht_1_p1));
  Multiplexer #(.select(1), .width(32), .disabled("Z"), .enable("false")) multiplexer_7 (
    .in0(EX_PC_4), .in1(BRADDR), .out(BRPC), .sel(branch));
  Counter #(.width(16), .max('hffff), .ongoal("stay"), .trigger("rising"), .behavior("old")) \u_总周期数  (
    .count(not_1_out), .Q(\总周期数 ), .clk(CLK));  // open: load, D, carry, clr, preset
  not not_2 (EX_Jump, comparator_1_eq);
  Comparator #(.width(32), .mode("unsigned")) comparator_1 (.a(BRPC), .b(IF_PC), .eq(comparator_1_eq));  // open: gt, lt
  not not_3 (ID_Jump, comparator_2_eq);
  Comparator #(.width(32), .mode("unsigned")) comparator_2 (.a(JPC), .b(IF_PC), .eq(comparator_2_eq));  // open: gt, lt
  or or_4 (BFail, EX_ID_RST, EX_RST);
  Hex_Digit_Display hex_digit_display_2 (.value(LedData[27:24]));  // open: dp
  Hex_Digit_Display hex_digit_display_3 (.value(LedData[23:20]));  // open: dp
  or or_5 (ID_RST, and_3_out, and_2_out);
  and and_2 (and_2_out, or_6_out, ID_Jump);
  and and_3 (and_3_out, JR, ID_Jump);
  Register #(.width(32), .trigger("rising"), .Select("low")) PC (
    .D(multiplexer_5_out), .en(nor_1_out), .Q(IF_PC), .clk(CLK));  // open: clr
  // BHT bht_1: pin names not known; wires that end beside it: bht_1_p1, bht_1_p2, CLK, IF_PC, EX_PC, BRADDR, BFail, EX_ID_RST
  Hex_Digit_Display hex_digit_display_4 (.value(LedData[19:16]));  // open: dp
  Hex_Digit_Display hex_digit_display_5 (.value(LedData[15:12]));  // open: dp
  or or_6 (or_6_out, JMP, JAL);
  and and_4 (EX_RST, EX_Jump, EX_BRP);
  Hex_Digit_Display hex_digit_display_6 (.value(LedData[7:4]));  // open: dp
  Hex_Digit_Display hex_digit_display_7 (.value(LedData[11:8]));  // open: dp
  Clock #(.highDuration(1), .lowDuration(1)) clock_1 (.out(CLK));
  or or_7 (or_7_out, ID_RST, EX_RST, IRC);
  Adder #(.width(32)) adder_1 (.a(IF_PC), .b(32'h4), .out(adder_1_out));  // open: cin, cout
  Multiplexer #(.select(1), .width(5), .disabled("Z"), .enable("false")) multiplexer_8 (
    .in0(R1_num), .in1(5'b01110), .out(multiplexer_8_out), .sel(C0Reg[0]));
  Hex_Digit_Display hex_digit_display_8 (.value(LedData[3:0]));  // open: dp
  IF_ID if_id_1 (
    .PCin(IF_PC), .IRin(rom_1_data), .CLK(CLK), .PCout(ID_PC), .IRout(IR), .\同步清零_气泡_高电平有效 (or_7_out),
    .\使能端_低电平有效_stall_高电平有效 (and_5_out), .PC_4in(adder_1_out), .PC_4out(if_id_1_pc_4out),
    .\使能传递端_低电平有效_stall_高电平有效 (\if_id_1_使能传递端_低电平有效_stall_高电平有效 ), .LoadUse(LoadUse));
  ROM #(.addrWidth(10), .dataWidth(32), .Select("high")) rom_1 (.addr(IF_PC[11:2]), .data(rom_1_data));
  and and_5 (and_5_out, ~IRC, Halt);  // AND_Gate
  \数据相关检测  \u_数据相关检测_1  (
    .R1_Used(R1_Used), .R1_num(multiplexer_8_out), .R2_Used(R2_Used), .R2_num(R2_num), .Collision(Col),
    .EX_RegWrite(EX_RegWrite), .EX_WriteReg_num(EX_W_num), .MEM_RegWrite(MEM_RegWrite),
    .MEM_WriteReg_num(MEM_W_num), .EX_Collision_R1(R1_Sel[1]), .EX_Collision_R2(R2_Sel[1]),
    .MEM_Collision_R1(R1_Sel[0]), .MEM_Collision_R2(R2_Sel[0]), .LoadUse(LoadUse), .Ex_MemToReg(EX_MemToReg));
  \单周期硬布线控制器  \u_单周期硬布线控制器_1  (
    .IR(IR), .ALU_OP(AluOP), .MemToReg(\单周期硬布线控制器_1_memtoreg ), .MemControl(\单周期硬布线控制器_1_memcontrol ),
    .ALU_SRC(\单周期硬布线控制器_1_alu_src ), .RegWrite(\单周期硬布线控制器_1_regwrite ), .SysCALL(Syscall),
    .SignedExt(SignedExt), .RegDst(\单周期硬布线控制器_1_regdst ), .JR(JR), .JMP(JMP), .JAL(JAL), .R1_Used(R1_Used),
    .R2_Used(R2_Used), .C0Reg(C0Reg));
  Multiplexer #(.select(1), .width(5), .disabled("Z"), .enable("false")) multiplexer_9 (
    .in0(IR[20:16]), .in1(IR[15:11]), .out(multiplexer_9_out), .sel(\单周期硬布线控制器_1_regdst ));
  Multiplexer #(.select(1), .width(5), .disabled("Z"), .enable("false")) multiplexer_10 (
    .in0(IR[25:21]), .in1(5'b00010), .out(R1_num), .sel(Syscall));
  Multiplexer #(.select(1), .width(5), .disabled("Z"), .enable("false")) multiplexer_11 (
    .in0(IR[15:11]), .in1(IR[20:16]), .out(multiplexer_11_out), .sel(\单周期硬布线控制器_1_regdst ));
  Multiplexer #(.select(1), .width(5), .disabled("Z"), .enable("false")) multiplexer_12 (
    .in0(multiplexer_11_out), .in1(5'b00100), .out(R2_num), .sel(Syscall));
  assign bit_extender_1_out = {{16{1'b0}}, IR[15:0]};  // Bit_Extender bit_extender_1
  assign bit_extender_2_out = {{16{IR[15]}}, IR[15:0]};  // Bit_Extender bit_extender_2
  Multiplexer #(.select(1), .width(32), .disabled("Z"), .enable("false")) multiplexer_13 (
    .in0(bit_extender_1_out), .in1(bit_extender_2_out), .out(multiplexer_13_out), .sel(SignedExt));
  Multiplexer #(.select(1), .width(5), .disabled("Z"), .enable("false")) multiplexer_14 (
    .in0(multiplexer_9_out), .in1({5{1'b1}}), .out(multiplexer_14_out), .sel(JAL));
  Multiplexer #(.select(2), .width(32), .disabled("Z"), .enable("false")) multiplexer_15 (
    .in0(ID_R1), .in1(RegD), .in2(R), .in3(R), .out(R1), .sel(R1_Sel));
  Multiplexer #(.select(2), .width(32), .disabled("Z"), .enable("false")) multiplexer_16 (
    .in0(ID_R2), .in1(RegD), .in2(R), .in3(R), .out(R2), .sel(R2_Sel));
  \MIPS_Regifile_下降沿_CP0  \mips_regifile_下降沿_cp0_1  (
    .R1(ID_R1), .Din(RDin), .Clk(CLK), .R1_num(R1_num), .Status(Status), .W_num(W_num), .R2(ID_R2),
    .EPC(EPC), .WE(RegWrite), .IR(IRC), .R2_num(R2_num), .C0Reg(C0Reg), .C0W(C0W));
  Shifter #(.width(32), .shift("ll")) shifter_1 (.in(multiplexer_13_out), .\dist (5'b00010), .out(shifter_1_out));
  MIPS_ALU mips_alu_1 (.X(ID_R1), .Y(ID_R2), .AluOP(AluOP), .Branch(branch));  // open: Result, Result_2, shamt
  Adder #(.width(32)) adder_2 (.a(if_id_1_pc_4out), .b(shifter_1_out), .out(BRADDR));  // open: cin, cout
  Comparator #(.width(32), .mode("unsigned")) comparator_3 (.a(R1), .b(32'h32), .eq(comparator_3_eq));  // open: gt, lt
  and and_6 (and_6_out, ~comparator_3_eq, Syscall);  // AND_Gate
  ID_EX id_ex_1 (
    .PCin(ID_PC), .IRin(IR), .Ain(ID_R1), .Bin(ID_R2), .IMMin(multiplexer_13_out),
    .MEMTOREGin(\单周期硬布线控制器_1_memtoreg ), .MEMCONTROLin(\单周期硬布线控制器_1_memcontrol ), .ALUOPin(AluOP),
    .ALUSRCBin(\单周期硬布线控制器_1_alu_src ), .CLK(CLK), .PCout(EX_PC), .IRout(id_ex_1_irout), .Aout(id_ex_1_aout),
    .Bout(id_ex_1_bout), .IMMout(id_ex_1_immout), .MEMTOREGout(EX_MemToReg),
    .MEMCONTROLout(id_ex_1_memcontrolout), .ALUOPout(id_ex_1_aluopout), .ALUSRCBout(id_ex_1_alusrcbout),
    .\同步清零_气泡_高电平有效 (LoadUse), .\使能端_低电平有效_stall_高电平有效 (\if_id_1_使能传递端_低电平有效_stall_高电平有效 ),
    .SHAMTin(IR[10:6]), .SHAMTout(id_ex_1_shamtout), .REGWRITEin(\单周期硬布线控制器_1_regwrite ),
    .REGWRITEout(EX_RegWrite), .W_in(multiplexer_14_out), .W_out(EX_W_num), .JALin(JAL),
    .JALout(id_ex_1_jalout), .\使能传递端_低电平有效_stall_高电平有效 (\id_ex_1_使能传递端_低电平有效_stall_高电平有效 ),
    .PC_4in(if_id_1_pc_4out), .PC_4out(EX_PC_4), .R1_SELin(R1_Sel), .R1_SELout(id_ex_1_r1_selout),
    .R2_SELin(R2_Sel), .R2_SELout(id_ex_1_r2_selout), .C0Win(C0Reg[1]), .C0Wout(id_ex_1_c0wout),
    .BRPin(ID_BRP), .BRPout(EX_BRP), .RSTin(ID_RST), .RSTout(EX_ID_RST));
  Register #(.width(32), .trigger("rising"), .Select("low")) register_1 (
    .D(R2), .en(and_6_out), .Q(register_1_q), .clk(CLK));  // open: clr
  Register #(.width(32), .trigger("rising"), .Select("low")) register_2 (
    .D(register_1_q), .Q(LedData), .clk(CLK));  // open: en, clr
  and and_7 (Halt, comparator_3_eq, Syscall);
  Multiplexer #(.select(2), .width(32), .disabled("Z"), .enable("false")) multiplexer_17 (
    .in0(id_ex_1_aout), .in1(RDin), .in2(RegD), .in3(RegD), .out(multiplexer_17_out), .sel(id_ex_1_r1_selout));
  Multiplexer #(.select(2), .width(32), .disabled("Z"), .enable("false")) multiplexer_18 (
    .in0(id_ex_1_bout), .in1(RDin), .in2(RegD), .in3(RegD), .out(multiplexer_18_out), .sel(id_ex_1_r2_selout));
  Multiplexer #(.select(1), .width(32), .disabled("Z"), .enable("false")) multiplexer_19 (
    .in0(multiplexer_18_out), .in1(id_ex_1_immout), .out(multiplexer_19_out), .sel(id_ex_1_alusrcbout));
  MIPS_ALU mips_alu_2 (
    .X(multiplexer_17_out), .Y(multiplexer_19_out), .AluOP(id_ex_1_aluopout), .Result(R),
    .shamt(id_ex_1_shamtout));  // open: Branch, Result_2
  EX_MEM ex_mem_1 (
    .PCin(EX_PC), .IRin(id_ex_1_irout), .Bin(multiplexer_18_out), .MEMTOREGin(EX_MemToReg),
    .MEMCONTROLin(id_ex_1_memcontrolout), .CLK(CLK), .PCout(M_PC), .IRout(ex_mem_1_irout), .Bout(MDin),
    .MEMTOREGout(ex_mem_1_memtoregout), .MEMCONTROLout({MemWrite, ex_mem_1_memcontrolout}),
    .\使能端_低电平有效_stall_高电平有效 (\id_ex_1_使能传递端_低电平有效_stall_高电平有效 ), .ALUin(R), .ALUout(ex_mem_1_aluout),
    .REGWRITEin(EX_RegWrite), .REGWRITEout(MEM_RegWrite), .W_in(EX_W_num), .W_out(MEM_W_num),
    .JALin(id_ex_1_jalout), .JALout(ex_mem_1_jalout),
    .\使能传递端_低电平有效_stall_高电平有效 (\ex_mem_1_使能传递端_低电平有效_stall_高电平有效 ), .PC_4in(EX_PC_4),
    .PC_4out(ex_mem_1_pc_4out), .C0Win(id_ex_1_c0wout), .C0Wout(ex_mem_1_c0wout));  // open: 同步清零_气泡_高电平有效
  \中断电路_下降沿  \u_中断电路_下降沿_1  (.CLK(CLK), .IRout(IRC), .A(\中断电路_下降沿_1_a ), .IRin(IRS), .Status(Status), .W(W));
  Multiplexer #(.select(1), .width(32), .disabled("Z"), .enable("false")) multiplexer_20 (
    .in0(ex_mem_1_aluout), .in1(ex_mem_1_pc_4out), .out(RegD), .sel(ex_mem_1_jalout));
  ROM #(.addrWidth(2), .dataWidth(32), .Select("low")) rom_2 (.addr(\中断电路_下降沿_1_a ), .data(IRPC));
  MIPS_Ram_Adapter mips_ram_adapter_1 (
    .Addr(ex_mem_1_aluout), .DataIn(MDin), .dout(ram_1_data), .CLK(CLK),
    .CONTROL({MemWrite, ex_mem_1_memcontrolout}), .A(mips_ram_adapter_1_a), .din(mips_ram_adapter_1_din),
    .DataOut(mips_ram_adapter_1_dataout), .clk_2(mips_ram_adapter_1_clk_2), .str(mips_ram_adapter_1_str));
  MEM_WB mem_wb_1 (
    .PCin(M_PC), .IRin(ex_mem_1_irout), .ALUin(RegD), .MEMin(mips_ram_adapter_1_dataout),
    .MEMTOREGin(ex_mem_1_memtoregout), .CLK(CLK), .PCout(WB_PC), .ALUout(mem_wb_1_aluout),
    .MEMout(mem_wb_1_memout), .MEMTOREGout(mem_wb_1_memtoregout),
    .\使能端_低电平有效_stall_高电平有效 (\ex_mem_1_使能传递端_低电平有效_stall_高电平有效 ), .REGWRITEin(MEM_RegWrite),
    .REGWRITEout(RegWrite), .W_in(MEM_W_num), .W_out(W_num), .\使能传递端_低电平有效_stall_高电平有效 (HaltOut),
    .C0Win(ex_mem_1_c0wout), .C0Wout(C0W));  // open: IRout, 同步清零_气泡_高电平有效
  RAM #(.addrWidth(10), .dataWidth(32), .bus("separate"), .Select("high")) ram_1 (
    .addr(mips_ram_adapter_1_a), .din(mips_ram_adapter_1_din), .data(ram_1_data),
    .str(mips_ram_adapter_1_str), .clk(mips_ram_adapter_1_clk_2));  // open: sel, ld, clr
  Multiplexer #(.select(1), .width(32), .disabled("Z"), .enable("false")) multiplexer_21 (
    .in0(mem_wb_1_aluout), .in1(mem_wb_1_memout), .out(RDin), .sel(mem_wb_1_memtoregout));

  // Other names for the same wires on the sheet: JADDR[25:0] = IR[25:0]; MEM_PC[31:0] = M_PC; RegW = RegWrite

  // Notes on the sheet:
  //   中断源
  //   NextPC
  //   JR
  //   J/JAL
  //   PC计数器
  //   动态分支预测
  //   中断等待指示
  //   总复位信号应将除ROM以外所有存储组件全部清零
  //   BEQ/BNE
  //   数码管输出
  //   数据相关检测
  //   数码管输出应该用寄存器锁存，否则显示数据只能一闪而过
  //   指令存储器
  //   PC+4
  //   指令字
  //   contents of rom_1 (hex, n*v repeats v):
  //   20110001 8000c05 20110001 20120002 20130003 8000c09 20110001 20120002 20130003 8000c0d 20110001
  //   20120002 20130003 8000c11 20110001 20120002 20130003 c000cb8 20100001 20110001 118fc0 112020
  //   20020022 c 118882 12200001 8000c15 112020 20020022 c 20110001 118880 112020 20020022 c 12200001
  //   8000c1f 20110001 118fc0 112020 20020022 c 1188c3 112020 20020022 c 118903 112020 20020022 c 118903
  //   112020 20020022 c 118903 112020 20020022 c 118903 112020 20020022 c 118903 112020 20020022 c 118903
  //   112020 20020022 c 118903 112020 20020022 c 20100001 109fc0 139fc3 8021 2012000c 24160003 26100001
  //   3210000f 20080008 20090001 139900 2709825 132020 20020022 c 1094022 1500fff9 22100001 2018000f
  //   2188024 108700 20080008 20090001 139902 2709825 132021 20020022 c 1094022 1500fff9 108702 2c9b022
  //   12c00001 8000c50 4020 1084027 84400 3508ffff 82021 20020022 c 2010ffff 20110000 ae300000 22100001
  //   22310004 ae300000 22100001 22310004 ae300000 22100001 22310004 ae300000 22100001 22310004 ae300000
  //   22100001 22310004 ae300000 22100001 22310004 ae300000 22100001 22310004 ae300000 22100001 22310004
  //   ae300000 22100001 22310004 ae300000 22100001 22310004 ae300000 22100001 22310004 ae300000 22100001
  //   22310004 ae300000 22100001 22310004 ae300000 22100001 22310004 ae300000 22100001 22310004 ae300000
  //   22100001 22310004 22100001 8020 2011003c 8e130000 8e340000 274402a 11000002 ae330000 ae140000
  //   2231fffc 1611fff8 102020 20020022 c 22100004 2011003c 1611fff2 20020032 c 20100000 22100001 102020
  //   20020022 c 22100002 102020 20020022 c 22100003 102020 20020022 c 22100004 102020 20020022 c 22100005
  //   102020 20020022 c 22100006 102020 20020022 c 22100007 102020 20020022 c 22100008 102020 20020022
  //   20020022 c 3e00008
  //   JMP
  //   JR
  //   IR
  //   rt
  //   rd
  //   rs
  //   rd
  //   rt
  //   addr
  //   imm
  //   shamt
  //   JAL
  //   Syscall
  //   MemToReg
  //   MemControl
  //   AluOP
  //   AluSrcB
  //   RegWrite
  //   RegDst
  //   为方便自动评测，需要输出流水线各段保存的PC值，注意是PC不是PC+4，另外ID段寄存器写入信息，Mem段内存写入信息也要输出
  //   Syscall功能实现
  //   v0
  //   a0
  //   中断相关实现
  //   contents of rom_2 (hex, n*v repeats v):
  //   4 50 a0
endmodule

module \中断按键参考电路  (
  input  \同步清零信号 ,
  output \与中断屏蔽位与 
);

  wire \_1号中断_out , and_1_out, clock_1_out, d_ff_1_q, or_1_out, or_2_out;

  Clock #(.highDuration(1), .lowDuration(1)) clock_1 (.out(clock_1_out));
  Button \_1号中断  (.out(\_1号中断_out ));
  or or_1 (or_1_out, \与中断屏蔽位与 , d_ff_1_q);
  LED #(.active("true")) \_1号中断等待指示灯  (.in(or_1_out));
  D_Flip_Flop #(.trigger("rising"), .Pre_Clr_Positions("LEGACY"), .NegatePresetClear("false"), .enable("true"), .NewFFLayout("false")) d_ff_1 (
    .clk(\_1号中断_out ), .D(1'b1), .Q(d_ff_1_q), .reset(\与中断屏蔽位与 ));  // open: Qn, preset, en
  or or_2 (or_2_out, d_ff_1_q, \与中断屏蔽位与 );
  and and_1 (and_1_out, or_2_out, ~\同步清零信号 );  // AND_Gate
  D_Flip_Flop #(.trigger("rising"), .Pre_Clr_Positions("LEGACY"), .NegatePresetClear("false"), .enable("true"), .NewFFLayout("false")) IR1 (
    .clk(clock_1_out), .D(and_1_out), .Q(\与中断屏蔽位与 ));  // open: Qn, preset, en, reset

  // Notes on the sheet:
  //   中断信号采样参考电路
  //   Reset 
endmodule
module IF_ID (
  input  [31:0] PCin,
  input  [31:0] IRin,
  input  [31:0] PC_4in,
  input  CLK,
  input  \同步清零_气泡_高电平有效 ,
  input  \使能端_低电平有效_stall_高电平有效 ,
  input  LoadUse,
  output [31:0] PCout,
  output [31:0] IRout,
  output [31:0] PC_4out,
  output \使能传递端_低电平有效_stall_高电平有效 
);

  wire nor_1_out;
  wire [31:0] multiplexer_1_out, multiplexer_2_out, multiplexer_3_out;

  Multiplexer #(.select(1), .width(32), .disabled("Z"), .enable("false")) multiplexer_1 (
    .in0(PCin), .in1({32{1'b0}}), .out(multiplexer_1_out), .sel(\同步清零_气泡_高电平有效 ));
  Multiplexer #(.select(1), .width(32), .disabled("Z"), .enable("false")) multiplexer_2 (
    .in0(IRin), .in1({32{1'b0}}), .out(multiplexer_2_out), .sel(\同步清零_气泡_高电平有效 ));
  Multiplexer #(.select(1), .width(32), .disabled("Z"), .enable("false")) multiplexer_3 (
    .in0(PC_4in), .in1({32{1'b0}}), .out(multiplexer_3_out), .sel(\同步清零_气泡_高电平有效 ));
  Pull_Resistor #(.pull(0)) pull_resistor_1 (.node(\同步清零_气泡_高电平有效 ));
  nor nor_1 (nor_1_out, LoadUse, \使能端_低电平有效_stall_高电平有效 );
  Register #(.width(32), .trigger("rising"), .Select("low")) register_1 (
    .D(multiplexer_1_out), .en(nor_1_out), .Q(PCout), .clk(CLK));  // open: clr
  Register #(.width(32), .trigger("rising"), .Select("low")) register_2 (
    .D(multiplexer_2_out), .en(nor_1_out), .Q(IRout), .clk(CLK));  // open: clr
  Register #(.width(32), .trigger("rising"), .Select("low")) register_3 (
    .D(multiplexer_3_out), .en(nor_1_out), .Q(PC_4out), .clk(CLK));  // open: clr
  Pull_Resistor #(.pull(0)) pull_resistor_2 (.node(nor_1_out));
  Register #(.width(1), .trigger("rising"), .Select("low")) register_4 (
    .D(\使能端_低电平有效_stall_高电平有效 ), .Q(\使能传递端_低电平有效_stall_高电平有效 ), .clk(CLK));  // open: en, clr
endmodule

module ID_EX (
  input  [31:0] PCin,
  input  [31:0] IRin,
  input  [31:0] Ain,
  input  [31:0] Bin,
  input  [31:0] IMMin,
  input  [31:0] PC_4in,
  input  [4:0] SHAMTin,
  input  MEMTOREGin,
  input  [3:0] MEMCONTROLin,
  input  [6:0] ALUOPin,
  input  ALUSRCBin,
  input  REGWRITEin,
  input  [4:0] W_in,
  input  JALin,
  input  [1:0] R1_SELin,
  input  [1:0] R2_SELin,
  input  C0Win,
  input  BRPin,
  input  RSTin,
  input  CLK,
  input  \同步清零_气泡_高电平有效 ,
  input  \使能端_低电平有效_stall_高电平有效 ,
  output [31:0] PCout,
  output [31:0] IRout,
  output [31:0] Aout,
  output [31:0] Bout,
  output [31:0] IMMout,
  output [31:0] PC_4out,
  output [4:0] SHAMTout,
  output MEMTOREGout,
  output [3:0] MEMCONTROLout,
  output [6:0] ALUOPout,
  output ALUSRCBout,
  output REGWRITEout,
  output [4:0] W_out,
  output JALout,
  output [1:0] R1_SELout,
  output [1:0] R2_SELout,
  output C0Wout,
  output BRPout,
  output RSTout,
  output \使能传递端_低电平有效_stall_高电平有效 
);

  wire multiplexer_8_out, multiplexer_11_out, multiplexer_12_out, multiplexer_14_out, multiplexer_17_out,
       multiplexer_18_out, multiplexer_19_out, not_1_out;
  wire [1:0] multiplexer_15_out, multiplexer_16_out;
  wire [3:0] multiplexer_9_out;
  wire [4:0] multiplexer_7_out, multiplexer_13_out;
  wire [6:0] multiplexer_10_out;
  wire [31:0] multiplexer_1_out, multiplexer_2_out, multiplexer_3_out, multiplexer_4_out, multiplexer_5_out,
       multiplexer_6_out;

  Multiplexer #(.select(1), .width(32), .disabled("Z"), .enable("false")) multiplexer_1 (
    .in0(PCin), .in1({32{1'b0}}), .out(multiplexer_1_out), .sel(\同步清零_气泡_高电平有效 ));
  Multiplexer #(.select(1), .width(32), .disabled("Z"), .enable("false")) multiplexer_2 (
    .in0(IRin), .in1({32{1'b0}}), .out(multiplexer_2_out), .sel(\同步清零_气泡_高电平有效 ));
  Multiplexer #(.select(1), .width(32), .disabled("Z"), .enable("false")) multiplexer_3 (
    .in0(Ain), .in1({32{1'b0}}), .out(multiplexer_3_out), .sel(\同步清零_气泡_高电平有效 ));
  Multiplexer #(.select(1), .width(32), .disabled("Z"), .enable("false")) multiplexer_4 (
    .in0(Bin), .in1({32{1'b0}}), .out(multiplexer_4_out), .sel(\同步清零_气泡_高电平有效 ));
  Multiplexer #(.select(1), .width(32), .disabled("Z"), .enable("false")) multiplexer_5 (
    .in0(IMMin), .in1({32{1'b0}}), .out(multiplexer_5_out), .sel(\同步清零_气泡_高电平有效 ));
  Multiplexer #(.select(1), .width(32), .disabled("Z"), .enable("false")) multiplexer_6 (
    .in0(PC_4in), .in1({32{1'b0}}), .out(multiplexer_6_out), .sel(\同步清零_气泡_高电平有效 ));
  Multiplexer #(.select(1), .width(5), .disabled("Z"), .enable("false")) multiplexer_7 (
    .in0(SHAMTin), .in1({5{1'b0}}), .out(multiplexer_7_out), .sel(\同步清零_气泡_高电平有效 ));
  Multiplexer #(.select(1), .width(1), .disabled("Z"), .enable("false")) multiplexer_8 (
    .in0(MEMTOREGin), .in1(1'b0), .out(multiplexer_8_out), .sel(\同步清零_气泡_高电平有效 ));
  Multiplexer #(.select(1), .width(4), .disabled("Z"), .enable("false")) multiplexer_9 (
    .in0(MEMCONTROLin), .in1(4'b0000), .out(multiplexer_9_out), .sel(\同步清零_气泡_高电平有效 ));
  Multiplexer #(.select(1), .width(7), .disabled("Z"), .enable("false")) multiplexer_10 (
    .in0(ALUOPin), .in1({7{1'b0}}), .out(multiplexer_10_out), .sel(\同步清零_气泡_高电平有效 ));
  Multiplexer #(.select(1), .width(1), .disabled("Z"), .enable("false")) multiplexer_11 (
    .in0(ALUSRCBin), .in1(1'b0), .out(multiplexer_11_out), .sel(\同步清零_气泡_高电平有效 ));
  Multiplexer #(.select(1), .width(1), .disabled("Z"), .enable("false")) multiplexer_12 (
    .in0(REGWRITEin), .in1(1'b0), .out(multiplexer_12_out), .sel(\同步清零_气泡_高电平有效 ));
  Multiplexer #(.select(1), .width(5), .disabled("Z"), .enable("false")) multiplexer_13 (
    .in0(W_in), .in1({5{1'b0}}), .out(multiplexer_13_out), .sel(\同步清零_气泡_高电平有效 ));
  Multiplexer #(.select(1), .width(1), .disabled("Z"), .enable("false")) multiplexer_14 (
    .in0(JALin), .in1(1'b0), .out(multiplexer_14_out), .sel(\同步清零_气泡_高电平有效 ));
  Multiplexer #(.select(1), .width(2), .disabled("Z"), .enable("false")) multiplexer_15 (
    .in0(R1_SELin), .in1(2'b00), .out(multiplexer_15_out), .sel(\同步清零_气泡_高电平有效 ));
  Multiplexer #(.select(1), .width(2), .disabled("Z"), .enable("false")) multiplexer_16 (
    .in0(R2_SELin), .in1(2'b00), .out(multiplexer_16_out), .sel(\同步清零_气泡_高电平有效 ));
  Multiplexer #(.select(1), .width(1), .disabled("Z"), .enable("false")) multiplexer_17 (
    .in0(C0Win), .in1(1'b0), .out(multiplexer_17_out), .sel(\同步清零_气泡_高电平有效 ));
  Multiplexer #(.select(1), .width(1), .disabled("Z"), .enable("false")) multiplexer_18 (
    .in0(BRPin), .in1(1'b0), .out(multiplexer_18_out), .sel(\同步清零_气泡_高电平有效 ));
  Multiplexer #(.select(1), .width(1), .disabled("Z"), .enable("false")) multiplexer_19 (
    .in0(RSTin), .in1(1'b0), .out(multiplexer_19_out), .sel(\同步清零_气泡_高电平有效 ));
  Pull_Resistor #(.pull(0)) pull_resistor_1 (.node(\同步清零_气泡_高电平有效 ));
  not not_1 (not_1_out, \使能端_低电平有效_stall_高电平有效 );
  Register #(.width(32), .trigger("rising"), .Select("low")) register_1 (
    .D(multiplexer_1_out), .en(not_1_out), .Q(PCout), .clk(CLK));  // open: clr
  Register #(.width(32), .trigger("rising"), .Select("low")) register_2 (
    .D(multiplexer_2_out), .en(not_1_out), .Q(IRout), .clk(CLK));  // open: clr
  Register #(.width(32), .trigger("rising"), .Select("low")) register_3 (
    .D(multiplexer_3_out), .en(not_1_out), .Q(Aout), .clk(CLK));  // open: clr
  Register #(.width(32), .trigger("rising"), .Select("low")) register_4 (
    .D(multiplexer_4_out), .en(not_1_out), .Q(Bout), .clk(CLK));  // open: clr
  Register #(.width(32), .trigger("rising"), .Select("low")) register_5 (
    .D(multiplexer_5_out), .en(not_1_out), .Q(IMMout), .clk(CLK));  // open: clr
  Register #(.width(32), .trigger("rising"), .Select("low")) register_6 (
    .D(multiplexer_6_out), .en(not_1_out), .Q(PC_4out), .clk(CLK));  // open: clr
  Register #(.width(5), .trigger("rising"), .Select("low")) register_7 (
    .D(multiplexer_7_out), .en(not_1_out), .Q(SHAMTout), .clk(CLK));  // open: clr
  Register #(.width(1), .trigger("rising"), .Select("low")) register_8 (
    .D(multiplexer_8_out), .en(not_1_out), .Q(MEMTOREGout), .clk(CLK));  // open: clr
  Register #(.width(4), .trigger("rising"), .Select("low")) register_9 (
    .D(multiplexer_9_out), .en(not_1_out), .Q(MEMCONTROLout), .clk(CLK));  // open: clr
  Register #(.width(7), .trigger("rising"), .Select("low")) register_10 (
    .D(multiplexer_10_out), .en(not_1_out), .Q(ALUOPout), .clk(CLK));  // open: clr
  Register #(.width(1), .trigger("rising"), .Select("low")) register_11 (
    .D(multiplexer_11_out), .en(not_1_out), .Q(ALUSRCBout), .clk(CLK));  // open: clr
  Register #(.width(1), .trigger("rising"), .Select("low")) register_12 (
    .D(multiplexer_12_out), .en(not_1_out), .Q(REGWRITEout), .clk(CLK));  // open: clr
  Register #(.width(5), .trigger("rising"), .Select("low")) register_13 (
    .D(multiplexer_13_out), .en(not_1_out), .Q(W_out), .clk(CLK));  // open: clr
  Register #(.width(1), .trigger("rising"), .Select("low")) register_14 (
    .D(multiplexer_14_out), .en(not_1_out), .Q(JALout), .clk(CLK));  // open: clr
  Register #(.width(2), .trigger("rising"), .Select("low")) register_15 (
    .D(multiplexer_15_out), .en(not_1_out), .Q(R1_SELout), .clk(CLK));  // open: clr
  Register #(.width(2), .trigger("rising"), .Select("low")) register_16 (
    .D(multiplexer_16_out), .en(not_1_out), .Q(R2_SELout), .clk(CLK));  // open: clr
  Register #(.width(1), .trigger("rising"), .Select("low")) register_17 (
    .D(multiplexer_17_out), .en(not_1_out), .Q(C0Wout), .clk(CLK));  // open: clr
  Register #(.width(1), .trigger("rising"), .Select("low")) register_18 (
    .D(multiplexer_18_out), .en(not_1_out), .Q(BRPout), .clk(CLK));  // open: clr
  Register #(.width(1), .trigger("rising"), .Select("low")) register_19 (
    .D(multiplexer_19_out), .en(not_1_out), .Q(RSTout), .clk(CLK));  // open: clr
  Pull_Resistor #(.pull(0)) pull_resistor_2 (.node(not_1_out));
  Register #(.width(1), .trigger("rising"), .Select("low")) register_20 (
    .D(\使能端_低电平有效_stall_高电平有效 ), .Q(\使能传递端_低电平有效_stall_高电平有效 ), .clk(CLK));  // open: en, clr
endmodule

module EX_MEM (
  input  [31:0] PCin,
  input  [31:0] IRin,
  input  [31:0] ALUin,
  input  [31:0] Bin,
  input  [31:0] PC_4in,
  input  MEMTOREGin,
  input  [3:0] MEMCONTROLin,
  input  REGWRITEin,
  input  [4:0] W_in,
  input  JALin,
  input  C0Win,
  input  CLK,
  input  \同步清零_气泡_高电平有效 ,
  input  \使能端_低电平有效_stall_高电平有效 ,
  output [31:0] PCout,
  output [31:0] IRout,
  output [31:0] ALUout,
  output [31:0] Bout,
  output [31:0] PC_4out,
  output MEMTOREGout,
  output [3:0] MEMCONTROLout,
  output REGWRITEout,
  output [4:0] W_out,
  output JALout,
  output C0Wout,
  output \使能传递端_低电平有效_stall_高电平有效 
);

  wire multiplexer_6_out, multiplexer_8_out, multiplexer_10_out, multiplexer_11_out, not_1_out;
  wire [3:0] multiplexer_7_out;
  wire [4:0] multiplexer_9_out;
  wire [31:0] multiplexer_1_out, multiplexer_2_out, multiplexer_3_out, multiplexer_4_out, multiplexer_5_out;

  Multiplexer #(.select(1), .width(32), .disabled("Z"), .enable("false")) multiplexer_1 (
    .in0(PCin), .in1({32{1'b0}}), .out(multiplexer_1_out), .sel(\同步清零_气泡_高电平有效 ));
  Multiplexer #(.select(1), .width(32), .disabled("Z"), .enable("false")) multiplexer_2 (
    .in0(IRin), .in1({32{1'b0}}), .out(multiplexer_2_out), .sel(\同步清零_气泡_高电平有效 ));
  Multiplexer #(.select(1), .width(32), .disabled("Z"), .enable("false")) multiplexer_3 (
    .in0(ALUin), .in1({32{1'b0}}), .out(multiplexer_3_out), .sel(\同步清零_气泡_高电平有效 ));
  Multiplexer #(.select(1), .width(32), .disabled("Z"), .enable("false")) multiplexer_4 (
    .in0(Bin), .in1({32{1'b0}}), .out(multiplexer_4_out), .sel(\同步清零_气泡_高电平有效 ));
  Multiplexer #(.select(1), .width(32), .disabled("Z"), .enable("false")) multiplexer_5 (
    .in0(PC_4in), .in1({32{1'b0}}), .out(multiplexer_5_out), .sel(\同步清零_气泡_高电平有效 ));
  Multiplexer #(.select(1), .width(1), .disabled("Z"), .enable("false")) multiplexer_6 (
    .in0(MEMTOREGin), .in1(1'b0), .out(multiplexer_6_out), .sel(\同步清零_气泡_高电平有效 ));
  Multiplexer #(.select(1), .width(4), .disabled("Z"), .enable("false")) multiplexer_7 (
    .in0(MEMCONTROLin), .in1(4'b0000), .out(multiplexer_7_out), .sel(\同步清零_气泡_高电平有效 ));
  Multiplexer #(.select(1), .width(1), .disabled("Z"), .enable("false")) multiplexer_8 (
    .in0(REGWRITEin), .in1(1'b0), .out(multiplexer_8_out), .sel(\同步清零_气泡_高电平有效 ));
  Multiplexer #(.select(1), .width(5), .disabled("Z"), .enable("false")) multiplexer_9 (
    .in0(W_in), .in1({5{1'b0}}), .out(multiplexer_9_out), .sel(\同步清零_气泡_高电平有效 ));
  Multiplexer #(.select(1), .width(1), .disabled("Z"), .enable("false")) multiplexer_10 (
    .in0(JALin), .in1(1'b0), .out(multiplexer_10_out), .sel(\同步清零_气泡_高电平有效 ));
  Multiplexer #(.select(1), .width(1), .disabled("Z"), .enable("false")) multiplexer_11 (
    .in0(C0Win), .in1(1'b0), .out(multiplexer_11_out), .sel(\同步清零_气泡_高电平有效 ));
  Pull_Resistor #(.pull(0)) pull_resistor_1 (.node(\同步清零_气泡_高电平有效 ));
  not not_1 (not_1_out, \使能端_低电平有效_stall_高电平有效 );
  Register #(.width(32), .trigger("rising"), .Select("low")) register_1 (
    .D(multiplexer_1_out), .en(not_1_out), .Q(PCout), .clk(CLK));  // open: clr
  Register #(.width(32), .trigger("rising"), .Select("low")) register_2 (
    .D(multiplexer_2_out), .en(not_1_out), .Q(IRout), .clk(CLK));  // open: clr
  Register #(.width(32), .trigger("rising"), .Select("low")) register_3 (
    .D(multiplexer_3_out), .en(not_1_out), .Q(ALUout), .clk(CLK));  // open: clr
  Register #(.width(32), .trigger("rising"), .Select("low")) register_4 (
    .D(multiplexer_4_out), .en(not_1_out), .Q(Bout), .clk(CLK));  // open: clr
  Register #(.width(32), .trigger("rising"), .Select("low")) register_5 (
    .D(multiplexer_5_out), .en(not_1_out), .Q(PC_4out), .clk(CLK));  // open: clr
  Register #(.width(1), .trigger("rising"), .Select("low")) register_6 (
    .D(multiplexer_6_out), .en(not_1_out), .Q(MEMTOREGout), .clk(CLK));  // open: clr
  Register #(.width(4), .trigger("rising"), .Select("low")) register_7 (
    .D(multiplexer_7_out), .en(not_1_out), .Q(MEMCONTROLout), .clk(CLK));  // open: clr
  Register #(.width(1), .trigger("rising"), .Select("low")) register_8 (
    .D(multiplexer_8_out), .en(not_1_out), .Q(REGWRITEout), .clk(CLK));  // open: clr
  Register #(.width(5), .trigger("rising"), .Select("low")) register_9 (
    .D(multiplexer_9_out), .en(not_1_out), .Q(W_out), .clk(CLK));  // open: clr
  Register #(.width(1), .trigger("rising"), .Select("low")) register_10 (
    .D(multiplexer_10_out), .en(not_1_out), .Q(JALout), .clk(CLK));  // open: clr
  Register #(.width(1), .trigger("rising"), .Select("low")) register_11 (
    .D(multiplexer_11_out), .en(not_1_out), .Q(C0Wout), .clk(CLK));  // open: clr
  Pull_Resistor #(.pull(0)) pull_resistor_2 (.node(not_1_out));
  Register #(.width(1), .trigger("rising"), .Select("low")) register_12 (
    .D(\使能端_低电平有效_stall_高电平有效 ), .Q(\使能传递端_低电平有效_stall_高电平有效 ), .clk(CLK));  // open: en, clr
endmodule

module MEM_WB (
  input  [31:0] PCin,
  input  [31:0] IRin,
  input  [31:0] ALUin,
  input  [31:0] MEMin,
  input  C0Win,
  input  MEMTOREGin,
  input  REGWRITEin,
  input  [4:0] W_in,
  input  CLK,
  input  \同步清零_气泡_高电平有效 ,
  input  \使能端_低电平有效_stall_高电平有效 ,
  output [31:0] PCout,
  output [31:0] IRout,
  output [31:0] ALUout,
  output [31:0] MEMout,
  output C0Wout,
  output MEMTOREGout,
  output REGWRITEout,
  output [4:0] W_out,
  output \使能传递端_低电平有效_stall_高电平有效 
);

  wire multiplexer_5_out, multiplexer_6_out, multiplexer_7_out, not_1_out;
  wire [4:0] multiplexer_8_out;
  wire [31:0] multiplexer_1_out, multiplexer_2_out, multiplexer_3_out, multiplexer_4_out;

  Multiplexer #(.select(1), .width(32), .disabled("Z"), .enable("false")) multiplexer_1 (
    .in0(PCin), .in1({32{1'b0}}), .out(multiplexer_1_out), .sel(\同步清零_气泡_高电平有效 ));
  Multiplexer #(.select(1), .width(32), .disabled("Z"), .enable("false")) multiplexer_2 (
    .in0(IRin), .in1({32{1'b0}}), .out(multiplexer_2_out), .sel(\同步清零_气泡_高电平有效 ));
  Multiplexer #(.select(1), .width(32), .disabled("Z"), .enable("false")) multiplexer_3 (
    .in0(ALUin), .in1({32{1'b0}}), .out(multiplexer_3_out), .sel(\同步清零_气泡_高电平有效 ));
  Multiplexer #(.select(1), .width(32), .disabled("Z"), .enable("false")) multiplexer_4 (
    .in0(MEMin), .in1({32{1'b0}}), .out(multiplexer_4_out), .sel(\同步清零_气泡_高电平有效 ));
  Multiplexer #(.select(1), .width(1), .disabled("Z"), .enable("false")) multiplexer_5 (
    .in0(C0Win), .in1(1'b0), .out(multiplexer_5_out), .sel(\同步清零_气泡_高电平有效 ));
  Multiplexer #(.select(1), .width(1), .disabled("Z"), .enable("false")) multiplexer_6 (
    .in0(MEMTOREGin), .in1(1'b0), .out(multiplexer_6_out), .sel(\同步清零_气泡_高电平有效 ));
  Multiplexer #(.select(1), .width(1), .disabled("Z"), .enable("false")) multiplexer_7 (
    .in0(REGWRITEin), .in1(1'b0), .out(multiplexer_7_out), .sel(\同步清零_气泡_高电平有效 ));
  Multiplexer #(.select(1), .width(5), .disabled("Z"), .enable("false")) multiplexer_8 (
    .in0(W_in), .in1({5{1'b0}}), .out(multiplexer_8_out), .sel(\同步清零_气泡_高电平有效 ));
  Pull_Resistor #(.pull(0)) pull_resistor_1 (.node(\同步清零_气泡_高电平有效 ));
  not not_1 (not_1_out, \使能端_低电平有效_stall_高电平有效 );
  Register #(.width(32), .trigger("rising"), .Select("low")) register_1 (
    .D(multiplexer_1_out), .en(not_1_out), .Q(PCout), .clk(CLK));  // open: clr
  Register #(.width(32), .trigger("rising"), .Select("low")) register_2 (
    .D(multiplexer_2_out), .en(not_1_out), .Q(IRout), .clk(CLK));  // open: clr
  Register #(.width(32), .trigger("rising"), .Select("low")) register_3 (
    .D(multiplexer_3_out), .en(not_1_out), .Q(ALUout), .clk(CLK));  // open: clr
  Register #(.width(32), .trigger("rising"), .Select("low")) register_4 (
    .D(multiplexer_4_out), .en(not_1_out), .Q(MEMout), .clk(CLK));  // open: clr
  Register #(.width(1), .trigger("rising"), .Select("low")) register_5 (
    .D(multiplexer_5_out), .en(not_1_out), .Q(C0Wout), .clk(CLK));  // open: clr
  Register #(.width(1), .trigger("rising"), .Select("low")) register_6 (
    .D(multiplexer_6_out), .en(not_1_out), .Q(MEMTOREGout), .clk(CLK));  // open: clr
  Register #(.width(1), .trigger("rising"), .Select("low")) register_7 (
    .D(multiplexer_7_out), .en(not_1_out), .Q(REGWRITEout), .clk(CLK));  // open: clr
  Register #(.width(5), .trigger("rising"), .Select("low")) register_8 (
    .D(multiplexer_8_out), .en(not_1_out), .Q(W_out), .clk(CLK));  // open: clr
  Pull_Resistor #(.pull(0)) pull_resistor_2 (.node(not_1_out));
  Register #(.width(1), .trigger("rising"), .Select("low")) register_9 (
    .D(\使能端_低电平有效_stall_高电平有效 ), .Q(\使能传递端_低电平有效_stall_高电平有效 ), .clk(CLK));  // open: en, clr
endmodule

module \源寄存器使用情况  (
  input  OP0,
  input  OP1,
  input  OP2,
  input  OP3,
  input  OP4,
  input  OP5,
  input  F0,
  input  F1,
  input  F2,
  input  F3,
  input  F4,
  input  F5,
  input  RS2,
  input  RS4,
  output R1_Used,
  output R2_Used
);

  wire and_1_out, and_2_out, and_3_out, and_4_out, and_5_out, and_6_out, and_7_out, and_8_out, and_9_out,
       and_10_out, and_11_out, and_12_out, and_13_out, and_14_out, and_15_out, and_16_out, and_17_out,
       and_18_out, and_19_out, and_20_out, and_21_out, and_22_out, not_1_out, not_2_out, not_3_out,
       not_4_out, not_5_out, not_6_out, not_7_out, not_8_out, not_9_out, not_10_out, not_11_out, not_12_out,
       not_13_out, not_14_out, not_15_out, not_16_out, not_17_out, not_18_out, not_19_out, not_20_out,
       not_21_out, not_22_out, not_23_out, not_24_out, not_25_out, not_26_out, not_27_out, not_28_out,
       not_29_out, not_30_out, not_31_out, not_32_out, not_33_out, not_34_out, not_35_out, not_36_out,
       not_37_out, not_38_out, not_39_out, not_40_out, not_41_out, not_42_out, not_43_out, not_44_out,
       not_45_out, not_46_out, not_47_out, not_48_out, not_49_out, not_50_out, not_51_out, not_52_out,
       not_53_out, not_54_out, not_55_out, not_56_out, not_57_out, not_58_out, not_59_out, not_60_out,
       not_61_out, not_62_out, not_63_out, not_64_out, not_65_out, not_66_out, not_67_out, not_68_out,
       not_69_out, not_70_out, not_71_out, not_72_out, not_73_out, not_74_out, not_75_out, not_76_out,
       not_77_out, not_78_out, not_79_out, not_80_out, not_81_out, not_82_out, not_83_out, not_84_out,
       not_85_out, not_86_out, not_87_out, not_88_out, not_89_out, not_90_out, not_91_out, not_92_out,
       not_93_out, not_94_out, not_95_out, not_96_out, not_97_out, not_98_out, not_99_out, not_100_out,
       not_101_out, not_102_out, not_103_out, not_104_out, not_105_out, not_106_out, not_107_out,
       not_108_out, not_109_out, not_110_out;

  not not_1 (not_1_out, OP1);
  not not_2 (not_2_out, OP2);
  not not_3 (not_3_out, OP4);
  not not_4 (not_4_out, F0);
  not not_5 (not_5_out, F1);
  not not_6 (not_6_out, F4);
  not not_7 (not_7_out, F5);
  not not_8 (not_8_out, OP1);
  not not_9 (not_9_out, OP2);
  not not_10 (not_10_out, OP4);
  not not_11 (not_11_out, F0);
  not not_12 (not_12_out, F3);
  not not_13 (not_13_out, F4);
  not not_14 (not_14_out, OP1);
  not not_15 (not_15_out, OP2);
  not not_16 (not_16_out, OP4);
  not not_17 (not_17_out, F3);
  not not_18 (not_18_out, F4);
  not not_19 (not_19_out, OP1);
  not not_20 (not_20_out, OP2);
  not not_21 (not_21_out, OP4);
  not not_22 (not_22_out, F3);
  not not_23 (not_23_out, F4);
  not not_24 (not_24_out, OP1);
  not not_25 (not_25_out, OP2);
  not not_26 (not_26_out, OP4);
  not not_27 (not_27_out, F2);
  not not_28 (not_28_out, F4);
  not not_29 (not_29_out, OP0);
  not not_30 (not_30_out, OP1);
  not not_31 (not_31_out, OP2);
  not not_32 (not_32_out, OP3);
  not not_33 (not_33_out, OP5);
  not not_34 (not_34_out, F0);
  not not_35 (not_35_out, F1);
  not not_36 (not_36_out, F2);
  not not_37 (not_37_out, F5);
  not not_38 (not_38_out, OP0);
  not not_39 (not_39_out, OP1);
  not not_40 (not_40_out, OP3);
  not not_41 (not_41_out, OP4);
  not not_42 (not_42_out, OP5);
  not not_43 (not_43_out, F0);
  not not_44 (not_44_out, F3);
  not not_45 (not_45_out, F4);
  not not_46 (not_46_out, OP0);
  not not_47 (not_47_out, OP1);
  not not_48 (not_48_out, OP3);
  not not_49 (not_49_out, OP4);
  not not_50 (not_50_out, OP5);
  not not_51 (not_51_out, F3);
  not not_52 (not_52_out, F4);
  not not_53 (not_53_out, OP0);
  not not_54 (not_54_out, OP1);
  not not_55 (not_55_out, OP3);
  not not_56 (not_56_out, OP4);
  not not_57 (not_57_out, OP5);
  not not_58 (not_58_out, F0);
  not not_59 (not_59_out, F1);
  not not_60 (not_60_out, F4);
  not not_61 (not_61_out, F5);
  not not_62 (not_62_out, OP0);
  not not_63 (not_63_out, OP1);
  not not_64 (not_64_out, OP3);
  not not_65 (not_65_out, OP4);
  not not_66 (not_66_out, OP5);
  not not_67 (not_67_out, F3);
  not not_68 (not_68_out, F4);
  not not_69 (not_69_out, OP0);
  not not_70 (not_70_out, OP1);
  not not_71 (not_71_out, OP3);
  not not_72 (not_72_out, OP4);
  not not_73 (not_73_out, OP5);
  not not_74 (not_74_out, F2);
  not not_75 (not_75_out, F4);
  not not_76 (not_76_out, OP0);
  not not_77 (not_77_out, OP1);
  not not_78 (not_78_out, OP2);
  not not_79 (not_79_out, OP3);
  not not_80 (not_80_out, OP5);
  not not_81 (not_81_out, RS4);
  not not_82 (not_82_out, OP1);
  not not_83 (not_83_out, OP2);
  not not_84 (not_84_out, OP4);
  not not_85 (not_85_out, OP1);
  not not_86 (not_86_out, OP3);
  not not_87 (not_87_out, OP4);
  not not_88 (not_88_out, OP5);
  not not_89 (not_89_out, OP2);
  not not_90 (not_90_out, OP4);
  not not_91 (not_91_out, OP1);
  not not_92 (not_92_out, OP3);
  not not_93 (not_93_out, OP4);
  not not_94 (not_94_out, OP0);
  not not_95 (not_95_out, OP4);
  not not_96 (not_96_out, OP5);
  not not_97 (not_97_out, OP1);
  not not_98 (not_98_out, OP2);
  not not_99 (not_99_out, OP4);
  not not_100 (not_100_out, OP2);
  not not_101 (not_101_out, OP4);
  not not_102 (not_102_out, OP5);
  not not_103 (not_103_out, OP3);
  not not_104 (not_104_out, OP4);
  not not_105 (not_105_out, OP5);
  not not_106 (not_106_out, OP1);
  not not_107 (not_107_out, OP4);
  not not_108 (not_108_out, OP5);
  not not_109 (not_109_out, OP2);
  not not_110 (not_110_out, OP4);
  and and_1 (and_1_out, not_38_out, not_39_out, not_40_out, not_41_out, not_42_out, not_43_out, not_44_out, not_45_out);
  and and_2 (and_2_out, not_46_out, not_47_out, not_48_out, not_49_out, not_50_out, not_51_out, not_52_out, F5);
  and and_3 (and_3_out, not_53_out, not_54_out, not_55_out, not_56_out, not_57_out, not_58_out, not_59_out, F2, not_60_out, not_61_out);
  and and_4 (and_4_out, not_62_out, not_63_out, not_64_out, not_65_out, not_66_out, F1, not_67_out, not_68_out);
  and and_5 (and_5_out, not_69_out, not_70_out, not_71_out, not_72_out, not_73_out, F1, not_74_out, not_75_out, F5);
  and and_6 (and_6_out, not_76_out, not_77_out, not_78_out, not_79_out, OP4, not_80_out, not_81_out);
  and and_7 (and_7_out, not_82_out, not_83_out, OP3, not_84_out, OP5);
  and and_8 (and_8_out, not_85_out, OP2, not_86_out, not_87_out, not_88_out);
  and and_9 (and_9_out, OP0, not_89_out, OP3, not_90_out, OP5);
  and and_10 (and_10_out, not_1_out, not_2_out, not_3_out, not_4_out, not_5_out, not_6_out, not_7_out);
  and and_11 (and_11_out, not_8_out, not_9_out, not_10_out, not_11_out, not_12_out, not_13_out);
  and and_12 (and_12_out, not_14_out, not_15_out, not_16_out, not_17_out, not_18_out, F5);
  and and_13 (and_13_out, not_19_out, not_20_out, not_21_out, F1, not_22_out, not_23_out);
  and and_14 (and_14_out, not_24_out, not_25_out, not_26_out, F1, not_27_out, not_28_out, F5);
  and and_15 (and_15_out, not_91_out, not_92_out, not_93_out, OP5);
  and and_16 (and_16_out, not_29_out, not_30_out, not_31_out, not_32_out, OP4, not_33_out, not_34_out, not_35_out, not_36_out, F3, F4, not_37_out, RS4);
  and and_17 (and_17_out, not_94_out, OP3, not_95_out, not_96_out);
  and and_18 (and_18_out, not_97_out, not_98_out, OP3, not_99_out);
  and and_19 (and_19_out, not_100_out, OP3, not_101_out, not_102_out);
  and and_20 (and_20_out, OP2, not_103_out, not_104_out, not_105_out);
  and and_21 (and_21_out, OP0, not_106_out, not_107_out, not_108_out);
  and and_22 (and_22_out, OP0, not_109_out, not_110_out, OP5);
  or or_1 (R1_Used, and_10_out, and_11_out, and_12_out, and_13_out, and_14_out, and_15_out, and_16_out, and_17_out, and_18_out, and_19_out, and_20_out, and_21_out, and_22_out);
  or or_2 (R2_Used, and_1_out, and_2_out, and_3_out, and_4_out, and_5_out, and_6_out, and_7_out, and_8_out, and_9_out);
endmodule

module \数据相关检测  (
  input  EX_RegWrite,
  input  [4:0] EX_WriteReg_num,
  input  MEM_RegWrite,
  input  [4:0] MEM_WriteReg_num,
  input  R1_Used,
  input  [4:0] R1_num,
  input  R2_Used,
  input  [4:0] R2_num,
  input  Ex_MemToReg,
  output Collision,
  output EX_Collision_R1,
  output MEM_Collision_R1,
  output LoadUse,
  output EX_Collision_R2,
  output MEM_Collision_R2
);

  wire comparator_1_eq, comparator_2_eq, comparator_3_eq, comparator_4_eq, comparator_5_eq, comparator_6_eq,
       or_1_out;

  and and_1 (LoadUse, Ex_MemToReg, or_1_out);
  Comparator #(.width(5), .mode("unsigned")) comparator_1 (
    .a(R1_num), .b({5{1'b0}}), .eq(comparator_1_eq));  // open: gt, lt
  Comparator #(.width(5), .mode("unsigned")) comparator_2 (
    .a(R1_num), .b(EX_WriteReg_num), .eq(comparator_2_eq));  // open: gt, lt
  Comparator #(.width(5), .mode("unsigned")) comparator_3 (
    .a(R2_num), .b({5{1'b0}}), .eq(comparator_3_eq));  // open: gt, lt
  Comparator #(.width(5), .mode("unsigned")) comparator_4 (
    .a(R2_num), .b(EX_WriteReg_num), .eq(comparator_4_eq));  // open: gt, lt
  or or_1 (or_1_out, EX_Collision_R1, EX_Collision_R2);
  and and_2 (EX_Collision_R1, comparator_2_eq, ~comparator_1_eq, R1_Used, EX_RegWrite);  // AND_Gate
  and and_3 (EX_Collision_R2, comparator_4_eq, ~comparator_3_eq, R2_Used, EX_RegWrite);  // AND_Gate
  Comparator #(.width(5), .mode("unsigned")) comparator_5 (
    .a(R1_num), .b(MEM_WriteReg_num), .eq(comparator_5_eq));  // open: gt, lt
  Comparator #(.width(5), .mode("unsigned")) comparator_6 (
    .a(R2_num), .b(MEM_WriteReg_num), .eq(comparator_6_eq));  // open: gt, lt
  and and_4 (MEM_Collision_R2, comparator_6_eq, ~comparator_3_eq, R2_Used, MEM_RegWrite);  // AND_Gate
  and and_5 (MEM_Collision_R1, comparator_5_eq, ~comparator_1_eq, R1_Used, MEM_RegWrite);  // AND_Gate
  or or_2 (Collision, MEM_Collision_R1, MEM_Collision_R2, EX_Collision_R1, EX_Collision_R2);
endmodule

// 中断逻辑
module \中断电路  (
  input  [3:0] IRin,
  input  [31:0] Status,
  input  CLK,
  output [3:0] W,
  output IRout,
  output [1:0] A
);

  wire and_1_out, and_2_out, and_3_out, and_4_out, and_5_out, and_6_out, and_7_out, and_8_out, d_ff_1_q,
       d_ff_2_q, d_ff_3_q, d_ff_4_q, IR1_q, IR2_q, IR3_q, IR4_q, or_1_out, or_2_out, or_3_out, or_4_out,
       pull_resistor_2_node, pull_resistor_3_node, pull_resistor_4_node, pull_resistor_5_node;

  Pull_Resistor #(.pull(0)) pull_resistor_1 (.node(IRin));
  D_Flip_Flop #(.trigger("rising"), .Pre_Clr_Positions("LEGACY"), .NegatePresetClear("false"), .enable("true"), .NewFFLayout("false")) d_ff_1 (
    .clk(IRin[0]), .D(1'b1), .Q(d_ff_1_q), .reset(IR1_q));  // open: Qn, preset, en
  D_Flip_Flop #(.trigger("rising"), .Pre_Clr_Positions("LEGACY"), .NegatePresetClear("false"), .enable("true"), .NewFFLayout("false")) d_ff_2 (
    .clk(IRin[1]), .D(1'b1), .Q(d_ff_2_q), .reset(IR2_q));  // open: Qn, preset, en
  D_Flip_Flop #(.trigger("rising"), .Pre_Clr_Positions("LEGACY"), .NegatePresetClear("false"), .enable("true"), .NewFFLayout("false")) d_ff_3 (
    .clk(IRin[2]), .D(1'b1), .Q(d_ff_3_q), .reset(IR3_q));  // open: Qn, preset, en
  D_Flip_Flop #(.trigger("rising"), .Pre_Clr_Positions("LEGACY"), .NegatePresetClear("false"), .enable("true"), .NewFFLayout("false")) d_ff_4 (
    .clk(IRin[3]), .D(1'b1), .Q(d_ff_4_q), .reset(IR4_q));  // open: Qn, preset, en
  or or_1 (or_1_out, d_ff_1_q, IR1_q);
  Pull_Resistor #(.pull(0)) pull_resistor_2 (.node(pull_resistor_2_node));
  or or_2 (or_2_out, d_ff_2_q, IR2_q);
  Pull_Resistor #(.pull(0)) pull_resistor_3 (.node(pull_resistor_3_node));
  or or_3 (or_3_out, d_ff_3_q, IR3_q);
  Pull_Resistor #(.pull(0)) pull_resistor_4 (.node(pull_resistor_4_node));
  or or_4 (or_4_out, d_ff_4_q, IR4_q);
  Pull_Resistor #(.pull(0)) pull_resistor_5 (.node(pull_resistor_5_node));
  and and_1 (and_1_out, or_1_out, ~pull_resistor_2_node);  // AND_Gate
  and and_2 (and_2_out, or_2_out, ~pull_resistor_3_node);  // AND_Gate
  and and_3 (and_3_out, or_3_out, ~pull_resistor_4_node);  // AND_Gate
  and and_4 (and_4_out, or_4_out, ~pull_resistor_5_node);  // AND_Gate
  D_Flip_Flop #(.trigger("rising"), .Pre_Clr_Positions("LEGACY"), .NegatePresetClear("false"), .enable("true"), .NewFFLayout("false")) IR1 (
    .clk(CLK), .D(and_1_out), .Q(IR1_q));  // open: Qn, preset, en, reset
  D_Flip_Flop #(.trigger("rising"), .Pre_Clr_Positions("LEGACY"), .NegatePresetClear("false"), .enable("true"), .NewFFLayout("false")) IR2 (
    .clk(CLK), .D(and_2_out), .Q(IR2_q));  // open: Qn, preset, en, reset
  D_Flip_Flop #(.trigger("rising"), .Pre_Clr_Positions("LEGACY"), .NegatePresetClear("false"), .enable("true"), .NewFFLayout("false")) IR3 (
    .clk(CLK), .D(and_3_out), .Q(IR3_q));  // open: Qn, preset, en, reset
  D_Flip_Flop #(.trigger("rising"), .Pre_Clr_Positions("LEGACY"), .NegatePresetClear("false"), .enable("true"), .NewFFLayout("false")) IR4 (
    .clk(CLK), .D(and_4_out), .Q(IR4_q));  // open: Qn, preset, en, reset
  or or_5 (W[0], IR1_q, d_ff_1_q);
  or or_6 (W[1], IR2_q, d_ff_2_q);
  or or_7 (W[2], IR3_q, d_ff_3_q);
  or or_8 (W[3], IR4_q, d_ff_4_q);
  and and_5 (and_5_out, IR1_q, Status[8]);
  and and_6 (and_6_out, IR2_q, Status[9]);
  and and_7 (and_7_out, IR3_q, Status[10]);
  and and_8 (and_8_out, IR4_q, Status[11]);
  Pull_Resistor #(.pull(0)) pull_resistor_6 (.node(W));
  Priority_Encoder #(.select(2), .disabled("Z")) priority_encoder_1 (
    .in0(and_5_out), .in1(and_6_out), .in2(and_7_out), .in3(and_8_out), .out(A), .gs(IRout), .en_in(Status[0]));  // open: en_out
  Decoder #(.select(2), .tristate("false"), .disabled("Z"), .enable("false")) decoder_1 (
    .out0(pull_resistor_2_node), .out1(pull_resistor_3_node), .out2(pull_resistor_4_node),
    .out3(pull_resistor_5_node), .sel(A));

  // Notes on the sheet:
  //   Reset 
  //   Reset 
  //   Reset 
  //   Reset 
endmodule

// 中断逻辑
module \中断电路_下降沿  (
  input  [3:0] IRin,
  input  [31:0] Status,
  input  CLK,
  output [3:0] W,
  output IRout,
  output [1:0] A
);

  wire and_1_out, and_2_out, and_3_out, and_4_out, and_5_out, and_6_out, and_7_out, and_8_out, d_ff_1_q,
       d_ff_2_q, d_ff_3_q, d_ff_4_q, IR1_q, IR2_q, IR3_q, IR4_q, or_1_out, or_2_out, or_3_out, or_4_out,
       pull_resistor_2_node, pull_resistor_3_node, pull_resistor_4_node, pull_resistor_5_node;

  Pull_Resistor #(.pull(0)) pull_resistor_1 (.node(IRin));
  D_Flip_Flop #(.trigger("rising"), .Pre_Clr_Positions("LEGACY"), .NegatePresetClear("false"), .enable("true"), .NewFFLayout("false")) d_ff_1 (
    .clk(IRin[0]), .D(1'b1), .Q(d_ff_1_q), .reset(IR1_q));  // open: Qn, preset, en
  D_Flip_Flop #(.trigger("rising"), .Pre_Clr_Positions("LEGACY"), .NegatePresetClear("false"), .enable("true"), .NewFFLayout("false")) d_ff_2 (
    .clk(IRin[1]), .D(1'b1), .Q(d_ff_2_q), .reset(IR2_q));  // open: Qn, preset, en
  D_Flip_Flop #(.trigger("rising"), .Pre_Clr_Positions("LEGACY"), .NegatePresetClear("false"), .enable("true"), .NewFFLayout("false")) d_ff_3 (
    .clk(IRin[2]), .D(1'b1), .Q(d_ff_3_q), .reset(IR3_q));  // open: Qn, preset, en
  D_Flip_Flop #(.trigger("rising"), .Pre_Clr_Positions("LEGACY"), .NegatePresetClear("false"), .enable("true"), .NewFFLayout("false")) d_ff_4 (
    .clk(IRin[3]), .D(1'b1), .Q(d_ff_4_q), .reset(IR4_q));  // open: Qn, preset, en
  or or_1 (or_1_out, d_ff_1_q, IR1_q);
  Pull_Resistor #(.pull(0)) pull_resistor_2 (.node(pull_resistor_2_node));
  or or_2 (or_2_out, d_ff_2_q, IR2_q);
  Pull_Resistor #(.pull(0)) pull_resistor_3 (.node(pull_resistor_3_node));
  or or_3 (or_3_out, d_ff_3_q, IR3_q);
  Pull_Resistor #(.pull(0)) pull_resistor_4 (.node(pull_resistor_4_node));
  or or_4 (or_4_out, d_ff_4_q, IR4_q);
  Pull_Resistor #(.pull(0)) pull_resistor_5 (.node(pull_resistor_5_node));
  and and_1 (and_1_out, or_1_out, ~pull_resistor_2_node);  // AND_Gate
  and and_2 (and_2_out, or_2_out, ~pull_resistor_3_node);  // AND_Gate
  and and_3 (and_3_out, or_3_out, ~pull_resistor_4_node);  // AND_Gate
  and and_4 (and_4_out, or_4_out, ~pull_resistor_5_node);  // AND_Gate
  D_Flip_Flop #(.trigger("falling"), .Pre_Clr_Positions("LEGACY"), .NegatePresetClear("false"), .enable("true"), .NewFFLayout("false")) IR1 (
    .clk(CLK), .D(and_1_out), .Q(IR1_q));  // open: Qn, preset, en, reset
  D_Flip_Flop #(.trigger("falling"), .Pre_Clr_Positions("LEGACY"), .NegatePresetClear("false"), .enable("true"), .NewFFLayout("false")) IR2 (
    .clk(CLK), .D(and_2_out), .Q(IR2_q));  // open: Qn, preset, en, reset
  D_Flip_Flop #(.trigger("falling"), .Pre_Clr_Positions("LEGACY"), .NegatePresetClear("false"), .enable("true"), .NewFFLayout("false")) IR3 (
    .clk(CLK), .D(and_3_out), .Q(IR3_q));  // open: Qn, preset, en, reset
  D_Flip_Flop #(.trigger("falling"), .Pre_Clr_Positions("LEGACY"), .NegatePresetClear("false"), .enable("true"), .NewFFLayout("false")) IR4 (
    .clk(CLK), .D(and_4_out), .Q(IR4_q));  // open: Qn, preset, en, reset
  or or_5 (W[0], IR1_q, d_ff_1_q);
  or or_6 (W[1], IR2_q, d_ff_2_q);
  or or_7 (W[2], IR3_q, d_ff_3_q);
  or or_8 (W[3], IR4_q, d_ff_4_q);
  and and_5 (and_5_out, IR1_q, Status[8]);
  and and_6 (and_6_out, IR2_q, Status[9]);
  and and_7 (and_7_out, IR3_q, Status[10]);
  and and_8 (and_8_out, IR4_q, Status[11]);
  Pull_Resistor #(.pull(0)) pull_resistor_6 (.node(W));
  Priority_Encoder #(.select(2), .disabled("Z")) priority_encoder_1 (
    .in0(and_5_out), .in1(and_6_out), .in2(and_7_out), .in3(and_8_out), .out(A), .gs(IRout), .en_in(Status[0]));  // open: en_out
  Decoder #(.select(2), .tristate("false"), .disabled("Z"), .enable("false")) decoder_1 (
    .out0(pull_resistor_2_node), .out1(pull_resistor_3_node), .out2(pull_resistor_4_node),
    .out3(pull_resistor_5_node), .sel(A));

  // Notes on the sheet:
  //   Reset 
  //   Reset 
  //   Reset 
  //   Reset 
endmodule

// 分支预测
module BHT (
  input  [31:0] JumpAddrIn,
  input  ID_RST,
  input  [31:0] OriginAddr,
  input  [31:0] CurAddr,
  input  Failed,
  input  CLK,
  output Jump,
  output [31:0] JumpAddrOut
);

  wire and_1_out, comparator_1_eq, comparator_2_eq, comparator_3_eq, comparator_4_eq, comparator_5_eq,
       comparator_6_eq, comparator_7_eq, comparator_8_eq, comparator_9_eq, comparator_10_eq,
       comparator_11_eq, comparator_12_eq, comparator_13_eq, comparator_14_eq, comparator_15_eq,
       comparator_16_eq, decoder_1_out0, decoder_1_out1, decoder_1_out2, decoder_1_out3, decoder_1_out4,
       decoder_1_out5, decoder_1_out6, decoder_1_out7, or_1_out, or_2_out;
  wire [1:0] bhtstate_1_nextstatebit0, cacheline_1_d0, cacheline_1_d1;
  wire [2:0] \max3_归并比较_1_max_num , \max3_归并比较_2_max_num , \max3_归并比较_3_max_num , \max3_归并比较_4_max_num ,
       \max3_归并比较_5_max_num , \max3_归并比较_6_max_num , \max3_归并比较_7_max_num ;
  wire [7:0] cacheline_1_c0, cacheline_2_c0, cacheline_3_c0, cacheline_4_c0, cacheline_5_c0, cacheline_6_c0,
       cacheline_7_c0, cacheline_8_c0, \max3_归并比较_1_max , \max3_归并比较_2_max , \max3_归并比较_3_max ,
       \max3_归并比较_4_max , \max3_归并比较_5_max , \max3_归并比较_7_max ;
  wire [29:0] cacheline_1_d0_2, multiplexer_2_out;
  wire [31:0] cacheline_1_vtag, cacheline_2_vtag, cacheline_3_vtag, cacheline_4_vtag, cacheline_5_vtag,
       cacheline_6_vtag, cacheline_7_vtag, cacheline_8_vtag, multiplexer_1_out;

  Decoder #(.select(3), .tristate("false"), .disabled(0), .enable("true")) decoder_1 (
    .out0(decoder_1_out0), .out1(decoder_1_out1), .out2(decoder_1_out2), .out3(decoder_1_out3),
    .out4(decoder_1_out4), .out5(decoder_1_out5), .out6(decoder_1_out6), .out7(decoder_1_out7),
    .sel(\max3_归并比较_6_max_num ), .en(and_1_out));
  and and_1 (and_1_out, Failed, ~or_2_out);  // AND_Gate
  Multiplexer #(.select(1), .width(32), .disabled("Z"), .enable("false")) multiplexer_1 (
    .in0(JumpAddrIn), .in1(CurAddr), .out(multiplexer_1_out), .sel(ID_RST));
  Multiplexer #(.select(1), .width(30), .disabled("Z"), .enable("false")) multiplexer_2 (
    .in0(cacheline_1_d0_2), .in1(multiplexer_1_out[31:2]), .out(multiplexer_2_out), .sel(Failed));
  Cacheline cacheline_1 (
    .CLK(CLK), .L0(comparator_9_eq), .VTag(cacheline_1_vtag), .C0(cacheline_1_c0),
    .D1({JumpAddrOut[31:2], cacheline_1_d1}), .Tag({OriginAddr[31:2], 2'b11}),
    .Din({multiplexer_2_out, bhtstate_1_nextstatebit0}), .R0(decoder_1_out0), .L1(comparator_1_eq),
    .D0({cacheline_1_d0_2, cacheline_1_d0}));
  Cacheline cacheline_2 (
    .CLK(CLK), .L0(comparator_10_eq), .VTag(cacheline_2_vtag), .C0(cacheline_2_c0),
    .D1({JumpAddrOut[31:2], cacheline_1_d1}), .Tag({OriginAddr[31:2], 2'b11}),
    .Din({multiplexer_2_out, bhtstate_1_nextstatebit0}), .R0(decoder_1_out1), .L1(comparator_2_eq),
    .D0({cacheline_1_d0_2, cacheline_1_d0}));
  Cacheline cacheline_3 (
    .CLK(CLK), .L0(comparator_11_eq), .VTag(cacheline_3_vtag), .C0(cacheline_3_c0),
    .D1({JumpAddrOut[31:2], cacheline_1_d1}), .Tag({OriginAddr[31:2], 2'b11}),
    .Din({multiplexer_2_out, bhtstate_1_nextstatebit0}), .R0(decoder_1_out2), .L1(comparator_3_eq),
    .D0({cacheline_1_d0_2, cacheline_1_d0}));
  Cacheline cacheline_4 (
    .CLK(CLK), .L0(comparator_12_eq), .VTag(cacheline_4_vtag), .C0(cacheline_4_c0),
    .D1({JumpAddrOut[31:2], cacheline_1_d1}), .Tag({OriginAddr[31:2], 2'b11}),
    .Din({multiplexer_2_out, bhtstate_1_nextstatebit0}), .R0(decoder_1_out3), .L1(comparator_4_eq),
    .D0({cacheline_1_d0_2, cacheline_1_d0}));
  Cacheline cacheline_5 (
    .CLK(CLK), .L0(comparator_13_eq), .VTag(cacheline_5_vtag), .C0(cacheline_5_c0),
    .D1({JumpAddrOut[31:2], cacheline_1_d1}), .Tag({OriginAddr[31:2], 2'b11}),
    .Din({multiplexer_2_out, bhtstate_1_nextstatebit0}), .R0(decoder_1_out4), .L1(comparator_5_eq),
    .D0({cacheline_1_d0_2, cacheline_1_d0}));
  Cacheline cacheline_6 (
    .CLK(CLK), .L0(comparator_14_eq), .VTag(cacheline_6_vtag), .C0(cacheline_6_c0),
    .D1({JumpAddrOut[31:2], cacheline_1_d1}), .Tag({OriginAddr[31:2], 2'b11}),
    .Din({multiplexer_2_out, bhtstate_1_nextstatebit0}), .R0(decoder_1_out5), .L1(comparator_6_eq),
    .D0({cacheline_1_d0_2, cacheline_1_d0}));
  Cacheline cacheline_7 (
    .CLK(CLK), .L0(comparator_15_eq), .VTag(cacheline_7_vtag), .C0(cacheline_7_c0),
    .D1({JumpAddrOut[31:2], cacheline_1_d1}), .Tag({OriginAddr[31:2], 2'b11}),
    .Din({multiplexer_2_out, bhtstate_1_nextstatebit0}), .R0(decoder_1_out6), .L1(comparator_7_eq),
    .D0({cacheline_1_d0_2, cacheline_1_d0}));
  Cacheline cacheline_8 (
    .CLK(CLK), .L0(comparator_16_eq), .VTag(cacheline_8_vtag), .C0(cacheline_8_c0),
    .D1({JumpAddrOut[31:2], cacheline_1_d1}), .Tag({OriginAddr[31:2], 2'b11}),
    .Din({multiplexer_2_out, bhtstate_1_nextstatebit0}), .R0(decoder_1_out7), .L1(comparator_8_eq),
    .D0({cacheline_1_d0_2, cacheline_1_d0}));
  Comparator #(.width(32), .mode("unsigned")) comparator_1 (
    .a(cacheline_1_vtag), .b({CurAddr[31:2], 2'b11}), .eq(comparator_1_eq));  // open: gt, lt
  Comparator #(.width(32), .mode("unsigned")) comparator_2 (
    .a(cacheline_2_vtag), .b({CurAddr[31:2], 2'b11}), .eq(comparator_2_eq));  // open: gt, lt
  Comparator #(.width(32), .mode("unsigned")) comparator_3 (
    .a(cacheline_3_vtag), .b({CurAddr[31:2], 2'b11}), .eq(comparator_3_eq));  // open: gt, lt
  Comparator #(.width(32), .mode("unsigned")) comparator_4 (
    .a(cacheline_4_vtag), .b({CurAddr[31:2], 2'b11}), .eq(comparator_4_eq));  // open: gt, lt
  Comparator #(.width(32), .mode("unsigned")) comparator_5 (
    .a(cacheline_5_vtag), .b({CurAddr[31:2], 2'b11}), .eq(comparator_5_eq));  // open: gt, lt
  Comparator #(.width(32), .mode("unsigned")) comparator_6 (
    .a(cacheline_6_vtag), .b({CurAddr[31:2], 2'b11}), .eq(comparator_6_eq));  // open: gt, lt
  Comparator #(.width(32), .mode("unsigned")) comparator_7 (
    .a(cacheline_7_vtag), .b({CurAddr[31:2], 2'b11}), .eq(comparator_7_eq));  // open: gt, lt
  Comparator #(.width(32), .mode("unsigned")) comparator_8 (
    .a(cacheline_8_vtag), .b({CurAddr[31:2], 2'b11}), .eq(comparator_8_eq));  // open: gt, lt
  or or_1 (or_1_out, comparator_8_eq, comparator_7_eq, comparator_6_eq, comparator_5_eq, comparator_4_eq, comparator_3_eq, comparator_2_eq, comparator_1_eq);
  Comparator #(.width(32), .mode("unsigned")) comparator_9 (
    .a(cacheline_1_vtag), .b({OriginAddr[31:2], 2'b11}), .eq(comparator_9_eq));  // open: gt, lt
  Comparator #(.width(32), .mode("unsigned")) comparator_10 (
    .a(cacheline_2_vtag), .b({OriginAddr[31:2], 2'b11}), .eq(comparator_10_eq));  // open: gt, lt
  Comparator #(.width(32), .mode("unsigned")) comparator_11 (
    .a(cacheline_3_vtag), .b({OriginAddr[31:2], 2'b11}), .eq(comparator_11_eq));  // open: gt, lt
  Comparator #(.width(32), .mode("unsigned")) comparator_12 (
    .a(cacheline_4_vtag), .b({OriginAddr[31:2], 2'b11}), .eq(comparator_12_eq));  // open: gt, lt
  Comparator #(.width(32), .mode("unsigned")) comparator_13 (
    .a(cacheline_5_vtag), .b({OriginAddr[31:2], 2'b11}), .eq(comparator_13_eq));  // open: gt, lt
  Comparator #(.width(32), .mode("unsigned")) comparator_14 (
    .a(cacheline_6_vtag), .b({OriginAddr[31:2], 2'b11}), .eq(comparator_14_eq));  // open: gt, lt
  Comparator #(.width(32), .mode("unsigned")) comparator_15 (
    .a(cacheline_7_vtag), .b({OriginAddr[31:2], 2'b11}), .eq(comparator_15_eq));  // open: gt, lt
  Comparator #(.width(32), .mode("unsigned")) comparator_16 (
    .a(cacheline_8_vtag), .b({OriginAddr[31:2], 2'b11}), .eq(comparator_16_eq));  // open: gt, lt
  or or_2 (or_2_out, comparator_16_eq, comparator_15_eq, comparator_14_eq, comparator_13_eq, comparator_12_eq, comparator_11_eq, comparator_10_eq, comparator_9_eq);
  \Max3_归并比较  \max3_归并比较_1  (
    .Y(cacheline_2_c0), .X(cacheline_1_c0), .Y_num(3'b001), .X_num(3'b000), .MAX(\max3_归并比较_1_max ),
    .Max_num(\max3_归并比较_1_max_num ));
  \Max3_归并比较  \max3_归并比较_2  (
    .Y(cacheline_4_c0), .X(cacheline_3_c0), .Y_num(3'b011), .X_num(3'b010), .MAX(\max3_归并比较_2_max ),
    .Max_num(\max3_归并比较_2_max_num ));
  \Max3_归并比较  \max3_归并比较_3  (
    .Y(cacheline_6_c0), .X(cacheline_5_c0), .Y_num(3'b101), .X_num(3'b100), .MAX(\max3_归并比较_3_max ),
    .Max_num(\max3_归并比较_3_max_num ));
  \Max3_归并比较  \max3_归并比较_4  (
    .Y(cacheline_8_c0), .X(cacheline_7_c0), .Y_num(3'b111), .X_num(3'b110), .MAX(\max3_归并比较_4_max ),
    .Max_num(\max3_归并比较_4_max_num ));
  \Max3_归并比较  \max3_归并比较_5  (
    .Y(\max3_归并比较_2_max ), .X(\max3_归并比较_1_max ), .Y_num(\max3_归并比较_2_max_num ),
    .X_num(\max3_归并比较_1_max_num ), .MAX(\max3_归并比较_5_max ), .Max_num(\max3_归并比较_5_max_num ));
  \Max3_归并比较  \max3_归并比较_6  (
    .Y(\max3_归并比较_7_max ), .X(\max3_归并比较_5_max ), .Y_num(\max3_归并比较_7_max_num ),
    .X_num(\max3_归并比较_5_max_num ), .Max_num(\max3_归并比较_6_max_num ));  // open: MAX
  \Max3_归并比较  \max3_归并比较_7  (
    .Y(\max3_归并比较_4_max ), .X(\max3_归并比较_3_max ), .Y_num(\max3_归并比较_4_max_num ),
    .X_num(\max3_归并比较_3_max_num ), .MAX(\max3_归并比较_7_max ), .Max_num(\max3_归并比较_7_max_num ));
  BHTState bhtstate_1 (
    .Found(or_2_out), .Failed(Failed), .NextStateBit1(bhtstate_1_nextstatebit0[1]),
    .CurStateBit1(cacheline_1_d0[1]), .CurStateBit0(cacheline_1_d0[0]),
    .NextStateBit0(bhtstate_1_nextstatebit0[0]));
  and and_2 (Jump, or_1_out, cacheline_1_d1[1]);

  assign JumpAddrOut[1:0] = 2'b00;
endmodule

module Cacheline (
  input  L1,
  input  [31:0] Tag,
  input  [31:0] Din,
  input  CLK,
  input  R0,
  input  L0,
  output [31:0] D1,
  output [31:0] VTag,
  output [7:0] C0,
  output [31:0] D0
);

  wire or_1_out;
  wire [31:0] \数据块_q ;

  Register #(.width(32), .trigger("rising"), .Select("low")) \u_有效位标记位  (
    .D(Tag), .en(or_1_out), .Q(VTag), .clk(CLK));  // open: clr
  or or_1 (or_1_out, L0, R0);
  Counter #(.width(8), .max('hf0), .ongoal("stay"), .trigger("rising"), .behavior("new")) \u_淘汰标记  (
    .Q(C0), .clk(CLK), .clr(L0));  // open: load, D, count, carry, preset, down
  Register #(.width(32), .trigger("rising"), .Select("low")) \u_数据块  (
    .D(Din), .en(or_1_out), .Q(\数据块_q ), .clk(CLK));  // open: clr
  assign D1 = L1 ? \数据块_q  : 32'bz;  // Controlled_Buffer controlled_buffer_1
  assign D0 = L0 ? \数据块_q  : 32'bz;  // Controlled_Buffer controlled_buffer_2
endmodule

// Max3
module \Max3_归并比较  (
  input  [7:0] Y,
  input  [7:0] X,
  input  [2:0] Y_num,
  input  [2:0] X_num,
  output [7:0] MAX,
  output [2:0] Max_num
);

  wire comparator_1_eq, comparator_1_gt, or_1_out;

  Multiplexer #(.select(1), .width(8), .disabled("Z"), .enable("false")) multiplexer_1 (
    .in0(Y), .in1(X), .out(MAX), .sel(or_1_out));
  Comparator #(.width(8), .mode("unsigned")) comparator_1 (
    .a(X), .b(Y), .gt(comparator_1_gt), .eq(comparator_1_eq));  // open: lt
  or or_1 (or_1_out, comparator_1_gt, comparator_1_eq);
  Multiplexer #(.select(1), .width(3), .disabled("Z"), .enable("false")) multiplexer_2 (
    .in0(Y_num), .in1(X_num), .out(Max_num), .sel(or_1_out));

  // Notes on the sheet:
  //   输出两个输入中的较大值，并输出较大值的3位编号
endmodule

// BHT SM
module BHTState (
  input  Found,
  input  Failed,
  input  CurStateBit1,
  input  CurStateBit0,
  output NextStateBit1,
  output NextStateBit0
);

  wire and_1_out, and_2_out, and_3_out, and_4_out, and_5_out, not_1_out, not_2_out, not_3_out, not_4_out,
       not_5_out, not_6_out;

  not not_1 (not_1_out, Found);
  and and_1 (and_1_out, not_1_out, Failed);
  not not_2 (not_2_out, CurStateBit1);
  and and_2 (and_2_out, Failed, not_2_out, CurStateBit0);
  and and_3 (and_3_out, Found, not_3_out, CurStateBit1);
  not not_3 (not_3_out, Failed);
  and and_4 (and_4_out, Found, CurStateBit1, not_4_out);
  not not_4 (not_4_out, CurStateBit0);
  not not_5 (not_5_out, Found);
  and and_5 (and_5_out, Failed, not_6_out);
  not not_6 (not_6_out, CurStateBit0);
  or or_1 (NextStateBit1, and_1_out, and_2_out, and_3_out, and_4_out);
  or or_2 (NextStateBit0, not_5_out, and_5_out);
endmodule

module Music (
);

  wire clock_1_out, dipswitch_1_p2;
  wire [4:0] counter_1_q, joystick_1_x, joystick_1_y;
  wire [7:0] slider_1_out;
  wire [31:0] and_1_out, demultiplexer_1_out0, demultiplexer_1_out1, demultiplexer_1_out2,
       demultiplexer_1_out3, demultiplexer_1_out4, demultiplexer_1_out5, demultiplexer_1_out6,
       demultiplexer_1_out7, demultiplexer_1_out8, demultiplexer_1_out9, demultiplexer_1_out10,
       demultiplexer_1_out11, demultiplexer_1_out12, demultiplexer_1_out13, demultiplexer_1_out14,
       demultiplexer_1_out15, demultiplexer_1_out16, demultiplexer_1_out17, demultiplexer_1_out18,
       demultiplexer_1_out19, demultiplexer_1_out20, demultiplexer_1_out21, demultiplexer_1_out22,
       demultiplexer_1_out23, demultiplexer_1_out24, demultiplexer_1_out25, demultiplexer_1_out26,
       demultiplexer_1_out27, demultiplexer_1_out28, demultiplexer_1_out29, demultiplexer_1_out30,
       demultiplexer_1_out31, random_1_out, random_2_out, random_3_out;

  Clock #(.highDuration(1), .lowDuration(1)) clock_1 (.out(clock_1_out));
  // RGBLed #(.multibit("false")) rgbled_1: pin names not known; wires that end beside it: joystick_1_x[2], joystick_1_x[3], joystick_1_x[4]
  Joystick #(.bits(5)) joystick_1 (.x(joystick_1_x), .y(joystick_1_y));
  Random #(.width(32), .seed(0), .trigger("rising")) random_1 (
    .clk(clock_1_out), .out(random_1_out));  // open: next, clr
  Random #(.width(32), .seed(100), .trigger("rising")) random_2 (
    .clk(clock_1_out), .out(random_2_out));  // open: next, clr
  Random #(.width(32), .seed(200), .trigger("rising")) random_3 (
    .clk(clock_1_out), .out(random_3_out));  // open: next, clr
  // Probe on joystick_1_x
  // Probe on joystick_1_y
  Demultiplexer #(.select(5), .width(32), .tristate("false"), .disabled("Z"), .enable("false")) demultiplexer_1 (
    .out0(demultiplexer_1_out0), .out1(demultiplexer_1_out1), .out2(demultiplexer_1_out2),
    .out3(demultiplexer_1_out3), .out4(demultiplexer_1_out4), .out5(demultiplexer_1_out5),
    .out6(demultiplexer_1_out6), .out7(demultiplexer_1_out7), .out8(demultiplexer_1_out8),
    .out9(demultiplexer_1_out9), .out10(demultiplexer_1_out10), .out11(demultiplexer_1_out11),
    .out12(demultiplexer_1_out12), .out13(demultiplexer_1_out13), .out14(demultiplexer_1_out14),
    .out15(demultiplexer_1_out15), .out16(demultiplexer_1_out16), .out17(demultiplexer_1_out17),
    .out18(demultiplexer_1_out18), .out19(demultiplexer_1_out19), .out20(demultiplexer_1_out20),
    .out21(demultiplexer_1_out21), .out22(demultiplexer_1_out22), .out23(demultiplexer_1_out23),
    .out24(demultiplexer_1_out24), .out25(demultiplexer_1_out25), .out26(demultiplexer_1_out26),
    .out27(demultiplexer_1_out27), .out28(demultiplexer_1_out28), .out29(demultiplexer_1_out29),
    .out30(demultiplexer_1_out30), .out31(demultiplexer_1_out31), .in(and_1_out), .sel(counter_1_q));
  assign and_1_out = random_1_out & random_2_out & random_3_out;  // AND_Gate and_1, 32 bits wide
  Counter #(.width(5), .max('h1f), .ongoal("wrap"), .trigger("rising"), .behavior("new")) counter_1 (
    .Q(counter_1_q), .clk(clock_1_out));  // open: load, D, count, carry, clr, preset, down
  Slider #(.width(8), .Direction("left_to_right"), .value('h21)) slider_1 (.out(slider_1_out));
  DotMatrix #(.inputtype("row"), .matrixcols(32), .matrixrows(32), .persist(64), .dotshape("square")) dotmatrix_1 (
    .row0(demultiplexer_1_out0), .row1(demultiplexer_1_out1), .row2(demultiplexer_1_out2),
    .row3(demultiplexer_1_out3), .row4(demultiplexer_1_out4), .row5(demultiplexer_1_out5),
    .row6(demultiplexer_1_out6), .row7(demultiplexer_1_out7), .row8(demultiplexer_1_out8),
    .row9(demultiplexer_1_out9), .row10(demultiplexer_1_out10), .row11(demultiplexer_1_out11),
    .row12(demultiplexer_1_out12), .row13(demultiplexer_1_out13), .row14(demultiplexer_1_out14),
    .row15(demultiplexer_1_out15), .row16(demultiplexer_1_out16), .row17(demultiplexer_1_out17),
    .row18(demultiplexer_1_out18), .row19(demultiplexer_1_out19), .row20(demultiplexer_1_out20),
    .row21(demultiplexer_1_out21), .row22(demultiplexer_1_out22), .row23(demultiplexer_1_out23),
    .row24(demultiplexer_1_out24), .row25(demultiplexer_1_out25), .row26(demultiplexer_1_out26),
    .row27(demultiplexer_1_out27), .row28(demultiplexer_1_out28), .row29(demultiplexer_1_out29),
    .row30(demultiplexer_1_out30), .row31(demultiplexer_1_out31));
  // Digital_Oscilloscope #(.nState(16), .frontlines("rising"), .showclock("true")) digital_oscilloscope_1: pin names not known; wires that end beside it: clock_1_out, joystick_1_x[0], joystick_1_x[1], joystick_1_x[2], joystick_1_x[3]
  // DipSwitch #(.NSwitches(1)) dipswitch_1: pin names not known; wires that end beside it: joystick_1_x[4], dipswitch_1_p2
  // Buzzer #(.freq_measure("Hz"), .vol_width(8)) buzzer_1: pin names not known; wires that end beside it: {4'b0000, joystick_1_y, joystick_1_x}, dipswitch_1_p2, slider_1_out
endmodule
