// Logisim project lyh-cpu24bht.circ as structural Verilog: 28 circuits, main circuit ◇单周期MIPS
module \单周期MIPS  (
  output RegWrite,
  output MemWrite,
  output [31:0] PC,
  output [31:0] IR,
  output [31:0] RDin,
  output [31:0] MDin,
  output [31:0] LedData
);

  wire and_3_out, and_4_out, and_5_out, Beq, BGTZ, Bne, branch, CLK, comparator_1_eq, equal, Go, IR1, IR2,
       IR3, JAL, JMP, JR, LBU, mips_alu_1_equal, not_1_out, not_2_out, not_3_out, not_4_out, not_5_out,
       or_1_out, SignedExt, SRLV, stop, Syscall, W1, W2, W3, \单周期硬布线控制器_1_alu_src , \单周期硬布线控制器_1_memtoreg ,
       \单周期硬布线控制器_1_regdst ;
  wire [3:0] \单周期硬布线控制器_1_alu_op ;
  wire [4:0] multiplexer_5_out, multiplexer_6_out, multiplexer_7_out, multiplexer_8_out, multiplexer_12_out;
  wire [15:0] \总周期数 , \无条件 , \有条件 ;
  wire [31:0] adder_2_out, and_6_out, bit_extender_1_out, bit_extender_2_out, bit_extender_3_out, JPC, JRPC,
       mips_alu_1_result, multiplexer_1_out, multiplexer_2_out, multiplexer_3_out, multiplexer_4_out,
       multiplexer_9_out, multiplexer_10_out, multiplexer_11_out, multiplexer_14_out, multiplexer_15_out,
       PC_4, ram_1_data, shifter_1_out, shifter_2_out, shifter_3_out, shifter_4_out;

  Clock #(.highDuration(1), .lowDuration(1)) clock_1 (.out(CLK));
  Button _1 (.out(IR1));
  Button _2 (.out(IR2));
  Button _3 (.out(IR3));
  Button \u_继续运行  (.out(Go));
  LED #(.active("true")) led_1 (.in(W1));
  LED #(.active("true")) led_2 (.in(W2));
  LED #(.active("true")) led_3 (.in(W3));
  Hex_Digit_Display hex_digit_display_1 (.value(LedData[31:28]));  // open: dp
  Hex_Digit_Display hex_digit_display_2 (.value(LedData[27:24]));  // open: dp
  Hex_Digit_Display hex_digit_display_3 (.value(LedData[23:20]));  // open: dp
  Hex_Digit_Display hex_digit_display_4 (.value(LedData[19:16]));  // open: dp
  Hex_Digit_Display hex_digit_display_5 (.value(LedData[15:12]));  // open: dp
  Hex_Digit_Display hex_digit_display_6 (.value(LedData[11:8]));  // open: dp
  Hex_Digit_Display hex_digit_display_7 (.value(LedData[7:4]));  // open: dp
  // Probe on \总周期数 
  Multiplexer #(.select(1), .width(32), .disabled("Z"), .enable("false")) multiplexer_1 (
    .in0(PC_4), .in1(adder_2_out), .out(multiplexer_1_out), .sel(branch));
  // Probe on JRPC
  Hex_Digit_Display hex_digit_display_8 (.value(LedData[3:0]));  // open: dp
  Multiplexer #(.select(1), .width(32), .disabled("Z"), .enable("false")) multiplexer_2 (
    .in0(multiplexer_1_out), .in1(JPC), .out(multiplexer_2_out), .sel(JMP));
  Comparator #(.width(32), .mode("twosComplement")) comparator_1 (
    .a(JRPC), .b(32'h22), .eq(comparator_1_eq));  // open: gt, lt
  not not_1 (not_1_out, stop);
  or or_1 (or_1_out, Go, not_1_out);
  Multiplexer #(.select(1), .width(32), .disabled("Z"), .enable("false")) multiplexer_3 (
    .in0(multiplexer_2_out), .in1(JRPC), .out(multiplexer_3_out), .sel(JR));
  Counter #(.width(16), .max('hffff), .ongoal("wrap"), .trigger("rising"), .behavior("old")) counter_1 (
    .D({16{1'b0}}), .count(or_1_out), .Q(\总周期数 ), .clk(CLK));  // open: load, carry, clr, preset
  Register #(.width(32), .trigger("rising"), .Select("low")) u_PC (
    .D(multiplexer_3_out), .en(or_1_out), .Q(PC), .clk(CLK));  // open: clr
  and and_1 (equal, Syscall, comparator_1_eq);
  and and_2 (stop, Syscall, not_2_out);
  not not_2 (not_2_out, comparator_1_eq);
  Adder #(.width(32)) adder_1 (.a(PC), .b(32'h4), .out(PC_4));  // open: cin, cout
  ROM #(.addrWidth(10), .dataWidth(32), .Select("high")) rom_1 (.addr(PC[11:2]), .data(IR));
  Multiplexer #(.select(1), .width(32), .disabled("Z"), .enable("false")) multiplexer_4 (
    .in1(MDin), .out(multiplexer_4_out), .sel(equal));  // open: in0
  // Probe on MDin
  Register #(.width(32), .trigger("rising"), .Select("low")) register_1 (
    .D(multiplexer_4_out), .Q(LedData), .clk(CLK));  // open: en, clr
  \单周期硬布线控制器  \u_单周期硬布线控制器_1  (
    .Func(IR[5:0]), .OP(IR[31:26]), .ALU_OP(\单周期硬布线控制器_1_alu_op ), .MemToReg(\单周期硬布线控制器_1_memtoreg ),
    .MemWrite(MemWrite), .ALU_SRC(\单周期硬布线控制器_1_alu_src ), .RegWrite(RegWrite), .SysCALL(Syscall),
    .SignedExt(SignedExt), .RegDst(\单周期硬布线控制器_1_regdst ), .JR(JR), .JMP(JMP), .Beq(Beq), .JAL(JAL),
    .Bne(Bne), .SRLV(SRLV), .LBU(LBU), .BGTZ(BGTZ));
  Multiplexer #(.select(1), .width(5), .disabled("Z"), .enable("false")) multiplexer_5 (
    .in0(IR[20:16]), .in1(IR[15:11]), .out(multiplexer_5_out), .sel(\单周期硬布线控制器_1_regdst ));
  Multiplexer #(.select(1), .width(5), .disabled("Z"), .enable("false")) multiplexer_6 (
    .in0(multiplexer_5_out), .in1({5{1'b1}}), .out(multiplexer_6_out), .sel(JAL));
  assign bit_extender_1_out = {{6{1'b0}}, IR[25:0]};  // Bit_Extender bit_extender_1
  assign bit_extender_2_out = {{16{1'b0}}, IR[15:0]};  // Bit_Extender bit_extender_2
  assign bit_extender_3_out = {{16{IR[15]}}, IR[15:0]};  // Bit_Extender bit_extender_3
  or or_2 (branch, and_3_out, and_4_out, and_5_out);
  Multiplexer #(.select(1), .width(5), .disabled("Z"), .enable("false")) multiplexer_7 (
    .in0(IR[25:21]), .in1(5'b00010), .out(multiplexer_7_out), .sel(Syscall));
  Multiplexer #(.select(1), .width(5), .disabled("Z"), .enable("false")) multiplexer_8 (
    .in0(IR[20:16]), .in1(5'b00100), .out(multiplexer_8_out), .sel(Syscall));
  MIPS_Regifile mips_regifile_1 (
    .Din(RDin), .Clk(CLK), .R1(JRPC), .R2(MDin), .WE(RegWrite), .W_num(multiplexer_6_out),
    .R1_num(multiplexer_7_out), .R2_num(multiplexer_8_out));
  Shifter #(.width(32), .shift("ll")) shifter_1 (.in(bit_extender_1_out), .\dist (5'b00010), .out(shifter_1_out));
  assign JPC = shifter_1_out | {PC_4[31:28], {28{1'b0}}};  // OR_Gate or_3, 32 bits wide
  Multiplexer #(.select(1), .width(32), .disabled("Z"), .enable("false")) multiplexer_9 (
    .in0(bit_extender_2_out), .in1(bit_extender_3_out), .out(multiplexer_9_out), .sel(SignedExt));
  Shifter #(.width(32), .shift("ll")) shifter_2 (.in(bit_extender_3_out), .\dist (5'b00010), .out(shifter_2_out));
  and and_3 (and_3_out, Bne, not_3_out);
  not not_3 (not_3_out, mips_alu_1_equal);
  Multiplexer #(.select(1), .width(32), .disabled("Z"), .enable("false")) multiplexer_10 (
    .in0(MDin), .in1(multiplexer_9_out), .out(multiplexer_10_out), .sel(\单周期硬布线控制器_1_alu_src ));
  Adder #(.width(32)) adder_2 (.a(shifter_2_out), .b(PC_4), .out(adder_2_out));  // open: cin, cout
  Counter #(.width(16), .max('hffff), .ongoal("wrap"), .trigger("rising"), .behavior("old")) counter_2 (
    .D({16{1'b0}}), .count(JMP), .Q(\无条件 ), .clk(CLK));  // open: load, carry, clr, preset
  Multiplexer #(.select(1), .width(32), .disabled("Z"), .enable("false")) multiplexer_11 (
    .in0(JRPC), .in1(multiplexer_10_out), .out(multiplexer_11_out), .sel(SRLV));
  // Probe on \无条件 
  and and_4 (and_4_out, not_5_out, not_4_out, BGTZ);
  and and_5 (and_5_out, Beq, mips_alu_1_equal);
  not not_4 (not_4_out, mips_alu_1_equal);
  not not_5 (not_5_out, mips_alu_1_result[0]);
  MIPS_ALU mips_alu_1 (
    .X(multiplexer_11_out), .Y(multiplexer_10_out), .AluOP(\单周期硬布线控制器_1_alu_op ), .Equal(mips_alu_1_equal),
    .Result(mips_alu_1_result), .shamt(multiplexer_12_out));  // open: Result_2
  Multiplexer #(.select(1), .width(5), .disabled("Z"), .enable("false")) multiplexer_12 (
    .in0(IR[10:6]), .in1(JRPC[4:0]), .out(multiplexer_12_out), .sel(SRLV));
  Multiplexer #(.select(1), .width(32), .disabled("Z"), .enable("false")) multiplexer_13 (
    .in0(multiplexer_15_out), .in1(PC_4), .out(RDin), .sel(JAL));
  Counter #(.width(16), .max('hffff), .ongoal("wrap"), .trigger("rising"), .behavior("old")) counter_3 (
    .D({16{1'b0}}), .count(branch), .Q(\有条件 ), .clk(CLK));  // open: load, carry, clr, preset
  // Probe on \有条件 
  RAM #(.addrWidth(10), .dataWidth(32), .bus("separate"), .Select("high")) ram_1 (
    .addr(mips_alu_1_result[11:2]), .din(MDin), .data(ram_1_data), .str(MemWrite), .sel(1'b1), .clk(CLK));  // open: ld, clr
  Multiplexer #(.select(1), .width(32), .disabled("Z"), .enable("false")) multiplexer_14 (
    .in0(mips_alu_1_result), .in1(ram_1_data), .out(multiplexer_14_out), .sel(\单周期硬布线控制器_1_memtoreg ));
  Shifter #(.width(32), .shift("ll")) shifter_3 (
    .in(32'hff), .\dist ({mips_alu_1_result[1:0], 3'b000}), .out(shifter_3_out));
  assign and_6_out = multiplexer_14_out & shifter_3_out;  // AND_Gate and_6, 32 bits wide
  Shifter #(.width(32), .shift("lr")) shifter_4 (
    .in(and_6_out), .\dist ({mips_alu_1_result[1:0], 3'b000}), .out(shifter_4_out));
  Multiplexer #(.select(1), .width(32), .disabled("Z"), .enable("false")) multiplexer_15 (
    .in0(multiplexer_14_out), .in1(shifter_4_out), .out(multiplexer_15_out), .sel(LBU));

  // Other names for the same wires on the sheet: a0[31:0] = MDin; v0[31:0] = JRPC

  // Notes on the sheet:
  //   中断源
  //   中断等待指示
  //   总复位信号应将除ROM以外所有存储组件全部清零
  //   数码管输出
  //   数码管输出应该用寄存器锁存，否则显示数据只能一闪而过
  //   指令存储器
  //   为方便自动评测，需要输出PC，IR，寄存器文件写入端口RDin，内存写入端口MDin等信号
  //   contents of rom_1 (hex, n*v repeats v):
  //   20110001 8000c05 20110001 20120002 20130003 8000c09 20110001 20120002 20130003 8000c0d 20110001
  //   20120002 20130003 8000c11 20110001 20120002 20130003 c000cb8 20100001 20110001 118fc0 112020
  //   20020022 c 118882 12200001 8000c15 112020 20020022 c 20110001 118880 112020 20020022 c 12200001
  //   8000c1f 20110001 118fc0 112020 20020022 c 1188c3 112020 20020022 c 118903 112020 20020022 c 118903
  //   112020 20020022 c 118903 112020 20020022 c 118903 112020 20020022 c 118903 112020 20020022 c 118903
  //   112020 20020022 c 118903 112020 20020022 c 20100001 109fc0 139fc3 8021 2012000c 24160003 26100001
  //   3210000f 20080008 20090001 139900 2709825 132020 20020022 c 1094022 1500fff9 22100001 2018000f
  //   2188024 108700 20080008 20090001 139902 2709825 132021 20020022 c 1094022 1500fff9 108702 2c9b022
  //   12c00001 8000c50 4020 1084027 84400 3508ffff 82021 20020022 c 2010ffff 20110000 ae300000 22100001
  //   22310004 ae300000 22100001 22310004 ae300000 22100001 22310004 ae300000 22100001 22310004 ae300000
  //   22100001 22310004 ae300000 22100001 22310004 ae300000 22100001 22310004 ae300000 22100001 22310004
  //   ae300000 22100001 22310004 ae300000 22100001 22310004 ae300000 22100001 22310004 ae300000 22100001
  //   22310004 ae300000 22100001 22310004 ae300000 22100001 22310004 ae300000 22100001 22310004 ae300000
  //   22100001 22310004 22100001 8020 2011003c 8e130000 8e340000 274402a 11000002 ae330000 ae140000
  //   2231fffc 1611fff8 102020 20020022 c 22100004 2011003c 1611fff2 20020032 c 20100000 22100001 102020
  //   20020022 c 22100002 102020 20020022 c 22100003 102020 20020022 c 22100004 102020 20020022 c 22100005
  //   102020 20020022 c 22100006 102020 20020022 c 22100007 102020 20020022 c 22100008 102020 20020022
  //   20020022 c 3e00008
  //   OP
  //   Func
  //   rs
  //   指令字
  //   rt
  //   rd
  //   JMP
  //   JR
  //   OP
  //   Func
  //   Syscall
  //   Beq
  //   Bne
  //   MemToReg
  //   MemWrite
  //   AluOP
  //   AluSrcB
  //   RegWrite
  //   JAL
  //   RegDst
endmodule

// 单周期硬布线控制器
module \单周期硬布线控制器  (
  input  [5:0] OP,
  input  [5:0] Func,
  output [3:0] ALU_OP,
  output MemToReg,
  output MemWrite,
  output ALU_SRC,
  output RegWrite,
  output SysCALL,
  output SignedExt,
  output RegDst,
  output Beq,
  output Bne,
  output JR,
  output JMP,
  output JAL,
  output SRLV,
  output LBU,
  output BGTZ
);

  \运算控制器自动生成  \u_运算控制器自动生成_1  (
    .OP0(OP[0]), .OP1(OP[1]), .OP2(OP[2]), .OP3(OP[3]), .OP4(OP[4]), .OP5(OP[5]), .F0(Func[0]), .F1(Func[1]),
    .F2(Func[2]), .F3(Func[3]), .F4(Func[4]), .F5(Func[5]), .S0(ALU_OP[0]), .S1(ALU_OP[1]), .S2(ALU_OP[2]),
    .S3(ALU_OP[3]));
  \控制信号自动生成  \u_控制信号自动生成_1  (
    .OP0(OP[0]), .OP1(OP[1]), .OP2(OP[2]), .OP3(OP[3]), .OP4(OP[4]), .OP5(OP[5]), .F0(Func[0]), .F1(Func[1]),
    .F2(Func[2]), .F3(Func[3]), .F4(Func[4]), .F5(Func[5]), .MemToReg(MemToReg), .MemWrite(MemWrite),
    .ALU_SRC(ALU_SRC), .RegWrite(RegWrite), .SysCALL(SysCALL), .SignedExt(SignedExt), .RegDst(RegDst),
    .BEQ(Beq), .BNE(Bne), .JR(JR), .JUMP(JMP), .JAL(JAL), .SRLV(SRLV), .LBU(LBU), .BGTZ(BGTZ));

  // Other names for the same wires on the sheet: OP_CODE[5:0] = OP

  // Notes on the sheet:
  //   运算器控制器，根据指令生成运算器功能选择信号
  //   控制信号生成，产生数据通路需要的其他控制信号
endmodule

// 运算器控制器
module \运算控制器自动生成  (
  input  OP0,
  input  OP1,
  input  OP2,
  input  OP3,
  input  OP4,
  input  OP5,
  input  F0,
  input  F1,
  input  F2,
  input  F3,
  input  F4,
  input  F5,
  output S0,
  output S1,
  output S2,
  output S3
);

  wire and_1_out, and_2_out, and_3_out, and_4_out, and_5_out, and_6_out, and_7_out, and_8_out, and_9_out,
       and_10_out, and_11_out, and_12_out, and_13_out, and_14_out, and_15_out, and_16_out, and_17_out,
       and_18_out, and_19_out, and_20_out, and_21_out, and_22_out, and_23_out, and_24_out, and_25_out,
       and_26_out, and_27_out, and_28_out, and_29_out, and_30_out, and_31_out, and_32_out, and_33_out,
       and_34_out, and_35_out, and_36_out, and_37_out, and_38_out, and_39_out, and_40_out, and_41_out,
       and_42_out, not_1_out, not_2_out, not_3_out, not_4_out, not_5_out, not_6_out, not_7_out, not_8_out,
       not_9_out, not_10_out, not_11_out, not_12_out, not_13_out, not_14_out, not_15_out, not_16_out,
       not_17_out, not_18_out, not_19_out, not_20_out, not_21_out, not_22_out, not_23_out, not_24_out,
       not_25_out, not_26_out, not_27_out, not_28_out, not_29_out, not_30_out, not_31_out, not_32_out,
       not_33_out, not_34_out, not_35_out, not_36_out, not_37_out, not_38_out, not_39_out, not_40_out,
       not_41_out, not_42_out, not_43_out, not_44_out, not_45_out, not_46_out, not_47_out, not_48_out,
       not_49_out, not_50_out, not_51_out, not_52_out, not_53_out, not_54_out, not_55_out, not_56_out,
       not_57_out, not_58_out, not_59_out, not_60_out, not_61_out, not_62_out, not_63_out, not_64_out,
       not_65_out, not_66_out, not_67_out, not_68_out, not_69_out, not_70_out, not_71_out, not_72_out,
       not_73_out, not_74_out, not_75_out, not_76_out, not_77_out, not_78_out, not_79_out, not_80_out,
       not_81_out, not_82_out, not_83_out, not_84_out, not_85_out, not_86_out, not_87_out, not_88_out,
       not_89_out, not_90_out, not_91_out, not_92_out, not_93_out, not_94_out, not_95_out, not_96_out,
       not_97_out, not_98_out, not_99_out, not_100_out, not_101_out, not_102_out, not_103_out, not_104_out,
       not_105_out, not_106_out, not_107_out, not_108_out, not_109_out, not_110_out, not_111_out,
       not_112_out, not_113_out, not_114_out, not_115_out, not_116_out, not_117_out, not_118_out,
       not_119_out, not_120_out, not_121_out, not_122_out, not_123_out, not_124_out, not_125_out,
       not_126_out, not_127_out, not_128_out, not_129_out, not_130_out, not_131_out, not_132_out,
       not_133_out, not_134_out, not_135_out, not_136_out, not_137_out, not_138_out, not_139_out,
       not_140_out, not_141_out, not_142_out, not_143_out, not_144_out, not_145_out, not_146_out,
       not_147_out, not_148_out, not_149_out, not_150_out, not_151_out, not_152_out, not_153_out,
       not_154_out, not_155_out, not_156_out, not_157_out, not_158_out, not_159_out, not_160_out,
       not_161_out, not_162_out, not_163_out, not_164_out, not_165_out, not_166_out, not_167_out,
       not_168_out, not_169_out, not_170_out, not_171_out, not_172_out, not_173_out, not_174_out,
       not_175_out, not_176_out, not_177_out, not_178_out, not_179_out, not_180_out, not_181_out,
       not_182_out, not_183_out, not_184_out, not_185_out, not_186_out, not_187_out, not_188_out,
       not_189_out, not_190_out, not_191_out, not_192_out, not_193_out, not_194_out, not_195_out,
       not_196_out, not_197_out, not_198_out, not_199_out, not_200_out, not_201_out, not_202_out,
       not_203_out, not_204_out, not_205_out, not_206_out, not_207_out, not_208_out, not_209_out,
       not_210_out, not_211_out, not_212_out, not_213_out, not_214_out, not_215_out, not_216_out,
       not_217_out, not_218_out, not_219_out, not_220_out, not_221_out, not_222_out, not_223_out,
       not_224_out, not_225_out, not_226_out, not_227_out, not_228_out, not_229_out, not_230_out,
       not_231_out, not_232_out, not_233_out, not_234_out, not_235_out, not_236_out, not_237_out,
       not_238_out, not_239_out, not_240_out, not_241_out, not_242_out, not_243_out, not_244_out,
       not_245_out, not_246_out, not_247_out, not_248_out, not_249_out, not_250_out, not_251_out,
       not_252_out, not_253_out, not_254_out, not_255_out, not_256_out, not_257_out, not_258_out,
       not_259_out, not_260_out, not_261_out, not_262_out, not_263_out, not_264_out, not_265_out,
       not_266_out, not_267_out, not_268_out, not_269_out, not_270_out, not_271_out, not_272_out,
       not_273_out, not_274_out, not_275_out, not_276_out, not_277_out, not_278_out, not_279_out,
       not_280_out, not_281_out;

  not not_1 (not_1_out, OP5);
  not not_2 (not_2_out, OP4);
  not not_3 (not_3_out, OP3);
  not not_4 (not_4_out, OP2);
  not not_5 (not_5_out, OP1);
  not not_6 (not_6_out, OP0);
  not not_7 (not_7_out, F5);
  not not_8 (not_8_out, F4);
  not not_9 (not_9_out, F3);
  not not_10 (not_10_out, F2);
  not not_11 (not_11_out, OP5);
  not not_12 (not_12_out, OP4);
  not not_13 (not_13_out, OP3);
  not not_14 (not_14_out, OP2);
  not not_15 (not_15_out, OP1);
  not not_16 (not_16_out, OP0);
  not not_17 (not_17_out, F4);
  not not_18 (not_18_out, F3);
  not not_19 (not_19_out, F2);
  not not_20 (not_20_out, F1);
  not not_21 (not_21_out, F0);
  not not_22 (not_22_out, OP5);
  not not_23 (not_23_out, OP4);
  not not_24 (not_24_out, OP3);
  not not_25 (not_25_out, OP2);
  not not_26 (not_26_out, OP1);
  not not_27 (not_27_out, OP0);
  not not_28 (not_28_out, F4);
  not not_29 (not_29_out, F3);
  not not_30 (not_30_out, F2);
  not not_31 (not_31_out, F1);
  not not_32 (not_32_out, OP5);
  not not_33 (not_33_out, OP4);
  not not_34 (not_34_out, OP3);
  not not_35 (not_35_out, OP2);
  not not_36 (not_36_out, OP1);
  not not_37 (not_37_out, OP0);
  not not_38 (not_38_out, F4);
  not not_39 (not_39_out, F3);
  not not_40 (not_40_out, F1);
  not not_41 (not_41_out, F0);
  not not_42 (not_42_out, OP5);
  not not_43 (not_43_out, OP4);
  not not_44 (not_44_out, OP3);
  not not_45 (not_45_out, OP2);
  not not_46 (not_46_out, OP1);
  not not_47 (not_47_out, OP0);
  not not_48 (not_48_out, F4);
  not not_49 (not_49_out, F2);
  not not_50 (not_50_out, F0);
  not not_51 (not_51_out, OP5);
  not not_52 (not_52_out, OP4);
  not not_53 (not_53_out, OP2);
  not not_54 (not_54_out, OP1);
  not not_55 (not_55_out, OP0);
  not not_56 (not_56_out, OP5);
  not not_57 (not_57_out, OP4);
  not not_58 (not_58_out, OP1);
  not not_59 (not_59_out, OP0);
  not not_60 (not_60_out, OP5);
  not not_61 (not_61_out, OP4);
  not not_62 (not_62_out, OP2);
  not not_63 (not_63_out, OP1);
  not not_64 (not_64_out, OP5);
  not not_65 (not_65_out, OP4);
  not not_66 (not_66_out, OP2);
  not not_67 (not_67_out, OP0);
  not not_68 (not_68_out, OP4);
  not not_69 (not_69_out, OP3);
  not not_70 (not_70_out, OP2);
  not not_71 (not_71_out, OP4);
  not not_72 (not_72_out, OP2);
  not not_73 (not_73_out, OP5);
  not not_74 (not_74_out, OP4);
  not not_75 (not_75_out, OP3);
  not not_76 (not_76_out, OP2);
  not not_77 (not_77_out, OP1);
  not not_78 (not_78_out, OP0);
  not not_79 (not_79_out, F4);
  not not_80 (not_80_out, F3);
  not not_81 (not_81_out, F0);
  not not_82 (not_82_out, OP4);
  not not_83 (not_83_out, OP3);
  not not_84 (not_84_out, OP1);
  not not_85 (not_85_out, OP0);
  not not_86 (not_86_out, OP5);
  not not_87 (not_87_out, OP4);
  not not_88 (not_88_out, OP3);
  not not_89 (not_89_out, OP5);
  not not_90 (not_90_out, OP4);
  not not_91 (not_91_out, OP3);
  not not_92 (not_92_out, OP2);
  not not_93 (not_93_out, OP1);
  not not_94 (not_94_out, OP0);
  not not_95 (not_95_out, F5);
  not not_96 (not_96_out, F4);
  not not_97 (not_97_out, F3);
  not not_98 (not_98_out, F2);
  not not_99 (not_99_out, F0);
  not not_100 (not_100_out, OP5);
  not not_101 (not_101_out, OP4);
  not not_102 (not_102_out, OP3);
  not not_103 (not_103_out, OP2);
  not not_104 (not_104_out, OP1);
  not not_105 (not_105_out, OP0);
  not not_106 (not_106_out, F4);
  not not_107 (not_107_out, F3);
  not not_108 (not_108_out, F2);
  not not_109 (not_109_out, F0);
  not not_110 (not_110_out, OP5);
  not not_111 (not_111_out, OP4);
  not not_112 (not_112_out, OP3);
  not not_113 (not_113_out, OP2);
  not not_114 (not_114_out, OP1);
  not not_115 (not_115_out, OP0);
  not not_116 (not_116_out, F4);
  not not_117 (not_117_out, F3);
  not not_118 (not_118_out, F1);
  not not_119 (not_119_out, F0);
  not not_120 (not_120_out, OP5);
  not not_121 (not_121_out, OP4);
  not not_122 (not_122_out, OP3);
  not not_123 (not_123_out, OP2);
  not not_124 (not_124_out, OP1);
  not not_125 (not_125_out, OP0);
  not not_126 (not_126_out, F4);
  not not_127 (not_127_out, F3);
  not not_128 (not_128_out, OP5);
  not not_129 (not_129_out, OP4);
  not not_130 (not_130_out, OP3);
  not not_131 (not_131_out, OP2);
  not not_132 (not_132_out, OP1);
  not not_133 (not_133_out, OP0);
  not not_134 (not_134_out, F4);
  not not_135 (not_135_out, F2);
  not not_136 (not_136_out, F0);
  not not_137 (not_137_out, OP5);
  not not_138 (not_138_out, OP4);
  not not_139 (not_139_out, OP1);
  not not_140 (not_140_out, OP0);
  not not_141 (not_141_out, OP5);
  not not_142 (not_142_out, OP4);
  not not_143 (not_143_out, OP2);
  not not_144 (not_144_out, OP0);
  not not_145 (not_145_out, OP5);
  not not_146 (not_146_out, OP4);
  not not_147 (not_147_out, OP3);
  not not_148 (not_148_out, OP2);
  not not_149 (not_149_out, OP1);
  not not_150 (not_150_out, OP0);
  not not_151 (not_151_out, F5);
  not not_152 (not_152_out, F4);
  not not_153 (not_153_out, F3);
  not not_154 (not_154_out, F0);
  not not_155 (not_155_out, OP5);
  not not_156 (not_156_out, OP4);
  not not_157 (not_157_out, OP3);
  not not_158 (not_158_out, OP5);
  not not_159 (not_159_out, OP4);
  not not_160 (not_160_out, OP3);
  not not_161 (not_161_out, OP2);
  not not_162 (not_162_out, OP1);
  not not_163 (not_163_out, OP0);
  not not_164 (not_164_out, F4);
  not not_165 (not_165_out, F3);
  not not_166 (not_166_out, F2);
  not not_167 (not_167_out, F1);
  not not_168 (not_168_out, F0);
  not not_169 (not_169_out, OP5);
  not not_170 (not_170_out, OP4);
  not not_171 (not_171_out, OP3);
  not not_172 (not_172_out, OP2);
  not not_173 (not_173_out, OP1);
  not not_174 (not_174_out, OP0);
  not not_175 (not_175_out, F4);
  not not_176 (not_176_out, F3);
  not not_177 (not_177_out, F2);
  not not_178 (not_178_out, F1);
  not not_179 (not_179_out, OP5);
  not not_180 (not_180_out, OP4);
  not not_181 (not_181_out, OP3);
  not not_182 (not_182_out, OP2);
  not not_183 (not_183_out, OP1);
  not not_184 (not_184_out, OP0);
  not not_185 (not_185_out, F4);
  not not_186 (not_186_out, F3);
  not not_187 (not_187_out, F2);
  not not_188 (not_188_out, F0);
  not not_189 (not_189_out, OP5);
  not not_190 (not_190_out, OP4);
  not not_191 (not_191_out, OP3);
  not not_192 (not_192_out, OP2);
  not not_193 (not_193_out, OP1);
  not not_194 (not_194_out, OP0);
  not not_195 (not_195_out, F4);
  not not_196 (not_196_out, F3);
  not not_197 (not_197_out, F1);
  not not_198 (not_198_out, F0);
  not not_199 (not_199_out, OP5);
  not not_200 (not_200_out, OP4);
  not not_201 (not_201_out, OP3);
  not not_202 (not_202_out, OP2);
  not not_203 (not_203_out, OP1);
  not not_204 (not_204_out, OP0);
  not not_205 (not_205_out, F4);
  not not_206 (not_206_out, F2);
  not not_207 (not_207_out, OP5);
  not not_208 (not_208_out, OP4);
  not not_209 (not_209_out, OP2);
  not not_210 (not_210_out, OP1);
  not not_211 (not_211_out, OP0);
  not not_212 (not_212_out, OP5);
  not not_213 (not_213_out, OP4);
  not not_214 (not_214_out, OP1);
  not not_215 (not_215_out, OP0);
  not not_216 (not_216_out, OP5);
  not not_217 (not_217_out, OP4);
  not not_218 (not_218_out, OP2);
  not not_219 (not_219_out, OP1);
  not not_220 (not_220_out, OP4);
  not not_221 (not_221_out, OP3);
  not not_222 (not_222_out, OP2);
  not not_223 (not_223_out, OP4);
  not not_224 (not_224_out, OP2);
  not not_225 (not_225_out, OP4);
  not not_226 (not_226_out, OP3);
  not not_227 (not_227_out, OP1);
  not not_228 (not_228_out, OP0);
  not not_229 (not_229_out, OP5);
  not not_230 (not_230_out, OP4);
  not not_231 (not_231_out, OP3);
  not not_232 (not_232_out, OP2);
  not not_233 (not_233_out, OP1);
  not not_234 (not_234_out, OP0);
  not not_235 (not_235_out, F4);
  not not_236 (not_236_out, F3);
  not not_237 (not_237_out, F1);
  not not_238 (not_238_out, OP5);
  not not_239 (not_239_out, OP4);
  not not_240 (not_240_out, OP3);
  not not_241 (not_241_out, OP2);
  not not_242 (not_242_out, OP1);
  not not_243 (not_243_out, OP0);
  not not_244 (not_244_out, F4);
  not not_245 (not_245_out, F3);
  not not_246 (not_246_out, OP5);
  not not_247 (not_247_out, OP4);
  not not_248 (not_248_out, OP3);
  not not_249 (not_249_out, OP2);
  not not_250 (not_250_out, OP1);
  not not_251 (not_251_out, OP0);
  not not_252 (not_252_out, F4);
  not not_253 (not_253_out, F2);
  not not_254 (not_254_out, F0);
  not not_255 (not_255_out, OP5);
  not not_256 (not_256_out, OP4);
  not not_257 (not_257_out, OP3);
  not not_258 (not_258_out, OP2);
  not not_259 (not_259_out, OP1);
  not not_260 (not_260_out, OP0);
  not not_261 (not_261_out, F4);
  not not_262 (not_262_out, F2);
  not not_263 (not_263_out, OP5);
  not not_264 (not_264_out, OP4);
  not not_265 (not_265_out, OP2);
  not not_266 (not_266_out, OP0);
  not not_267 (not_267_out, OP5);
  not not_268 (not_268_out, OP4);
  not not_269 (not_269_out, OP1);
  not not_270 (not_270_out, OP5);
  not not_271 (not_271_out, OP4);
  not not_272 (not_272_out, OP3);
  not not_273 (not_273_out, OP2);
  not not_274 (not_274_out, OP1);
  not not_275 (not_275_out, OP0);
  not not_276 (not_276_out, F4);
  not not_277 (not_277_out, F3);
  not not_278 (not_278_out, F0);
  not not_279 (not_279_out, OP5);
  not not_280 (not_280_out, OP4);
  not not_281 (not_281_out, OP3);
  and and_1 (and_1_out, not_1_out, not_2_out, not_3_out, not_4_out, not_5_out, not_6_out, not_7_out, not_8_out, not_9_out, not_10_out, F1, F0);
  and and_2 (and_2_out, not_11_out, not_12_out, not_13_out, not_14_out, not_15_out, not_16_out, F5, not_17_out, not_18_out, not_19_out, not_20_out, not_21_out);
  and and_3 (and_3_out, not_22_out, not_23_out, not_24_out, not_25_out, not_26_out, not_27_out, F5, not_28_out, not_29_out, not_30_out, not_31_out, F0);
  and and_4 (and_4_out, not_32_out, not_33_out, not_34_out, not_35_out, not_36_out, not_37_out, F5, not_38_out, not_39_out, F2, not_40_out, not_41_out);
  and and_5 (and_5_out, not_42_out, not_43_out, not_44_out, not_45_out, not_46_out, not_47_out, F5, not_48_out, F3, not_49_out, F1, not_50_out);
  and and_6 (and_6_out, not_51_out, not_52_out, OP3, not_53_out, not_54_out, not_55_out);
  and and_7 (and_7_out, not_56_out, not_57_out, OP3, OP2, not_58_out, not_59_out);
  and and_8 (and_8_out, not_60_out, not_61_out, OP3, not_62_out, not_63_out, OP0);
  and and_9 (and_9_out, not_64_out, not_65_out, OP3, not_66_out, OP1, not_67_out);
  and and_10 (and_10_out, OP5, not_68_out, not_69_out, not_70_out, OP1, OP0);
  and and_11 (and_11_out, OP5, not_71_out, OP3, not_72_out, OP1, OP0);
  and and_12 (and_12_out, not_73_out, not_74_out, not_75_out, not_76_out, not_77_out, not_78_out, F5, not_79_out, not_80_out, F2, F1, not_81_out);
  and and_13 (and_13_out, OP5, not_82_out, not_83_out, OP2, not_84_out, not_85_out);
  and and_14 (and_14_out, not_86_out, not_87_out, not_88_out, OP2, OP1, OP0);
  and and_15 (and_15_out, not_89_out, not_90_out, not_91_out, not_92_out, not_93_out, not_94_out, not_95_out, not_96_out, not_97_out, not_98_out, F1, not_99_out);
  and and_16 (and_16_out, not_100_out, not_101_out, not_102_out, not_103_out, not_104_out, not_105_out, F5, not_106_out, not_107_out, not_108_out, F1, not_109_out);
  and and_17 (and_17_out, not_110_out, not_111_out, not_112_out, not_113_out, not_114_out, not_115_out, F5, not_116_out, not_117_out, F2, not_118_out, not_119_out);
  and and_18 (and_18_out, not_120_out, not_121_out, not_122_out, not_123_out, not_124_out, not_125_out, F5, not_126_out, not_127_out, F2, F1, F0);
  and and_19 (and_19_out, not_128_out, not_129_out, not_130_out, not_131_out, not_132_out, not_133_out, F5, not_134_out, F3, not_135_out, F1, not_136_out);
  and and_20 (and_20_out, not_137_out, not_138_out, OP3, OP2, not_139_out, not_140_out);
  and and_21 (and_21_out, not_141_out, not_142_out, OP3, not_143_out, OP1, not_144_out);
  and and_22 (and_22_out, not_145_out, not_146_out, not_147_out, not_148_out, not_149_out, not_150_out, not_151_out, not_152_out, not_153_out, F2, F1, not_154_out);
  and and_23 (and_23_out, not_155_out, not_156_out, not_157_out, OP2, OP1, OP0);
  and and_24 (and_24_out, not_158_out, not_159_out, not_160_out, not_161_out, not_162_out, not_163_out, F5, not_164_out, not_165_out, not_166_out, not_167_out, not_168_out);
  and and_25 (and_25_out, not_169_out, not_170_out, not_171_out, not_172_out, not_173_out, not_174_out, F5, not_175_out, not_176_out, not_177_out, not_178_out, F0);
  and and_26 (and_26_out, not_179_out, not_180_out, not_181_out, not_182_out, not_183_out, not_184_out, F5, not_185_out, not_186_out, not_187_out, F1, not_188_out);
  and and_27 (and_27_out, not_189_out, not_190_out, not_191_out, not_192_out, not_193_out, not_194_out, F5, not_195_out, not_196_out, F2, not_197_out, not_198_out);
  and and_28 (and_28_out, not_199_out, not_200_out, not_201_out, not_202_out, not_203_out, not_204_out, F5, not_205_out, F3, not_206_out, F1, F0);
  and and_29 (and_29_out, not_207_out, not_208_out, OP3, not_209_out, not_210_out, not_211_out);
  and and_30 (and_30_out, not_212_out, not_213_out, OP3, OP2, not_214_out, not_215_out);
  and and_31 (and_31_out, not_216_out, not_217_out, OP3, not_218_out, not_219_out, OP0);
  and and_32 (and_32_out, OP5, not_220_out, not_221_out, not_222_out, OP1, OP0);
  and and_33 (and_33_out, OP5, not_223_out, OP3, not_224_out, OP1, OP0);
  and and_34 (and_34_out, OP5, not_225_out, not_226_out, OP2, not_227_out, not_228_out);
  and and_35 (and_35_out, not_229_out, not_230_out, not_231_out, not_232_out, not_233_out, not_234_out, F5, not_235_out, not_236_out, F2, not_237_out, F0);
  and and_36 (and_36_out, not_238_out, not_239_out, not_240_out, not_241_out, not_242_out, not_243_out, F5, not_244_out, not_245_out, F2, F1, F0);
  and and_37 (and_37_out, not_246_out, not_247_out, not_248_out, not_249_out, not_250_out, not_251_out, F5, not_252_out, F3, not_253_out, F1, not_254_out);
  and and_38 (and_38_out, not_255_out, not_256_out, not_257_out, not_258_out, not_259_out, not_260_out, F5, not_261_out, F3, not_262_out, F1, F0);
  and and_39 (and_39_out, not_263_out, not_264_out, OP3, not_265_out, OP1, not_266_out);
  and and_40 (and_40_out, not_267_out, not_268_out, OP3, OP2, not_269_out, OP0);
  and and_41 (and_41_out, not_270_out, not_271_out, not_272_out, not_273_out, not_274_out, not_275_out, F5, not_276_out, not_277_out, F2, F1, not_278_out);
  and and_42 (and_42_out, not_279_out, not_280_out, not_281_out, OP2, OP1, OP0);
  or or_1 (S1, and_15_out, and_16_out, and_17_out, and_18_out, and_19_out, and_20_out, and_21_out, and_22_out, and_23_out);
  or or_2 (S2, and_24_out, and_25_out, and_26_out, and_27_out, and_28_out, and_29_out, and_30_out, and_31_out, and_32_out, and_33_out, and_34_out);
  or or_3 (S3, and_35_out, and_36_out, and_37_out, and_38_out, and_39_out, and_40_out, and_41_out, and_42_out);
  or or_4 (S0, and_1_out, and_2_out, and_3_out, and_4_out, and_5_out, and_6_out, and_7_out, and_8_out, and_9_out, and_10_out, and_11_out, and_12_out, and_13_out, and_14_out);
endmodule

// 控制信号生成
module \控制信号自动生成  (
  input  OP0,
  input  OP1,
  input  OP2,
  input  OP3,
  input  OP4,
  input  OP5,
  input  F0,
  input  F1,
  input  F2,
  input  F3,
  input  F4,
  input  F5,
  output MemToReg,
  output MemWrite,
  output ALU_SRC,
  output RegWrite,
  output SysCALL,
  output SignedExt,
  output RegDst,
  output BEQ,
  output BNE,
  output JR,
  output JUMP,
  output JAL,
  output SRLV,
  output LBU,
  output BGTZ
);

  wire and_1_out, and_2_out, and_4_out, and_5_out, and_6_out, and_7_out, and_8_out, and_9_out, and_10_out,
       and_11_out, and_12_out, and_13_out, and_14_out, and_15_out, and_16_out, and_17_out, and_18_out,
       and_19_out, and_20_out, and_21_out, and_22_out, and_23_out, and_24_out, and_25_out, and_26_out,
       and_27_out, and_28_out, and_29_out, and_30_out, and_31_out, and_32_out, and_34_out, and_35_out,
       and_36_out, and_37_out, and_38_out, and_39_out, and_40_out, and_41_out, and_42_out, and_43_out,
       and_44_out, and_45_out, and_46_out, and_47_out, and_48_out, and_49_out, and_50_out, and_51_out,
       and_52_out, and_53_out, and_57_out, and_58_out, and_59_out, not_1_out, not_2_out, not_3_out,
       not_4_out, not_5_out, not_6_out, not_7_out, not_8_out, not_9_out, not_10_out, not_11_out, not_12_out,
       not_13_out, not_14_out, not_15_out, not_16_out, not_17_out, not_18_out, not_19_out, not_20_out,
       not_21_out, not_22_out, not_23_out, not_24_out, not_25_out, not_26_out, not_27_out, not_28_out,
       not_29_out, not_30_out, not_31_out, not_32_out, not_33_out, not_34_out, not_35_out, not_36_out,
       not_37_out, not_38_out, not_39_out, not_40_out, not_41_out, not_42_out, not_43_out, not_44_out,
       not_45_out, not_46_out, not_47_out, not_48_out, not_49_out, not_50_out, not_51_out, not_52_out,
       not_53_out, not_54_out, not_55_out, not_56_out, not_57_out, not_58_out, not_59_out, not_60_out,
       not_61_out, not_62_out, not_63_out, not_64_out, not_65_out, not_66_out, not_67_out, not_68_out,
       not_69_out, not_70_out, not_71_out, not_72_out, not_73_out, not_74_out, not_75_out, not_76_out,
       not_77_out, not_78_out, not_79_out, not_80_out, not_81_out, not_82_out, not_83_out, not_84_out,
       not_85_out, not_86_out, not_87_out, not_88_out, not_89_out, not_90_out, not_91_out, not_92_out,
       not_93_out, not_94_out, not_95_out, not_96_out, not_97_out, not_98_out, not_99_out, not_100_out,
       not_101_out, not_102_out, not_103_out, not_104_out, not_105_out, not_106_out, not_107_out,
       not_108_out, not_109_out, not_110_out, not_111_out, not_112_out, not_113_out, not_114_out,
       not_115_out, not_116_out, not_117_out, not_118_out, not_119_out, not_120_out, not_121_out,
       not_122_out, not_123_out, not_124_out, not_125_out, not_126_out, not_127_out, not_128_out,
       not_129_out, not_130_out, not_131_out, not_132_out, not_133_out, not_134_out, not_135_out,
       not_136_out, not_137_out, not_138_out, not_139_out, not_140_out, not_141_out, not_142_out,
       not_143_out, not_144_out, not_145_out, not_146_out, not_147_out, not_148_out, not_149_out,
       not_150_out, not_151_out, not_152_out, not_153_out, not_154_out, not_155_out, not_156_out,
       not_157_out, not_158_out, not_159_out, not_160_out, not_161_out, not_162_out, not_163_out,
       not_164_out, not_165_out, not_166_out, not_167_out, not_168_out, not_169_out, not_170_out,
       not_171_out, not_172_out, not_173_out, not_174_out, not_175_out, not_176_out, not_177_out,
       not_178_out, not_179_out, not_180_out, not_181_out, not_182_out, not_183_out, not_184_out,
       not_185_out, not_186_out, not_187_out, not_188_out, not_189_out, not_190_out, not_191_out,
       not_192_out, not_193_out, not_194_out, not_195_out, not_196_out, not_197_out, not_198_out,
       not_199_out, not_200_out, not_201_out, not_202_out, not_203_out, not_204_out, not_205_out,
       not_206_out, not_207_out, not_208_out, not_209_out, not_210_out, not_211_out, not_212_out,
       not_213_out, not_214_out, not_215_out, not_216_out, not_217_out, not_218_out, not_219_out,
       not_220_out, not_221_out, not_222_out, not_223_out, not_224_out, not_225_out, not_226_out,
       not_227_out, not_228_out, not_229_out, not_230_out, not_231_out, not_232_out, not_233_out,
       not_234_out, not_235_out, not_236_out, not_237_out, not_238_out, not_239_out, not_240_out,
       not_241_out, not_242_out, not_243_out, not_244_out, not_245_out, not_246_out, not_247_out,
       not_248_out, not_249_out, not_250_out, not_251_out, not_252_out, not_253_out, not_254_out,
       not_255_out, not_256_out, not_257_out, not_258_out, not_259_out, not_260_out, not_261_out,
       not_262_out, not_263_out, not_264_out, not_265_out, not_266_out, not_267_out, not_268_out,
       not_269_out, not_270_out, not_271_out, not_272_out, not_273_out, not_274_out, not_275_out,
       not_276_out, not_277_out, not_278_out, not_279_out, not_280_out, not_281_out, not_282_out,
       not_283_out, not_284_out, not_285_out, not_286_out, not_287_out, not_288_out, not_289_out,
       not_290_out, not_291_out, not_292_out, not_293_out, not_294_out, not_295_out, not_296_out,
       not_297_out, not_298_out, not_299_out, not_300_out, not_301_out, not_302_out, not_303_out,
       not_304_out, not_305_out, not_306_out, not_307_out, not_308_out, not_309_out, not_310_out,
       not_311_out, not_312_out, not_313_out, not_314_out, not_315_out, not_316_out, not_317_out,
       not_318_out, not_319_out, not_320_out, not_321_out, not_322_out, not_323_out, not_324_out,
       not_325_out, not_326_out, not_327_out, not_328_out, not_329_out, not_330_out, not_331_out,
       not_332_out, not_333_out, not_334_out, not_335_out, not_336_out, not_337_out, not_338_out,
       not_339_out, not_340_out, not_341_out, not_342_out, not_343_out, not_344_out, not_345_out,
       not_346_out, not_347_out, not_348_out, not_349_out, not_350_out, not_351_out, not_352_out,
       not_353_out, not_354_out, not_355_out, not_356_out, not_357_out, not_358_out, not_359_out,
       not_360_out, not_361_out, not_362_out, not_363_out, not_364_out, not_365_out, not_366_out,
       not_367_out, not_368_out, not_369_out, not_370_out, not_371_out, not_372_out, not_373_out,
       not_374_out, not_375_out, not_376_out, not_377_out, not_378_out, not_379_out, not_380_out,
       not_381_out, not_382_out, not_383_out, not_384_out, not_385_out, not_386_out, not_387_out,
       not_388_out, not_389_out, not_390_out, not_391_out, not_392_out, not_393_out, not_394_out,
       not_395_out, not_396_out, not_397_out, not_398_out, not_399_out, not_400_out, not_401_out,
       not_402_out, not_403_out, not_404_out, not_405_out, not_406_out, not_407_out, not_408_out,
       not_409_out, not_410_out, not_411_out, not_412_out, not_413_out, not_414_out, not_415_out,
       not_416_out, not_417_out, not_418_out, not_419_out, not_420_out, not_421_out, not_422_out,
       not_423_out, not_424_out, not_425_out, not_426_out, not_427_out;

  not not_1 (not_1_out, OP4);
  not not_2 (not_2_out, OP3);
  not not_3 (not_3_out, OP2);
  not not_4 (not_4_out, OP4);
  not not_5 (not_5_out, OP3);
  not not_6 (not_6_out, OP1);
  not not_7 (not_7_out, OP0);
  not not_8 (not_8_out, OP4);
  not not_9 (not_9_out, OP2);
  not not_10 (not_10_out, OP5);
  not not_11 (not_11_out, OP4);
  not not_12 (not_12_out, OP2);
  not not_13 (not_13_out, OP1);
  not not_14 (not_14_out, OP0);
  not not_15 (not_15_out, OP5);
  not not_16 (not_16_out, OP4);
  not not_17 (not_17_out, OP1);
  not not_18 (not_18_out, OP0);
  not not_19 (not_19_out, OP5);
  not not_20 (not_20_out, OP4);
  not not_21 (not_21_out, OP2);
  not not_22 (not_22_out, OP1);
  not not_23 (not_23_out, OP5);
  not not_24 (not_24_out, OP4);
  not not_25 (not_25_out, OP2);
  not not_26 (not_26_out, OP0);
  not not_27 (not_27_out, OP5);
  not not_28 (not_28_out, OP4);
  not not_29 (not_29_out, OP1);
  not not_30 (not_30_out, OP4);
  not not_31 (not_31_out, OP3);
  not not_32 (not_32_out, OP2);
  not not_33 (not_33_out, OP4);
  not not_34 (not_34_out, OP2);
  not not_35 (not_35_out, OP4);
  not not_36 (not_36_out, OP3);
  not not_37 (not_37_out, OP1);
  not not_38 (not_38_out, OP0);
  not not_39 (not_39_out, OP5);
  not not_40 (not_40_out, OP4);
  not not_41 (not_41_out, OP3);
  not not_42 (not_42_out, OP2);
  not not_43 (not_43_out, OP1);
  not not_44 (not_44_out, OP0);
  not not_45 (not_45_out, F5);
  not not_46 (not_46_out, F4);
  not not_47 (not_47_out, F3);
  not not_48 (not_48_out, F2);
  not not_49 (not_49_out, F1);
  not not_50 (not_50_out, F0);
  not not_51 (not_51_out, OP5);
  not not_52 (not_52_out, OP4);
  not not_53 (not_53_out, OP3);
  not not_54 (not_54_out, OP2);
  not not_55 (not_55_out, OP1);
  not not_56 (not_56_out, OP0);
  not not_57 (not_57_out, F5);
  not not_58 (not_58_out, F4);
  not not_59 (not_59_out, F3);
  not not_60 (not_60_out, F2);
  not not_61 (not_61_out, OP5);
  not not_62 (not_62_out, OP4);
  not not_63 (not_63_out, OP3);
  not not_64 (not_64_out, OP2);
  not not_65 (not_65_out, OP1);
  not not_66 (not_66_out, OP0);
  not not_67 (not_67_out, F5);
  not not_68 (not_68_out, F4);
  not not_69 (not_69_out, F3);
  not not_70 (not_70_out, F2);
  not not_71 (not_71_out, F0);
  not not_72 (not_72_out, OP5);
  not not_73 (not_73_out, OP4);
  not not_74 (not_74_out, OP3);
  not not_75 (not_75_out, OP2);
  not not_76 (not_76_out, OP1);
  not not_77 (not_77_out, OP0);
  not not_78 (not_78_out, F4);
  not not_79 (not_79_out, F3);
  not not_80 (not_80_out, F2);
  not not_81 (not_81_out, F1);
  not not_82 (not_82_out, F0);
  not not_83 (not_83_out, OP5);
  not not_84 (not_84_out, OP4);
  not not_85 (not_85_out, OP3);
  not not_86 (not_86_out, OP2);
  not not_87 (not_87_out, OP1);
  not not_88 (not_88_out, OP0);
  not not_89 (not_89_out, F4);
  not not_90 (not_90_out, F3);
  not not_91 (not_91_out, F2);
  not not_92 (not_92_out, F1);
  not not_93 (not_93_out, OP5);
  not not_94 (not_94_out, OP4);
  not not_95 (not_95_out, OP3);
  not not_96 (not_96_out, OP2);
  not not_97 (not_97_out, OP1);
  not not_98 (not_98_out, OP0);
  not not_99 (not_99_out, F4);
  not not_100 (not_100_out, F3);
  not not_101 (not_101_out, F2);
  not not_102 (not_102_out, F0);
  not not_103 (not_103_out, OP5);
  not not_104 (not_104_out, OP4);
  not not_105 (not_105_out, OP3);
  not not_106 (not_106_out, OP2);
  not not_107 (not_107_out, OP1);
  not not_108 (not_108_out, OP0);
  not not_109 (not_109_out, F4);
  not not_110 (not_110_out, F3);
  not not_111 (not_111_out, F1);
  not not_112 (not_112_out, F0);
  not not_113 (not_113_out, OP5);
  not not_114 (not_114_out, OP4);
  not not_115 (not_115_out, OP3);
  not not_116 (not_116_out, OP2);
  not not_117 (not_117_out, OP1);
  not not_118 (not_118_out, OP0);
  not not_119 (not_119_out, F4);
  not not_120 (not_120_out, F3);
  not not_121 (not_121_out, F1);
  not not_122 (not_122_out, OP5);
  not not_123 (not_123_out, OP4);
  not not_124 (not_124_out, OP3);
  not not_125 (not_125_out, OP2);
  not not_126 (not_126_out, OP1);
  not not_127 (not_127_out, OP0);
  not not_128 (not_128_out, F4);
  not not_129 (not_129_out, F3);
  not not_130 (not_130_out, OP5);
  not not_131 (not_131_out, OP4);
  not not_132 (not_132_out, OP3);
  not not_133 (not_133_out, OP2);
  not not_134 (not_134_out, OP1);
  not not_135 (not_135_out, OP0);
  not not_136 (not_136_out, F4);
  not not_137 (not_137_out, F2);
  not not_138 (not_138_out, F0);
  not not_139 (not_139_out, OP5);
  not not_140 (not_140_out, OP4);
  not not_141 (not_141_out, OP3);
  not not_142 (not_142_out, OP2);
  not not_143 (not_143_out, OP1);
  not not_144 (not_144_out, OP0);
  not not_145 (not_145_out, F4);
  not not_146 (not_146_out, F2);
  not not_147 (not_147_out, OP5);
  not not_148 (not_148_out, OP4);
  not not_149 (not_149_out, OP3);
  not not_150 (not_150_out, OP2);
  not not_151 (not_151_out, OP5);
  not not_152 (not_152_out, OP4);
  not not_153 (not_153_out, OP2);
  not not_154 (not_154_out, OP1);
  not not_155 (not_155_out, OP0);
  not not_156 (not_156_out, OP5);
  not not_157 (not_157_out, OP4);
  not not_158 (not_158_out, OP1);
  not not_159 (not_159_out, OP0);
  not not_160 (not_160_out, OP5);
  not not_161 (not_161_out, OP4);
  not not_162 (not_162_out, OP2);
  not not_163 (not_163_out, OP1);
  not not_164 (not_164_out, OP5);
  not not_165 (not_165_out, OP4);
  not not_166 (not_166_out, OP2);
  not not_167 (not_167_out, OP0);
  not not_168 (not_168_out, OP5);
  not not_169 (not_169_out, OP4);
  not not_170 (not_170_out, OP1);
  not not_171 (not_171_out, OP4);
  not not_172 (not_172_out, OP3);
  not not_173 (not_173_out, OP2);
  not not_174 (not_174_out, OP5);
  not not_175 (not_175_out, OP4);
  not not_176 (not_176_out, OP3);
  not not_177 (not_177_out, OP2);
  not not_178 (not_178_out, OP1);
  not not_179 (not_179_out, OP0);
  not not_180 (not_180_out, F5);
  not not_181 (not_181_out, F4);
  not not_182 (not_182_out, F3);
  not not_183 (not_183_out, F0);
  not not_184 (not_184_out, OP5);
  not not_185 (not_185_out, OP4);
  not not_186 (not_186_out, OP3);
  not not_187 (not_187_out, OP2);
  not not_188 (not_188_out, OP1);
  not not_189 (not_189_out, OP0);
  not not_190 (not_190_out, F4);
  not not_191 (not_191_out, F3);
  not not_192 (not_192_out, F0);
  not not_193 (not_193_out, OP4);
  not not_194 (not_194_out, OP3);
  not not_195 (not_195_out, OP1);
  not not_196 (not_196_out, OP0);
  not not_197 (not_197_out, OP5);
  not not_198 (not_198_out, OP4);
  not not_199 (not_199_out, OP3);
  not not_200 (not_200_out, OP2);
  not not_201 (not_201_out, OP1);
  not not_202 (not_202_out, OP0);
  not not_203 (not_203_out, F5);
  not not_204 (not_204_out, F4);
  not not_205 (not_205_out, F1);
  not not_206 (not_206_out, F0);
  not not_207 (not_207_out, OP5);
  not not_208 (not_208_out, OP4);
  not not_209 (not_209_out, OP2);
  not not_210 (not_210_out, OP1);
  not not_211 (not_211_out, OP0);
  not not_212 (not_212_out, OP5);
  not not_213 (not_213_out, OP4);
  not not_214 (not_214_out, OP2);
  not not_215 (not_215_out, OP1);
  not not_216 (not_216_out, OP5);
  not not_217 (not_217_out, OP4);
  not not_218 (not_218_out, OP2);
  not not_219 (not_219_out, OP0);
  not not_220 (not_220_out, OP4);
  not not_221 (not_221_out, OP3);
  not not_222 (not_222_out, OP2);
  not not_223 (not_223_out, OP4);
  not not_224 (not_224_out, OP2);
  not not_225 (not_225_out, OP4);
  not not_226 (not_226_out, OP3);
  not not_227 (not_227_out, OP1);
  not not_228 (not_228_out, OP0);
  not not_229 (not_229_out, OP5);
  not not_230 (not_230_out, OP4);
  not not_231 (not_231_out, OP3);
  not not_232 (not_232_out, OP2);
  not not_233 (not_233_out, OP1);
  not not_234 (not_234_out, OP0);
  not not_235 (not_235_out, F5);
  not not_236 (not_236_out, F4);
  not not_237 (not_237_out, F3);
  not not_238 (not_238_out, F2);
  not not_239 (not_239_out, F1);
  not not_240 (not_240_out, F0);
  not not_241 (not_241_out, OP5);
  not not_242 (not_242_out, OP4);
  not not_243 (not_243_out, OP3);
  not not_244 (not_244_out, OP2);
  not not_245 (not_245_out, OP1);
  not not_246 (not_246_out, OP0);
  not not_247 (not_247_out, F5);
  not not_248 (not_248_out, F4);
  not not_249 (not_249_out, F3);
  not not_250 (not_250_out, F2);
  not not_251 (not_251_out, OP5);
  not not_252 (not_252_out, OP4);
  not not_253 (not_253_out, OP3);
  not not_254 (not_254_out, OP2);
  not not_255 (not_255_out, OP1);
  not not_256 (not_256_out, OP0);
  not not_257 (not_257_out, F5);
  not not_258 (not_258_out, F4);
  not not_259 (not_259_out, F3);
  not not_260 (not_260_out, F2);
  not not_261 (not_261_out, F0);
  not not_262 (not_262_out, OP5);
  not not_263 (not_263_out, OP4);
  not not_264 (not_264_out, OP3);
  not not_265 (not_265_out, OP2);
  not not_266 (not_266_out, OP1);
  not not_267 (not_267_out, OP0);
  not not_268 (not_268_out, F4);
  not not_269 (not_269_out, F3);
  not not_270 (not_270_out, F2);
  not not_271 (not_271_out, F1);
  not not_272 (not_272_out, F0);
  not not_273 (not_273_out, OP5);
  not not_274 (not_274_out, OP4);
  not not_275 (not_275_out, OP3);
  not not_276 (not_276_out, OP2);
  not not_277 (not_277_out, OP1);
  not not_278 (not_278_out, OP0);
  not not_279 (not_279_out, F4);
  not not_280 (not_280_out, F3);
  not not_281 (not_281_out, F2);
  not not_282 (not_282_out, F1);
  not not_283 (not_283_out, OP5);
  not not_284 (not_284_out, OP4);
  not not_285 (not_285_out, OP3);
  not not_286 (not_286_out, OP2);
  not not_287 (not_287_out, OP1);
  not not_288 (not_288_out, OP0);
  not not_289 (not_289_out, F4);
  not not_290 (not_290_out, F3);
  not not_291 (not_291_out, F2);
  not not_292 (not_292_out, F0);
  not not_293 (not_293_out, OP5);
  not not_294 (not_294_out, OP4);
  not not_295 (not_295_out, OP3);
  not not_296 (not_296_out, OP2);
  not not_297 (not_297_out, OP1);
  not not_298 (not_298_out, OP0);
  not not_299 (not_299_out, F4);
  not not_300 (not_300_out, F3);
  not not_301 (not_301_out, F1);
  not not_302 (not_302_out, F0);
  not not_303 (not_303_out, OP5);
  not not_304 (not_304_out, OP4);
  not not_305 (not_305_out, OP3);
  not not_306 (not_306_out, OP2);
  not not_307 (not_307_out, OP1);
  not not_308 (not_308_out, OP0);
  not not_309 (not_309_out, F4);
  not not_310 (not_310_out, F3);
  not not_311 (not_311_out, F1);
  not not_312 (not_312_out, OP5);
  not not_313 (not_313_out, OP4);
  not not_314 (not_314_out, OP3);
  not not_315 (not_315_out, OP2);
  not not_316 (not_316_out, OP1);
  not not_317 (not_317_out, OP0);
  not not_318 (not_318_out, F4);
  not not_319 (not_319_out, F3);
  not not_320 (not_320_out, OP5);
  not not_321 (not_321_out, OP4);
  not not_322 (not_322_out, OP3);
  not not_323 (not_323_out, OP2);
  not not_324 (not_324_out, OP1);
  not not_325 (not_325_out, OP0);
  not not_326 (not_326_out, F4);
  not not_327 (not_327_out, F2);
  not not_328 (not_328_out, F0);
  not not_329 (not_329_out, OP5);
  not not_330 (not_330_out, OP4);
  not not_331 (not_331_out, OP3);
  not not_332 (not_332_out, OP2);
  not not_333 (not_333_out, OP1);
  not not_334 (not_334_out, OP0);
  not not_335 (not_335_out, F4);
  not not_336 (not_336_out, F2);
  not not_337 (not_337_out, OP5);
  not not_338 (not_338_out, OP4);
  not not_339 (not_339_out, OP3);
  not not_340 (not_340_out, OP2);
  not not_341 (not_341_out, OP1);
  not not_342 (not_342_out, OP0);
  not not_343 (not_343_out, F5);
  not not_344 (not_344_out, F4);
  not not_345 (not_345_out, F2);
  not not_346 (not_346_out, F1);
  not not_347 (not_347_out, F0);
  not not_348 (not_348_out, OP5);
  not not_349 (not_349_out, OP4);
  not not_350 (not_350_out, OP3);
  not not_351 (not_351_out, OP2);
  not not_352 (not_352_out, OP1);
  not not_353 (not_353_out, OP0);
  not not_354 (not_354_out, F5);
  not not_355 (not_355_out, F4);
  not not_356 (not_356_out, F3);
  not not_357 (not_357_out, F0);
  not not_358 (not_358_out, OP5);
  not not_359 (not_359_out, OP4);
  not not_360 (not_360_out, OP3);
  not not_361 (not_361_out, OP2);
  not not_362 (not_362_out, OP1);
  not not_363 (not_363_out, OP0);
  not not_364 (not_364_out, F4);
  not not_365 (not_365_out, F3);
  not not_366 (not_366_out, F0);
  not not_367 (not_367_out, OP5);
  not not_368 (not_368_out, OP4);
  not not_369 (not_369_out, OP3);
  not not_370 (not_370_out, OP1);
  not not_371 (not_371_out, OP0);
  not not_372 (not_372_out, OP5);
  not not_373 (not_373_out, OP4);
  not not_374 (not_374_out, OP3);
  not not_375 (not_375_out, OP1);
  not not_376 (not_376_out, OP5);
  not not_377 (not_377_out, OP4);
  not not_378 (not_378_out, OP3);
  not not_379 (not_379_out, OP2);
  not not_380 (not_380_out, OP1);
  not not_381 (not_381_out, OP0);
  not not_382 (not_382_out, F5);
  not not_383 (not_383_out, F4);
  not not_384 (not_384_out, F2);
  not not_385 (not_385_out, F1);
  not not_386 (not_386_out, F0);
  not not_387 (not_387_out, OP5);
  not not_388 (not_388_out, OP4);
  not not_389 (not_389_out, OP3);
  not not_390 (not_390_out, OP2);
  not not_391 (not_391_out, OP1);
  not not_392 (not_392_out, OP0);
  not not_393 (not_393_out, F5);
  not not_394 (not_394_out, F4);
  not not_395 (not_395_out, F2);
  not not_396 (not_396_out, F1);
  not not_397 (not_397_out, F0);
  not not_398 (not_398_out, OP5);
  not not_399 (not_399_out, OP4);
  not not_400 (not_400_out, OP3);
  not not_401 (not_401_out, OP2);
  not not_402 (not_402_out, OP0);
  not not_403 (not_403_out, OP5);
  not not_404 (not_404_out, OP4);
  not not_405 (not_405_out, OP3);
  not not_406 (not_406_out, OP2);
  not not_407 (not_407_out, OP5);
  not not_408 (not_408_out, OP4);
  not not_409 (not_409_out, OP3);
  not not_410 (not_410_out, OP2);
  not not_411 (not_411_out, OP5);
  not not_412 (not_412_out, OP4);
  not not_413 (not_413_out, OP3);
  not not_414 (not_414_out, OP2);
  not not_415 (not_415_out, OP1);
  not not_416 (not_416_out, OP0);
  not not_417 (not_417_out, F5);
  not not_418 (not_418_out, F4);
  not not_419 (not_419_out, F3);
  not not_420 (not_420_out, F0);
  not not_421 (not_421_out, OP4);
  not not_422 (not_422_out, OP3);
  not not_423 (not_423_out, OP1);
  not not_424 (not_424_out, OP0);
  not not_425 (not_425_out, OP5);
  not not_426 (not_426_out, OP4);
  not not_427 (not_427_out, OP3);
  and and_1 (and_1_out, OP5, not_1_out, not_2_out, not_3_out, OP1, OP0);
  and and_2 (and_2_out, OP5, not_4_out, not_5_out, OP2, not_6_out, not_7_out);
  and and_3 (MemWrite, OP5, not_8_out, OP3, not_9_out, OP1, OP0);
  and and_4 (and_4_out, not_10_out, not_11_out, OP3, not_12_out, not_13_out, not_14_out);
  and and_5 (and_5_out, not_15_out, not_16_out, OP3, OP2, not_17_out, not_18_out);
  and and_6 (and_6_out, not_19_out, not_20_out, OP3, not_21_out, not_22_out, OP0);
  and and_7 (and_7_out, not_23_out, not_24_out, OP3, not_25_out, OP1, not_26_out);
  and and_8 (and_8_out, not_27_out, not_28_out, OP3, OP2, not_29_out, OP0);
  and and_9 (and_9_out, OP5, not_30_out, not_31_out, not_32_out, OP1, OP0);
  and and_10 (and_10_out, OP5, not_33_out, OP3, not_34_out, OP1, OP0);
  and and_11 (and_11_out, OP5, not_35_out, not_36_out, OP2, not_37_out, not_38_out);
  and and_12 (and_12_out, not_39_out, not_40_out, not_41_out, not_42_out, not_43_out, not_44_out, not_45_out, not_46_out, not_47_out, not_48_out, not_49_out, not_50_out);
  and and_13 (and_13_out, not_51_out, not_52_out, not_53_out, not_54_out, not_55_out, not_56_out, not_57_out, not_58_out, not_59_out, not_60_out, F1, F0);
  and and_14 (and_14_out, not_61_out, not_62_out, not_63_out, not_64_out, not_65_out, not_66_out, not_67_out, not_68_out, not_69_out, not_70_out, F1, not_71_out);
  and and_15 (and_15_out, not_72_out, not_73_out, not_74_out, not_75_out, not_76_out, not_77_out, F5, not_78_out, not_79_out, not_80_out, not_81_out, not_82_out);
  and and_16 (and_16_out, not_83_out, not_84_out, not_85_out, not_86_out, not_87_out, not_88_out, F5, not_89_out, not_90_out, not_91_out, not_92_out, F0);
  and and_17 (and_17_out, not_93_out, not_94_out, not_95_out, not_96_out, not_97_out, not_98_out, F5, not_99_out, not_100_out, not_101_out, F1, not_102_out);
  and and_18 (and_18_out, not_103_out, not_104_out, not_105_out, not_106_out, not_107_out, not_108_out, F5, not_109_out, not_110_out, F2, not_111_out, not_112_out);
  and and_19 (and_19_out, not_113_out, not_114_out, not_115_out, not_116_out, not_117_out, not_118_out, F5, not_119_out, not_120_out, F2, not_121_out, F0);
  and and_20 (and_20_out, not_122_out, not_123_out, not_124_out, not_125_out, not_126_out, not_127_out, F5, not_128_out, not_129_out, F2, F1, F0);
  and and_21 (and_21_out, not_130_out, not_131_out, not_132_out, not_133_out, not_134_out, not_135_out, F5, not_136_out, F3, not_137_out, F1, not_138_out);
  and and_22 (and_22_out, not_139_out, not_140_out, not_141_out, not_142_out, not_143_out, not_144_out, F5, not_145_out, F3, not_146_out, F1, F0);
  and and_23 (and_23_out, not_147_out, not_148_out, not_149_out, not_150_out, OP1, OP0);
  and and_24 (and_24_out, not_151_out, not_152_out, OP3, not_153_out, not_154_out, not_155_out);
  and and_25 (and_25_out, not_156_out, not_157_out, OP3, OP2, not_158_out, not_159_out);
  and and_26 (and_26_out, not_160_out, not_161_out, OP3, not_162_out, not_163_out, OP0);
  and and_27 (and_27_out, not_164_out, not_165_out, OP3, not_166_out, OP1, not_167_out);
  and and_28 (and_28_out, not_168_out, not_169_out, OP3, OP2, not_170_out, OP0);
  and and_29 (and_29_out, OP5, not_171_out, not_172_out, not_173_out, OP1, OP0);
  and and_30 (and_30_out, not_174_out, not_175_out, not_176_out, not_177_out, not_178_out, not_179_out, not_180_out, not_181_out, not_182_out, F2, F1, not_183_out);
  and and_31 (and_31_out, not_184_out, not_185_out, not_186_out, not_187_out, not_188_out, not_189_out, F5, not_190_out, not_191_out, F2, F1, not_192_out);
  and and_32 (and_32_out, OP5, not_193_out, not_194_out, OP2, not_195_out, not_196_out);
  and and_33 (SysCALL, not_197_out, not_198_out, not_199_out, not_200_out, not_201_out, not_202_out, not_203_out, not_204_out, F3, F2, not_205_out, not_206_out);
  and and_34 (and_34_out, not_207_out, not_208_out, OP3, not_209_out, not_210_out, not_211_out);
  and and_35 (and_35_out, not_212_out, not_213_out, OP3, not_214_out, not_215_out, OP0);
  and and_36 (and_36_out, not_216_out, not_217_out, OP3, not_218_out, OP1, not_219_out);
  and and_37 (and_37_out, OP5, not_220_out, not_221_out, not_222_out, OP1, OP0);
  and and_38 (and_38_out, OP5, not_223_out, OP3, not_224_out, OP1, OP0);
  and and_39 (and_39_out, OP5, not_225_out, not_226_out, OP2, not_227_out, not_228_out);
  and and_40 (and_40_out, not_229_out, not_230_out, not_231_out, not_232_out, not_233_out, not_234_out, not_235_out, not_236_out, not_237_out, not_238_out, not_239_out, not_240_out);
  and and_41 (and_41_out, not_241_out, not_242_out, not_243_out, not_244_out, not_245_out, not_246_out, not_247_out, not_248_out, not_249_out, not_250_out, F1, F0);
  and and_42 (and_42_out, not_251_out, not_252_out, not_253_out, not_254_out, not_255_out, not_256_out, not_257_out, not_258_out, not_259_out, not_260_out, F1, not_261_out);
  and and_43 (and_43_out, not_262_out, not_263_out, not_264_out, not_265_out, not_266_out, not_267_out, F5, not_268_out, not_269_out, not_270_out, not_271_out, not_272_out);
  and and_44 (and_44_out, not_273_out, not_274_out, not_275_out, not_276_out, not_277_out, not_278_out, F5, not_279_out, not_280_out, not_281_out, not_282_out, F0);
  and and_45 (and_45_out, not_283_out, not_284_out, not_285_out, not_286_out, not_287_out, not_288_out, F5, not_289_out, not_290_out, not_291_out, F1, not_292_out);
  and and_46 (and_46_out, not_293_out, not_294_out, not_295_out, not_296_out, not_297_out, not_298_out, F5, not_299_out, not_300_out, F2, not_301_out, not_302_out);
  and and_47 (and_47_out, not_303_out, not_304_out, not_305_out, not_306_out, not_307_out, not_308_out, F5, not_309_out, not_310_out, F2, not_311_out, F0);
  and and_48 (and_48_out, not_312_out, not_313_out, not_314_out, not_315_out, not_316_out, not_317_out, F5, not_318_out, not_319_out, F2, F1, F0);
  and and_49 (and_49_out, not_320_out, not_321_out, not_322_out, not_323_out, not_324_out, not_325_out, F5, not_326_out, F3, not_327_out, F1, not_328_out);
  and and_50 (and_50_out, not_329_out, not_330_out, not_331_out, not_332_out, not_333_out, not_334_out, F5, not_335_out, F3, not_336_out, F1, F0);
  and and_51 (and_51_out, not_337_out, not_338_out, not_339_out, not_340_out, not_341_out, not_342_out, not_343_out, not_344_out, F3, not_345_out, not_346_out, not_347_out);
  and and_52 (and_52_out, not_348_out, not_349_out, not_350_out, not_351_out, not_352_out, not_353_out, not_354_out, not_355_out, not_356_out, F2, F1, not_357_out);
  and and_53 (and_53_out, not_358_out, not_359_out, not_360_out, not_361_out, not_362_out, not_363_out, F5, not_364_out, not_365_out, F2, F1, not_366_out);
  and and_54 (BEQ, not_367_out, not_368_out, not_369_out, OP2, not_370_out, not_371_out);
  and and_55 (BNE, not_372_out, not_373_out, not_374_out, OP2, not_375_out, OP0);
  and and_56 (JR, not_376_out, not_377_out, not_378_out, not_379_out, not_380_out, not_381_out, not_382_out, not_383_out, F3, not_384_out, not_385_out, not_386_out);
  and and_57 (and_57_out, not_387_out, not_388_out, not_389_out, not_390_out, not_391_out, not_392_out, not_393_out, not_394_out, F3, not_395_out, not_396_out, not_397_out);
  and and_58 (and_58_out, not_398_out, not_399_out, not_400_out, not_401_out, OP1, not_402_out);
  and and_59 (and_59_out, not_403_out, not_404_out, not_405_out, not_406_out, OP1, OP0);
  and and_60 (JAL, not_407_out, not_408_out, not_409_out, not_410_out, OP1, OP0);
  and and_61 (SRLV, not_411_out, not_412_out, not_413_out, not_414_out, not_415_out, not_416_out, not_417_out, not_418_out, not_419_out, F2, F1, not_420_out);
  and and_62 (LBU, OP5, not_421_out, not_422_out, OP2, not_423_out, not_424_out);
  and and_63 (BGTZ, not_425_out, not_426_out, not_427_out, OP2, OP1, OP0);
  or or_1 (MemToReg, and_1_out, and_2_out);
  or or_2 (ALU_SRC, and_4_out, and_5_out, and_6_out, and_7_out, and_8_out, and_9_out, and_10_out, and_11_out);
  or or_3 (SignedExt, and_34_out, and_35_out, and_36_out, and_37_out, and_38_out, and_39_out);
  or or_4 (JUMP, and_57_out, and_58_out, and_59_out);
  or or_5 (RegWrite, and_12_out, and_13_out, and_14_out, and_15_out, and_16_out, and_17_out, and_18_out, and_19_out, and_20_out, and_21_out, and_22_out, and_23_out, and_24_out, and_25_out, and_26_out, and_27_out, and_28_out, and_29_out, and_30_out, and_31_out, and_32_out);
  or or_6 (RegDst, and_40_out, and_41_out, and_42_out, and_43_out, and_44_out, and_45_out, and_46_out, and_47_out, and_48_out, and_49_out, and_50_out, and_51_out, and_52_out, and_53_out);
endmodule

// ALU
module MIPS_ALU (
  input  [4:0] shamt,
  input  [31:0] X,
  input  [31:0] Y,
  input  [3:0] AluOP,
  output Equal,
  output [31:0] Result,
  output [31:0] Result_2
);

  wire [0:0] comparator_1_lt, comparator_2_lt;
  wire [31:0] adder_1_out, AND_out, divider_1_out, divider_1_rem, multiplier_1_cout, multiplier_1_out,
       NOR_out, OR_out, shifter_1_out, shifter_2_out, shifter_3_out, subtractor_1_out, XOR_out;

  assign AND_out = X & Y;  // AND_Gate AND, 32 bits wide
  assign OR_out = X | Y;  // OR_Gate OR, 32 bits wide
  Shifter #(.width(32), .shift("ll")) shifter_1 (.in(Y), .\dist (shamt), .out(shifter_1_out));
  Shifter #(.width(32), .shift("ar")) shifter_2 (.in(Y), .\dist (shamt), .out(shifter_2_out));
  Shifter #(.width(32), .shift("lr")) shifter_3 (.in(Y), .\dist (shamt), .out(shifter_3_out));
  Multiplier #(.width(32)) multiplier_1 (.a(X), .b(Y), .out(multiplier_1_out), .cout(multiplier_1_cout));  // open: cin
  Divider #(.width(32)) divider_1 (.a(X), .b(Y), .out(divider_1_out), .rem(divider_1_rem));  // open: upper
  Adder #(.width(32)) adder_1 (.a(X), .b(Y), .out(adder_1_out));  // open: cin, cout
  Subtractor #(.width(32)) subtractor_1 (.a(X), .b(Y), .out(subtractor_1_out));  // open: bin, bout
  assign XOR_out = X ^ Y;  // XOR_Gate XOR, 32 bits wide
  assign NOR_out = ~(X | Y);  // NOR_Gate NOR, 32 bits wide
  Comparator #(.width(32), .mode("twosComplement")) comparator_1 (
    .a(X), .b(Y), .eq(Equal), .lt(comparator_1_lt[0]));  // open: gt
  Comparator #(.width(32), .mode("unsigned")) comparator_2 (.a(X), .b(Y), .lt(comparator_2_lt[0]));  // open: gt, eq
  Multiplexer #(.select(4), .width(32), .disabled("Z"), .enable("false")) multiplexer_1 (
    .in0(shifter_1_out), .in1(shifter_2_out), .in2(shifter_3_out), .in3(multiplier_1_out),
    .in4(divider_1_out), .in5(adder_1_out), .in6(subtractor_1_out), .in7(AND_out), .in8(OR_out),
    .in9(XOR_out), .in10(NOR_out), .in11({{31{1'b0}}, comparator_1_lt[0]}),
    .in12({{31{1'b0}}, comparator_2_lt[0]}), .in13({32{1'b0}}), .in14({32{1'b0}}), .in15({32{1'b0}}),
    .out(Result), .sel(AluOP));
  Multiplexer #(.select(4), .width(32), .disabled("Z"), .enable("false")) multiplexer_2 (
    .in0({32{1'b0}}), .in1({32{1'b0}}), .in2({32{1'b0}}), .in3(multiplier_1_cout), .in4(divider_1_rem),
    .in5({32{1'b0}}), .in6({32{1'b0}}), .in7({32{1'b0}}), .in8({32{1'b0}}), .in9({32{1'b0}}),
    .in10({32{1'b0}}), .in11({32{1'b0}}), .in12({32{1'b0}}), .in13({32{1'b0}}), .in14({32{1'b0}}),
    .in15({32{1'b0}}), .out(Result_2), .sel(AluOP));

  // Other names for the same wires on the sheet: Result2[31:0] = Result_2; S[3:0] = AluOP

  // Notes on the sheet:
  //   不要改变此引脚区域内容，也不要改变ALU封装形式
  //   输入引脚
  //   输出引脚
endmodule

module MIPS_Regifile (
  input  [31:0] Din,
  input  Clk,
  input  WE,
  input  [4:0] R1_num,
  input  [4:0] W_num,
  input  [4:0] R2_num,
  output [31:0] R1,
  output [31:0] R2
);

  // RegisterFile registerfile_1: pin names not known; wires that end beside it: Din, Clk, WE, W_num, R1_num, R2_num, R1, R2
endmodule

module \理想流水线  (
  output RegWrite,
  output MemWrite,
  output [31:0] IF_PC,
  output [31:0] ID_PC,
  output [31:0] EX_PC,
  output [31:0] M_PC,
  output [31:0] WB_PC,
  output [31:0] RDin,
  output [31:0] MDin,
  output [31:0] LedData
);

  wire CLK, equal, \ex_执行_1_memtoreg_prime , \ex_执行_1_regdst_prime , \ex_执行_1_regwrite_prime , Go,
       \id_译码_1_alusrcb_prime , \id_译码_1_memtoreg_prime , \id_译码_1_memwrite_prime , \id_译码_1_regdst_prime ,
       \id_译码_1_regwrite_prime , IR1, IR2, IR3, \mem_访存_1_memtoreg_prime , \mem_访存_1_memtoreg_prime_2 ,
       not_1_out, RST, stop, W1, W2, W3, \单周期硬布线控制器_1_alu_src , \单周期硬布线控制器_1_memtoreg ,
       \单周期硬布线控制器_1_memwrite , \单周期硬布线控制器_1_regdst , \单周期硬布线控制器_1_regwrite ;
  wire [3:0] \id_译码_1_aluop_prime , \单周期硬布线控制器_1_alu_op ;
  wire [4:0] multiplexer_2_out;
  wire [15:0] \LoadUse次数 , \总周期数 , \插入气泡数 , \无条件分支数 , \条件分支成功数 ;
  wire [31:0] a0, adder_1_out, bit_extender_1_out, \ex_执行_1_alu_prime , \ex_执行_1_ir_prime ,
       \id_译码_1_a_prime , \id_译码_1_b_prime , \id_译码_1_imm_prime , \id_译码_1_ir_prime , \if_取指令_1_ir_prime ,
       IR_final, \mem_访存_1_alu_prime , \mem_访存_1_md_prime , mips_alu_1_result, mips_regifile_1_r1,
       mips_regifile_1_r2, multiplexer_1_out, multiplexer_3_out, ram_1_data, rom_1_data;

  Button \u_总复位  (.out(RST));
  Button _1 (.out(IR1));
  Button _2 (.out(IR2));
  Button _3 (.out(IR3));
  Button \u_继续运行  (.out(Go));
  LED #(.active("true")) led_1 (.in(W1));
  LED #(.active("true")) led_2 (.in(W2));
  LED #(.active("true")) led_3 (.in(W3));
  Hex_Digit_Display hex_digit_display_1 (.value(LedData[31:28]));  // open: dp
  Hex_Digit_Display hex_digit_display_2 (.value(LedData[23:20]));  // open: dp
  Hex_Digit_Display hex_digit_display_3 (.value(LedData[27:24]));  // open: dp
  Hex_Digit_Display hex_digit_display_4 (.value(LedData[19:16]));  // open: dp
  Hex_Digit_Display hex_digit_display_5 (.value(LedData[15:12]));  // open: dp
  Hex_Digit_Display hex_digit_display_6 (.value(LedData[11:8]));  // open: dp
  Hex_Digit_Display hex_digit_display_7 (.value(LedData[7:4]));  // open: dp
  Clock #(.highDuration(1), .lowDuration(1)) clock_1 (.out(CLK));
  not not_1 (not_1_out, stop);
  Register #(.width(32), .trigger("rising"), .Select("low")) PC (
    .D(adder_1_out), .en(not_1_out), .Q(IF_PC), .clk(CLK));  // open: clr
  Hex_Digit_Display hex_digit_display_8 (.value(LedData[3:0]));  // open: dp
  Counter #(.width(16), .max('hffff), .ongoal("wrap"), .trigger("rising"), .behavior("old")) counter_1 (
    .D({16{1'b0}}), .count(not_1_out), .Q(\总周期数 ), .clk(CLK));  // open: load, carry, clr, preset
  // Probe on \总周期数 
  // Probe on \无条件分支数 
  // Probe on \条件分支成功数 
  // Probe on \插入气泡数 
  // Probe on \LoadUse次数 
  Adder #(.width(32)) adder_1 (.a(IF_PC), .b(32'h4), .out(adder_1_out));  // open: cin, cout
  ROM #(.addrWidth(10), .dataWidth(32), .Select("high")) rom_1 (.addr(IF_PC[11:2]), .data(rom_1_data));
  // Probe on IF_PC[11:0]
  // Probe on ID_PC[11:0]
  // Probe on EX_PC[11:0]
  \IF_取指令  \if_取指令_1  (
    .IR(rom_1_data), .PC(IF_PC), .CLK(CLK), .PC_prime(ID_PC), .\同步清零_高电平有效 (RST), .\使能端_低电平有效 (stop),
    .IR_prime(\if_取指令_1_ir_prime ));
  // Probe on M_PC[11:0]
  Multiplexer #(.select(1), .width(32), .disabled("Z"), .enable("false")) multiplexer_1 (
    .in1(a0), .out(multiplexer_1_out), .sel(equal));  // open: in0
  // Probe on a0
  // Probe on WB_PC[11:0]
  \单周期硬布线控制器  \u_单周期硬布线控制器_1  (
    .Func(\if_取指令_1_ir_prime [5:0]), .OP(\if_取指令_1_ir_prime [31:26]), .ALU_OP(\单周期硬布线控制器_1_alu_op ),
    .MemToReg(\单周期硬布线控制器_1_memtoreg ), .MemWrite(\单周期硬布线控制器_1_memwrite ), .ALU_SRC(\单周期硬布线控制器_1_alu_src ),
    .RegWrite(\单周期硬布线控制器_1_regwrite ), .RegDst(\单周期硬布线控制器_1_regdst ));  // open: SysCALL, SignedExt, JR, JMP, Beq, JAL, Bne, SRLV, LBU, BGTZ
  Multiplexer #(.select(1), .width(5), .disabled("Z"), .enable("false")) multiplexer_2 (
    .in0(IR_final[20:16]), .in1(IR_final[15:11]), .out(multiplexer_2_out), .sel(\mem_访存_1_memtoreg_prime ));
  Register #(.width(32), .trigger("rising"), .Select("low")) register_1 (
    .D(multiplexer_1_out), .Q(LedData), .clk(CLK));  // open: en, clr
  assign bit_extender_1_out = {{16{\if_取指令_1_ir_prime [15]}}, \if_取指令_1_ir_prime [15:0]};  // Bit_Extender bit_extender_1
  MIPS_Regifile mips_regifile_1 (
    .Din(RDin), .Clk(CLK), .R1(mips_regifile_1_r1), .R2(mips_regifile_1_r2), .WE(RegWrite),
    .W_num(multiplexer_2_out), .R1_num(\if_取指令_1_ir_prime [25:21]), .R2_num(\if_取指令_1_ir_prime [20:16]));
  \ID_译码  \id_译码_1  (
    .MemToReg(\单周期硬布线控制器_1_memtoreg ), .RegWirte(\单周期硬布线控制器_1_regwrite ), .MemWrite(\单周期硬布线控制器_1_memwrite ),
    .ALUSRCB(\单周期硬布线控制器_1_alu_src ), .ALUOP(\单周期硬布线控制器_1_alu_op ), .IR(\if_取指令_1_ir_prime ), .PC(ID_PC),
    .CLK(CLK), .MemToReg_prime(\id_译码_1_memtoreg_prime ), .RegWrite_prime(\id_译码_1_regwrite_prime ),
    .MemWrite_prime(\id_译码_1_memwrite_prime ), .ALUSRCB_prime(\id_译码_1_alusrcb_prime ),
    .ALUOP_prime(\id_译码_1_aluop_prime ), .IR_prime(\id_译码_1_ir_prime ), .PC_prime(EX_PC), .\同步清零_高电平有效 (RST),
    .\使能端_低电平有效 (stop), .A_prime(\id_译码_1_a_prime ), .A(mips_regifile_1_r1), .B(mips_regifile_1_r2),
    .B_prime(\id_译码_1_b_prime ), .Imm(bit_extender_1_out), .Imm_prime(\id_译码_1_imm_prime ),
    .RegDst(\单周期硬布线控制器_1_regdst ), .RegDst_prime(\id_译码_1_regdst_prime ));
  Multiplexer #(.select(1), .width(32), .disabled("Z"), .enable("false")) multiplexer_3 (
    .in0(\id_译码_1_b_prime ), .in1(\id_译码_1_imm_prime ), .out(multiplexer_3_out), .sel(\id_译码_1_alusrcb_prime ));
  MIPS_ALU mips_alu_1 (
    .X(\id_译码_1_a_prime ), .Y(multiplexer_3_out), .AluOP(\id_译码_1_aluop_prime ), .Result(mips_alu_1_result),
    .shamt({5{1'b0}}));  // open: Equal, Result_2
  \EX_执行  \ex_执行_1  (
    .MemToReg(\id_译码_1_memtoreg_prime ), .MemToReg_prime(\ex_执行_1_memtoreg_prime ),
    .RegWirte(\id_译码_1_regwrite_prime ), .RegWrite_prime(\ex_执行_1_regwrite_prime ),
    .MemWrite(\id_译码_1_memwrite_prime ), .MemWrite_prime(MemWrite), .IR(\id_译码_1_ir_prime ),
    .IR_prime(\ex_执行_1_ir_prime ), .PC(EX_PC), .PC_prime(M_PC), .B(\id_译码_1_b_prime ), .B_prime(MDin),
    .ALU(mips_alu_1_result), .ALU_prime(\ex_执行_1_alu_prime ), .CLK(CLK), .\同步清零_高电平有效 (RST),
    .\使能端_低电平有效 (stop), .RegDst(\id_译码_1_regdst_prime ), .RegDst_prime(\ex_执行_1_regdst_prime ));
  RAM #(.addrWidth(10), .dataWidth(32), .bus("separate"), .Select("high")) ram_1 (
    .addr(\ex_执行_1_alu_prime [11:2]), .din(MDin), .data(ram_1_data), .str(MemWrite), .sel(1'b1), .clk(CLK));  // open: ld, clr
  \MEM_访存  \mem_访存_1  (
    .MemToReg(\ex_执行_1_memtoreg_prime ), .MemToReg_prime_2(\mem_访存_1_memtoreg_prime_2 ),
    .RegWirte(\ex_执行_1_regwrite_prime ), .RegWrite_prime(RegWrite), .IR(\ex_执行_1_ir_prime ),
    .IR_prime(IR_final), .PC(M_PC), .PC_prime(WB_PC), .ALU(\ex_执行_1_alu_prime ),
    .ALU_prime(\mem_访存_1_alu_prime ), .MD(ram_1_data), .MD_prime(\mem_访存_1_md_prime ), .CLK(CLK),
    .\同步清零_高电平有效 (RST), .\使能端_低电平有效 (stop), .RegDst(\ex_执行_1_regdst_prime ),
    .MemToReg_prime(\mem_访存_1_memtoreg_prime ));
  Multiplexer #(.select(1), .width(32), .disabled("Z"), .enable("false")) multiplexer_4 (
    .in0(\mem_访存_1_alu_prime ), .in1(\mem_访存_1_md_prime ), .out(RDin), .sel(\mem_访存_1_memtoreg_prime_2 ));
  Comparator #(.width(32), .mode("twosComplement")) comparator_1 (.a(IR_final), .b(32'hc), .eq(stop));  // open: gt, lt

  // Other names for the same wires on the sheet: MEM_PC[31:0] = M_PC

  // Notes on the sheet:
  //   中断源
  //   中断等待指示
  //   数码管输出
  //   contents of rom_1 (hex, n*v repeats v):
  //   20100000 20110000 20120000 20130000 36100000 36310001 36520002 36730003 ae100000 ae110004 ae120008
  //   ae13000c 2002000a 20110000 20120000 20130000 c
  //   流水调试日志用
  //   OP
  //   rs
  //   rt
  //   rd
  //   为方便自动评测，需要输出流水线各段保存的PC值，注意是PC不是PC+4，另外ID段寄存器写入信息，Mem段内存写入信息也要输出
endmodule

module \气泡流水线  (
  output RegWrite,
  output MemWrite,
  output [31:0] IF_PC,
  output [31:0] ID_PC,
  output [31:0] EX_PC,
  output [31:0] M_PC,
  output [31:0] WB_PC,
  output [31:0] RDin,
  output [31:0] MDin,
  output [31:0] LedData
);

  wire ALUSRC, and_1_out, and_2_out, and_5_out, and_6_out, and_7_out, BEQ, beq_t, BGTZ, bgtz_t, BNE, bne_t,
       Branch, CLK, comparator_1_eq, equal, ex_mem_1_jal_prime, ex_mem_1_lbu_prime, ex_mem_1_memtoreg_prime,
       ex_mem_1_regdst_prime, ex_mem_1_regwrite_prime, Go, id_ex_1_alusrcb_prime, id_ex_1_jal_prime,
       id_ex_1_lbu_prime, id_ex_1_memtoreg_prime, id_ex_1_memwrite_prime, id_ex_1_regdst_prime,
       id_ex_1_regwrite_prime, id_ex_1_srlv_prime, IR1, IR2, IR3, JAL, JMP, jmp_t, JR, jr_t, LBU,
       mem_wb_1_jal_prime, mem_wb_1_lbu_prime, mem_wb_1_memtoreg_prime, mem_wb_1_regdst_prime, MemtoReg,
       Memwrite_t, mips_alu_1_equal, not_1_out, not_2_out, not_3_out, not_4_out, not_5_out, not_6_out,
       or_1_out, or_2_out, or_3_out, or_4_out, OUTPUT, RegDst, Regwrite_t, RST, Sign, SRLV, stop, syscall,
       W1, W2, W3, \单周期硬布线控制器_1_syscall , \源寄存器使用情况_1_r1_used , \源寄存器使用情况_1_r2_used ;
  wire [3:0] ALUOP, id_ex_1_aluop_prime;
  wire [4:0] EXWriteReg, id_ex_1_shamt_prime, MEMWriteReg, multiplexer_5_out, multiplexer_12_out,
       multiplexer_13_out, multiplexer_16_out, R1_num, R2_num, WRITEREG;
  wire [15:0] imm16, \LoadUse次数 , \总周期数 , \插入气泡数 , \无条件 , \无条件分支数 , \有条件 , \条件分支成功数 ;
  wire [27:0] pc_4;
  wire [31:0] a0, adder_3_out, adder_4_out, and_8_out, bit_extender_1_out, ex_mem_1_a_prime,
       ex_mem_1_alu_prime, ex_mem_1_ir_prime, id_ex_1_b_prime, id_ex_1_imm16_prime, id_ex_1_imm26_prime,
       id_ex_1_ir_prime, id_ex_1_sign16_prime, IMM, imm26, IR, IR_final, JPC, JRPC, mem_wb_1_alu_prime,
       mem_wb_1_md_prime, mips_alu_1_result, mips_regifile_1_r1, mips_regifile_1_r2, multiplexer_1_out,
       multiplexer_2_out, multiplexer_3_out, multiplexer_9_out, multiplexer_10_out, multiplexer_11_out,
       multiplexer_14_out, multiplexer_17_out, PC, ram_1_data, shifter_1_out, shifter_3_out, shifter_4_out,
       Sign16, v0;
  wire [31:16] IR_NOW;
  wire [31:28] shifter_2_out;

  Button \u_总复位  (.out(RST));
  Button _1 (.out(IR1));
  Button _2 (.out(IR2));
  Button _3 (.out(IR3));
  Button \u_继续运行  (.out(Go));
  LED #(.active("true")) led_1 (.in(W1));
  LED #(.active("true")) led_2 (.in(W2));
  LED #(.active("true")) led_3 (.in(W3));
  Hex_Digit_Display hex_digit_display_1 (.value(LedData[31:28]));  // open: dp
  Hex_Digit_Display hex_digit_display_2 (.value(LedData[23:20]));  // open: dp
  Hex_Digit_Display hex_digit_display_3 (.value(LedData[27:24]));  // open: dp
  Multiplexer #(.select(1), .width(32), .disabled("Z"), .enable("false")) multiplexer_1 (
    .in0(PC), .in1(adder_3_out), .out(multiplexer_1_out), .sel(Branch));
  Hex_Digit_Display hex_digit_display_4 (.value(LedData[15:12]));  // open: dp
  Hex_Digit_Display hex_digit_display_5 (.value(LedData[19:16]));  // open: dp
  not not_1 (not_1_out, stop);
  and and_1 (and_1_out, not_1_out, OUTPUT);
  not not_2 (not_2_out, OUTPUT);
  or or_1 (or_1_out, Go, and_2_out);
  Multiplexer #(.select(1), .width(32), .disabled("Z"), .enable("false")) multiplexer_2 (
    .in0(multiplexer_1_out), .in1(JPC), .out(multiplexer_2_out), .sel(JMP));
  Multiplexer #(.select(1), .width(32), .disabled("Z"), .enable("false")) multiplexer_3 (
    .in0(multiplexer_2_out), .in1(JRPC), .out(multiplexer_3_out), .sel(JR));
  Hex_Digit_Display hex_digit_display_6 (.value(LedData[11:8]));  // open: dp
  Hex_Digit_Display hex_digit_display_7 (.value(LedData[7:4]));  // open: dp
  Clock #(.highDuration(1), .lowDuration(1)) clock_1 (.out(CLK));
  not not_3 (not_3_out, stop);
  and and_2 (and_2_out, not_2_out, not_3_out);
  Register #(.width(32), .trigger("rising"), .Select("low")) u_PC (
    .D(multiplexer_3_out), .en(or_1_out), .Q(IF_PC), .clk(CLK));  // open: clr
  Hex_Digit_Display hex_digit_display_8 (.value(LedData[3:0]));  // open: dp
  Counter #(.width(16), .max('hffff), .ongoal("wrap"), .trigger("rising"), .behavior("old")) counter_1 (
    .D({16{1'b0}}), .count(and_1_out), .Q(\插入气泡数 ), .clk(CLK));  // open: load, carry, clr, preset
  Counter #(.width(16), .max('hffff), .ongoal("wrap"), .trigger("rising"), .behavior("old")) counter_2 (
    .D({16{1'b0}}), .count(not_3_out), .Q(\总周期数 ), .clk(CLK));  // open: load, carry, clr, preset
  // Probe on \插入气泡数 
  // Probe on \总周期数 
  // Probe on \无条件分支数 
  // Probe on \条件分支成功数 
  // Probe on \插入气泡数 
  // Probe on \LoadUse次数 
  Adder #(.width(32)) adder_1 (.a(IF_PC), .b(32'h4), .out(PC));  // open: cin, cout
  // Probe on IF_PC[11:0]
  ROM #(.addrWidth(10), .dataWidth(32), .Select("high")) rom_1 (.addr(IF_PC[11:2]), .data(IR));
  Comparator #(.width(32), .mode("twosComplement")) comparator_1 (
    .a(v0), .b(32'h22), .eq(comparator_1_eq));  // open: gt, lt
  // Probe on EX_PC[11:0]
  // Probe on ID_PC[11:0]
  or or_2 (or_2_out, JMP, Branch);
  or or_3 (or_3_out, stop, OUTPUT);
  IF_ID if_id_1 (
    .IR(IR), .PC(IF_PC), .CLK(CLK), .IR_prime({IR_NOW, imm16}), .PC_prime(ID_PC), .\同步清零_高电平有效 (or_2_out),
    .\使能端_低电平有效 (or_3_out));  // open: 原PC, 原PC_prime, hit, hit_prime, status, status_prime
  assign bit_extender_1_out = {{16{1'b0}}, imm16};  // Bit_Extender bit_extender_1
  Multiplexer #(.select(1), .width(32), .disabled("Z"), .enable("false")) multiplexer_4 (
    .in0(bit_extender_1_out), .in1(Sign16), .out(IMM), .sel(Sign));
  assign Sign16 = {{16{imm16[15]}}, imm16};  // Bit_Extender bit_extender_2
  Multiplexer #(.select(1), .width(5), .disabled("Z"), .enable("false")) multiplexer_5 (
    .in0(IR_NOW[20:16]), .in1(imm16[15:11]), .out(multiplexer_5_out), .sel(RegDst));
  Multiplexer #(.select(1), .width(5), .disabled("Z"), .enable("false")) multiplexer_6 (
    .in0(multiplexer_5_out), .in1({5{1'b1}}), .out(WRITEREG), .sel(JAL));
  // Probe on M_PC[11:0]
  and and_3 (equal, syscall, comparator_1_eq);
  and and_4 (stop, syscall, not_4_out);
  not not_4 (not_4_out, comparator_1_eq);
  // Probe on WB_PC[11:0]
  // Probe on a0
  \源寄存器使用情况  \u_源寄存器使用情况_1  (
    .OP0(IR_NOW[26]), .OP1(IR_NOW[27]), .OP2(IR_NOW[28]), .OP3(IR_NOW[29]), .OP4(IR_NOW[30]),
    .OP5(IR_NOW[31]), .F0(imm16[0]), .F1(imm16[1]), .F2(imm16[2]), .F3(imm16[3]), .F4(imm16[4]),
    .F5(imm16[5]), .R1_Used(\源寄存器使用情况_1_r1_used ), .R2_Used(\源寄存器使用情况_1_r2_used ));
  \单周期硬布线控制器  \u_单周期硬布线控制器_1  (
    .Func(imm16[5:0]), .OP(IR_NOW[31:26]), .ALU_OP(ALUOP), .MemToReg(MemtoReg), .MemWrite(Memwrite_t),
    .ALU_SRC(ALUSRC), .RegWrite(Regwrite_t), .SysCALL(\单周期硬布线控制器_1_syscall ), .SignedExt(Sign),
    .RegDst(RegDst), .JR(jr_t), .JMP(jmp_t), .Beq(BEQ), .JAL(JAL), .Bne(BNE), .SRLV(SRLV), .LBU(LBU),
    .BGTZ(BGTZ));
  Multiplexer #(.select(1), .width(5), .disabled("Z"), .enable("false")) multiplexer_7 (
    .in0(IR_NOW[25:21]), .in1(5'b00010), .out(R1_num), .sel(\单周期硬布线控制器_1_syscall ));
  Multiplexer #(.select(1), .width(5), .disabled("Z"), .enable("false")) multiplexer_8 (
    .in0(IR_NOW[20:16]), .in1(5'b00100), .out(R2_num), .sel(\单周期硬布线控制器_1_syscall ));
  assign imm26 = {{6{IR_NOW[25]}}, {IR_NOW[25:16], imm16}};  // Bit_Extender bit_extender_3
  Multiplexer #(.select(1), .width(32), .disabled("Z"), .enable("false")) multiplexer_9 (
    .in1(a0), .out(multiplexer_9_out), .sel(equal));  // open: in0
  Register #(.width(32), .trigger("rising"), .Select("low")) register_1 (
    .D(multiplexer_9_out), .Q(LedData), .clk(CLK));  // open: en, clr
  \数据相关检测  \u_数据相关检测_1  (
    .MEM_RegWrite(ex_mem_1_regwrite_prime), .EX_RegWrite(id_ex_1_regwrite_prime),
    .R2_Used(\源寄存器使用情况_1_r2_used ), .R1_Used(\源寄存器使用情况_1_r1_used ), .R1_num(R1_num), .R2_num(R2_num),
    .EX_WriteReg_num(EXWriteReg), .MEM_WriteReg_num(MEMWriteReg), .OUTPUT(OUTPUT));
  MIPS_Regifile mips_regifile_1 (
    .Din(RDin), .Clk(CLK), .R1(mips_regifile_1_r1), .R2(mips_regifile_1_r2), .WE(RegWrite),
    .W_num(multiplexer_16_out), .R1_num(R1_num), .R2_num(R2_num));
  or or_4 (or_4_out, or_2_out, OUTPUT);
  ID_EX id_ex_1 (
    .RegDst(RegDst), .MemToReg(MemtoReg), .RegWirte(Regwrite_t), .MemWrite(Memwrite_t), .ALUSRCB(ALUSRC),
    .J(jmp_t), .JR(jr_t), .JAL(JAL), .BEQ(BEQ), .BNE(BNE), .ALUOP(ALUOP), .IR({IR_NOW, imm16}), .PC(ID_PC),
    .A(mips_regifile_1_r1), .B(mips_regifile_1_r2), .Imm16(IMM), .CLK(CLK),
    .RegDst_prime(id_ex_1_regdst_prime), .MemToReg_prime(id_ex_1_memtoreg_prime),
    .RegWrite_prime(id_ex_1_regwrite_prime), .MemWrite_prime(id_ex_1_memwrite_prime),
    .ALUSRCB_prime(id_ex_1_alusrcb_prime), .J_prime(JMP), .JR_prime(JR), .JAL_prime(id_ex_1_jal_prime),
    .BEQ_prime(beq_t), .BNE_prime(bne_t), .ALUOP_prime(id_ex_1_aluop_prime), .IR_prime(id_ex_1_ir_prime),
    .PC_prime(EX_PC), .A_prime(JRPC), .B_prime(id_ex_1_b_prime), .Imm16_prime(id_ex_1_imm16_prime),
    .\同步清零_高电平有效 (or_4_out), .\使能端_低电平有效 (stop), .Imm26(imm26), .Imm26_prime(id_ex_1_imm26_prime),
    .shamt_prime(id_ex_1_shamt_prime), .WriteReg_prime(EXWriteReg), .WriteReg(WRITEREG), .shamt(imm16[10:6]),
    .BGTZ(BGTZ), .BGTZ_prime(bgtz_t), .LBU(LBU), .LBU_prime(id_ex_1_lbu_prime), .SRLV(SRLV),
    .SRLV_prime(id_ex_1_srlv_prime), .sign16(Sign16), .sign16_prime(id_ex_1_sign16_prime));  // open: A_choose, A_Choose_prime, B_Choose, B_Choose_prime, hit, hit_prime, 原PC, 原PC_prime, status, status_prime
  Adder #(.width(32)) adder_2 (.a(EX_PC), .b(32'h4), .out({JPC[31:28], pc_4}));  // open: cin, cout
  Multiplexer #(.select(1), .width(32), .disabled("Z"), .enable("false")) multiplexer_10 (
    .in0(JRPC), .in1(id_ex_1_b_prime), .out(multiplexer_10_out), .sel(id_ex_1_srlv_prime));
  Multiplexer #(.select(1), .width(32), .disabled("Z"), .enable("false")) multiplexer_11 (
    .in0(id_ex_1_b_prime), .in1(id_ex_1_imm16_prime), .out(multiplexer_11_out), .sel(id_ex_1_alusrcb_prime));
  Multiplexer #(.select(1), .width(5), .disabled("Z"), .enable("false")) multiplexer_12 (
    .in0(id_ex_1_shamt_prime), .in1(JRPC[4:0]), .out(multiplexer_12_out), .sel(id_ex_1_srlv_prime));
  Shifter #(.width(32), .shift("ll")) shifter_1 (.in(id_ex_1_sign16_prime), .\dist (5'b00010), .out(shifter_1_out));
  Shifter #(.width(32), .shift("ll")) shifter_2 (
    .in(id_ex_1_imm26_prime), .\dist (5'b00010), .out({shifter_2_out, JPC[27:0]}));
  Counter #(.width(16), .max('hffff), .ongoal("wrap"), .trigger("rising"), .behavior("old")) counter_3 (
    .D({16{1'b0}}), .count(JMP), .Q(\无条件 ), .clk(CLK));  // open: load, carry, clr, preset
  // Probe on \无条件 
  MIPS_ALU mips_alu_1 (
    .X(multiplexer_10_out), .Y(multiplexer_11_out), .AluOP(id_ex_1_aluop_prime), .Equal(mips_alu_1_equal),
    .Result(mips_alu_1_result), .shamt(multiplexer_12_out));  // open: Result_2
  Adder #(.width(32)) adder_3 (.a(shifter_1_out), .b({JPC[31:28], pc_4}), .out(adder_3_out));  // open: cin, cout
  Counter #(.width(16), .max('hffff), .ongoal("wrap"), .trigger("rising"), .behavior("old")) counter_4 (
    .D({16{1'b0}}), .count(Branch), .Q(\有条件 ), .clk(CLK));  // open: load, carry, clr, preset
  // Probe on \有条件 
  not not_5 (not_5_out, mips_alu_1_equal);
  not not_6 (not_6_out, mips_alu_1_result[0]);
  and and_5 (and_5_out, not_5_out, bne_t);
  and and_6 (and_6_out, mips_alu_1_equal, beq_t);
  and and_7 (and_7_out, not_5_out, not_6_out, bgtz_t);
  or or_5 (Branch, and_5_out, and_6_out, and_7_out);
  EX_MEM ex_mem_1 (
    .JAL(id_ex_1_jal_prime), .RegDst(id_ex_1_regdst_prime), .MemToReg(id_ex_1_memtoreg_prime),
    .RegWirte(id_ex_1_regwrite_prime), .MemWrite(id_ex_1_memwrite_prime), .IR(id_ex_1_ir_prime), .PC(EX_PC),
    .B(id_ex_1_b_prime), .ALU(mips_alu_1_result), .CLK(CLK), .JAL_prime(ex_mem_1_jal_prime),
    .RegDst_prime(ex_mem_1_regdst_prime), .MemToReg_prime(ex_mem_1_memtoreg_prime),
    .RegWrite_prime(ex_mem_1_regwrite_prime), .MemWrite_prime(MemWrite), .IR_prime(ex_mem_1_ir_prime),
    .PC_prime(M_PC), .B_prime(MDin), .ALU_prime(ex_mem_1_alu_prime), .\使能端_低电平有效 (stop), .A(JRPC),
    .A_prime(ex_mem_1_a_prime), .WriteReg(EXWriteReg), .WriteReg_prime(MEMWriteReg), .LBU(id_ex_1_lbu_prime),
    .LBU_prime(ex_mem_1_lbu_prime));  // open: 同步清零_高电平有效
  RAM #(.addrWidth(10), .dataWidth(32), .bus("separate"), .Select("high")) ram_1 (
    .addr(ex_mem_1_alu_prime[11:2]), .din(MDin), .data(ram_1_data), .str(MemWrite), .sel(1'b1), .clk(CLK));  // open: ld, clr
  MEM_WB mem_wb_1 (
    .JAL(ex_mem_1_jal_prime), .RegDst(ex_mem_1_regdst_prime), .MemToReg(ex_mem_1_memtoreg_prime),
    .RegWirte(ex_mem_1_regwrite_prime), .IR(ex_mem_1_ir_prime), .PC(M_PC), .ALU(ex_mem_1_alu_prime),
    .MD(ram_1_data), .CLK(CLK), .JAL_prime(mem_wb_1_jal_prime), .RegDst_prime(mem_wb_1_regdst_prime),
    .MemToReg_prime(mem_wb_1_memtoreg_prime), .RegWrite_prime(RegWrite), .IR_prime(IR_final),
    .PC_prime(WB_PC), .ALU_prime(mem_wb_1_alu_prime), .MD_prime(mem_wb_1_md_prime), .\使能端_低电平有效 (stop),
    .A(ex_mem_1_a_prime), .A_prime(v0), .B(MDin), .B_prime(a0), .WriteReg(MEMWriteReg),
    .LBU(ex_mem_1_lbu_prime), .LBU_prime(mem_wb_1_lbu_prime));  // open: 同步清零_高电平有效, WriteReg_prime
  Multiplexer #(.select(1), .width(5), .disabled("Z"), .enable("false")) multiplexer_13 (
    .in0(IR_final[20:16]), .in1(IR_final[15:11]), .out(multiplexer_13_out), .sel(mem_wb_1_regdst_prime));
  Multiplexer #(.select(1), .width(32), .disabled("Z"), .enable("false")) multiplexer_14 (
    .in0(mem_wb_1_alu_prime), .in1(mem_wb_1_md_prime), .out(multiplexer_14_out), .sel(mem_wb_1_memtoreg_prime));
  Multiplexer #(.select(1), .width(32), .disabled("Z"), .enable("false")) multiplexer_15 (
    .in0(multiplexer_17_out), .in1(adder_4_out), .out(RDin), .sel(mem_wb_1_jal_prime));
  Multiplexer #(.select(1), .width(5), .disabled("Z"), .enable("false")) multiplexer_16 (
    .in0(multiplexer_13_out), .in1({5{1'b1}}), .out(multiplexer_16_out), .sel(mem_wb_1_jal_prime));
  Comparator #(.width(32), .mode("twosComplement")) comparator_2 (
    .a(IR_final), .b(32'hc), .eq(syscall));  // open: gt, lt
  Shifter #(.width(32), .shift("ll")) shifter_3 (
    .in(32'hff), .\dist ({mem_wb_1_alu_prime[1:0], 3'b000}), .out(shifter_3_out));
  Adder #(.width(32)) adder_4 (.a(WB_PC), .b(32'h4), .out(adder_4_out));  // open: cin, cout
  assign and_8_out = multiplexer_14_out & shifter_3_out;  // AND_Gate and_8, 32 bits wide
  Shifter #(.width(32), .shift("lr")) shifter_4 (
    .in(and_8_out), .\dist ({mem_wb_1_alu_prime[1:0], 3'b000}), .out(shifter_4_out));
  Multiplexer #(.select(1), .width(32), .disabled("Z"), .enable("false")) multiplexer_17 (
    .in0(multiplexer_14_out), .in1(shifter_4_out), .out(multiplexer_17_out), .sel(mem_wb_1_lbu_prime));

  // Other names for the same wires on the sheet: IR_NOW[15:0] = imm16; shamt[4:0] = imm16[10:6];
  //   pc_4[31:28] = JPC[31:28]; MEM_PC[31:0] = M_PC

  // Notes on the sheet:
  //   中断源
  //   中断等待指示
  //   数码管输出
  //   contents of rom_1 (hex, n*v repeats v):
  //   20110001 8000c05 20110001 20120002 20130003 8000c09 20110001 20120002 20130003 8000c0d 20110001
  //   20120002 20130003 8000c11 20110001 20120002 20130003 c000cb8 20100001 20110001 118fc0 112020
  //   20020022 c 118882 12200001 8000c15 112020 20020022 c 20110001 118880 112020 20020022 c 12200001
  //   8000c1f 20110001 118fc0 112020 20020022 c 1188c3 112020 20020022 c 118903 112020 20020022 c 118903
  //   112020 20020022 c 118903 112020 20020022 c 118903 112020 20020022 c 118903 112020 20020022 c 118903
  //   112020 20020022 c 118903 112020 20020022 c 20100001 109fc0 139fc3 8021 2012000c 24160003 26100001
  //   3210000f 20080008 20090001 139900 2709825 132020 20020022 c 1094022 1500fff9 22100001 2018000f
  //   2188024 108700 20080008 20090001 139902 2709825 132021 20020022 c 1094022 1500fff9 108702 2c9b022
  //   12c00001 8000c50 4020 1084027 84400 3508ffff 82021 20020022 c 2010ffff 20110000 ae300000 22100001
  //   22310004 ae300000 22100001 22310004 ae300000 22100001 22310004 ae300000 22100001 22310004 ae300000
  //   22100001 22310004 ae300000 22100001 22310004 ae300000 22100001 22310004 ae300000 22100001 22310004
  //   ae300000 22100001 22310004 ae300000 22100001 22310004 ae300000 22100001 22310004 ae300000 22100001
  //   22310004 ae300000 22100001 22310004 ae300000 22100001 22310004 ae300000 22100001 22310004 ae300000
  //   22100001 22310004 22100001 8020 2011003c 8e130000 8e340000 274402a 11000002 ae330000 ae140000
  //   2231fffc 1611fff8 102020 20020022 c 22100004 2011003c 1611fff2 20020032 c 20100000 22100001 102020
  //   20020022 c 22100002 102020 20020022 c 22100003 102020 20020022 c 22100004 102020 20020022 c 22100005
  //   102020 20020022 c 22100006 102020 20020022 c 22100007 102020 20020022 c 22100008 102020 20020022
  //   20020022 c 3e00008
  //   rt
  //   流水调试日志用
  //   rs
  //   rd
  //   OP
  //   为方便自动评测，需要输出流水线各段保存的PC值，注意是PC不是PC+4，另外ID段寄存器写入信息，Mem段内存写入信息也要输出
  //   rt
endmodule
module \重定向流水线  (
  output RegWrite,
  output MemWrite,
  output [31:0] IF_PC,
  output [31:0] ID_PC,
  output [31:0] EX_PC,
  output [31:0] M_PC,
  output [31:0] WB_PC,
  output [31:0] RDin,
  output [31:0] MDin,
  output [31:0] LedData
);

  wire ALUSRC, and_1_out, and_2_out, and_5_out, and_6_out, and_7_out, BEQ, beq_t, BGTZ, bgtz_t, BNE, bne_t,
       Branch, CLK, comparator_1_eq, equal, ex_mem_1_jal_prime, ex_mem_1_lbu_prime, ex_mem_1_memtoreg_prime,
       ex_mem_1_regdst_prime, exregwrite, Go, id_ex_1_alusrcb_prime, id_ex_1_jal_prime, id_ex_1_lbu_prime,
       id_ex_1_memtoreg_prime, id_ex_1_memwrite_prime, id_ex_1_regdst_prime, id_ex_1_srlv_prime, IR1, IR2,
       IR3, JAL, JMP, jmp_t, JR, jr_t, LBU, mem_wb_1_jal_prime, mem_wb_1_lbu_prime, mem_wb_1_memtoreg_prime,
       mem_wb_1_regdst_prime, memregwrite, MemtoReg, Memwrite_t, mips_alu_1_equal, not_1_out, not_2_out,
       not_3_out, not_4_out, not_5_out, not_6_out, or_1_out, or_2_out, or_3_out, OUTPUT, R1_USED, R2_USED,
       RegDst, Regwrite_t, RST, Sign, SRLV, stop, syscall, W1, W2, W3, \单周期硬布线控制器_1_syscall ;
  wire [1:0] C_1, C_2, id_ex_1_a_choose_prime, id_ex_1_b_choose_prime;
  wire [3:0] ALUOP, id_ex_1_aluop_prime;
  wire [4:0] EXWriteReg, id_ex_1_shamt_prime, MEMWriteReg, multiplexer_5_out, multiplexer_13_out,
       multiplexer_15_out, multiplexer_18_out, R1_num, R2_num, WRITEREG;
  wire [15:0] imm16, \LoadUse次数 , \总周期数 , \插入气泡数 , \无条件 , \无条件分支数 , \有条件 , \条件分支成功数 ;
  wire [27:0] pc_4;
  wire [31:0] A, a0, adder_3_out, adder_4_out, ALU_1, ALU_2, and_8_out, B, bit_extender_1_out,
       ex_mem_1_a_prime, EXIR, id_ex_1_imm16_prime, id_ex_1_imm26_prime, id_ex_1_sign16_prime, IMM, imm26,
       IR, IR_final, JPC, JRPC, MD, mem_wb_1_md_prime, MEMIR, mips_alu_1_result, mips_regifile_1_r1,
       mips_regifile_1_r2, multiplexer_1_out, multiplexer_2_out, multiplexer_3_out, multiplexer_9_out,
       multiplexer_12_out, multiplexer_16_out, PC, R1, R2, ram_1_data, shifter_1_out, shifter_3_out,
       shifter_4_out, Sign16, v0;
  wire [31:16] IR_NOW;
  wire [31:28] shifter_2_out;

  Button \u_总复位  (.out(RST));
  Button _1 (.out(IR1));
  Button _2 (.out(IR2));
  Button _3 (.out(IR3));
  Button \u_继续运行  (.out(Go));
  LED #(.active("true")) led_1 (.in(W1));
  LED #(.active("true")) led_2 (.in(W2));
  LED #(.active("true")) led_3 (.in(W3));
  Hex_Digit_Display hex_digit_display_1 (.value(LedData[31:28]));  // open: dp
  Hex_Digit_Display hex_digit_display_2 (.value(LedData[27:24]));  // open: dp
  Hex_Digit_Display hex_digit_display_3 (.value(LedData[23:20]));  // open: dp
  Multiplexer #(.select(1), .width(32), .disabled("Z"), .enable("false")) multiplexer_1 (
    .in0(PC), .in1(adder_3_out), .out(multiplexer_1_out), .sel(Branch));
  Multiplexer #(.select(1), .width(32), .disabled("Z"), .enable("false")) multiplexer_2 (
    .in0(multiplexer_1_out), .in1(JPC), .out(multiplexer_2_out), .sel(JMP));
  Hex_Digit_Display hex_digit_display_4 (.value(LedData[15:12]));  // open: dp
  Hex_Digit_Display hex_digit_display_5 (.value(LedData[19:16]));  // open: dp
  not not_1 (not_1_out, stop);
  and and_1 (and_1_out, not_1_out, OUTPUT);
  not not_2 (not_2_out, OUTPUT);
  not not_3 (not_3_out, stop);
  and and_2 (and_2_out, not_2_out, not_3_out);
  Multiplexer #(.select(1), .width(32), .disabled("Z"), .enable("false")) multiplexer_3 (
    .in0(multiplexer_2_out), .in1(JRPC), .out(multiplexer_3_out), .sel(JR));
  assign bit_extender_1_out = {{16{1'b0}}, imm16};  // Bit_Extender bit_extender_1
  assign Sign16 = {{16{imm16[15]}}, imm16};  // Bit_Extender bit_extender_2
  Hex_Digit_Display hex_digit_display_6 (.value(LedData[7:4]));  // open: dp
  Hex_Digit_Display hex_digit_display_7 (.value(LedData[11:8]));  // open: dp
  Clock #(.highDuration(1), .lowDuration(1)) clock_1 (.out(CLK));
  Register #(.width(32), .trigger("rising"), .Select("low")) u_PC (
    .D(multiplexer_3_out), .en(and_2_out), .Q(IF_PC), .clk(CLK));  // open: clr
  Multiplexer #(.select(1), .width(32), .disabled("Z"), .enable("false")) multiplexer_4 (
    .in0(bit_extender_1_out), .in1(Sign16), .out(IMM), .sel(Sign));
  Hex_Digit_Display hex_digit_display_8 (.value(LedData[3:0]));  // open: dp
  Counter #(.width(16), .max('hffff), .ongoal("wrap"), .trigger("rising"), .behavior("old")) counter_1 (
    .D({16{1'b0}}), .count(and_1_out), .Q(\插入气泡数 ), .clk(CLK));  // open: load, carry, clr, preset
  Counter #(.width(16), .max('hffff), .ongoal("wrap"), .trigger("rising"), .behavior("old")) counter_2 (
    .D({16{1'b0}}), .count(not_3_out), .Q(\总周期数 ), .clk(CLK));  // open: load, carry, clr, preset
  // Probe on \插入气泡数 
  // Probe on \总周期数 
  // Probe on \无条件分支数 
  // Probe on \条件分支成功数 
  // Probe on \插入气泡数 
  // Probe on \LoadUse次数 
  Adder #(.width(32)) adder_1 (.a(IF_PC), .b(32'h4), .out(PC));  // open: cin, cout
  ROM #(.addrWidth(10), .dataWidth(32), .Select("high")) rom_1 (.addr(IF_PC[11:2]), .data(IR));
  Multiplexer #(.select(1), .width(5), .disabled("Z"), .enable("false")) multiplexer_5 (
    .in0(IR_NOW[20:16]), .in1(imm16[15:11]), .out(multiplexer_5_out), .sel(RegDst));
  // Probe on IF_PC[11:0]
  or or_1 (or_1_out, stop, OUTPUT);
  Multiplexer #(.select(1), .width(5), .disabled("Z"), .enable("false")) multiplexer_6 (
    .in0(multiplexer_5_out), .in1({5{1'b1}}), .out(WRITEREG), .sel(JAL));
  // Probe on EX_PC[11:0]
  // Probe on ID_PC[11:0]
  or or_2 (or_2_out, JMP, Branch);
  IF_ID if_id_1 (
    .IR(IR), .PC(IF_PC), .CLK(CLK), .IR_prime({IR_NOW, imm16}), .PC_prime(ID_PC), .\同步清零_高电平有效 (or_2_out),
    .\使能端_低电平有效 (or_1_out));  // open: 原PC, 原PC_prime, hit, hit_prime, status, status_prime
  // Probe on M_PC[11:0]
  // Probe on WB_PC[11:0]
  \单周期硬布线控制器  \u_单周期硬布线控制器_1  (
    .Func(imm16[5:0]), .OP(IR_NOW[31:26]), .ALU_OP(ALUOP), .MemToReg(MemtoReg), .MemWrite(Memwrite_t),
    .ALU_SRC(ALUSRC), .RegWrite(Regwrite_t), .SysCALL(\单周期硬布线控制器_1_syscall ), .SignedExt(Sign),
    .RegDst(RegDst), .JR(jr_t), .JMP(jmp_t), .Beq(BEQ), .JAL(JAL), .Bne(BNE), .SRLV(SRLV), .LBU(LBU),
    .BGTZ(BGTZ));
  Multiplexer #(.select(1), .width(5), .disabled("Z"), .enable("false")) multiplexer_7 (
    .in0(IR_NOW[25:21]), .in1(5'b00010), .out(R1_num), .sel(\单周期硬布线控制器_1_syscall ));
  Multiplexer #(.select(1), .width(5), .disabled("Z"), .enable("false")) multiplexer_8 (
    .in0(IR_NOW[20:16]), .in1(5'b00100), .out(R2_num), .sel(\单周期硬布线控制器_1_syscall ));
  Comparator #(.width(32), .mode("twosComplement")) comparator_1 (
    .a(v0), .b(32'h22), .eq(comparator_1_eq));  // open: gt, lt
  \源寄存器使用情况  \u_源寄存器使用情况_1  (
    .OP0(IR_NOW[26]), .OP1(IR_NOW[27]), .OP2(IR_NOW[28]), .OP3(IR_NOW[29]), .OP4(IR_NOW[30]),
    .OP5(IR_NOW[31]), .F0(imm16[0]), .F1(imm16[1]), .F2(imm16[2]), .F3(imm16[3]), .F4(imm16[4]),
    .F5(imm16[5]), .R1_Used(R1_USED), .R2_Used(R2_USED));
  not not_4 (not_4_out, comparator_1_eq);
  MIPS_Regifile mips_regifile_1 (
    .Din(RDin), .Clk(CLK), .R1(mips_regifile_1_r1), .R2(mips_regifile_1_r2), .WE(RegWrite),
    .W_num(multiplexer_18_out), .R1_num(R1_num), .R2_num(R2_num));
  assign imm26 = {{6{IR_NOW[25]}}, {IR_NOW[25:16], imm16}};  // Bit_Extender bit_extender_3
  and and_3 (equal, syscall, comparator_1_eq);
  and and_4 (stop, syscall, not_4_out);
  \LOAD_USE检测  \load_use检测_1  (
    .EX_RegWrite(exregwrite), .R2_Used(R2_USED), .R1_Used(R1_USED), .R1_num(R1_num), .R2_num(R2_num),
    .EX_WriteReg_num(EXWriteReg), .OP(EXIR[31:26]), .OUTPUT(OUTPUT));
  Multiplexer #(.select(1), .width(32), .disabled("Z"), .enable("false")) multiplexer_9 (
    .in1(a0), .out(multiplexer_9_out), .sel(equal));  // open: in0
  // Probe on a0
  or or_3 (or_3_out, or_2_out, OUTPUT);
  ID_EX id_ex_1 (
    .RegDst(RegDst), .MemToReg(MemtoReg), .RegWirte(Regwrite_t), .MemWrite(Memwrite_t), .ALUSRCB(ALUSRC),
    .J(jmp_t), .JR(jr_t), .JAL(JAL), .BEQ(BEQ), .BNE(BNE), .ALUOP(ALUOP), .IR({IR_NOW, imm16}), .PC(ID_PC),
    .A(mips_regifile_1_r1), .B(mips_regifile_1_r2), .Imm16(IMM), .CLK(CLK),
    .RegDst_prime(id_ex_1_regdst_prime), .MemToReg_prime(id_ex_1_memtoreg_prime),
    .RegWrite_prime(exregwrite), .MemWrite_prime(id_ex_1_memwrite_prime),
    .ALUSRCB_prime(id_ex_1_alusrcb_prime), .J_prime(JMP), .JR_prime(JR), .JAL_prime(id_ex_1_jal_prime),
    .BEQ_prime(beq_t), .BNE_prime(bne_t), .ALUOP_prime(id_ex_1_aluop_prime), .IR_prime(EXIR),
    .PC_prime(EX_PC), .A_prime(R1), .B_prime(R2), .Imm16_prime(id_ex_1_imm16_prime), .\同步清零_高电平有效 (or_3_out),
    .\使能端_低电平有效 (stop), .Imm26(imm26), .Imm26_prime(id_ex_1_imm26_prime), .shamt_prime(id_ex_1_shamt_prime),
    .WriteReg_prime(EXWriteReg), .WriteReg(WRITEREG), .shamt(imm16[10:6]), .A_choose(C_1),
    .A_Choose_prime(id_ex_1_a_choose_prime), .B_Choose(C_2), .B_Choose_prime(id_ex_1_b_choose_prime),
    .BGTZ(BGTZ), .BGTZ_prime(bgtz_t), .LBU(LBU), .LBU_prime(id_ex_1_lbu_prime), .SRLV(SRLV),
    .SRLV_prime(id_ex_1_srlv_prime), .sign16(Sign16), .sign16_prime(id_ex_1_sign16_prime));  // open: hit, hit_prime, 原PC, 原PC_prime, status, status_prime
  Register #(.width(32), .trigger("rising"), .Select("low")) register_1 (
    .D(multiplexer_9_out), .Q(LedData), .clk(CLK));  // open: en, clr
  Multiplexer #(.select(2), .width(32), .disabled("Z"), .enable("false")) multiplexer_10 (
    .in0(R1), .in1(ALU_1), .in2(ALU_2), .in3(MD), .out(A), .sel(id_ex_1_a_choose_prime));
  Multiplexer #(.select(1), .width(32), .disabled("Z"), .enable("false")) multiplexer_11 (
    .in0(A), .in1(B), .out(JRPC), .sel(id_ex_1_srlv_prime));
  Multiplexer #(.select(1), .width(32), .disabled("Z"), .enable("false")) multiplexer_12 (
    .in0(B), .in1(id_ex_1_imm16_prime), .out(multiplexer_12_out), .sel(id_ex_1_alusrcb_prime));
  // Probe on multiplexer_12_out
  Shifter #(.width(32), .shift("ll")) shifter_1 (.in(id_ex_1_sign16_prime), .\dist (5'b00010), .out(shifter_1_out));
  Shifter #(.width(32), .shift("ll")) shifter_2 (
    .in(id_ex_1_imm26_prime), .\dist (5'b00010), .out({shifter_2_out, JPC[27:0]}));
  Adder #(.width(32)) adder_2 (.a(EX_PC), .b(32'h4), .out({JPC[31:28], pc_4}));  // open: cin, cout
  Multiplexer #(.select(1), .width(5), .disabled("Z"), .enable("false")) multiplexer_13 (
    .in0(id_ex_1_shamt_prime), .in1(A[4:0]), .out(multiplexer_13_out), .sel(id_ex_1_srlv_prime));
  Multiplexer #(.select(2), .width(32), .disabled("Z"), .enable("false")) multiplexer_14 (
    .in0(R2), .in1(ALU_1), .in2(ALU_2), .in3(MD), .out(B), .sel(id_ex_1_b_choose_prime));
  Adder #(.width(32)) adder_3 (.a(shifter_1_out), .b({JPC[31:28], pc_4}), .out(adder_3_out));  // open: cin, cout
  \重定向相关  \u_重定向相关_1  (
    .MEM_RegWrite(memregwrite), .EX_RegWrite(exregwrite), .R2_Used(R2_USED), .R1_Used(R1_USED),
    .R1_num(R1_num), .R2_num(R2_num), .EX_WriteReg_num(EXWriteReg), .MEM_WriteReg_num(MEMWriteReg),
    .OP(MEMIR[31:26]), .A_Choose(C_1), .B_Choose(C_2));
  MIPS_ALU mips_alu_1 (
    .X(JRPC), .Y(multiplexer_12_out), .AluOP(id_ex_1_aluop_prime), .Equal(mips_alu_1_equal),
    .Result(mips_alu_1_result), .shamt(multiplexer_13_out));  // open: Result_2
  Counter #(.width(16), .max('hffff), .ongoal("wrap"), .trigger("rising"), .behavior("old")) counter_3 (
    .D({16{1'b0}}), .count(JMP), .Q(\无条件 ), .clk(CLK));  // open: load, carry, clr, preset
  // Probe on JRPC
  not not_5 (not_5_out, mips_alu_1_equal);
  not not_6 (not_6_out, mips_alu_1_result[0]);
  // Probe on \无条件 
  and and_5 (and_5_out, not_5_out, bne_t);
  and and_6 (and_6_out, mips_alu_1_equal, beq_t);
  and and_7 (and_7_out, not_5_out, not_6_out, bgtz_t);
  or or_4 (Branch, and_5_out, and_6_out, and_7_out);
  Counter #(.width(16), .max('hffff), .ongoal("wrap"), .trigger("rising"), .behavior("old")) counter_4 (
    .D({16{1'b0}}), .count(Branch), .Q(\有条件 ), .clk(CLK));  // open: load, carry, clr, preset
  // Probe on \有条件 
  EX_MEM ex_mem_1 (
    .JAL(id_ex_1_jal_prime), .RegDst(id_ex_1_regdst_prime), .MemToReg(id_ex_1_memtoreg_prime),
    .RegWirte(exregwrite), .MemWrite(id_ex_1_memwrite_prime), .IR(EXIR), .PC(EX_PC), .B(B),
    .ALU(mips_alu_1_result), .CLK(CLK), .JAL_prime(ex_mem_1_jal_prime), .RegDst_prime(ex_mem_1_regdst_prime),
    .MemToReg_prime(ex_mem_1_memtoreg_prime), .RegWrite_prime(memregwrite), .MemWrite_prime(MemWrite),
    .IR_prime(MEMIR), .PC_prime(M_PC), .B_prime(MDin), .ALU_prime(ALU_1), .\使能端_低电平有效 (stop), .A(A),
    .A_prime(ex_mem_1_a_prime), .WriteReg(EXWriteReg), .WriteReg_prime(MEMWriteReg), .LBU(id_ex_1_lbu_prime),
    .LBU_prime(ex_mem_1_lbu_prime));  // open: 同步清零_高电平有效
  RAM #(.addrWidth(10), .dataWidth(32), .bus("separate"), .Select("high")) ram_1 (
    .addr(ALU_1[11:2]), .din(MDin), .data(ram_1_data), .str(MemWrite), .sel(1'b1), .clk(CLK));  // open: ld, clr
  MEM_WB mem_wb_1 (
    .JAL(ex_mem_1_jal_prime), .RegDst(ex_mem_1_regdst_prime), .MemToReg(ex_mem_1_memtoreg_prime),
    .RegWirte(memregwrite), .IR(MEMIR), .PC(M_PC), .ALU(ALU_1), .MD(ram_1_data), .CLK(CLK),
    .JAL_prime(mem_wb_1_jal_prime), .RegDst_prime(mem_wb_1_regdst_prime),
    .MemToReg_prime(mem_wb_1_memtoreg_prime), .RegWrite_prime(RegWrite), .IR_prime(IR_final),
    .PC_prime(WB_PC), .ALU_prime(ALU_2), .MD_prime(mem_wb_1_md_prime), .\使能端_低电平有效 (stop),
    .A(ex_mem_1_a_prime), .A_prime(v0), .B(MDin), .B_prime(a0), .WriteReg(MEMWriteReg),
    .LBU(ex_mem_1_lbu_prime), .LBU_prime(mem_wb_1_lbu_prime));  // open: 同步清零_高电平有效, WriteReg_prime
  Multiplexer #(.select(1), .width(5), .disabled("Z"), .enable("false")) multiplexer_15 (
    .in0(IR_final[20:16]), .in1(IR_final[15:11]), .out(multiplexer_15_out), .sel(mem_wb_1_regdst_prime));
  Multiplexer #(.select(1), .width(32), .disabled("Z"), .enable("false")) multiplexer_16 (
    .in0(ALU_2), .in1(mem_wb_1_md_prime), .out(multiplexer_16_out), .sel(mem_wb_1_memtoreg_prime));
  Multiplexer #(.select(1), .width(32), .disabled("Z"), .enable("false")) multiplexer_17 (
    .in0(MD), .in1(adder_4_out), .out(RDin), .sel(mem_wb_1_jal_prime));
  Multiplexer #(.select(1), .width(5), .disabled("Z"), .enable("false")) multiplexer_18 (
    .in0(multiplexer_15_out), .in1({5{1'b1}}), .out(multiplexer_18_out), .sel(mem_wb_1_jal_prime));
  Comparator #(.width(32), .mode("twosComplement")) comparator_2 (
    .a(IR_final), .b(32'hc), .eq(syscall));  // open: gt, lt
  Shifter #(.width(32), .shift("ll")) shifter_3 (.in(32'hff), .\dist ({ALU_2[1:0], 3'b000}), .out(shifter_3_out));
  Adder #(.width(32)) adder_4 (.a(WB_PC), .b(32'h4), .out(adder_4_out));  // open: cin, cout
  assign and_8_out = multiplexer_16_out & shifter_3_out;  // AND_Gate and_8, 32 bits wide
  Shifter #(.width(32), .shift("lr")) shifter_4 (.in(and_8_out), .\dist ({ALU_2[1:0], 3'b000}), .out(shifter_4_out));
  Multiplexer #(.select(1), .width(32), .disabled("Z"), .enable("false")) multiplexer_19 (
    .in0(multiplexer_16_out), .in1(shifter_4_out), .out(MD), .sel(mem_wb_1_lbu_prime));

  // Other names for the same wires on the sheet: IR_NOW[15:0] = imm16; shamt[4:0] = imm16[10:6];
  //   pc_4[31:28] = JPC[31:28]; MEM_PC[31:0] = M_PC

  // Notes on the sheet:
  //   中断源
  //   中断等待指示
  //   数码管输出
  //   contents of rom_1 (hex, n*v repeats v):
  //   20110001 8000c05 20110001 20120002 20130003 8000c09 20110001 20120002 20130003 8000c0d 20110001
  //   20120002 20130003 8000c11 20110001 20120002 20130003 c000cb8 20100001 20110001 118fc0 112020
  //   20020022 c 118882 12200001 8000c15 112020 20020022 c 20110001 118880 112020 20020022 c 12200001
  //   8000c1f 20110001 118fc0 112020 20020022 c 1188c3 112020 20020022 c 118903 112020 20020022 c 118903
  //   112020 20020022 c 118903 112020 20020022 c 118903 112020 20020022 c 118903 112020 20020022 c 118903
  //   112020 20020022 c 118903 112020 20020022 c 20100001 109fc0 139fc3 8021 2012000c 24160003 26100001
  //   3210000f 20080008 20090001 139900 2709825 132020 20020022 c 1094022 1500fff9 22100001 2018000f
  //   2188024 108700 20080008 20090001 139902 2709825 132021 20020022 c 1094022 1500fff9 108702 2c9b022
  //   12c00001 8000c50 4020 1084027 84400 3508ffff 82021 20020022 c 2010ffff 20110000 ae300000 22100001
  //   22310004 ae300000 22100001 22310004 ae300000 22100001 22310004 ae300000 22100001 22310004 ae300000
  //   22100001 22310004 ae300000 22100001 22310004 ae300000 22100001 22310004 ae300000 22100001 22310004
  //   ae300000 22100001 22310004 ae300000 22100001 22310004 ae300000 22100001 22310004 ae300000 22100001
  //   22310004 ae300000 22100001 22310004 ae300000 22100001 22310004 ae300000 22100001 22310004 ae300000
  //   22100001 22310004 22100001 8020 2011003c 8e130000 8e340000 274402a 11000002 ae330000 ae140000
  //   2231fffc 1611fff8 102020 20020022 c 22100004 2011003c 1611fff2 20020032 c 20100000 22100001 102020
  //   20020022 c 22100002 102020 20020022 c 22100003 102020 20020022 c 22100004 102020 20020022 c 22100005
  //   102020 20020022 c 22100006 102020 20020022 c 22100007 102020 20020022 c 22100008 102020 20020022
  //   20020022 c 3e00008
  //   rt
  //   流水调试日志用
  //   OP
  //   OP
  //   rs
  //   为方便自动评测，需要输出流水线各段保存的PC值，注意是PC不是PC+4，另外ID段寄存器写入信息，Mem段内存写入信息也要输出
  //   rt
endmodule

module \单周期MIPS_多级中断  (
  input  IR1,
  input  IR2,
  input  IR3,
  output RegWrite,
  output MemWrite,
  output [31:0] PC,
  output [31:0] IR,
  output [31:0] RDin,
  output [31:0] MDin,
  output [31:0] LedData
);

  wire and_6_out, and_7_out, and_8_out, and_9_out, and_10_out, and_11_out, and_12_out, and_13_out,
       and_14_out, and_16_out, and_17_out, and_18_out, and_22_out, and_23_out, and_24_out, and_26_out,
       and_27_out, Beq, BGTZ, Bne, branch, CLK, comparator_1_eq, comparator_2_eq, comparator_3_eq,
       comparator_4_eq, comparator_5_eq, comparator_6_eq, comparator_7_eq, comparator_8_eq, comparator_9_eq,
       comparator_10_eq, comparator_11_eq, comparator_12_eq, comparator_13_eq, comparator_14_eq,
       comparator_15_eq, \CPU中断请求 , d_ff_1_q, d_ff_2_q, d_ff_3_q, decoder_1_out1, decoder_1_out2,
       decoder_1_out3, equal, ERET, ex1, ex2, ex3, flag1, flag2, flag3, Go, IE, IR1_t, IR2_t, IR3_t, IRA,
       IRB, IRC, JAL, JMP, JR, LBU, MFC0, mips_alu_1_equal, MTC0, not_1_out, not_2_out, not_3_out, not_4_out,
       not_5_out, not_6_out, not_7_out, not_8_out, or_1_out, or_6_out, or_7_out, or_8_out, or_13_out,
       or_14_out, or_15_out, or_16_out, or_17_out, or_18_out, rst1, rst2, rst3, SignedExt, SRLV, stop,
       Syscall, W1, W2, W3, \单周期硬布线控制器_1_alu_src , \单周期硬布线控制器_1_memtoreg , \单周期硬布线控制器_1_regdst ;
  wire [1:0] counter_4_q, priority_encoder_1_out, XY, xy_t;
  wire [3:0] \单周期硬布线控制器_1_alu_op ;
  wire [4:0] multiplexer_7_out, multiplexer_8_out, multiplexer_9_out, multiplexer_10_out, multiplexer_14_out;
  wire [15:0] \总周期数 , \无条件 , \有条件 ;
  wire [31:0] adder_2_out, and_15_out, bit_extender_1_out, bit_extender_2_out, bit_extender_3_out, EPC,
       EPC_2_q, EPC_3_q, EPC_q, JPC, JRPC, mips_alu_1_result, multiplexer_1_out, multiplexer_2_out,
       multiplexer_3_out, multiplexer_4_out, multiplexer_5_out, multiplexer_6_out, multiplexer_11_out,
       multiplexer_12_out, multiplexer_13_out, multiplexer_16_out, multiplexer_17_out, multiplexer_19_out,
       multiplexer_20_out, multiplexer_21_out, PC_4, PC_OUT, ram_1_data, shifter_1_out, shifter_2_out,
       shifter_3_out, shifter_4_out;

  Clock #(.highDuration(1), .lowDuration(1)) clock_1 (.out(CLK));
  Button _1 (.out(IRA));
  Button _2 (.out(IRB));
  Button _3 (.out(IRC));
  Button \u_继续运行  (.out(Go));
  LED #(.active("true")) led_1 (.in(W1));
  LED #(.active("true")) led_2 (.in(W2));
  LED #(.active("true")) led_3 (.in(W3));
  Hex_Digit_Display hex_digit_display_1 (.value(LedData[31:28]));  // open: dp
  Hex_Digit_Display hex_digit_display_2 (.value(LedData[27:24]));  // open: dp
  Hex_Digit_Display hex_digit_display_3 (.value(LedData[23:20]));  // open: dp
  Hex_Digit_Display hex_digit_display_4 (.value(LedData[19:16]));  // open: dp
  Hex_Digit_Display hex_digit_display_5 (.value(LedData[15:12]));  // open: dp
  Multiplexer #(.select(1), .width(32), .disabled("Z"), .enable("false")) multiplexer_1 (
    .in0(PC_4), .in1(adder_2_out), .out(multiplexer_1_out), .sel(branch));
  Multiplexer #(.select(1), .width(32), .disabled("Z"), .enable("false")) multiplexer_2 (
    .in0(multiplexer_1_out), .in1(PC_OUT), .out(multiplexer_2_out), .sel(\CPU中断请求 ));
  Hex_Digit_Display hex_digit_display_6 (.value(LedData[7:4]));  // open: dp
  Hex_Digit_Display hex_digit_display_7 (.value(LedData[11:8]));  // open: dp
  // Probe on \总周期数 
  Multiplexer #(.select(1), .width(32), .disabled("Z"), .enable("false")) multiplexer_3 (
    .in0(multiplexer_2_out), .in1(EPC), .out(multiplexer_3_out), .sel(ERET));
  // Probe on EPC
  // Probe on JRPC
  Hex_Digit_Display hex_digit_display_8 (.value(LedData[3:0]));  // open: dp
  // Probe on PC
  Multiplexer #(.select(1), .width(32), .disabled("Z"), .enable("false")) multiplexer_4 (
    .in0(multiplexer_3_out), .in1(JPC), .out(multiplexer_4_out), .sel(JMP));
  Comparator #(.width(32), .mode("twosComplement")) comparator_1 (
    .a(JRPC), .b(32'h22), .eq(comparator_1_eq));  // open: gt, lt
  not not_1 (not_1_out, stop);
  or or_1 (or_1_out, Go, not_1_out);
  Multiplexer #(.select(1), .width(32), .disabled("Z"), .enable("false")) multiplexer_5 (
    .in0(multiplexer_4_out), .in1(JRPC), .out(multiplexer_5_out), .sel(JR));
  or or_2 (IR1_t, IR1, IRA);
  Counter #(.width(16), .max('hffff), .ongoal("wrap"), .trigger("rising"), .behavior("old")) counter_1 (
    .D({16{1'b0}}), .count(or_1_out), .Q(\总周期数 ), .clk(CLK));  // open: load, carry, clr, preset
  Register #(.width(32), .trigger("rising"), .Select("low")) u_PC (
    .D(multiplexer_5_out), .en(or_1_out), .Q(PC), .clk(CLK));  // open: clr
  and and_1 (equal, Syscall, comparator_1_eq);
  and and_2 (stop, Syscall, not_2_out);
  not not_2 (not_2_out, comparator_1_eq);
  or or_3 (IR2_t, IR2, IRB);
  Adder #(.width(32)) adder_1 (.a(PC), .b(32'h4), .out(PC_4));  // open: cin, cout
  Priority_Encoder #(.select(2), .disabled("Z")) priority_encoder_1 (
    .in0(1'b1), .in1(ex1), .in2(ex2), .in3(ex3), .out(priority_encoder_1_out));  // open: gs, en_out, en_in
  not not_3 (not_3_out, IE);
  ROM #(.addrWidth(10), .dataWidth(32), .Select("high")) rom_1 (.addr(PC[11:2]), .data(IR));
  Register #(.width(2), .trigger("rising"), .Select("low")) IM (
    .D(priority_encoder_1_out), .en(not_3_out), .Q(xy_t), .clk(CLK));  // open: clr
  or or_4 (IR3_t, IR3, IRC);
  Multiplexer #(.select(1), .width(32), .disabled("Z"), .enable("false")) multiplexer_6 (
    .in1(MDin), .out(multiplexer_6_out), .sel(equal));  // open: in0
  // Probe on MDin
  Decoder #(.select(2), .tristate("false"), .disabled("Z"), .enable("false")) decoder_1 (
    .out1(decoder_1_out1), .out2(decoder_1_out2), .out3(decoder_1_out3), .sel(xy_t));  // open: out0
  Register #(.width(32), .trigger("rising"), .Select("low")) register_1 (
    .D(multiplexer_6_out), .Q(LedData), .clk(CLK));  // open: en, clr
  \单周期硬布线控制器  \u_单周期硬布线控制器_1  (
    .Func(IR[5:0]), .OP(IR[31:26]), .ALU_OP(\单周期硬布线控制器_1_alu_op ), .MemToReg(\单周期硬布线控制器_1_memtoreg ),
    .MemWrite(MemWrite), .ALU_SRC(\单周期硬布线控制器_1_alu_src ), .RegWrite(RegWrite), .SysCALL(Syscall),
    .SignedExt(SignedExt), .RegDst(\单周期硬布线控制器_1_regdst ), .JR(JR), .JMP(JMP), .Beq(Beq), .JAL(JAL),
    .Bne(Bne), .SRLV(SRLV), .LBU(LBU), .BGTZ(BGTZ));
  Multiplexer #(.select(1), .width(5), .disabled("Z"), .enable("false")) multiplexer_7 (
    .in0(IR[20:16]), .in1(IR[15:11]), .out(multiplexer_7_out), .sel(\单周期硬布线控制器_1_regdst ));
  Multiplexer #(.select(1), .width(5), .disabled("Z"), .enable("false")) multiplexer_8 (
    .in0(multiplexer_7_out), .in1({5{1'b1}}), .out(multiplexer_8_out), .sel(JAL));
  assign bit_extender_1_out = {{6{1'b0}}, IR[25:0]};  // Bit_Extender bit_extender_1
  assign bit_extender_2_out = {{16{1'b0}}, IR[15:0]};  // Bit_Extender bit_extender_2
  assign bit_extender_3_out = {{16{IR[15]}}, IR[15:0]};  // Bit_Extender bit_extender_3
  and and_3 (rst1, ERET, decoder_1_out1);
  and and_4 (rst2, decoder_1_out2, ERET);
  and and_5 (rst3, decoder_1_out3, ERET);
  Comparator #(.width(2), .mode("twosComplement")) comparator_2 (
    .a(XY), .b(2'b01), .eq(comparator_2_eq));  // open: gt, lt
  Comparator #(.width(2), .mode("twosComplement")) comparator_3 (
    .a(XY), .b(2'b10), .eq(comparator_3_eq));  // open: gt, lt
  Comparator #(.width(2), .mode("twosComplement")) comparator_4 (
    .a(XY), .b(2'b11), .eq(comparator_4_eq));  // open: gt, lt
  or or_5 (branch, and_6_out, and_10_out, and_11_out);
  Multiplexer #(.select(1), .width(5), .disabled("Z"), .enable("false")) multiplexer_9 (
    .in0(IR[25:21]), .in1(5'b00010), .out(multiplexer_9_out), .sel(Syscall));
  Multiplexer #(.select(1), .width(5), .disabled("Z"), .enable("false")) multiplexer_10 (
    .in0(IR[20:16]), .in1(5'b00100), .out(multiplexer_10_out), .sel(Syscall));
  or or_6 (or_6_out, rst1, comparator_2_eq);
  or or_7 (or_7_out, rst2, comparator_3_eq);
  or or_8 (or_8_out, rst3, comparator_4_eq);
  MIPS_Regifile mips_regifile_1 (
    .Din(RDin), .Clk(CLK), .R1(JRPC), .R2(MDin), .WE(RegWrite), .W_num(multiplexer_8_out),
    .R1_num(multiplexer_9_out), .R2_num(multiplexer_10_out));
  Shifter #(.width(32), .shift("ll")) shifter_1 (.in(bit_extender_1_out), .\dist (5'b00010), .out(shifter_1_out));
  assign JPC = shifter_1_out | {PC_4[31:28], {28{1'b0}}};  // OR_Gate or_9, 32 bits wide
  Multiplexer #(.select(1), .width(32), .disabled("Z"), .enable("false")) multiplexer_11 (
    .in0(bit_extender_2_out), .in1(bit_extender_3_out), .out(multiplexer_11_out), .sel(SignedExt));
  Shifter #(.width(32), .shift("ll")) shifter_2 (.in(bit_extender_3_out), .\dist (5'b00010), .out(shifter_2_out));
  and and_6 (and_6_out, Bne, not_4_out);
  not not_4 (not_4_out, mips_alu_1_equal);
  Multiplexer #(.select(1), .width(32), .disabled("Z"), .enable("false")) multiplexer_12 (
    .in0(MDin), .in1(multiplexer_11_out), .out(multiplexer_12_out), .sel(\单周期硬布线控制器_1_alu_src ));
  Adder #(.width(32)) adder_2 (.a(shifter_2_out), .b(PC_4), .out(adder_2_out));  // open: cin, cout
  Counter #(.width(16), .max('hffff), .ongoal("wrap"), .trigger("rising"), .behavior("old")) counter_2 (
    .D({16{1'b0}}), .count(JMP), .Q(\无条件 ), .clk(CLK));  // open: load, carry, clr, preset
  D_Flip_Flop #(.trigger("rising"), .Pre_Clr_Positions("LEGACY"), .NegatePresetClear("false"), .enable("true"), .NewFFLayout("false")) d_ff_1 (
    .clk(IR1_t), .D(1'b1), .Q(d_ff_1_q), .reset(ex1));  // open: Qn, preset, en
  or or_10 (W1, ex1, d_ff_1_q);
  D_Flip_Flop #(.trigger("rising"), .Pre_Clr_Positions("LEGACY"), .NegatePresetClear("false"), .enable("true"), .NewFFLayout("false")) d_ff_2 (
    .clk(IR2_t), .D(1'b1), .Q(d_ff_2_q), .reset(ex2));  // open: Qn, preset, en
  or or_11 (W2, ex2, d_ff_2_q);
  D_Flip_Flop #(.trigger("rising"), .Pre_Clr_Positions("LEGACY"), .NegatePresetClear("false"), .enable("true"), .NewFFLayout("false")) d_ff_3 (
    .clk(IR3_t), .D(1'b1), .Q(d_ff_3_q), .reset(ex3));  // open: Qn, preset, en
  or or_12 (W3, ex3, d_ff_3_q);
  and and_7 (and_7_out, ex1, ~rst1, comparator_5_eq);  // AND_Gate
  Comparator #(.width(2), .mode("twosComplement")) comparator_5 (
    .a(xy_t), .b(2'b01), .eq(comparator_5_eq));  // open: gt, lt
  and and_8 (and_8_out, ex2, ~rst2, comparator_6_eq);  // AND_Gate
  Comparator #(.width(2), .mode("twosComplement")) comparator_6 (
    .a(xy_t), .b(2'b10), .eq(comparator_6_eq));  // open: gt, lt
  and and_9 (and_9_out, ex3, ~rst3, comparator_7_eq);  // AND_Gate
  Comparator #(.width(2), .mode("twosComplement")) comparator_7 (
    .a(xy_t), .b(2'b11), .eq(comparator_7_eq));  // open: gt, lt
  Multiplexer #(.select(1), .width(32), .disabled("Z"), .enable("false")) multiplexer_13 (
    .in0(JRPC), .in1(multiplexer_12_out), .out(multiplexer_13_out), .sel(SRLV));
  // Probe on \无条件 
  and and_10 (and_10_out, not_6_out, not_5_out, BGTZ);
  and and_11 (and_11_out, Beq, mips_alu_1_equal);
  not not_5 (not_5_out, mips_alu_1_equal);
  not not_6 (not_6_out, mips_alu_1_result[0]);
  MIPS_ALU mips_alu_1 (
    .X(multiplexer_13_out), .Y(multiplexer_12_out), .AluOP(\单周期硬布线控制器_1_alu_op ), .Equal(mips_alu_1_equal),
    .Result(mips_alu_1_result), .shamt(multiplexer_14_out));  // open: Result_2
  Multiplexer #(.select(1), .width(5), .disabled("Z"), .enable("false")) multiplexer_14 (
    .in0(IR[10:6]), .in1(JRPC[4:0]), .out(multiplexer_14_out), .sel(SRLV));
  Multiplexer #(.select(1), .width(32), .disabled("Z"), .enable("false")) multiplexer_15 (
    .in0(multiplexer_17_out), .in1(PC_4), .out(RDin), .sel(JAL));
  or or_13 (or_13_out, d_ff_1_q, ex1);
  and and_12 (and_12_out, or_13_out, ~rst1);  // AND_Gate
  or or_14 (or_14_out, d_ff_2_q, ex2);
  and and_13 (and_13_out, or_14_out, ~rst2);  // AND_Gate
  or or_15 (or_15_out, d_ff_3_q, ex3);
  and and_14 (and_14_out, or_15_out, ~rst3);  // AND_Gate
  Register #(.width(1), .trigger("rising"), .Select("low")) IM_2 (
    .D(and_7_out), .en(or_6_out), .Q(flag1), .clk(CLK));  // open: clr
  Register #(.width(1), .trigger("rising"), .Select("low")) IM_3 (
    .D(and_8_out), .en(or_7_out), .Q(flag2), .clk(CLK));  // open: clr
  Register #(.width(1), .trigger("rising"), .Select("low")) IM_4 (
    .D(and_9_out), .en(or_8_out), .Q(flag3), .clk(CLK));  // open: clr
  Counter #(.width(16), .max('hffff), .ongoal("wrap"), .trigger("rising"), .behavior("old")) counter_3 (
    .D({16{1'b0}}), .count(branch), .Q(\有条件 ), .clk(CLK));  // open: load, carry, clr, preset
  // Probe on \有条件 
  D_Flip_Flop #(.trigger("rising"), .Pre_Clr_Positions("LEGACY"), .NegatePresetClear("false"), .enable("true"), .NewFFLayout("false")) u_IR1 (
    .clk(CLK), .D(and_12_out), .Q(ex1));  // open: Qn, preset, en, reset
  D_Flip_Flop #(.trigger("rising"), .Pre_Clr_Positions("LEGACY"), .NegatePresetClear("false"), .enable("true"), .NewFFLayout("false")) u_IR2 (
    .clk(CLK), .D(and_13_out), .Q(ex2));  // open: Qn, preset, en, reset
  D_Flip_Flop #(.trigger("rising"), .Pre_Clr_Positions("LEGACY"), .NegatePresetClear("false"), .enable("true"), .NewFFLayout("false")) u_IR3 (
    .clk(CLK), .D(and_14_out), .Q(ex3));  // open: Qn, preset, en, reset
  RAM #(.addrWidth(10), .dataWidth(32), .bus("separate"), .Select("high")) ram_1 (
    .addr(mips_alu_1_result[11:2]), .din(MDin), .data(ram_1_data), .str(MemWrite), .sel(1'b1), .clk(CLK));  // open: ld, clr
  Multiplexer #(.select(1), .width(32), .disabled("Z"), .enable("false")) multiplexer_16 (
    .in0(mips_alu_1_result), .in1(ram_1_data), .out(multiplexer_16_out), .sel(\单周期硬布线控制器_1_memtoreg ));
  Shifter #(.width(32), .shift("ll")) shifter_3 (
    .in(32'hff), .\dist ({mips_alu_1_result[1:0], 3'b000}), .out(shifter_3_out));
  assign and_15_out = multiplexer_16_out & shifter_3_out;  // AND_Gate and_15, 32 bits wide
  Shifter #(.width(32), .shift("lr")) shifter_4 (
    .in(and_15_out), .\dist ({mips_alu_1_result[1:0], 3'b000}), .out(shifter_4_out));
  or or_16 (or_16_out, ERET, \CPU中断请求 );
  Counter #(.width(2), .max('h3), .ongoal("wrap"), .trigger("rising"), .behavior("new")) counter_4 (
    .D(2'b00), .count(or_16_out), .Q(counter_4_q), .clk(CLK), .down(ERET));  // open: load, carry, clr, preset
  and and_16 (and_16_out, ~flag1, ~flag2, ~flag3, ex1);  // AND_Gate
  and and_17 (and_17_out, ~flag2, ~flag3, ex2);  // AND_Gate
  and and_18 (and_18_out, ~flag3, ex3);  // AND_Gate
  Comparator #(.width(6), .mode("twosComplement")) comparator_8 (
    .a(IR[31:26]), .b(6'b010000), .eq(comparator_8_eq));  // open: gt, lt
  Comparator #(.width(6), .mode("twosComplement")) comparator_9 (
    .a(IR[5:0]), .b(6'b011000), .eq(comparator_9_eq));  // open: gt, lt
  Comparator #(.width(5), .mode("twosComplement")) comparator_10 (
    .a(IR[25:21]), .b(5'b00100), .eq(comparator_10_eq));  // open: gt, lt
  Comparator #(.width(5), .mode("twosComplement")) comparator_11 (
    .a(IR[25:21]), .b({5{1'b0}}), .eq(comparator_11_eq));  // open: gt, lt
  Multiplexer #(.select(1), .width(32), .disabled("Z"), .enable("false")) multiplexer_17 (
    .in0(multiplexer_16_out), .in1(shifter_4_out), .out(multiplexer_17_out), .sel(LBU));
  Comparator #(.width(2), .mode("unsigned")) comparator_12 (
    .a(2'b00), .b(counter_4_q), .eq(comparator_12_eq));  // open: gt, lt
  Comparator #(.width(2), .mode("unsigned")) comparator_13 (
    .a(2'b01), .b(counter_4_q), .eq(comparator_13_eq));  // open: gt, lt
  Comparator #(.width(2), .mode("unsigned")) comparator_14 (
    .a(counter_4_q), .b(2'b10), .eq(comparator_14_eq));  // open: gt, lt
  and and_19 (ERET, comparator_8_eq, comparator_9_eq);
  and and_20 (MTC0, comparator_8_eq, comparator_10_eq);
  and and_21 (MFC0, comparator_8_eq, comparator_11_eq);
  Priority_Encoder #(.select(2), .disabled("Z")) priority_encoder_2 (
    .in0(1'b1), .in1(and_16_out), .in2(and_17_out), .in3(and_18_out), .out(XY));  // open: gs, en_out, en_in
  and and_22 (and_22_out, \CPU中断请求 , comparator_12_eq);
  and and_23 (and_23_out, \CPU中断请求 , comparator_13_eq);
  and and_24 (and_24_out, \CPU中断请求 , comparator_14_eq);
  Multiplexer #(.select(2), .width(32), .disabled("Z"), .enable("false")) multiplexer_18 (
    .in0(EPC), .in1(32'h30ac), .in2(32'h3158), .in3(32'h3204), .out(PC_OUT), .sel(XY));
  Multiplexer #(.select(1), .width(32), .disabled("Z"), .enable("false")) multiplexer_19 (
    .in0(PC_4), .in1(adder_2_out), .out(multiplexer_19_out), .sel(branch));
  Register #(.width(32), .trigger("rising"), .Select("low")) u_EPC (
    .D(multiplexer_21_out), .en(and_22_out), .Q(EPC_q), .clk(CLK));  // open: clr
  Register #(.width(32), .trigger("rising"), .Select("low")) EPC_2 (
    .D(multiplexer_21_out), .en(and_23_out), .Q(EPC_2_q), .clk(CLK));  // open: clr
  Register #(.width(32), .trigger("rising"), .Select("low")) EPC_3 (
    .D(multiplexer_21_out), .en(and_24_out), .Q(EPC_3_q), .clk(CLK));  // open: clr
  Register #(.width(1), .trigger("rising"), .Select("low")) u_IE (
    .D(and_26_out), .en(or_17_out), .Q(IE), .clk(CLK), .preset(MTC0));  // open: clr, cs
  or or_17 (or_17_out, not_7_out, MFC0, ERET, MTC0);
  Multiplexer #(.select(1), .width(32), .disabled("Z"), .enable("false")) multiplexer_20 (
    .in0(multiplexer_19_out), .in1(JPC), .out(multiplexer_20_out), .sel(JMP));
  // Probe on XY
  and and_25 (\CPU中断请求 , not_8_out, ~IE);  // AND_Gate
  and and_26 (and_26_out, \CPU中断请求 , and_27_out);
  not not_7 (not_7_out, IE);
  Multiplexer #(.select(1), .width(32), .disabled("Z"), .enable("false")) multiplexer_21 (
    .in0(multiplexer_20_out), .in1(JRPC), .out(multiplexer_21_out), .sel(JR));
  Multiplexer #(.select(2), .width(32), .disabled("Z"), .enable("false")) multiplexer_22 (
    .in1(EPC_q), .in2(EPC_2_q), .in3(EPC_3_q), .out(EPC), .sel(counter_4_q));  // open: in0
  Comparator #(.width(2), .mode("unsigned")) comparator_15 (.a(XY), .b(2'b00), .eq(comparator_15_eq));  // open: gt, lt
  not not_8 (not_8_out, comparator_15_eq);
  and and_27 (and_27_out, ~or_18_out, 1'b1);  // AND_Gate
  or or_18 (or_18_out, ERET, MFC0);

  // Other names for the same wires on the sheet: a0[31:0] = MDin; v0[31:0] = JRPC

  // Notes on the sheet:
  //   中断源
  //   中断等待指示
  //   数码管输出
  //   指令存储器
  //   contents of rom_1 (hex, n*v repeats v):
  //   201d07d0 20100001 109fc0 139fc3 8021 2012000c 24160008 26100001 3210000f 20080008 20090001 139900
  //   2709825 132020 20020022 c 1094022 1500fff9 22100001 2018000f 2188024 108700 20080008 20090001 139902
  //   2709825 132021 20020022 c 1094022 1500fff9 108702 2c9b022 12c00001 8000c07 4020 1084027 84400
  //   3508ffff 82021 20020022 c 8000c01 afa20000 23bd0004 afa40000 23bd0004 afb00000 23bd0004 afb30000
  //   23bd0004 afb40000 23bd0004 afb50000 23bd0004 afb60000 23bd0004 40000000 20160001 20140003 20150001
  //   168020 108100 2149825 132020 20020022 c 1600fffa 295a022 1680fff7 40800000 23bdfffc 8fb60000
  //   23bdfffc 8fb50000 23bdfffc 8fb40000 23bdfffc 8fb30000 23bdfffc 8fb00000 23bdfffc 8fa40000 23bdfffc
  //   8fa20000 42000018 afa20000 23bd0004 afa40000 23bd0004 afb00000 23bd0004 afb30000 23bd0004 afb40000
  //   23bd0004 afb50000 23bd0004 afb60000 23bd0004 40000000 20160002 20140003 20150001 168020 108100
  //   2149825 132020 20020022 c 1600fffa 295a022 1680fff7 40800000 23bdfffc 8fb60000 23bdfffc 8fb50000
  //   23bdfffc 8fb40000 23bdfffc 8fb30000 23bdfffc 8fb00000 23bdfffc 8fa40000 23bdfffc 8fa20000 42000018
  //   afa20000 23bd0004 afa40000 23bd0004 afb00000 23bd0004 afb30000 23bd0004 afb40000 23bd0004 afb50000
  //   23bd0004 afb60000 23bd0004 40000000 20160003 20140003 20150001 168020 108100 2149825 132020 20020022
  //   c 1600fffa 295a022 1680fff7 40800000 23bdfffc 8fb60000 23bdfffc 8fb50000 23bdfffc 8fb40000 23bdfffc
  //   8fb30000 23bdfffc 8fb00000 23bdfffc 8fa40000 23bdfffc 8fa20000 42000018
  //   OP
  //   Func
  //   rs
  //   指令字
  //   rt
  //   rd
  //   JMP
  //   JR
  //   OP
  //   Func
  //   Syscall
  //   Beq
  //   Bne
  //   MemToReg
  //   MemWrite
  //   AluOP
  //   AluSrcB
  //   RegWrite
  //   JAL
  //   RegDst
  //   为方便自动评测，需要输出PC，IR，寄存器堆写如数据RDin
  //   RAM写使能MemWrite、RAM写入数据MDin等信号
  //   Reset 
  //   Reset 
  //   Reset 
endmodule

module \IF_取指令  (
  input  [31:0] IR,
  input  [31:0] PC,
  input  CLK,
  input  \同步清零_高电平有效 ,
  input  \使能端_低电平有效 ,
  output [31:0] IR_prime,
  output [31:0] PC_prime
);

  wire pull_resistor_2_node;
  wire [31:0] multiplexer_1_out, multiplexer_2_out;

  Multiplexer #(.select(1), .width(32), .disabled("Z"), .enable("false")) multiplexer_1 (
    .in0(IR), .in1({32{1'b0}}), .out(multiplexer_1_out), .sel(\同步清零_高电平有效 ));
  Multiplexer #(.select(1), .width(32), .disabled("Z"), .enable("false")) multiplexer_2 (
    .in0(PC), .in1({32{1'b0}}), .out(multiplexer_2_out), .sel(\同步清零_高电平有效 ));
  Pull_Resistor #(.pull(0)) pull_resistor_1 (.node(\同步清零_高电平有效 ));
  Pull_Resistor #(.pull(0)) pull_resistor_2 (.node(pull_resistor_2_node));
  not not_1 (pull_resistor_2_node, \使能端_低电平有效 );
  Register #(.width(32), .trigger("rising"), .Select("low")) register_1 (
    .D(multiplexer_1_out), .en(pull_resistor_2_node), .Q(IR_prime), .clk(CLK));  // open: clr
  Register #(.width(32), .trigger("rising"), .Select("low")) register_2 (
    .D(multiplexer_2_out), .en(pull_resistor_2_node), .Q(PC_prime), .clk(CLK));  // open: clr

  // Notes on the sheet:
  //   使能端_低电平有效: pull=down
  //   同步清零_高电平有效: pull=down
  //   下拉电阻使得引脚可以悬空
endmodule

module \ID_译码  (
  input  RegDst,
  input  MemToReg,
  input  RegWirte,
  input  MemWrite,
  input  ALUSRCB,
  input  [3:0] ALUOP,
  input  [31:0] IR,
  input  [31:0] PC,
  input  [31:0] A,
  input  [31:0] B,
  input  [31:0] Imm,
  input  CLK,
  input  \同步清零_高电平有效 ,
  input  \使能端_低电平有效 ,
  output RegDst_prime,
  output MemToReg_prime,
  output RegWrite_prime,
  output MemWrite_prime,
  output ALUSRCB_prime,
  output [3:0] ALUOP_prime,
  output [31:0] IR_prime,
  output [31:0] PC_prime,
  output [31:0] A_prime,
  output [31:0] B_prime,
  output [31:0] Imm_prime
);

  wire multiplexer_1_out, multiplexer_2_out, multiplexer_3_out, multiplexer_4_out, multiplexer_5_out,
       pull_resistor_2_node;
  wire [3:0] multiplexer_6_out;
  wire [31:0] multiplexer_7_out, multiplexer_8_out, multiplexer_9_out, multiplexer_10_out, multiplexer_11_out;

  Multiplexer #(.select(1), .width(1), .disabled("Z"), .enable("false")) multiplexer_1 (
    .in0(RegDst), .in1(1'b0), .out(multiplexer_1_out), .sel(\同步清零_高电平有效 ));
  Multiplexer #(.select(1), .width(1), .disabled("Z"), .enable("false")) multiplexer_2 (
    .in0(MemToReg), .in1(1'b0), .out(multiplexer_2_out), .sel(\同步清零_高电平有效 ));
  Multiplexer #(.select(1), .width(1), .disabled("Z"), .enable("false")) multiplexer_3 (
    .in0(RegWirte), .in1(1'b0), .out(multiplexer_3_out), .sel(\同步清零_高电平有效 ));
  Multiplexer #(.select(1), .width(1), .disabled("Z"), .enable("false")) multiplexer_4 (
    .in0(MemWrite), .in1(1'b0), .out(multiplexer_4_out), .sel(\同步清零_高电平有效 ));
  Multiplexer #(.select(1), .width(1), .disabled("Z"), .enable("false")) multiplexer_5 (
    .in0(ALUSRCB), .in1(1'b0), .out(multiplexer_5_out), .sel(\同步清零_高电平有效 ));
  Multiplexer #(.select(1), .width(4), .disabled("Z"), .enable("false")) multiplexer_6 (
    .in0(ALUOP), .in1(4'b0000), .out(multiplexer_6_out), .sel(\同步清零_高电平有效 ));
  Multiplexer #(.select(1), .width(32), .disabled("Z"), .enable("false")) multiplexer_7 (
    .in0(IR), .in1({32{1'b0}}), .out(multiplexer_7_out), .sel(\同步清零_高电平有效 ));
  Multiplexer #(.select(1), .width(32), .disabled("Z"), .enable("false")) multiplexer_8 (
    .in0(PC), .in1({32{1'b0}}), .out(multiplexer_8_out), .sel(\同步清零_高电平有效 ));
  Multiplexer #(.select(1), .width(32), .disabled("Z"), .enable("false")) multiplexer_9 (
    .in0(A), .in1({32{1'b0}}), .out(multiplexer_9_out), .sel(\同步清零_高电平有效 ));
  Multiplexer #(.select(1), .width(32), .disabled("Z"), .enable("false")) multiplexer_10 (
    .in0(B), .in1({32{1'b0}}), .out(multiplexer_10_out), .sel(\同步清零_高电平有效 ));
  Multiplexer #(.select(1), .width(32), .disabled("Z"), .enable("false")) multiplexer_11 (
    .in0(Imm), .in1({32{1'b0}}), .out(multiplexer_11_out), .sel(\同步清零_高电平有效 ));
  Pull_Resistor #(.pull(0)) pull_resistor_1 (.node(\同步清零_高电平有效 ));
  Register #(.width(1), .trigger("rising"), .Select("low")) register_1 (
    .D(multiplexer_1_out), .en(pull_resistor_2_node), .Q(RegDst_prime), .clk(CLK));  // open: clr
  Register #(.width(1), .trigger("rising"), .Select("low")) register_2 (
    .D(multiplexer_2_out), .en(pull_resistor_2_node), .Q(MemToReg_prime), .clk(CLK));  // open: clr
  Register #(.width(1), .trigger("rising"), .Select("low")) register_3 (
    .D(multiplexer_3_out), .en(pull_resistor_2_node), .Q(RegWrite_prime), .clk(CLK));  // open: clr
  Register #(.width(1), .trigger("rising"), .Select("low")) register_4 (
    .D(multiplexer_4_out), .en(pull_resistor_2_node), .Q(MemWrite_prime), .clk(CLK));  // open: clr
  Register #(.width(1), .trigger("rising"), .Select("low")) register_5 (
    .D(multiplexer_5_out), .en(pull_resistor_2_node), .Q(ALUSRCB_prime), .clk(CLK));  // open: clr
  Register #(.width(4), .trigger("rising"), .Select("low")) register_6 (
    .D(multiplexer_6_out), .en(pull_resistor_2_node), .Q(ALUOP_prime), .clk(CLK));  // open: clr
  Register #(.width(32), .trigger("rising"), .Select("low")) register_7 (
    .D(multiplexer_7_out), .en(pull_resistor_2_node), .Q(IR_prime), .clk(CLK));  // open: clr
  Register #(.width(32), .trigger("rising"), .Select("low")) register_8 (
    .D(multiplexer_8_out), .en(pull_resistor_2_node), .Q(PC_prime), .clk(CLK));  // open: clr
  Register #(.width(32), .trigger("rising"), .Select("low")) register_9 (
    .D(multiplexer_9_out), .en(pull_resistor_2_node), .Q(A_prime), .clk(CLK));  // open: clr
  Register #(.width(32), .trigger("rising"), .Select("low")) register_10 (
    .D(multiplexer_10_out), .en(pull_resistor_2_node), .Q(B_prime), .clk(CLK));  // open: clr
  Register #(.width(32), .trigger("rising"), .Select("low")) register_11 (
    .D(multiplexer_11_out), .en(pull_resistor_2_node), .Q(Imm_prime), .clk(CLK));  // open: clr
  Pull_Resistor #(.pull(0)) pull_resistor_2 (.node(pull_resistor_2_node));
  not not_1 (pull_resistor_2_node, \使能端_低电平有效 );

  // Notes on the sheet:
  //   同步清零_高电平有效: pull=down
  //   使能端_低电平有效: pull=down
  //   下拉电阻使得引脚可以悬空
endmodule

module \EX_执行  (
  input  RegDst,
  input  MemToReg,
  input  RegWirte,
  input  MemWrite,
  input  [31:0] IR,
  input  [31:0] PC,
  input  [31:0] B,
  input  [31:0] ALU,
  input  CLK,
  input  \同步清零_高电平有效 ,
  input  \使能端_低电平有效 ,
  output RegDst_prime,
  output MemToReg_prime,
  output RegWrite_prime,
  output MemWrite_prime,
  output [31:0] IR_prime,
  output [31:0] PC_prime,
  output [31:0] B_prime,
  output [31:0] ALU_prime
);

  wire multiplexer_1_out, multiplexer_2_out, multiplexer_3_out, multiplexer_4_out, pull_resistor_2_node;
  wire [31:0] multiplexer_5_out, multiplexer_6_out, multiplexer_7_out, multiplexer_8_out;

  Multiplexer #(.select(1), .width(1), .disabled("Z"), .enable("false")) multiplexer_1 (
    .in0(RegDst), .in1(1'b0), .out(multiplexer_1_out), .sel(\同步清零_高电平有效 ));
  Multiplexer #(.select(1), .width(1), .disabled("Z"), .enable("false")) multiplexer_2 (
    .in0(MemToReg), .in1(1'b0), .out(multiplexer_2_out), .sel(\同步清零_高电平有效 ));
  Multiplexer #(.select(1), .width(1), .disabled("Z"), .enable("false")) multiplexer_3 (
    .in0(RegWirte), .in1(1'b0), .out(multiplexer_3_out), .sel(\同步清零_高电平有效 ));
  Multiplexer #(.select(1), .width(1), .disabled("Z"), .enable("false")) multiplexer_4 (
    .in0(MemWrite), .in1(1'b0), .out(multiplexer_4_out), .sel(\同步清零_高电平有效 ));
  Multiplexer #(.select(1), .width(32), .disabled("Z"), .enable("false")) multiplexer_5 (
    .in0(IR), .in1({32{1'b0}}), .out(multiplexer_5_out), .sel(\同步清零_高电平有效 ));
  Multiplexer #(.select(1), .width(32), .disabled("Z"), .enable("false")) multiplexer_6 (
    .in0(PC), .in1({32{1'b0}}), .out(multiplexer_6_out), .sel(\同步清零_高电平有效 ));
  Multiplexer #(.select(1), .width(32), .disabled("Z"), .enable("false")) multiplexer_7 (
    .in0(B), .in1({32{1'b0}}), .out(multiplexer_7_out), .sel(\同步清零_高电平有效 ));
  Multiplexer #(.select(1), .width(32), .disabled("Z"), .enable("false")) multiplexer_8 (
    .in0(ALU), .in1({32{1'b0}}), .out(multiplexer_8_out), .sel(\同步清零_高电平有效 ));
  Pull_Resistor #(.pull(0)) pull_resistor_1 (.node(\同步清零_高电平有效 ));
  Register #(.width(1), .trigger("rising"), .Select("low")) register_1 (
    .D(multiplexer_1_out), .en(pull_resistor_2_node), .Q(RegDst_prime), .clk(CLK));  // open: clr
  Register #(.width(1), .trigger("rising"), .Select("low")) register_2 (
    .D(multiplexer_2_out), .en(pull_resistor_2_node), .Q(MemToReg_prime), .clk(CLK));  // open: clr
  Register #(.width(1), .trigger("rising"), .Select("low")) register_3 (
    .D(multiplexer_3_out), .en(pull_resistor_2_node), .Q(RegWrite_prime), .clk(CLK));  // open: clr
  Register #(.width(1), .trigger("rising"), .Select("low")) register_4 (
    .D(multiplexer_4_out), .en(pull_resistor_2_node), .Q(MemWrite_prime), .clk(CLK));  // open: clr
  Register #(.width(32), .trigger("rising"), .Select("low")) register_5 (
    .D(multiplexer_5_out), .en(pull_resistor_2_node), .Q(IR_prime), .clk(CLK));  // open: clr
  Register #(.width(32), .trigger("rising"), .Select("low")) register_6 (
    .D(multiplexer_6_out), .en(pull_resistor_2_node), .Q(PC_prime), .clk(CLK));  // open: clr
  Register #(.width(32), .trigger("rising"), .Select("low")) register_7 (
    .D(multiplexer_7_out), .en(pull_resistor_2_node), .Q(B_prime), .clk(CLK));  // open: clr
  Register #(.width(32), .trigger("rising"), .Select("low")) register_8 (
    .D(multiplexer_8_out), .en(pull_resistor_2_node), .Q(ALU_prime), .clk(CLK));  // open: clr
  Pull_Resistor #(.pull(0)) pull_resistor_2 (.node(pull_resistor_2_node));
  not not_1 (pull_resistor_2_node, \使能端_低电平有效 );

  // Notes on the sheet:
  //   同步清零_高电平有效: pull=down
  //   使能端_低电平有效: pull=down
  //   下拉电阻使得引脚可以悬空
endmodule

module \MEM_访存  (
  input  RegDst,
  input  MemToReg,
  input  RegWirte,
  input  [31:0] IR,
  input  [31:0] PC,
  input  [31:0] ALU,
  input  [31:0] MD,
  input  CLK,
  input  \同步清零_高电平有效 ,
  input  \使能端_低电平有效 ,
  output MemToReg_prime,
  output MemToReg_prime_2,
  output RegWrite_prime,
  output [31:0] IR_prime,
  output [31:0] PC_prime,
  output [31:0] ALU_prime,
  output [31:0] MD_prime
);

  wire multiplexer_1_out, multiplexer_2_out, multiplexer_3_out, pull_resistor_2_node;
  wire [31:0] multiplexer_4_out, multiplexer_5_out, multiplexer_6_out, multiplexer_7_out;

  Multiplexer #(.select(1), .width(1), .disabled("Z"), .enable("false")) multiplexer_1 (
    .in0(RegDst), .in1(1'b0), .out(multiplexer_1_out), .sel(\同步清零_高电平有效 ));
  Multiplexer #(.select(1), .width(1), .disabled("Z"), .enable("false")) multiplexer_2 (
    .in0(MemToReg), .in1(1'b0), .out(multiplexer_2_out), .sel(\同步清零_高电平有效 ));
  Multiplexer #(.select(1), .width(1), .disabled("Z"), .enable("false")) multiplexer_3 (
    .in0(RegWirte), .in1(1'b0), .out(multiplexer_3_out), .sel(\同步清零_高电平有效 ));
  Multiplexer #(.select(1), .width(32), .disabled("Z"), .enable("false")) multiplexer_4 (
    .in0(IR), .in1({32{1'b0}}), .out(multiplexer_4_out), .sel(\同步清零_高电平有效 ));
  Multiplexer #(.select(1), .width(32), .disabled("Z"), .enable("false")) multiplexer_5 (
    .in0(PC), .in1({32{1'b0}}), .out(multiplexer_5_out), .sel(\同步清零_高电平有效 ));
  Multiplexer #(.select(1), .width(32), .disabled("Z"), .enable("false")) multiplexer_6 (
    .in0(ALU), .in1({32{1'b0}}), .out(multiplexer_6_out), .sel(\同步清零_高电平有效 ));
  Multiplexer #(.select(1), .width(32), .disabled("Z"), .enable("false")) multiplexer_7 (
    .in0(MD), .in1({32{1'b0}}), .out(multiplexer_7_out), .sel(\同步清零_高电平有效 ));
  Pull_Resistor #(.pull(0)) pull_resistor_1 (.node(\同步清零_高电平有效 ));
  Register #(.width(1), .trigger("rising"), .Select("low")) register_1 (
    .D(multiplexer_1_out), .en(pull_resistor_2_node), .Q(MemToReg_prime), .clk(CLK));  // open: clr
  Register #(.width(1), .trigger("rising"), .Select("low")) register_2 (
    .D(multiplexer_2_out), .en(pull_resistor_2_node), .Q(MemToReg_prime_2), .clk(CLK));  // open: clr
  Register #(.width(1), .trigger("rising"), .Select("low")) register_3 (
    .D(multiplexer_3_out), .en(pull_resistor_2_node), .Q(RegWrite_prime), .clk(CLK));  // open: clr
  Register #(.width(32), .trigger("rising"), .Select("low")) register_4 (
    .D(multiplexer_4_out), .en(pull_resistor_2_node), .Q(IR_prime), .clk(CLK));  // open: clr
  Register #(.width(32), .trigger("rising"), .Select("low")) register_5 (
    .D(multiplexer_5_out), .en(pull_resistor_2_node), .Q(PC_prime), .clk(CLK));  // open: clr
  Register #(.width(32), .trigger("rising"), .Select("low")) register_6 (
    .D(multiplexer_6_out), .en(pull_resistor_2_node), .Q(ALU_prime), .clk(CLK));  // open: clr
  Register #(.width(32), .trigger("rising"), .Select("low")) register_7 (
    .D(multiplexer_7_out), .en(pull_resistor_2_node), .Q(MD_prime), .clk(CLK));  // open: clr
  Pull_Resistor #(.pull(0)) pull_resistor_2 (.node(pull_resistor_2_node));
  not not_1 (pull_resistor_2_node, \使能端_低电平有效 );

  // Notes on the sheet:
  //   同步清零_高电平有效: pull=down
  //   使能端_低电平有效: pull=down
  //   下拉电阻使得引脚可以悬空
endmodule

module IF_ID (
  input  [1:0] status,
  input  hit,
  input  [31:0] \原PC ,
  input  [31:0] IR,
  input  [31:0] PC,
  input  CLK,
  input  \同步清零_高电平有效 ,
  input  \使能端_低电平有效 ,
  output [1:0] status_prime,
  output hit_prime,
  output [31:0] \原PC_prime ,
  output [31:0] IR_prime,
  output [31:0] PC_prime
);

  wire multiplexer_2_out, not_1_out;
  wire [1:0] multiplexer_1_out;
  wire [31:0] multiplexer_3_out, multiplexer_4_out, multiplexer_5_out;

  Multiplexer #(.select(1), .width(2), .disabled("Z"), .enable("false")) multiplexer_1 (
    .in0(status), .in1(2'b00), .out(multiplexer_1_out), .sel(\同步清零_高电平有效 ));
  Multiplexer #(.select(1), .width(1), .disabled("Z"), .enable("false")) multiplexer_2 (
    .in0(hit), .in1(1'b0), .out(multiplexer_2_out), .sel(\同步清零_高电平有效 ));
  Multiplexer #(.select(1), .width(32), .disabled("Z"), .enable("false")) multiplexer_3 (
    .in0(\原PC ), .in1({32{1'b0}}), .out(multiplexer_3_out), .sel(\同步清零_高电平有效 ));
  Multiplexer #(.select(1), .width(32), .disabled("Z"), .enable("false")) multiplexer_4 (
    .in0(IR), .in1({32{1'b0}}), .out(multiplexer_4_out), .sel(\同步清零_高电平有效 ));
  Multiplexer #(.select(1), .width(32), .disabled("Z"), .enable("false")) multiplexer_5 (
    .in0(PC), .in1({32{1'b0}}), .out(multiplexer_5_out), .sel(\同步清零_高电平有效 ));
  Pull_Resistor #(.pull(0)) pull_resistor_1 (.node(\同步清零_高电平有效 ));
  not not_1 (not_1_out, \使能端_低电平有效 );
  Register #(.width(2), .trigger("rising"), .Select("low")) register_1 (
    .D(multiplexer_1_out), .en(not_1_out), .Q(status_prime), .clk(CLK));  // open: clr
  Register #(.width(1), .trigger("rising"), .Select("low")) register_2 (
    .D(multiplexer_2_out), .en(not_1_out), .Q(hit_prime), .clk(CLK));  // open: clr
  Register #(.width(32), .trigger("rising"), .Select("low")) register_3 (
    .D(multiplexer_3_out), .en(not_1_out), .Q(\原PC_prime ), .clk(CLK));  // open: clr
  Register #(.width(32), .trigger("rising"), .Select("low")) register_4 (
    .D(multiplexer_4_out), .en(not_1_out), .Q(IR_prime), .clk(CLK));  // open: clr
  Register #(.width(32), .trigger("rising"), .Select("low")) register_5 (
    .D(multiplexer_5_out), .en(not_1_out), .Q(PC_prime), .clk(CLK));  // open: clr
  Pull_Resistor #(.pull(0)) pull_resistor_2 (.node(not_1_out));

  // Notes on the sheet:
  //   使能端_低电平有效: pull=down
  //   同步清零_高电平有效: pull=down
  //   下拉电阻使得引脚可以悬空
endmodule

module \分支流水线  (
  output RegWrite,
  output MemWrite,
  output [31:0] PC,
  output [31:0] IR,
  output [31:0] RDin,
  output [31:0] MDin
);

  wire ALUSRC, and_3_out, and_4_out, and_5_out, BEQ, beq_t, BGTZ, bgtz_t, BNE, bne_t, Branch, CLK,
       comparator_1_eq, equal, ex_mem_1_jal_prime, ex_mem_1_lbu_prime, ex_mem_1_memtoreg_prime,
       ex_mem_1_memwrite_prime, ex_mem_1_regdst_prime, ex_mem_1_regwrite_prime, Go, id_ex_1_alusrcb_prime,
       id_ex_1_jal_prime, id_ex_1_lbu_prime, id_ex_1_memtoreg_prime, id_ex_1_memwrite_prime,
       id_ex_1_regdst_prime, id_ex_1_regwrite_prime, id_ex_1_srlv_prime, IR1, IR2, IR3, JAL, JMP, jmp_t, JR,
       jr_t, LBU, mem_wb_1_jal_prime, mem_wb_1_lbu_prime, mem_wb_1_memtoreg_prime, mem_wb_1_regdst_prime,
       MemtoReg, mips_alu_1_equal, not_1_out, not_2_out, not_3_out, not_4_out, not_5_out, or_1_out, RegDst,
       Regwrite_t, regwrite_t_t, Sign, SRLV, stop, syscall, W1, W2, W3, \单周期硬布线控制器_1_syscall ;
  wire [3:0] ALUOP, id_ex_1_aluop_prime;
  wire [4:0] ex_mem_1_writereg_prime, id_ex_1_shamt_prime, id_ex_1_writereg_prime, multiplexer_5_out,
       multiplexer_8_out, multiplexer_9_out, multiplexer_12_out, multiplexer_13_out, multiplexer_16_out,
       WRITEREG;
  wire [15:0] imm16, \总周期数 , \插入气泡数 , \无条件 , \有条件 ;
  wire [27:0] id_ex_1_pc_prime;
  wire [31:0] a0, adder_2_out, and_6_out, bit_extender_1_out, bit_extender_2_out, ex_mem_1_a_prime,
       ex_mem_1_alu_prime, ex_mem_1_ir_prime, ex_mem_1_pc_prime, id_ex_1_b_prime, id_ex_1_imm16_prime,
       id_ex_1_imm26_prime, id_ex_1_ir_prime, if_id_1_pc_prime, IMM, imm26, IR_final, JPC, JRPC, LedData,
       mem_wb_1_alu_prime, mem_wb_1_md_prime, mem_wb_1_pc_prime, mips_alu_1_result, mips_regifile_1_r1,
       mips_regifile_1_r2, multiplexer_1_out, multiplexer_2_out, multiplexer_3_out, multiplexer_7_out,
       multiplexer_10_out, multiplexer_11_out, multiplexer_14_out, multiplexer_17_out, PC_q, ram_1_data,
       shifter_1_out, shifter_3_out, shifter_4_out, v0;
  wire [31:16] IR_NOW;
  wire [31:28] shifter_2_out;

  Clock #(.highDuration(1), .lowDuration(1)) clock_1 (.out(CLK));
  Button _1 (.out(IR1));
  Button _2 (.out(IR2));
  Button _3 (.out(IR3));
  Button \u_继续运行  (.out(Go));
  LED #(.active("true")) led_1 (.in(W1));
  LED #(.active("true")) led_2 (.in(W2));
  LED #(.active("true")) led_3 (.in(W3));
  Multiplexer #(.select(1), .width(32), .disabled("Z"), .enable("false")) multiplexer_1 (
    .in0(PC), .in1(adder_2_out), .out(multiplexer_1_out), .sel(Branch));
  Multiplexer #(.select(1), .width(32), .disabled("Z"), .enable("false")) multiplexer_2 (
    .in0(multiplexer_1_out), .in1(JPC), .out(multiplexer_2_out), .sel(JMP));
  Hex_Digit_Display hex_digit_display_1 (.value(LedData[31:28]));  // open: dp
  not not_1 (not_1_out, stop);
  not not_2 (not_2_out, stop);
  Multiplexer #(.select(1), .width(32), .disabled("Z"), .enable("false")) multiplexer_3 (
    .in0(multiplexer_2_out), .in1(JRPC), .out(multiplexer_3_out), .sel(JR));
  Hex_Digit_Display hex_digit_display_2 (.value(LedData[23:20]));  // open: dp
  Hex_Digit_Display hex_digit_display_3 (.value(LedData[27:24]));  // open: dp
  Counter #(.width(16), .max('hffff), .ongoal("wrap"), .trigger("rising"), .behavior("old")) counter_1 (
    .D({16{1'b0}}), .count(not_2_out), .Q(\总周期数 ), .clk(CLK));  // open: load, carry, clr, preset
  Register #(.width(32), .trigger("rising"), .Select("low")) u_PC (
    .D(multiplexer_3_out), .en(not_2_out), .Q(PC_q), .clk(CLK));  // open: clr
  Hex_Digit_Display hex_digit_display_4 (.value(LedData[15:12]));  // open: dp
  Hex_Digit_Display hex_digit_display_5 (.value(LedData[19:16]));  // open: dp
  Counter #(.width(16), .max('hffff), .ongoal("wrap"), .trigger("rising"), .behavior("old")) counter_2 (
    .D({16{1'b0}}), .count(not_1_out), .Q(\插入气泡数 ), .clk(CLK));  // open: load, carry, clr, preset
  Hex_Digit_Display hex_digit_display_6 (.value(LedData[11:8]));  // open: dp
  Hex_Digit_Display hex_digit_display_7 (.value(LedData[7:4]));  // open: dp
  // Probe on \插入气泡数 
  Hex_Digit_Display hex_digit_display_8 (.value(LedData[3:0]));  // open: dp
  // Probe on \总周期数 
  Adder #(.width(32)) adder_1 (.a(PC_q), .b(32'h4), .out(PC));  // open: cin, cout
  ROM #(.addrWidth(10), .dataWidth(32), .Select("high")) rom_1 (.addr(PC_q[11:2]), .data(IR));
  assign bit_extender_1_out = {{16{1'b0}}, imm16};  // Bit_Extender bit_extender_1
  assign bit_extender_2_out = {{16{imm16[15]}}, imm16};  // Bit_Extender bit_extender_2
  Comparator #(.width(32), .mode("twosComplement")) comparator_1 (
    .a(v0), .b(32'h22), .eq(comparator_1_eq));  // open: gt, lt
  or or_1 (or_1_out, JMP, Branch);
  IF_ID if_id_1 (
    .IR(IR), .PC(PC), .CLK(CLK), .IR_prime({IR_NOW, imm16}), .PC_prime(if_id_1_pc_prime),
    .\同步清零_高电平有效 (or_1_out), .\使能端_低电平有效 (stop));  // open: 原PC, 原PC_prime, hit, hit_prime, status, status_prime
  Multiplexer #(.select(1), .width(32), .disabled("Z"), .enable("false")) multiplexer_4 (
    .in0(bit_extender_1_out), .in1(bit_extender_2_out), .out(IMM), .sel(Sign));
  Multiplexer #(.select(1), .width(5), .disabled("Z"), .enable("false")) multiplexer_5 (
    .in0(IR_NOW[20:16]), .in1(imm16[15:11]), .out(multiplexer_5_out), .sel(RegDst));
  Multiplexer #(.select(1), .width(5), .disabled("Z"), .enable("false")) multiplexer_6 (
    .in0(multiplexer_5_out), .in1({5{1'b1}}), .out(WRITEREG), .sel(JAL));
  and and_1 (equal, syscall, comparator_1_eq);
  and and_2 (stop, syscall, not_3_out);
  not not_3 (not_3_out, comparator_1_eq);
  Multiplexer #(.select(1), .width(32), .disabled("Z"), .enable("false")) multiplexer_7 (
    .in1(a0), .out(multiplexer_7_out), .sel(equal));  // open: in0
  // Probe on a0
  \单周期硬布线控制器  \u_单周期硬布线控制器_1  (
    .Func(imm16[5:0]), .OP(IR_NOW[31:26]), .ALU_OP(ALUOP), .MemToReg(MemtoReg), .MemWrite(MemWrite),
    .ALU_SRC(ALUSRC), .RegWrite(Regwrite_t), .SysCALL(\单周期硬布线控制器_1_syscall ), .SignedExt(Sign),
    .RegDst(RegDst), .JR(jr_t), .JMP(jmp_t), .Beq(BEQ), .JAL(JAL), .Bne(BNE), .SRLV(SRLV), .LBU(LBU),
    .BGTZ(BGTZ));
  Multiplexer #(.select(1), .width(5), .disabled("Z"), .enable("false")) multiplexer_8 (
    .in0(IR_NOW[25:21]), .in1(5'b00010), .out(multiplexer_8_out), .sel(\单周期硬布线控制器_1_syscall ));
  Multiplexer #(.select(1), .width(5), .disabled("Z"), .enable("false")) multiplexer_9 (
    .in0(IR_NOW[20:16]), .in1(5'b00100), .out(multiplexer_9_out), .sel(\单周期硬布线控制器_1_syscall ));
  assign imm26 = {{6{IR_NOW[25]}}, {IR_NOW[25:16], imm16}};  // Bit_Extender bit_extender_3
  Register #(.width(32), .trigger("rising"), .Select("low")) register_1 (
    .D(multiplexer_7_out), .Q(LedData), .clk(CLK));  // open: en, clr
  MIPS_Regifile mips_regifile_1 (
    .Din(RDin), .Clk(CLK), .R1(mips_regifile_1_r1), .R2(mips_regifile_1_r2), .WE(regwrite_t_t),
    .W_num(multiplexer_16_out), .R1_num(multiplexer_8_out), .R2_num(multiplexer_9_out));
  ID_EX id_ex_1 (
    .RegDst(RegDst), .MemToReg(MemtoReg), .RegWirte(Regwrite_t), .MemWrite(MemWrite), .ALUSRCB(ALUSRC),
    .J(jmp_t), .JR(jr_t), .JAL(JAL), .BEQ(BEQ), .BNE(BNE), .ALUOP(ALUOP), .IR({IR_NOW, imm16}),
    .PC(if_id_1_pc_prime), .A(mips_regifile_1_r1), .B(mips_regifile_1_r2), .Imm16(IMM), .CLK(CLK),
    .RegDst_prime(id_ex_1_regdst_prime), .MemToReg_prime(id_ex_1_memtoreg_prime),
    .RegWrite_prime(id_ex_1_regwrite_prime), .MemWrite_prime(id_ex_1_memwrite_prime),
    .ALUSRCB_prime(id_ex_1_alusrcb_prime), .J_prime(JMP), .JR_prime(JR), .JAL_prime(id_ex_1_jal_prime),
    .BEQ_prime(beq_t), .BNE_prime(bne_t), .ALUOP_prime(id_ex_1_aluop_prime), .IR_prime(id_ex_1_ir_prime),
    .PC_prime({JPC[31:28], id_ex_1_pc_prime}), .A_prime(JRPC), .B_prime(id_ex_1_b_prime),
    .Imm16_prime(id_ex_1_imm16_prime), .\同步清零_高电平有效 (or_1_out), .\使能端_低电平有效 (stop), .Imm26(imm26),
    .Imm26_prime(id_ex_1_imm26_prime), .shamt_prime(id_ex_1_shamt_prime),
    .WriteReg_prime(id_ex_1_writereg_prime), .WriteReg(WRITEREG), .shamt(imm16[10:6]), .BGTZ(BGTZ),
    .BGTZ_prime(bgtz_t), .LBU(LBU), .LBU_prime(id_ex_1_lbu_prime), .SRLV(SRLV),
    .SRLV_prime(id_ex_1_srlv_prime));  // open: A_choose, A_Choose_prime, B_Choose, B_Choose_prime, hit, hit_prime, 原PC, 原PC_prime, status, status_prime, sign16, sign16_prime
  Multiplexer #(.select(1), .width(32), .disabled("Z"), .enable("false")) multiplexer_10 (
    .in0(id_ex_1_b_prime), .in1(id_ex_1_imm16_prime), .out(multiplexer_10_out), .sel(id_ex_1_alusrcb_prime));
  Shifter #(.width(32), .shift("ll")) shifter_1 (.in(id_ex_1_imm16_prime), .\dist (5'b00010), .out(shifter_1_out));
  Shifter #(.width(32), .shift("ll")) shifter_2 (
    .in(id_ex_1_imm26_prime), .\dist (5'b00010), .out({shifter_2_out, JPC[27:0]}));
  Multiplexer #(.select(1), .width(32), .disabled("Z"), .enable("false")) multiplexer_11 (
    .in0(JRPC), .in1(id_ex_1_b_prime), .out(multiplexer_11_out), .sel(id_ex_1_srlv_prime));
  Multiplexer #(.select(1), .width(5), .disabled("Z"), .enable("false")) multiplexer_12 (
    .in0(id_ex_1_shamt_prime), .in1(JRPC[4:0]), .out(multiplexer_12_out), .sel(id_ex_1_srlv_prime));
  Adder #(.width(32)) adder_2 (
    .a(shifter_1_out), .b({JPC[31:28], id_ex_1_pc_prime}), .out(adder_2_out));  // open: cin, cout
  Counter #(.width(16), .max('hffff), .ongoal("wrap"), .trigger("rising"), .behavior("old")) counter_3 (
    .D({16{1'b0}}), .count(JMP), .Q(\无条件 ), .clk(CLK));  // open: load, carry, clr, preset
  // Probe on \无条件 
  MIPS_ALU mips_alu_1 (
    .X(multiplexer_11_out), .Y(multiplexer_10_out), .AluOP(id_ex_1_aluop_prime), .Equal(mips_alu_1_equal),
    .Result(mips_alu_1_result), .shamt(multiplexer_12_out));  // open: Result_2
  Counter #(.width(16), .max('hffff), .ongoal("wrap"), .trigger("rising"), .behavior("old")) counter_4 (
    .D({16{1'b0}}), .count(Branch), .Q(\有条件 ), .clk(CLK));  // open: load, carry, clr, preset
  // Probe on \有条件 
  not not_4 (not_4_out, mips_alu_1_equal);
  not not_5 (not_5_out, mips_alu_1_result[0]);
  and and_3 (and_3_out, not_4_out, bne_t);
  and and_4 (and_4_out, mips_alu_1_equal, beq_t);
  or or_2 (Branch, and_3_out, and_4_out, and_5_out);
  and and_5 (and_5_out, not_4_out, not_5_out, bgtz_t);
  EX_MEM ex_mem_1 (
    .JAL(id_ex_1_jal_prime), .RegDst(id_ex_1_regdst_prime), .MemToReg(id_ex_1_memtoreg_prime),
    .RegWirte(id_ex_1_regwrite_prime), .MemWrite(id_ex_1_memwrite_prime), .IR(id_ex_1_ir_prime),
    .PC({JPC[31:28], id_ex_1_pc_prime}), .B(id_ex_1_b_prime), .ALU(mips_alu_1_result), .CLK(CLK),
    .JAL_prime(ex_mem_1_jal_prime), .RegDst_prime(ex_mem_1_regdst_prime),
    .MemToReg_prime(ex_mem_1_memtoreg_prime), .RegWrite_prime(ex_mem_1_regwrite_prime),
    .MemWrite_prime(ex_mem_1_memwrite_prime), .IR_prime(ex_mem_1_ir_prime), .PC_prime(ex_mem_1_pc_prime),
    .B_prime(MDin), .ALU_prime(ex_mem_1_alu_prime), .\使能端_低电平有效 (stop), .A(JRPC), .A_prime(ex_mem_1_a_prime),
    .WriteReg(id_ex_1_writereg_prime), .WriteReg_prime(ex_mem_1_writereg_prime), .LBU(id_ex_1_lbu_prime),
    .LBU_prime(ex_mem_1_lbu_prime));  // open: 同步清零_高电平有效
  RAM #(.addrWidth(10), .dataWidth(32), .bus("separate"), .Select("high")) ram_1 (
    .addr(ex_mem_1_alu_prime[11:2]), .din(MDin), .data(ram_1_data), .str(ex_mem_1_memwrite_prime),
    .sel(1'b1), .clk(CLK));  // open: ld, clr
  MEM_WB mem_wb_1 (
    .JAL(ex_mem_1_jal_prime), .RegDst(ex_mem_1_regdst_prime), .MemToReg(ex_mem_1_memtoreg_prime),
    .RegWirte(ex_mem_1_regwrite_prime), .IR(ex_mem_1_ir_prime), .PC(ex_mem_1_pc_prime),
    .ALU(ex_mem_1_alu_prime), .MD(ram_1_data), .CLK(CLK), .JAL_prime(mem_wb_1_jal_prime),
    .RegDst_prime(mem_wb_1_regdst_prime), .MemToReg_prime(mem_wb_1_memtoreg_prime),
    .RegWrite_prime(regwrite_t_t), .IR_prime(IR_final), .PC_prime(mem_wb_1_pc_prime),
    .ALU_prime(mem_wb_1_alu_prime), .MD_prime(mem_wb_1_md_prime), .\使能端_低电平有效 (stop), .A(ex_mem_1_a_prime),
    .A_prime(v0), .B(MDin), .B_prime(a0), .WriteReg(ex_mem_1_writereg_prime), .LBU(ex_mem_1_lbu_prime),
    .LBU_prime(mem_wb_1_lbu_prime));  // open: 同步清零_高电平有效, WriteReg_prime
  Multiplexer #(.select(1), .width(5), .disabled("Z"), .enable("false")) multiplexer_13 (
    .in0(IR_final[20:16]), .in1(IR_final[15:11]), .out(multiplexer_13_out), .sel(mem_wb_1_regdst_prime));
  Multiplexer #(.select(1), .width(32), .disabled("Z"), .enable("false")) multiplexer_14 (
    .in0(mem_wb_1_alu_prime), .in1(mem_wb_1_md_prime), .out(multiplexer_14_out), .sel(mem_wb_1_memtoreg_prime));
  Multiplexer #(.select(1), .width(32), .disabled("Z"), .enable("false")) multiplexer_15 (
    .in0(multiplexer_17_out), .in1(mem_wb_1_pc_prime), .out(RDin), .sel(mem_wb_1_jal_prime));
  Multiplexer #(.select(1), .width(5), .disabled("Z"), .enable("false")) multiplexer_16 (
    .in0(multiplexer_13_out), .in1({5{1'b1}}), .out(multiplexer_16_out), .sel(mem_wb_1_jal_prime));
  Comparator #(.width(32), .mode("twosComplement")) comparator_2 (
    .a(IR_final), .b(32'hc), .eq(syscall));  // open: gt, lt
  Shifter #(.width(32), .shift("ll")) shifter_3 (
    .in(32'hff), .\dist ({mem_wb_1_alu_prime[1:0], 3'b000}), .out(shifter_3_out));
  assign and_6_out = multiplexer_14_out & shifter_3_out;  // AND_Gate and_6, 32 bits wide
  Shifter #(.width(32), .shift("lr")) shifter_4 (
    .in(and_6_out), .\dist ({mem_wb_1_alu_prime[1:0], 3'b000}), .out(shifter_4_out));
  Multiplexer #(.select(1), .width(32), .disabled("Z"), .enable("false")) multiplexer_17 (
    .in0(multiplexer_14_out), .in1(shifter_4_out), .out(multiplexer_17_out), .sel(mem_wb_1_lbu_prime));

  // Other names for the same wires on the sheet: IR_NOW[15:0] = imm16; shamt[4:0] = imm16[10:6]

  // Notes on the sheet:
  //   中断源
  //   中断等待指示
  //   总复位信号应将除ROM以外所有存储组件全部清零
  //   数码管输出
  //   数码管输出应该用寄存器锁存，否则显示数据只能一闪而过
  //   contents of rom_1 (hex, n*v repeats v):
  //   20110020 20020022 8000006 20110004 20120005 20130006 10000003 20110007 20120008 20130009 14110003
  //   2011000a 2012000b 2013000c c000014 2002000a 0 0 0 c 2231ffff 0 0 0 112020 0 0 0 c 1620fff6 3e00008
  //   rt
  //   为方便自动评测，需要输出PC，IR，寄存器文件写入端口RDin，内存写入端口MDin等信号
  //   rs
  //   rd
  //   OP
  //   rt
endmodule

module ID_EX (
  input  [31:0] sign16,
  input  [1:0] status,
  input  hit,
  input  [31:0] \原PC ,
  input  SRLV,
  input  LBU,
  input  BGTZ,
  input  RegDst,
  input  MemToReg,
  input  RegWirte,
  input  MemWrite,
  input  ALUSRCB,
  input  J,
  input  JR,
  input  JAL,
  input  BEQ,
  input  BNE,
  input  [3:0] ALUOP,
  input  [31:0] IR,
  input  [31:0] PC,
  input  [31:0] A,
  input  [31:0] B,
  input  [31:0] Imm16,
  input  [31:0] Imm26,
  input  [4:0] shamt,
  input  [4:0] WriteReg,
  input  [1:0] A_choose,
  input  [1:0] B_Choose,
  input  CLK,
  input  \同步清零_高电平有效 ,
  input  \使能端_低电平有效 ,
  output [31:0] sign16_prime,
  output [1:0] status_prime,
  output hit_prime,
  output [31:0] \原PC_prime ,
  output SRLV_prime,
  output LBU_prime,
  output BGTZ_prime,
  output RegDst_prime,
  output MemToReg_prime,
  output RegWrite_prime,
  output MemWrite_prime,
  output ALUSRCB_prime,
  output J_prime,
  output JR_prime,
  output JAL_prime,
  output BEQ_prime,
  output BNE_prime,
  output [3:0] ALUOP_prime,
  output [31:0] IR_prime,
  output [31:0] PC_prime,
  output [31:0] A_prime,
  output [31:0] B_prime,
  output [31:0] Imm16_prime,
  output [31:0] Imm26_prime,
  output [4:0] shamt_prime,
  output [4:0] WriteReg_prime,
  output [1:0] A_Choose_prime,
  output [1:0] B_Choose_prime
);

  wire multiplexer_3_out, multiplexer_5_out, multiplexer_6_out, multiplexer_7_out, multiplexer_8_out,
       multiplexer_9_out, multiplexer_10_out, multiplexer_11_out, multiplexer_12_out, multiplexer_13_out,
       multiplexer_14_out, multiplexer_15_out, multiplexer_16_out, multiplexer_17_out, pull_resistor_2_node;
  wire [1:0] multiplexer_2_out, multiplexer_27_out, multiplexer_28_out;
  wire [3:0] multiplexer_18_out;
  wire [4:0] multiplexer_25_out, multiplexer_26_out;
  wire [31:0] multiplexer_1_out, multiplexer_4_out, multiplexer_19_out, multiplexer_20_out,
       multiplexer_21_out, multiplexer_22_out, multiplexer_23_out, multiplexer_24_out;

  Multiplexer #(.select(1), .width(32), .disabled("Z"), .enable("false")) multiplexer_1 (
    .in0(sign16), .in1({32{1'b0}}), .out(multiplexer_1_out), .sel(\同步清零_高电平有效 ));
  Multiplexer #(.select(1), .width(2), .disabled("Z"), .enable("false")) multiplexer_2 (
    .in0(status), .in1(2'b00), .out(multiplexer_2_out), .sel(\同步清零_高电平有效 ));
  Multiplexer #(.select(1), .width(1), .disabled("Z"), .enable("false")) multiplexer_3 (
    .in0(hit), .in1(1'b0), .out(multiplexer_3_out), .sel(\同步清零_高电平有效 ));
  Multiplexer #(.select(1), .width(32), .disabled("Z"), .enable("false")) multiplexer_4 (
    .in0(\原PC ), .in1({32{1'b0}}), .out(multiplexer_4_out), .sel(\同步清零_高电平有效 ));
  Multiplexer #(.select(1), .width(1), .disabled("Z"), .enable("false")) multiplexer_5 (
    .in0(SRLV), .in1(1'b0), .out(multiplexer_5_out), .sel(\同步清零_高电平有效 ));
  Multiplexer #(.select(1), .width(1), .disabled("Z"), .enable("false")) multiplexer_6 (
    .in0(LBU), .in1(1'b0), .out(multiplexer_6_out), .sel(\同步清零_高电平有效 ));
  Multiplexer #(.select(1), .width(1), .disabled("Z"), .enable("false")) multiplexer_7 (
    .in0(BGTZ), .in1(1'b0), .out(multiplexer_7_out), .sel(\同步清零_高电平有效 ));
  Multiplexer #(.select(1), .width(1), .disabled("Z"), .enable("false")) multiplexer_8 (
    .in0(RegDst), .in1(1'b0), .out(multiplexer_8_out), .sel(\同步清零_高电平有效 ));
  Multiplexer #(.select(1), .width(1), .disabled("Z"), .enable("false")) multiplexer_9 (
    .in0(MemToReg), .in1(1'b0), .out(multiplexer_9_out), .sel(\同步清零_高电平有效 ));
  Multiplexer #(.select(1), .width(1), .disabled("Z"), .enable("false")) multiplexer_10 (
    .in0(RegWirte), .in1(1'b0), .out(multiplexer_10_out), .sel(\同步清零_高电平有效 ));
  Multiplexer #(.select(1), .width(1), .disabled("Z"), .enable("false")) multiplexer_11 (
    .in0(MemWrite), .in1(1'b0), .out(multiplexer_11_out), .sel(\同步清零_高电平有效 ));
  Multiplexer #(.select(1), .width(1), .disabled("Z"), .enable("false")) multiplexer_12 (
    .in0(ALUSRCB), .in1(1'b0), .out(multiplexer_12_out), .sel(\同步清零_高电平有效 ));
  Multiplexer #(.select(1), .width(1), .disabled("Z"), .enable("false")) multiplexer_13 (
    .in0(J), .in1(1'b0), .out(multiplexer_13_out), .sel(\同步清零_高电平有效 ));
  Multiplexer #(.select(1), .width(1), .disabled("Z"), .enable("false")) multiplexer_14 (
    .in0(JR), .in1(1'b0), .out(multiplexer_14_out), .sel(\同步清零_高电平有效 ));
  Multiplexer #(.select(1), .width(1), .disabled("Z"), .enable("false")) multiplexer_15 (
    .in0(JAL), .in1(1'b0), .out(multiplexer_15_out), .sel(\同步清零_高电平有效 ));
  Multiplexer #(.select(1), .width(1), .disabled("Z"), .enable("false")) multiplexer_16 (
    .in0(BEQ), .in1(1'b0), .out(multiplexer_16_out), .sel(\同步清零_高电平有效 ));
  Multiplexer #(.select(1), .width(1), .disabled("Z"), .enable("false")) multiplexer_17 (
    .in0(BNE), .in1(1'b0), .out(multiplexer_17_out), .sel(\同步清零_高电平有效 ));
  Multiplexer #(.select(1), .width(4), .disabled("Z"), .enable("false")) multiplexer_18 (
    .in0(ALUOP), .in1(4'b0000), .out(multiplexer_18_out), .sel(\同步清零_高电平有效 ));
  Multiplexer #(.select(1), .width(32), .disabled("Z"), .enable("false")) multiplexer_19 (
    .in0(IR), .in1({32{1'b0}}), .out(multiplexer_19_out), .sel(\同步清零_高电平有效 ));
  Multiplexer #(.select(1), .width(32), .disabled("Z"), .enable("false")) multiplexer_20 (
    .in0(PC), .in1({32{1'b0}}), .out(multiplexer_20_out), .sel(\同步清零_高电平有效 ));
  Multiplexer #(.select(1), .width(32), .disabled("Z"), .enable("false")) multiplexer_21 (
    .in0(A), .in1({32{1'b0}}), .out(multiplexer_21_out), .sel(\同步清零_高电平有效 ));
  Multiplexer #(.select(1), .width(32), .disabled("Z"), .enable("false")) multiplexer_22 (
    .in0(B), .in1({32{1'b0}}), .out(multiplexer_22_out), .sel(\同步清零_高电平有效 ));
  Multiplexer #(.select(1), .width(32), .disabled("Z"), .enable("false")) multiplexer_23 (
    .in0(Imm16), .in1({32{1'b0}}), .out(multiplexer_23_out), .sel(\同步清零_高电平有效 ));
  Multiplexer #(.select(1), .width(32), .disabled("Z"), .enable("false")) multiplexer_24 (
    .in0(Imm26), .in1({32{1'b0}}), .out(multiplexer_24_out), .sel(\同步清零_高电平有效 ));
  Multiplexer #(.select(1), .width(5), .disabled("Z"), .enable("false")) multiplexer_25 (
    .in0(shamt), .in1({5{1'b0}}), .out(multiplexer_25_out), .sel(\同步清零_高电平有效 ));
  Multiplexer #(.select(1), .width(5), .disabled("Z"), .enable("false")) multiplexer_26 (
    .in0(WriteReg), .in1({5{1'b0}}), .out(multiplexer_26_out), .sel(\同步清零_高电平有效 ));
  Multiplexer #(.select(1), .width(2), .disabled("Z"), .enable("false")) multiplexer_27 (
    .in0(A_choose), .in1(2'b00), .out(multiplexer_27_out), .sel(\同步清零_高电平有效 ));
  Multiplexer #(.select(1), .width(2), .disabled("Z"), .enable("false")) multiplexer_28 (
    .in0(B_Choose), .in1(2'b00), .out(multiplexer_28_out), .sel(\同步清零_高电平有效 ));
  Pull_Resistor #(.pull(0)) pull_resistor_1 (.node(\同步清零_高电平有效 ));
  Register #(.width(32), .trigger("rising"), .Select("low")) register_1 (
    .D(multiplexer_1_out), .en(pull_resistor_2_node), .Q(sign16_prime), .clk(CLK));  // open: clr
  Register #(.width(2), .trigger("rising"), .Select("low")) register_2 (
    .D(multiplexer_2_out), .en(pull_resistor_2_node), .Q(status_prime), .clk(CLK));  // open: clr
  Register #(.width(1), .trigger("rising"), .Select("low")) register_3 (
    .D(multiplexer_3_out), .en(pull_resistor_2_node), .Q(hit_prime), .clk(CLK));  // open: clr
  Register #(.width(32), .trigger("rising"), .Select("low")) register_4 (
    .D(multiplexer_4_out), .en(pull_resistor_2_node), .Q(\原PC_prime ), .clk(CLK));  // open: clr
  Register #(.width(1), .trigger("rising"), .Select("low")) register_5 (
    .D(multiplexer_5_out), .en(pull_resistor_2_node), .Q(SRLV_prime), .clk(CLK));  // open: clr
  Register #(.width(1), .trigger("rising"), .Select("low")) register_6 (
    .D(multiplexer_6_out), .en(pull_resistor_2_node), .Q(LBU_prime), .clk(CLK));  // open: clr
  Register #(.width(1), .trigger("rising"), .Select("low")) register_7 (
    .D(multiplexer_7_out), .en(pull_resistor_2_node), .Q(BGTZ_prime), .clk(CLK));  // open: clr
  Register #(.width(1), .trigger("rising"), .Select("low")) register_8 (
    .D(multiplexer_8_out), .en(pull_resistor_2_node), .Q(RegDst_prime), .clk(CLK));  // open: clr
  Register #(.width(1), .trigger("rising"), .Select("low")) register_9 (
    .D(multiplexer_9_out), .en(pull_resistor_2_node), .Q(MemToReg_prime), .clk(CLK));  // open: clr
  Register #(.width(1), .trigger("rising"), .Select("low")) register_10 (
    .D(multiplexer_10_out), .en(pull_resistor_2_node), .Q(RegWrite_prime), .clk(CLK));  // open: clr
  Register #(.width(1), .trigger("rising"), .Select("low")) register_11 (
    .D(multiplexer_11_out), .en(pull_resistor_2_node), .Q(MemWrite_prime), .clk(CLK));  // open: clr
  Register #(.width(1), .trigger("rising"), .Select("low")) register_12 (
    .D(multiplexer_12_out), .en(pull_resistor_2_node), .Q(ALUSRCB_prime), .clk(CLK));  // open: clr
  Register #(.width(1), .trigger("rising"), .Select("low")) register_13 (
    .D(multiplexer_13_out), .en(pull_resistor_2_node), .Q(J_prime), .clk(CLK));  // open: clr
  Register #(.width(1), .trigger("rising"), .Select("low")) register_14 (
    .D(multiplexer_14_out), .en(pull_resistor_2_node), .Q(JR_prime), .clk(CLK));  // open: clr
  Register #(.width(1), .trigger("rising"), .Select("low")) register_15 (
    .D(multiplexer_15_out), .en(pull_resistor_2_node), .Q(JAL_prime), .clk(CLK));  // open: clr
  Register #(.width(1), .trigger("rising"), .Select("low")) register_16 (
    .D(multiplexer_16_out), .en(pull_resistor_2_node), .Q(BEQ_prime), .clk(CLK));  // open: clr
  Register #(.width(1), .trigger("rising"), .Select("low")) register_17 (
    .D(multiplexer_17_out), .en(pull_resistor_2_node), .Q(BNE_prime), .clk(CLK));  // open: clr
  Register #(.width(4), .trigger("rising"), .Select("low")) register_18 (
    .D(multiplexer_18_out), .en(pull_resistor_2_node), .Q(ALUOP_prime), .clk(CLK));  // open: clr
  Register #(.width(32), .trigger("rising"), .Select("low")) register_19 (
    .D(multiplexer_19_out), .en(pull_resistor_2_node), .Q(IR_prime), .clk(CLK));  // open: clr
  Register #(.width(32), .trigger("rising"), .Select("low")) register_20 (
    .D(multiplexer_20_out), .en(pull_resistor_2_node), .Q(PC_prime), .clk(CLK));  // open: clr
  Register #(.width(32), .trigger("rising"), .Select("low")) register_21 (
    .D(multiplexer_21_out), .en(pull_resistor_2_node), .Q(A_prime), .clk(CLK));  // open: clr
  Register #(.width(32), .trigger("rising"), .Select("low")) register_22 (
    .D(multiplexer_22_out), .en(pull_resistor_2_node), .Q(B_prime), .clk(CLK));  // open: clr
  Register #(.width(32), .trigger("rising"), .Select("low")) register_23 (
    .D(multiplexer_23_out), .en(pull_resistor_2_node), .Q(Imm16_prime), .clk(CLK));  // open: clr
  Register #(.width(32), .trigger("rising"), .Select("low")) register_24 (
    .D(multiplexer_24_out), .en(pull_resistor_2_node), .Q(Imm26_prime), .clk(CLK));  // open: clr
  Register #(.width(5), .trigger("rising"), .Select("low")) register_25 (
    .D(multiplexer_25_out), .en(pull_resistor_2_node), .Q(shamt_prime), .clk(CLK));  // open: clr
  Register #(.width(5), .trigger("rising"), .Select("low")) register_26 (
    .D(multiplexer_26_out), .en(pull_resistor_2_node), .Q(WriteReg_prime), .clk(CLK));  // open: clr
  Register #(.width(2), .trigger("rising"), .Select("low")) register_27 (
    .D(multiplexer_27_out), .en(pull_resistor_2_node), .Q(A_Choose_prime), .clk(CLK));  // open: clr
  Register #(.width(2), .trigger("rising"), .Select("low")) register_28 (
    .D(multiplexer_28_out), .en(pull_resistor_2_node), .Q(B_Choose_prime), .clk(CLK));  // open: clr
  Pull_Resistor #(.pull(0)) pull_resistor_2 (.node(pull_resistor_2_node));
  not not_1 (pull_resistor_2_node, \使能端_低电平有效 );

  // Notes on the sheet:
  //   使能端_低电平有效: pull=down
  //   同步清零_高电平有效: pull=down
  //   下拉电阻使得引脚可以悬空
endmodule

module EX_MEM (
  input  LBU,
  input  JAL,
  input  RegDst,
  input  MemToReg,
  input  RegWirte,
  input  MemWrite,
  input  [31:0] IR,
  input  [31:0] A,
  input  [31:0] PC,
  input  [31:0] B,
  input  [31:0] ALU,
  input  [4:0] WriteReg,
  input  CLK,
  input  \同步清零_高电平有效 ,
  input  \使能端_低电平有效 ,
  output LBU_prime,
  output JAL_prime,
  output RegDst_prime,
  output MemToReg_prime,
  output RegWrite_prime,
  output MemWrite_prime,
  output [31:0] IR_prime,
  output [31:0] A_prime,
  output [31:0] PC_prime,
  output [31:0] B_prime,
  output [31:0] ALU_prime,
  output [4:0] WriteReg_prime
);

  wire multiplexer_1_out, multiplexer_2_out, multiplexer_3_out, multiplexer_4_out, multiplexer_5_out,
       multiplexer_6_out, pull_resistor_2_node;
  wire [4:0] multiplexer_12_out;
  wire [31:0] multiplexer_7_out, multiplexer_8_out, multiplexer_9_out, multiplexer_10_out, multiplexer_11_out;

  Multiplexer #(.select(1), .width(1), .disabled("Z"), .enable("false")) multiplexer_1 (
    .in0(LBU), .in1(1'b0), .out(multiplexer_1_out), .sel(\同步清零_高电平有效 ));
  Multiplexer #(.select(1), .width(1), .disabled("Z"), .enable("false")) multiplexer_2 (
    .in0(JAL), .in1(1'b0), .out(multiplexer_2_out), .sel(\同步清零_高电平有效 ));
  Multiplexer #(.select(1), .width(1), .disabled("Z"), .enable("false")) multiplexer_3 (
    .in0(RegDst), .in1(1'b0), .out(multiplexer_3_out), .sel(\同步清零_高电平有效 ));
  Multiplexer #(.select(1), .width(1), .disabled("Z"), .enable("false")) multiplexer_4 (
    .in0(MemToReg), .in1(1'b0), .out(multiplexer_4_out), .sel(\同步清零_高电平有效 ));
  Multiplexer #(.select(1), .width(1), .disabled("Z"), .enable("false")) multiplexer_5 (
    .in0(RegWirte), .in1(1'b0), .out(multiplexer_5_out), .sel(\同步清零_高电平有效 ));
  Multiplexer #(.select(1), .width(1), .disabled("Z"), .enable("false")) multiplexer_6 (
    .in0(MemWrite), .in1(1'b0), .out(multiplexer_6_out), .sel(\同步清零_高电平有效 ));
  Multiplexer #(.select(1), .width(32), .disabled("Z"), .enable("false")) multiplexer_7 (
    .in0(IR), .in1({32{1'b0}}), .out(multiplexer_7_out), .sel(\同步清零_高电平有效 ));
  Multiplexer #(.select(1), .width(32), .disabled("Z"), .enable("false")) multiplexer_8 (
    .in0(A), .in1({32{1'b0}}), .out(multiplexer_8_out), .sel(\同步清零_高电平有效 ));
  Multiplexer #(.select(1), .width(32), .disabled("Z"), .enable("false")) multiplexer_9 (
    .in0(PC), .in1({32{1'b0}}), .out(multiplexer_9_out), .sel(\同步清零_高电平有效 ));
  Multiplexer #(.select(1), .width(32), .disabled("Z"), .enable("false")) multiplexer_10 (
    .in0(B), .in1({32{1'b0}}), .out(multiplexer_10_out), .sel(\同步清零_高电平有效 ));
  Multiplexer #(.select(1), .width(32), .disabled("Z"), .enable("false")) multiplexer_11 (
    .in0(ALU), .in1({32{1'b0}}), .out(multiplexer_11_out), .sel(\同步清零_高电平有效 ));
  Multiplexer #(.select(1), .width(5), .disabled("Z"), .enable("false")) multiplexer_12 (
    .in0(WriteReg), .in1({5{1'b0}}), .out(multiplexer_12_out), .sel(\同步清零_高电平有效 ));
  Pull_Resistor #(.pull(0)) pull_resistor_1 (.node(\同步清零_高电平有效 ));
  Pull_Resistor #(.pull(0)) pull_resistor_2 (.node(pull_resistor_2_node));
  not not_1 (pull_resistor_2_node, \使能端_低电平有效 );
  Register #(.width(1), .trigger("rising"), .Select("low")) register_1 (
    .D(multiplexer_1_out), .en(pull_resistor_2_node), .Q(LBU_prime), .clk(CLK));  // open: clr
  Register #(.width(1), .trigger("rising"), .Select("low")) register_2 (
    .D(multiplexer_2_out), .en(pull_resistor_2_node), .Q(JAL_prime), .clk(CLK));  // open: clr
  Register #(.width(1), .trigger("rising"), .Select("low")) register_3 (
    .D(multiplexer_3_out), .en(pull_resistor_2_node), .Q(RegDst_prime), .clk(CLK));  // open: clr
  Register #(.width(1), .trigger("rising"), .Select("low")) register_4 (
    .D(multiplexer_4_out), .en(pull_resistor_2_node), .Q(MemToReg_prime), .clk(CLK));  // open: clr
  Register #(.width(1), .trigger("rising"), .Select("low")) register_5 (
    .D(multiplexer_5_out), .en(pull_resistor_2_node), .Q(RegWrite_prime), .clk(CLK));  // open: clr
  Register #(.width(1), .trigger("rising"), .Select("low")) register_6 (
    .D(multiplexer_6_out), .en(pull_resistor_2_node), .Q(MemWrite_prime), .clk(CLK));  // open: clr
  Register #(.width(32), .trigger("rising"), .Select("low")) register_7 (
    .D(multiplexer_7_out), .en(pull_resistor_2_node), .Q(IR_prime), .clk(CLK));  // open: clr
  Register #(.width(32), .trigger("rising"), .Select("low")) register_8 (
    .D(multiplexer_8_out), .en(pull_resistor_2_node), .Q(A_prime), .clk(CLK));  // open: clr
  Register #(.width(32), .trigger("rising"), .Select("low")) register_9 (
    .D(multiplexer_9_out), .en(pull_resistor_2_node), .Q(PC_prime), .clk(CLK));  // open: clr
  Register #(.width(32), .trigger("rising"), .Select("low")) register_10 (
    .D(multiplexer_10_out), .en(pull_resistor_2_node), .Q(B_prime), .clk(CLK));  // open: clr
  Register #(.width(32), .trigger("rising"), .Select("low")) register_11 (
    .D(multiplexer_11_out), .en(pull_resistor_2_node), .Q(ALU_prime), .clk(CLK));  // open: clr
  Register #(.width(5), .trigger("rising"), .Select("low")) register_12 (
    .D(multiplexer_12_out), .en(pull_resistor_2_node), .Q(WriteReg_prime), .clk(CLK));  // open: clr

  // Notes on the sheet:
  //   使能端_低电平有效: pull=down
  //   同步清零_高电平有效: pull=down
  //   下拉电阻使得引脚可以悬空
endmodule

module MEM_WB (
  input  LBU,
  input  JAL,
  input  RegDst,
  input  MemToReg,
  input  RegWirte,
  input  [31:0] IR,
  input  [31:0] A,
  input  [31:0] B,
  input  [31:0] PC,
  input  [31:0] ALU,
  input  [31:0] MD,
  input  [4:0] WriteReg,
  input  CLK,
  input  \同步清零_高电平有效 ,
  input  \使能端_低电平有效 ,
  output LBU_prime,
  output JAL_prime,
  output RegDst_prime,
  output MemToReg_prime,
  output RegWrite_prime,
  output [31:0] IR_prime,
  output [31:0] A_prime,
  output [31:0] B_prime,
  output [31:0] PC_prime,
  output [31:0] ALU_prime,
  output [31:0] MD_prime,
  output [4:0] WriteReg_prime
);

  wire multiplexer_1_out, multiplexer_2_out, multiplexer_3_out, multiplexer_4_out, multiplexer_5_out,
       not_1_out;
  wire [4:0] multiplexer_12_out;
  wire [31:0] multiplexer_6_out, multiplexer_7_out, multiplexer_8_out, multiplexer_9_out, multiplexer_10_out,
       multiplexer_11_out;

  Multiplexer #(.select(1), .width(1), .disabled("Z"), .enable("false")) multiplexer_1 (
    .in0(LBU), .in1(1'b0), .out(multiplexer_1_out), .sel(\同步清零_高电平有效 ));
  Multiplexer #(.select(1), .width(1), .disabled("Z"), .enable("false")) multiplexer_2 (
    .in0(JAL), .in1(1'b0), .out(multiplexer_2_out), .sel(\同步清零_高电平有效 ));
  Multiplexer #(.select(1), .width(1), .disabled("Z"), .enable("false")) multiplexer_3 (
    .in0(RegDst), .in1(1'b0), .out(multiplexer_3_out), .sel(\同步清零_高电平有效 ));
  Multiplexer #(.select(1), .width(1), .disabled("Z"), .enable("false")) multiplexer_4 (
    .in0(MemToReg), .in1(1'b0), .out(multiplexer_4_out), .sel(\同步清零_高电平有效 ));
  Multiplexer #(.select(1), .width(1), .disabled("Z"), .enable("false")) multiplexer_5 (
    .in0(RegWirte), .in1(1'b0), .out(multiplexer_5_out), .sel(\同步清零_高电平有效 ));
  Multiplexer #(.select(1), .width(32), .disabled("Z"), .enable("false")) multiplexer_6 (
    .in0(IR), .in1({32{1'b0}}), .out(multiplexer_6_out), .sel(\同步清零_高电平有效 ));
  Multiplexer #(.select(1), .width(32), .disabled("Z"), .enable("false")) multiplexer_7 (
    .in0(A), .in1({32{1'b0}}), .out(multiplexer_7_out), .sel(\同步清零_高电平有效 ));
  Multiplexer #(.select(1), .width(32), .disabled("Z"), .enable("false")) multiplexer_8 (
    .in0(B), .in1({32{1'b0}}), .out(multiplexer_8_out), .sel(\同步清零_高电平有效 ));
  Multiplexer #(.select(1), .width(32), .disabled("Z"), .enable("false")) multiplexer_9 (
    .in0(PC), .in1({32{1'b0}}), .out(multiplexer_9_out), .sel(\同步清零_高电平有效 ));
  Multiplexer #(.select(1), .width(32), .disabled("Z"), .enable("false")) multiplexer_10 (
    .in0(ALU), .in1({32{1'b0}}), .out(multiplexer_10_out), .sel(\同步清零_高电平有效 ));
  Multiplexer #(.select(1), .width(32), .disabled("Z"), .enable("false")) multiplexer_11 (
    .in0(MD), .in1({32{1'b0}}), .out(multiplexer_11_out), .sel(\同步清零_高电平有效 ));
  Multiplexer #(.select(1), .width(5), .disabled("Z"), .enable("false")) multiplexer_12 (
    .in0(WriteReg), .in1({5{1'b0}}), .out(multiplexer_12_out), .sel(\同步清零_高电平有效 ));
  Pull_Resistor #(.pull(0)) pull_resistor_1 (.node(\同步清零_高电平有效 ));
  not not_1 (not_1_out, \使能端_低电平有效 );
  Register #(.width(1), .trigger("rising"), .Select("low")) register_1 (
    .D(multiplexer_1_out), .en(not_1_out), .Q(LBU_prime), .clk(CLK));  // open: clr
  Register #(.width(1), .trigger("rising"), .Select("low")) register_2 (
    .D(multiplexer_2_out), .en(not_1_out), .Q(JAL_prime), .clk(CLK));  // open: clr
  Register #(.width(1), .trigger("rising"), .Select("low")) register_3 (
    .D(multiplexer_3_out), .en(not_1_out), .Q(RegDst_prime), .clk(CLK));  // open: clr
  Register #(.width(1), .trigger("rising"), .Select("low")) register_4 (
    .D(multiplexer_4_out), .en(not_1_out), .Q(MemToReg_prime), .clk(CLK));  // open: clr
  Register #(.width(1), .trigger("rising"), .Select("low")) register_5 (
    .D(multiplexer_5_out), .en(not_1_out), .Q(RegWrite_prime), .clk(CLK));  // open: clr
  Register #(.width(32), .trigger("rising"), .Select("low")) register_6 (
    .D(multiplexer_6_out), .en(not_1_out), .Q(IR_prime), .clk(CLK));  // open: clr
  Register #(.width(32), .trigger("rising"), .Select("low")) register_7 (
    .D(multiplexer_7_out), .en(not_1_out), .Q(A_prime), .clk(CLK));  // open: clr
  Register #(.width(32), .trigger("rising"), .Select("low")) register_8 (
    .D(multiplexer_8_out), .en(not_1_out), .Q(B_prime), .clk(CLK));  // open: clr
  Register #(.width(32), .trigger("rising"), .Select("low")) register_9 (
    .D(multiplexer_9_out), .en(not_1_out), .Q(PC_prime), .clk(CLK));  // open: clr
  Register #(.width(32), .trigger("rising"), .Select("low")) register_10 (
    .D(multiplexer_10_out), .en(not_1_out), .Q(ALU_prime), .clk(CLK));  // open: clr
  Register #(.width(32), .trigger("rising"), .Select("low")) register_11 (
    .D(multiplexer_11_out), .en(not_1_out), .Q(MD_prime), .clk(CLK));  // open: clr
  Register #(.width(5), .trigger("rising"), .Select("low")) register_12 (
    .D(multiplexer_12_out), .en(not_1_out), .Q(WriteReg_prime), .clk(CLK));  // open: clr
  Pull_Resistor #(.pull(0)) pull_resistor_2 (.node(not_1_out));

  // Notes on the sheet:
  //   使能端_低电平有效: pull=down
  //   同步清零_高电平有效: pull=down
  //   下拉电阻使得引脚可以悬空
endmodule
module \源寄存器使用情况  (
  input  OP0,
  input  OP1,
  input  OP2,
  input  OP3,
  input  OP4,
  input  OP5,
  input  F0,
  input  F1,
  input  F2,
  input  F3,
  input  F4,
  input  F5,
  output R1_Used,
  output R2_Used
);

  wire and_1_out, and_2_out, and_3_out, and_4_out, and_5_out, and_6_out, and_7_out, and_8_out, and_9_out,
       and_10_out, and_11_out, and_12_out, and_13_out, and_14_out, and_15_out, and_16_out, and_17_out,
       and_18_out, and_19_out, and_20_out, and_21_out, and_22_out, and_23_out, and_24_out, and_25_out,
       and_26_out, and_27_out, and_28_out, and_29_out, and_30_out, and_31_out, and_32_out, and_33_out,
       and_34_out, and_35_out, and_36_out, and_37_out, and_38_out, and_39_out, and_40_out, and_41_out,
       not_1_out, not_2_out, not_3_out, not_4_out, not_5_out, not_6_out, not_7_out, not_8_out, not_9_out,
       not_10_out, not_11_out, not_12_out, not_13_out, not_14_out, not_15_out, not_16_out, not_17_out,
       not_18_out, not_19_out, not_20_out, not_21_out, not_22_out, not_23_out, not_24_out, not_25_out,
       not_26_out, not_27_out, not_28_out, not_29_out, not_30_out, not_31_out, not_32_out, not_33_out,
       not_34_out, not_35_out, not_36_out, not_37_out, not_38_out, not_39_out, not_40_out, not_41_out,
       not_42_out, not_43_out, not_44_out, not_45_out, not_46_out, not_47_out, not_48_out, not_49_out,
       not_50_out, not_51_out, not_52_out, not_53_out, not_54_out, not_55_out, not_56_out, not_57_out,
       not_58_out, not_59_out, not_60_out, not_61_out, not_62_out, not_63_out, not_64_out, not_65_out,
       not_66_out, not_67_out, not_68_out, not_69_out, not_70_out, not_71_out, not_72_out, not_73_out,
       not_74_out, not_75_out, not_76_out, not_77_out, not_78_out, not_79_out, not_80_out, not_81_out,
       not_82_out, not_83_out, not_84_out, not_85_out, not_86_out, not_87_out, not_88_out, not_89_out,
       not_90_out, not_91_out, not_92_out, not_93_out, not_94_out, not_95_out, not_96_out, not_97_out,
       not_98_out, not_99_out, not_100_out, not_101_out, not_102_out, not_103_out, not_104_out, not_105_out,
       not_106_out, not_107_out, not_108_out, not_109_out, not_110_out, not_111_out, not_112_out,
       not_113_out, not_114_out, not_115_out, not_116_out, not_117_out, not_118_out, not_119_out,
       not_120_out, not_121_out, not_122_out, not_123_out, not_124_out, not_125_out, not_126_out,
       not_127_out, not_128_out, not_129_out, not_130_out, not_131_out, not_132_out, not_133_out,
       not_134_out, not_135_out, not_136_out, not_137_out, not_138_out, not_139_out, not_140_out,
       not_141_out, not_142_out, not_143_out, not_144_out, not_145_out, not_146_out, not_147_out,
       not_148_out, not_149_out, not_150_out, not_151_out, not_152_out, not_153_out, not_154_out,
       not_155_out, not_156_out, not_157_out, not_158_out, not_159_out, not_160_out, not_161_out,
       not_162_out, not_163_out, not_164_out, not_165_out, not_166_out, not_167_out, not_168_out,
       not_169_out, not_170_out, not_171_out, not_172_out, not_173_out, not_174_out, not_175_out,
       not_176_out, not_177_out, not_178_out, not_179_out, not_180_out, not_181_out, not_182_out,
       not_183_out, not_184_out, not_185_out, not_186_out, not_187_out, not_188_out, not_189_out,
       not_190_out, not_191_out, not_192_out, not_193_out, not_194_out, not_195_out, not_196_out,
       not_197_out, not_198_out, not_199_out, not_200_out, not_201_out, not_202_out, not_203_out,
       not_204_out, not_205_out, not_206_out, not_207_out, not_208_out, not_209_out, not_210_out,
       not_211_out, not_212_out, not_213_out, not_214_out, not_215_out, not_216_out, not_217_out,
       not_218_out, not_219_out, not_220_out, not_221_out, not_222_out, not_223_out, not_224_out,
       not_225_out, not_226_out, not_227_out, not_228_out, not_229_out, not_230_out, not_231_out,
       not_232_out, not_233_out, not_234_out, not_235_out, not_236_out, not_237_out, not_238_out,
       not_239_out, not_240_out, not_241_out, not_242_out, not_243_out, not_244_out, not_245_out,
       not_246_out, not_247_out, not_248_out, not_249_out, not_250_out, not_251_out, not_252_out,
       not_253_out, not_254_out, not_255_out, not_256_out, not_257_out, not_258_out, not_259_out,
       not_260_out, not_261_out, not_262_out, not_263_out, not_264_out, not_265_out, not_266_out,
       not_267_out, not_268_out, not_269_out, not_270_out, not_271_out, not_272_out, not_273_out,
       not_274_out, not_275_out, not_276_out, not_277_out, not_278_out, not_279_out, not_280_out,
       not_281_out, not_282_out, not_283_out, not_284_out, not_285_out, not_286_out, not_287_out,
       not_288_out, not_289_out, not_290_out, not_291_out, not_292_out, not_293_out, not_294_out,
       not_295_out, not_296_out, not_297_out, not_298_out, not_299_out, not_300_out, not_301_out,
       not_302_out, not_303_out, not_304_out, not_305_out, not_306_out, not_307_out, not_308_out,
       not_309_out, not_310_out, not_311_out, not_312_out, not_313_out, not_314_out, not_315_out;

  not not_1 (not_1_out, OP5);
  not not_2 (not_2_out, OP4);
  not not_3 (not_3_out, OP3);
  not not_4 (not_4_out, OP2);
  not not_5 (not_5_out, OP1);
  not not_6 (not_6_out, OP0);
  not not_7 (not_7_out, F5);
  not not_8 (not_8_out, F4);
  not not_9 (not_9_out, F3);
  not not_10 (not_10_out, F2);
  not not_11 (not_11_out, F0);
  not not_12 (not_12_out, OP5);
  not not_13 (not_13_out, OP4);
  not not_14 (not_14_out, OP3);
  not not_15 (not_15_out, OP2);
  not not_16 (not_16_out, OP1);
  not not_17 (not_17_out, OP0);
  not not_18 (not_18_out, F4);
  not not_19 (not_19_out, F3);
  not not_20 (not_20_out, F2);
  not not_21 (not_21_out, F1);
  not not_22 (not_22_out, F0);
  not not_23 (not_23_out, OP5);
  not not_24 (not_24_out, OP4);
  not not_25 (not_25_out, OP3);
  not not_26 (not_26_out, OP2);
  not not_27 (not_27_out, OP1);
  not not_28 (not_28_out, OP0);
  not not_29 (not_29_out, F4);
  not not_30 (not_30_out, F3);
  not not_31 (not_31_out, F2);
  not not_32 (not_32_out, F1);
  not not_33 (not_33_out, OP5);
  not not_34 (not_34_out, OP4);
  not not_35 (not_35_out, OP3);
  not not_36 (not_36_out, OP2);
  not not_37 (not_37_out, OP1);
  not not_38 (not_38_out, OP0);
  not not_39 (not_39_out, F4);
  not not_40 (not_40_out, F3);
  not not_41 (not_41_out, F2);
  not not_42 (not_42_out, F0);
  not not_43 (not_43_out, OP5);
  not not_44 (not_44_out, OP4);
  not not_45 (not_45_out, OP3);
  not not_46 (not_46_out, OP2);
  not not_47 (not_47_out, OP1);
  not not_48 (not_48_out, OP0);
  not not_49 (not_49_out, F4);
  not not_50 (not_50_out, F3);
  not not_51 (not_51_out, F1);
  not not_52 (not_52_out, F0);
  not not_53 (not_53_out, OP5);
  not not_54 (not_54_out, OP4);
  not not_55 (not_55_out, OP3);
  not not_56 (not_56_out, OP2);
  not not_57 (not_57_out, OP1);
  not not_58 (not_58_out, OP0);
  not not_59 (not_59_out, F4);
  not not_60 (not_60_out, F3);
  not not_61 (not_61_out, F1);
  not not_62 (not_62_out, OP5);
  not not_63 (not_63_out, OP4);
  not not_64 (not_64_out, OP3);
  not not_65 (not_65_out, OP2);
  not not_66 (not_66_out, OP1);
  not not_67 (not_67_out, OP0);
  not not_68 (not_68_out, F4);
  not not_69 (not_69_out, F3);
  not not_70 (not_70_out, OP5);
  not not_71 (not_71_out, OP4);
  not not_72 (not_72_out, OP3);
  not not_73 (not_73_out, OP2);
  not not_74 (not_74_out, OP1);
  not not_75 (not_75_out, OP0);
  not not_76 (not_76_out, F4);
  not not_77 (not_77_out, F2);
  not not_78 (not_78_out, F0);
  not not_79 (not_79_out, OP5);
  not not_80 (not_80_out, OP4);
  not not_81 (not_81_out, OP3);
  not not_82 (not_82_out, OP2);
  not not_83 (not_83_out, OP1);
  not not_84 (not_84_out, OP0);
  not not_85 (not_85_out, F4);
  not not_86 (not_86_out, F2);
  not not_87 (not_87_out, OP5);
  not not_88 (not_88_out, OP4);
  not not_89 (not_89_out, OP3);
  not not_90 (not_90_out, OP2);
  not not_91 (not_91_out, OP1);
  not not_92 (not_92_out, OP0);
  not not_93 (not_93_out, F5);
  not not_94 (not_94_out, F4);
  not not_95 (not_95_out, F2);
  not not_96 (not_96_out, F1);
  not not_97 (not_97_out, F0);
  not not_98 (not_98_out, OP5);
  not not_99 (not_99_out, OP4);
  not not_100 (not_100_out, OP3);
  not not_101 (not_101_out, OP2);
  not not_102 (not_102_out, OP1);
  not not_103 (not_103_out, OP0);
  not not_104 (not_104_out, F5);
  not not_105 (not_105_out, F4);
  not not_106 (not_106_out, F1);
  not not_107 (not_107_out, F0);
  not not_108 (not_108_out, OP5);
  not not_109 (not_109_out, OP4);
  not not_110 (not_110_out, OP3);
  not not_111 (not_111_out, OP1);
  not not_112 (not_112_out, OP0);
  not not_113 (not_113_out, OP5);
  not not_114 (not_114_out, OP4);
  not not_115 (not_115_out, OP3);
  not not_116 (not_116_out, OP1);
  not not_117 (not_117_out, OP5);
  not not_118 (not_118_out, OP4);
  not not_119 (not_119_out, OP2);
  not not_120 (not_120_out, OP1);
  not not_121 (not_121_out, OP0);
  not not_122 (not_122_out, OP5);
  not not_123 (not_123_out, OP4);
  not not_124 (not_124_out, OP1);
  not not_125 (not_125_out, OP0);
  not not_126 (not_126_out, OP5);
  not not_127 (not_127_out, OP4);
  not not_128 (not_128_out, OP2);
  not not_129 (not_129_out, OP1);
  not not_130 (not_130_out, OP5);
  not not_131 (not_131_out, OP4);
  not not_132 (not_132_out, OP2);
  not not_133 (not_133_out, OP0);
  not not_134 (not_134_out, OP5);
  not not_135 (not_135_out, OP4);
  not not_136 (not_136_out, OP1);
  not not_137 (not_137_out, OP4);
  not not_138 (not_138_out, OP3);
  not not_139 (not_139_out, OP2);
  not not_140 (not_140_out, OP4);
  not not_141 (not_141_out, OP2);
  not not_142 (not_142_out, OP5);
  not not_143 (not_143_out, OP4);
  not not_144 (not_144_out, OP3);
  not not_145 (not_145_out, OP2);
  not not_146 (not_146_out, OP1);
  not not_147 (not_147_out, OP0);
  not not_148 (not_148_out, F5);
  not not_149 (not_149_out, F4);
  not not_150 (not_150_out, F3);
  not not_151 (not_151_out, F0);
  not not_152 (not_152_out, OP5);
  not not_153 (not_153_out, OP4);
  not not_154 (not_154_out, OP3);
  not not_155 (not_155_out, OP2);
  not not_156 (not_156_out, OP1);
  not not_157 (not_157_out, OP0);
  not not_158 (not_158_out, F4);
  not not_159 (not_159_out, F3);
  not not_160 (not_160_out, F0);
  not not_161 (not_161_out, OP4);
  not not_162 (not_162_out, OP3);
  not not_163 (not_163_out, OP1);
  not not_164 (not_164_out, OP0);
  not not_165 (not_165_out, OP5);
  not not_166 (not_166_out, OP4);
  not not_167 (not_167_out, OP3);
  not not_168 (not_168_out, OP5);
  not not_169 (not_169_out, OP4);
  not not_170 (not_170_out, OP3);
  not not_171 (not_171_out, OP2);
  not not_172 (not_172_out, OP1);
  not not_173 (not_173_out, OP0);
  not not_174 (not_174_out, F5);
  not not_175 (not_175_out, F4);
  not not_176 (not_176_out, F3);
  not not_177 (not_177_out, F2);
  not not_178 (not_178_out, F1);
  not not_179 (not_179_out, F0);
  not not_180 (not_180_out, OP5);
  not not_181 (not_181_out, OP4);
  not not_182 (not_182_out, OP3);
  not not_183 (not_183_out, OP2);
  not not_184 (not_184_out, OP1);
  not not_185 (not_185_out, OP0);
  not not_186 (not_186_out, F5);
  not not_187 (not_187_out, F4);
  not not_188 (not_188_out, F3);
  not not_189 (not_189_out, F2);
  not not_190 (not_190_out, OP5);
  not not_191 (not_191_out, OP4);
  not not_192 (not_192_out, OP3);
  not not_193 (not_193_out, OP2);
  not not_194 (not_194_out, OP1);
  not not_195 (not_195_out, OP0);
  not not_196 (not_196_out, F5);
  not not_197 (not_197_out, F4);
  not not_198 (not_198_out, F3);
  not not_199 (not_199_out, F2);
  not not_200 (not_200_out, F0);
  not not_201 (not_201_out, OP5);
  not not_202 (not_202_out, OP4);
  not not_203 (not_203_out, OP3);
  not not_204 (not_204_out, OP2);
  not not_205 (not_205_out, OP1);
  not not_206 (not_206_out, OP0);
  not not_207 (not_207_out, F4);
  not not_208 (not_208_out, F3);
  not not_209 (not_209_out, F2);
  not not_210 (not_210_out, F1);
  not not_211 (not_211_out, F0);
  not not_212 (not_212_out, OP5);
  not not_213 (not_213_out, OP4);
  not not_214 (not_214_out, OP3);
  not not_215 (not_215_out, OP2);
  not not_216 (not_216_out, OP1);
  not not_217 (not_217_out, OP0);
  not not_218 (not_218_out, F4);
  not not_219 (not_219_out, F3);
  not not_220 (not_220_out, F2);
  not not_221 (not_221_out, F1);
  not not_222 (not_222_out, OP5);
  not not_223 (not_223_out, OP4);
  not not_224 (not_224_out, OP3);
  not not_225 (not_225_out, OP2);
  not not_226 (not_226_out, OP1);
  not not_227 (not_227_out, OP0);
  not not_228 (not_228_out, F4);
  not not_229 (not_229_out, F3);
  not not_230 (not_230_out, F2);
  not not_231 (not_231_out, F0);
  not not_232 (not_232_out, OP5);
  not not_233 (not_233_out, OP4);
  not not_234 (not_234_out, OP3);
  not not_235 (not_235_out, OP2);
  not not_236 (not_236_out, OP1);
  not not_237 (not_237_out, OP0);
  not not_238 (not_238_out, F4);
  not not_239 (not_239_out, F3);
  not not_240 (not_240_out, F1);
  not not_241 (not_241_out, F0);
  not not_242 (not_242_out, OP5);
  not not_243 (not_243_out, OP4);
  not not_244 (not_244_out, OP3);
  not not_245 (not_245_out, OP2);
  not not_246 (not_246_out, OP1);
  not not_247 (not_247_out, OP0);
  not not_248 (not_248_out, F4);
  not not_249 (not_249_out, F3);
  not not_250 (not_250_out, F1);
  not not_251 (not_251_out, OP5);
  not not_252 (not_252_out, OP4);
  not not_253 (not_253_out, OP3);
  not not_254 (not_254_out, OP2);
  not not_255 (not_255_out, OP1);
  not not_256 (not_256_out, OP0);
  not not_257 (not_257_out, F4);
  not not_258 (not_258_out, F3);
  not not_259 (not_259_out, OP5);
  not not_260 (not_260_out, OP4);
  not not_261 (not_261_out, OP3);
  not not_262 (not_262_out, OP2);
  not not_263 (not_263_out, OP1);
  not not_264 (not_264_out, OP0);
  not not_265 (not_265_out, F4);
  not not_266 (not_266_out, F2);
  not not_267 (not_267_out, F0);
  not not_268 (not_268_out, OP5);
  not not_269 (not_269_out, OP4);
  not not_270 (not_270_out, OP3);
  not not_271 (not_271_out, OP2);
  not not_272 (not_272_out, OP1);
  not not_273 (not_273_out, OP0);
  not not_274 (not_274_out, F4);
  not not_275 (not_275_out, F2);
  not not_276 (not_276_out, OP5);
  not not_277 (not_277_out, OP4);
  not not_278 (not_278_out, OP3);
  not not_279 (not_279_out, OP2);
  not not_280 (not_280_out, OP1);
  not not_281 (not_281_out, OP0);
  not not_282 (not_282_out, F5);
  not not_283 (not_283_out, F4);
  not not_284 (not_284_out, F1);
  not not_285 (not_285_out, F0);
  not not_286 (not_286_out, OP5);
  not not_287 (not_287_out, OP4);
  not not_288 (not_288_out, OP3);
  not not_289 (not_289_out, OP1);
  not not_290 (not_290_out, OP0);
  not not_291 (not_291_out, OP5);
  not not_292 (not_292_out, OP4);
  not not_293 (not_293_out, OP3);
  not not_294 (not_294_out, OP1);
  not not_295 (not_295_out, OP4);
  not not_296 (not_296_out, OP2);
  not not_297 (not_297_out, OP5);
  not not_298 (not_298_out, OP4);
  not not_299 (not_299_out, OP3);
  not not_300 (not_300_out, OP2);
  not not_301 (not_301_out, OP1);
  not not_302 (not_302_out, OP0);
  not not_303 (not_303_out, F5);
  not not_304 (not_304_out, F4);
  not not_305 (not_305_out, F3);
  not not_306 (not_306_out, F0);
  not not_307 (not_307_out, OP5);
  not not_308 (not_308_out, OP4);
  not not_309 (not_309_out, OP3);
  not not_310 (not_310_out, OP2);
  not not_311 (not_311_out, OP1);
  not not_312 (not_312_out, OP0);
  not not_313 (not_313_out, F4);
  not not_314 (not_314_out, F3);
  not not_315 (not_315_out, F0);
  and and_1 (and_1_out, not_1_out, not_2_out, not_3_out, not_4_out, not_5_out, not_6_out, not_7_out, not_8_out, not_9_out, not_10_out, F1, not_11_out);
  and and_2 (and_2_out, not_12_out, not_13_out, not_14_out, not_15_out, not_16_out, not_17_out, F5, not_18_out, not_19_out, not_20_out, not_21_out, not_22_out);
  and and_3 (and_3_out, not_23_out, not_24_out, not_25_out, not_26_out, not_27_out, not_28_out, F5, not_29_out, not_30_out, not_31_out, not_32_out, F0);
  and and_4 (and_4_out, not_33_out, not_34_out, not_35_out, not_36_out, not_37_out, not_38_out, F5, not_39_out, not_40_out, not_41_out, F1, not_42_out);
  and and_5 (and_5_out, not_43_out, not_44_out, not_45_out, not_46_out, not_47_out, not_48_out, F5, not_49_out, not_50_out, F2, not_51_out, not_52_out);
  and and_6 (and_6_out, not_53_out, not_54_out, not_55_out, not_56_out, not_57_out, not_58_out, F5, not_59_out, not_60_out, F2, not_61_out, F0);
  and and_7 (and_7_out, not_62_out, not_63_out, not_64_out, not_65_out, not_66_out, not_67_out, F5, not_68_out, not_69_out, F2, F1, F0);
  and and_8 (and_8_out, not_70_out, not_71_out, not_72_out, not_73_out, not_74_out, not_75_out, F5, not_76_out, F3, not_77_out, F1, not_78_out);
  and and_9 (and_9_out, not_79_out, not_80_out, not_81_out, not_82_out, not_83_out, not_84_out, F5, not_85_out, F3, not_86_out, F1, F0);
  and and_10 (and_10_out, not_87_out, not_88_out, not_89_out, not_90_out, not_91_out, not_92_out, not_93_out, not_94_out, F3, not_95_out, not_96_out, not_97_out);
  and and_11 (and_11_out, not_98_out, not_99_out, not_100_out, not_101_out, not_102_out, not_103_out, not_104_out, not_105_out, F3, F2, not_106_out, not_107_out);
  and and_12 (and_12_out, not_108_out, not_109_out, not_110_out, OP2, not_111_out, not_112_out);
  and and_13 (and_13_out, not_113_out, not_114_out, not_115_out, OP2, not_116_out, OP0);
  and and_14 (and_14_out, not_117_out, not_118_out, OP3, not_119_out, not_120_out, not_121_out);
  and and_15 (and_15_out, not_122_out, not_123_out, OP3, OP2, not_124_out, not_125_out);
  and and_16 (and_16_out, not_126_out, not_127_out, OP3, not_128_out, not_129_out, OP0);
  and and_17 (and_17_out, not_130_out, not_131_out, OP3, not_132_out, OP1, not_133_out);
  and and_18 (and_18_out, not_134_out, not_135_out, OP3, OP2, not_136_out, OP0);
  and and_19 (and_19_out, OP5, not_137_out, not_138_out, not_139_out, OP1, OP0);
  and and_20 (and_20_out, OP5, not_140_out, OP3, not_141_out, OP1, OP0);
  and and_21 (and_21_out, not_142_out, not_143_out, not_144_out, not_145_out, not_146_out, not_147_out, not_148_out, not_149_out, not_150_out, F2, F1, not_151_out);
  and and_22 (and_22_out, not_152_out, not_153_out, not_154_out, not_155_out, not_156_out, not_157_out, F5, not_158_out, not_159_out, F2, F1, not_160_out);
  and and_23 (and_23_out, OP5, not_161_out, not_162_out, OP2, not_163_out, not_164_out);
  and and_24 (and_24_out, not_165_out, not_166_out, not_167_out, OP2, OP1, OP0);
  and and_25 (and_25_out, not_168_out, not_169_out, not_170_out, not_171_out, not_172_out, not_173_out, not_174_out, not_175_out, not_176_out, not_177_out, not_178_out, not_179_out);
  and and_26 (and_26_out, not_180_out, not_181_out, not_182_out, not_183_out, not_184_out, not_185_out, not_186_out, not_187_out, not_188_out, not_189_out, F1, F0);
  and and_27 (and_27_out, not_190_out, not_191_out, not_192_out, not_193_out, not_194_out, not_195_out, not_196_out, not_197_out, not_198_out, not_199_out, F1, not_200_out);
  and and_28 (and_28_out, not_201_out, not_202_out, not_203_out, not_204_out, not_205_out, not_206_out, F5, not_207_out, not_208_out, not_209_out, not_210_out, not_211_out);
  and and_29 (and_29_out, not_212_out, not_213_out, not_214_out, not_215_out, not_216_out, not_217_out, F5, not_218_out, not_219_out, not_220_out, not_221_out, F0);
  and and_30 (and_30_out, not_222_out, not_223_out, not_224_out, not_225_out, not_226_out, not_227_out, F5, not_228_out, not_229_out, not_230_out, F1, not_231_out);
  and and_31 (and_31_out, not_232_out, not_233_out, not_234_out, not_235_out, not_236_out, not_237_out, F5, not_238_out, not_239_out, F2, not_240_out, not_241_out);
  and and_32 (and_32_out, not_242_out, not_243_out, not_244_out, not_245_out, not_246_out, not_247_out, F5, not_248_out, not_249_out, F2, not_250_out, F0);
  and and_33 (and_33_out, not_251_out, not_252_out, not_253_out, not_254_out, not_255_out, not_256_out, F5, not_257_out, not_258_out, F2, F1, F0);
  and and_34 (and_34_out, not_259_out, not_260_out, not_261_out, not_262_out, not_263_out, not_264_out, F5, not_265_out, F3, not_266_out, F1, not_267_out);
  and and_35 (and_35_out, not_268_out, not_269_out, not_270_out, not_271_out, not_272_out, not_273_out, F5, not_274_out, F3, not_275_out, F1, F0);
  and and_36 (and_36_out, not_276_out, not_277_out, not_278_out, not_279_out, not_280_out, not_281_out, not_282_out, not_283_out, F3, F2, not_284_out, not_285_out);
  and and_37 (and_37_out, not_286_out, not_287_out, not_288_out, OP2, not_289_out, not_290_out);
  and and_38 (and_38_out, not_291_out, not_292_out, not_293_out, OP2, not_294_out, OP0);
  and and_39 (and_39_out, OP5, not_295_out, OP3, not_296_out, OP1, OP0);
  and and_40 (and_40_out, not_297_out, not_298_out, not_299_out, not_300_out, not_301_out, not_302_out, not_303_out, not_304_out, not_305_out, F2, F1, not_306_out);
  and and_41 (and_41_out, not_307_out, not_308_out, not_309_out, not_310_out, not_311_out, not_312_out, F5, not_313_out, not_314_out, F2, F1, not_315_out);
  or or_1 (R1_Used, and_1_out, and_2_out, and_3_out, and_4_out, and_5_out, and_6_out, and_7_out, and_8_out, and_9_out, and_10_out, and_11_out, and_12_out, and_13_out, and_14_out, and_15_out, and_16_out, and_17_out, and_18_out, and_19_out, and_20_out, and_21_out, and_22_out, and_23_out, and_24_out);
  or or_2 (R2_Used, and_25_out, and_26_out, and_27_out, and_28_out, and_29_out, and_30_out, and_31_out, and_32_out, and_33_out, and_34_out, and_35_out, and_36_out, and_37_out, and_38_out, and_39_out, and_40_out, and_41_out);
endmodule

module \数据相关检测  (
  input  MEM_RegWrite,
  input  EX_RegWrite,
  input  R2_Used,
  input  R1_Used,
  input  [4:0] R1_num,
  input  [4:0] R2_num,
  input  [4:0] EX_WriteReg_num,
  input  [4:0] MEM_WriteReg_num,
  output OUTPUT
);

  wire and_1_out, and_2_out, and_3_out, and_4_out, comparator_1_eq, comparator_2_eq, comparator_3_eq,
       comparator_4_eq, comparator_5_eq, comparator_6_eq, not_1_out, not_2_out;

  Comparator #(.width(5), .mode("twosComplement")) comparator_1 (
    .a(R1_num), .b(EX_WriteReg_num), .eq(comparator_1_eq));  // open: gt, lt
  Comparator #(.width(5), .mode("twosComplement")) comparator_2 (
    .a(R1_num), .b(MEM_WriteReg_num), .eq(comparator_2_eq));  // open: gt, lt
  Comparator #(.width(5), .mode("twosComplement")) comparator_3 (
    .a(R2_num), .b(EX_WriteReg_num), .eq(comparator_3_eq));  // open: gt, lt
  Comparator #(.width(5), .mode("twosComplement")) comparator_4 (
    .a(R2_num), .b(MEM_WriteReg_num), .eq(comparator_4_eq));  // open: gt, lt
  Comparator #(.width(5), .mode("twosComplement")) comparator_5 (
    .a(R1_num), .b({5{1'b0}}), .eq(comparator_5_eq));  // open: gt, lt
  Comparator #(.width(5), .mode("twosComplement")) comparator_6 (
    .a(R2_num), .b({5{1'b0}}), .eq(comparator_6_eq));  // open: gt, lt
  not not_1 (not_1_out, comparator_5_eq);
  not not_2 (not_2_out, comparator_6_eq);
  and and_1 (and_1_out, not_1_out, R1_Used, comparator_1_eq, EX_RegWrite);
  and and_2 (and_2_out, R1_Used, comparator_2_eq, MEM_RegWrite, not_1_out);
  and and_3 (and_3_out, R2_Used, comparator_3_eq, EX_RegWrite, not_2_out);
  and and_4 (and_4_out, R2_Used, comparator_4_eq, MEM_RegWrite, not_2_out);
  or or_1 (OUTPUT, and_1_out, and_2_out, and_3_out, and_4_out);
endmodule

module \LOAD_USE检测  (
  input  EX_RegWrite,
  input  R2_Used,
  input  R1_Used,
  input  [4:0] R1_num,
  input  [4:0] R2_num,
  input  [4:0] EX_WriteReg_num,
  input  [5:0] OP,
  output OUTPUT
);

  wire and_1_out, and_2_out, comparator_1_eq, comparator_2_eq, comparator_3_eq, comparator_4_eq,
       comparator_5_eq, comparator_6_eq, not_1_out, not_2_out, or_1_out;

  Comparator #(.width(6), .mode("twosComplement")) comparator_1 (
    .a(OP), .b(6'b100011), .eq(comparator_1_eq));  // open: gt, lt
  Comparator #(.width(6), .mode("twosComplement")) comparator_2 (
    .a(OP), .b(6'b100100), .eq(comparator_2_eq));  // open: gt, lt
  Comparator #(.width(5), .mode("twosComplement")) comparator_3 (
    .a(R1_num), .b(EX_WriteReg_num), .eq(comparator_3_eq));  // open: gt, lt
  Comparator #(.width(5), .mode("twosComplement")) comparator_4 (
    .a(R2_num), .b(EX_WriteReg_num), .eq(comparator_4_eq));  // open: gt, lt
  not not_1 (not_1_out, comparator_5_eq);
  Comparator #(.width(5), .mode("twosComplement")) comparator_5 (
    .a(R1_num), .b({5{1'b0}}), .eq(comparator_5_eq));  // open: gt, lt
  Comparator #(.width(5), .mode("twosComplement")) comparator_6 (
    .a(R2_num), .b({5{1'b0}}), .eq(comparator_6_eq));  // open: gt, lt
  not not_2 (not_2_out, comparator_6_eq);
  or or_1 (or_1_out, comparator_1_eq, comparator_2_eq);
  and and_1 (and_1_out, R1_Used, comparator_3_eq, or_1_out, not_1_out, EX_RegWrite);
  and and_2 (and_2_out, R2_Used, comparator_4_eq, or_1_out, EX_RegWrite, not_2_out);
  or or_2 (OUTPUT, and_1_out, and_2_out);
endmodule

module \重定向相关  (
  input  MEM_RegWrite,
  input  EX_RegWrite,
  input  R2_Used,
  input  R1_Used,
  input  [4:0] R1_num,
  input  [4:0] R2_num,
  input  [4:0] EX_WriteReg_num,
  input  [4:0] MEM_WriteReg_num,
  input  [5:0] OP,
  output [1:0] A_Choose,
  output [1:0] B_Choose
);

  wire and_3_out, and_4_out, comparator_1_eq, comparator_2_eq, comparator_3_eq, comparator_4_eq,
       comparator_5_eq, comparator_6_eq, comparator_7_eq, comparator_8_eq, EX_R1, EX_R2, MEM_ALU_1,
       MEM_ALU_2, MEM_MD_R1, MEM_MD_R2, nor_1_out, nor_2_out, not_1_out, not_2_out, not_3_out, not_4_out,
       not_5_out, not_6_out, or_1_out;

  Comparator #(.width(5), .mode("twosComplement")) comparator_1 (
    .a(R1_num), .b(EX_WriteReg_num), .eq(comparator_1_eq));  // open: gt, lt
  Comparator #(.width(5), .mode("twosComplement")) comparator_2 (
    .a(R2_num), .b(EX_WriteReg_num), .eq(comparator_2_eq));  // open: gt, lt
  Comparator #(.width(5), .mode("twosComplement")) comparator_3 (
    .a(R1_num), .b({5{1'b0}}), .eq(comparator_3_eq));  // open: gt, lt
  Comparator #(.width(5), .mode("twosComplement")) comparator_4 (
    .a(R2_num), .b({5{1'b0}}), .eq(comparator_4_eq));  // open: gt, lt
  Comparator #(.width(5), .mode("twosComplement")) comparator_5 (
    .a(R1_num), .b(MEM_WriteReg_num), .eq(comparator_5_eq));  // open: gt, lt
  Comparator #(.width(6), .mode("twosComplement")) comparator_6 (
    .a(OP), .b(6'b100011), .eq(comparator_6_eq));  // open: gt, lt
  Comparator #(.width(5), .mode("twosComplement")) comparator_7 (
    .a(R2_num), .b(MEM_WriteReg_num), .eq(comparator_7_eq));  // open: gt, lt
  Comparator #(.width(6), .mode("twosComplement")) comparator_8 (
    .a(OP), .b(6'b100100), .eq(comparator_8_eq));  // open: gt, lt
  not not_1 (not_1_out, comparator_1_eq);
  not not_2 (not_2_out, comparator_2_eq);
  not not_3 (not_3_out, comparator_3_eq);
  not not_4 (not_4_out, comparator_4_eq);
  and and_1 (EX_R1, comparator_1_eq, R1_Used, EX_RegWrite, not_3_out);
  and and_2 (EX_R2, comparator_2_eq, R2_Used, not_4_out, EX_RegWrite);
  and and_3 (and_3_out, not_3_out, R1_Used, not_1_out, comparator_5_eq, MEM_RegWrite);
  or or_1 (or_1_out, comparator_6_eq, comparator_8_eq);
  and and_4 (and_4_out, MEM_RegWrite, R2_Used, not_2_out, comparator_7_eq, not_4_out);
  not not_5 (not_5_out, or_1_out);
  not not_6 (not_6_out, or_1_out);
  assign A_Choose = nor_1_out ? 2'b00 : 2'bz;  // Controlled_Buffer controlled_buffer_1
  nor nor_1 (nor_1_out, EX_R1, MEM_ALU_1, MEM_MD_R1);
  and and_5 (MEM_ALU_1, and_3_out, not_5_out);
  and and_6 (MEM_MD_R1, and_3_out, or_1_out);
  and and_7 (MEM_MD_R2, or_1_out, and_4_out);
  and and_8 (MEM_ALU_2, not_6_out, and_4_out);
  assign A_Choose = EX_R1 ? 2'b01 : 2'bz;  // Controlled_Buffer controlled_buffer_2
  assign B_Choose = nor_2_out ? 2'b00 : 2'bz;  // Controlled_Buffer controlled_buffer_3
  nor nor_2 (nor_2_out, EX_R2, MEM_ALU_2, MEM_MD_R2);
  assign A_Choose = MEM_ALU_1 ? 2'b10 : 2'bz;  // Controlled_Buffer controlled_buffer_4
  assign B_Choose = EX_R2 ? 2'b01 : 2'bz;  // Controlled_Buffer controlled_buffer_5
  assign A_Choose = MEM_MD_R1 ? 2'b11 : 2'bz;  // Controlled_Buffer controlled_buffer_6
  assign B_Choose = MEM_ALU_2 ? 2'b10 : 2'bz;  // Controlled_Buffer controlled_buffer_7
  assign B_Choose = MEM_MD_R2 ? 2'b11 : 2'bz;  // Controlled_Buffer controlled_buffer_8
endmodule

module \单周期MIPS_单级中断  (
  input  IR1,
  input  IR2,
  input  IR3,
  output RegWrite,
  output MemWrite,
  output [31:0] PC,
  output [31:0] IR,
  output [31:0] RDin,
  output [31:0] MDin,
  output [31:0] LedData
);

  wire and_1_out, and_2_out, and_3_out, and_9_out, and_13_out, and_14_out, and_15_out, and_18_out, Beq, BGTZ,
       Bne, branch, CLK, comparator_1_eq, comparator_2_eq, comparator_3_eq, comparator_4_eq, comparator_5_eq,
       d_ff_1_q, d_ff_2_q, d_ff_3_q, decoder_1_out1, decoder_1_out2, decoder_1_out3, equal, ERET, EX1, EX2,
       EX3, Go, IE_q, IR1_t, IR2_t, IR3_t, IR_CPU, IRA, IRB, IRC, IRQ, JAL, JMP, JR, LBU, MFC0,
       mips_alu_1_equal, MTC0, not_1_out, not_2_out, not_3_out, not_4_out, not_5_out, not_6_out, not_7_out,
       not_8_out, not_9_out, or_4_out, or_5_out, or_6_out, or_7_out, or_13_out, rst1, rst2, rst3, SignedExt,
       SRLV, stop, Syscall, W1, W2, W3, \单周期硬布线控制器_1_alu_src , \单周期硬布线控制器_1_memtoreg , \单周期硬布线控制器_1_regdst ;
  wire [1:0] curr_xy, priority_encoder_1_out;
  wire [3:0] \单周期硬布线控制器_1_alu_op ;
  wire [4:0] multiplexer_7_out, multiplexer_8_out, multiplexer_9_out, multiplexer_10_out, multiplexer_14_out;
  wire [15:0] \总周期数 , \无条件 , \有条件 ;
  wire [31:0] adder_2_out, and_16_out, bit_extender_1_out, bit_extender_2_out, bit_extender_3_out, EPC, JPC,
       JRPC, mips_alu_1_result, multiplexer_1_out, multiplexer_2_out, multiplexer_3_out, multiplexer_4_out,
       multiplexer_5_out, multiplexer_6_out, multiplexer_11_out, multiplexer_12_out, multiplexer_13_out,
       multiplexer_16_out, multiplexer_17_out, multiplexer_18_out, multiplexer_19_out, multiplexer_20_out,
       PC_4, PC_OUT, ram_1_data, shifter_1_out, shifter_2_out, shifter_3_out, shifter_4_out;

  Clock #(.highDuration(1), .lowDuration(1)) clock_1 (.out(CLK));
  Button _1 (.out(IRA));
  Button _2 (.out(IRB));
  Button _3 (.out(IRC));
  Button \u_继续运行  (.out(Go));
  LED #(.active("true")) led_1 (.in(W1));
  LED #(.active("true")) led_2 (.in(W2));
  LED #(.active("true")) led_3 (.in(W3));
  Hex_Digit_Display hex_digit_display_1 (.value(LedData[31:28]));  // open: dp
  Hex_Digit_Display hex_digit_display_2 (.value(LedData[27:24]));  // open: dp
  Hex_Digit_Display hex_digit_display_3 (.value(LedData[23:20]));  // open: dp
  D_Flip_Flop #(.trigger("rising"), .Pre_Clr_Positions("LEGACY"), .NegatePresetClear("false"), .enable("true"), .NewFFLayout("false")) d_ff_1 (
    .clk(IR1_t), .D(1'b1), .Q(d_ff_1_q), .reset(EX1));  // open: Qn, preset, en
  or or_1 (W1, EX1, d_ff_1_q);
  D_Flip_Flop #(.trigger("rising"), .Pre_Clr_Positions("LEGACY"), .NegatePresetClear("false"), .enable("true"), .NewFFLayout("false")) d_ff_2 (
    .clk(IR2_t), .D(1'b1), .Q(d_ff_2_q), .reset(EX2));  // open: Qn, preset, en
  or or_2 (W2, EX2, d_ff_2_q);
  D_Flip_Flop #(.trigger("rising"), .Pre_Clr_Positions("LEGACY"), .NegatePresetClear("false"), .enable("true"), .NewFFLayout("false")) d_ff_3 (
    .clk(IR3_t), .D(1'b1), .Q(d_ff_3_q), .reset(EX3));  // open: Qn, preset, en
  or or_3 (W3, EX3, d_ff_3_q);
  Hex_Digit_Display hex_digit_display_4 (.value(LedData[19:16]));  // open: dp
  Hex_Digit_Display hex_digit_display_5 (.value(LedData[15:12]));  // open: dp
  Multiplexer #(.select(1), .width(32), .disabled("Z"), .enable("false")) multiplexer_1 (
    .in0(PC_4), .in1(adder_2_out), .out(multiplexer_1_out), .sel(branch));
  Hex_Digit_Display hex_digit_display_6 (.value(LedData[7:4]));  // open: dp
  Hex_Digit_Display hex_digit_display_7 (.value(LedData[11:8]));  // open: dp
  // Probe on \总周期数 
  Multiplexer #(.select(1), .width(32), .disabled("Z"), .enable("false")) multiplexer_2 (
    .in0(multiplexer_1_out), .in1(PC_OUT), .out(multiplexer_2_out), .sel(IR_CPU));
  Multiplexer #(.select(1), .width(32), .disabled("Z"), .enable("false")) multiplexer_3 (
    .in0(multiplexer_2_out), .in1(EPC), .out(multiplexer_3_out), .sel(ERET));
  // Probe on JRPC
  or or_4 (or_4_out, d_ff_1_q, EX1);
  or or_5 (or_5_out, d_ff_2_q, EX2);
  or or_6 (or_6_out, d_ff_3_q, EX3);
  Hex_Digit_Display hex_digit_display_8 (.value(LedData[3:0]));  // open: dp
  Multiplexer #(.select(1), .width(32), .disabled("Z"), .enable("false")) multiplexer_4 (
    .in0(multiplexer_3_out), .in1(JPC), .out(multiplexer_4_out), .sel(JMP));
  and and_1 (and_1_out, or_4_out, not_1_out);
  not not_1 (not_1_out, rst1);
  and and_2 (and_2_out, or_5_out, not_2_out);
  not not_2 (not_2_out, rst2);
  and and_3 (and_3_out, or_6_out, not_3_out);
  not not_3 (not_3_out, rst3);
  // Probe on PC
  not not_4 (not_4_out, stop);
  or or_7 (or_7_out, Go, not_4_out);
  // Probe on multiplexer_5_out
  Multiplexer #(.select(1), .width(32), .disabled("Z"), .enable("false")) multiplexer_5 (
    .in0(multiplexer_4_out), .in1(JRPC), .out(multiplexer_5_out), .sel(JR));
  Comparator #(.width(32), .mode("twosComplement")) comparator_1 (
    .a(JRPC), .b(32'h22), .eq(comparator_1_eq));  // open: gt, lt
  D_Flip_Flop #(.trigger("rising"), .Pre_Clr_Positions("LEGACY"), .NegatePresetClear("false"), .enable("true"), .NewFFLayout("false")) u_IR1 (
    .clk(CLK), .D(and_1_out), .Q(EX1));  // open: Qn, preset, en, reset
  D_Flip_Flop #(.trigger("rising"), .Pre_Clr_Positions("LEGACY"), .NegatePresetClear("false"), .enable("true"), .NewFFLayout("false")) u_IR2 (
    .clk(CLK), .D(and_2_out), .Q(EX2));  // open: Qn, preset, en, reset
  D_Flip_Flop #(.trigger("rising"), .Pre_Clr_Positions("LEGACY"), .NegatePresetClear("false"), .enable("true"), .NewFFLayout("false")) u_IR3 (
    .clk(CLK), .D(and_3_out), .Q(EX3));  // open: Qn, preset, en, reset
  or or_8 (IR1_t, IR1, IRA);
  Register #(.width(32), .trigger("rising"), .Select("low")) u_PC (
    .D(multiplexer_5_out), .en(or_7_out), .Q(PC), .clk(CLK));  // open: clr
  and and_4 (equal, Syscall, comparator_1_eq);
  and and_5 (stop, Syscall, not_5_out);
  not not_5 (not_5_out, comparator_1_eq);
  or or_9 (IR2_t, IR2, IRB);
  Counter #(.width(16), .max('hffff), .ongoal("wrap"), .trigger("rising"), .behavior("old")) counter_1 (
    .D({16{1'b0}}), .count(or_7_out), .Q(\总周期数 ), .clk(CLK));  // open: load, carry, clr, preset
  // Mips_Probe mips_probe_1: pin names not known; wires that end beside it: IR
  // Probe on IR
  ROM #(.addrWidth(10), .dataWidth(32), .Select("high")) rom_1 (.addr(PC[11:2]), .data(IR));
  Adder #(.width(32)) adder_1 (.a(PC), .b(32'h4), .out(PC_4));  // open: cin, cout
  or or_10 (IR3_t, IR3, IRC);
  Multiplexer #(.select(1), .width(32), .disabled("Z"), .enable("false")) multiplexer_6 (
    .in1(MDin), .out(multiplexer_6_out), .sel(equal));  // open: in0
  // Probe on MDin
  Comparator #(.width(6), .mode("twosComplement")) comparator_2 (
    .a(IR[31:26]), .b(6'b010000), .eq(comparator_2_eq));  // open: gt, lt
  Comparator #(.width(6), .mode("twosComplement")) comparator_3 (
    .a(IR[5:0]), .b(6'b011000), .eq(comparator_3_eq));  // open: gt, lt
  Comparator #(.width(5), .mode("twosComplement")) comparator_4 (
    .a(IR[25:21]), .b(5'b00100), .eq(comparator_4_eq));  // open: gt, lt
  Comparator #(.width(5), .mode("twosComplement")) comparator_5 (
    .a(IR[25:21]), .b({5{1'b0}}), .eq(comparator_5_eq));  // open: gt, lt
  and and_6 (ERET, comparator_2_eq, comparator_3_eq);
  and and_7 (MTC0, comparator_2_eq, comparator_4_eq);
  and and_8 (MFC0, comparator_2_eq, comparator_5_eq);
  \单周期硬布线控制器  \u_单周期硬布线控制器_1  (
    .Func(IR[5:0]), .OP(IR[31:26]), .ALU_OP(\单周期硬布线控制器_1_alu_op ), .MemToReg(\单周期硬布线控制器_1_memtoreg ),
    .MemWrite(MemWrite), .ALU_SRC(\单周期硬布线控制器_1_alu_src ), .RegWrite(RegWrite), .SysCALL(Syscall),
    .SignedExt(SignedExt), .RegDst(\单周期硬布线控制器_1_regdst ), .JR(JR), .JMP(JMP), .Beq(Beq), .JAL(JAL),
    .Bne(Bne), .SRLV(SRLV), .LBU(LBU), .BGTZ(BGTZ));
  Multiplexer #(.select(1), .width(5), .disabled("Z"), .enable("false")) multiplexer_7 (
    .in0(IR[20:16]), .in1(IR[15:11]), .out(multiplexer_7_out), .sel(\单周期硬布线控制器_1_regdst ));
  assign bit_extender_1_out = {{6{1'b0}}, IR[25:0]};  // Bit_Extender bit_extender_1
  assign bit_extender_2_out = {{16{1'b0}}, IR[15:0]};  // Bit_Extender bit_extender_2
  assign bit_extender_3_out = {{16{IR[15]}}, IR[15:0]};  // Bit_Extender bit_extender_3
  Register #(.width(32), .trigger("rising"), .Select("low")) register_1 (
    .D(multiplexer_6_out), .Q(LedData), .clk(CLK));  // open: en, clr
  or or_11 (branch, and_9_out, and_14_out, and_13_out);
  Multiplexer #(.select(1), .width(5), .disabled("Z"), .enable("false")) multiplexer_8 (
    .in0(IR[25:21]), .in1(5'b00010), .out(multiplexer_8_out), .sel(Syscall));
  Multiplexer #(.select(1), .width(5), .disabled("Z"), .enable("false")) multiplexer_9 (
    .in0(IR[20:16]), .in1(5'b00100), .out(multiplexer_9_out), .sel(Syscall));
  Multiplexer #(.select(1), .width(5), .disabled("Z"), .enable("false")) multiplexer_10 (
    .in0(multiplexer_7_out), .in1({5{1'b1}}), .out(multiplexer_10_out), .sel(JAL));
  MIPS_Regifile mips_regifile_1 (
    .Din(RDin), .Clk(CLK), .R1(JRPC), .R2(MDin), .WE(RegWrite), .W_num(multiplexer_10_out),
    .R1_num(multiplexer_8_out), .R2_num(multiplexer_9_out));
  Shifter #(.width(32), .shift("ll")) shifter_1 (.in(bit_extender_1_out), .\dist (5'b00010), .out(shifter_1_out));
  Multiplexer #(.select(1), .width(32), .disabled("Z"), .enable("false")) multiplexer_11 (
    .in0(bit_extender_2_out), .in1(bit_extender_3_out), .out(multiplexer_11_out), .sel(SignedExt));
  Shifter #(.width(32), .shift("ll")) shifter_2 (.in(bit_extender_3_out), .\dist (5'b00010), .out(shifter_2_out));
  and and_9 (and_9_out, Bne, not_6_out);
  not not_6 (not_6_out, mips_alu_1_equal);
  Multiplexer #(.select(1), .width(32), .disabled("Z"), .enable("false")) multiplexer_12 (
    .in0(MDin), .in1(multiplexer_11_out), .out(multiplexer_12_out), .sel(\单周期硬布线控制器_1_alu_src ));
  assign JPC = shifter_1_out | {PC_4[31:28], {28{1'b0}}};  // OR_Gate or_12, 32 bits wide
  Adder #(.width(32)) adder_2 (.a(shifter_2_out), .b(PC_4), .out(adder_2_out));  // open: cin, cout
  Counter #(.width(16), .max('hffff), .ongoal("wrap"), .trigger("rising"), .behavior("old")) counter_2 (
    .D({16{1'b0}}), .count(JMP), .Q(\无条件 ), .clk(CLK));  // open: load, carry, clr, preset
  Decoder #(.select(2), .tristate("false"), .disabled("Z"), .enable("false")) decoder_1 (
    .out1(decoder_1_out1), .out2(decoder_1_out2), .out3(decoder_1_out3), .sel(curr_xy));  // open: out0
  Multiplexer #(.select(1), .width(32), .disabled("Z"), .enable("false")) multiplexer_13 (
    .in0(JRPC), .in1(multiplexer_12_out), .out(multiplexer_13_out), .sel(SRLV));
  // Probe on \无条件 
  and and_10 (rst1, ERET, decoder_1_out1);
  and and_11 (rst2, decoder_1_out2, ERET);
  and and_12 (rst3, decoder_1_out3, ERET);
  and and_13 (and_13_out, Beq, mips_alu_1_equal);
  not not_7 (not_7_out, mips_alu_1_result[0]);
  MIPS_ALU mips_alu_1 (
    .X(multiplexer_13_out), .Y(multiplexer_12_out), .AluOP(\单周期硬布线控制器_1_alu_op ), .Equal(mips_alu_1_equal),
    .Result(mips_alu_1_result), .shamt(multiplexer_14_out));  // open: Result_2
  Multiplexer #(.select(1), .width(5), .disabled("Z"), .enable("false")) multiplexer_14 (
    .in0(IR[10:6]), .in1(JRPC[4:0]), .out(multiplexer_14_out), .sel(SRLV));
  and and_14 (and_14_out, not_7_out, not_8_out, BGTZ);
  not not_8 (not_8_out, mips_alu_1_equal);
  Multiplexer #(.select(1), .width(32), .disabled("Z"), .enable("false")) multiplexer_15 (
    .in0(multiplexer_20_out), .in1(PC_4), .out(RDin), .sel(JAL));
  Counter #(.width(16), .max('hffff), .ongoal("wrap"), .trigger("rising"), .behavior("old")) counter_3 (
    .D({16{1'b0}}), .count(branch), .Q(\有条件 ), .clk(CLK));  // open: load, carry, clr, preset
  // Probe on \有条件 
  and and_15 (and_15_out, ~ERET, IR_CPU);  // AND_Gate
  RAM #(.addrWidth(10), .dataWidth(32), .bus("separate"), .Select("high")) ram_1 (
    .addr(mips_alu_1_result[11:2]), .din(MDin), .data(ram_1_data), .str(MemWrite), .sel(1'b1), .clk(CLK));  // open: ld, clr
  Register #(.width(32), .trigger("rising"), .Select("low")) u_EPC (
    .D(multiplexer_19_out), .en(and_15_out), .Q(EPC), .clk(CLK));  // open: clr
  Multiplexer #(.select(1), .width(32), .disabled("Z"), .enable("false")) multiplexer_16 (
    .in0(mips_alu_1_result), .in1(ram_1_data), .out(multiplexer_16_out), .sel(\单周期硬布线控制器_1_memtoreg ));
  Shifter #(.width(32), .shift("ll")) shifter_3 (
    .in(32'hff), .\dist ({mips_alu_1_result[1:0], 3'b000}), .out(shifter_3_out));
  Multiplexer #(.select(1), .width(32), .disabled("Z"), .enable("false")) multiplexer_17 (
    .in0(PC_4), .in1(adder_2_out), .out(multiplexer_17_out), .sel(branch));
  Register #(.width(1), .trigger("rising"), .Select("low")) IE (
    .D(IR_CPU), .en(not_9_out), .Q(IE_q), .clk(CLK), .clr(or_13_out), .preset(MTC0));  // open: cs
  not not_9 (not_9_out, IE_q);
  assign and_16_out = multiplexer_16_out & shifter_3_out;  // AND_Gate and_16, 32 bits wide
  Shifter #(.width(32), .shift("lr")) shifter_4 (
    .in(and_16_out), .\dist ({mips_alu_1_result[1:0], 3'b000}), .out(shifter_4_out));
  Multiplexer #(.select(1), .width(32), .disabled("Z"), .enable("false")) multiplexer_18 (
    .in0(multiplexer_17_out), .in1(JPC), .out(multiplexer_18_out), .sel(JMP));
  or or_13 (or_13_out, ERET, MFC0);
  Multiplexer #(.select(1), .width(32), .disabled("Z"), .enable("false")) multiplexer_19 (
    .in0(multiplexer_18_out), .in1(JRPC), .out(multiplexer_19_out), .sel(JR));
  and and_17 (IR_CPU, IRQ, ~IE_q);  // AND_Gate
  Multiplexer #(.select(1), .width(32), .disabled("Z"), .enable("false")) multiplexer_20 (
    .in0(multiplexer_16_out), .in1(shifter_4_out), .out(multiplexer_20_out), .sel(LBU));
  Priority_Encoder #(.select(2), .disabled("Z")) priority_encoder_1 (
    .in0(1'b0), .in1(EX1), .in2(EX2), .in3(EX3), .out(priority_encoder_1_out), .gs(IRQ));  // open: en_out, en_in
  Register #(.width(2), .trigger("rising"), .Select("low")) EPC_2 (
    .D(priority_encoder_1_out), .Q(curr_xy), .clk(and_18_out));  // open: en, clr
  and and_18 (and_18_out, ~ERET, IR_CPU);  // AND_Gate
  Multiplexer #(.select(2), .width(32), .disabled("Z"), .enable("false")) multiplexer_21 (
    .in1(32'h30ac), .in2(32'h3150), .in3(32'h31f4), .out(PC_OUT), .sel(priority_encoder_1_out));  // open: in0

  // Other names for the same wires on the sheet: a0[31:0] = MDin; v0[31:0] = JRPC

  // Notes on the sheet:
  //   中断源
  //   中断等待指示
  //   总复位信号应将除ROM以外所有存储组件全部清零
  //   数码管输出
  //   数码管输出应该用寄存器锁存，否则显示数据只能一闪而过
  //   指令存储器
  //   contents of rom_1 (hex, n*v repeats v):
  //   201d07d0 20100001 109fc0 139fc3 8021 2012000c 24160008 26100001 3210000f 20080008 20090001 139900
  //   2709825 132020 20020022 c 1094022 1500fff9 22100001 2018000f 2188024 108700 20080008 20090001 139902
  //   2709825 132021 20020022 c 1094022 1500fff9 108702 2c9b022 12c00001 8000c07 4020 1084027 84400
  //   3508ffff 82021 20020022 c 8000c01 afa20000 23bd0004 afa40000 23bd0004 afb00000 23bd0004 afb30000
  //   23bd0004 afb40000 23bd0004 afb50000 23bd0004 afb60000 23bd0004 20160001 20140003 20150001 168020
  //   108100 2149825 132020 20020022 c 1600fffa 295a022 1680fff7 23bdfffc 8fb60000 23bdfffc 8fb50000
  //   23bdfffc 8fb40000 23bdfffc 8fb30000 23bdfffc 8fb00000 23bdfffc 8fa40000 23bdfffc 8fa20000 42000018
  //   afa20000 23bd0004 afa40000 23bd0004 afb00000 23bd0004 afb30000 23bd0004 afb40000 23bd0004 afb50000
  //   23bd0004 afb60000 23bd0004 20160002 20140003 20150001 168020 108100 2149825 132020 20020022 c
  //   1600fffa 295a022 1680fff7 23bdfffc 8fb60000 23bdfffc 8fb50000 23bdfffc 8fb40000 23bdfffc 8fb30000
  //   23bdfffc 8fb00000 23bdfffc 8fa40000 23bdfffc 8fa20000 42000018 afa20000 23bd0004 afa40000 23bd0004
  //   afb00000 23bd0004 afb30000 23bd0004 afb40000 23bd0004 afb50000 23bd0004 afb60000 23bd0004 20160003
  //   20140003 20150001 168020 108100 2149825 132020 20020022 c 1600fffa 295a022 1680fff7 23bdfffc
  //   8fb60000 23bdfffc 8fb50000 23bdfffc 8fb40000 23bdfffc 8fb30000 23bdfffc 8fb00000 23bdfffc 8fa40000
  //   23bdfffc 8fa20000 42000018
  //   OP
  //   Func
  //   rs
  //   指令字
  //   rt
  //   rd
  //   JMP
  //   JR
  //   OP
  //   Func
  //   Syscall
  //   Beq
  //   Bne
  //   MemToReg
  //   MemWrite
  //   AluOP
  //   AluSrcB
  //   RegWrite
  //   JAL
  //   RegDst
  //   为方便自动评测，需要输出PC，IR，寄存器堆写如数据RDin
  //   RAM写使能MemWrite、RAM写入数据MDin等信号
endmodule

// BHT表
module BHT (
  input  can,
  input  [31:0] PC,
  input  ex_hit,
  input  [31:0] EX_PC,
  input  CLK,
  input  [31:0] ADDR,
  input  \分支 ,
  output hit,
  output [1:0] Status,
  output [31:0] OUTADDR
);

  wire and_1_out, and_10_out, and_11_out, and_12_out, and_13_out, and_14_out, and_15_out, and_16_out,
       and_17_out, comparator_1_eq, comparator_2_eq, comparator_3_eq, comparator_4_eq, comparator_5_eq,
       comparator_6_eq, comparator_7_eq, comparator_8_eq, comparator_9_eq, comparator_10_eq,
       comparator_11_eq, comparator_12_eq, comparator_13_eq, comparator_14_eq, comparator_15_eq,
       comparator_16_eq, decoder_1_out0, decoder_1_out1, decoder_1_out2, decoder_1_out3, decoder_1_out4,
       decoder_1_out5, decoder_1_out6, decoder_1_out7, en1, en2, en3, en4, en5, en6, en7, en8, enable1,
       enable2, enable3, enable4, enable5, enable6, enable7, enable8, h1, h2, h3, h4, h5, h6, h7, h8, L1, L2,
       L3, L4, L5, L6, L7, L8, not_1_out, not_2_out, not_3_out, not_4_out, not_5_out, not_6_out, not_7_out,
       not_8_out, not_9_out, or_1_out, or_2_out, or_3_out, or_4_out, or_5_out, or_6_out, or_7_out, or_8_out,
       or_9_out, or_10_out, or_11_out, or_12_out, or_13_out, or_14_out, or_15_out, or_16_out, or_17_out,
       or_18_out, or_19_out, or_20_out, or_22_out, or_23_out, or_24_out, or_25_out, V1, V2, V3, V4, V5, V6,
       V7, V8, WRITE1, WRITE2, WRITE3, WRITE4, WRITE5, WRITE6, WRITE7, WRITE8, \命中 ;
  wire [1:0] \分支预测历史_2_q , \分支预测历史_3_q , \分支预测历史_4_q , \分支预测历史_5_q , \分支预测历史_6_q , \分支预测历史_7_q ,
       \分支预测历史_8_q , \分支预测历史_q , \状态转换_1_newstate , \状态转换_2_newstate , \状态转换_3_newstate , \状态转换_4_newstate ,
       \状态转换_5_newstate , \状态转换_6_newstate , \状态转换_7_newstate , \状态转换_8_newstate ;
  wire [2:0] MAX, \max2归并比较_1_max_num , \max2归并比较_2_max_num , \max2归并比较_3_max_num , \max2归并比较_4_max_num ,
       \max2归并比较_5_max_num , \max2归并比较_6_max_num ;
  wire [15:0] C1, C2, C3, C4, C5, C6, C7, C8, \max2归并比较_1_max , \max2归并比较_2_max , \max2归并比较_3_max ,
       \max2归并比较_4_max , \max2归并比较_5_max , \max2归并比较_6_max ;
  wire [31:0] PC1, PC2, PC3, PC4, PC5, PC6, PC7, PC8, \分支目标地址_2_q , \分支目标地址_3_q , \分支目标地址_4_q , \分支目标地址_5_q ,
       \分支目标地址_6_q , \分支目标地址_7_q , \分支目标地址_8_q , \分支目标地址_q ;

  Register #(.width(1), .trigger("rising"), .Select("low")) valid (
    .D(1'b1), .en(enable1), .Q(V1), .clk(CLK));  // open: clr
  Register #(.width(1), .trigger("rising"), .Select("low")) valid_2 (
    .D(1'b1), .en(enable2), .Q(V2), .clk(CLK));  // open: clr
  Register #(.width(1), .trigger("rising"), .Select("low")) valid_3 (
    .D(1'b1), .en(enable3), .Q(V3), .clk(CLK));  // open: clr
  Register #(.width(1), .trigger("rising"), .Select("low")) valid_4 (
    .D(1'b1), .en(enable4), .Q(V4), .clk(CLK));  // open: clr
  Register #(.width(1), .trigger("rising"), .Select("low")) valid_5 (
    .D(1'b1), .en(enable5), .Q(V5), .clk(CLK));  // open: clr
  Register #(.width(1), .trigger("rising"), .Select("low")) valid_6 (
    .D(1'b1), .en(enable6), .Q(V6), .clk(CLK));  // open: clr
  Register #(.width(1), .trigger("rising"), .Select("low")) valid_7 (
    .D(1'b1), .en(enable7), .Q(V7), .clk(CLK));  // open: clr
  Register #(.width(1), .trigger("rising"), .Select("low")) valid_8 (
    .D(1'b1), .en(enable8), .Q(V8), .clk(CLK));  // open: clr
  Comparator #(.width(32), .mode("twosComplement")) comparator_1 (
    .a(PC), .b(PC1), .eq(comparator_1_eq));  // open: gt, lt
  Comparator #(.width(32), .mode("twosComplement")) comparator_2 (
    .a(PC), .b(PC2), .eq(comparator_2_eq));  // open: gt, lt
  Comparator #(.width(32), .mode("twosComplement")) comparator_3 (
    .a(PC), .b(PC3), .eq(comparator_3_eq));  // open: gt, lt
  Comparator #(.width(32), .mode("twosComplement")) comparator_4 (
    .a(PC), .b(PC4), .eq(comparator_4_eq));  // open: gt, lt
  Comparator #(.width(32), .mode("twosComplement")) comparator_5 (
    .a(PC), .b(PC5), .eq(comparator_5_eq));  // open: gt, lt
  Comparator #(.width(32), .mode("twosComplement")) comparator_6 (
    .a(PC), .b(PC6), .eq(comparator_6_eq));  // open: gt, lt
  Comparator #(.width(32), .mode("twosComplement")) comparator_7 (
    .a(PC), .b(PC7), .eq(comparator_7_eq));  // open: gt, lt
  Comparator #(.width(32), .mode("twosComplement")) comparator_8 (
    .a(PC), .b(PC8), .eq(comparator_8_eq));  // open: gt, lt
  not not_1 (not_1_out, ex_hit);
  not not_2 (not_2_out, V1);
  not not_3 (not_3_out, V2);
  not not_4 (not_4_out, V3);
  not not_5 (not_5_out, V4);
  not not_6 (not_6_out, V5);
  not not_7 (not_7_out, V6);
  not not_8 (not_8_out, V7);
  not not_9 (not_9_out, V8);
  Decoder #(.select(3), .tristate("false"), .disabled(0), .enable("true")) decoder_1 (
    .out0(decoder_1_out0), .out1(decoder_1_out1), .out2(decoder_1_out2), .out3(decoder_1_out3),
    .out4(decoder_1_out4), .out5(decoder_1_out5), .out6(decoder_1_out6), .out7(decoder_1_out7), .sel(MAX),
    .en(and_1_out));
  and and_1 (and_1_out, V1, V2, V3, V4, V5, V6, V7, V8);
  Register #(.width(32), .trigger("rising"), .Select("low")) \u_分支指令地址  (
    .D(EX_PC), .en(WRITE1), .Q(PC1), .clk(CLK));  // open: clr
  Register #(.width(32), .trigger("rising"), .Select("low")) \u_分支指令地址_2  (
    .D(EX_PC), .en(WRITE2), .Q(PC2), .clk(CLK));  // open: clr
  Register #(.width(32), .trigger("rising"), .Select("low")) \u_分支指令地址_3  (
    .D(EX_PC), .en(WRITE3), .Q(PC3), .clk(CLK));  // open: clr
  Register #(.width(32), .trigger("rising"), .Select("low")) \u_分支指令地址_4  (
    .D(EX_PC), .en(WRITE4), .Q(PC4), .clk(CLK));  // open: clr
  Register #(.width(32), .trigger("rising"), .Select("low")) \u_分支指令地址_5  (
    .D(EX_PC), .en(WRITE5), .Q(PC5), .clk(CLK));  // open: clr
  Register #(.width(32), .trigger("rising"), .Select("low")) \u_分支指令地址_6  (
    .D(EX_PC), .en(WRITE6), .Q(PC6), .clk(CLK));  // open: clr
  Register #(.width(32), .trigger("rising"), .Select("low")) \u_分支指令地址_7  (
    .D(EX_PC), .en(WRITE7), .Q(PC7), .clk(CLK));  // open: clr
  Register #(.width(32), .trigger("rising"), .Select("low")) \u_分支指令地址_8  (
    .D(EX_PC), .en(WRITE8), .Q(PC8), .clk(CLK));  // open: clr
  and and_2 (h1, comparator_1_eq, V1);
  and and_3 (h2, comparator_2_eq, V2);
  and and_4 (h3, comparator_3_eq, V3);
  and and_5 (h4, comparator_4_eq, V4);
  and and_6 (h5, comparator_5_eq, V5);
  and and_7 (h6, comparator_6_eq, V6);
  and and_8 (h7, comparator_7_eq, V7);
  and and_9 (h8, comparator_8_eq, V8);
  and and_10 (and_10_out, not_1_out, not_2_out);
  and and_11 (and_11_out, V1, not_3_out, not_1_out);
  and and_12 (and_12_out, not_4_out, not_1_out, V1, V2);
  and and_13 (and_13_out, not_5_out, not_1_out, V1, V2, V3);
  and and_14 (and_14_out, not_6_out, not_1_out, V1, V2, V3, V4);
  and and_15 (and_15_out, not_7_out, not_1_out, V1, V2, V3, V4, V5);
  and and_16 (and_16_out, not_8_out, not_1_out, V1, V2, V3, V4, V5, V6);
  and and_17 (and_17_out, not_9_out, not_1_out, V1, V2, V3, V4, V5, V6, V7);
  // Probe on {ex_hit, \分支 }
  // Probe on PC
  \状态转换  \u_状态转换_1  (.OldState(Status), .NewState(\状态转换_1_newstate ), .key({ex_hit, \分支 }));
  \状态转换  \u_状态转换_2  (.OldState(Status), .NewState(\状态转换_2_newstate ), .key({ex_hit, \分支 }));
  \状态转换  \u_状态转换_3  (.OldState(Status), .NewState(\状态转换_3_newstate ), .key({ex_hit, \分支 }));
  \状态转换  \u_状态转换_4  (.OldState(Status), .NewState(\状态转换_4_newstate ), .key({ex_hit, \分支 }));
  \状态转换  \u_状态转换_5  (.OldState(Status), .NewState(\状态转换_5_newstate ), .key({ex_hit, \分支 }));
  \状态转换  \u_状态转换_6  (.OldState(Status), .NewState(\状态转换_6_newstate ), .key({ex_hit, \分支 }));
  \状态转换  \u_状态转换_7  (.OldState(Status), .NewState(\状态转换_7_newstate ), .key({ex_hit, \分支 }));
  \状态转换  \u_状态转换_8  (.OldState(Status), .NewState(\状态转换_8_newstate ), .key({ex_hit, \分支 }));
  or or_1 (or_1_out, h1, h2);
  or or_2 (or_2_out, h3, h4);
  or or_3 (or_3_out, h5, h6);
  or or_4 (or_4_out, h7, h8);
  or or_5 (or_5_out, and_10_out, decoder_1_out0);
  or or_6 (or_6_out, and_11_out, decoder_1_out1);
  or or_7 (or_7_out, and_12_out, decoder_1_out2);
  or or_8 (or_8_out, and_13_out, decoder_1_out3);
  or or_9 (or_9_out, and_14_out, decoder_1_out4);
  or or_10 (or_10_out, and_15_out, decoder_1_out5);
  or or_11 (or_11_out, and_16_out, decoder_1_out6);
  or or_12 (or_12_out, and_17_out, decoder_1_out7);
  assign Status = or_13_out ? \分支预测历史_q  : 2'bz;  // Controlled_Buffer controlled_buffer_1
  Register #(.width(2), .trigger("rising"), .Select("low")) \u_分支预测历史  (
    .D(\状态转换_1_newstate ), .en(enable1), .Q(\分支预测历史_q ), .clk(CLK));  // open: clr
  or or_13 (or_13_out, h1, L1);
  assign Status = or_14_out ? \分支预测历史_2_q  : 2'bz;  // Controlled_Buffer controlled_buffer_2
  Register #(.width(2), .trigger("rising"), .Select("low")) \u_分支预测历史_2  (
    .D(\状态转换_2_newstate ), .en(enable2), .Q(\分支预测历史_2_q ), .clk(CLK));  // open: clr
  or or_14 (or_14_out, h2, L2);
  assign Status = or_15_out ? \分支预测历史_3_q  : 2'bz;  // Controlled_Buffer controlled_buffer_3
  Register #(.width(2), .trigger("rising"), .Select("low")) \u_分支预测历史_3  (
    .D(\状态转换_3_newstate ), .en(enable3), .Q(\分支预测历史_3_q ), .clk(CLK));  // open: clr
  or or_15 (or_15_out, h3, L3);
  Register #(.width(2), .trigger("rising"), .Select("low")) \u_分支预测历史_4  (
    .D(\状态转换_4_newstate ), .en(enable4), .Q(\分支预测历史_4_q ), .clk(CLK));  // open: clr
  assign Status = or_16_out ? \分支预测历史_4_q  : 2'bz;  // Controlled_Buffer controlled_buffer_4
  or or_16 (or_16_out, h4, L4);
  assign Status = or_17_out ? \分支预测历史_5_q  : 2'bz;  // Controlled_Buffer controlled_buffer_5
  Register #(.width(2), .trigger("rising"), .Select("low")) \u_分支预测历史_5  (
    .D(\状态转换_5_newstate ), .en(enable5), .Q(\分支预测历史_5_q ), .clk(CLK));  // open: clr
  or or_17 (or_17_out, h5, L5);
  Register #(.width(2), .trigger("rising"), .Select("low")) \u_分支预测历史_6  (
    .D(\状态转换_6_newstate ), .en(enable6), .Q(\分支预测历史_6_q ), .clk(CLK));  // open: clr
  assign Status = or_18_out ? \分支预测历史_6_q  : 2'bz;  // Controlled_Buffer controlled_buffer_6
  or or_18 (or_18_out, h6, L6);
  assign Status = or_19_out ? \分支预测历史_7_q  : 2'bz;  // Controlled_Buffer controlled_buffer_7
  Register #(.width(2), .trigger("rising"), .Select("low")) \u_分支预测历史_7  (
    .D(\状态转换_7_newstate ), .en(enable7), .Q(\分支预测历史_7_q ), .clk(CLK));  // open: clr
  or or_19 (or_19_out, h7, L7);
  Register #(.width(2), .trigger("rising"), .Select("low")) \u_分支预测历史_8  (
    .D(\状态转换_8_newstate ), .en(enable8), .Q(\分支预测历史_8_q ), .clk(CLK));  // open: clr
  assign Status = or_20_out ? \分支预测历史_8_q  : 2'bz;  // Controlled_Buffer controlled_buffer_8
  or or_20 (or_20_out, h8, L8);
  and and_18 (WRITE1, can, not_1_out, or_5_out);
  and and_19 (WRITE2, can, not_1_out, or_6_out);
  and and_20 (WRITE3, can, not_1_out, or_7_out);
  and and_21 (WRITE4, can, not_1_out, or_8_out);
  and and_22 (WRITE5, can, not_1_out, or_9_out);
  and and_23 (WRITE6, can, not_1_out, or_10_out);
  and and_24 (WRITE7, can, not_1_out, or_11_out);
  and and_25 (WRITE8, can, not_1_out, or_12_out);
  or or_21 (hit, or_1_out, or_2_out, or_3_out, or_4_out);
  Counter #(.width(16), .max('hffff), .ongoal("wrap"), .trigger("rising"), .behavior("old")) \u_淘汰标志位  (
    .load(1'b0), .count(can), .Q(C1), .clk(CLK), .clr(L1));  // open: D, carry, preset
  Counter #(.width(16), .max('hffff), .ongoal("wrap"), .trigger("rising"), .behavior("old")) \u_淘汰标志位_2  (
    .load(1'b0), .count(can), .Q(C2), .clk(CLK), .clr(L2));  // open: D, carry, preset
  Counter #(.width(16), .max('hffff), .ongoal("wrap"), .trigger("rising"), .behavior("old")) \u_淘汰标志位_3  (
    .load(1'b0), .count(can), .Q(C3), .clk(CLK), .clr(L3));  // open: D, carry, preset
  Counter #(.width(16), .max('hffff), .ongoal("wrap"), .trigger("rising"), .behavior("old")) \u_淘汰标志位_4  (
    .load(1'b0), .count(can), .Q(C4), .clk(CLK), .clr(L4));  // open: D, carry, preset
  Counter #(.width(16), .max('hffff), .ongoal("wrap"), .trigger("rising"), .behavior("old")) \u_淘汰标志位_5  (
    .load(1'b0), .count(can), .Q(C5), .clk(CLK), .clr(L5));  // open: D, carry, preset
  Counter #(.width(16), .max('hffff), .ongoal("wrap"), .trigger("rising"), .behavior("old")) \u_淘汰标志位_6  (
    .load(1'b0), .count(can), .Q(C6), .clk(CLK), .clr(L6));  // open: D, carry, preset
  Counter #(.width(16), .max('hffff), .ongoal("wrap"), .trigger("rising"), .behavior("old")) \u_淘汰标志位_7  (
    .load(1'b0), .count(can), .Q(C7), .clk(CLK), .clr(L7));  // open: D, carry, preset
  Counter #(.width(16), .max('hffff), .ongoal("wrap"), .trigger("rising"), .behavior("old")) \u_淘汰标志位_8  (
    .load(1'b0), .count(can), .Q(C8), .clk(CLK), .clr(L8));  // open: D, carry, preset
  Comparator #(.width(32), .mode("twosComplement")) comparator_9 (
    .a(EX_PC), .b(PC1), .eq(comparator_9_eq));  // open: gt, lt
  Comparator #(.width(32), .mode("twosComplement")) comparator_10 (
    .a(EX_PC), .b(PC2), .eq(comparator_10_eq));  // open: gt, lt
  Comparator #(.width(32), .mode("twosComplement")) comparator_11 (
    .a(EX_PC), .b(PC3), .eq(comparator_11_eq));  // open: gt, lt
  Comparator #(.width(32), .mode("twosComplement")) comparator_12 (
    .a(EX_PC), .b(PC4), .eq(comparator_12_eq));  // open: gt, lt
  Comparator #(.width(32), .mode("twosComplement")) comparator_13 (
    .a(EX_PC), .b(PC5), .eq(comparator_13_eq));  // open: gt, lt
  Comparator #(.width(32), .mode("twosComplement")) comparator_14 (
    .a(EX_PC), .b(PC6), .eq(comparator_14_eq));  // open: gt, lt
  Comparator #(.width(32), .mode("twosComplement")) comparator_15 (
    .a(EX_PC), .b(PC7), .eq(comparator_15_eq));  // open: gt, lt
  Comparator #(.width(32), .mode("twosComplement")) comparator_16 (
    .a(EX_PC), .b(PC8), .eq(comparator_16_eq));  // open: gt, lt
  \MAX2归并比较  \max2归并比较_1  (
    .Y(C2), .X(C1), .Y_num(3'b001), .X_num(3'b000), .MAX(\max2归并比较_1_max ), .MAX_num(\max2归并比较_1_max_num ));
  \MAX2归并比较  \max2归并比较_2  (
    .Y(C4), .X(C3), .Y_num(3'b011), .X_num(3'b010), .MAX(\max2归并比较_2_max ), .MAX_num(\max2归并比较_2_max_num ));
  \MAX2归并比较  \max2归并比较_3  (
    .Y(C6), .X(C5), .Y_num(3'b101), .X_num(3'b100), .MAX(\max2归并比较_3_max ), .MAX_num(\max2归并比较_3_max_num ));
  \MAX2归并比较  \max2归并比较_4  (
    .Y(C8), .X(C7), .Y_num(3'b111), .X_num(3'b110), .MAX(\max2归并比较_4_max ), .MAX_num(\max2归并比较_4_max_num ));
  Register #(.width(32), .trigger("rising"), .Select("low")) \u_分支目标地址  (
    .D(ADDR), .en(WRITE1), .Q(\分支目标地址_q ), .clk(CLK));  // open: clr
  Register #(.width(32), .trigger("rising"), .Select("low")) \u_分支目标地址_2  (
    .D(ADDR), .en(WRITE2), .Q(\分支目标地址_2_q ), .clk(CLK));  // open: clr
  Register #(.width(32), .trigger("rising"), .Select("low")) \u_分支目标地址_3  (
    .D(ADDR), .en(WRITE3), .Q(\分支目标地址_3_q ), .clk(CLK));  // open: clr
  Register #(.width(32), .trigger("rising"), .Select("low")) \u_分支目标地址_4  (
    .D(ADDR), .en(WRITE4), .Q(\分支目标地址_4_q ), .clk(CLK));  // open: clr
  Register #(.width(32), .trigger("rising"), .Select("low")) \u_分支目标地址_5  (
    .D(ADDR), .en(WRITE5), .Q(\分支目标地址_5_q ), .clk(CLK));  // open: clr
  Register #(.width(32), .trigger("rising"), .Select("low")) \u_分支目标地址_6  (
    .D(ADDR), .en(WRITE6), .Q(\分支目标地址_6_q ), .clk(CLK));  // open: clr
  Register #(.width(32), .trigger("rising"), .Select("low")) \u_分支目标地址_7  (
    .D(ADDR), .en(WRITE7), .Q(\分支目标地址_7_q ), .clk(CLK));  // open: clr
  Register #(.width(32), .trigger("rising"), .Select("low")) \u_分支目标地址_8  (
    .D(ADDR), .en(WRITE8), .Q(\分支目标地址_8_q ), .clk(CLK));  // open: clr
  and and_26 (L1, comparator_9_eq, V1);
  and and_27 (L2, comparator_10_eq, V2);
  and and_28 (L3, comparator_11_eq, V3);
  and and_29 (L4, comparator_12_eq, V4);
  and and_30 (L5, comparator_13_eq, V5);
  and and_31 (L6, comparator_14_eq, V6);
  and and_32 (L7, comparator_15_eq, V7);
  and and_33 (L8, comparator_16_eq, V8);
  \MAX2归并比较  \max2归并比较_5  (
    .Y(\max2归并比较_2_max ), .X(\max2归并比较_1_max ), .Y_num(\max2归并比较_2_max_num ), .X_num(\max2归并比较_1_max_num ),
    .MAX(\max2归并比较_5_max ), .MAX_num(\max2归并比较_5_max_num ));
  \MAX2归并比较  \max2归并比较_6  (
    .Y(\max2归并比较_4_max ), .X(\max2归并比较_3_max ), .Y_num(\max2归并比较_4_max_num ), .X_num(\max2归并比较_3_max_num ),
    .MAX(\max2归并比较_6_max ), .MAX_num(\max2归并比较_6_max_num ));
  and and_34 (en1, ex_hit, can, L1);
  and and_35 (en2, ex_hit, can, L2);
  and and_36 (en3, ex_hit, can, L3);
  and and_37 (en4, ex_hit, can, L4);
  and and_38 (en5, ex_hit, can, L5);
  and and_39 (en6, ex_hit, can, L6);
  and and_40 (en7, ex_hit, can, L7);
  and and_41 (en8, ex_hit, can, L8);
  assign OUTADDR = h1 ? \分支目标地址_q  : 32'bz;  // Controlled_Buffer controlled_buffer_9
  assign OUTADDR = h2 ? \分支目标地址_2_q  : 32'bz;  // Controlled_Buffer controlled_buffer_10
  assign OUTADDR = h3 ? \分支目标地址_3_q  : 32'bz;  // Controlled_Buffer controlled_buffer_11
  assign OUTADDR = h4 ? \分支目标地址_4_q  : 32'bz;  // Controlled_Buffer controlled_buffer_12
  assign OUTADDR = h5 ? \分支目标地址_5_q  : 32'bz;  // Controlled_Buffer controlled_buffer_13
  assign OUTADDR = h6 ? \分支目标地址_6_q  : 32'bz;  // Controlled_Buffer controlled_buffer_14
  assign OUTADDR = h7 ? \分支目标地址_7_q  : 32'bz;  // Controlled_Buffer controlled_buffer_15
  assign OUTADDR = h8 ? \分支目标地址_8_q  : 32'bz;  // Controlled_Buffer controlled_buffer_16
  \MAX2归并比较  \max2归并比较_7  (
    .Y(\max2归并比较_6_max ), .X(\max2归并比较_5_max ), .Y_num(\max2归并比较_6_max_num ), .X_num(\max2归并比较_5_max_num ),
    .MAX_num(MAX));  // open: MAX
  or or_22 (or_22_out, L1, L2);
  or or_23 (or_23_out, L3, L4);
  or or_24 (or_24_out, L5, L6);
  or or_25 (or_25_out, L7, L8);
  or or_26 (\命中 , or_22_out, or_23_out, or_24_out, or_25_out);
  or or_27 (enable1, WRITE1, en1);
  or or_28 (enable2, WRITE2, en2);
  or or_29 (enable3, WRITE3, en3);
  or or_30 (enable4, WRITE4, en4);
  or or_31 (enable5, WRITE5, en5);
  or or_32 (enable6, WRITE6, en6);
  or or_33 (enable7, WRITE7, en7);
  or or_34 (enable8, WRITE8, en8);
endmodule

module \MAX2归并比较  (
  input  [15:0] Y,
  input  [15:0] X,
  input  [2:0] Y_num,
  input  [2:0] X_num,
  output [15:0] MAX,
  output [2:0] MAX_num
);

  wire comparator_1_eq, comparator_1_gt, or_1_out;

  Multiplexer #(.select(1), .width(16), .disabled("Z"), .enable("true")) multiplexer_1 (
    .in0(Y), .in1(X), .out(MAX), .sel(or_1_out), .en(1'b1));
  Comparator #(.width(16), .mode("unsigned")) comparator_1 (
    .a(X), .b(Y), .gt(comparator_1_gt), .eq(comparator_1_eq));  // open: lt
  or or_1 (or_1_out, comparator_1_gt, comparator_1_eq);
  Multiplexer #(.select(1), .width(3), .disabled("Z"), .enable("false")) multiplexer_2 (
    .in0(Y_num), .in1(X_num), .out(MAX_num), .sel(or_1_out));

  // Notes on the sheet:
  //   输出两个输入中的较大值，并输出较大值的2位编号
endmodule

module \状态转换  (
  input  [1:0] OldState,
  input  [1:0] key,
  output [1:0] NewState
);

  wire [1:0] multiplexer_1_out, multiplexer_2_out;

  Multiplexer #(.select(2), .width(2), .disabled("Z"), .enable("false")) multiplexer_1 (
    .in0(2'b00), .in1(2'b00), .in2(2'b11), .in3(2'b00), .out(multiplexer_1_out), .sel(OldState));
  Multiplexer #(.select(2), .width(2), .disabled("Z"), .enable("false")) multiplexer_2 (
    .in0(2'b01), .in1(2'b10), .in2(2'b10), .in3(2'b10), .out(multiplexer_2_out), .sel(OldState));
  Multiplexer #(.select(2), .width(2), .disabled("Z"), .enable("false")) multiplexer_3 (
    .in0(2'b00), .in1(2'b10), .in2(multiplexer_1_out), .in3(multiplexer_2_out), .out(NewState), .sel(key));
endmodule

module \BHT_流水  (
  output RegWrite,
  output MemWrite,
  output [31:0] PC,
  output [31:0] IR,
  output [31:0] RDin,
  output [31:0] MDin
);

  wire ALUSRC, and_1_out, and_2_out, and_3_out, and_5_out, and_6_out, and_9_out, and_10_out, and_11_out, BEQ,
       beq_t, BGTZ, bgtz_t, BNE, bne_t, Branch, Can, CLK, comparator_1_eq, comparator_2_eq, equal, ex_hit,
       ex_mem_1_jal_prime, ex_mem_1_lbu_prime, ex_mem_1_memtoreg_prime, ex_mem_1_memwrite_prime,
       ex_mem_1_regdst_prime, exregwrite, Go, hit, id_ex_1_alusrcb_prime, id_ex_1_jal_prime,
       id_ex_1_lbu_prime, id_ex_1_memtoreg_prime, id_ex_1_memwrite_prime, id_ex_1_regdst_prime,
       id_ex_1_srlv_prime, if_id_1_hit_prime, IR1, IR2, IR3, JAL, JMP, jmp_t, JR, jr_t, LBU,
       mem_wb_1_jal_prime, mem_wb_1_lbu_prime, mem_wb_1_memtoreg_prime, mem_wb_1_regdst_prime, memregwrite,
       MemtoReg, mips_alu_1_equal, not_1_out, not_2_out, not_3_out, not_4_out, not_5_out, not_6_out,
       or_1_out, or_4_out, OUTPUT, R1_USED, R2_USED, RegDst, Regwrite_t, regwrite_t_t, Sign, SRLV, stop,
       syscall, W1, W2, W3, \分支 , \单周期硬布线控制器_1_syscall , \预测失败 , \预测成功 ;
  wire [1:0] C_1, C_2, id_ex_1_a_choose_prime, id_ex_1_b_choose_prime, if_id_1_status_prime, STATUS, status_t;
  wire [3:0] ALUOP, id_ex_1_aluop_prime;
  wire [4:0] EXWriteReg, id_ex_1_shamt_prime, MEMWriteReg, multiplexer_5_out, multiplexer_13_out,
       multiplexer_17_out, multiplexer_20_out, R1_num, R2_num, WRITEREG;
  wire [15:0] imm16, \失败次数 , \总周期数 , \成功次数 , \插入气泡数 , \无条件 , \有条件 ;
  wire [27:0] JPC;
  wire [31:0] A, a0, adder_2_out, ADDR, ALU_1, ALU_2, and_12_out, B, bit_extender_1_out, ex_mem_1_a_prime,
       ex_mem_1_pc_prime, EX_PC, EXIR, EXPC, id_ex_1_imm16_prime, id_ex_1_imm26_prime, id_ex_1_sign16_prime,
       if_id_1_pc_prime, \if_id_1_原pc_prime , IMM, imm26, IR_final, JRPC, LedData, MD, mem_wb_1_md_prime,
       mem_wb_1_pc_prime, MEMIR, mips_alu_1_result, mips_regifile_1_r1, mips_regifile_1_r2,
       multiplexer_1_out, multiplexer_2_out, multiplexer_3_out, multiplexer_9_out, multiplexer_12_out,
       multiplexer_16_out, multiplexer_18_out, OUTADDR, PC_q, R1, R2, ram_1_data, shifter_1_out,
       shifter_3_out, shifter_4_out, Sign16, v0;
  wire [31:16] IR_NOW;
  wire [31:28] shifter_2_out;

  Clock #(.highDuration(1), .lowDuration(1)) clock_1 (.out(CLK));
  Button _1 (.out(IR1));
  Button _2 (.out(IR2));
  Button _3 (.out(IR3));
  Button \u_继续运行  (.out(Go));
  LED #(.active("true")) led_1 (.in(W1));
  LED #(.active("true")) led_2 (.in(W2));
  LED #(.active("true")) led_3 (.in(W3));
  // Probe on ADDR
  Hex_Digit_Display hex_digit_display_1 (.value(LedData[31:28]));  // open: dp
  Counter #(.width(16), .max('hffff), .ongoal("wrap"), .trigger("rising"), .behavior("old")) counter_1 (
    .D({16{1'b0}}), .count(\预测成功 ), .Q(\成功次数 ), .clk(CLK));  // open: load, carry, clr, preset
  Multiplexer #(.select(1), .width(32), .disabled("Z"), .enable("false")) multiplexer_1 (
    .in0(EXPC), .in1(ADDR), .out(multiplexer_1_out), .sel(\分支 ));
  // Probe on OUTADDR
  Hex_Digit_Display hex_digit_display_2 (.value(LedData[27:24]));  // open: dp
  Hex_Digit_Display hex_digit_display_3 (.value(LedData[23:20]));  // open: dp
  // Probe on \成功次数 
  and and_1 (and_1_out, status_t[1], hit);
  Multiplexer #(.select(1), .width(32), .disabled("Z"), .enable("false")) multiplexer_2 (
    .in0(PC), .in1(OUTADDR), .out(multiplexer_2_out), .sel(and_1_out));
  Hex_Digit_Display hex_digit_display_4 (.value(LedData[15:12]));  // open: dp
  Hex_Digit_Display hex_digit_display_5 (.value(LedData[19:16]));  // open: dp
  not not_1 (not_1_out, stop);
  and and_2 (and_2_out, not_1_out, OUTPUT);
  not not_2 (not_2_out, OUTPUT);
  and and_3 (and_3_out, not_2_out, not_3_out);
  Multiplexer #(.select(1), .width(32), .disabled("Z"), .enable("false")) multiplexer_3 (
    .in0(multiplexer_2_out), .in1(multiplexer_1_out), .out(multiplexer_3_out), .sel(\预测失败 ));
  // Probe on multiplexer_3_out
  assign bit_extender_1_out = {{16{1'b0}}, imm16};  // Bit_Extender bit_extender_1
  assign Sign16 = {{16{imm16[15]}}, imm16};  // Bit_Extender bit_extender_2
  Hex_Digit_Display hex_digit_display_6 (.value(LedData[11:8]));  // open: dp
  Hex_Digit_Display hex_digit_display_7 (.value(LedData[7:4]));  // open: dp
  Counter #(.width(16), .max('hffff), .ongoal("wrap"), .trigger("rising"), .behavior("old")) counter_2 (
    .D({16{1'b0}}), .count(\预测失败 ), .Q(\失败次数 ), .clk(CLK));  // open: load, carry, clr, preset
  // Probe on \失败次数 
  not not_3 (not_3_out, stop);
  // Probe on \预测失败 
  Register #(.width(32), .trigger("rising"), .Select("low")) u_PC (
    .D(multiplexer_3_out), .en(and_3_out), .Q(PC_q), .clk(CLK));  // open: clr
  Multiplexer #(.select(1), .width(32), .disabled("Z"), .enable("false")) multiplexer_4 (
    .in0(bit_extender_1_out), .in1(Sign16), .out(IMM), .sel(Sign));
  Hex_Digit_Display hex_digit_display_8 (.value(LedData[3:0]));  // open: dp
  // Probe on \总周期数 
  Counter #(.width(16), .max('hffff), .ongoal("wrap"), .trigger("rising"), .behavior("old")) counter_3 (
    .D({16{1'b0}}), .count(and_2_out), .Q(\插入气泡数 ), .clk(CLK));  // open: load, carry, clr, preset
  Counter #(.width(16), .max('hffff), .ongoal("wrap"), .trigger("rising"), .behavior("old")) counter_4 (
    .D({16{1'b0}}), .count(not_3_out), .Q(\总周期数 ), .clk(CLK));  // open: load, carry, clr, preset
  // Probe on \插入气泡数 
  // Probe on PC_q
  BHT bht_1 (
    .PC(PC_q), .ex_hit(ex_hit), .hit(hit), .EX_PC(EX_PC), .CLK(CLK), .Status(status_t), .ADDR(ADDR),
    .OUTADDR(OUTADDR), .\分支 (\分支 ), .can(Can));
  Adder #(.width(32)) adder_1 (.a(PC_q), .b(32'h4), .out(PC));  // open: cin, cout
  ROM #(.addrWidth(10), .dataWidth(32), .Select("high")) rom_1 (.addr(PC_q[11:2]), .data(IR));
  Multiplexer #(.select(1), .width(5), .disabled("Z"), .enable("false")) multiplexer_5 (
    .in0(IR_NOW[20:16]), .in1(imm16[15:11]), .out(multiplexer_5_out), .sel(RegDst));
  or or_1 (or_1_out, stop, OUTPUT);
  Multiplexer #(.select(1), .width(5), .disabled("Z"), .enable("false")) multiplexer_6 (
    .in0(multiplexer_5_out), .in1({5{1'b1}}), .out(WRITEREG), .sel(JAL));
  IF_ID if_id_1 (
    .IR(IR), .PC(PC), .CLK(CLK), .IR_prime({IR_NOW, imm16}), .PC_prime(if_id_1_pc_prime),
    .\同步清零_高电平有效 (\预测失败 ), .\使能端_低电平有效 (or_1_out), .\原PC (PC_q), .\原PC_prime (\if_id_1_原pc_prime ),
    .hit(hit), .hit_prime(if_id_1_hit_prime), .status(status_t), .status_prime(if_id_1_status_prime));
  or or_2 (\分支 , JMP, Branch);
  // Probe on \if_id_1_原pc_prime 
  Comparator #(.width(1), .mode("twosComplement")) comparator_1 (
    .a(STATUS[1]), .b(\分支 ), .eq(comparator_1_eq));  // open: gt, lt
  \单周期硬布线控制器  \u_单周期硬布线控制器_1  (
    .Func(imm16[5:0]), .OP(IR_NOW[31:26]), .ALU_OP(ALUOP), .MemToReg(MemtoReg), .MemWrite(MemWrite),
    .ALU_SRC(ALUSRC), .RegWrite(Regwrite_t), .SysCALL(\单周期硬布线控制器_1_syscall ), .SignedExt(Sign),
    .RegDst(RegDst), .JR(jr_t), .JMP(jmp_t), .Beq(BEQ), .JAL(JAL), .Bne(BNE), .SRLV(SRLV), .LBU(LBU),
    .BGTZ(BGTZ));
  Multiplexer #(.select(1), .width(5), .disabled("Z"), .enable("false")) multiplexer_7 (
    .in0(IR_NOW[25:21]), .in1(5'b00010), .out(R1_num), .sel(\单周期硬布线控制器_1_syscall ));
  Multiplexer #(.select(1), .width(5), .disabled("Z"), .enable("false")) multiplexer_8 (
    .in0(IR_NOW[20:16]), .in1(5'b00100), .out(R2_num), .sel(\单周期硬布线控制器_1_syscall ));
  Comparator #(.width(32), .mode("twosComplement")) comparator_2 (
    .a(v0), .b(32'h22), .eq(comparator_2_eq));  // open: gt, lt
  and and_4 (\预测成功 , comparator_1_eq, ex_hit);
  \源寄存器使用情况  \u_源寄存器使用情况_1  (
    .OP0(IR_NOW[26]), .OP1(IR_NOW[27]), .OP2(IR_NOW[28]), .OP3(IR_NOW[29]), .OP4(IR_NOW[30]),
    .OP5(IR_NOW[31]), .F0(imm16[0]), .F1(imm16[1]), .F2(imm16[2]), .F3(imm16[3]), .F4(imm16[4]),
    .F5(imm16[5]), .R1_Used(R1_USED), .R2_Used(R2_USED));
  not not_4 (not_4_out, comparator_2_eq);
  and and_5 (and_5_out, ex_hit, ~comparator_1_eq);  // AND_Gate
  and and_6 (and_6_out, ~ex_hit, \分支 );  // AND_Gate
  MIPS_Regifile mips_regifile_1 (
    .Din(RDin), .Clk(CLK), .R1(mips_regifile_1_r1), .R2(mips_regifile_1_r2), .WE(regwrite_t_t),
    .W_num(multiplexer_20_out), .R1_num(R1_num), .R2_num(R2_num));
  assign imm26 = {{6{IR_NOW[25]}}, {IR_NOW[25:16], imm16}};  // Bit_Extender bit_extender_3
  and and_7 (equal, syscall, comparator_2_eq);
  and and_8 (stop, syscall, not_4_out);
  or or_3 (\预测失败 , and_5_out, and_6_out);
  \LOAD_USE检测  \load_use检测_1  (
    .EX_RegWrite(exregwrite), .R2_Used(R2_USED), .R1_Used(R1_USED), .R1_num(R1_num), .R2_num(R2_num),
    .EX_WriteReg_num(EXWriteReg), .OP(EXIR[31:26]), .OUTPUT(OUTPUT));
  // Probe on EX_PC
  Multiplexer #(.select(1), .width(32), .disabled("Z"), .enable("false")) multiplexer_9 (
    .in1(a0), .out(multiplexer_9_out), .sel(equal));  // open: in0
  // Probe on a0
  or or_4 (or_4_out, \预测失败 , OUTPUT);
  ID_EX id_ex_1 (
    .RegDst(RegDst), .MemToReg(MemtoReg), .RegWirte(Regwrite_t), .MemWrite(MemWrite), .ALUSRCB(ALUSRC),
    .J(jmp_t), .JR(jr_t), .JAL(JAL), .BEQ(BEQ), .BNE(BNE), .ALUOP(ALUOP), .IR({IR_NOW, imm16}),
    .PC(if_id_1_pc_prime), .A(mips_regifile_1_r1), .B(mips_regifile_1_r2), .Imm16(IMM), .CLK(CLK),
    .RegDst_prime(id_ex_1_regdst_prime), .MemToReg_prime(id_ex_1_memtoreg_prime),
    .RegWrite_prime(exregwrite), .MemWrite_prime(id_ex_1_memwrite_prime),
    .ALUSRCB_prime(id_ex_1_alusrcb_prime), .J_prime(JMP), .JR_prime(JR), .JAL_prime(id_ex_1_jal_prime),
    .BEQ_prime(beq_t), .BNE_prime(bne_t), .ALUOP_prime(id_ex_1_aluop_prime), .IR_prime(EXIR),
    .PC_prime(EXPC), .A_prime(R1), .B_prime(R2), .Imm16_prime(id_ex_1_imm16_prime), .\同步清零_高电平有效 (or_4_out),
    .\使能端_低电平有效 (stop), .Imm26(imm26), .Imm26_prime(id_ex_1_imm26_prime), .shamt_prime(id_ex_1_shamt_prime),
    .WriteReg_prime(EXWriteReg), .WriteReg(WRITEREG), .shamt(imm16[10:6]), .A_choose(C_1),
    .A_Choose_prime(id_ex_1_a_choose_prime), .B_Choose(C_2), .B_Choose_prime(id_ex_1_b_choose_prime),
    .BGTZ(BGTZ), .BGTZ_prime(bgtz_t), .LBU(LBU), .LBU_prime(id_ex_1_lbu_prime), .SRLV(SRLV),
    .SRLV_prime(id_ex_1_srlv_prime), .hit(if_id_1_hit_prime), .hit_prime(ex_hit),
    .\原PC (\if_id_1_原pc_prime ), .\原PC_prime (EX_PC), .status(if_id_1_status_prime), .status_prime(STATUS),
    .sign16(Sign16), .sign16_prime(id_ex_1_sign16_prime));
  Register #(.width(32), .trigger("rising"), .Select("low")) register_1 (
    .D(multiplexer_9_out), .Q(LedData), .clk(CLK));  // open: en, clr
  Multiplexer #(.select(2), .width(32), .disabled("Z"), .enable("false")) multiplexer_10 (
    .in0(R1), .in1(ALU_1), .in2(ALU_2), .in3(MD), .out(A), .sel(id_ex_1_a_choose_prime));
  Multiplexer #(.select(1), .width(32), .disabled("Z"), .enable("false")) multiplexer_11 (
    .in0(A), .in1(B), .out(JRPC), .sel(id_ex_1_srlv_prime));
  Multiplexer #(.select(1), .width(32), .disabled("Z"), .enable("false")) multiplexer_12 (
    .in0(B), .in1(id_ex_1_imm16_prime), .out(multiplexer_12_out), .sel(id_ex_1_alusrcb_prime));
  Shifter #(.width(32), .shift("ll")) shifter_1 (.in(id_ex_1_sign16_prime), .\dist (5'b00010), .out(shifter_1_out));
  Shifter #(.width(32), .shift("ll")) shifter_2 (
    .in(id_ex_1_imm26_prime), .\dist (5'b00010), .out({shifter_2_out, JPC}));
  Multiplexer #(.select(1), .width(5), .disabled("Z"), .enable("false")) multiplexer_13 (
    .in0(id_ex_1_shamt_prime), .in1(A[4:0]), .out(multiplexer_13_out), .sel(id_ex_1_srlv_prime));
  // Probe on multiplexer_12_out
  Multiplexer #(.select(2), .width(32), .disabled("Z"), .enable("false")) multiplexer_14 (
    .in0(R2), .in1(ALU_1), .in2(ALU_2), .in3(MD), .out(B), .sel(id_ex_1_b_choose_prime));
  Adder #(.width(32)) adder_2 (.a(shifter_1_out), .b(EXPC), .out(adder_2_out));  // open: cin, cout
  // Probe on {EXPC[31:28], JPC}
  // Probe on ADDR
  \重定向相关  \u_重定向相关_1  (
    .MEM_RegWrite(memregwrite), .EX_RegWrite(exregwrite), .R2_Used(R2_USED), .R1_Used(R1_USED),
    .R1_num(R1_num), .R2_num(R2_num), .EX_WriteReg_num(EXWriteReg), .MEM_WriteReg_num(MEMWriteReg),
    .OP(MEMIR[31:26]), .A_Choose(C_1), .B_Choose(C_2));
  MIPS_ALU mips_alu_1 (
    .X(JRPC), .Y(multiplexer_12_out), .AluOP(id_ex_1_aluop_prime), .Equal(mips_alu_1_equal),
    .Result(mips_alu_1_result), .shamt(multiplexer_13_out));  // open: Result_2
  Multiplexer #(.select(1), .width(32), .disabled("Z"), .enable("false")) multiplexer_15 (
    .in0(multiplexer_16_out), .in1(JRPC), .out(ADDR), .sel(JR));
  // Probe on JRPC
  not not_5 (not_5_out, mips_alu_1_equal);
  not not_6 (not_6_out, mips_alu_1_result[0]);
  // Probe on EXPC
  // Probe on adder_2_out
  Multiplexer #(.select(1), .width(32), .disabled("Z"), .enable("false")) multiplexer_16 (
    .in0(adder_2_out), .in1({EXPC[31:28], JPC}), .out(multiplexer_16_out), .sel(JMP));
  Counter #(.width(16), .max('hffff), .ongoal("wrap"), .trigger("rising"), .behavior("old")) counter_5 (
    .D({16{1'b0}}), .count(JMP), .Q(\无条件 ), .clk(CLK));  // open: load, carry, clr, preset
  // Probe on \无条件 
  and and_9 (and_9_out, not_5_out, bne_t);
  and and_10 (and_10_out, mips_alu_1_equal, beq_t);
  and and_11 (and_11_out, not_5_out, not_6_out, bgtz_t);
  or or_5 (Can, bne_t, bgtz_t, beq_t, JMP);
  or or_6 (Branch, and_9_out, and_10_out, and_11_out);
  Counter #(.width(16), .max('hffff), .ongoal("wrap"), .trigger("rising"), .behavior("old")) counter_6 (
    .D({16{1'b0}}), .count(Branch), .Q(\有条件 ), .clk(CLK));  // open: load, carry, clr, preset
  // Probe on \有条件 
  EX_MEM ex_mem_1 (
    .JAL(id_ex_1_jal_prime), .RegDst(id_ex_1_regdst_prime), .MemToReg(id_ex_1_memtoreg_prime),
    .RegWirte(exregwrite), .MemWrite(id_ex_1_memwrite_prime), .IR(EXIR), .PC(EXPC), .B(B),
    .ALU(mips_alu_1_result), .CLK(CLK), .JAL_prime(ex_mem_1_jal_prime), .RegDst_prime(ex_mem_1_regdst_prime),
    .MemToReg_prime(ex_mem_1_memtoreg_prime), .RegWrite_prime(memregwrite),
    .MemWrite_prime(ex_mem_1_memwrite_prime), .IR_prime(MEMIR), .PC_prime(ex_mem_1_pc_prime), .B_prime(MDin),
    .ALU_prime(ALU_1), .\使能端_低电平有效 (stop), .A(A), .A_prime(ex_mem_1_a_prime), .WriteReg(EXWriteReg),
    .WriteReg_prime(MEMWriteReg), .LBU(id_ex_1_lbu_prime), .LBU_prime(ex_mem_1_lbu_prime));  // open: 同步清零_高电平有效
  RAM #(.addrWidth(10), .dataWidth(32), .bus("separate"), .Select("high")) ram_1 (
    .addr(ALU_1[11:2]), .din(MDin), .data(ram_1_data), .str(ex_mem_1_memwrite_prime), .sel(1'b1), .clk(CLK));  // open: ld, clr
  MEM_WB mem_wb_1 (
    .JAL(ex_mem_1_jal_prime), .RegDst(ex_mem_1_regdst_prime), .MemToReg(ex_mem_1_memtoreg_prime),
    .RegWirte(memregwrite), .IR(MEMIR), .PC(ex_mem_1_pc_prime), .ALU(ALU_1), .MD(ram_1_data), .CLK(CLK),
    .JAL_prime(mem_wb_1_jal_prime), .RegDst_prime(mem_wb_1_regdst_prime),
    .MemToReg_prime(mem_wb_1_memtoreg_prime), .RegWrite_prime(regwrite_t_t), .IR_prime(IR_final),
    .PC_prime(mem_wb_1_pc_prime), .ALU_prime(ALU_2), .MD_prime(mem_wb_1_md_prime), .\使能端_低电平有效 (stop),
    .A(ex_mem_1_a_prime), .A_prime(v0), .B(MDin), .B_prime(a0), .WriteReg(MEMWriteReg),
    .LBU(ex_mem_1_lbu_prime), .LBU_prime(mem_wb_1_lbu_prime));  // open: 同步清零_高电平有效, WriteReg_prime
  Multiplexer #(.select(1), .width(5), .disabled("Z"), .enable("false")) multiplexer_17 (
    .in0(IR_final[20:16]), .in1(IR_final[15:11]), .out(multiplexer_17_out), .sel(mem_wb_1_regdst_prime));
  Multiplexer #(.select(1), .width(32), .disabled("Z"), .enable("false")) multiplexer_18 (
    .in0(ALU_2), .in1(mem_wb_1_md_prime), .out(multiplexer_18_out), .sel(mem_wb_1_memtoreg_prime));
  Multiplexer #(.select(1), .width(32), .disabled("Z"), .enable("false")) multiplexer_19 (
    .in0(MD), .in1(mem_wb_1_pc_prime), .out(RDin), .sel(mem_wb_1_jal_prime));
  Multiplexer #(.select(1), .width(5), .disabled("Z"), .enable("false")) multiplexer_20 (
    .in0(multiplexer_17_out), .in1({5{1'b1}}), .out(multiplexer_20_out), .sel(mem_wb_1_jal_prime));
  Shifter #(.width(32), .shift("ll")) shifter_3 (.in(32'hff), .\dist ({ALU_2[1:0], 3'b000}), .out(shifter_3_out));
  Comparator #(.width(32), .mode("twosComplement")) comparator_3 (
    .a(IR_final), .b(32'hc), .eq(syscall));  // open: gt, lt
  assign and_12_out = multiplexer_18_out & shifter_3_out;  // AND_Gate and_12, 32 bits wide
  Shifter #(.width(32), .shift("lr")) shifter_4 (.in(and_12_out), .\dist ({ALU_2[1:0], 3'b000}), .out(shifter_4_out));
  Multiplexer #(.select(1), .width(32), .disabled("Z"), .enable("false")) multiplexer_21 (
    .in0(multiplexer_18_out), .in1(shifter_4_out), .out(MD), .sel(mem_wb_1_lbu_prime));

  // Other names for the same wires on the sheet: IR_NOW[15:0] = imm16; shamt[4:0] = imm16[10:6];
  //   JPC[31:28] = EXPC[31:28]

  // Notes on the sheet:
  //   中断源
  //   中断等待指示
  //   总复位信号应将除ROM以外所有存储组件全部清零
  //   数码管输出
  //   数码管输出应该用寄存器锁存，否则显示数据只能一闪而过
  //   contents of rom_1 (hex, n*v repeats v):
  //   20110001 8000c05 20110001 20120002 20130003 8000c09 20110001 20120002 20130003 8000c0d 20110001
  //   20120002 20130003 8000c11 20110001 20120002 20130003 c000cb8 20100001 20110001 118fc0 112020
  //   20020022 c 118882 12200001 8000c15 112020 20020022 c 20110001 118880 112020 20020022 c 12200001
  //   8000c1f 20110001 118fc0 112020 20020022 c 1188c3 112020 20020022 c 118903 112020 20020022 c 118903
  //   112020 20020022 c 118903 112020 20020022 c 118903 112020 20020022 c 118903 112020 20020022 c 118903
  //   112020 20020022 c 118903 112020 20020022 c 20100001 109fc0 139fc3 8021 2012000c 24160003 26100001
  //   3210000f 20080008 20090001 139900 2709825 132020 20020022 c 1094022 1500fff9 22100001 2018000f
  //   2188024 108700 20080008 20090001 139902 2709825 132021 20020022 c 1094022 1500fff9 108702 2c9b022
  //   12c00001 8000c50 4020 1084027 84400 3508ffff 82021 20020022 c 2010ffff 20110000 ae300000 22100001
  //   22310004 ae300000 22100001 22310004 ae300000 22100001 22310004 ae300000 22100001 22310004 ae300000
  //   22100001 22310004 ae300000 22100001 22310004 ae300000 22100001 22310004 ae300000 22100001 22310004
  //   ae300000 22100001 22310004 ae300000 22100001 22310004 ae300000 22100001 22310004 ae300000 22100001
  //   22310004 ae300000 22100001 22310004 ae300000 22100001 22310004 ae300000 22100001 22310004 ae300000
  //   22100001 22310004 22100001 8020 2011003c 8e130000 8e340000 274402a 11000002 ae330000 ae140000
  //   2231fffc 1611fff8 102020 20020022 c 22100004 2011003c 1611fff2 20020032 c 20100000 22100001 102020
  //   20020022 c 22100002 102020 20020022 c 22100003 102020 20020022 c 22100004 102020 20020022 c 22100005
  //   102020 20020022 c 22100006 102020 20020022 c 22100007 102020 20020022 c 22100008 102020 20020022
  //   20020022 c 3e00008
  //   rt
  //   为方便自动评测，需要输出PC，IR，寄存器文件写入端口RDin，内存写入端口MDin等信号
  //   OP
  //   OP
  //   rs
  //   rt
endmodule
