// Logisim project wl-cpu24-backup.circ as structural Verilog: 32 circuits, main circuit ◇单周期MIPS
module \单周期MIPS  (
  input  IR1,
  input  IR2,
  input  IR3,
  output RegWrite,
  output MemWrite,
  output [31:0] PC,
  output [31:0] IR,
  output [31:0] RDin,
  output [31:0] MDin,
  output [31:0] LedData
);

  wire and_1_out, and_3_out, and_4_out, bgtz, CLK, comparator_1_gt, comparator_2_eq, comparator_3_eq, Go,
       Halt, IR1_t, IR2_t, IR3_t, IRA, IRB, IRC, jal, mips_alu_1_equal, not_1_out, not_2_out, or_1_out,
       or_5_out, SH, SignedExt, SLLV, syscall, W1, W2, W3, \单周期硬布线控制器_1_alu_src , \单周期硬布线控制器_1_beq ,
       \单周期硬布线控制器_1_bne , \单周期硬布线控制器_1_jmp , \单周期硬布线控制器_1_memtoreg , \单周期硬布线控制器_1_regdst ;
  wire [0:0] \单周期硬布线控制器_1_jr ;
  wire [1:1] and_2_out;
  wire [3:0] \单周期硬布线控制器_1_alu_op ;
  wire [4:0] multiplexer_8_out, multiplexer_9_out, multiplexer_10_out, multiplexer_11_out, multiplexer_13_out;
  wire [15:0] \总周期数 ;
  wire [27:0] adder_1_out_2;
  wire [31:0] adder_2_out, addr, bit_extender_1_out, bit_extender_2_out, MDinTemp, MemData,
       multiplexer_1_out, multiplexer_2_out, multiplexer_3_out, multiplexer_4_out, multiplexer_5_out,
       multiplexer_7_out, multiplexer_12_out, multiplexer_17_out, R1, R2, shifter_1_out, shifter_2_out;
  wire [31:28] adder_1_out;

  Clock clock_1 (.out(CLK));
  Button _1 (.out(IRA));
  Button _2 (.out(IRB));
  Button _3 (.out(IRC));
  Button \u_继续运行  (.out(Go));
  LED led_1 (.in(W1));
  LED led_2 (.in(W2));
  LED led_3 (.in(W3));
  Hex_Digit_Display hex_digit_display_1 (.value(LedData[31:28]));  // open: dp
  Hex_Digit_Display hex_digit_display_2 (.value(LedData[27:24]));  // open: dp
  Hex_Digit_Display hex_digit_display_3 (.value(LedData[23:20]));  // open: dp
  Comparator #(.width(32)) comparator_1 (.a(R1), .b({32{1'b0}}), .gt(comparator_1_gt));  // open: eq, lt
  Multiplexer #(.width(32), .enable("false")) multiplexer_1 (
    .in0({32{1'b0}}), .in1(R1), .out(multiplexer_1_out), .sel(syscall));
  Hex_Digit_Display hex_digit_display_4 (.value(LedData[15:12]));  // open: dp
  Hex_Digit_Display hex_digit_display_5 (.value(LedData[19:16]));  // open: dp
  and and_1 (and_1_out, comparator_1_gt, bgtz);
  or or_1 (or_1_out, and_1_out, or_5_out);
  Multiplexer #(.width(32), .enable("false")) multiplexer_2 (
    .in0({adder_1_out, adder_1_out_2}), .in1(adder_2_out), .out(multiplexer_2_out), .sel(or_1_out));
  Comparator #(.width(32), .mode("unsigned")) comparator_2 (
    .a(multiplexer_1_out), .b(32'h22), .eq(comparator_2_eq));  // open: gt, lt
  Multiplexer #(.width(32), .enable("false")) multiplexer_3 (
    .in0({32{1'b0}}), .in1(R1), .out(multiplexer_3_out), .sel(syscall));
  Comparator #(.width(32), .mode("unsigned")) comparator_3 (
    .a(multiplexer_3_out), .b(32'ha), .eq(comparator_3_eq));  // open: gt, lt
  Hex_Digit_Display hex_digit_display_6 (.value(LedData[7:4]));  // open: dp
  Hex_Digit_Display hex_digit_display_7 (.value(LedData[11:8]));  // open: dp
  // Probe on \总周期数 
  Multiplexer #(.select(2), .width(32), .enable("false")) multiplexer_4 (
    .in0({adder_1_out, shifter_1_out[27:0]}), .in1(R1), .in2({adder_1_out, shifter_1_out[27:0]}),
    .out(multiplexer_4_out), .sel({jal, \单周期硬布线控制器_1_jr [0]}));  // open: in3
  Register #(.width(32)) register_1 (.D(multiplexer_5_out), .en(comparator_2_eq), .Q(LedData), .clk(CLK));  // open: clr
  Multiplexer #(.width(32), .enable("false")) multiplexer_5 (
    .in0({32{1'b0}}), .in1(R2), .out(multiplexer_5_out), .sel(comparator_2_eq));
  Multiplexer #(.enable("false")) multiplexer_6 (.in0(1'b0), .in1(1'b1), .out(Halt), .sel(comparator_3_eq));
  Hex_Digit_Display hex_digit_display_8 (.value(LedData[3:0]));  // open: dp
  Multiplexer #(.width(32), .enable("false")) multiplexer_7 (
    .in0(multiplexer_2_out), .in1(multiplexer_4_out), .out(multiplexer_7_out), .sel(\单周期硬布线控制器_1_jmp ));
  not not_1 (not_1_out, Halt);
  Register #(.width(32)) u_PC (.D(multiplexer_7_out), .en(not_1_out), .Q(PC), .clk(CLK));  // open: clr
  or or_2 (IR1_t, IR1, IRA);
  Adder #(.width(32)) adder_1 (.a(PC), .b(32'h4), .out({adder_1_out, adder_1_out_2}));  // open: cin, cout
  not not_2 (not_2_out, Halt);
  or or_3 (IR2_t, IR2, IRB);
  ROM #(.addrWidth(10), .dataWidth(32)) rom_1 (.addr(PC[11:2]), .data(IR));  // open: sel
  Counter #(.width(16), .max('hffff)) counter_1 (
    .count(not_2_out), .Q(\总周期数 ), .clk(CLK));  // open: load, D, carry, clr
  or or_4 (IR3_t, IR3, IRC);
  \单周期硬布线控制器  \u_单周期硬布线控制器_1  (
    .Func(IR[5:0]), .OP(IR[31:26]), .ALU_OP(\单周期硬布线控制器_1_alu_op ), .MemToReg(\单周期硬布线控制器_1_memtoreg ),
    .MemWrite(MemWrite), .ALU_SRC(\单周期硬布线控制器_1_alu_src ), .RegWrite(RegWrite), .SysCALL(syscall),
    .SignedExt(SignedExt), .RegDst(\单周期硬布线控制器_1_regdst ), .JR(\单周期硬布线控制器_1_jr [0]), .JMP(\单周期硬布线控制器_1_jmp ),
    .Beq(\单周期硬布线控制器_1_beq ), .JAL(jal), .Bne(\单周期硬布线控制器_1_bne ), .Bgtz(bgtz));  // open: INS1, INS2, INS3, RET
  Multiplexer #(.width(5), .enable("false")) multiplexer_8 (
    .in0(IR[20:16]), .in1(IR[15:11]), .out(multiplexer_8_out), .sel(\单周期硬布线控制器_1_regdst ));
  assign bit_extender_1_out = {{6{1'b0}}, IR[25:0]};  // Bit_Extender bit_extender_1
  Multiplexer #(.width(5), .enable("false")) multiplexer_9 (
    .in0(IR[25:21]), .in1(5'b00010), .out(multiplexer_9_out), .sel(syscall));
  Multiplexer #(.width(5), .enable("false")) multiplexer_10 (
    .in0(IR[20:16]), .in1(5'b00100), .out(multiplexer_10_out), .sel(syscall));
  Shifter #(.width(32)) shifter_1 (.in(bit_extender_1_out), .\dist (5'b00010), .out(shifter_1_out));
  Comparator #(.width(6)) comparator_4 (.a(IR[31:26]), .b(6'b101001), .eq(SH));  // open: gt, lt
  Comparator #(.width(6)) comparator_5 (.a(IR[5:0]), .b(6'b000100), .eq(SLLV));  // open: gt, lt
  Multiplexer #(.width(5), .enable("false")) multiplexer_11 (
    .in0(multiplexer_8_out), .in1({5{1'b1}}), .out(multiplexer_11_out), .sel(jal));
  MIPS_Regifile mips_regifile_1 (
    .Din(RDin), .Clk(CLK), .R1(R1), .R2(R2), .WE(RegWrite), .W_num(multiplexer_11_out),
    .R1_num(multiplexer_9_out), .R2_num(multiplexer_10_out));
  assign bit_extender_2_out = {{16{IR[15]}}, IR[15:0]};  // Bit_Extender bit_extender_2
  Multiplexer #(.width(32), .enable("false")) multiplexer_12 (
    .in0(R2), .in1(bit_extender_2_out), .out(multiplexer_12_out), .sel(\单周期硬布线控制器_1_alu_src ));
  Multiplexer #(.width(5), .enable("false")) multiplexer_13 (
    .in0(IR[10:6]), .in1(R1[4:0]), .out(multiplexer_13_out), .sel(SLLV));
  Shifter #(.width(32)) shifter_2 (.in(bit_extender_2_out), .\dist (5'b00010), .out(shifter_2_out));
  MIPS_ALU mips_alu_1 (
    .X(R1), .Y(multiplexer_12_out), .AluOP(\单周期硬布线控制器_1_alu_op ), .Equal(mips_alu_1_equal), .Result(addr),
    .shamt(multiplexer_13_out));  // open: Result_2
  Adder #(.width(32)) adder_2 (
    .a(shifter_2_out), .b({adder_1_out, adder_1_out_2}), .out(adder_2_out));  // open: cin, cout
  and and_2 (and_2_out[1], addr[1], SH);
  and and_3 (and_3_out, \单周期硬布线控制器_1_beq , mips_alu_1_equal);
  and and_4 (and_4_out, \单周期硬布线控制器_1_bne , ~mips_alu_1_equal);  // AND_Gate
  Multiplexer #(.select(2), .width(32), .enable("false")) multiplexer_14 (
    .in0(R2), .in1({MemData[31:16], R2[15:0]}), .in3({R2[15:0], MemData[15:0]}), .out(MDinTemp),
    .sel({and_2_out[1], SH}));  // open: in2
  or or_5 (or_5_out, and_3_out, and_4_out);
  Multiplexer #(.width(32), .enable("false")) multiplexer_15 (
    .in0({32{1'b0}}), .in1(MDinTemp), .out(MDin), .sel(MemWrite));
  Multiplexer #(.width(32), .enable("false")) multiplexer_16 (
    .in0(multiplexer_17_out), .in1({adder_1_out, adder_1_out_2}), .out(RDin), .sel(jal));
  RAM #(.addrWidth(10), .dataWidth(32), .bus("separate")) ram_1 (
    .addr(addr[11:2]), .din(MDinTemp), .data(MemData), .str(MemWrite), .clk(CLK));  // open: sel, ld, clr
  Multiplexer #(.width(32), .enable("false")) multiplexer_17 (
    .in0(addr), .in1(MemData), .out(multiplexer_17_out), .sel(\单周期硬布线控制器_1_memtoreg ));

  // Other names for the same wires on the sheet: sel = addr[1]; func[5:0] = IR[5:0]; rs[4:0] = IR[25:21];
  //   op[5:0] = IR[31:26]; sel1[31:0] = {MemData[31:16], R2[15:0]}; sel2[31:0] = {R2[15:0], MemData[15:0]}

  // Notes on the sheet:
  //   中断源
  //   中断等待指示
  //   总复位信号应将除ROM以外所有存储组件全部清零
  //   数码管输出
  //   数码管输出应该用寄存器锁存，否则显示数据只能一闪而过
  //   指令存储器
  //   contents of rom_1 (hex, n*v repeats v):
  //   8000c55 24020004 20040000 c 24020005 c 3e00008 24020001 c 24020022 20040014 c 1021 3e00008 240b0001
  //   afab0018 8fa9000c 8faa0018 112a0007 8000c14 240b0002 afab001c 8fa9000c 8faa001c 112a0001 8000c1e
  //   240b0001 afab0020 8fa20020 3e00008 240b0003 afab0024 8fa9000c 8faa0024 12a082a 10200001 8000c51
  //   8f89004c 95821 afab0010 8f89004c 95821 af8b0008 240b0001 afab0038 8fa9000c 8faa0038 12a5822 afab003c
  //   1d4021 23bdffa8 afbf0000 8d09003c 95821 afab000c c000c0e 8fbf0000 23bd0058 afa20040 240b0002
  //   afab0044 8fa9000c 8faa0044 12a5822 afab0048 1d4021 23bdffa8 afbf0000 8d090048 95821 afab000c c000c0e
  //   8fbf0000 23bd0058 afa2004c 8fa90040 8faa004c 12a5820 afab0050 8fa20050 3e00008 240b0000 afab0054
  //   8fa20054 3e00008 23bdffc8 240b0001 afab0018 8fa90018 95821 afab0010 240b000a afab001c 8fa90010
  //   8faa001c 12a082a 14200001 8000ca5 240b0009 afab0000 8fa90010 8faa0000 149082a 14200001 8000c7e
  //   1d4021 23bdffa8 afbf0000 8d090010 95821 afab000c c000c0e 8fbf0000 23bd0058 afa20004 8fa90004 95821
  //   afab0014 8fa40014 23bdfffc afbf0000 c000c07 8fbf0000 23bd0004 8000ca5 8000c92 1d4021 23bdffa8
  //   afbf0000 8d090010 95821 afab000c c000c0e 8fbf0000 23bd0058 afa2000c 8fa9000c 95821 afab0014 8fa40014
  //   23bdfffc afbf0000 c000c07 8fbf0000 23bd0004 8000c9b 240b0001 afab0014 8fa90010 8faa0014 12a5820
  //   afab0018 8fa90018 95821 afab0010 240b0001 afab0020 8fa90010 8faa0020 12a5820 afab0024 8fa90024 95821
  //   afab0010 8000c5b 240b0001 afab0034 2402000a c
  //   JMP
  //   JR
  //   OP
  //   Func
  //   指令字
  //   rs
  //   rt
  //   rd
  //   shmat
  //   Imm
  //   Beq
  //   bgtz
  //   Bne
  //   MemWrite
  //   AluOP
  //   AluSrcB
  //   RegWrite
  //   JAL
  //   RegDst
  //   Syscall
  //   MemToReg
  //   为方便自动评测，需要输出PC，IR，寄存器堆写如数据RDin
  //   RAM写使能MemWrite、RAM写入数据MDin等信号
endmodule

// 单周期硬布线控制器
module \单周期硬布线控制器  (
  input  [5:0] OP,
  input  [5:0] Func,
  output [3:0] ALU_OP,
  output MemToReg,
  output MemWrite,
  output ALU_SRC,
  output RegWrite,
  output SysCALL,
  output SignedExt,
  output RegDst,
  output Beq,
  output Bne,
  output JR,
  output JMP,
  output JAL,
  output Bgtz,
  output INS1,
  output INS2,
  output INS3,
  output RET
);

  \运算控制器自动生成  \u_运算控制器自动生成_1  (
    .OP0(OP[0]), .OP1(OP[1]), .OP2(OP[2]), .OP3(OP[3]), .OP4(OP[4]), .OP5(OP[5]), .F0(Func[0]), .F1(Func[1]),
    .F2(Func[2]), .F3(Func[3]), .F4(Func[4]), .F5(Func[5]), .S0(ALU_OP[0]), .S1(ALU_OP[1]), .S2(ALU_OP[2]),
    .S3(ALU_OP[3]));
  \控制信号自动生成  \u_控制信号自动生成_1  (
    .OP0(OP[0]), .OP1(OP[1]), .OP2(OP[2]), .OP3(OP[3]), .OP4(OP[4]), .OP5(OP[5]), .F0(Func[0]), .F1(Func[1]),
    .F2(Func[2]), .F3(Func[3]), .F4(Func[4]), .F5(Func[5]), .MemToReg(MemToReg), .MemWrite(MemWrite),
    .ALU_SRC(ALU_SRC), .RegWrite(RegWrite), .SysCALL(SysCALL), .SignedExt(SignedExt), .RegDst(RegDst),
    .BEQ(Beq), .BNE(Bne), .JR(JR), .JUMP(JMP), .JAL(JAL), .Bgtz(Bgtz), .INS1(INS1), .INS2(INS2), .INS3(INS3),
    .RET(RET));

  // Other names for the same wires on the sheet: OP_CODE[5:0] = OP

  // Notes on the sheet:
  //   控制信号生成，产生数据通路需要的其他控制信号
  //   运算器控制器，根据指令生成运算器功能选择信号
endmodule

// 运算器控制器
module \运算控制器自动生成  (
  input  OP0,
  input  OP1,
  input  OP2,
  input  OP3,
  input  OP4,
  input  OP5,
  input  F0,
  input  F1,
  input  F2,
  input  F3,
  input  F4,
  input  F5,
  output S0,
  output S1,
  output S2,
  output S3
);

  wire and_1_out, and_2_out, and_3_out, and_4_out, and_5_out, and_6_out, and_7_out, and_8_out, and_9_out,
       and_10_out, and_11_out, and_12_out, and_13_out, and_14_out, and_15_out, and_16_out, and_17_out,
       and_18_out, and_19_out, and_20_out, and_21_out, and_22_out, and_23_out, and_24_out, and_25_out,
       and_26_out, and_27_out, and_28_out, and_29_out, and_30_out, and_31_out, and_32_out, and_33_out,
       and_34_out, and_35_out, and_36_out, and_37_out, and_38_out, not_1_out, not_2_out, not_3_out,
       not_4_out, not_5_out, not_6_out, not_7_out, not_8_out, not_9_out, not_10_out, not_11_out, not_12_out,
       not_13_out, not_14_out, not_15_out, not_16_out, not_17_out, not_18_out, not_19_out, not_20_out,
       not_21_out, not_22_out, not_23_out, not_24_out, not_25_out, not_26_out, not_27_out, not_28_out,
       not_29_out, not_30_out, not_31_out, not_32_out, not_33_out, not_34_out, not_35_out, not_36_out,
       not_37_out, not_38_out, not_39_out, not_40_out, not_41_out, not_42_out, not_43_out, not_44_out,
       not_45_out, not_46_out, not_47_out, not_48_out, not_49_out, not_50_out, not_51_out, not_52_out,
       not_53_out, not_54_out, not_55_out, not_56_out, not_57_out, not_58_out, not_59_out, not_60_out,
       not_61_out, not_62_out, not_63_out, not_64_out, not_65_out, not_66_out, not_67_out, not_68_out,
       not_69_out, not_70_out, not_71_out, not_72_out, not_73_out, not_74_out, not_75_out, not_76_out,
       not_77_out, not_78_out, not_79_out, not_80_out, not_81_out, not_82_out, not_83_out, not_84_out,
       not_85_out, not_86_out, not_87_out, not_88_out, not_89_out, not_90_out, not_91_out, not_92_out,
       not_93_out, not_94_out, not_95_out, not_96_out, not_97_out, not_98_out, not_99_out, not_100_out,
       not_101_out, not_102_out, not_103_out, not_104_out, not_105_out, not_106_out, not_107_out,
       not_108_out, not_109_out, not_110_out, not_111_out, not_112_out, not_113_out, not_114_out,
       not_115_out, not_116_out, not_117_out, not_118_out, not_119_out, not_120_out, not_121_out,
       not_122_out, not_123_out, not_124_out, not_125_out, not_126_out, not_127_out, not_128_out,
       not_129_out, not_130_out, not_131_out, not_132_out, not_133_out, not_134_out, not_135_out,
       not_136_out, not_137_out, not_138_out, not_139_out, not_140_out, not_141_out, not_142_out,
       not_143_out, not_144_out, not_145_out, not_146_out, not_147_out, not_148_out, not_149_out,
       not_150_out, not_151_out, not_152_out, not_153_out, not_154_out, not_155_out, not_156_out,
       not_157_out, not_158_out, not_159_out, not_160_out, not_161_out, not_162_out, not_163_out,
       not_164_out, not_165_out, not_166_out, not_167_out, not_168_out, not_169_out, not_170_out,
       not_171_out, not_172_out, not_173_out, not_174_out, not_175_out, not_176_out, not_177_out,
       not_178_out, not_179_out, not_180_out, not_181_out, not_182_out, not_183_out, not_184_out,
       not_185_out, not_186_out, not_187_out, not_188_out, not_189_out, not_190_out, not_191_out,
       not_192_out, not_193_out, not_194_out, not_195_out, not_196_out, not_197_out, not_198_out,
       not_199_out, not_200_out, not_201_out, not_202_out, not_203_out, not_204_out, not_205_out,
       not_206_out, not_207_out, not_208_out, not_209_out, not_210_out, not_211_out, not_212_out,
       not_213_out, not_214_out, not_215_out, not_216_out, not_217_out, not_218_out, not_219_out,
       not_220_out, not_221_out, not_222_out, not_223_out, not_224_out, not_225_out, not_226_out,
       not_227_out, not_228_out, not_229_out, not_230_out, not_231_out, not_232_out, not_233_out,
       not_234_out, not_235_out, not_236_out, not_237_out, not_238_out, not_239_out, not_240_out,
       not_241_out, not_242_out, not_243_out, not_244_out, not_245_out, not_246_out, not_247_out,
       not_248_out, not_249_out, not_250_out, not_251_out, not_252_out, not_253_out, not_254_out,
       not_255_out, not_256_out, not_257_out, not_258_out, not_259_out, not_260_out;

  not not_1 (not_1_out, OP5);
  not not_2 (not_2_out, OP4);
  not not_3 (not_3_out, OP3);
  not not_4 (not_4_out, OP2);
  not not_5 (not_5_out, OP1);
  not not_6 (not_6_out, OP0);
  not not_7 (not_7_out, F5);
  not not_8 (not_8_out, F4);
  not not_9 (not_9_out, F3);
  not not_10 (not_10_out, F2);
  not not_11 (not_11_out, OP5);
  not not_12 (not_12_out, OP4);
  not not_13 (not_13_out, OP3);
  not not_14 (not_14_out, OP2);
  not not_15 (not_15_out, OP1);
  not not_16 (not_16_out, OP0);
  not not_17 (not_17_out, F4);
  not not_18 (not_18_out, F3);
  not not_19 (not_19_out, F2);
  not not_20 (not_20_out, F1);
  not not_21 (not_21_out, F0);
  not not_22 (not_22_out, OP5);
  not not_23 (not_23_out, OP4);
  not not_24 (not_24_out, OP3);
  not not_25 (not_25_out, OP2);
  not not_26 (not_26_out, OP1);
  not not_27 (not_27_out, OP0);
  not not_28 (not_28_out, F4);
  not not_29 (not_29_out, F3);
  not not_30 (not_30_out, F2);
  not not_31 (not_31_out, F1);
  not not_32 (not_32_out, OP5);
  not not_33 (not_33_out, OP4);
  not not_34 (not_34_out, OP3);
  not not_35 (not_35_out, OP2);
  not not_36 (not_36_out, OP1);
  not not_37 (not_37_out, OP0);
  not not_38 (not_38_out, F4);
  not not_39 (not_39_out, F3);
  not not_40 (not_40_out, F1);
  not not_41 (not_41_out, F0);
  not not_42 (not_42_out, OP5);
  not not_43 (not_43_out, OP4);
  not not_44 (not_44_out, OP3);
  not not_45 (not_45_out, OP2);
  not not_46 (not_46_out, OP1);
  not not_47 (not_47_out, OP0);
  not not_48 (not_48_out, F4);
  not not_49 (not_49_out, F2);
  not not_50 (not_50_out, F0);
  not not_51 (not_51_out, OP5);
  not not_52 (not_52_out, OP4);
  not not_53 (not_53_out, OP2);
  not not_54 (not_54_out, OP1);
  not not_55 (not_55_out, OP0);
  not not_56 (not_56_out, OP5);
  not not_57 (not_57_out, OP4);
  not not_58 (not_58_out, OP1);
  not not_59 (not_59_out, OP0);
  not not_60 (not_60_out, OP5);
  not not_61 (not_61_out, OP4);
  not not_62 (not_62_out, OP2);
  not not_63 (not_63_out, OP1);
  not not_64 (not_64_out, OP5);
  not not_65 (not_65_out, OP4);
  not not_66 (not_66_out, OP2);
  not not_67 (not_67_out, OP0);
  not not_68 (not_68_out, OP4);
  not not_69 (not_69_out, OP3);
  not not_70 (not_70_out, OP2);
  not not_71 (not_71_out, OP4);
  not not_72 (not_72_out, OP2);
  not not_73 (not_73_out, OP5);
  not not_74 (not_74_out, OP4);
  not not_75 (not_75_out, OP3);
  not not_76 (not_76_out, OP2);
  not not_77 (not_77_out, OP1);
  not not_78 (not_78_out, OP0);
  not not_79 (not_79_out, F4);
  not not_80 (not_80_out, F3);
  not not_81 (not_81_out, F0);
  not not_82 (not_82_out, OP4);
  not not_83 (not_83_out, OP2);
  not not_84 (not_84_out, OP1);
  not not_85 (not_85_out, OP5);
  not not_86 (not_86_out, OP4);
  not not_87 (not_87_out, OP3);
  not not_88 (not_88_out, OP2);
  not not_89 (not_89_out, OP1);
  not not_90 (not_90_out, OP0);
  not not_91 (not_91_out, F5);
  not not_92 (not_92_out, F4);
  not not_93 (not_93_out, F3);
  not not_94 (not_94_out, F2);
  not not_95 (not_95_out, F0);
  not not_96 (not_96_out, OP5);
  not not_97 (not_97_out, OP4);
  not not_98 (not_98_out, OP3);
  not not_99 (not_99_out, OP2);
  not not_100 (not_100_out, OP1);
  not not_101 (not_101_out, OP0);
  not not_102 (not_102_out, F4);
  not not_103 (not_103_out, F3);
  not not_104 (not_104_out, F2);
  not not_105 (not_105_out, F0);
  not not_106 (not_106_out, OP5);
  not not_107 (not_107_out, OP4);
  not not_108 (not_108_out, OP3);
  not not_109 (not_109_out, OP2);
  not not_110 (not_110_out, OP1);
  not not_111 (not_111_out, OP0);
  not not_112 (not_112_out, F4);
  not not_113 (not_113_out, F3);
  not not_114 (not_114_out, F1);
  not not_115 (not_115_out, F0);
  not not_116 (not_116_out, OP5);
  not not_117 (not_117_out, OP4);
  not not_118 (not_118_out, OP3);
  not not_119 (not_119_out, OP2);
  not not_120 (not_120_out, OP1);
  not not_121 (not_121_out, OP0);
  not not_122 (not_122_out, F4);
  not not_123 (not_123_out, F3);
  not not_124 (not_124_out, OP5);
  not not_125 (not_125_out, OP4);
  not not_126 (not_126_out, OP3);
  not not_127 (not_127_out, OP2);
  not not_128 (not_128_out, OP1);
  not not_129 (not_129_out, OP0);
  not not_130 (not_130_out, F4);
  not not_131 (not_131_out, F2);
  not not_132 (not_132_out, F0);
  not not_133 (not_133_out, OP5);
  not not_134 (not_134_out, OP4);
  not not_135 (not_135_out, OP1);
  not not_136 (not_136_out, OP0);
  not not_137 (not_137_out, OP5);
  not not_138 (not_138_out, OP4);
  not not_139 (not_139_out, OP2);
  not not_140 (not_140_out, OP0);
  not not_141 (not_141_out, OP5);
  not not_142 (not_142_out, OP4);
  not not_143 (not_143_out, OP3);
  not not_144 (not_144_out, OP2);
  not not_145 (not_145_out, OP1);
  not not_146 (not_146_out, OP0);
  not not_147 (not_147_out, F4);
  not not_148 (not_148_out, F3);
  not not_149 (not_149_out, F2);
  not not_150 (not_150_out, F1);
  not not_151 (not_151_out, F0);
  not not_152 (not_152_out, OP5);
  not not_153 (not_153_out, OP4);
  not not_154 (not_154_out, OP3);
  not not_155 (not_155_out, OP2);
  not not_156 (not_156_out, OP1);
  not not_157 (not_157_out, OP0);
  not not_158 (not_158_out, F4);
  not not_159 (not_159_out, F3);
  not not_160 (not_160_out, F2);
  not not_161 (not_161_out, F1);
  not not_162 (not_162_out, OP5);
  not not_163 (not_163_out, OP4);
  not not_164 (not_164_out, OP3);
  not not_165 (not_165_out, OP2);
  not not_166 (not_166_out, OP1);
  not not_167 (not_167_out, OP0);
  not not_168 (not_168_out, F4);
  not not_169 (not_169_out, F3);
  not not_170 (not_170_out, F2);
  not not_171 (not_171_out, F0);
  not not_172 (not_172_out, OP5);
  not not_173 (not_173_out, OP4);
  not not_174 (not_174_out, OP3);
  not not_175 (not_175_out, OP2);
  not not_176 (not_176_out, OP1);
  not not_177 (not_177_out, OP0);
  not not_178 (not_178_out, F4);
  not not_179 (not_179_out, F3);
  not not_180 (not_180_out, F1);
  not not_181 (not_181_out, F0);
  not not_182 (not_182_out, OP5);
  not not_183 (not_183_out, OP4);
  not not_184 (not_184_out, OP3);
  not not_185 (not_185_out, OP2);
  not not_186 (not_186_out, OP1);
  not not_187 (not_187_out, OP0);
  not not_188 (not_188_out, F4);
  not not_189 (not_189_out, F2);
  not not_190 (not_190_out, OP5);
  not not_191 (not_191_out, OP4);
  not not_192 (not_192_out, OP2);
  not not_193 (not_193_out, OP1);
  not not_194 (not_194_out, OP0);
  not not_195 (not_195_out, OP5);
  not not_196 (not_196_out, OP4);
  not not_197 (not_197_out, OP1);
  not not_198 (not_198_out, OP0);
  not not_199 (not_199_out, OP5);
  not not_200 (not_200_out, OP4);
  not not_201 (not_201_out, OP2);
  not not_202 (not_202_out, OP1);
  not not_203 (not_203_out, OP4);
  not not_204 (not_204_out, OP3);
  not not_205 (not_205_out, OP2);
  not not_206 (not_206_out, OP4);
  not not_207 (not_207_out, OP2);
  not not_208 (not_208_out, OP4);
  not not_209 (not_209_out, OP2);
  not not_210 (not_210_out, OP1);
  not not_211 (not_211_out, OP5);
  not not_212 (not_212_out, OP4);
  not not_213 (not_213_out, OP3);
  not not_214 (not_214_out, OP2);
  not not_215 (not_215_out, OP1);
  not not_216 (not_216_out, OP0);
  not not_217 (not_217_out, F4);
  not not_218 (not_218_out, F3);
  not not_219 (not_219_out, F1);
  not not_220 (not_220_out, OP5);
  not not_221 (not_221_out, OP4);
  not not_222 (not_222_out, OP3);
  not not_223 (not_223_out, OP2);
  not not_224 (not_224_out, OP1);
  not not_225 (not_225_out, OP0);
  not not_226 (not_226_out, F4);
  not not_227 (not_227_out, F3);
  not not_228 (not_228_out, OP5);
  not not_229 (not_229_out, OP4);
  not not_230 (not_230_out, OP3);
  not not_231 (not_231_out, OP2);
  not not_232 (not_232_out, OP1);
  not not_233 (not_233_out, OP0);
  not not_234 (not_234_out, F4);
  not not_235 (not_235_out, F2);
  not not_236 (not_236_out, F0);
  not not_237 (not_237_out, OP5);
  not not_238 (not_238_out, OP4);
  not not_239 (not_239_out, OP3);
  not not_240 (not_240_out, OP2);
  not not_241 (not_241_out, OP1);
  not not_242 (not_242_out, OP0);
  not not_243 (not_243_out, F4);
  not not_244 (not_244_out, F2);
  not not_245 (not_245_out, OP5);
  not not_246 (not_246_out, OP4);
  not not_247 (not_247_out, OP2);
  not not_248 (not_248_out, OP0);
  not not_249 (not_249_out, OP5);
  not not_250 (not_250_out, OP4);
  not not_251 (not_251_out, OP1);
  not not_252 (not_252_out, OP5);
  not not_253 (not_253_out, OP4);
  not not_254 (not_254_out, OP3);
  not not_255 (not_255_out, OP2);
  not not_256 (not_256_out, OP1);
  not not_257 (not_257_out, OP0);
  not not_258 (not_258_out, F4);
  not not_259 (not_259_out, F3);
  not not_260 (not_260_out, F0);
  and and_1 (and_1_out, not_1_out, not_2_out, not_3_out, not_4_out, not_5_out, not_6_out, not_7_out, not_8_out, not_9_out, not_10_out, F1, F0);
  and and_2 (and_2_out, not_11_out, not_12_out, not_13_out, not_14_out, not_15_out, not_16_out, F5, not_17_out, not_18_out, not_19_out, not_20_out, not_21_out);
  and and_3 (and_3_out, not_22_out, not_23_out, not_24_out, not_25_out, not_26_out, not_27_out, F5, not_28_out, not_29_out, not_30_out, not_31_out, F0);
  and and_4 (and_4_out, not_32_out, not_33_out, not_34_out, not_35_out, not_36_out, not_37_out, F5, not_38_out, not_39_out, F2, not_40_out, not_41_out);
  and and_5 (and_5_out, not_42_out, not_43_out, not_44_out, not_45_out, not_46_out, not_47_out, F5, not_48_out, F3, not_49_out, F1, not_50_out);
  and and_6 (and_6_out, not_51_out, not_52_out, OP3, not_53_out, not_54_out, not_55_out);
  and and_7 (and_7_out, not_56_out, not_57_out, OP3, OP2, not_58_out, not_59_out);
  and and_8 (and_8_out, not_60_out, not_61_out, OP3, not_62_out, not_63_out, OP0);
  and and_9 (and_9_out, not_64_out, not_65_out, OP3, not_66_out, OP1, not_67_out);
  and and_10 (and_10_out, OP5, not_68_out, not_69_out, not_70_out, OP1, OP0);
  and and_11 (and_11_out, OP5, not_71_out, OP3, not_72_out, OP1, OP0);
  and and_12 (and_12_out, not_73_out, not_74_out, not_75_out, not_76_out, not_77_out, not_78_out, F5, not_79_out, not_80_out, F2, F1, not_81_out);
  and and_13 (and_13_out, OP5, not_82_out, OP3, not_83_out, not_84_out, OP0);
  and and_14 (and_14_out, not_85_out, not_86_out, not_87_out, not_88_out, not_89_out, not_90_out, not_91_out, not_92_out, not_93_out, not_94_out, F1, not_95_out);
  and and_15 (and_15_out, not_96_out, not_97_out, not_98_out, not_99_out, not_100_out, not_101_out, F5, not_102_out, not_103_out, not_104_out, F1, not_105_out);
  and and_16 (and_16_out, not_106_out, not_107_out, not_108_out, not_109_out, not_110_out, not_111_out, F5, not_112_out, not_113_out, F2, not_114_out, not_115_out);
  and and_17 (and_17_out, not_116_out, not_117_out, not_118_out, not_119_out, not_120_out, not_121_out, F5, not_122_out, not_123_out, F2, F1, F0);
  and and_18 (and_18_out, not_124_out, not_125_out, not_126_out, not_127_out, not_128_out, not_129_out, F5, not_130_out, F3, not_131_out, F1, not_132_out);
  and and_19 (and_19_out, not_133_out, not_134_out, OP3, OP2, not_135_out, not_136_out);
  and and_20 (and_20_out, not_137_out, not_138_out, OP3, not_139_out, OP1, not_140_out);
  and and_21 (and_21_out, not_141_out, not_142_out, not_143_out, not_144_out, not_145_out, not_146_out, F5, not_147_out, not_148_out, not_149_out, not_150_out, not_151_out);
  and and_22 (and_22_out, not_152_out, not_153_out, not_154_out, not_155_out, not_156_out, not_157_out, F5, not_158_out, not_159_out, not_160_out, not_161_out, F0);
  and and_23 (and_23_out, not_162_out, not_163_out, not_164_out, not_165_out, not_166_out, not_167_out, F5, not_168_out, not_169_out, not_170_out, F1, not_171_out);
  and and_24 (and_24_out, not_172_out, not_173_out, not_174_out, not_175_out, not_176_out, not_177_out, F5, not_178_out, not_179_out, F2, not_180_out, not_181_out);
  and and_25 (and_25_out, not_182_out, not_183_out, not_184_out, not_185_out, not_186_out, not_187_out, F5, not_188_out, F3, not_189_out, F1, F0);
  and and_26 (and_26_out, not_190_out, not_191_out, OP3, not_192_out, not_193_out, not_194_out);
  and and_27 (and_27_out, not_195_out, not_196_out, OP3, OP2, not_197_out, not_198_out);
  and and_28 (and_28_out, not_199_out, not_200_out, OP3, not_201_out, not_202_out, OP0);
  and and_29 (and_29_out, OP5, not_203_out, not_204_out, not_205_out, OP1, OP0);
  and and_30 (and_30_out, OP5, not_206_out, OP3, not_207_out, OP1, OP0);
  and and_31 (and_31_out, OP5, not_208_out, OP3, not_209_out, not_210_out, OP0);
  and and_32 (and_32_out, not_211_out, not_212_out, not_213_out, not_214_out, not_215_out, not_216_out, F5, not_217_out, not_218_out, F2, not_219_out, F0);
  and and_33 (and_33_out, not_220_out, not_221_out, not_222_out, not_223_out, not_224_out, not_225_out, F5, not_226_out, not_227_out, F2, F1, F0);
  and and_34 (and_34_out, not_228_out, not_229_out, not_230_out, not_231_out, not_232_out, not_233_out, F5, not_234_out, F3, not_235_out, F1, not_236_out);
  and and_35 (and_35_out, not_237_out, not_238_out, not_239_out, not_240_out, not_241_out, not_242_out, F5, not_243_out, F3, not_244_out, F1, F0);
  and and_36 (and_36_out, not_245_out, not_246_out, OP3, not_247_out, OP1, not_248_out);
  and and_37 (and_37_out, not_249_out, not_250_out, OP3, OP2, not_251_out, OP0);
  and and_38 (and_38_out, not_252_out, not_253_out, not_254_out, not_255_out, not_256_out, not_257_out, F5, not_258_out, not_259_out, F2, F1, not_260_out);
  or or_1 (S1, and_14_out, and_15_out, and_16_out, and_17_out, and_18_out, and_19_out, and_20_out);
  or or_2 (S2, and_21_out, and_22_out, and_23_out, and_24_out, and_25_out, and_26_out, and_27_out, and_28_out, and_29_out, and_30_out, and_31_out);
  or or_3 (S3, and_32_out, and_33_out, and_34_out, and_35_out, and_36_out, and_37_out, and_38_out);
  or or_4 (S0, and_1_out, and_2_out, and_3_out, and_4_out, and_5_out, and_6_out, and_7_out, and_8_out, and_9_out, and_10_out, and_11_out, and_12_out, and_13_out);
endmodule

// 控制信号生成
module \控制信号自动生成  (
  input  OP0,
  input  OP1,
  input  OP2,
  input  OP3,
  input  OP4,
  input  OP5,
  input  F0,
  input  F1,
  input  F2,
  input  F3,
  input  F4,
  input  F5,
  output MemToReg,
  output MemWrite,
  output ALU_SRC,
  output RegWrite,
  output SysCALL,
  output SignedExt,
  output RegDst,
  output BEQ,
  output BNE,
  output JR,
  output JUMP,
  output JAL,
  output Bgtz,
  output INS1,
  output INS2,
  output INS3,
  output RET
);

  wire and_2_out, and_3_out, and_4_out, and_5_out, and_6_out, and_7_out, and_8_out, and_9_out, and_10_out,
       and_11_out, and_12_out, and_13_out, and_14_out, and_15_out, and_16_out, and_17_out, and_18_out,
       and_19_out, and_20_out, and_21_out, and_22_out, and_23_out, and_24_out, and_25_out, and_26_out,
       and_27_out, and_28_out, and_29_out, and_30_out, and_31_out, and_33_out, and_34_out, and_35_out,
       and_36_out, and_37_out, and_38_out, and_39_out, and_40_out, and_41_out, and_42_out, and_43_out,
       and_44_out, and_45_out, and_46_out, and_47_out, and_48_out, and_49_out, and_50_out, and_51_out,
       and_55_out, and_56_out, and_57_out, and_60_out, and_61_out, and_62_out, and_63_out, and_64_out,
       and_65_out, and_66_out, and_67_out, and_68_out, and_69_out, and_70_out, and_71_out, and_72_out,
       and_73_out, and_74_out, and_75_out, and_76_out, and_77_out, and_78_out, and_79_out, and_80_out,
       and_81_out, and_82_out, and_83_out, and_84_out, and_85_out, not_1_out, not_2_out, not_3_out,
       not_4_out, not_5_out, not_6_out, not_7_out, not_8_out, not_9_out, not_10_out, not_11_out, not_12_out,
       not_13_out, not_14_out, not_15_out, not_16_out, not_17_out, not_18_out, not_19_out, not_20_out,
       not_21_out, not_22_out, not_23_out, not_24_out, not_25_out, not_26_out, not_27_out, not_28_out,
       not_29_out, not_30_out, not_31_out, not_32_out, not_33_out, not_34_out, not_35_out, not_36_out,
       not_37_out, not_38_out, not_39_out, not_40_out, not_41_out, not_42_out, not_43_out, not_44_out,
       not_45_out, not_46_out, not_47_out, not_48_out, not_49_out, not_50_out, not_51_out, not_52_out,
       not_53_out, not_54_out, not_55_out, not_56_out, not_57_out, not_58_out, not_59_out, not_60_out,
       not_61_out, not_62_out, not_63_out, not_64_out, not_65_out, not_66_out, not_67_out, not_68_out,
       not_69_out, not_70_out, not_71_out, not_72_out, not_73_out, not_74_out, not_75_out, not_76_out,
       not_77_out, not_78_out, not_79_out, not_80_out, not_81_out, not_82_out, not_83_out, not_84_out,
       not_85_out, not_86_out, not_87_out, not_88_out, not_89_out, not_90_out, not_91_out, not_92_out,
       not_93_out, not_94_out, not_95_out, not_96_out, not_97_out, not_98_out, not_99_out, not_100_out,
       not_101_out, not_102_out, not_103_out, not_104_out, not_105_out, not_106_out, not_107_out,
       not_108_out, not_109_out, not_110_out, not_111_out, not_112_out, not_113_out, not_114_out,
       not_115_out, not_116_out, not_117_out, not_118_out, not_119_out, not_120_out, not_121_out,
       not_122_out, not_123_out, not_124_out, not_125_out, not_126_out, not_127_out, not_128_out,
       not_129_out, not_130_out, not_131_out, not_132_out, not_133_out, not_134_out, not_135_out,
       not_136_out, not_137_out, not_138_out, not_139_out, not_140_out, not_141_out, not_142_out,
       not_143_out, not_144_out, not_145_out, not_146_out, not_147_out, not_148_out, not_149_out,
       not_150_out, not_151_out, not_152_out, not_153_out, not_154_out, not_155_out, not_156_out,
       not_157_out, not_158_out, not_159_out, not_160_out, not_161_out, not_162_out, not_163_out,
       not_164_out, not_165_out, not_166_out, not_167_out, not_168_out, not_169_out, not_170_out,
       not_171_out, not_172_out, not_173_out, not_174_out, not_175_out, not_176_out, not_177_out,
       not_178_out, not_179_out, not_180_out, not_181_out, not_182_out, not_183_out, not_184_out,
       not_185_out, not_186_out, not_187_out, not_188_out, not_189_out, not_190_out, not_191_out,
       not_192_out, not_193_out, not_194_out, not_195_out, not_196_out, not_197_out, not_198_out,
       not_199_out, not_200_out, not_201_out, not_202_out, not_203_out, not_204_out, not_205_out,
       not_206_out, not_207_out, not_208_out, not_209_out, not_210_out, not_211_out, not_212_out,
       not_213_out, not_214_out, not_215_out, not_216_out, not_217_out, not_218_out, not_219_out,
       not_220_out, not_221_out, not_222_out, not_223_out, not_224_out, not_225_out, not_226_out,
       not_227_out, not_228_out, not_229_out, not_230_out, not_231_out, not_232_out, not_233_out,
       not_234_out, not_235_out, not_236_out, not_237_out, not_238_out, not_239_out, not_240_out,
       not_241_out, not_242_out, not_243_out, not_244_out, not_245_out, not_246_out, not_247_out,
       not_248_out, not_249_out, not_250_out, not_251_out, not_252_out, not_253_out, not_254_out,
       not_255_out, not_256_out, not_257_out, not_258_out, not_259_out, not_260_out, not_261_out,
       not_262_out, not_263_out, not_264_out, not_265_out, not_266_out, not_267_out, not_268_out,
       not_269_out, not_270_out, not_271_out, not_272_out, not_273_out, not_274_out, not_275_out,
       not_276_out, not_277_out, not_278_out, not_279_out, not_280_out, not_281_out, not_282_out,
       not_283_out, not_284_out, not_285_out, not_286_out, not_287_out, not_288_out, not_289_out,
       not_290_out, not_291_out, not_292_out, not_293_out, not_294_out, not_295_out, not_296_out,
       not_297_out, not_298_out, not_299_out, not_300_out, not_301_out, not_302_out, not_303_out,
       not_304_out, not_305_out, not_306_out, not_307_out, not_308_out, not_309_out, not_310_out,
       not_311_out, not_312_out, not_313_out, not_314_out, not_315_out, not_316_out, not_317_out,
       not_318_out, not_319_out, not_320_out, not_321_out, not_322_out, not_323_out, not_324_out,
       not_325_out, not_326_out, not_327_out, not_328_out, not_329_out, not_330_out, not_331_out,
       not_332_out, not_333_out, not_334_out, not_335_out, not_336_out, not_337_out, not_338_out,
       not_339_out, not_340_out, not_341_out, not_342_out, not_343_out, not_344_out, not_345_out,
       not_346_out, not_347_out, not_348_out, not_349_out, not_350_out, not_351_out, not_352_out,
       not_353_out, not_354_out, not_355_out, not_356_out, not_357_out, not_358_out, not_359_out,
       not_360_out, not_361_out, not_362_out, not_363_out, not_364_out, not_365_out, not_366_out,
       not_367_out, not_368_out, not_369_out, not_370_out, not_371_out, not_372_out, not_373_out,
       not_374_out, not_375_out, not_376_out, not_377_out, not_378_out, not_379_out, not_380_out,
       not_381_out, not_382_out, not_383_out, not_384_out, not_385_out, not_386_out, not_387_out,
       not_388_out, not_389_out, not_390_out, not_391_out, not_392_out, not_393_out, not_394_out,
       not_395_out, not_396_out, not_397_out, not_398_out, not_399_out, not_400_out, not_401_out,
       not_402_out, not_403_out, not_404_out, not_405_out, not_406_out, not_407_out, not_408_out,
       not_409_out, not_410_out, not_411_out, not_412_out, not_413_out, not_414_out, not_415_out,
       not_416_out, not_417_out, not_418_out, not_419_out, not_420_out, not_421_out, not_422_out,
       not_423_out, not_424_out, not_425_out, not_426_out, not_427_out, not_428_out, not_429_out,
       not_430_out, not_431_out, not_432_out, not_433_out, not_434_out, not_435_out, not_436_out,
       not_437_out, not_438_out, not_439_out, not_440_out, not_441_out, not_442_out, not_443_out,
       not_444_out, not_445_out, not_446_out, not_447_out, not_448_out, not_449_out, not_450_out,
       not_451_out, not_452_out, not_453_out, not_454_out, not_455_out, not_456_out, not_457_out,
       not_458_out, not_459_out, not_460_out, not_461_out, not_462_out, not_463_out, not_464_out,
       not_465_out, not_466_out, not_467_out, not_468_out, not_469_out, not_470_out, not_471_out,
       not_472_out, not_473_out, not_474_out, not_475_out, not_476_out, not_477_out, not_478_out,
       not_479_out, not_480_out, not_481_out, not_482_out, not_483_out, not_484_out, not_485_out,
       not_486_out, not_487_out, not_488_out, not_489_out, not_490_out, not_491_out, not_492_out,
       not_493_out, not_494_out, not_495_out, not_496_out, not_497_out, not_498_out, not_499_out,
       not_500_out, not_501_out, not_502_out, not_503_out, not_504_out, not_505_out, not_506_out,
       not_507_out, not_508_out, not_509_out, not_510_out, not_511_out, not_512_out, not_513_out,
       not_514_out, not_515_out, not_516_out, not_517_out, not_518_out, not_519_out, not_520_out,
       not_521_out, not_522_out, not_523_out, not_524_out, not_525_out, not_526_out, not_527_out,
       not_528_out, not_529_out, not_530_out, not_531_out, not_532_out, not_533_out, not_534_out,
       not_535_out, not_536_out, not_537_out, not_538_out, not_539_out, not_540_out, not_541_out,
       not_542_out, not_543_out, not_544_out, not_545_out, not_546_out, not_547_out, not_548_out,
       not_549_out, not_550_out, not_551_out, not_552_out, not_553_out, not_554_out, not_555_out,
       not_556_out, not_557_out, not_558_out, not_559_out, not_560_out, not_561_out, not_562_out,
       not_563_out, not_564_out, not_565_out, not_566_out, not_567_out, not_568_out, not_569_out,
       not_570_out, not_571_out, not_572_out, not_573_out, not_574_out, not_575_out, not_576_out,
       not_577_out, not_578_out, not_579_out, not_580_out, not_581_out, not_582_out, not_583_out,
       not_584_out, not_585_out, not_586_out, not_587_out, not_588_out, not_589_out, not_590_out, not_591_out;

  not not_1 (not_1_out, OP4);
  not not_2 (not_2_out, OP3);
  not not_3 (not_3_out, OP2);
  not not_4 (not_4_out, OP4);
  not not_5 (not_5_out, OP2);
  not not_6 (not_6_out, OP4);
  not not_7 (not_7_out, OP2);
  not not_8 (not_8_out, OP1);
  not not_9 (not_9_out, OP5);
  not not_10 (not_10_out, OP4);
  not not_11 (not_11_out, OP2);
  not not_12 (not_12_out, OP1);
  not not_13 (not_13_out, OP0);
  not not_14 (not_14_out, OP5);
  not not_15 (not_15_out, OP4);
  not not_16 (not_16_out, OP1);
  not not_17 (not_17_out, OP0);
  not not_18 (not_18_out, OP5);
  not not_19 (not_19_out, OP4);
  not not_20 (not_20_out, OP2);
  not not_21 (not_21_out, OP1);
  not not_22 (not_22_out, OP5);
  not not_23 (not_23_out, OP4);
  not not_24 (not_24_out, OP2);
  not not_25 (not_25_out, OP0);
  not not_26 (not_26_out, OP5);
  not not_27 (not_27_out, OP4);
  not not_28 (not_28_out, OP1);
  not not_29 (not_29_out, OP4);
  not not_30 (not_30_out, OP3);
  not not_31 (not_31_out, OP2);
  not not_32 (not_32_out, OP4);
  not not_33 (not_33_out, OP2);
  not not_34 (not_34_out, OP4);
  not not_35 (not_35_out, OP2);
  not not_36 (not_36_out, OP1);
  not not_37 (not_37_out, OP5);
  not not_38 (not_38_out, OP4);
  not not_39 (not_39_out, OP3);
  not not_40 (not_40_out, OP2);
  not not_41 (not_41_out, OP1);
  not not_42 (not_42_out, OP0);
  not not_43 (not_43_out, F5);
  not not_44 (not_44_out, F4);
  not not_45 (not_45_out, F3);
  not not_46 (not_46_out, F2);
  not not_47 (not_47_out, F1);
  not not_48 (not_48_out, F0);
  not not_49 (not_49_out, OP5);
  not not_50 (not_50_out, OP4);
  not not_51 (not_51_out, OP3);
  not not_52 (not_52_out, OP2);
  not not_53 (not_53_out, OP1);
  not not_54 (not_54_out, OP0);
  not not_55 (not_55_out, F5);
  not not_56 (not_56_out, F4);
  not not_57 (not_57_out, F3);
  not not_58 (not_58_out, F2);
  not not_59 (not_59_out, OP5);
  not not_60 (not_60_out, OP4);
  not not_61 (not_61_out, OP3);
  not not_62 (not_62_out, OP2);
  not not_63 (not_63_out, OP1);
  not not_64 (not_64_out, OP0);
  not not_65 (not_65_out, F5);
  not not_66 (not_66_out, F4);
  not not_67 (not_67_out, F3);
  not not_68 (not_68_out, F2);
  not not_69 (not_69_out, F0);
  not not_70 (not_70_out, OP5);
  not not_71 (not_71_out, OP4);
  not not_72 (not_72_out, OP3);
  not not_73 (not_73_out, OP2);
  not not_74 (not_74_out, OP1);
  not not_75 (not_75_out, OP0);
  not not_76 (not_76_out, F4);
  not not_77 (not_77_out, F3);
  not not_78 (not_78_out, F2);
  not not_79 (not_79_out, F1);
  not not_80 (not_80_out, F0);
  not not_81 (not_81_out, OP5);
  not not_82 (not_82_out, OP4);
  not not_83 (not_83_out, OP3);
  not not_84 (not_84_out, OP2);
  not not_85 (not_85_out, OP1);
  not not_86 (not_86_out, OP0);
  not not_87 (not_87_out, F4);
  not not_88 (not_88_out, F3);
  not not_89 (not_89_out, F2);
  not not_90 (not_90_out, F1);
  not not_91 (not_91_out, OP5);
  not not_92 (not_92_out, OP4);
  not not_93 (not_93_out, OP3);
  not not_94 (not_94_out, OP2);
  not not_95 (not_95_out, OP1);
  not not_96 (not_96_out, OP0);
  not not_97 (not_97_out, F4);
  not not_98 (not_98_out, F3);
  not not_99 (not_99_out, F2);
  not not_100 (not_100_out, F0);
  not not_101 (not_101_out, OP5);
  not not_102 (not_102_out, OP4);
  not not_103 (not_103_out, OP3);
  not not_104 (not_104_out, OP2);
  not not_105 (not_105_out, OP1);
  not not_106 (not_106_out, OP0);
  not not_107 (not_107_out, F4);
  not not_108 (not_108_out, F3);
  not not_109 (not_109_out, F1);
  not not_110 (not_110_out, F0);
  not not_111 (not_111_out, OP5);
  not not_112 (not_112_out, OP4);
  not not_113 (not_113_out, OP3);
  not not_114 (not_114_out, OP2);
  not not_115 (not_115_out, OP1);
  not not_116 (not_116_out, OP0);
  not not_117 (not_117_out, F4);
  not not_118 (not_118_out, F3);
  not not_119 (not_119_out, F1);
  not not_120 (not_120_out, OP5);
  not not_121 (not_121_out, OP4);
  not not_122 (not_122_out, OP3);
  not not_123 (not_123_out, OP2);
  not not_124 (not_124_out, OP1);
  not not_125 (not_125_out, OP0);
  not not_126 (not_126_out, F4);
  not not_127 (not_127_out, F3);
  not not_128 (not_128_out, OP5);
  not not_129 (not_129_out, OP4);
  not not_130 (not_130_out, OP3);
  not not_131 (not_131_out, OP2);
  not not_132 (not_132_out, OP1);
  not not_133 (not_133_out, OP0);
  not not_134 (not_134_out, F4);
  not not_135 (not_135_out, F2);
  not not_136 (not_136_out, F0);
  not not_137 (not_137_out, OP5);
  not not_138 (not_138_out, OP4);
  not not_139 (not_139_out, OP3);
  not not_140 (not_140_out, OP2);
  not not_141 (not_141_out, OP1);
  not not_142 (not_142_out, OP0);
  not not_143 (not_143_out, F4);
  not not_144 (not_144_out, F2);
  not not_145 (not_145_out, OP5);
  not not_146 (not_146_out, OP4);
  not not_147 (not_147_out, OP3);
  not not_148 (not_148_out, OP2);
  not not_149 (not_149_out, OP5);
  not not_150 (not_150_out, OP4);
  not not_151 (not_151_out, OP2);
  not not_152 (not_152_out, OP1);
  not not_153 (not_153_out, OP0);
  not not_154 (not_154_out, OP5);
  not not_155 (not_155_out, OP4);
  not not_156 (not_156_out, OP1);
  not not_157 (not_157_out, OP0);
  not not_158 (not_158_out, OP5);
  not not_159 (not_159_out, OP4);
  not not_160 (not_160_out, OP2);
  not not_161 (not_161_out, OP1);
  not not_162 (not_162_out, OP5);
  not not_163 (not_163_out, OP4);
  not not_164 (not_164_out, OP2);
  not not_165 (not_165_out, OP0);
  not not_166 (not_166_out, OP5);
  not not_167 (not_167_out, OP4);
  not not_168 (not_168_out, OP1);
  not not_169 (not_169_out, OP4);
  not not_170 (not_170_out, OP3);
  not not_171 (not_171_out, OP2);
  not not_172 (not_172_out, OP5);
  not not_173 (not_173_out, OP4);
  not not_174 (not_174_out, OP3);
  not not_175 (not_175_out, OP2);
  not not_176 (not_176_out, OP1);
  not not_177 (not_177_out, OP0);
  not not_178 (not_178_out, F4);
  not not_179 (not_179_out, F3);
  not not_180 (not_180_out, F0);
  not not_181 (not_181_out, OP5);
  not not_182 (not_182_out, OP4);
  not not_183 (not_183_out, OP3);
  not not_184 (not_184_out, OP2);
  not not_185 (not_185_out, OP1);
  not not_186 (not_186_out, OP0);
  not not_187 (not_187_out, F5);
  not not_188 (not_188_out, F4);
  not not_189 (not_189_out, F3);
  not not_190 (not_190_out, F1);
  not not_191 (not_191_out, F0);
  not not_192 (not_192_out, OP5);
  not not_193 (not_193_out, OP4);
  not not_194 (not_194_out, OP3);
  not not_195 (not_195_out, OP2);
  not not_196 (not_196_out, OP1);
  not not_197 (not_197_out, OP0);
  not not_198 (not_198_out, F5);
  not not_199 (not_199_out, F4);
  not not_200 (not_200_out, F1);
  not not_201 (not_201_out, F0);
  not not_202 (not_202_out, OP5);
  not not_203 (not_203_out, OP4);
  not not_204 (not_204_out, OP2);
  not not_205 (not_205_out, OP1);
  not not_206 (not_206_out, OP0);
  not not_207 (not_207_out, OP5);
  not not_208 (not_208_out, OP4);
  not not_209 (not_209_out, OP2);
  not not_210 (not_210_out, OP1);
  not not_211 (not_211_out, OP5);
  not not_212 (not_212_out, OP4);
  not not_213 (not_213_out, OP2);
  not not_214 (not_214_out, OP0);
  not not_215 (not_215_out, OP4);
  not not_216 (not_216_out, OP3);
  not not_217 (not_217_out, OP2);
  not not_218 (not_218_out, OP4);
  not not_219 (not_219_out, OP2);
  not not_220 (not_220_out, OP4);
  not not_221 (not_221_out, OP2);
  not not_222 (not_222_out, OP1);
  not not_223 (not_223_out, OP5);
  not not_224 (not_224_out, OP4);
  not not_225 (not_225_out, OP3);
  not not_226 (not_226_out, OP2);
  not not_227 (not_227_out, OP1);
  not not_228 (not_228_out, OP0);
  not not_229 (not_229_out, F5);
  not not_230 (not_230_out, F4);
  not not_231 (not_231_out, F3);
  not not_232 (not_232_out, F2);
  not not_233 (not_233_out, F1);
  not not_234 (not_234_out, F0);
  not not_235 (not_235_out, OP5);
  not not_236 (not_236_out, OP4);
  not not_237 (not_237_out, OP3);
  not not_238 (not_238_out, OP2);
  not not_239 (not_239_out, OP1);
  not not_240 (not_240_out, OP0);
  not not_241 (not_241_out, F5);
  not not_242 (not_242_out, F4);
  not not_243 (not_243_out, F3);
  not not_244 (not_244_out, F2);
  not not_245 (not_245_out, OP5);
  not not_246 (not_246_out, OP4);
  not not_247 (not_247_out, OP3);
  not not_248 (not_248_out, OP2);
  not not_249 (not_249_out, OP1);
  not not_250 (not_250_out, OP0);
  not not_251 (not_251_out, F5);
  not not_252 (not_252_out, F4);
  not not_253 (not_253_out, F3);
  not not_254 (not_254_out, F2);
  not not_255 (not_255_out, F0);
  not not_256 (not_256_out, OP5);
  not not_257 (not_257_out, OP4);
  not not_258 (not_258_out, OP3);
  not not_259 (not_259_out, OP2);
  not not_260 (not_260_out, OP1);
  not not_261 (not_261_out, OP0);
  not not_262 (not_262_out, F4);
  not not_263 (not_263_out, F3);
  not not_264 (not_264_out, F2);
  not not_265 (not_265_out, F1);
  not not_266 (not_266_out, F0);
  not not_267 (not_267_out, OP5);
  not not_268 (not_268_out, OP4);
  not not_269 (not_269_out, OP3);
  not not_270 (not_270_out, OP2);
  not not_271 (not_271_out, OP1);
  not not_272 (not_272_out, OP0);
  not not_273 (not_273_out, F4);
  not not_274 (not_274_out, F3);
  not not_275 (not_275_out, F2);
  not not_276 (not_276_out, F1);
  not not_277 (not_277_out, OP5);
  not not_278 (not_278_out, OP4);
  not not_279 (not_279_out, OP3);
  not not_280 (not_280_out, OP2);
  not not_281 (not_281_out, OP1);
  not not_282 (not_282_out, OP0);
  not not_283 (not_283_out, F4);
  not not_284 (not_284_out, F3);
  not not_285 (not_285_out, F2);
  not not_286 (not_286_out, F0);
  not not_287 (not_287_out, OP5);
  not not_288 (not_288_out, OP4);
  not not_289 (not_289_out, OP3);
  not not_290 (not_290_out, OP2);
  not not_291 (not_291_out, OP1);
  not not_292 (not_292_out, OP0);
  not not_293 (not_293_out, F4);
  not not_294 (not_294_out, F3);
  not not_295 (not_295_out, F1);
  not not_296 (not_296_out, F0);
  not not_297 (not_297_out, OP5);
  not not_298 (not_298_out, OP4);
  not not_299 (not_299_out, OP3);
  not not_300 (not_300_out, OP2);
  not not_301 (not_301_out, OP1);
  not not_302 (not_302_out, OP0);
  not not_303 (not_303_out, F4);
  not not_304 (not_304_out, F3);
  not not_305 (not_305_out, F1);
  not not_306 (not_306_out, OP5);
  not not_307 (not_307_out, OP4);
  not not_308 (not_308_out, OP3);
  not not_309 (not_309_out, OP2);
  not not_310 (not_310_out, OP1);
  not not_311 (not_311_out, OP0);
  not not_312 (not_312_out, F4);
  not not_313 (not_313_out, F3);
  not not_314 (not_314_out, OP5);
  not not_315 (not_315_out, OP4);
  not not_316 (not_316_out, OP3);
  not not_317 (not_317_out, OP2);
  not not_318 (not_318_out, OP1);
  not not_319 (not_319_out, OP0);
  not not_320 (not_320_out, F4);
  not not_321 (not_321_out, F2);
  not not_322 (not_322_out, F0);
  not not_323 (not_323_out, OP5);
  not not_324 (not_324_out, OP4);
  not not_325 (not_325_out, OP3);
  not not_326 (not_326_out, OP2);
  not not_327 (not_327_out, OP1);
  not not_328 (not_328_out, OP0);
  not not_329 (not_329_out, F4);
  not not_330 (not_330_out, F2);
  not not_331 (not_331_out, OP5);
  not not_332 (not_332_out, OP4);
  not not_333 (not_333_out, OP3);
  not not_334 (not_334_out, OP2);
  not not_335 (not_335_out, OP1);
  not not_336 (not_336_out, OP0);
  not not_337 (not_337_out, F4);
  not not_338 (not_338_out, F3);
  not not_339 (not_339_out, F0);
  not not_340 (not_340_out, OP5);
  not not_341 (not_341_out, OP4);
  not not_342 (not_342_out, OP3);
  not not_343 (not_343_out, OP2);
  not not_344 (not_344_out, OP1);
  not not_345 (not_345_out, OP0);
  not not_346 (not_346_out, F5);
  not not_347 (not_347_out, F4);
  not not_348 (not_348_out, F3);
  not not_349 (not_349_out, F1);
  not not_350 (not_350_out, F0);
  not not_351 (not_351_out, OP5);
  not not_352 (not_352_out, OP4);
  not not_353 (not_353_out, OP3);
  not not_354 (not_354_out, OP1);
  not not_355 (not_355_out, OP0);
  not not_356 (not_356_out, OP5);
  not not_357 (not_357_out, OP4);
  not not_358 (not_358_out, OP3);
  not not_359 (not_359_out, OP1);
  not not_360 (not_360_out, OP5);
  not not_361 (not_361_out, OP4);
  not not_362 (not_362_out, OP3);
  not not_363 (not_363_out, OP2);
  not not_364 (not_364_out, OP1);
  not not_365 (not_365_out, OP0);
  not not_366 (not_366_out, F5);
  not not_367 (not_367_out, F4);
  not not_368 (not_368_out, F2);
  not not_369 (not_369_out, F1);
  not not_370 (not_370_out, F0);
  not not_371 (not_371_out, OP5);
  not not_372 (not_372_out, OP4);
  not not_373 (not_373_out, OP3);
  not not_374 (not_374_out, OP2);
  not not_375 (not_375_out, OP1);
  not not_376 (not_376_out, OP0);
  not not_377 (not_377_out, F5);
  not not_378 (not_378_out, F4);
  not not_379 (not_379_out, F2);
  not not_380 (not_380_out, F1);
  not not_381 (not_381_out, F0);
  not not_382 (not_382_out, OP5);
  not not_383 (not_383_out, OP4);
  not not_384 (not_384_out, OP3);
  not not_385 (not_385_out, OP2);
  not not_386 (not_386_out, OP0);
  not not_387 (not_387_out, OP5);
  not not_388 (not_388_out, OP4);
  not not_389 (not_389_out, OP3);
  not not_390 (not_390_out, OP2);
  not not_391 (not_391_out, OP5);
  not not_392 (not_392_out, OP4);
  not not_393 (not_393_out, OP3);
  not not_394 (not_394_out, OP2);
  not not_395 (not_395_out, OP5);
  not not_396 (not_396_out, OP4);
  not not_397 (not_397_out, OP3);
  not not_398 (not_398_out, OP5);
  not not_399 (not_399_out, OP4);
  not not_400 (not_400_out, OP3);
  not not_401 (not_401_out, OP2);
  not not_402 (not_402_out, OP1);
  not not_403 (not_403_out, OP0);
  not not_404 (not_404_out, F4);
  not not_405 (not_405_out, F3);
  not not_406 (not_406_out, F2);
  not not_407 (not_407_out, F1);
  not not_408 (not_408_out, F0);
  not not_409 (not_409_out, OP5);
  not not_410 (not_410_out, OP4);
  not not_411 (not_411_out, OP3);
  not not_412 (not_412_out, OP2);
  not not_413 (not_413_out, OP1);
  not not_414 (not_414_out, OP0);
  not not_415 (not_415_out, F4);
  not not_416 (not_416_out, F3);
  not not_417 (not_417_out, F2);
  not not_418 (not_418_out, F1);
  not not_419 (not_419_out, OP5);
  not not_420 (not_420_out, OP4);
  not not_421 (not_421_out, OP3);
  not not_422 (not_422_out, OP2);
  not not_423 (not_423_out, OP1);
  not not_424 (not_424_out, OP0);
  not not_425 (not_425_out, F4);
  not not_426 (not_426_out, F3);
  not not_427 (not_427_out, F2);
  not not_428 (not_428_out, F0);
  not not_429 (not_429_out, OP5);
  not not_430 (not_430_out, OP4);
  not not_431 (not_431_out, OP3);
  not not_432 (not_432_out, OP2);
  not not_433 (not_433_out, OP1);
  not not_434 (not_434_out, OP0);
  not not_435 (not_435_out, F4);
  not not_436 (not_436_out, F3);
  not not_437 (not_437_out, F1);
  not not_438 (not_438_out, F0);
  not not_439 (not_439_out, OP5);
  not not_440 (not_440_out, OP4);
  not not_441 (not_441_out, OP3);
  not not_442 (not_442_out, OP2);
  not not_443 (not_443_out, OP1);
  not not_444 (not_444_out, OP0);
  not not_445 (not_445_out, F4);
  not not_446 (not_446_out, F3);
  not not_447 (not_447_out, F1);
  not not_448 (not_448_out, OP5);
  not not_449 (not_449_out, OP4);
  not not_450 (not_450_out, OP3);
  not not_451 (not_451_out, OP2);
  not not_452 (not_452_out, OP1);
  not not_453 (not_453_out, OP0);
  not not_454 (not_454_out, F4);
  not not_455 (not_455_out, F3);
  not not_456 (not_456_out, OP5);
  not not_457 (not_457_out, OP4);
  not not_458 (not_458_out, OP3);
  not not_459 (not_459_out, OP2);
  not not_460 (not_460_out, OP1);
  not not_461 (not_461_out, OP0);
  not not_462 (not_462_out, F4);
  not not_463 (not_463_out, F2);
  not not_464 (not_464_out, F0);
  not not_465 (not_465_out, OP5);
  not not_466 (not_466_out, OP4);
  not not_467 (not_467_out, OP3);
  not not_468 (not_468_out, OP2);
  not not_469 (not_469_out, OP1);
  not not_470 (not_470_out, OP0);
  not not_471 (not_471_out, F4);
  not not_472 (not_472_out, F2);
  not not_473 (not_473_out, OP5);
  not not_474 (not_474_out, OP4);
  not not_475 (not_475_out, OP3);
  not not_476 (not_476_out, OP2);
  not not_477 (not_477_out, OP1);
  not not_478 (not_478_out, OP0);
  not not_479 (not_479_out, F5);
  not not_480 (not_480_out, F4);
  not not_481 (not_481_out, F1);
  not not_482 (not_482_out, F0);
  not not_483 (not_483_out, OP5);
  not not_484 (not_484_out, OP4);
  not not_485 (not_485_out, OP3);
  not not_486 (not_486_out, OP1);
  not not_487 (not_487_out, OP0);
  not not_488 (not_488_out, OP5);
  not not_489 (not_489_out, OP4);
  not not_490 (not_490_out, OP3);
  not not_491 (not_491_out, OP1);
  not not_492 (not_492_out, OP4);
  not not_493 (not_493_out, OP2);
  not not_494 (not_494_out, OP5);
  not not_495 (not_495_out, OP4);
  not not_496 (not_496_out, OP3);
  not not_497 (not_497_out, OP2);
  not not_498 (not_498_out, OP1);
  not not_499 (not_499_out, OP0);
  not not_500 (not_500_out, F4);
  not not_501 (not_501_out, F3);
  not not_502 (not_502_out, F0);
  not not_503 (not_503_out, OP5);
  not not_504 (not_504_out, OP4);
  not not_505 (not_505_out, OP3);
  not not_506 (not_506_out, OP2);
  not not_507 (not_507_out, OP1);
  not not_508 (not_508_out, OP0);
  not not_509 (not_509_out, F5);
  not not_510 (not_510_out, F4);
  not not_511 (not_511_out, F3);
  not not_512 (not_512_out, F1);
  not not_513 (not_513_out, F0);
  not not_514 (not_514_out, OP4);
  not not_515 (not_515_out, OP2);
  not not_516 (not_516_out, OP1);
  not not_517 (not_517_out, OP5);
  not not_518 (not_518_out, OP4);
  not not_519 (not_519_out, OP3);
  not not_520 (not_520_out, OP2);
  not not_521 (not_521_out, OP1);
  not not_522 (not_522_out, OP0);
  not not_523 (not_523_out, F5);
  not not_524 (not_524_out, F4);
  not not_525 (not_525_out, F2);
  not not_526 (not_526_out, F1);
  not not_527 (not_527_out, F0);
  not not_528 (not_528_out, OP5);
  not not_529 (not_529_out, OP4);
  not not_530 (not_530_out, OP2);
  not not_531 (not_531_out, OP1);
  not not_532 (not_532_out, OP0);
  not not_533 (not_533_out, OP5);
  not not_534 (not_534_out, OP4);
  not not_535 (not_535_out, OP1);
  not not_536 (not_536_out, OP0);
  not not_537 (not_537_out, OP5);
  not not_538 (not_538_out, OP4);
  not not_539 (not_539_out, OP2);
  not not_540 (not_540_out, OP1);
  not not_541 (not_541_out, OP5);
  not not_542 (not_542_out, OP4);
  not not_543 (not_543_out, OP2);
  not not_544 (not_544_out, OP0);
  not not_545 (not_545_out, OP5);
  not not_546 (not_546_out, OP4);
  not not_547 (not_547_out, OP1);
  not not_548 (not_548_out, OP4);
  not not_549 (not_549_out, OP3);
  not not_550 (not_550_out, OP2);
  not not_551 (not_551_out, OP5);
  not not_552 (not_552_out, OP4);
  not not_553 (not_553_out, OP3);
  not not_554 (not_554_out, OP5);
  not not_555 (not_555_out, OP4);
  not not_556 (not_556_out, OP3);
  not not_557 (not_557_out, OP2);
  not not_558 (not_558_out, OP1);
  not not_559 (not_559_out, OP0);
  not not_560 (not_560_out, F5);
  not not_561 (not_561_out, F4);
  not not_562 (not_562_out, F3);
  not not_563 (not_563_out, F2);
  not not_564 (not_564_out, F1);
  not not_565 (not_565_out, F0);
  not not_566 (not_566_out, OP5);
  not not_567 (not_567_out, OP4);
  not not_568 (not_568_out, OP3);
  not not_569 (not_569_out, OP2);
  not not_570 (not_570_out, OP1);
  not not_571 (not_571_out, OP0);
  not not_572 (not_572_out, F5);
  not not_573 (not_573_out, F4);
  not not_574 (not_574_out, F3);
  not not_575 (not_575_out, F2);
  not not_576 (not_576_out, OP5);
  not not_577 (not_577_out, OP4);
  not not_578 (not_578_out, OP3);
  not not_579 (not_579_out, OP2);
  not not_580 (not_580_out, OP1);
  not not_581 (not_581_out, OP0);
  not not_582 (not_582_out, F5);
  not not_583 (not_583_out, F4);
  not not_584 (not_584_out, F3);
  not not_585 (not_585_out, F2);
  not not_586 (not_586_out, F0);
  not not_587 (not_587_out, OP5);
  not not_588 (not_588_out, OP3);
  not not_589 (not_589_out, OP2);
  not not_590 (not_590_out, OP1);
  not not_591 (not_591_out, OP0);
  and and_1 (MemToReg, OP5, not_1_out, not_2_out, not_3_out, OP1, OP0);
  and and_2 (and_2_out, OP5, not_4_out, OP3, not_5_out, OP1, OP0);
  and and_3 (and_3_out, OP5, not_6_out, OP3, not_7_out, not_8_out, OP0);
  and and_4 (and_4_out, not_9_out, not_10_out, OP3, not_11_out, not_12_out, not_13_out);
  and and_5 (and_5_out, not_14_out, not_15_out, OP3, OP2, not_16_out, not_17_out);
  and and_6 (and_6_out, not_18_out, not_19_out, OP3, not_20_out, not_21_out, OP0);
  and and_7 (and_7_out, not_22_out, not_23_out, OP3, not_24_out, OP1, not_25_out);
  and and_8 (and_8_out, not_26_out, not_27_out, OP3, OP2, not_28_out, OP0);
  and and_9 (and_9_out, OP5, not_29_out, not_30_out, not_31_out, OP1, OP0);
  and and_10 (and_10_out, OP5, not_32_out, OP3, not_33_out, OP1, OP0);
  and and_11 (and_11_out, OP5, not_34_out, OP3, not_35_out, not_36_out, OP0);
  and and_12 (and_12_out, not_37_out, not_38_out, not_39_out, not_40_out, not_41_out, not_42_out, not_43_out, not_44_out, not_45_out, not_46_out, not_47_out, not_48_out);
  and and_13 (and_13_out, not_49_out, not_50_out, not_51_out, not_52_out, not_53_out, not_54_out, not_55_out, not_56_out, not_57_out, not_58_out, F1, F0);
  and and_14 (and_14_out, not_59_out, not_60_out, not_61_out, not_62_out, not_63_out, not_64_out, not_65_out, not_66_out, not_67_out, not_68_out, F1, not_69_out);
  and and_15 (and_15_out, not_70_out, not_71_out, not_72_out, not_73_out, not_74_out, not_75_out, F5, not_76_out, not_77_out, not_78_out, not_79_out, not_80_out);
  and and_16 (and_16_out, not_81_out, not_82_out, not_83_out, not_84_out, not_85_out, not_86_out, F5, not_87_out, not_88_out, not_89_out, not_90_out, F0);
  and and_17 (and_17_out, not_91_out, not_92_out, not_93_out, not_94_out, not_95_out, not_96_out, F5, not_97_out, not_98_out, not_99_out, F1, not_100_out);
  and and_18 (and_18_out, not_101_out, not_102_out, not_103_out, not_104_out, not_105_out, not_106_out, F5, not_107_out, not_108_out, F2, not_109_out, not_110_out);
  and and_19 (and_19_out, not_111_out, not_112_out, not_113_out, not_114_out, not_115_out, not_116_out, F5, not_117_out, not_118_out, F2, not_119_out, F0);
  and and_20 (and_20_out, not_120_out, not_121_out, not_122_out, not_123_out, not_124_out, not_125_out, F5, not_126_out, not_127_out, F2, F1, F0);
  and and_21 (and_21_out, not_128_out, not_129_out, not_130_out, not_131_out, not_132_out, not_133_out, F5, not_134_out, F3, not_135_out, F1, not_136_out);
  and and_22 (and_22_out, not_137_out, not_138_out, not_139_out, not_140_out, not_141_out, not_142_out, F5, not_143_out, F3, not_144_out, F1, F0);
  and and_23 (and_23_out, not_145_out, not_146_out, not_147_out, not_148_out, OP1, OP0);
  and and_24 (and_24_out, not_149_out, not_150_out, OP3, not_151_out, not_152_out, not_153_out);
  and and_25 (and_25_out, not_154_out, not_155_out, OP3, OP2, not_156_out, not_157_out);
  and and_26 (and_26_out, not_158_out, not_159_out, OP3, not_160_out, not_161_out, OP0);
  and and_27 (and_27_out, not_162_out, not_163_out, OP3, not_164_out, OP1, not_165_out);
  and and_28 (and_28_out, not_166_out, not_167_out, OP3, OP2, not_168_out, OP0);
  and and_29 (and_29_out, OP5, not_169_out, not_170_out, not_171_out, OP1, OP0);
  and and_30 (and_30_out, not_172_out, not_173_out, not_174_out, not_175_out, not_176_out, not_177_out, F5, not_178_out, not_179_out, F2, F1, not_180_out);
  and and_31 (and_31_out, not_181_out, not_182_out, not_183_out, not_184_out, not_185_out, not_186_out, not_187_out, not_188_out, not_189_out, F2, not_190_out, not_191_out);
  and and_32 (SysCALL, not_192_out, not_193_out, not_194_out, not_195_out, not_196_out, not_197_out, not_198_out, not_199_out, F3, F2, not_200_out, not_201_out);
  and and_33 (and_33_out, not_202_out, not_203_out, OP3, not_204_out, not_205_out, not_206_out);
  and and_34 (and_34_out, not_207_out, not_208_out, OP3, not_209_out, not_210_out, OP0);
  and and_35 (and_35_out, not_211_out, not_212_out, OP3, not_213_out, OP1, not_214_out);
  and and_36 (and_36_out, OP5, not_215_out, not_216_out, not_217_out, OP1, OP0);
  and and_37 (and_37_out, OP5, not_218_out, OP3, not_219_out, OP1, OP0);
  and and_38 (and_38_out, OP5, not_220_out, OP3, not_221_out, not_222_out, OP0);
  and and_39 (and_39_out, not_223_out, not_224_out, not_225_out, not_226_out, not_227_out, not_228_out, not_229_out, not_230_out, not_231_out, not_232_out, not_233_out, not_234_out);
  and and_40 (and_40_out, not_235_out, not_236_out, not_237_out, not_238_out, not_239_out, not_240_out, not_241_out, not_242_out, not_243_out, not_244_out, F1, F0);
  and and_41 (and_41_out, not_245_out, not_246_out, not_247_out, not_248_out, not_249_out, not_250_out, not_251_out, not_252_out, not_253_out, not_254_out, F1, not_255_out);
  and and_42 (and_42_out, not_256_out, not_257_out, not_258_out, not_259_out, not_260_out, not_261_out, F5, not_262_out, not_263_out, not_264_out, not_265_out, not_266_out);
  and and_43 (and_43_out, not_267_out, not_268_out, not_269_out, not_270_out, not_271_out, not_272_out, F5, not_273_out, not_274_out, not_275_out, not_276_out, F0);
  and and_44 (and_44_out, not_277_out, not_278_out, not_279_out, not_280_out, not_281_out, not_282_out, F5, not_283_out, not_284_out, not_285_out, F1, not_286_out);
  and and_45 (and_45_out, not_287_out, not_288_out, not_289_out, not_290_out, not_291_out, not_292_out, F5, not_293_out, not_294_out, F2, not_295_out, not_296_out);
  and and_46 (and_46_out, not_297_out, not_298_out, not_299_out, not_300_out, not_301_out, not_302_out, F5, not_303_out, not_304_out, F2, not_305_out, F0);
  and and_47 (and_47_out, not_306_out, not_307_out, not_308_out, not_309_out, not_310_out, not_311_out, F5, not_312_out, not_313_out, F2, F1, F0);
  and and_48 (and_48_out, not_314_out, not_315_out, not_316_out, not_317_out, not_318_out, not_319_out, F5, not_320_out, F3, not_321_out, F1, not_322_out);
  and and_49 (and_49_out, not_323_out, not_324_out, not_325_out, not_326_out, not_327_out, not_328_out, F5, not_329_out, F3, not_330_out, F1, F0);
  and and_50 (and_50_out, not_331_out, not_332_out, not_333_out, not_334_out, not_335_out, not_336_out, F5, not_337_out, not_338_out, F2, F1, not_339_out);
  and and_51 (and_51_out, not_340_out, not_341_out, not_342_out, not_343_out, not_344_out, not_345_out, not_346_out, not_347_out, not_348_out, F2, not_349_out, not_350_out);
  and and_52 (BEQ, not_351_out, not_352_out, not_353_out, OP2, not_354_out, not_355_out);
  and and_53 (BNE, not_356_out, not_357_out, not_358_out, OP2, not_359_out, OP0);
  and and_54 (JR, not_360_out, not_361_out, not_362_out, not_363_out, not_364_out, not_365_out, not_366_out, not_367_out, F3, not_368_out, not_369_out, not_370_out);
  and and_55 (and_55_out, not_371_out, not_372_out, not_373_out, not_374_out, not_375_out, not_376_out, not_377_out, not_378_out, F3, not_379_out, not_380_out, not_381_out);
  and and_56 (and_56_out, not_382_out, not_383_out, not_384_out, not_385_out, OP1, not_386_out);
  and and_57 (and_57_out, not_387_out, not_388_out, not_389_out, not_390_out, OP1, OP0);
  and and_58 (JAL, not_391_out, not_392_out, not_393_out, not_394_out, OP1, OP0);
  and and_59 (Bgtz, not_395_out, not_396_out, not_397_out, OP2, OP1, OP0);
  and and_60 (and_60_out, not_398_out, not_399_out, not_400_out, not_401_out, not_402_out, not_403_out, F5, not_404_out, not_405_out, not_406_out, not_407_out, not_408_out);
  and and_61 (and_61_out, not_409_out, not_410_out, not_411_out, not_412_out, not_413_out, not_414_out, F5, not_415_out, not_416_out, not_417_out, not_418_out, F0);
  and and_62 (and_62_out, not_419_out, not_420_out, not_421_out, not_422_out, not_423_out, not_424_out, F5, not_425_out, not_426_out, not_427_out, F1, not_428_out);
  and and_63 (and_63_out, not_429_out, not_430_out, not_431_out, not_432_out, not_433_out, not_434_out, F5, not_435_out, not_436_out, F2, not_437_out, not_438_out);
  and and_64 (and_64_out, not_439_out, not_440_out, not_441_out, not_442_out, not_443_out, not_444_out, F5, not_445_out, not_446_out, F2, not_447_out, F0);
  and and_65 (and_65_out, not_448_out, not_449_out, not_450_out, not_451_out, not_452_out, not_453_out, F5, not_454_out, not_455_out, F2, F1, F0);
  and and_66 (and_66_out, not_456_out, not_457_out, not_458_out, not_459_out, not_460_out, not_461_out, F5, not_462_out, F3, not_463_out, F1, not_464_out);
  and and_67 (and_67_out, not_465_out, not_466_out, not_467_out, not_468_out, not_469_out, not_470_out, F5, not_471_out, F3, not_472_out, F1, F0);
  and and_68 (and_68_out, not_473_out, not_474_out, not_475_out, not_476_out, not_477_out, not_478_out, not_479_out, not_480_out, F3, F2, not_481_out, not_482_out);
  and and_69 (and_69_out, not_483_out, not_484_out, not_485_out, OP2, not_486_out, not_487_out);
  and and_70 (and_70_out, not_488_out, not_489_out, not_490_out, OP2, not_491_out, OP0);
  and and_71 (and_71_out, OP5, not_492_out, OP3, not_493_out, OP1, OP0);
  and and_72 (and_72_out, not_494_out, not_495_out, not_496_out, not_497_out, not_498_out, not_499_out, F5, not_500_out, not_501_out, F2, F1, not_502_out);
  and and_73 (and_73_out, not_503_out, not_504_out, not_505_out, not_506_out, not_507_out, not_508_out, not_509_out, not_510_out, not_511_out, F2, not_512_out, not_513_out);
  and and_74 (and_74_out, OP5, not_514_out, OP3, not_515_out, not_516_out, OP0);
  and and_75 (and_75_out, not_517_out, not_518_out, not_519_out, not_520_out, not_521_out, not_522_out, not_523_out, not_524_out, F3, not_525_out, not_526_out, not_527_out);
  and and_76 (and_76_out, not_528_out, not_529_out, OP3, not_530_out, not_531_out, not_532_out);
  and and_77 (and_77_out, not_533_out, not_534_out, OP3, OP2, not_535_out, not_536_out);
  and and_78 (and_78_out, not_537_out, not_538_out, OP3, not_539_out, not_540_out, OP0);
  and and_79 (and_79_out, not_541_out, not_542_out, OP3, not_543_out, OP1, not_544_out);
  and and_80 (and_80_out, not_545_out, not_546_out, OP3, OP2, not_547_out, OP0);
  and and_81 (and_81_out, OP5, not_548_out, not_549_out, not_550_out, OP1, OP0);
  and and_82 (and_82_out, not_551_out, not_552_out, not_553_out, OP2, OP1, OP0);
  and and_83 (and_83_out, not_554_out, not_555_out, not_556_out, not_557_out, not_558_out, not_559_out, not_560_out, not_561_out, not_562_out, not_563_out, not_564_out, not_565_out);
  and and_84 (and_84_out, not_566_out, not_567_out, not_568_out, not_569_out, not_570_out, not_571_out, not_572_out, not_573_out, not_574_out, not_575_out, F1, F0);
  and and_85 (and_85_out, not_576_out, not_577_out, not_578_out, not_579_out, not_580_out, not_581_out, not_582_out, not_583_out, not_584_out, not_585_out, F1, not_586_out);
  and and_86 (RET, not_587_out, OP4, not_588_out, not_589_out, not_590_out, not_591_out);
  or or_1 (MemWrite, and_2_out, and_3_out);
  or or_2 (ALU_SRC, and_4_out, and_5_out, and_6_out, and_7_out, and_8_out, and_9_out, and_10_out, and_11_out);
  or or_3 (SignedExt, and_33_out, and_34_out, and_35_out, and_36_out, and_37_out, and_38_out);
  or or_4 (JUMP, and_55_out, and_56_out, and_57_out);
  or or_5 (INS2, and_75_out, and_76_out, and_77_out, and_78_out, and_79_out, and_80_out, and_81_out, and_82_out);
  or or_6 (INS3, and_83_out, and_84_out, and_85_out);
  or or_7 (RegWrite, and_12_out, and_13_out, and_14_out, and_15_out, and_16_out, and_17_out, and_18_out, and_19_out, and_20_out, and_21_out, and_22_out, and_23_out, and_24_out, and_25_out, and_26_out, and_27_out, and_28_out, and_29_out, and_30_out, and_31_out);
  or or_8 (RegDst, and_39_out, and_40_out, and_41_out, and_42_out, and_43_out, and_44_out, and_45_out, and_46_out, and_47_out, and_48_out, and_49_out, and_50_out, and_51_out);
  or or_9 (INS1, and_60_out, and_61_out, and_62_out, and_63_out, and_64_out, and_65_out, and_66_out, and_67_out, and_68_out, and_69_out, and_70_out, and_71_out, and_72_out, and_73_out, and_74_out);
endmodule

// ALU
module MIPS_ALU (
  input  [4:0] shamt,
  input  [31:0] X,
  input  [31:0] Y,
  input  [3:0] AluOP,
  output Equal,
  output [31:0] Result,
  output [31:0] Result_2
);

  wire [0:0] comparator_1_lt, comparator_2_lt;
  wire [31:0] adder_1_out, AND_out, divider_1_out, divider_1_rem, multiplier_1_cout, multiplier_1_out,
       NOR_out, OR_out, shifter_1_out, shifter_2_out, shifter_3_out, subtractor_1_out, XOR_out;

  assign AND_out = X & Y;  // AND_Gate AND, 32 bits wide
  assign OR_out = X | Y;  // OR_Gate OR, 32 bits wide
  Shifter #(.width(32)) shifter_1 (.in(Y), .\dist (shamt), .out(shifter_1_out));
  Shifter #(.width(32), .shift("ar")) shifter_2 (.in(Y), .\dist (shamt), .out(shifter_2_out));
  Shifter #(.width(32), .shift("lr")) shifter_3 (.in(Y), .\dist (shamt), .out(shifter_3_out));
  Multiplier #(.width(32)) multiplier_1 (.a(X), .b(Y), .out(multiplier_1_out), .cout(multiplier_1_cout));  // open: cin
  Divider #(.width(32)) divider_1 (.a(X), .b(Y), .out(divider_1_out), .rem(divider_1_rem));  // open: upper
  Adder #(.width(32)) adder_1 (.a(X), .b(Y), .out(adder_1_out));  // open: cin, cout
  Subtractor #(.width(32)) subtractor_1 (.a(X), .b(Y), .out(subtractor_1_out));  // open: bin, bout
  assign XOR_out = X ^ Y;  // XOR_Gate XOR, 32 bits wide
  assign NOR_out = ~(X | Y);  // NOR_Gate NOR, 32 bits wide
  Comparator #(.width(32)) comparator_1 (.a(X), .b(Y), .eq(Equal), .lt(comparator_1_lt[0]));  // open: gt
  Comparator #(.width(32), .mode("unsigned")) comparator_2 (.a(X), .b(Y), .lt(comparator_2_lt[0]));  // open: gt, eq
  Multiplexer #(.select(4), .width(32), .enable("false")) multiplexer_1 (
    .in0(shifter_1_out), .in1(shifter_2_out), .in2(shifter_3_out), .in3(multiplier_1_out),
    .in4(divider_1_out), .in5(adder_1_out), .in6(subtractor_1_out), .in7(AND_out), .in8(OR_out),
    .in9(XOR_out), .in10(NOR_out), .in11({{31{1'b0}}, comparator_1_lt[0]}),
    .in12({{31{1'b0}}, comparator_2_lt[0]}), .in13({32{1'b0}}), .in14({32{1'b0}}), .in15({32{1'b0}}),
    .out(Result), .sel(AluOP));
  Multiplexer #(.select(4), .width(32), .enable("false")) multiplexer_2 (
    .in0({32{1'b0}}), .in1({32{1'b0}}), .in2({32{1'b0}}), .in3(multiplier_1_cout), .in4(divider_1_rem),
    .in5({32{1'b0}}), .in6({32{1'b0}}), .in7({32{1'b0}}), .in8({32{1'b0}}), .in9({32{1'b0}}),
    .in10({32{1'b0}}), .in11({32{1'b0}}), .in12({32{1'b0}}), .in13({32{1'b0}}), .in14({32{1'b0}}),
    .in15({32{1'b0}}), .out(Result_2), .sel(AluOP));

  // Other names for the same wires on the sheet: Result2[31:0] = Result_2; S[3:0] = AluOP

  // Notes on the sheet:
  //   不要改变此引脚区域内容，也不要改变ALU封装形式
  //   输入引脚
  //   输出引脚
endmodule

module MIPS_Regifile (
  input  [31:0] Din,
  input  Clk,
  input  WE,
  input  [4:0] R1_num,
  input  [4:0] W_num,
  input  [4:0] R2_num,
  output [31:0] R1,
  output [31:0] R2
);

  // RegisterFile registerfile_1: pin names not known; wires that end beside it: Din, Clk, WE, W_num, R1_num, R2_num, R1, R2
endmodule

module \理想流水线  (
  output RegWrite,
  output MemWrite,
  output [31:0] IF_PC,
  output [31:0] ID_PC,
  output [31:0] EX_PC,
  output [31:0] M_PC,
  output [31:0] WB_PC,
  output [31:0] RDin,
  output [31:0] MDin,
  output [31:0] LedData
);

  wire AluSrcB, and_1_out, and_2_out, Beq, Bgtz, Bne, Branch, CLK, comparator_1_eq, comparator_2_eq, Go,
       Halt, IR1, IR2, IR3, jal, jmp, jr, MemToReg, mips_alu_1_equal, not_1_out, RegDst, RST, syscall, W1,
       W2, W3;
  wire [3:0] \单周期硬布线控制器_1_alu_op ;
  wire [4:0] ex_mem_1_rdo, ex_mem_1_rto, id_ex_1_rdo, id_ex_1_rto, id_ex_1_shammto, multiplexer_5_out,
       multiplexer_6_out, multiplexer_7_out, multiplexer_8_out, rd5, rt5;
  wire [15:0] \LoadUse次数 , \总周期数 , \插入气泡数 , \无条件分支数 , \条件分支成功数 ;
  wire [16:0] ex_mem_1_controlo, mem_wb_1_controlo, \单周期硬布线控制器_1_jr ;
  wire [16:5] id_ex_1_controlo;
  wire [31:0] EX_IR, ex_mem_1_aluo, ex_mem_1_pco, id_ex_1_pco, id_ex_1_reg1o, id_ex_1_reg2o, ID_IR,
       if_id_1_pc_4o, IF_IR, imm, Imm32, MEM_IR, mem_wb_1_aluo, mem_wb_1_dmouto, mem_wb_1_pco,
       mips_alu_1_result, multiplexer_1_out, multiplexer_2_out, multiplexer_3_out, multiplexer_10_out,
       multiplexer_11_out, PC_4, pcout_1_out_10, ram_1_data, Reg1, Reg2, WB_IR;

  Button \u_总复位  (.out(RST));
  Button _1 (.out(IR1));
  Button _2 (.out(IR2));
  Button _3 (.out(IR3));
  // Probe on \总周期数 
  // Probe on \总周期数 
  Button \u_继续运行  (.out(Go));
  LED led_1 (.in(W1));
  LED led_2 (.in(W2));
  LED led_3 (.in(W3));
  PCout pcout_1 (
    .PC_4(PC_4), .Imm26(ID_IR[25:0]), .Imm32(Imm32), .Reg1(Reg1), .JMP(jmp), .JR(jr), .JAL(jal),
    .Branch(Branch), .out_10(pcout_1_out_10));  // open: PC_4_3
  Hex_Digit_Display hex_digit_display_1 (.value(LedData[31:28]));  // open: dp
  // Probe on IF_PC[19:0]
  // Mips_Probe mips_probe_1: pin names not known; wires that end beside it: IF_IR
  not not_1 (not_1_out, Halt);
  Multiplexer #(.width(32), .enable("false")) multiplexer_1 (
    .in0({32{1'b0}}), .in1(Reg1), .out(multiplexer_1_out), .sel(syscall));
  Multiplexer #(.width(32), .enable("false")) multiplexer_2 (
    .in0({32{1'b0}}), .in1(Reg1), .out(multiplexer_2_out), .sel(syscall));
  Hex_Digit_Display hex_digit_display_2 (.value(LedData[23:20]));  // open: dp
  Hex_Digit_Display hex_digit_display_3 (.value(LedData[27:24]));  // open: dp
  // Probe on ID_PC[19:0]
  // Mips_Probe mips_probe_2: pin names not known; wires that end beside it: ID_IR
  Register #(.width(32)) PC (.D(pcout_1_out_10), .en(not_1_out), .Q(IF_PC), .clk(CLK), .clr(RST));
  Comparator #(.width(32), .mode("unsigned")) comparator_1 (
    .a(multiplexer_1_out), .b(32'h22), .eq(comparator_1_eq));  // open: gt, lt
  Multiplexer #(.width(32), .enable("false")) multiplexer_3 (
    .in0({32{1'b0}}), .in1(Reg2), .out(multiplexer_3_out), .sel(comparator_1_eq));
  Comparator #(.width(32), .mode("unsigned")) comparator_2 (
    .a(multiplexer_2_out), .b(32'ha), .eq(comparator_2_eq));  // open: gt, lt
  Hex_Digit_Display hex_digit_display_4 (.value(LedData[19:16]));  // open: dp
  Hex_Digit_Display hex_digit_display_5 (.value(LedData[15:12]));  // open: dp
  Register #(.width(32)) register_1 (.D(multiplexer_3_out), .en(comparator_1_eq), .Q(LedData), .clk(CLK));  // open: clr
  Multiplexer #(.enable("false")) multiplexer_4 (.in0(1'b0), .in1(1'b1), .out(Halt), .sel(comparator_2_eq));
  Hex_Digit_Display hex_digit_display_6 (.value(LedData[11:8]));  // open: dp
  Hex_Digit_Display hex_digit_display_7 (.value(LedData[7:4]));  // open: dp
  Clock clock_1 (.out(CLK));
  // Probe on EX_PC[19:0]
  // Mips_Probe mips_probe_3: pin names not known; wires that end beside it: EX_IR
  Adder #(.width(32)) adder_1 (.a(IF_PC), .b(32'h4), .out(PC_4));  // open: cin, cout
  Hex_Digit_Display hex_digit_display_8 (.value(LedData[3:0]));  // open: dp
  ROM #(.addrWidth(10), .dataWidth(32)) rom_1 (.addr(IF_PC[11:2]), .data(IF_IR));  // open: sel
  // Probe on \总周期数 
  // Probe on M_PC[19:0]
  // Mips_Probe mips_probe_4: pin names not known; wires that end beside it: MEM_IR
  IF_ID if_id_1 (
    .CLK(CLK), .RST(RST), .Halt(Halt), .PC_4(PC_4), .IR(IF_IR), .PC_4O(if_id_1_pc_4o), .IRO(ID_IR),
    .IF_PC(IF_PC), .IF_PCO(ID_PC));  // open: jump_att, hit, pc_att, hit_pos, pc_attO, hit_posO, jump_attO, hitO, PC, PCO
  // Probe on \总周期数 
  // Probe on \无条件分支数 
  // Probe on \条件分支成功数 
  // Probe on \插入气泡数 
  // Probe on \LoadUse次数 
  counter counter_1 (
    .rst(RST), .clk(CLK), .jmp(jmp), .jr(jr), .branch(Branch), .halt(Halt), .\总周期数 (\总周期数 ),
    .\条件分支成功数 (\条件分支成功数 ), .\无条件分支数 (\无条件分支数 ));  // open: pop, 气泡数
  // Probe on IF_PC[11:0]
  // Probe on WB_PC[19:0]
  // Mips_Probe mips_probe_5: pin names not known; wires that end beside it: WB_IR
  \单周期硬布线控制器  \u_单周期硬布线控制器_1  (
    .Func(ID_IR[5:0]), .OP(ID_IR[31:26]), .ALU_OP(\单周期硬布线控制器_1_alu_op ), .MemToReg(\单周期硬布线控制器_1_jr [5]),
    .MemWrite(\单周期硬布线控制器_1_jr [6]), .ALU_SRC(\单周期硬布线控制器_1_jr [11]), .RegWrite(\单周期硬布线控制器_1_jr [12]),
    .SysCALL(\单周期硬布线控制器_1_jr [15]), .SignedExt(\单周期硬布线控制器_1_jr [16]), .RegDst(\单周期硬布线控制器_1_jr [14]),
    .JR(\单周期硬布线控制器_1_jr [0]), .JMP(\单周期硬布线控制器_1_jr [1]), .Beq(\单周期硬布线控制器_1_jr [2]),
    .JAL(\单周期硬布线控制器_1_jr [13]), .Bne(\单周期硬布线控制器_1_jr [4]), .Bgtz(\单周期硬布线控制器_1_jr [3]));  // open: INS1, INS2, INS3, RET
  Multiplexer #(.width(5), .enable("false")) multiplexer_5 (
    .in0(ID_IR[25:21]), .in1(5'b00010), .out(multiplexer_5_out), .sel(syscall));
  Multiplexer #(.width(5), .enable("false")) multiplexer_6 (
    .in0(ID_IR[20:16]), .in1(5'b00100), .out(multiplexer_6_out), .sel(syscall));
  Multiplexer #(.width(5), .enable("false")) multiplexer_7 (
    .in0(rt5), .in1(rd5), .out(multiplexer_7_out), .sel(RegDst));
  assign Imm32 = {{16{ID_IR[15]}}, ID_IR[15:0]};  // Bit_Extender bit_extender_1
  // Probe on EX_PC[11:0]
  // Probe on ID_PC[11:0]
  Multiplexer #(.width(5), .enable("false")) multiplexer_8 (
    .in0(multiplexer_7_out), .in1({5{1'b1}}), .out(multiplexer_8_out), .sel(jal));
  Multiplexer #(.width(32), .enable("false")) multiplexer_9 (
    .in0(multiplexer_10_out), .in1(mem_wb_1_pco), .out(RDin), .sel(jal));
  Multiplexer #(.width(32), .enable("false")) multiplexer_10 (
    .in0(mem_wb_1_aluo), .in1(mem_wb_1_dmouto), .out(multiplexer_10_out), .sel(MemToReg));
  // Probe on M_PC[11:0]
  // Probe on WB_PC[11:0]
  ID_EX id_ex_1 (
    .CLK(CLK), .rd(ID_IR[15:11]), .rt(ID_IR[20:16]), .reg1(Reg1), .reg2(Reg2), .Imm(Imm32),
    .PC_4(if_id_1_pc_4o), .Control({\单周期硬布线控制器_1_jr [16:11], \单周期硬布线控制器_1_alu_op , \单周期硬布线控制器_1_jr [6:0]}),
    .RST(RST), .Halt(Halt), .Shammt(ID_IR[10:6]), .rdO(id_ex_1_rdo), .rtO(id_ex_1_rto),
    .ControlO({id_ex_1_controlo[16:12], AluSrcB, id_ex_1_controlo[10:5], Bne, Bgtz, Beq, jmp, jr}),
    .PCO(id_ex_1_pco), .reg1O(id_ex_1_reg1o), .reg2O(id_ex_1_reg2o), .ImmO(imm), .ShammtO(id_ex_1_shammto),
    .IR(ID_IR), .IR_2(EX_IR), .IR_PC(ID_PC), .IR_PCO(EX_PC));  // open: imm26, ra2, rt2, load_2, INS1_2, INS1_3, INS1_4, imm26O, ra2O, rd2O, loadO, INS3_O, INS2_O, INS1_O, jump_att, hit, pc_att, hit_pos, pc_attO, hit_posO, jump_attO, hitO, PCO_2, PC
  MIPS_Regifile mips_regifile_1 (
    .Din(RDin), .Clk(CLK), .R1(Reg1), .R2(Reg2), .WE(RegWrite), .W_num(multiplexer_8_out),
    .R1_num(multiplexer_5_out), .R2_num(multiplexer_6_out));
  Multiplexer #(.width(32), .enable("false")) multiplexer_11 (
    .in0(id_ex_1_reg2o), .in1(imm), .out(multiplexer_11_out), .sel(AluSrcB));
  MIPS_ALU mips_alu_1 (
    .X(id_ex_1_reg1o), .Y(multiplexer_11_out), .AluOP(id_ex_1_controlo[10:7]), .Equal(mips_alu_1_equal),
    .Result(mips_alu_1_result), .shamt(id_ex_1_shammto));  // open: Result_2
  and and_1 (and_1_out, Beq, mips_alu_1_equal);
  or or_1 (Branch, and_1_out, and_2_out);
  and and_2 (and_2_out, Bne, ~mips_alu_1_equal);  // AND_Gate
  EX_MEM ex_mem_1 (
    .CLK(CLK), .RST(RST), .Halt(Halt),
    .Control({id_ex_1_controlo[16:12], AluSrcB, id_ex_1_controlo[10:5], Bne, Bgtz, Beq, jmp, jr}),
    .PC(id_ex_1_pco), .reg2(id_ex_1_reg2o), .Alu(mips_alu_1_result), .rd(id_ex_1_rdo), .rt(id_ex_1_rto),
    .rdO(ex_mem_1_rdo), .rtO(ex_mem_1_rto),
    .ControlO({ex_mem_1_controlo[16:7], MemWrite, ex_mem_1_controlo[5:0]}), .PCO(ex_mem_1_pco), .reg2O(MDin),
    .AluO(ex_mem_1_aluo), .IR(EX_IR), .IR_2(MEM_IR), .EX_PC(EX_PC), .EX_PCO(M_PC));  // open: Reg1_3, Reg1_O, Reg2_3, Reg2_O
  RAM #(.addrWidth(10), .dataWidth(32), .bus("separate")) ram_1 (
    .addr(ex_mem_1_aluo[11:2]), .din(MDin), .data(ram_1_data), .str(MemWrite), .clk(CLK), .clr(RST));  // open: sel, ld
  MEM_WB mem_wb_1 (
    .CLK(CLK), .RST(RST), .Halt(Halt), .Control({ex_mem_1_controlo[16:7], MemWrite, ex_mem_1_controlo[5:0]}),
    .Alu(ex_mem_1_aluo), .PC(ex_mem_1_pco), .DMout(ram_1_data), .rd(ex_mem_1_rdo), .rt(ex_mem_1_rto),
    .rdO(rd5), .rtO(rt5),
    .ControlO({mem_wb_1_controlo[16], syscall, RegDst, jal, RegWrite, mem_wb_1_controlo[11:6], MemToReg, mem_wb_1_controlo[4:0]}),
    .PCO(mem_wb_1_pco), .DMoutO(mem_wb_1_dmouto), .AluO(mem_wb_1_aluo), .IR_2(WB_IR), .IR(MEM_IR),
    .MEM_PC(M_PC), .MEM_PCO(WB_PC));  // open: Reg1_3, Reg2_3, Reg1_O, Reg2_O

  // Other names for the same wires on the sheet: Imm26[25:0] = ID_IR[25:0]; rd[4:0] = ID_IR[15:11];
  //   rt[4:0] = ID_IR[20:16]; MEM_PC[31:0] = M_PC

  // Notes on the sheet:
  //   中断源
  //   时空图监测，可删除
  //   中断等待指示
  //   数码管输出
  //   指令存储器
  //   指令字
  //   contents of rom_1 (hex, n*v repeats v):
  //   20100000 20110000 20120000 20130000 36100000 36310001 36520002 36730003 ae100000 ae110004 ae120008
  //   ae13000c 2002000a 20110000 20120000 20130000 c
  //   JMP
  //   JR
  //   OP
  //   Func
  //   rs
  //   rt
  //   rd
  //   shmat
  //   Imm
  //   Beq
  //   Bgtz
  //   Bne
  //   MemToReg
  //   MemWrite
  //   AluOP
  //   AluSrcB
  //   RegWrite
  //   JAL
  //   RegDst
  //   Syscall
  //   流水调试日志用
  //   EX执行
  //   EX/MEM
  //   为方便自动评测，需要输出流水线各段保存的PC值，注意是PC不是PC+4，另外ID段寄存器写入信息，Mem段内存写入信息也要输出
  //   MEM/WB
endmodule

module \气泡流水线  (
  output RegWrite,
  output MemWrite,
  output [31:0] IF_PC,
  output [31:0] ID_PC,
  output [31:0] EX_PC,
  output [31:0] M_PC,
  output [31:0] WB_PC,
  output [31:0] RDin,
  output [31:0] MDin,
  output [31:0] LedData
);

  wire AluSrcB_3, and_1_out, and_2_out, and_3_out, Beq_3, Beq_4, Bgtz_3, Bgtz_4, Bne_3, Bne_4, Branch, CLK,
       comparator_1_eq, comparator_2_eq, comparator_3_gt, equal, Go, Halt, INS1, INS2, INS3, IR1, IR2, IR3,
       j_rst, jal_3, jal_5, jmp_3, jmp_4, jr_3, jr_4, MemToReg_5, not_1_out, or_1_out, or_2_out, or_3_out,
       or_4_out, or_6_out, pop, RegDst_3, RegDst_4, RegDst_5, RegWrite_3, RegWrite_4, RST, syscall_2,
       syscall_3, syscall_5, W1, W2, W3;
  wire [3:0] AluOp_3, \单周期硬布线控制器_1_alu_op ;
  wire [4:0] id_ex_1_shammto, multiplexer_7_out, multiplexer_8_out, ra2, rb2, rd3, rd4, rd5, rt3, rt4, rt5,
       rw_3, rw_4;
  wire [15:0] \LoadUse次数 , \总周期数 , \插入气泡数 , \无条件分支数 , \条件分支成功数 ;
  wire [16:0] mem_wb_1_controlo, \单周期硬布线控制器_1_jr ;
  wire [16:5] ex_mem_1_controlo, id_ex_1_controlo;
  wire [25:0] Imm26_3;
  wire [31:0] EX_IR, ex_mem_1_aluo, ex_mem_1_pco, ID_IR, if_id_1_pc_4o, IF_IR, imm, Imm32, MEM_IR,
       mem_wb_1_aluo, mem_wb_1_dmouto, mem_wb_1_pco, mips_alu_1_result, multiplexer_1_out, multiplexer_2_out,
       multiplexer_3_out, multiplexer_9_out, multiplexer_11_out, PC_4, PC_4_3, pcout_1_out_10, ram_1_data,
       Reg1, Reg1_3, Reg1_4, Reg1_5, Reg2, Reg2_3, Reg2_4, Reg2_5, WB_IR;

  Button \u_总复位  (.out(RST));
  Button _1 (.out(IR1));
  Button _2 (.out(IR2));
  Button _3 (.out(IR3));
  // Probe on \总周期数 
  // Probe on \总周期数 
  Button \u_继续运行  (.out(Go));
  LED led_1 (.in(W1));
  LED led_2 (.in(W2));
  LED led_3 (.in(W3));
  Hex_Digit_Display hex_digit_display_1 (.value(LedData[31:28]));  // open: dp
  // Probe on IF_PC[19:0]
  // Mips_Probe mips_probe_1: pin names not known; wires that end beside it: IF_IR
  PCout pcout_1 (
    .PC_4(PC_4), .Imm26(Imm26_3), .Imm32(imm), .Reg1(Reg1_3), .JMP(jmp_3), .JR(jr_3), .JAL(jal_5),
    .Branch(Branch), .PC_4_3(PC_4_3), .out_10(pcout_1_out_10));
  Hex_Digit_Display hex_digit_display_2 (.value(LedData[23:20]));  // open: dp
  Hex_Digit_Display hex_digit_display_3 (.value(LedData[27:24]));  // open: dp
  // Probe on ID_PC[19:0]
  // Mips_Probe mips_probe_2: pin names not known; wires that end beside it: ID_IR
  not not_1 (not_1_out, or_1_out);
  or or_1 (or_1_out, Halt, pop);
  Multiplexer #(.width(32), .enable("false")) multiplexer_1 (
    .in0({32{1'b0}}), .in1(Reg1_3), .out(multiplexer_1_out), .sel(syscall_3));
  Multiplexer #(.width(32), .enable("false")) multiplexer_2 (
    .in0({32{1'b0}}), .in1(Reg1_5), .out(multiplexer_2_out), .sel(syscall_5));
  Hex_Digit_Display hex_digit_display_4 (.value(LedData[15:12]));  // open: dp
  Hex_Digit_Display hex_digit_display_5 (.value(LedData[19:16]));  // open: dp
  Register #(.width(32)) PC (.D(pcout_1_out_10), .en(not_1_out), .Q(IF_PC), .clk(CLK), .clr(RST));
  Adder #(.width(32)) adder_1 (.a(IF_PC), .b(32'h4), .out(PC_4));  // open: cin, cout
  Comparator #(.width(32), .mode("unsigned")) comparator_1 (
    .a(multiplexer_1_out), .b(32'h22), .eq(comparator_1_eq));  // open: gt, lt
  Comparator #(.width(32), .mode("unsigned")) comparator_2 (
    .a(multiplexer_2_out), .b(32'ha), .eq(comparator_2_eq));  // open: gt, lt
  Hex_Digit_Display hex_digit_display_6 (.value(LedData[7:4]));  // open: dp
  Hex_Digit_Display hex_digit_display_7 (.value(LedData[11:8]));  // open: dp
  Clock clock_1 (.out(CLK));
  // Probe on EX_PC[19:0]
  // Mips_Probe mips_probe_3: pin names not known; wires that end beside it: EX_IR
  Register #(.width(32)) register_1 (.D(multiplexer_3_out), .en(comparator_1_eq), .Q(LedData), .clk(CLK), .clr(RST));
  Multiplexer #(.width(32), .enable("false")) multiplexer_3 (
    .in0({32{1'b0}}), .in1(Reg2_3), .out(multiplexer_3_out), .sel(comparator_1_eq));
  Multiplexer #(.enable("false")) multiplexer_4 (.in0(1'b0), .in1(1'b1), .out(Halt), .sel(comparator_2_eq));
  Hex_Digit_Display hex_digit_display_8 (.value(LedData[3:0]));  // open: dp
  ROM #(.addrWidth(10), .dataWidth(32)) rom_1 (.addr(IF_PC[11:2]), .data(IF_IR));  // open: sel
  // Probe on \总周期数 
  // Probe on M_PC[19:0]
  // Mips_Probe mips_probe_4: pin names not known; wires that end beside it: MEM_IR
  IF_ID if_id_1 (
    .CLK(CLK), .RST(or_2_out), .Halt(or_3_out), .PC_4(PC_4), .IR(IF_IR), .PC_4O(if_id_1_pc_4o), .IRO(ID_IR),
    .IF_PC(IF_PC), .IF_PCO(ID_PC));  // open: jump_att, hit, pc_att, hit_pos, pc_attO, hit_posO, jump_attO, hitO, PC, PCO
  or or_2 (or_2_out, j_rst, RST);
  or or_3 (or_3_out, Halt, pop);
  // Probe on \总周期数 
  // Probe on \无条件分支数 
  // Probe on \条件分支成功数 
  // Probe on \插入气泡数 
  // Probe on \LoadUse次数 
  // Probe on IF_PC[11:0]
  // Probe on WB_PC[19:0]
  // Mips_Probe mips_probe_5: pin names not known; wires that end beside it: WB_IR
  \单周期硬布线控制器  \u_单周期硬布线控制器_1  (
    .Func(ID_IR[5:0]), .OP(ID_IR[31:26]), .ALU_OP(\单周期硬布线控制器_1_alu_op ), .MemToReg(\单周期硬布线控制器_1_jr [5]),
    .MemWrite(\单周期硬布线控制器_1_jr [6]), .ALU_SRC(\单周期硬布线控制器_1_jr [11]), .RegWrite(\单周期硬布线控制器_1_jr [12]),
    .SysCALL(syscall_2), .SignedExt(\单周期硬布线控制器_1_jr [16]), .RegDst(\单周期硬布线控制器_1_jr [14]),
    .JR(\单周期硬布线控制器_1_jr [0]), .JMP(\单周期硬布线控制器_1_jr [1]), .Beq(\单周期硬布线控制器_1_jr [2]),
    .JAL(\单周期硬布线控制器_1_jr [13]), .Bne(\单周期硬布线控制器_1_jr [4]), .INS1(INS1), .INS2(INS2), .INS3(INS3),
    .Bgtz(\单周期硬布线控制器_1_jr [3]));  // open: RET
  \分支相关  \u_分支相关_1  (.j(jmp_3), .jr(jr_3), .jal(jal_3), .branch(Branch), .j_rst(j_rst));
  \数据相关  \u_数据相关_1  (
    .rw3(rw_3), .rw4(rw_4), .ra2(ra2), .rb2(rb2), .RegWrite3(RegWrite_3), .RegWrite4(RegWrite_4),
    .INS1(INS1), .INS2(INS2), .INS3(INS3), .pop(pop));
  // Probe on ID_PC[11:0]
  // Probe on EX_PC[11:0]
  Multiplexer #(.width(5), .enable("false")) multiplexer_5 (
    .in0(ID_IR[25:21]), .in1(5'b00010), .out(ra2), .sel(syscall_2));
  Multiplexer #(.width(5), .enable("false")) multiplexer_6 (
    .in0(ID_IR[20:16]), .in1(5'b00100), .out(rb2), .sel(syscall_2));
  Multiplexer #(.width(5), .enable("false")) multiplexer_7 (
    .in0(multiplexer_8_out), .in1({5{1'b1}}), .out(multiplexer_7_out), .sel(jal_5));
  Multiplexer #(.width(5), .enable("false")) multiplexer_8 (
    .in0(rt5), .in1(rd5), .out(multiplexer_8_out), .sel(RegDst_5));
  assign Imm32 = {{16{ID_IR[15]}}, ID_IR[15:0]};  // Bit_Extender bit_extender_1
  Multiplexer #(.width(32), .enable("false")) multiplexer_9 (
    .in0(mem_wb_1_aluo), .in1(mem_wb_1_dmouto), .out(multiplexer_9_out), .sel(MemToReg_5));
  // Probe on M_PC[11:0]
  Multiplexer #(.width(32), .enable("false")) multiplexer_10 (
    .in0(multiplexer_9_out), .in1(mem_wb_1_pco), .out(RDin), .sel(jal_5));
  // Probe on WB_PC[11:0]
  MIPS_Regifile mips_regifile_1 (
    .Din(RDin), .Clk(CLK), .R1(Reg1), .R2(Reg2), .WE(RegWrite), .W_num(multiplexer_7_out), .R1_num(ra2),
    .R2_num(rb2));
  ID_EX id_ex_1 (
    .CLK(CLK), .rd(ID_IR[15:11]), .rt(ID_IR[20:16]), .reg1(Reg1), .reg2(Reg2), .Imm(Imm32),
    .PC_4(if_id_1_pc_4o),
    .Control({\单周期硬布线控制器_1_jr [16], syscall_2, \单周期硬布线控制器_1_jr [14:11], \单周期硬布线控制器_1_alu_op , \单周期硬布线控制器_1_jr [6:0]}),
    .RST(or_4_out), .Halt(Halt), .Shammt(ID_IR[10:6]), .imm26(ID_IR[25:0]), .imm26O(Imm26_3), .rdO(rd3),
    .rtO(rt3),
    .ControlO({id_ex_1_controlo[16], syscall_3, RegDst_3, jal_3, RegWrite_3, AluSrcB_3, AluOp_3, id_ex_1_controlo[6:5], Bne_3, Bgtz_3, Beq_3, jmp_3, jr_3}),
    .PCO(PC_4_3), .reg1O(Reg1_3), .reg2O(Reg2_3), .ImmO(imm), .ShammtO(id_ex_1_shammto), .IR(ID_IR),
    .IR_2(EX_IR), .IR_PC(ID_PC), .IR_PCO(EX_PC));  // open: ra2, rt2, load_2, INS1_2, INS1_3, INS1_4, ra2O, rd2O, loadO, INS3_O, INS2_O, INS1_O, jump_att, hit, pc_att, hit_pos, pc_attO, hit_posO, jump_attO, hitO, PCO_2, PC
  or or_4 (or_4_out, j_rst, RST, pop);
  counter counter_1 (
    .rst(RST), .clk(CLK), .jmp(jmp_3), .jr(jr_3), .branch(Branch), .halt(Halt), .\总周期数 (\总周期数 ),
    .\条件分支成功数 (\条件分支成功数 ), .\无条件分支数 (\无条件分支数 ), .pop(pop), .\气泡数 (\插入气泡数 ));
  Multiplexer #(.width(32), .enable("false")) multiplexer_11 (
    .in0(Reg2_3), .in1(imm), .out(multiplexer_11_out), .sel(AluSrcB_3));
  Comparator #(.width(32)) comparator_3 (.a(Reg1_3), .b({32{1'b0}}), .gt(comparator_3_gt));  // open: eq, lt
  and and_1 (and_1_out, Beq_3, equal);
  and and_2 (and_2_out, Bne_3, ~equal);  // AND_Gate
  MIPS_ALU mips_alu_1 (
    .X(Reg1_3), .Y(multiplexer_11_out), .AluOP(AluOp_3), .Equal(equal), .Result(mips_alu_1_result),
    .shamt(id_ex_1_shammto));  // open: Result_2
  Multiplexer #(.width(5), .enable("false")) multiplexer_12 (.in0(rt3), .in1(rd3), .out(rw_3), .sel(RegDst_3));
  and and_3 (and_3_out, comparator_3_gt, Bgtz_3);
  or or_5 (Branch, and_3_out, or_6_out);
  or or_6 (or_6_out, and_1_out, and_2_out);
  EX_MEM ex_mem_1 (
    .CLK(CLK), .RST(RST), .Halt(Halt),
    .Control({id_ex_1_controlo[16], syscall_3, RegDst_3, jal_3, RegWrite_3, AluSrcB_3, AluOp_3, id_ex_1_controlo[6:5], Bne_3, Bgtz_3, Beq_3, jmp_3, jr_3}),
    .PC(PC_4_3), .reg2(Reg2_3), .Alu(mips_alu_1_result), .rd(rd3), .rt(rt3), .rdO(rd4), .rtO(rt4),
    .ControlO({ex_mem_1_controlo[16:15], RegDst_4, ex_mem_1_controlo[13], RegWrite_4, ex_mem_1_controlo[11:7], MemWrite, ex_mem_1_controlo[5], Bne_4, Bgtz_4, Beq_4, jmp_4, jr_4}),
    .PCO(ex_mem_1_pco), .reg2O(MDin), .AluO(ex_mem_1_aluo), .IR(EX_IR), .IR_2(MEM_IR), .Reg1_3(Reg1_3),
    .Reg1_O(Reg1_4), .Reg2_3(Reg2_3), .Reg2_O(Reg2_4), .EX_PC(EX_PC), .EX_PCO(M_PC));
  Multiplexer #(.width(5), .enable("false")) multiplexer_13 (.in0(rt4), .in1(rd4), .out(rw_4), .sel(RegDst_4));
  RAM #(.addrWidth(10), .dataWidth(32), .bus("separate")) ram_1 (
    .addr(ex_mem_1_aluo[11:2]), .din(MDin), .data(ram_1_data), .str(MemWrite), .clk(CLK), .clr(RST));  // open: sel, ld
  MEM_WB mem_wb_1 (
    .CLK(CLK), .RST(RST), .Halt(Halt),
    .Control({ex_mem_1_controlo[16:15], RegDst_4, ex_mem_1_controlo[13], RegWrite_4, ex_mem_1_controlo[11:7], MemWrite, ex_mem_1_controlo[5], Bne_4, Bgtz_4, Beq_4, jmp_4, jr_4}),
    .Alu(ex_mem_1_aluo), .PC(ex_mem_1_pco), .DMout(ram_1_data), .rd(rd4), .rt(rt4), .rdO(rd5), .rtO(rt5),
    .ControlO({mem_wb_1_controlo[16], syscall_5, RegDst_5, jal_5, RegWrite, mem_wb_1_controlo[11:6], MemToReg_5, mem_wb_1_controlo[4:0]}),
    .PCO(mem_wb_1_pco), .DMoutO(mem_wb_1_dmouto), .AluO(mem_wb_1_aluo), .IR_2(WB_IR), .IR(MEM_IR),
    .Reg1_3(Reg1_4), .Reg2_3(Reg2_4), .Reg1_O(Reg1_5), .Reg2_O(Reg2_5), .MEM_PC(M_PC), .MEM_PCO(WB_PC));

  // Other names for the same wires on the sheet: MemWrite_4 = MemWrite; RegWrite_5 = RegWrite;
  //   Imm26[25:0] = ID_IR[25:0]; rd2[4:0] = ID_IR[15:11]; rt2[4:0] = ID_IR[20:16]; MEM_PC[31:0] = M_PC

  // Notes on the sheet:
  //   中断源
  //   时空图监测，可删除
  //   中断等待指示
  //   数码管输出
  //   指令存储器
  //   contents of rom_1 (hex, n*v repeats v):
  //   20110001 8000c05 20110001 20120002 20130003 8000c09 20110001 20120002 20130003 8000c0d 20110001
  //   20120002 20130003 8000c11 20110001 20120002 20130003 c000cb8 20100001 20110001 118fc0 112020
  //   20020022 c 118882 12200001 8000c15 112020 20020022 c 20110001 118880 112020 20020022 c 12200001
  //   8000c1f 20110001 118fc0 112020 20020022 c 1188c3 112020 20020022 c 118903 112020 20020022 c 118903
  //   112020 20020022 c 118903 112020 20020022 c 118903 112020 20020022 c 118903 112020 20020022 c 118903
  //   112020 20020022 c 118903 112020 20020022 c 20100001 109fc0 139fc3 8021 2012000c 24160003 26100001
  //   3210000f 20080008 20090001 139900 2709825 132020 20020022 c 1094022 1500fff9 22100001 2018000f
  //   2188024 108700 20080008 20090001 139902 2709825 132021 20020022 c 1094022 1500fff9 108702 2c9b022
  //   12c00001 8000c50 4020 1084027 84400 3508ffff 82021 20020022 c 2010ffff 20110000 ae300000 22100001
  //   22310004 ae300000 22100001 22310004 ae300000 22100001 22310004 ae300000 22100001 22310004 ae300000
  //   22100001 22310004 ae300000 22100001 22310004 ae300000 22100001 22310004 ae300000 22100001 22310004
  //   ae300000 22100001 22310004 ae300000 22100001 22310004 ae300000 22100001 22310004 ae300000 22100001
  //   22310004 ae300000 22100001 22310004 ae300000 22100001 22310004 ae300000 22100001 22310004 ae300000
  //   22100001 22310004 22100001 8020 2011003c 8e130000 8e340000 274402a 11000002 ae330000 ae140000
  //   2231fffc 1611fff8 102020 20020022 c 22100004 2011003c 1611fff2 20020032 c 20100000 22100001 102020
  //   20020022 c 22100002 102020 20020022 c 22100003 102020 20020022 c 22100004 102020 20020022 c 22100005
  //   102020 20020022 c 22100006 102020 20020022 c 22100007 102020 20020022 c 22100008 102020 20020022
  //   20020022 c 3e00008
  //   JMP
  //   JR
  //   OP
  //   Func
  //   rs
  //   rt
  //   rd
  //   shmat
  //   Imm
  //   Beq
  //   Bgtz
  //   Bne
  //   MemToReg
  //   MemWrite
  //   AluOP
  //   AluSrcB
  //   RegWrite
  //   JAL
  //   RegDst
  //   Syscall
  //   流水调试日志用
  //   EX执行
  //   为方便自动评测，需要输出流水线各段保存的PC值，注意是PC不是PC+4，另外ID段寄存器写入信息，Mem段内存写入信息也要输出
  //   MEM访存
  //   WB写回
endmodule
module \重定向流水线  (
  output RegWrite,
  output MemWrite,
  output [31:0] IF_PC,
  output [31:0] ID_PC,
  output [31:0] EX_PC,
  output [31:0] M_PC,
  output [31:0] WB_PC,
  output [31:0] RDin,
  output [31:0] MDin,
  output [31:0] LedData
);

  wire AluSrcB_3, and_1_out, and_2_out, and_3_out, Beq_3, Beq_4, Bgtz_3, Bgtz_4, Bne_3, Bne_4, Branch, CLK,
       comparator_1_eq, comparator_2_eq, comparator_3_gt, equal, Go, Halt, INS1, INS1_3, INS2, INS2_3, INS3,
       INS3_3, IR1, IR2, IR3, j_rst, jal_3, jal_5, jmp_3, jmp_4, jr_3, jr_4, load_2, load_3, MemToReg_5,
       not_1_out, or_1_out, or_2_out, or_3_out, or_4_out, or_6_out, RegDst_3, RegDst_4, RegDst_5, RegWrite_3,
       RegWrite_4, RST, sel1, sel2, sel3, sel4, stall, syscall_2, syscall_3, syscall_5, W1, W2, W3;
  wire [3:0] AluOp_3, \单周期硬布线控制器_1_alu_op ;
  wire [4:0] id_ex_1_shammto, multiplexer_8_out, ra2, ra3, rb2, rb3, rd3, rd4, rd5, rt3, rt4, rt5, rw_3,
       rw_4, rw_5;
  wire [15:0] \LoadUse次数 , \总周期数 , \插入气泡数 , \无条件分支数 , \条件分支成功数 ;
  wire [16:0] mem_wb_1_controlo, \单周期硬布线控制器_1_jr ;
  wire [16:5] ex_mem_1_controlo, id_ex_1_controlo;
  wire [25:0] Imm26_3;
  wire [31:0] alur_4, EX_IR, ex_mem_1_pco, id_ex_1_reg1o, id_ex_1_reg2o, ID_IR, if_id_1_pc_4o, IF_IR, imm,
       Imm32, MEM_IR, mem_wb_1_aluo, mem_wb_1_dmouto, mem_wb_1_pco, mips_alu_1_result, multiplexer_1_out,
       multiplexer_2_out, multiplexer_3_out, multiplexer_9_out, multiplexer_11_out, multiplexer_13_out,
       multiplexer_16_out, PC_4, PC_4_3, pcout_1_out_10, ram_1_data, Reg1, Reg1_3, Reg1_4, Reg1_5, Reg2,
       Reg2_3, WB_IR;

  Button \u_总复位  (.out(RST));
  Button _1 (.out(IR1));
  Button _2 (.out(IR2));
  Button _3 (.out(IR3));
  // Probe on \总周期数 
  // Probe on \总周期数 
  Button \u_继续运行  (.out(Go));
  LED led_1 (.in(W1));
  LED led_2 (.in(W2));
  LED led_3 (.in(W3));
  Hex_Digit_Display hex_digit_display_1 (.value(LedData[31:28]));  // open: dp
  // Probe on IF_PC[19:0]
  // Mips_Probe mips_probe_1: pin names not known; wires that end beside it: IF_IR
  PCout pcout_1 (
    .PC_4(PC_4), .Imm26(Imm26_3), .Imm32(imm), .Reg1(Reg1_3), .JMP(jmp_3), .JR(jr_3), .JAL(jal_5),
    .Branch(Branch), .PC_4_3(PC_4_3), .out_10(pcout_1_out_10));
  Hex_Digit_Display hex_digit_display_2 (.value(LedData[23:20]));  // open: dp
  Hex_Digit_Display hex_digit_display_3 (.value(LedData[27:24]));  // open: dp
  // Probe on ID_PC[19:0]
  // Mips_Probe mips_probe_2: pin names not known; wires that end beside it: ID_IR
  not not_1 (not_1_out, or_1_out);
  or or_1 (or_1_out, Halt, stall);
  Multiplexer #(.width(32), .enable("false")) multiplexer_1 (
    .in0({32{1'b0}}), .in1(Reg1_3), .out(multiplexer_1_out), .sel(syscall_3));
  Multiplexer #(.width(32), .enable("false")) multiplexer_2 (
    .in0({32{1'b0}}), .in1(Reg1_5), .out(multiplexer_2_out), .sel(syscall_5));
  Hex_Digit_Display hex_digit_display_4 (.value(LedData[19:16]));  // open: dp
  Hex_Digit_Display hex_digit_display_5 (.value(LedData[15:12]));  // open: dp
  Register #(.width(32)) PC (.D(pcout_1_out_10), .en(not_1_out), .Q(IF_PC), .clk(CLK), .clr(RST));
  Adder #(.width(32)) adder_1 (.a(IF_PC), .b(32'h4), .out(PC_4));  // open: cin, cout
  Comparator #(.width(32), .mode("unsigned")) comparator_1 (
    .a(multiplexer_1_out), .b(32'h22), .eq(comparator_1_eq));  // open: gt, lt
  Multiplexer #(.width(32), .enable("false")) multiplexer_3 (
    .in0({32{1'b0}}), .in1(Reg2_3), .out(multiplexer_3_out), .sel(comparator_1_eq));
  Comparator #(.width(32), .mode("unsigned")) comparator_2 (
    .a(multiplexer_2_out), .b(32'ha), .eq(comparator_2_eq));  // open: gt, lt
  Hex_Digit_Display hex_digit_display_6 (.value(LedData[7:4]));  // open: dp
  Hex_Digit_Display hex_digit_display_7 (.value(LedData[11:8]));  // open: dp
  Clock clock_1 (.out(CLK));
  // Probe on EX_PC[19:0]
  // Mips_Probe mips_probe_3: pin names not known; wires that end beside it: EX_IR
  Register #(.width(32)) register_1 (.D(multiplexer_3_out), .en(comparator_1_eq), .Q(LedData), .clk(CLK), .clr(RST));
  Multiplexer #(.enable("false")) multiplexer_4 (.in0(1'b0), .in1(1'b1), .out(Halt), .sel(comparator_2_eq));
  Hex_Digit_Display hex_digit_display_8 (.value(LedData[3:0]));  // open: dp
  ROM #(.addrWidth(10), .dataWidth(32)) rom_1 (.addr(IF_PC[11:2]), .data(IF_IR));  // open: sel
  or or_2 (or_2_out, j_rst, RST);
  // Probe on \总周期数 
  // Probe on M_PC[19:0]
  // Mips_Probe mips_probe_4: pin names not known; wires that end beside it: MEM_IR
  IF_ID if_id_1 (
    .CLK(CLK), .RST(or_2_out), .Halt(or_3_out), .PC_4(PC_4), .IR(IF_IR), .PC_4O(if_id_1_pc_4o), .IRO(ID_IR),
    .IF_PC(IF_PC), .IF_PCO(ID_PC));  // open: jump_att, hit, pc_att, hit_pos, pc_attO, hit_posO, jump_attO, hitO, PC, PCO
  or or_3 (or_3_out, stall, Halt);
  // Probe on \总周期数 
  // Probe on \无条件分支数 
  // Probe on \条件分支成功数 
  // Probe on \插入气泡数 
  // Probe on \LoadUse次数 
  // Probe on IF_PC[11:0]
  // Probe on WB_PC[19:0]
  // Mips_Probe mips_probe_5: pin names not known; wires that end beside it: WB_IR
  \单周期硬布线控制器  \u_单周期硬布线控制器_1  (
    .Func(ID_IR[5:0]), .OP(ID_IR[31:26]), .ALU_OP(\单周期硬布线控制器_1_alu_op ), .MemToReg(\单周期硬布线控制器_1_jr [5]),
    .MemWrite(\单周期硬布线控制器_1_jr [6]), .ALU_SRC(\单周期硬布线控制器_1_jr [11]), .RegWrite(\单周期硬布线控制器_1_jr [12]),
    .SysCALL(syscall_2), .SignedExt(\单周期硬布线控制器_1_jr [16]), .RegDst(\单周期硬布线控制器_1_jr [14]),
    .JR(\单周期硬布线控制器_1_jr [0]), .JMP(\单周期硬布线控制器_1_jr [1]), .Beq(\单周期硬布线控制器_1_jr [2]),
    .JAL(\单周期硬布线控制器_1_jr [13]), .Bne(\单周期硬布线控制器_1_jr [4]), .INS1(INS1), .INS2(INS2), .INS3(INS3),
    .Bgtz(\单周期硬布线控制器_1_jr [3]));  // open: RET
  Comparator #(.width(32)) comparator_3 (.a(Reg1_3), .b({32{1'b0}}), .gt(comparator_3_gt));  // open: eq, lt
  and and_1 (and_1_out, comparator_3_gt, Bgtz_3);
  and and_2 (and_2_out, Beq_3, equal);
  or or_4 (or_4_out, and_2_out, and_3_out);
  and and_3 (and_3_out, Bne_3, ~equal);  // AND_Gate
  // Probe on EX_PC[11:0]
  // Probe on ID_PC[11:0]
  Multiplexer #(.width(5), .enable("false")) multiplexer_5 (
    .in0(ID_IR[25:21]), .in1(5'b00010), .out(ra2), .sel(syscall_2));
  Multiplexer #(.width(5), .enable("false")) multiplexer_6 (
    .in0(ID_IR[20:16]), .in1(5'b00100), .out(rb2), .sel(syscall_2));
  Multiplexer #(.width(5), .enable("false")) multiplexer_7 (
    .in0(multiplexer_8_out), .in1({5{1'b1}}), .out(rw_5), .sel(jal_5));
  Multiplexer #(.width(5), .enable("false")) multiplexer_8 (
    .in0(rt5), .in1(rd5), .out(multiplexer_8_out), .sel(RegDst_5));
  assign Imm32 = {{16{ID_IR[15]}}, ID_IR[15:0]};  // Bit_Extender bit_extender_1
  Multiplexer #(.width(32), .enable("false")) multiplexer_9 (
    .in0(mem_wb_1_aluo), .in1(mem_wb_1_dmouto), .out(multiplexer_9_out), .sel(MemToReg_5));
  or or_5 (Branch, and_1_out, or_4_out);
  // Probe on M_PC[11:0]
  Comparator #(.width(6), .mode("unsigned")) comparator_4 (
    .a(ID_IR[31:26]), .b(6'b100011), .eq(load_2));  // open: gt, lt
  Multiplexer #(.width(32), .enable("false")) multiplexer_10 (
    .in0(multiplexer_9_out), .in1(mem_wb_1_pco), .out(RDin), .sel(jal_5));
  // Probe on WB_PC[11:0]
  MIPS_Regifile mips_regifile_1 (
    .Din(RDin), .Clk(CLK), .R1(Reg1), .R2(Reg2), .WE(RegWrite), .W_num(rw_5), .R1_num(ra2), .R2_num(rb2));
  ID_EX id_ex_1 (
    .CLK(CLK), .rd(ID_IR[15:11]), .rt(ID_IR[20:16]), .reg1(Reg1), .reg2(Reg2), .Imm(Imm32),
    .PC_4(if_id_1_pc_4o),
    .Control({\单周期硬布线控制器_1_jr [16], syscall_2, \单周期硬布线控制器_1_jr [14:11], \单周期硬布线控制器_1_alu_op , \单周期硬布线控制器_1_jr [6:0]}),
    .RST(or_6_out), .Halt(Halt), .Shammt(ID_IR[10:6]), .imm26(ID_IR[25:0]), .ra2(ra2), .rt2(rb2),
    .load_2(load_2), .INS1_2(INS1), .INS1_3(INS2), .INS1_4(INS3), .imm26O(Imm26_3), .rdO(rd3), .rtO(rt3),
    .ControlO({id_ex_1_controlo[16], syscall_3, RegDst_3, jal_3, RegWrite_3, AluSrcB_3, AluOp_3, id_ex_1_controlo[6:5], Bne_3, Bgtz_3, Beq_3, jmp_3, jr_3}),
    .PCO(PC_4_3), .reg1O(id_ex_1_reg1o), .reg2O(id_ex_1_reg2o), .ImmO(imm), .ShammtO(id_ex_1_shammto),
    .ra2O(ra3), .rd2O(rb3), .loadO(load_3), .INS3_O(INS3_3), .INS2_O(INS2_3), .INS1_O(INS1_3), .IR(ID_IR),
    .IR_2(EX_IR), .IR_PC(ID_PC), .IR_PCO(EX_PC));  // open: jump_att, hit, pc_att, hit_pos, pc_attO, hit_posO, jump_attO, hitO, PCO_2, PC
  or or_6 (or_6_out, j_rst, RST, stall);
  \分支相关  \u_分支相关_1  (.j(jmp_3), .jr(jr_3), .jal(jal_3), .branch(Branch), .j_rst(j_rst));
  \重定向  \u_重定向_1  (
    .INS1(INS1_3), .INS2(INS2_3), .INS3(INS3_3), .RegWrite4(RegWrite_4), .RegWrite5(RegWrite), .ra3(ra3),
    .rb3(rb3), .rw4(rw_4), .rw5(rw_5), .sel1(sel1), .sel2(sel2), .sel3(sel3), .sel4(sel4));
  Multiplexer #(.width(32), .enable("false")) multiplexer_11 (
    .in0(id_ex_1_reg1o), .in1(RDin), .out(multiplexer_11_out), .sel(sel3));
  Multiplexer #(.width(32), .enable("false")) multiplexer_12 (
    .in0(multiplexer_11_out), .in1(alur_4), .out(Reg1_3), .sel(sel1));
  Multiplexer #(.width(32), .enable("false")) multiplexer_13 (
    .in0(id_ex_1_reg2o), .in1(RDin), .out(multiplexer_13_out), .sel(sel4));
  Multiplexer #(.width(32), .enable("false")) multiplexer_14 (
    .in0(multiplexer_13_out), .in1(alur_4), .out(Reg2_3), .sel(sel2));
  Multiplexer #(.width(5), .enable("false")) multiplexer_15 (.in0(rt3), .in1(rd3), .out(rw_3), .sel(RegDst_3));
  Multiplexer #(.width(32), .enable("false")) multiplexer_16 (
    .in0(Reg2_3), .in1(imm), .out(multiplexer_16_out), .sel(AluSrcB_3));
  EX_MEM ex_mem_1 (
    .CLK(CLK), .RST(RST), .Halt(Halt),
    .Control({id_ex_1_controlo[16], syscall_3, RegDst_3, jal_3, RegWrite_3, AluSrcB_3, AluOp_3, id_ex_1_controlo[6:5], Bne_3, Bgtz_3, Beq_3, jmp_3, jr_3}),
    .PC(PC_4_3), .reg2(Reg2_3), .Alu(mips_alu_1_result), .rd(rd3), .rt(rt3), .rdO(rd4), .rtO(rt4),
    .ControlO({ex_mem_1_controlo[16:15], RegDst_4, ex_mem_1_controlo[13], RegWrite_4, ex_mem_1_controlo[11:7], MemWrite, ex_mem_1_controlo[5], Bne_4, Bgtz_4, Beq_4, jmp_4, jr_4}),
    .PCO(ex_mem_1_pco), .reg2O(MDin), .AluO(alur_4), .IR(EX_IR), .IR_2(MEM_IR), .Reg1_3(Reg1_3),
    .Reg1_O(Reg1_4), .EX_PC(EX_PC), .EX_PCO(M_PC));  // open: Reg2_3, Reg2_O
  MIPS_ALU mips_alu_1 (
    .X(Reg1_3), .Y(multiplexer_16_out), .AluOP(AluOp_3), .Equal(equal), .Result(mips_alu_1_result),
    .shamt(id_ex_1_shammto));  // open: Result_2
  Load_Use load_use_1 (
    .INS1(INS1), .stall(stall), .INS2(INS2), .INS3(INS3), .RegDin3(load_3), .ra(ra2), .rb(rb2), .rw3(rw_3));
  counter counter_1 (
    .rst(RST), .clk(CLK), .jmp(jmp_3), .jr(jr_3), .branch(Branch), .halt(Halt), .\总周期数 (\总周期数 ),
    .\条件分支成功数 (\条件分支成功数 ), .\无条件分支数 (\无条件分支数 ), .pop(stall), .\气泡数 (\LoadUse次数 ));
  Multiplexer #(.width(5), .enable("false")) multiplexer_17 (.in0(rt4), .in1(rd4), .out(rw_4), .sel(RegDst_4));
  RAM #(.addrWidth(10), .dataWidth(32), .bus("separate")) ram_1 (
    .addr(alur_4[11:2]), .din(MDin), .data(ram_1_data), .str(MemWrite), .clk(CLK), .clr(RST));  // open: sel, ld
  MEM_WB mem_wb_1 (
    .CLK(CLK), .RST(RST), .Halt(Halt),
    .Control({ex_mem_1_controlo[16:15], RegDst_4, ex_mem_1_controlo[13], RegWrite_4, ex_mem_1_controlo[11:7], MemWrite, ex_mem_1_controlo[5], Bne_4, Bgtz_4, Beq_4, jmp_4, jr_4}),
    .Alu(alur_4), .PC(ex_mem_1_pco), .DMout(ram_1_data), .rd(rd4), .rt(rt4), .rdO(rd5), .rtO(rt5),
    .ControlO({mem_wb_1_controlo[16], syscall_5, RegDst_5, jal_5, RegWrite, mem_wb_1_controlo[11:6], MemToReg_5, mem_wb_1_controlo[4:0]}),
    .PCO(mem_wb_1_pco), .DMoutO(mem_wb_1_dmouto), .AluO(mem_wb_1_aluo), .IR_2(WB_IR), .IR(MEM_IR),
    .Reg1_3(Reg1_4), .Reg1_O(Reg1_5), .MEM_PC(M_PC), .MEM_PCO(WB_PC));  // open: Reg2_3, Reg2_O

  // Other names for the same wires on the sheet: MemWrite_4 = MemWrite; RegWrite_5 = RegWrite;
  //   Imm26[25:0] = ID_IR[25:0]; rd2[4:0] = ID_IR[15:11]; rt2[4:0] = ID_IR[20:16]; op2[5:0] = ID_IR[31:26];
  //   MEM_PC[31:0] = M_PC; RegD_5[31:0] = RDin

  // Notes on the sheet:
  //   中断源
  //   时空图监测，可删除
  //   中断等待指示
  //   数码管输出
  //   指令存储器
  //   contents of rom_1 (hex, n*v repeats v):
  //   20110001 8000c05 20110001 20120002 20130003 8000c09 20110001 20120002 20130003 8000c0d 20110001
  //   20120002 20130003 8000c11 20110001 20120002 20130003 c000cb8 20100001 20110001 118fc0 112020
  //   20020022 c 118882 12200001 8000c15 112020 20020022 c 20110001 118880 112020 20020022 c 12200001
  //   8000c1f 20110001 118fc0 112020 20020022 c 1188c3 112020 20020022 c 118903 112020 20020022 c 118903
  //   112020 20020022 c 118903 112020 20020022 c 118903 112020 20020022 c 118903 112020 20020022 c 118903
  //   112020 20020022 c 118903 112020 20020022 c 20100001 109fc0 139fc3 8021 2012000c 24160003 26100001
  //   3210000f 20080008 20090001 139900 2709825 132020 20020022 c 1094022 1500fff9 22100001 2018000f
  //   2188024 108700 20080008 20090001 139902 2709825 132021 20020022 c 1094022 1500fff9 108702 2c9b022
  //   12c00001 8000c50 4020 1084027 84400 3508ffff 82021 20020022 c 2010ffff 20110000 ae300000 22100001
  //   22310004 ae300000 22100001 22310004 ae300000 22100001 22310004 ae300000 22100001 22310004 ae300000
  //   22100001 22310004 ae300000 22100001 22310004 ae300000 22100001 22310004 ae300000 22100001 22310004
  //   ae300000 22100001 22310004 ae300000 22100001 22310004 ae300000 22100001 22310004 ae300000 22100001
  //   22310004 ae300000 22100001 22310004 ae300000 22100001 22310004 ae300000 22100001 22310004 ae300000
  //   22100001 22310004 22100001 8020 2011003c 8e130000 8e340000 274402a 11000002 ae330000 ae140000
  //   2231fffc 1611fff8 102020 20020022 c 22100004 2011003c 1611fff2 20020032 c 20100000 22100001 102020
  //   20020022 c 22100002 102020 20020022 c 22100003 102020 20020022 c 22100004 102020 20020022 c 22100005
  //   102020 20020022 c 22100006 102020 20020022 c 22100007 102020 20020022 c 22100008 102020 20020022
  //   20020022 c 3e00008
  //   JMP
  //   JR
  //   OP
  //   Func
  //   rs
  //   rt
  //   rd
  //   shmat
  //   Imm
  //   Beq
  //   Bgtz
  //   Bne
  //   MemToReg
  //   MemWrite
  //   AluOP
  //   AluSrcB
  //   RegWrite
  //   JAL
  //   RegDst
  //   Syscall
  //   流水调试日志用
  //   为方便自动评测，需要输出流水线各段保存的PC值，注意是PC不是PC+4，另外ID段寄存器写入信息，Mem段内存写入信息也要输出
endmodule

module \中断按键参考电路  (
  input  \同步清零信号 ,
  output \与中断屏蔽位与 
);

  wire \_1号中断_out , and_1_out, clock_1_out, d_ff_1_q, or_1_out, or_2_out;

  Clock clock_1 (.out(clock_1_out));
  Button \_1号中断  (.out(\_1号中断_out ));
  LED \_1号中断等待指示灯  (.in(or_1_out));
  or or_1 (or_1_out, \与中断屏蔽位与 , d_ff_1_q);
  D_Flip_Flop d_ff_1 (.clk(\_1号中断_out ), .D(1'b1), .Q(d_ff_1_q), .reset(\与中断屏蔽位与 ));  // open: Qn, preset, en
  or or_2 (or_2_out, d_ff_1_q, \与中断屏蔽位与 );
  and and_1 (and_1_out, or_2_out, ~\同步清零信号 );  // AND_Gate
  D_Flip_Flop IR1 (.clk(clock_1_out), .D(and_1_out), .Q(\与中断屏蔽位与 ));  // open: Qn, preset, en, reset

  // Notes on the sheet:
  //   中断信号采样参考电路
  //   Reset 
endmodule

module \单周期MIPS_单级中断  (
  input  IR1,
  input  IR2,
  input  IR3,
  output RegWrite,
  output MemWrite,
  output [31:0] PC,
  output [31:0] IR,
  output [31:0] RDin,
  output [31:0] MDin,
  output [31:0] LedData
);

  wire and_1_out, and_2_out, and_3_out, and_8_out, and_9_out, and_11_out, and_12_out, and_13_out, Beq, Bgtz,
       Bne, Branch, CLK, comparator_1_eq, comparator_2_gt, comparator_3_eq, comparator_4_eq, d_ff_1_q,
       d_ff_2_q, d_ff_3_q, d_ff_4_q, decoder_1_out1, decoder_1_out2, decoder_1_out3, equal, eret, Go, Halt,
       IE_q, IR1_t, ir1_t_t, IR2_t, ir2_t_t, IR3_t, ir3_t_t, IR_CPU, IRA, IRB, IRC, jal, jmp, jr, MemToReg,
       not_1_out, not_2_out, not_3_out, not_4_out, or_4_out, or_5_out, or_6_out, or_10_out,
       priority_encoder_1_gs, Ret, RST, rst1, rst2, rst3, SignedExt, syscall, W1, W2, W3,
       \单周期硬布线控制器_1_alu_src , \单周期硬布线控制器_1_regdst ;
  wire [1:0] cur_index, priority_encoder_1_out;
  wire [3:0] \单周期硬布线控制器_1_alu_op ;
  wire [4:0] multiplexer_3_out, multiplexer_4_out, multiplexer_5_out, multiplexer_6_out;
  wire [15:0] \总周期数 ;
  wire [31:0] EPC, imm32, irPC, mips_alu_1_result, multiplexer_1_out, multiplexer_2_out, multiplexer_8_out,
       multiplexer_9_out, multiplexer_10_out, multiplexer_11_out, nextPC, PC_4, ram_1_data, Reg1;

  Clock clock_1 (.out(CLK));
  Button _1 (.out(IRA));
  Button _2 (.out(IRB));
  Button _3 (.out(IRC));
  Button \u_总复位  (.out(RST));
  Button \u_继续运行  (.out(Go));
  LED led_1 (.in(W1));
  LED led_2 (.in(W2));
  LED led_3 (.in(W3));
  PCout pcout_1 (
    .PC_4(PC_4), .Imm26(IR[25:0]), .Imm32(imm32), .Reg1(Reg1), .JMP(jmp), .JR(jr), .JAL(jal),
    .Branch(Branch), .PC_4_3(PC_4), .out_10(nextPC));
  or or_1 (W1, ir1_t_t, d_ff_1_q);
  or or_2 (W2, ir2_t_t, d_ff_2_q);
  or or_3 (W3, ir3_t_t, d_ff_3_q);
  Hex_Digit_Display hex_digit_display_1 (.value(LedData[31:28]));  // open: dp
  D_Flip_Flop d_ff_1 (.clk(IR1_t), .D(1'b1), .Q(d_ff_1_q), .reset(ir1_t_t));  // open: Qn, preset, en
  D_Flip_Flop d_ff_2 (.clk(IR2_t), .D(1'b1), .Q(d_ff_2_q), .reset(ir2_t_t));  // open: Qn, preset, en
  D_Flip_Flop d_ff_3 (.clk(IR3_t), .D(1'b1), .Q(d_ff_3_q), .reset(ir3_t_t));  // open: Qn, preset, en
  Decoder #(.select(2), .enable("false")) decoder_1 (
    .out1(decoder_1_out1), .out2(decoder_1_out2), .out3(decoder_1_out3), .sel(cur_index));  // open: out0
  Hex_Digit_Display hex_digit_display_2 (.value(LedData[23:20]));  // open: dp
  Hex_Digit_Display hex_digit_display_3 (.value(LedData[27:24]));  // open: dp
  Multiplexer #(.width(32), .enable("false")) multiplexer_1 (
    .in0(nextPC), .in1(irPC), .out(multiplexer_1_out), .sel(IR_CPU));
  Multiplexer #(.width(32), .enable("false")) multiplexer_2 (
    .in0(multiplexer_1_out), .in1(EPC), .out(multiplexer_2_out), .sel(eret));
  or or_4 (or_4_out, d_ff_1_q, ir1_t_t);
  or or_5 (or_5_out, d_ff_2_q, ir2_t_t);
  or or_6 (or_6_out, d_ff_3_q, ir3_t_t);
  Hex_Digit_Display hex_digit_display_4 (.value(LedData[15:12]));  // open: dp
  Hex_Digit_Display hex_digit_display_5 (.value(LedData[19:16]));  // open: dp
  Register #(.width(32)) u_PC (.D(multiplexer_2_out), .en(not_1_out), .Q(PC), .clk(CLK), .clr(RST));
  not not_1 (not_1_out, Halt);
  and and_1 (and_1_out, or_4_out, ~rst1);  // AND_Gate
  and and_2 (and_2_out, or_5_out, ~rst2);  // AND_Gate
  and and_3 (and_3_out, or_6_out, ~rst3);  // AND_Gate
  and and_4 (rst1, eret, decoder_1_out1);
  and and_5 (rst2, decoder_1_out2, eret);
  and and_6 (rst3, decoder_1_out3, eret);
  Hex_Digit_Display hex_digit_display_6 (.value(LedData[7:4]));  // open: dp
  Hex_Digit_Display hex_digit_display_7 (.value(LedData[11:8]));  // open: dp
  // Probe on \总周期数 
  // Probe on \总周期数 
  Comparator #(.width(5), .mode("unsigned")) comparator_1 (
    .a(IR[25:21]), .b(5'b10000), .eq(comparator_1_eq));  // open: gt, lt
  Adder #(.width(32)) adder_1 (.a(PC), .b(32'h4), .out(PC_4));  // open: cin, cout
  D_Flip_Flop u_IR1 (.clk(CLK), .D(and_1_out), .Q(ir1_t_t));  // open: Qn, preset, en, reset
  D_Flip_Flop u_IR2 (.clk(CLK), .D(and_2_out), .Q(ir2_t_t));  // open: Qn, preset, en, reset
  D_Flip_Flop u_IR3 (.clk(CLK), .D(and_3_out), .Q(ir3_t_t));  // open: Qn, preset, en, reset
  Hex_Digit_Display hex_digit_display_8 (.value(LedData[3:0]));  // open: dp
  and and_7 (eret, Ret, comparator_1_eq);
  // Mips_Probe mips_probe_1: pin names not known; wires that end beside it: IR
  ROM #(.addrWidth(10), .dataWidth(32)) rom_1 (.addr(PC[11:2]), .data(IR));  // open: sel
  or or_7 (IR1_t, IR1, IRA);
  not not_2 (not_2_out, eret);
  or or_8 (IR2_t, IR2, IRB);
  \单周期硬布线控制器  \u_单周期硬布线控制器_1  (
    .Func(IR[5:0]), .OP(IR[31:26]), .ALU_OP(\单周期硬布线控制器_1_alu_op ), .MemToReg(MemToReg), .MemWrite(MemWrite),
    .ALU_SRC(\单周期硬布线控制器_1_alu_src ), .RegWrite(RegWrite), .SysCALL(syscall), .SignedExt(SignedExt),
    .RegDst(\单周期硬布线控制器_1_regdst ), .JR(jr), .JMP(jmp), .Beq(Beq), .JAL(jal), .Bne(Bne), .Bgtz(Bgtz), .RET(Ret));  // open: INS1, INS2, INS3
  Priority_Encoder #(.select(2)) priority_encoder_1 (
    .in0(1'b0), .in1(ir1_t_t), .in2(ir2_t_t), .in3(ir3_t_t), .out(priority_encoder_1_out),
    .gs(priority_encoder_1_gs));  // open: en_out, en_in
  D_Flip_Flop IE (.clk(CLK), .D(1'b1), .Q(IE_q), .preset(eret), .en(not_3_out), .reset(and_8_out));  // open: Qn
  and and_8 (and_8_out, not_2_out, d_ff_4_q);
  D_Flip_Flop d_ff_4 (.clk(CLK), .D(and_9_out), .Q(d_ff_4_q), .en(IR_CPU));  // open: Qn, preset, reset
  Register #(.width(32)) u_EPC (.D(nextPC), .en(and_9_out), .Q(EPC), .clk(CLK));  // open: clr
  and and_9 (and_9_out, not_2_out, IR_CPU);
  Multiplexer #(.width(5), .enable("false")) multiplexer_3 (
    .in0(IR[20:16]), .in1(IR[15:11]), .out(multiplexer_3_out), .sel(\单周期硬布线控制器_1_regdst ));
  assign imm32 = {{16{IR[15]}}, IR[15:0]};  // Bit_Extender bit_extender_1
  and and_10 (IR_CPU, priority_encoder_1_gs, IE_q);
  not not_3 (not_3_out, IE_q);
  or or_9 (IR3_t, IR3, IRC);
  Multiplexer #(.width(5), .enable("false")) multiplexer_4 (
    .in0(IR[25:21]), .in1(5'b00010), .out(multiplexer_4_out), .sel(syscall));
  Multiplexer #(.width(5), .enable("false")) multiplexer_5 (
    .in0(IR[20:16]), .in1(5'b00100), .out(multiplexer_5_out), .sel(syscall));
  Multiplexer #(.width(5), .enable("false")) multiplexer_6 (
    .in0(multiplexer_3_out), .in1({5{1'b1}}), .out(multiplexer_6_out), .sel(jal));
  Multiplexer #(.select(2), .width(32), .enable("false")) multiplexer_7 (
    .in0({32{1'b0}}), .in1(32'h30ac), .in2(32'h3150), .in3(32'h31f4), .out(irPC), .sel(priority_encoder_1_out));
  Register #(.width(2)) register_1 (.D(priority_encoder_1_out), .Q(cur_index), .clk(and_9_out));  // open: en, clr
  MIPS_Regifile mips_regifile_1 (
    .Din(RDin), .Clk(CLK), .R1(Reg1), .R2(MDin), .WE(RegWrite), .W_num(multiplexer_6_out),
    .R1_num(multiplexer_4_out), .R2_num(multiplexer_5_out));
  Multiplexer #(.width(32), .enable("false")) multiplexer_8 (
    .in0(MDin), .in1(imm32), .out(multiplexer_8_out), .sel(\单周期硬布线控制器_1_alu_src ));
  MIPS_ALU mips_alu_1 (
    .X(Reg1), .Y(multiplexer_8_out), .AluOP(\单周期硬布线控制器_1_alu_op ), .Equal(equal), .Result(mips_alu_1_result),
    .shamt(IR[10:6]));  // open: Result_2
  Comparator #(.width(32)) comparator_2 (.a(Reg1), .b({32{1'b0}}), .gt(comparator_2_gt));  // open: eq, lt
  Multiplexer #(.width(32), .enable("false")) multiplexer_9 (
    .in0({32{1'b0}}), .in1(Reg1), .out(multiplexer_9_out), .sel(syscall));
  Multiplexer #(.width(32), .enable("false")) multiplexer_10 (
    .in0({32{1'b0}}), .in1(Reg1), .out(multiplexer_10_out), .sel(syscall));
  and and_11 (and_11_out, comparator_2_gt, Bgtz);
  and and_12 (and_12_out, Beq, equal);
  or or_10 (or_10_out, and_12_out, and_13_out);
  and and_13 (and_13_out, Bne, ~equal);  // AND_Gate
  Counter #(.width(16), .max('hffff)) counter_1 (
    .count(not_4_out), .Q(\总周期数 ), .clk(CLK), .clr(RST));  // open: load, D, carry
  not not_4 (not_4_out, Halt);
  Comparator #(.width(32), .mode("unsigned")) comparator_3 (
    .a(multiplexer_9_out), .b(32'h22), .eq(comparator_3_eq));  // open: gt, lt
  Comparator #(.width(32), .mode("unsigned")) comparator_4 (
    .a(multiplexer_10_out), .b(32'ha), .eq(comparator_4_eq));  // open: gt, lt
  or or_11 (Branch, and_11_out, or_10_out);
  RAM #(.addrWidth(10), .dataWidth(32), .bus("separate")) ram_1 (
    .addr(mips_alu_1_result[11:2]), .din(MDin), .data(ram_1_data), .str(MemWrite), .clk(CLK), .clr(RST));  // open: sel, ld
  Multiplexer #(.width(32), .enable("false")) multiplexer_11 (
    .in0({32{1'b0}}), .in1(MDin), .out(multiplexer_11_out), .sel(comparator_3_eq));
  Register #(.width(32)) register_2 (.D(multiplexer_11_out), .en(comparator_3_eq), .Q(LedData), .clk(CLK), .clr(RST));
  Multiplexer #(.enable("false")) multiplexer_12 (.in0(1'b0), .in1(1'b1), .out(Halt), .sel(comparator_4_eq));
  Multiplexer #(.width(32), .enable("false")) multiplexer_13 (
    .in0(mips_alu_1_result), .in1(ram_1_data), .out(RDin), .sel(MemToReg));

  // Other names for the same wires on the sheet: imm26[25:0] = IR[25:0]; rs[4:0] = IR[25:21]; Reg2[31:0] = MDin

  // Notes on the sheet:
  //   中断源
  //   中断等待指示
  //   总复位信号应将除ROM以外所有存储组件全部清零
  //   中断按键电路
  //   数码管输出
  //   Reset 
  //   Reset 
  //   Reset 
  //   数码管输出应该用寄存器锁存，否则显示数据只能一闪而过
  //   指令存储器
  //   指令字
  //   contents of rom_1 (hex, n*v repeats v):
  //   201d07d0 20100001 109fc0 139fc3 8021 2012000c 24160008 26100001 3210000f 20080008 20090001 139900
  //   2709825 132020 20020022 c 1094022 1500fff9 22100001 2018000f 2188024 108700 20080008 20090001 139902
  //   2709825 132021 20020022 c 1094022 1500fff9 108702 2c9b022 12c00001 8000c07 4020 1084027 84400
  //   3508ffff 82021 20020022 c 8000c01 afa20000 23bd0004 afa40000 23bd0004 afb00000 23bd0004 afb30000
  //   23bd0004 afb40000 23bd0004 afb50000 23bd0004 afb60000 23bd0004 20160001 20140003 20150001 168020
  //   108100 2149825 132020 20020022 c 1600fffa 295a022 1680fff7 23bdfffc 8fb60000 23bdfffc 8fb50000
  //   23bdfffc 8fb40000 23bdfffc 8fb30000 23bdfffc 8fb00000 23bdfffc 8fa40000 23bdfffc 8fa20000 42000018
  //   afa20000 23bd0004 afa40000 23bd0004 afb00000 23bd0004 afb30000 23bd0004 afb40000 23bd0004 afb50000
  //   23bd0004 afb60000 23bd0004 20160002 20140003 20150001 168020 108100 2149825 132020 20020022 c
  //   1600fffa 295a022 1680fff7 23bdfffc 8fb60000 23bdfffc 8fb50000 23bdfffc 8fb40000 23bdfffc 8fb30000
  //   23bdfffc 8fb00000 23bdfffc 8fa40000 23bdfffc 8fa20000 42000018 afa20000 23bd0004 afa40000 23bd0004
  //   afb00000 23bd0004 afb30000 23bd0004 afb40000 23bd0004 afb50000 23bd0004 afb60000 23bd0004 20160003
  //   20140003 20150001 168020 108100 2149825 132020 20020022 c 1600fffa 295a022 1680fff7 23bdfffc
  //   8fb60000 23bdfffc 8fb50000 23bdfffc 8fb40000 23bdfffc 8fb30000 23bdfffc 8fb00000 23bdfffc 8fa40000
  //   23bdfffc 8fa20000 42000018
  //   JMP
  //   JR
  //   OP
  //   rs
  //   rt
  //   rd
  //   shmat
  //   Imm
  //   Beq
  //   Bgtz
  //   Bne
  //   AluOP
  //   AluSrcB
  //   RegWrite
  //   JAL
  //   RegDst
  //   Func
  //   Syscall
  //   主数据通路
  //   MemToReg
  //   MemWrite
  //   中断仲裁与中断识别
  //   为方便自动评测，需要输出PC，IR，寄存器堆写如数据RDin
  //   RAM写使能MemWrite、RAM写入数据MDin等信号
  //   时钟周期计数器
  //   LED显示电路
  //   停机信号
endmodule

module \单周期MIPS_多级中断  (
  input  IR1,
  input  IR2,
  input  IR3,
  output RegWrite,
  output MemWrite,
  output [31:0] PC,
  output [31:0] IR,
  output [31:0] RDin,
  output [31:0] MDin,
  output [31:0] LedData
);

  wire and_1_out, and_2_out, and_3_out, and_7_out, and_8_out, and_9_out, and_10_out, and_15_out, and_16_out,
       and_17_out, Beq, Bgtz, Bne, Branch, CLK, comparator_1_eq, comparator_2_eq, comparator_3_eq,
       comparator_4_eq, comparator_5_eq, comparator_6_eq, comparator_7_eq, comparator_8_eq, comparator_9_gt,
       comparator_10_eq, comparator_11_eq, d_ff_1_q, d_ff_2_q, d_ff_3_q, d_ff_4_qn, d_ff_5_qn, d_ff_6_qn,
       d_ff_7_qn, d_ff_8_q, decoder_1_out1, decoder_1_out2, decoder_1_out3, equal, eret, Go, Halt, IE_q,
       IR1_t, ir1_t_t, IR2_t, ir2_t_t, IR3_t, ir3_t_t, IR_CPU, IRA, IRa_t, IRB, IRb_t, IRC, IRc_t, jal, jmp,
       jr, MemToReg, mfc0, mtc0, multiplexer_10_out, multiplexer_11_out, multiplexer_12_out,
       multiplexer_13_out, multiplexer_16_out, not_1_out, not_2_out, not_3_out, or_4_out, or_5_out, or_6_out,
       or_7_out, or_8_out, or_11_out, or_13_out, or_14_out, or_16_out, or_17_out, or_18_out,
       priority_encoder_2_gs, Ret, RST, rst1, rst2, rst3, SignedExt, syscall, W1, W2, W3,
       \单周期硬布线控制器_1_alu_src , \单周期硬布线控制器_1_regdst ;
  wire [1:0] cur_index, priority_encoder_1_out, priority_encoder_2_out;
  wire [3:0] inword, multiplexer_3_out, multiplexer_4_out, multiplexer_5_out, \单周期硬布线控制器_1_alu_op , \屏蔽字 ;
  wire [4:0] multiplexer_7_out, multiplexer_8_out, multiplexer_9_out, multiplexer_14_out;
  wire [15:0] \总周期数 ;
  wire [31:0] adder_2_out, adder_3_out, EPC, EPCS, imm32, INM, INMS, irPC, MemOut, mips_alu_1_result,
       multiplexer_1_out, multiplexer_2_out, multiplexer_15_out, multiplexer_19_out, multiplexer_20_out,
       multiplexer_21_out, multiplexer_22_out, multiplexer_23_out, nextPC, PC_4, Reg1, subtractor_1_out,
       subtractor_2_out;

  Clock clock_1 (.out(CLK));
  Button _1 (.out(IRA));
  Button _2 (.out(IRB));
  Button _3 (.out(IRC));
  Button \u_总复位  (.out(RST));
  Button \u_继续运行  (.out(Go));
  LED led_1 (.in(W1));
  LED led_2 (.in(W2));
  LED led_3 (.in(W3));
  PCout pcout_1 (
    .PC_4(PC_4), .Imm26(IR[25:0]), .Imm32(imm32), .Reg1(Reg1), .JMP(jmp), .JR(jr), .JAL(jal),
    .Branch(Branch), .PC_4_3(PC_4), .out_10(nextPC));
  or or_1 (W1, ir1_t_t, d_ff_1_q);
  or or_2 (W2, ir2_t_t, d_ff_2_q);
  or or_3 (W3, ir3_t_t, d_ff_3_q);
  Hex_Digit_Display hex_digit_display_1 (.value(LedData[31:28]));  // open: dp
  Multiplexer #(.width(32), .enable("false")) multiplexer_1 (
    .in0(nextPC), .in1(irPC), .out(multiplexer_1_out), .sel(IR_CPU));
  D_Flip_Flop d_ff_1 (.clk(IR1_t), .D(1'b1), .Q(d_ff_1_q), .reset(ir1_t_t));  // open: Qn, preset, en
  D_Flip_Flop d_ff_2 (.clk(IR2_t), .D(1'b1), .Q(d_ff_2_q), .reset(ir2_t_t));  // open: Qn, preset, en
  D_Flip_Flop d_ff_3 (.clk(IR3_t), .D(1'b1), .Q(d_ff_3_q), .reset(ir3_t_t));  // open: Qn, preset, en
  Hex_Digit_Display hex_digit_display_2 (.value(LedData[27:24]));  // open: dp
  Hex_Digit_Display hex_digit_display_3 (.value(LedData[23:20]));  // open: dp
  Multiplexer #(.width(32), .enable("false")) multiplexer_2 (
    .in0(multiplexer_1_out), .in1(EPC), .out(multiplexer_2_out), .sel(eret));
  not not_1 (not_1_out, Halt);
  or or_4 (or_4_out, d_ff_1_q, ir1_t_t);
  or or_5 (or_5_out, d_ff_2_q, ir2_t_t);
  or or_6 (or_6_out, d_ff_3_q, ir3_t_t);
  Priority_Encoder #(.select(2)) priority_encoder_1 (
    .in0(1'b0), .in1(ir1_t_t), .in2(ir2_t_t), .in3(ir3_t_t), .out(priority_encoder_1_out));  // open: gs, en_out, en_in
  Hex_Digit_Display hex_digit_display_4 (.value(LedData[15:12]));  // open: dp
  Hex_Digit_Display hex_digit_display_5 (.value(LedData[19:16]));  // open: dp
  Comparator #(.width(16)) comparator_1 (.a(16'h258), .b(\总周期数 ), .eq(comparator_1_eq));  // open: gt, lt
  Comparator #(.width(16)) comparator_2 (.a(\总周期数 ), .b(16'h1), .eq(comparator_2_eq));  // open: gt, lt
  Comparator #(.width(16)) comparator_3 (.a(\总周期数 ), .b(16'h4), .eq(comparator_3_eq));  // open: gt, lt
  Comparator #(.width(16)) comparator_4 (.a(\总周期数 ), .b(16'h7), .eq(comparator_4_eq));  // open: gt, lt
  Comparator #(.width(16)) comparator_5 (.a(\总周期数 ), .b(16'h241), .eq(comparator_5_eq));  // open: gt, lt
  Register #(.width(32)) u_PC (.D(multiplexer_2_out), .en(not_1_out), .Q(PC), .clk(CLK), .clr(RST));
  and and_1 (and_1_out, or_4_out, ~rst1);  // AND_Gate
  and and_2 (and_2_out, or_5_out, ~rst2);  // AND_Gate
  and and_3 (and_3_out, or_6_out, ~rst3);  // AND_Gate
  Decoder #(.select(2), .enable("false")) decoder_1 (
    .out1(decoder_1_out1), .out2(decoder_1_out2), .out3(decoder_1_out3), .sel(priority_encoder_1_out));  // open: out0
  Hex_Digit_Display hex_digit_display_6 (.value(LedData[7:4]));  // open: dp
  Hex_Digit_Display hex_digit_display_7 (.value(LedData[11:8]));  // open: dp
  // Probe on \总周期数 
  // Probe on \总周期数 
  or or_7 (or_7_out, comparator_1_eq, comparator_2_eq);
  assign IRa_t = or_7_out ? ~CLK : 1'bz;  // Controlled_Inverter controlled_inverter_1
  assign IRb_t = comparator_3_eq ? ~CLK : 1'bz;  // Controlled_Inverter controlled_inverter_2
  or or_8 (or_8_out, comparator_4_eq, comparator_5_eq);
  assign IRc_t = or_8_out ? ~CLK : 1'bz;  // Controlled_Inverter controlled_inverter_3
  Adder #(.width(32)) adder_1 (.a(PC), .b(32'h4), .out(PC_4));  // open: cin, cout
  D_Flip_Flop u_IR1 (.clk(CLK), .D(and_1_out), .Q(ir1_t_t));  // open: Qn, preset, en, reset
  D_Flip_Flop u_IR2 (.clk(CLK), .D(and_2_out), .Q(ir2_t_t));  // open: Qn, preset, en, reset
  D_Flip_Flop u_IR3 (.clk(CLK), .D(and_3_out), .Q(ir3_t_t));  // open: Qn, preset, en, reset
  and and_4 (rst1, decoder_1_out1, eret);
  and and_5 (rst2, decoder_1_out2, eret);
  and and_6 (rst3, decoder_1_out3, eret);
  Hex_Digit_Display hex_digit_display_8 (.value(LedData[3:0]));  // open: dp
  Pull_Resistor pull_resistor_1 (.node(IRa_t));
  Pull_Resistor pull_resistor_2 (.node(IRb_t));
  Pull_Resistor pull_resistor_3 (.node(IRc_t));
  // Mips_Probe mips_probe_1: pin names not known; wires that end beside it: IR, IR[31:26], IR[5:0]
  ROM #(.addrWidth(10), .dataWidth(32)) rom_1 (.addr(PC[11:2]), .data(IR));  // open: sel
  Multiplexer #(.width(4), .enable("false")) multiplexer_3 (
    .in0(4'b0000), .in1(4'b0011), .out(multiplexer_3_out), .sel(ir1_t_t));
  or or_9 (IR1_t, IR1, IRa_t, IRA);
  Multiplexer #(.width(4), .enable("false")) multiplexer_4 (
    .in0(multiplexer_3_out), .in1(4'b0111), .out(multiplexer_4_out), .sel(ir2_t_t));
  or or_10 (IR2_t, IR2, IRb_t, IRB);
  \单周期硬布线控制器  \u_单周期硬布线控制器_1  (
    .Func(IR[5:0]), .OP(IR[31:26]), .ALU_OP(\单周期硬布线控制器_1_alu_op ), .MemToReg(MemToReg), .MemWrite(MemWrite),
    .ALU_SRC(\单周期硬布线控制器_1_alu_src ), .RegWrite(RegWrite), .SysCALL(syscall), .SignedExt(SignedExt),
    .RegDst(\单周期硬布线控制器_1_regdst ), .JR(jr), .JMP(jmp), .Beq(Beq), .JAL(jal), .Bne(Bne), .Bgtz(Bgtz), .RET(Ret));  // open: INS1, INS2, INS3
  Multiplexer #(.width(4), .enable("false")) multiplexer_5 (
    .in0(multiplexer_4_out), .in1(4'b1111), .out(multiplexer_5_out), .sel(ir3_t_t));
  Multiplexer #(.width(4), .enable("false")) multiplexer_6 (
    .in0(multiplexer_5_out), .in1(INM[3:0]), .out(inword), .sel(eret));
  Multiplexer #(.width(5), .enable("false")) multiplexer_7 (
    .in0(IR[20:16]), .in1(IR[15:11]), .out(multiplexer_7_out), .sel(\单周期硬布线控制器_1_regdst ));
  assign imm32 = {{16{IR[15]}}, IR[15:0]};  // Bit_Extender bit_extender_1
  or or_11 (or_11_out, eret, IR_CPU);
  or or_12 (IR3_t, IR3, IRc_t, IRC);
  Multiplexer #(.width(5), .enable("false")) multiplexer_8 (
    .in0(IR[25:21]), .in1(5'b00010), .out(multiplexer_8_out), .sel(syscall));
  Multiplexer #(.width(5), .enable("false")) multiplexer_9 (
    .in0(IR[20:16]), .in1(5'b00100), .out(multiplexer_9_out), .sel(syscall));
  Multiplexer #(.enable("false")) multiplexer_10 (
    .in0(1'b0), .in1(inword[0]), .out(multiplexer_10_out), .sel(or_11_out));
  Multiplexer #(.enable("false")) multiplexer_11 (
    .in0(1'b0), .in1(inword[1]), .out(multiplexer_11_out), .sel(or_11_out));
  Multiplexer #(.enable("false")) multiplexer_12 (
    .in0(1'b0), .in1(inword[2]), .out(multiplexer_12_out), .sel(or_11_out));
  Multiplexer #(.enable("false")) multiplexer_13 (
    .in0(1'b0), .in1(inword[3]), .out(multiplexer_13_out), .sel(or_11_out));
  Multiplexer #(.width(5), .enable("false")) multiplexer_14 (
    .in0(multiplexer_7_out), .in1({5{1'b1}}), .out(multiplexer_14_out), .sel(jal));
  D_Flip_Flop d_ff_4 (
    .clk(CLK), .D(multiplexer_10_out), .Q(\屏蔽字 [0]), .Qn(d_ff_4_qn), .en(or_11_out));  // open: preset, reset
  D_Flip_Flop d_ff_5 (
    .clk(CLK), .D(multiplexer_11_out), .Q(\屏蔽字 [1]), .Qn(d_ff_5_qn), .en(or_11_out));  // open: preset, reset
  D_Flip_Flop d_ff_6 (
    .clk(CLK), .D(multiplexer_12_out), .Q(\屏蔽字 [2]), .Qn(d_ff_6_qn), .en(or_11_out));  // open: preset, reset
  D_Flip_Flop d_ff_7 (
    .clk(CLK), .D(multiplexer_13_out), .Q(\屏蔽字 [3]), .Qn(d_ff_7_qn), .en(or_11_out));  // open: preset, reset
  Comparator #(.width(5), .mode("unsigned")) comparator_6 (
    .a(IR[25:21]), .b({5{1'b0}}), .eq(comparator_6_eq));  // open: gt, lt
  Comparator #(.width(5), .mode("unsigned")) comparator_7 (
    .a(IR[25:21]), .b(5'b00100), .eq(comparator_7_eq));  // open: gt, lt
  MIPS_Regifile mips_regifile_1 (
    .Din(RDin), .Clk(CLK), .R1(Reg1), .R2(MDin), .WE(RegWrite), .W_num(multiplexer_14_out),
    .R1_num(multiplexer_8_out), .R2_num(multiplexer_9_out));
  and and_7 (and_7_out, 1'b0, d_ff_4_qn);
  and and_8 (and_8_out, ir1_t_t, d_ff_5_qn);
  and and_9 (and_9_out, ir2_t_t, d_ff_6_qn);
  and and_10 (and_10_out, ir3_t_t, d_ff_7_qn);
  not not_2 (not_2_out, d_ff_8_q);
  D_Flip_Flop d_ff_8 (.clk(CLK), .D(1'b1), .Q(d_ff_8_q));  // open: Qn, preset, en, reset
  and and_11 (mfc0, Ret, comparator_6_eq);
  and and_12 (mtc0, Ret, comparator_7_eq);
  Multiplexer #(.width(32), .enable("false")) multiplexer_15 (
    .in0(MDin), .in1(imm32), .out(multiplexer_15_out), .sel(\单周期硬布线控制器_1_alu_src ));
  Multiplexer #(.enable("false")) multiplexer_16 (.in0(1'b0), .in1(1'b1), .out(multiplexer_16_out), .sel(or_13_out));
  or or_13 (or_13_out, not_2_out, eret, mfc0);
  Comparator #(.width(5), .mode("unsigned")) comparator_8 (
    .a(IR[25:21]), .b(5'b10000), .eq(comparator_8_eq));  // open: gt, lt
  Priority_Encoder #(.select(2)) priority_encoder_2 (
    .in0(and_7_out), .in1(and_8_out), .in2(and_9_out), .in3(and_10_out), .out(priority_encoder_2_out),
    .gs(priority_encoder_2_gs));  // open: en_out, en_in
  D_Flip_Flop IE (.clk(CLK), .D(multiplexer_16_out), .Q(IE_q), .en(or_14_out));  // open: Qn, preset, reset
  or or_14 (or_14_out, not_2_out, eret, mtc0, mfc0, IR_CPU);
  and and_13 (eret, Ret, comparator_8_eq);
  MIPS_ALU mips_alu_1 (
    .X(Reg1), .Y(multiplexer_15_out), .AluOP(\单周期硬布线控制器_1_alu_op ), .Equal(equal),
    .Result(mips_alu_1_result), .shamt(IR[10:6]));  // open: Result_2
  Multiplexer #(.select(2), .width(32), .enable("false")) multiplexer_17 (
    .in0({32{1'b0}}), .in1(32'h30ac), .in2(32'h3158), .in3(32'h3204), .out(irPC), .sel(priority_encoder_2_out));
  and and_14 (IR_CPU, priority_encoder_2_gs, IE_q);
  Comparator #(.width(32)) comparator_9 (.a(Reg1), .b({32{1'b0}}), .gt(comparator_9_gt));  // open: eq, lt
  and and_15 (and_15_out, Beq, equal);
  and and_16 (and_16_out, Bne, ~equal);  // AND_Gate
  Register #(.width(2)) register_1 (.D(priority_encoder_2_out), .Q(cur_index));  // open: en, clk, clr
  and and_17 (and_17_out, comparator_9_gt, Bgtz);
  or or_15 (Branch, and_17_out, or_16_out);
  or or_16 (or_16_out, and_15_out, and_16_out);
  RAM #(.addrWidth(10), .dataWidth(32), .bus("separate")) ram_1 (
    .addr(mips_alu_1_result[11:2]), .din(MDin), .data(MemOut), .str(MemWrite), .clk(CLK), .clr(RST));  // open: sel, ld
  Multiplexer #(.width(32), .enable("false")) multiplexer_18 (
    .in0(mips_alu_1_result), .in1(MemOut), .out(RDin), .sel(MemToReg));
  Adder #(.width(32)) adder_2 (.a(EPCS), .b(32'h4), .out(adder_2_out));  // open: cin, cout
  Multiplexer #(.select(2), .width(32), .enable("false")) multiplexer_19 (
    .in1(adder_2_out), .in2(subtractor_1_out), .out(multiplexer_19_out), .sel({mtc0, mfc0}));  // open: in0, in3
  Subtractor #(.width(32)) subtractor_1 (.a(EPCS), .b(32'h4), .out(subtractor_1_out));  // open: bin, bout
  Adder #(.width(32)) adder_3 (.a(INMS), .b(32'h4), .out(adder_3_out));  // open: cin, cout
  Multiplexer #(.select(2), .width(32), .enable("false")) multiplexer_20 (
    .in1(adder_3_out), .in2(subtractor_2_out), .out(multiplexer_20_out), .sel({mtc0, IR_CPU}));  // open: in0, in3
  Subtractor #(.width(32)) subtractor_2 (.a(INMS), .b(32'h4), .out(subtractor_2_out));  // open: bin, bout
  Register #(.width(32)) u_EPCS (.D(multiplexer_19_out), .en(or_17_out), .Q(EPCS), .clk(CLK));  // open: clr
  or or_17 (or_17_out, mtc0, mfc0);
  Register #(.width(32)) u_INMS (.D(multiplexer_20_out), .en(or_18_out), .Q(INMS), .clk(CLK));  // open: clr
  or or_18 (or_18_out, mtc0, IR_CPU);
  Multiplexer #(.width(32), .enable("false")) multiplexer_21 (
    .in0({32{1'b0}}), .in1(Reg1), .out(multiplexer_21_out), .sel(syscall));
  Multiplexer #(.width(32), .enable("false")) multiplexer_22 (
    .in0({32{1'b0}}), .in1(Reg1), .out(multiplexer_22_out), .sel(syscall));
  Comparator #(.width(32), .mode("unsigned")) comparator_10 (
    .a(multiplexer_21_out), .b(32'h22), .eq(comparator_10_eq));  // open: gt, lt
  Comparator #(.width(32), .mode("unsigned")) comparator_11 (
    .a(multiplexer_22_out), .b(32'ha), .eq(comparator_11_eq));  // open: gt, lt
  Counter #(.width(16), .max('hffff)) counter_1 (
    .count(not_3_out), .Q(\总周期数 ), .clk(CLK), .clr(RST));  // open: load, D, carry
  not not_3 (not_3_out, Halt);
  Register #(.width(32)) register_2 (.D(multiplexer_23_out), .en(comparator_10_eq), .Q(LedData), .clk(CLK), .clr(RST));
  Multiplexer #(.width(32), .enable("false")) multiplexer_23 (
    .in0({32{1'b0}}), .in1(MDin), .out(multiplexer_23_out), .sel(comparator_10_eq));
  Multiplexer #(.enable("false")) multiplexer_24 (.in0(1'b0), .in1(1'b1), .out(Halt), .sel(comparator_11_eq));
  RAM #(.addrWidth(10), .dataWidth(32), .bus("separate")) ram_2 (
    .addr(EPCS[11:2]), .din(nextPC), .data(EPC), .str(IR_CPU), .clk(CLK), .clr(RST));  // open: sel, ld
  RAM #(.addrWidth(10), .dataWidth(32), .bus("separate")) ram_3 (
    .addr(INMS[11:2]), .din({{28{1'b0}}, \屏蔽字 }), .data(INM), .str(IR_CPU), .clk(CLK), .clr(RST));  // open: sel, ld

  // Other names for the same wires on the sheet: imm26[25:0] = IR[25:0]; rs[4:0] = IR[25:21]; Reg2[31:0] = MDin

  // Notes on the sheet:
  //   中断源
  //   中断等待指示
  //   总复位信号应将除ROM以外所有存储组件全部清零
  //   中断按键电路
  //   数码管输出
  //   Reset 
  //   Reset 
  //   Reset 
  //   数码管输出应该用寄存器锁存，否则显示数据只能一闪而过
  //   指令存储器
  //   指令字
  //   contents of rom_1 (hex, n*v repeats v):
  //   201d07d0 20100001 109fc0 139fc3 8021 2012000c 24160008 26100001 3210000f 20080008 20090001 139900
  //   2709825 132020 20020022 c 1094022 1500fff9 22100001 2018000f 2188024 108700 20080008 20090001 139902
  //   2709825 132021 20020022 c 1094022 1500fff9 108702 2c9b022 12c00001 8000c07 4020 1084027 84400
  //   3508ffff 82021 20020022 c 8000c01 afa20000 23bd0004 afa40000 23bd0004 afb00000 23bd0004 afb30000
  //   23bd0004 afb40000 23bd0004 afb50000 23bd0004 afb60000 23bd0004 40000000 20160001 20140003 20150001
  //   168020 108100 2149825 132020 20020022 c 1600fffa 295a022 1680fff7 40800000 23bdfffc 8fb60000
  //   23bdfffc 8fb50000 23bdfffc 8fb40000 23bdfffc 8fb30000 23bdfffc 8fb00000 23bdfffc 8fa40000 23bdfffc
  //   8fa20000 42000018 afa20000 23bd0004 afa40000 23bd0004 afb00000 23bd0004 afb30000 23bd0004 afb40000
  //   23bd0004 afb50000 23bd0004 afb60000 23bd0004 40000000 20160002 20140003 20150001 168020 108100
  //   2149825 132020 20020022 c 1600fffa 295a022 1680fff7 40800000 23bdfffc 8fb60000 23bdfffc 8fb50000
  //   23bdfffc 8fb40000 23bdfffc 8fb30000 23bdfffc 8fb00000 23bdfffc 8fa40000 23bdfffc 8fa20000 42000018
  //   afa20000 23bd0004 afa40000 23bd0004 afb00000 23bd0004 afb30000 23bd0004 afb40000 23bd0004 afb50000
  //   23bd0004 afb60000 23bd0004 40000000 20160003 20140003 20150001 168020 108100 2149825 132020 20020022
  //   c 1600fffa 295a022 1680fff7 40800000 23bdfffc 8fb60000 23bdfffc 8fb50000 23bdfffc 8fb40000 23bdfffc
  //   8fb30000 23bdfffc 8fb00000 23bdfffc 8fa40000 23bdfffc 8fa20000 42000018
  //   OP
  //   Func
  //   rs
  //   rt
  //   rd
  //   shmat
  //   Imm
  //   JMP
  //   JR
  //   Syscall
  //   主数据通路
  //   Beq
  //   Bgtz
  //   Bne
  //   MemToReg
  //   MemWrite
  //   AluOP
  //   AluSrcB
  //   RegWrite
  //   JAL
  //   RegDst
  //   中断仲裁与中断识别
  //   为方便自动评测，需要输出PC，IR，寄存器堆写如数据RDin
  //   RAM写使能MemWrite、RAM写入数据MDin等信号
  //   EPC硬件堆栈
  //   屏蔽字硬件堆栈
  //   LED显示电路
  //   停机信号
  //   时钟周期计数器
endmodule

module \重定向流水线_单级中断  (
  output RegWrite,
  output MemWrite,
  output [31:0] IF_PC,
  output [31:0] ID_PC,
  output [31:0] EX_PC,
  output [31:0] M_PC,
  output [31:0] WB_PC,
  output [31:0] RDin,
  output [31:0] MDin,
  output [31:0] LedData
);

  wire AluSrcB_3, and_1_out, and_2_out, and_3_out, and_7_out, and_8_out, and_11_out, and_12_out, and_13_out,
       Beq_3, Beq_4, Bgtz_3, Bgtz_4, Bne_3, Bne_4, Branch, CLK, comparator_1_eq, comparator_3_eq,
       comparator_4_eq, comparator_5_gt, d_ff_1_q, d_ff_2_q, d_ff_3_q, d_ff_4_q, decoder_1_out1,
       decoder_1_out2, decoder_1_out3, equal, eret, Go, Halt, IE_q, INS1, INS1_3, INS2, INS2_3, INS3, INS3_3,
       IR1, ir1_t, IR2, ir2_t, IR3, ir3_t, IR_CPU, j_rst, jal_3, jal_5, jmp_3, jmp_4, jr_3, jr_4, load_2,
       load_3, MemToReg_5, not_1_out, not_2_out, not_3_out, or_4_out, or_5_out, or_6_out, or_7_out, or_8_out,
       or_9_out, or_10_out, or_12_out, priority_encoder_1_gs, RegDst_3, RegDst_4, RegDst_5, RegWrite_3,
       RegWrite_4, Ret, RST, rst1, rst2, rst3, sel1, sel2, sel3, sel4, stall, syscall_2, syscall_3,
       syscall_5, W1, W2, W3;
  wire [1:0] cur_index, priority_encoder_1_out;
  wire [3:0] AluOp_3;
  wire [4:0] id_ex_1_shammto, multiplexer_5_out, ra2, ra3, rb2, rb3, rd3, rd4, rd5, rt3, rt4, rt5, rw_3,
       rw_4, rw_5;
  wire [15:0] \LoadUse次数 , \总周期数 , \插入气泡数 , \无条件分支数 , \条件分支成功数 ;
  wire [16:0] mem_wb_1_controlo, \单周期硬布线控制器_1_jr ;
  wire [16:5] ex_mem_1_controlo, id_ex_1_controlo;
  wire [25:0] Imm26_3;
  wire [31:0] alur_4, EPC, EX_IR, ex_mem_1_pco, id_ex_1_reg1o, id_ex_1_reg2o, ID_IR, if_id_1_pc_4o, IF_IR,
       imm, Imm32, irPC, MEM_IR, mem_wb_1_aluo, mem_wb_1_dmouto, mem_wb_1_pco, mips_alu_1_result,
       multiplexer_6_out, multiplexer_9_out, multiplexer_11_out, multiplexer_14_out, multiplexer_16_out,
       multiplexer_17_out, multiplexer_18_out, nextPC, PC_4, PC_4_3, ram_1_data, Reg1, Reg1_3, Reg1_4,
       Reg1_5, Reg2, Reg2_3, WB_IR;

  Button \u_总复位  (.out(RST));
  Button _1 (.out(IR1));
  Button _2 (.out(IR2));
  Button _3 (.out(IR3));
  // Probe on \总周期数 
  // Probe on \总周期数 
  Button \u_继续运行  (.out(Go));
  LED led_1 (.in(W1));
  LED led_2 (.in(W2));
  LED led_3 (.in(W3));
  Hex_Digit_Display hex_digit_display_1 (.value(LedData[31:28]));  // open: dp
  // Probe on IF_PC[19:0]
  // Mips_Probe mips_probe_1: pin names not known; wires that end beside it: IF_IR
  PCout pcout_1 (
    .PC_4(PC_4), .Imm26(Imm26_3), .Imm32(imm), .Reg1(Reg1_3), .JMP(jmp_3), .JR(jr_3), .JAL(jal_5),
    .Branch(Branch), .PC_4_3(PC_4_3));  // open: out_10
  Hex_Digit_Display hex_digit_display_2 (.value(LedData[23:20]));  // open: dp
  Hex_Digit_Display hex_digit_display_3 (.value(LedData[27:24]));  // open: dp
  // Probe on ID_PC[19:0]
  // Mips_Probe mips_probe_2: pin names not known; wires that end beside it: ID_IR
  or or_1 (W1, ir1_t, d_ff_1_q);
  or or_2 (W2, ir2_t, d_ff_2_q);
  or or_3 (W3, ir3_t, d_ff_3_q);
  Hex_Digit_Display hex_digit_display_4 (.value(LedData[15:12]));  // open: dp
  Hex_Digit_Display hex_digit_display_5 (.value(LedData[19:16]));  // open: dp
  D_Flip_Flop d_ff_1 (.clk(IR1), .D(1'b1), .Q(d_ff_1_q), .reset(ir1_t));  // open: Qn, preset, en
  D_Flip_Flop d_ff_2 (.clk(IR2), .D(1'b1), .Q(d_ff_2_q), .reset(ir2_t));  // open: Qn, preset, en
  D_Flip_Flop d_ff_3 (.clk(IR3), .D(1'b1), .Q(d_ff_3_q), .reset(ir3_t));  // open: Qn, preset, en
  Decoder #(.select(2), .enable("false")) decoder_1 (
    .out1(decoder_1_out1), .out2(decoder_1_out2), .out3(decoder_1_out3), .sel(cur_index));  // open: out0
  Hex_Digit_Display hex_digit_display_6 (.value(LedData[11:8]));  // open: dp
  Hex_Digit_Display hex_digit_display_7 (.value(LedData[7:4]));  // open: dp
  Clock clock_1 (.out(CLK));
  // Probe on EX_PC[19:0]
  // Mips_Probe mips_probe_3: pin names not known; wires that end beside it: EX_IR
  Multiplexer #(.width(32), .enable("false")) multiplexer_1 ();  // open: in0, in1, out, sel
  not not_1 (not_1_out, or_4_out);
  or or_4 (or_4_out, Halt, stall);
  or or_5 (or_5_out, d_ff_1_q, ir1_t);
  or or_6 (or_6_out, d_ff_2_q, ir2_t);
  or or_7 (or_7_out, d_ff_3_q, ir3_t);
  Hex_Digit_Display hex_digit_display_8 (.value(LedData[3:0]));  // open: dp
  Register #(.width(32)) PC (.en(not_1_out), .Q(IF_PC), .clk(CLK), .clr(RST));  // open: D
  Adder #(.width(32)) adder_1 (.a(IF_PC), .b(32'h4), .out(PC_4));  // open: cin, cout
  and and_1 (and_1_out, or_5_out, ~rst1);  // AND_Gate
  and and_2 (and_2_out, or_6_out, ~rst2);  // AND_Gate
  and and_3 (and_3_out, or_7_out, ~rst3);  // AND_Gate
  and and_4 (rst1, eret, decoder_1_out1);
  and and_5 (rst2, decoder_1_out2, eret);
  and and_6 (rst3, decoder_1_out3, eret);
  // Probe on \总周期数 
  // Probe on M_PC[19:0]
  // Mips_Probe mips_probe_4: pin names not known; wires that end beside it: MEM_IR
  D_Flip_Flop u_IR1 (.clk(CLK), .D(and_1_out), .Q(ir1_t));  // open: Qn, preset, en, reset
  D_Flip_Flop u_IR2 (.clk(CLK), .D(and_2_out), .Q(ir2_t));  // open: Qn, preset, en, reset
  D_Flip_Flop u_IR3 (.clk(CLK), .D(and_3_out), .Q(ir3_t));  // open: Qn, preset, en, reset
  // Probe on \总周期数 
  // Probe on \无条件分支数 
  // Probe on \条件分支成功数 
  // Probe on \插入气泡数 
  // Probe on \LoadUse次数 
  ROM #(.addrWidth(10), .dataWidth(32)) rom_1 (.addr(IF_PC[11:2]), .data(IF_IR));  // open: sel
  or or_8 (or_8_out, j_rst, RST);
  // Probe on IF_PC[11:0]
  // Probe on WB_PC[19:0]
  // Mips_Probe mips_probe_5: pin names not known; wires that end beside it: WB_IR
  IF_ID if_id_1 (
    .CLK(CLK), .RST(or_8_out), .Halt(or_9_out), .PC_4(PC_4), .IR(IF_IR), .PC_4O(if_id_1_pc_4o), .IRO(ID_IR),
    .IF_PC(IF_PC), .IF_PCO(ID_PC));  // open: jump_att, hit, pc_att, hit_pos, pc_attO, hit_posO, jump_attO, hitO, PC, PCO
  or or_9 (or_9_out, stall, Halt);
  // Probe on ID_PC[11:0]
  // Probe on EX_PC[11:0]
  not not_2 (not_2_out, eret);
  Register #(.width(32)) u_EPC (.D(nextPC), .en(and_7_out), .Q(EPC), .clk(CLK));  // open: clr
  and and_7 (and_7_out, not_2_out, IR_CPU);
  // Probe on M_PC[11:0]
  \单周期硬布线控制器  \u_单周期硬布线控制器_1  (
    .Func(ID_IR[5:0]), .OP(ID_IR[31:26]), .ALU_OP(\单周期硬布线控制器_1_jr [10:7]), .MemToReg(\单周期硬布线控制器_1_jr [5]),
    .MemWrite(\单周期硬布线控制器_1_jr [6]), .ALU_SRC(\单周期硬布线控制器_1_jr [11]), .RegWrite(\单周期硬布线控制器_1_jr [12]),
    .SysCALL(syscall_2), .SignedExt(\单周期硬布线控制器_1_jr [16]), .RegDst(\单周期硬布线控制器_1_jr [14]),
    .JR(\单周期硬布线控制器_1_jr [0]), .JMP(\单周期硬布线控制器_1_jr [1]), .Beq(\单周期硬布线控制器_1_jr [2]),
    .JAL(\单周期硬布线控制器_1_jr [13]), .Bne(\单周期硬布线控制器_1_jr [4]), .INS1(INS1), .INS2(INS2), .INS3(INS3),
    .Bgtz(\单周期硬布线控制器_1_jr [3]), .RET(Ret));
  Priority_Encoder #(.select(2)) priority_encoder_1 (
    .in0(1'b0), .in1(ir1_t), .in2(ir2_t), .in3(ir3_t), .out(priority_encoder_1_out),
    .gs(priority_encoder_1_gs));  // open: en_out, en_in
  D_Flip_Flop IE (.clk(CLK), .D(1'b1), .Q(IE_q), .preset(eret), .en(not_3_out), .reset(and_8_out));  // open: Qn
  not not_3 (not_3_out, IE_q);
  and and_8 (and_8_out, not_2_out, d_ff_4_q);
  D_Flip_Flop d_ff_4 (.clk(CLK), .D(and_7_out), .Q(d_ff_4_q), .en(IR_CPU));  // open: Qn, preset, reset
  // Probe on WB_PC[11:0]
  Comparator #(.width(5), .mode("unsigned")) comparator_1 (
    .a(ra2), .b(5'b10000), .eq(comparator_1_eq));  // open: gt, lt
  Multiplexer #(.width(5), .enable("false")) multiplexer_2 (
    .in0(ID_IR[25:21]), .in1(5'b00010), .out(ra2), .sel(syscall_2));
  Multiplexer #(.width(5), .enable("false")) multiplexer_3 (
    .in0(ID_IR[20:16]), .in1(5'b00100), .out(rb2), .sel(syscall_2));
  Multiplexer #(.width(5), .enable("false")) multiplexer_4 (
    .in0(multiplexer_5_out), .in1({5{1'b1}}), .out(rw_5), .sel(jal_5));
  Multiplexer #(.width(5), .enable("false")) multiplexer_5 (
    .in0(rt5), .in1(rd5), .out(multiplexer_5_out), .sel(RegDst_5));
  assign Imm32 = {{16{ID_IR[15]}}, ID_IR[15:0]};  // Bit_Extender bit_extender_1
  Multiplexer #(.width(32), .enable("false")) multiplexer_6 (
    .in0(mem_wb_1_aluo), .in1(mem_wb_1_dmouto), .out(multiplexer_6_out), .sel(MemToReg_5));
  and and_9 (IR_CPU, priority_encoder_1_gs, IE_q);
  and and_10 (eret, Ret, comparator_1_eq);
  Comparator #(.width(6), .mode("unsigned")) comparator_2 (
    .a(ID_IR[31:26]), .b(6'b100011), .eq(load_2));  // open: gt, lt
  Multiplexer #(.width(32), .enable("false")) multiplexer_7 (
    .in0(multiplexer_6_out), .in1(mem_wb_1_pco), .out(RDin), .sel(jal_5));
  Multiplexer #(.select(2), .width(32), .enable("false")) multiplexer_8 (
    .in0({32{1'b0}}), .in1(32'h30ac), .in2(32'h3150), .in3(32'h31f4), .out(irPC), .sel(priority_encoder_1_out));
  Register #(.width(2)) register_1 (.D(priority_encoder_1_out), .Q(cur_index), .clk(and_7_out));  // open: en, clr
  MIPS_Regifile mips_regifile_1 (
    .Din(RDin), .Clk(CLK), .R1(Reg1), .R2(Reg2), .WE(RegWrite), .W_num(rw_5), .R1_num(ra2), .R2_num(rb2));
  ID_EX id_ex_1 (
    .CLK(CLK), .rd(ID_IR[15:11]), .rt(ID_IR[20:16]), .reg1(Reg1), .reg2(Reg2), .Imm(Imm32),
    .PC_4(if_id_1_pc_4o), .Control({\单周期硬布线控制器_1_jr [16], syscall_2, \单周期硬布线控制器_1_jr [14:0]}),
    .RST(or_10_out), .Halt(Halt), .Shammt(ID_IR[10:6]), .imm26(ID_IR[25:0]), .ra2(ra2), .rt2(rb2),
    .load_2(load_2), .INS1_2(INS1), .INS1_3(INS2), .INS1_4(INS3), .imm26O(Imm26_3), .rdO(rd3), .rtO(rt3),
    .ControlO({id_ex_1_controlo[16], syscall_3, RegDst_3, jal_3, RegWrite_3, AluSrcB_3, AluOp_3, id_ex_1_controlo[6:5], Bne_3, Bgtz_3, Beq_3, jmp_3, jr_3}),
    .PCO(PC_4_3), .reg1O(id_ex_1_reg1o), .reg2O(id_ex_1_reg2o), .ImmO(imm), .ShammtO(id_ex_1_shammto),
    .ra2O(ra3), .rd2O(rb3), .loadO(load_3), .INS3_O(INS3_3), .INS2_O(INS2_3), .INS1_O(INS1_3), .IR(ID_IR),
    .IR_2(EX_IR), .IR_PC(ID_PC), .IR_PCO(EX_PC));  // open: jump_att, hit, pc_att, hit_pos, pc_attO, hit_posO, jump_attO, hitO, PCO_2, PC
  or or_10 (or_10_out, j_rst, RST, stall);
  Multiplexer #(.width(32), .enable("false")) multiplexer_9 (
    .in0(id_ex_1_reg1o), .in1(RDin), .out(multiplexer_9_out), .sel(sel3));
  Multiplexer #(.width(32), .enable("false")) multiplexer_10 (
    .in0(multiplexer_9_out), .in1(alur_4), .out(Reg1_3), .sel(sel1));
  Multiplexer #(.width(32), .enable("false")) multiplexer_11 (
    .in0(id_ex_1_reg2o), .in1(RDin), .out(multiplexer_11_out), .sel(sel4));
  Multiplexer #(.width(32), .enable("false")) multiplexer_12 (
    .in0(multiplexer_11_out), .in1(alur_4), .out(Reg2_3), .sel(sel2));
  Multiplexer #(.width(5), .enable("false")) multiplexer_13 (.in0(rt3), .in1(rd3), .out(rw_3), .sel(RegDst_3));
  Multiplexer #(.width(32), .enable("false")) multiplexer_14 (
    .in0(Reg2_3), .in1(imm), .out(multiplexer_14_out), .sel(AluSrcB_3));
  EX_MEM ex_mem_1 (
    .CLK(CLK), .RST(RST), .Halt(Halt),
    .Control({id_ex_1_controlo[16], syscall_3, RegDst_3, jal_3, RegWrite_3, AluSrcB_3, AluOp_3, id_ex_1_controlo[6:5], Bne_3, Bgtz_3, Beq_3, jmp_3, jr_3}),
    .PC(PC_4_3), .reg2(Reg2_3), .Alu(mips_alu_1_result), .rd(rd3), .rt(rt3), .rdO(rd4), .rtO(rt4),
    .ControlO({ex_mem_1_controlo[16:15], RegDst_4, ex_mem_1_controlo[13], RegWrite_4, ex_mem_1_controlo[11:7], MemWrite, ex_mem_1_controlo[5], Bne_4, Bgtz_4, Beq_4, jmp_4, jr_4}),
    .PCO(ex_mem_1_pco), .reg2O(MDin), .AluO(alur_4), .IR(EX_IR), .IR_2(MEM_IR), .Reg1_3(Reg1_3),
    .Reg1_O(Reg1_4), .EX_PC(EX_PC), .EX_PCO(M_PC));  // open: Reg2_3, Reg2_O
  MIPS_ALU mips_alu_1 (
    .X(Reg1_3), .Y(multiplexer_14_out), .AluOP(AluOp_3), .Equal(equal), .Result(mips_alu_1_result),
    .shamt(id_ex_1_shammto));  // open: Result_2
  Multiplexer #(.width(5), .enable("false")) multiplexer_15 (.in0(rt4), .in1(rd4), .out(rw_4), .sel(RegDst_4));
  RAM #(.addrWidth(10), .dataWidth(32), .bus("separate")) ram_1 (
    .addr(alur_4[11:2]), .din(MDin), .data(ram_1_data), .str(MemWrite), .clk(CLK), .clr(RST));  // open: sel, ld
  MEM_WB mem_wb_1 (
    .CLK(CLK), .RST(RST), .Halt(Halt),
    .Control({ex_mem_1_controlo[16:15], RegDst_4, ex_mem_1_controlo[13], RegWrite_4, ex_mem_1_controlo[11:7], MemWrite, ex_mem_1_controlo[5], Bne_4, Bgtz_4, Beq_4, jmp_4, jr_4}),
    .Alu(alur_4), .PC(ex_mem_1_pco), .DMout(ram_1_data), .rd(rd4), .rt(rt4), .rdO(rd5), .rtO(rt5),
    .ControlO({mem_wb_1_controlo[16], syscall_5, RegDst_5, jal_5, RegWrite, mem_wb_1_controlo[11:6], MemToReg_5, mem_wb_1_controlo[4:0]}),
    .PCO(mem_wb_1_pco), .DMoutO(mem_wb_1_dmouto), .AluO(mem_wb_1_aluo), .IR_2(WB_IR), .IR(MEM_IR),
    .Reg1_3(Reg1_4), .Reg1_O(Reg1_5), .MEM_PC(M_PC), .MEM_PCO(WB_PC));  // open: Reg2_3, Reg2_O
  Multiplexer #(.width(32), .enable("false")) multiplexer_16 (
    .in0({32{1'b0}}), .in1(Reg1_3), .out(multiplexer_16_out), .sel(syscall_3));
  Multiplexer #(.width(32), .enable("false")) multiplexer_17 (
    .in0({32{1'b0}}), .in1(Reg1_5), .out(multiplexer_17_out), .sel(syscall_5));
  Comparator #(.width(32), .mode("unsigned")) comparator_3 (
    .a(multiplexer_16_out), .b(32'h22), .eq(comparator_3_eq));  // open: gt, lt
  Comparator #(.width(32), .mode("unsigned")) comparator_4 (
    .a(multiplexer_17_out), .b(32'ha), .eq(comparator_4_eq));  // open: gt, lt
  Comparator #(.width(32)) comparator_5 (.a(Reg1_3), .b({32{1'b0}}), .gt(comparator_5_gt));  // open: eq, lt
  and and_11 (and_11_out, Beq_3, equal);
  and and_12 (and_12_out, Bne_3, ~equal);  // AND_Gate
  \分支相关  \u_分支相关_1  (.j(jmp_3), .jr(jr_3), .jal(jal_3), .branch(Branch), .j_rst(j_rst));
  \重定向  \u_重定向_1  (
    .INS1(INS1_3), .INS2(INS2_3), .INS3(INS3_3), .RegWrite4(RegWrite_4), .RegWrite5(RegWrite), .ra3(ra3),
    .rb3(rb3), .rw4(rw_4), .rw5(rw_5), .sel1(sel1), .sel2(sel2), .sel3(sel3), .sel4(sel4));
  Multiplexer #(.width(32), .enable("false")) multiplexer_18 (
    .in0({32{1'b0}}), .in1(Reg2_3), .out(multiplexer_18_out), .sel(comparator_3_eq));
  Multiplexer #(.enable("false")) multiplexer_19 (.in0(1'b0), .in1(1'b1), .out(Halt), .sel(comparator_4_eq));
  and and_13 (and_13_out, comparator_5_gt, Bgtz_3);
  or or_11 (Branch, and_13_out, or_12_out);
  or or_12 (or_12_out, and_11_out, and_12_out);
  Register #(.width(32)) register_2 (.D(multiplexer_18_out), .en(comparator_3_eq), .Q(LedData), .clk(CLK), .clr(RST));
  Load_Use load_use_1 (
    .INS1(INS1), .stall(stall), .INS2(INS2), .INS3(INS3), .RegDin3(load_3), .ra(ra2), .rb(rb2), .rw3(rw_3));
  counter counter_1 (
    .rst(RST), .clk(CLK), .jmp(jmp_3), .jr(jr_3), .branch(Branch), .halt(Halt), .\总周期数 (\总周期数 ),
    .\条件分支成功数 (\条件分支成功数 ), .\无条件分支数 (\无条件分支数 ), .pop(stall), .\气泡数 (\LoadUse次数 ));

  // Other names for the same wires on the sheet: MemWrite_4 = MemWrite; RegWrite_5 = RegWrite;
  //   Imm26[25:0] = ID_IR[25:0]; rd2[4:0] = ID_IR[15:11]; rt2[4:0] = ID_IR[20:16]; op2[5:0] = ID_IR[31:26];
  //   MEM_PC[31:0] = M_PC; RegD_5[31:0] = RDin

  // Notes on the sheet:
  //   中断源
  //   时空图监测，可删除
  //   中断等待指示
  //   数码管输出
  //   Reset 
  //   Reset 
  //   Reset 
  //   指令存储器
  //   contents of rom_1 (hex, n*v repeats v):
  //   20110001 8000c05 20110001 20120002 20130003 8000c09 20110001 20120002 20130003 8000c0d 20110001
  //   20120002 20130003 8000c11 20110001 20120002 20130003 c000cb8 20100001 20110001 118fc0 112020
  //   20020022 c 118882 12200001 8000c15 112020 20020022 c 20110001 118880 112020 20020022 c 12200001
  //   8000c1f 20110001 118fc0 112020 20020022 c 1188c3 112020 20020022 c 118903 112020 20020022 c 118903
  //   112020 20020022 c 118903 112020 20020022 c 118903 112020 20020022 c 118903 112020 20020022 c 118903
  //   112020 20020022 c 118903 112020 20020022 c 20100001 109fc0 139fc3 8021 2012000c 24160003 26100001
  //   3210000f 20080008 20090001 139900 2709825 132020 20020022 c 1094022 1500fff9 22100001 2018000f
  //   2188024 108700 20080008 20090001 139902 2709825 132021 20020022 c 1094022 1500fff9 108702 2c9b022
  //   12c00001 8000c50 4020 1084027 84400 3508ffff 82021 20020022 c 2010ffff 20110000 ae300000 22100001
  //   22310004 ae300000 22100001 22310004 ae300000 22100001 22310004 ae300000 22100001 22310004 ae300000
  //   22100001 22310004 ae300000 22100001 22310004 ae300000 22100001 22310004 ae300000 22100001 22310004
  //   ae300000 22100001 22310004 ae300000 22100001 22310004 ae300000 22100001 22310004 ae300000 22100001
  //   22310004 ae300000 22100001 22310004 ae300000 22100001 22310004 ae300000 22100001 22310004 ae300000
  //   22100001 22310004 22100001 8020 2011003c 8e130000 8e340000 274402a 11000002 ae330000 ae140000
  //   2231fffc 1611fff8 102020 20020022 c 22100004 2011003c 1611fff2 20020032 c 20100000 22100001 102020
  //   20020022 c 22100002 102020 20020022 c 22100003 102020 20020022 c 22100004 102020 20020022 c 22100005
  //   102020 20020022 c 22100006 102020 20020022 c 22100007 102020 20020022 c 22100008 102020 20020022
  //   20020022 c 3e00008
  //   JMP
  //   JR
  //   OP
  //   Func
  //   rs
  //   rt
  //   rd
  //   shmat
  //   Imm
  //   流水调试日志用
  //   Beq
  //   Bgtz
  //   Bne
  //   MemToReg
  //   MemWrite
  //   AluOP
  //   AluSrcB
  //   RegWrite
  //   JAL
  //   RegDst
  //   Syscall
  //   为方便自动评测，需要输出流水线各段保存的PC值，注意是PC不是PC+4，另外ID段寄存器写入信息，Mem段内存写入信息也要输出
endmodule

module \动态分支预测  (
  output RegWrite,
  output MemWrite,
  output [31:0] IF_PC,
  output [31:0] ID_PC,
  output [31:0] EX_PC,
  output [31:0] M_PC,
  output [31:0] WB_PC,
  output [31:0] RDin,
  output [31:0] MDin,
  output [31:0] LedData
);

  wire AluSrcB_3, att_fail, att_suc, Beq_3, Beq_4, Bgtz_3, Bgtz_4, Bne_3, Bne_4, Branch, CLK,
       comparator_1_eq, comparator_2_eq, comparator_3_eq, equal, Go, Halt, hit, hit_2, hit_3, INS1, INS1_3,
       INS2, INS2_3, INS3, INS3_3, IR1, IR2, IR3, j_rst, jal_3, jal_5, jb_3, jmp_3, jmp_4, jr_3, jr_4,
       jump_att, jump_att_2, jump_att_3, jump_suc, load_2, load_3, MemToReg_5, not_1_out, or_1_out, or_2_out,
       or_3_out, or_4_out, or_5_out, RegDst_3, RegDst_4, RegDst_5, RegWrite_3, RegWrite_4, RST, sel1, sel2,
       sel3, sel4, stall, syscall_2, syscall_3, syscall_5, W1, W2, W3;
  wire [2:0] hit_pos, hit_pos_2, hit_pos_3;
  wire [3:0] AluOp_3;
  wire [4:0] id_ex_1_shammto, multiplexer_8_out, ra2, ra3, rb2, rb3, rd3, rd4, rd5, rt3, rt4, rt5, rw_3,
       rw_4, rw_5;
  wire [15:0] \LoadUse次数 , \总周期数 , \插入气泡数 , \无条件分支数 , \条件分支成功数 ;
  wire [16:0] mem_wb_1_controlo, \单周期硬布线控制器_1_jr ;
  wire [16:5] ex_mem_1_controlo, id_ex_1_controlo;
  wire [25:0] Imm26_3;
  wire [31:0] alur_4, dest_addr, EX_IR, ex_mem_1_pco, id_ex_1_reg1o, id_ex_1_reg2o, ID_IR, if_id_1_pc_4o,
       IF_IR, imm, Imm32, MEM_IR, mem_wb_1_aluo, mem_wb_1_dmouto, mem_wb_1_pco, mips_alu_1_result,
       multiplexer_1_out, multiplexer_2_out, multiplexer_3_out, multiplexer_9_out, multiplexer_11_out,
       multiplexer_13_out, multiplexer_16_out, PC_2, PC_3, PC_4, PC_4_3, pc_att, pc_att_2, pc_att_3,
       ram_1_data, Reg1, Reg1_3, Reg1_4, Reg1_5, Reg2, Reg2_3, WB_IR, \分支预测pcout_1_pcout ;

  Button \u_总复位  (.out(RST));
  Button _1 (.out(IR1));
  Button _2 (.out(IR2));
  Button _3 (.out(IR3));
  // Probe on \总周期数 
  // Probe on \总周期数 
  Button \u_继续运行  (.out(Go));
  LED led_1 (.in(W1));
  LED led_2 (.in(W2));
  LED led_3 (.in(W3));
  Hex_Digit_Display hex_digit_display_1 (.value(LedData[31:28]));  // open: dp
  // Probe on IF_PC[19:0]
  // Mips_Probe mips_probe_1: pin names not known; wires that end beside it: IF_IR
  Hex_Digit_Display hex_digit_display_2 (.value(LedData[23:20]));  // open: dp
  Hex_Digit_Display hex_digit_display_3 (.value(LedData[27:24]));  // open: dp
  // Probe on ID_PC[19:0]
  // Mips_Probe mips_probe_2: pin names not known; wires that end beside it: ID_IR
  \分支预测PCout  \u_分支预测pcout_1  (
    .PC_4(PC_4), .Imm26(Imm26_3), .Imm32(imm), .Reg1(Reg1_3), .JMP(jmp_3), .JR(jr_3), .JAL(jal_5),
    .Branch(Branch), .PC_4_3(PC_4_3), .jump_suc(jump_suc), .jb_3(jb_3), .hit_3(hit_3), .hit(hit),
    .pc_att(pc_att), .jump_att(jump_att), .jump_att_3(jump_att_3), .PCout(\分支预测pcout_1_pcout ),
    .att_fail(att_fail), .att_suc(att_suc), .dest_attr(dest_addr));
  Multiplexer #(.width(32), .enable("false")) multiplexer_1 (
    .in0({32{1'b0}}), .in1(Reg1_3), .out(multiplexer_1_out), .sel(syscall_3));
  Multiplexer #(.width(32), .enable("false")) multiplexer_2 (
    .in0({32{1'b0}}), .in1(Reg1_5), .out(multiplexer_2_out), .sel(syscall_5));
  Hex_Digit_Display hex_digit_display_4 (.value(LedData[19:16]));  // open: dp
  Hex_Digit_Display hex_digit_display_5 (.value(LedData[15:12]));  // open: dp
  not not_1 (not_1_out, or_1_out);
  or or_1 (or_1_out, Halt, stall);
  BHT bht_1 (
    .CLK(CLK), .RST(RST), .PC(IF_PC), .PC_3(PC_3), .dest_attr(dest_addr), .hit_pos_3(hit_pos_3), .jb_3(jb_3),
    .hit_3(hit_3), .jump_suc_3(jump_suc), .hit(hit), .jump_att(jump_att), .pc_att(pc_att), .hit_pos(hit_pos));
  Comparator #(.width(32), .mode("unsigned")) comparator_1 (
    .a(multiplexer_1_out), .b(32'h22), .eq(comparator_1_eq));  // open: gt, lt
  Multiplexer #(.width(32), .enable("false")) multiplexer_3 (
    .in0({32{1'b0}}), .in1(Reg2_3), .out(multiplexer_3_out), .sel(comparator_1_eq));
  Comparator #(.width(32), .mode("unsigned")) comparator_2 (
    .a(multiplexer_2_out), .b(32'ha), .eq(comparator_2_eq));  // open: gt, lt
  Comparator #(.width(32), .mode("unsigned")) comparator_3 (
    .a(multiplexer_2_out), .b(32'h32), .eq(comparator_3_eq));  // open: gt, lt
  Hex_Digit_Display hex_digit_display_6 (.value(LedData[7:4]));  // open: dp
  Hex_Digit_Display hex_digit_display_7 (.value(LedData[11:8]));  // open: dp
  Clock clock_1 (.out(CLK));
  // Probe on EX_PC[19:0]
  // Mips_Probe mips_probe_3: pin names not known; wires that end beside it: EX_IR
  Register #(.width(32)) PC (.D(\分支预测pcout_1_pcout ), .en(not_1_out), .Q(IF_PC), .clk(CLK), .clr(RST));
  Adder #(.width(32)) adder_1 (.a(IF_PC), .b(32'h4), .out(PC_4));  // open: cin, cout
  Register #(.width(32)) register_1 (.D(multiplexer_3_out), .en(comparator_1_eq), .Q(LedData), .clk(CLK), .clr(RST));
  or or_2 (or_2_out, comparator_3_eq, comparator_2_eq);
  Multiplexer #(.enable("false")) multiplexer_4 (.in0(1'b0), .in1(1'b1), .out(Halt), .sel(or_2_out));
  Hex_Digit_Display hex_digit_display_8 (.value(LedData[3:0]));  // open: dp
  // Probe on \总周期数 
  // Probe on M_PC[19:0]
  // Mips_Probe mips_probe_4: pin names not known; wires that end beside it: MEM_IR
  ROM #(.addrWidth(10), .dataWidth(32)) rom_1 (.addr(IF_PC[11:2]), .data(IF_IR));  // open: sel
  or or_3 (or_3_out, att_fail, RST);
  // Probe on \总周期数 
  // Probe on \无条件分支数 
  // Probe on \条件分支成功数 
  // Probe on \插入气泡数 
  // Probe on \LoadUse次数 
  IF_ID if_id_1 (
    .CLK(CLK), .RST(or_3_out), .Halt(or_4_out), .PC_4(PC_4), .IR(IF_IR), .PC_4O(if_id_1_pc_4o), .IRO(ID_IR),
    .IF_PC(IF_PC), .IF_PCO(ID_PC), .jump_att(jump_att), .hit(hit), .pc_att(pc_att), .hit_pos(hit_pos),
    .pc_attO(pc_att_2), .hit_posO(hit_pos_2), .jump_attO(jump_att_2), .hitO(hit_2), .PC(IF_PC), .PCO(PC_2));
  or or_4 (or_4_out, stall, Halt);
  // Probe on IF_PC[11:0]
  // Probe on WB_PC[19:0]
  // Mips_Probe mips_probe_5: pin names not known; wires that end beside it: WB_IR
  // Probe on ID_PC[11:0]
  // Probe on EX_PC[11:0]
  \单周期硬布线控制器  \u_单周期硬布线控制器_1  (
    .Func(ID_IR[5:0]), .OP(ID_IR[31:26]), .ALU_OP(\单周期硬布线控制器_1_jr [10:7]), .MemToReg(\单周期硬布线控制器_1_jr [5]),
    .MemWrite(\单周期硬布线控制器_1_jr [6]), .ALU_SRC(\单周期硬布线控制器_1_jr [11]), .RegWrite(\单周期硬布线控制器_1_jr [12]),
    .SysCALL(syscall_2), .SignedExt(\单周期硬布线控制器_1_jr [16]), .RegDst(\单周期硬布线控制器_1_jr [14]),
    .JR(\单周期硬布线控制器_1_jr [0]), .JMP(\单周期硬布线控制器_1_jr [1]), .Beq(\单周期硬布线控制器_1_jr [2]),
    .JAL(\单周期硬布线控制器_1_jr [13]), .Bne(\单周期硬布线控制器_1_jr [4]), .INS1(INS1), .INS2(INS2), .INS3(INS3),
    .Bgtz(\单周期硬布线控制器_1_jr [3]));  // open: RET
  branch_jump branch_jump_1 (
    .Reg1_3(Reg1_3), .Beq_3(Beq_3), .Bne_3(Bne_3), .Bgtz_3(Bgtz_3), .equal(equal), .j_3(jmp_3),
    .Branch(Branch), .jump_suc(jump_suc), .jb_3(jb_3));
  // Probe on M_PC[11:0]
  Multiplexer #(.width(5), .enable("false")) multiplexer_5 (
    .in0(ID_IR[25:21]), .in1(5'b00010), .out(ra2), .sel(syscall_2));
  Multiplexer #(.width(5), .enable("false")) multiplexer_6 (
    .in0(ID_IR[20:16]), .in1(5'b00100), .out(rb2), .sel(syscall_2));
  Multiplexer #(.width(5), .enable("false")) multiplexer_7 (
    .in0(multiplexer_8_out), .in1({5{1'b1}}), .out(rw_5), .sel(jal_5));
  Multiplexer #(.width(5), .enable("false")) multiplexer_8 (
    .in0(rt5), .in1(rd5), .out(multiplexer_8_out), .sel(RegDst_5));
  assign Imm32 = {{16{ID_IR[15]}}, ID_IR[15:0]};  // Bit_Extender bit_extender_1
  Multiplexer #(.width(32), .enable("false")) multiplexer_9 (
    .in0(mem_wb_1_aluo), .in1(mem_wb_1_dmouto), .out(multiplexer_9_out), .sel(MemToReg_5));
  // Probe on WB_PC[11:0]
  Comparator #(.width(6), .mode("unsigned")) comparator_4 (
    .a(ID_IR[31:26]), .b(6'b100011), .eq(load_2));  // open: gt, lt
  Multiplexer #(.width(32), .enable("false")) multiplexer_10 (
    .in0(multiplexer_9_out), .in1(mem_wb_1_pco), .out(RDin), .sel(jal_5));
  MIPS_Regifile mips_regifile_1 (
    .Din(RDin), .Clk(CLK), .R1(Reg1), .R2(Reg2), .WE(RegWrite), .W_num(rw_5), .R1_num(ra2), .R2_num(rb2));
  ID_EX id_ex_1 (
    .CLK(CLK), .rd(ID_IR[15:11]), .rt(ID_IR[20:16]), .reg1(Reg1), .reg2(Reg2), .Imm(Imm32),
    .PC_4(if_id_1_pc_4o), .Control({\单周期硬布线控制器_1_jr [16], syscall_2, \单周期硬布线控制器_1_jr [14:0]}),
    .RST(or_5_out), .Halt(Halt), .Shammt(ID_IR[10:6]), .imm26(ID_IR[25:0]), .ra2(ra2), .rt2(rb2),
    .load_2(load_2), .INS1_2(INS1), .INS1_3(INS2), .INS1_4(INS3), .imm26O(Imm26_3), .rdO(rd3), .rtO(rt3),
    .ControlO({id_ex_1_controlo[16], syscall_3, RegDst_3, jal_3, RegWrite_3, AluSrcB_3, AluOp_3, id_ex_1_controlo[6:5], Bne_3, Bgtz_3, Beq_3, jmp_3, jr_3}),
    .PCO(PC_4_3), .reg1O(id_ex_1_reg1o), .reg2O(id_ex_1_reg2o), .ImmO(imm), .ShammtO(id_ex_1_shammto),
    .ra2O(ra3), .rd2O(rb3), .loadO(load_3), .INS3_O(INS3_3), .INS2_O(INS2_3), .INS1_O(INS1_3), .IR(ID_IR),
    .IR_2(EX_IR), .IR_PC(ID_PC), .IR_PCO(EX_PC), .jump_att(jump_att_2), .hit(hit_2), .pc_att(pc_att_2),
    .hit_pos(hit_pos_2), .pc_attO(pc_att_3), .hit_posO(hit_pos_3), .jump_attO(jump_att_3), .hitO(hit_3),
    .PCO_2(PC_3), .PC(PC_2));
  or or_5 (or_5_out, att_fail, RST, stall);
  \分支相关  \u_分支相关_1  (.j(jmp_3), .jr(jr_3), .jal(jal_3), .branch(Branch), .j_rst(j_rst));
  \重定向  \u_重定向_1  (
    .INS1(INS1_3), .INS2(INS2_3), .INS3(INS3_3), .RegWrite4(RegWrite_4), .RegWrite5(RegWrite), .ra3(ra3),
    .rb3(rb3), .rw4(rw_4), .rw5(rw_5), .sel1(sel1), .sel2(sel2), .sel3(sel3), .sel4(sel4));
  Multiplexer #(.width(32), .enable("false")) multiplexer_11 (
    .in0(id_ex_1_reg1o), .in1(RDin), .out(multiplexer_11_out), .sel(sel3));
  Multiplexer #(.width(32), .enable("false")) multiplexer_12 (
    .in0(multiplexer_11_out), .in1(alur_4), .out(Reg1_3), .sel(sel1));
  Multiplexer #(.width(32), .enable("false")) multiplexer_13 (
    .in0(id_ex_1_reg2o), .in1(RDin), .out(multiplexer_13_out), .sel(sel4));
  Multiplexer #(.width(32), .enable("false")) multiplexer_14 (
    .in0(multiplexer_13_out), .in1(alur_4), .out(Reg2_3), .sel(sel2));
  Multiplexer #(.width(5), .enable("false")) multiplexer_15 (.in0(rt3), .in1(rd3), .out(rw_3), .sel(RegDst_3));
  Multiplexer #(.width(32), .enable("false")) multiplexer_16 (
    .in0(Reg2_3), .in1(imm), .out(multiplexer_16_out), .sel(AluSrcB_3));
  EX_MEM ex_mem_1 (
    .CLK(CLK), .RST(RST), .Halt(Halt),
    .Control({id_ex_1_controlo[16], syscall_3, RegDst_3, jal_3, RegWrite_3, AluSrcB_3, AluOp_3, id_ex_1_controlo[6:5], Bne_3, Bgtz_3, Beq_3, jmp_3, jr_3}),
    .PC(PC_4_3), .reg2(Reg2_3), .Alu(mips_alu_1_result), .rd(rd3), .rt(rt3), .rdO(rd4), .rtO(rt4),
    .ControlO({ex_mem_1_controlo[16:15], RegDst_4, ex_mem_1_controlo[13], RegWrite_4, ex_mem_1_controlo[11:7], MemWrite, ex_mem_1_controlo[5], Bne_4, Bgtz_4, Beq_4, jmp_4, jr_4}),
    .PCO(ex_mem_1_pco), .reg2O(MDin), .AluO(alur_4), .IR(EX_IR), .IR_2(MEM_IR), .Reg1_3(Reg1_3),
    .Reg1_O(Reg1_4), .EX_PC(EX_PC), .EX_PCO(M_PC));  // open: Reg2_3, Reg2_O
  MIPS_ALU mips_alu_1 (
    .X(Reg1_3), .Y(multiplexer_16_out), .AluOP(AluOp_3), .Equal(equal), .Result(mips_alu_1_result),
    .shamt(id_ex_1_shammto));  // open: Result_2
  Load_Use load_use_1 (
    .INS1(INS1), .stall(stall), .INS2(INS2), .INS3(INS3), .RegDin3(load_3), .ra(ra2), .rb(rb2), .rw3(rw_3));
  counter counter_1 (
    .rst(RST), .clk(CLK), .jmp(jmp_3), .jr(jr_3), .branch(Branch), .halt(Halt), .\总周期数 (\总周期数 ),
    .\条件分支成功数 (\条件分支成功数 ), .\无条件分支数 (\无条件分支数 ), .pop(stall), .\气泡数 (\LoadUse次数 ));
  Multiplexer #(.width(5), .enable("false")) multiplexer_17 (.in0(rt4), .in1(rd4), .out(rw_4), .sel(RegDst_4));
  RAM #(.addrWidth(10), .dataWidth(32), .bus("separate")) ram_1 (
    .addr(alur_4[11:2]), .din(MDin), .data(ram_1_data), .str(MemWrite), .clk(CLK), .clr(RST));  // open: sel, ld
  MEM_WB mem_wb_1 (
    .CLK(CLK), .RST(RST), .Halt(Halt),
    .Control({ex_mem_1_controlo[16:15], RegDst_4, ex_mem_1_controlo[13], RegWrite_4, ex_mem_1_controlo[11:7], MemWrite, ex_mem_1_controlo[5], Bne_4, Bgtz_4, Beq_4, jmp_4, jr_4}),
    .Alu(alur_4), .PC(ex_mem_1_pco), .DMout(ram_1_data), .rd(rd4), .rt(rt4), .rdO(rd5), .rtO(rt5),
    .ControlO({mem_wb_1_controlo[16], syscall_5, RegDst_5, jal_5, RegWrite, mem_wb_1_controlo[11:6], MemToReg_5, mem_wb_1_controlo[4:0]}),
    .PCO(mem_wb_1_pco), .DMoutO(mem_wb_1_dmouto), .AluO(mem_wb_1_aluo), .IR_2(WB_IR), .IR(MEM_IR),
    .Reg1_3(Reg1_4), .Reg1_O(Reg1_5), .MEM_PC(M_PC), .MEM_PCO(WB_PC));  // open: Reg2_3, Reg2_O

  // Other names for the same wires on the sheet: MemWrite_4 = MemWrite; RegWrite_5 = RegWrite;
  //   Imm26[25:0] = ID_IR[25:0]; rd2[4:0] = ID_IR[15:11]; rt2[4:0] = ID_IR[20:16]; op2[5:0] = ID_IR[31:26];
  //   MEM_PC[31:0] = M_PC; PC[31:0] = IF_PC; RegD_5[31:0] = RDin

  // Notes on the sheet:
  //   中断源
  //   时空图监测，可删除
  //   中断等待指示
  //   数码管输出
  //   指令存储器
  //   contents of rom_1 (hex, n*v repeats v):
  //   20110001 8000c05 20110001 20120002 20130003 8000c09 20110001 20120002 20130003 8000c0d 20110001
  //   20120002 20130003 8000c11 20110001 20120002 20130003 c000cb8 20100001 20110001 118fc0 112020
  //   20020022 c 118882 12200001 8000c15 112020 20020022 c 20110001 118880 112020 20020022 c 12200001
  //   8000c1f 20110001 118fc0 112020 20020022 c 1188c3 112020 20020022 c 118903 112020 20020022 c 118903
  //   112020 20020022 c 118903 112020 20020022 c 118903 112020 20020022 c 118903 112020 20020022 c 118903
  //   112020 20020022 c 118903 112020 20020022 c 20100001 109fc0 139fc3 8021 2012000c 24160003 26100001
  //   3210000f 20080008 20090001 139900 2709825 132020 20020022 c 1094022 1500fff9 22100001 2018000f
  //   2188024 108700 20080008 20090001 139902 2709825 132021 20020022 c 1094022 1500fff9 108702 2c9b022
  //   12c00001 8000c50 4020 1084027 84400 3508ffff 82021 20020022 c 2010ffff 20110000 ae300000 22100001
  //   22310004 ae300000 22100001 22310004 ae300000 22100001 22310004 ae300000 22100001 22310004 ae300000
  //   22100001 22310004 ae300000 22100001 22310004 ae300000 22100001 22310004 ae300000 22100001 22310004
  //   ae300000 22100001 22310004 ae300000 22100001 22310004 ae300000 22100001 22310004 ae300000 22100001
  //   22310004 ae300000 22100001 22310004 ae300000 22100001 22310004 ae300000 22100001 22310004 ae300000
  //   22100001 22310004 22100001 8020 2011003c 8e130000 8e340000 274402a 11000002 ae330000 ae140000
  //   2231fffc 1611fff8 102020 20020022 c 22100004 2011003c 1611fff2 20020032 c 20100000 22100001 102020
  //   20020022 c 22100002 102020 20020022 c 22100003 102020 20020022 c 22100004 102020 20020022 c 22100005
  //   102020 20020022 c 22100006 102020 20020022 c 22100007 102020 20020022 c 22100008 102020 20020022
  //   20020022 c 3e00008
  //   JMP
  //   JR
  //   OP
  //   Func
  //   rs
  //   rt
  //   rd
  //   shmat
  //   Imm
  //   Beq
  //   Bgtz
  //   Bne
  //   MemToReg
  //   MemWrite
  //   AluOP
  //   AluSrcB
  //   RegWrite
  //   JAL
  //   RegDst
  //   Syscall
  //   流水调试日志用
  //   为方便自动评测，需要输出流水线各段保存的PC值，注意是PC不是PC+4，另外ID段寄存器写入信息，Mem段内存写入信息也要输出
endmodule

module \封装正确性测试  (
);

  wire IR1, IR2, IR3, MemW, RegW;
  wire [31:0] EX_PC, ID_PC, IF_PC, IR, LED, MDin, MDinr, MEM_PC, PC, RDin, RDinr, WB_PC;

  \单周期MIPS  \u_单周期mips_1  (
    .RegWrite(RegW), .MemWrite(MemW), .PC(PC), .IR(IR), .RDin(RDin), .MDin(MDin), .LedData(LED));  // open: IR1, IR2, IR3
  \气泡流水线  \u_气泡流水线_1  (
    .RegWrite(RegW), .MemWrite(MemW), .IF_PC(IF_PC), .ID_PC(ID_PC), .EX_PC(EX_PC), .M_PC(MEM_PC),
    .WB_PC(WB_PC), .RDin(RDinr), .MDin(MDinr), .LedData(LED));
  \单周期MIPS_单级中断  \u_单周期mips_单级中断_1  (
    .IR1(IR1), .IR2(IR2), .IR3(IR3), .RegWrite(RegW), .MemWrite(MemW), .PC(PC), .IR(IR), .RDin(RDin),
    .MDin(MDin), .LedData(LED));
  \理想流水线  \u_理想流水线_1  (
    .RegWrite(RegW), .MemWrite(MemW), .IF_PC(IF_PC), .ID_PC(ID_PC), .EX_PC(EX_PC), .M_PC(MEM_PC),
    .WB_PC(WB_PC), .RDin(RDinr), .MDin(MDinr), .LedData(LED));
  \气泡流水线  \u_气泡流水线_2  (
    .RegWrite(RegW), .MemWrite(MemW), .IF_PC(IF_PC), .ID_PC(ID_PC), .EX_PC(EX_PC), .M_PC(MEM_PC),
    .WB_PC(WB_PC), .RDin(RDinr), .MDin(MDinr), .LedData(LED));
  \单周期MIPS_多级中断  \u_单周期mips_多级中断_1  (
    .IR1(IR1), .IR2(IR2), .IR3(IR3), .RegWrite(RegW), .MemWrite(MemW), .PC(PC), .IR(IR), .RDin(RDin),
    .MDin(MDin), .LedData(LED));

  // Notes on the sheet:
  //   单周期封装测试
  //   气泡流水封装测试
  //   单周期+单级中断封装测试
  //   请检查上面封装有无位宽不匹配，引脚标签是否和连接的标签相对应，否则无法在educoder平台上正确测试
  //   理想流水封装测试
  //   重定向流水封装测试
  //   单周期+多级中断封装测试
endmodule

module IF_ID (
  input  CLK,
  input  RST,
  input  Halt,
  input  [31:0] PC_4,
  input  [31:0] IR,
  input  [31:0] IF_PC,
  input  jump_att,
  input  hit,
  input  [31:0] pc_att,
  input  [2:0] hit_pos,
  input  [31:0] PC,
  output [31:0] PC_4O,
  output [31:0] IRO,
  output [31:0] IF_PCO,
  output [31:0] pc_attO,
  output [2:0] hit_posO,
  output jump_attO,
  output hitO,
  output [31:0] PCO
);

  wire multiplexer_4_out, multiplexer_5_out, not_1_out;
  wire [2:0] multiplexer_3_out;
  wire [31:0] multiplexer_1_out, multiplexer_2_out, multiplexer_6_out, multiplexer_7_out, multiplexer_8_out;

  Multiplexer #(.width(32), .enable("false")) multiplexer_1 (
    .in0(PC), .in1({32{1'b0}}), .out(multiplexer_1_out), .sel(RST));
  Multiplexer #(.width(32), .enable("false")) multiplexer_2 (
    .in0(pc_att), .in1({32{1'b0}}), .out(multiplexer_2_out), .sel(RST));
  Multiplexer #(.width(3), .enable("false")) multiplexer_3 (
    .in0(hit_pos), .in1(3'b000), .out(multiplexer_3_out), .sel(RST));
  Multiplexer #(.enable("false")) multiplexer_4 (.in0(jump_att), .in1(1'b0), .out(multiplexer_4_out), .sel(RST));
  Multiplexer #(.enable("false")) multiplexer_5 (.in0(hit), .in1(1'b0), .out(multiplexer_5_out), .sel(RST));
  Multiplexer #(.width(32), .enable("false")) multiplexer_6 (
    .in0(IF_PC), .in1({32{1'b0}}), .out(multiplexer_6_out), .sel(RST));
  Multiplexer #(.width(32), .enable("false")) multiplexer_7 (
    .in0(PC_4), .in1({32{1'b0}}), .out(multiplexer_7_out), .sel(RST));
  Multiplexer #(.width(32), .enable("false")) multiplexer_8 (
    .in0(IR), .in1({32{1'b0}}), .out(multiplexer_8_out), .sel(RST));
  not not_1 (not_1_out, Halt);
  Register #(.width(32)) register_1 (.D(multiplexer_1_out), .en(not_1_out), .Q(PCO), .clk(CLK));  // open: clr
  Register #(.width(32)) register_2 (.D(multiplexer_2_out), .en(not_1_out), .Q(pc_attO), .clk(CLK));  // open: clr
  Register #(.width(3)) register_3 (.D(multiplexer_3_out), .en(not_1_out), .Q(hit_posO), .clk(CLK));  // open: clr
  Register #(.width(1)) register_4 (.D(multiplexer_4_out), .en(not_1_out), .Q(jump_attO), .clk(CLK));  // open: clr
  Register #(.width(1)) register_5 (.D(multiplexer_5_out), .en(not_1_out), .Q(hitO), .clk(CLK));  // open: clr
  Register #(.width(32)) register_6 (.D(multiplexer_6_out), .en(not_1_out), .Q(IF_PCO), .clk(CLK));  // open: clr
  Register #(.width(32)) register_7 (.D(multiplexer_7_out), .en(not_1_out), .Q(PC_4O), .clk(CLK));  // open: clr
  Register #(.width(32)) register_8 (.D(multiplexer_8_out), .en(not_1_out), .Q(IRO), .clk(CLK));  // open: clr

  // Notes on the sheet:
  //   PC
  //   IR
endmodule

module ID_EX (
  input  CLK,
  input  [4:0] rd,
  input  [4:0] rt,
  input  [31:0] reg1,
  input  [31:0] reg2,
  input  [31:0] Imm,
  input  [31:0] PC_4,
  input  [16:0] Control,
  input  RST,
  input  Halt,
  input  [4:0] Shammt,
  input  [25:0] imm26,
  input  [4:0] ra2,
  input  [4:0] rt2,
  input  load_2,
  input  INS1_2,
  input  INS1_3,
  input  INS1_4,
  input  [31:0] IR,
  input  [31:0] IR_PC,
  input  [31:0] pc_att,
  input  [2:0] hit_pos,
  input  jump_att,
  input  hit,
  input  [31:0] PC,
  output [25:0] imm26O,
  output [4:0] rdO,
  output [4:0] rtO,
  output [16:0] ControlO,
  output [31:0] PCO,
  output [31:0] reg1O,
  output [31:0] reg2O,
  output [31:0] ImmO,
  output [4:0] ShammtO,
  output [4:0] ra2O,
  output [4:0] rd2O,
  output loadO,
  output INS3_O,
  output INS2_O,
  output INS1_O,
  output [31:0] IR_2,
  output [31:0] IR_PCO,
  output [31:0] pc_attO,
  output [2:0] hit_posO,
  output jump_attO,
  output hitO,
  output [31:0] PCO_2
);

  wire multiplexer_3_out, multiplexer_4_out, multiplexer_5_out, multiplexer_6_out, multiplexer_21_out,
       multiplexer_22_out, not_1_out;
  wire [2:0] multiplexer_20_out;
  wire [4:0] multiplexer_7_out, multiplexer_8_out, multiplexer_10_out, multiplexer_11_out, multiplexer_12_out;
  wire [16:0] multiplexer_13_out;
  wire [25:0] multiplexer_9_out;
  wire [31:0] multiplexer_1_out, multiplexer_2_out, multiplexer_14_out, multiplexer_15_out,
       multiplexer_16_out, multiplexer_17_out, multiplexer_18_out, multiplexer_19_out;

  Multiplexer #(.width(32), .enable("false")) multiplexer_1 (
    .in0(IR_PC), .in1({32{1'b0}}), .out(multiplexer_1_out), .sel(RST));
  Multiplexer #(.width(32), .enable("false")) multiplexer_2 (
    .in0(IR), .in1({32{1'b0}}), .out(multiplexer_2_out), .sel(RST));
  Multiplexer #(.enable("false")) multiplexer_3 (.in0(INS1_4), .in1(1'b0), .out(multiplexer_3_out), .sel(RST));
  Multiplexer #(.enable("false")) multiplexer_4 (.in0(INS1_3), .in1(1'b0), .out(multiplexer_4_out), .sel(RST));
  Multiplexer #(.enable("false")) multiplexer_5 (.in0(INS1_2), .in1(1'b0), .out(multiplexer_5_out), .sel(RST));
  Multiplexer #(.enable("false")) multiplexer_6 (.in0(load_2), .in1(1'b0), .out(multiplexer_6_out), .sel(RST));
  Multiplexer #(.width(5), .enable("false")) multiplexer_7 (
    .in0(ra2), .in1({5{1'b0}}), .out(multiplexer_7_out), .sel(RST));
  Multiplexer #(.width(5), .enable("false")) multiplexer_8 (
    .in0(rt2), .in1({5{1'b0}}), .out(multiplexer_8_out), .sel(RST));
  Multiplexer #(.width(26), .enable("false")) multiplexer_9 (
    .in0(imm26), .in1({26{1'b0}}), .out(multiplexer_9_out), .sel(RST));
  Multiplexer #(.width(5), .enable("false")) multiplexer_10 (
    .in0(Shammt), .in1({5{1'b0}}), .out(multiplexer_10_out), .sel(RST));
  Multiplexer #(.width(5), .enable("false")) multiplexer_11 (
    .in0(rd), .in1({5{1'b0}}), .out(multiplexer_11_out), .sel(RST));
  Multiplexer #(.width(5), .enable("false")) multiplexer_12 (
    .in0(rt), .in1({5{1'b0}}), .out(multiplexer_12_out), .sel(RST));
  Multiplexer #(.width(17), .enable("false")) multiplexer_13 (
    .in0(Control), .in1({17{1'b0}}), .out(multiplexer_13_out), .sel(RST));
  Multiplexer #(.width(32), .enable("false")) multiplexer_14 (
    .in0(PC_4), .in1({32{1'b0}}), .out(multiplexer_14_out), .sel(RST));
  Multiplexer #(.width(32), .enable("false")) multiplexer_15 (
    .in0(reg1), .in1({32{1'b0}}), .out(multiplexer_15_out), .sel(RST));
  Multiplexer #(.width(32), .enable("false")) multiplexer_16 (
    .in0(reg2), .in1({32{1'b0}}), .out(multiplexer_16_out), .sel(RST));
  Multiplexer #(.width(32), .enable("false")) multiplexer_17 (
    .in0(Imm), .in1({32{1'b0}}), .out(multiplexer_17_out), .sel(RST));
  Multiplexer #(.width(32), .enable("false")) multiplexer_18 (
    .in0(PC), .in1({32{1'b0}}), .out(multiplexer_18_out), .sel(RST));
  Multiplexer #(.width(32), .enable("false")) multiplexer_19 (
    .in0(pc_att), .in1({32{1'b0}}), .out(multiplexer_19_out), .sel(RST));
  Multiplexer #(.width(3), .enable("false")) multiplexer_20 (
    .in0(hit_pos), .in1(3'b000), .out(multiplexer_20_out), .sel(RST));
  Multiplexer #(.enable("false")) multiplexer_21 (.in0(jump_att), .in1(1'b0), .out(multiplexer_21_out), .sel(RST));
  Multiplexer #(.enable("false")) multiplexer_22 (.in0(hit), .in1(1'b0), .out(multiplexer_22_out), .sel(RST));
  not not_1 (not_1_out, Halt);
  Register #(.width(32)) register_1 (.D(multiplexer_18_out), .en(not_1_out), .Q(PCO_2), .clk(CLK));  // open: clr
  Register #(.width(32)) register_2 (.D(multiplexer_19_out), .en(not_1_out), .Q(pc_attO), .clk(CLK));  // open: clr
  Register #(.width(3)) register_3 (.D(multiplexer_20_out), .en(not_1_out), .Q(hit_posO), .clk(CLK));  // open: clr
  Register #(.width(1)) register_4 (.D(multiplexer_21_out), .en(not_1_out), .Q(jump_attO), .clk(CLK));  // open: clr
  Register #(.width(1)) register_5 (.D(multiplexer_22_out), .en(not_1_out), .Q(hitO), .clk(CLK));  // open: clr
  Register #(.width(32)) register_6 (.D(multiplexer_1_out), .en(not_1_out), .Q(IR_PCO), .clk(CLK));  // open: clr
  Register #(.width(32)) register_7 (.D(multiplexer_2_out), .en(not_1_out), .Q(IR_2), .clk(CLK));  // open: clr
  Register #(.width(1)) register_8 (.D(multiplexer_3_out), .en(not_1_out), .Q(INS3_O), .clk(CLK));  // open: clr
  Register #(.width(1)) register_9 (.D(multiplexer_4_out), .en(not_1_out), .Q(INS2_O), .clk(CLK));  // open: clr
  Register #(.width(1)) register_10 (.D(multiplexer_5_out), .en(not_1_out), .Q(INS1_O), .clk(CLK));  // open: clr
  Register #(.width(1)) register_11 (.D(multiplexer_6_out), .en(not_1_out), .Q(loadO), .clk(CLK));  // open: clr
  Register #(.width(5)) register_12 (.D(multiplexer_7_out), .en(not_1_out), .Q(ra2O), .clk(CLK));  // open: clr
  Register #(.width(5)) register_13 (.D(multiplexer_8_out), .en(not_1_out), .Q(rd2O), .clk(CLK));  // open: clr
  Register #(.width(26)) register_14 (.D(multiplexer_9_out), .en(not_1_out), .Q(imm26O), .clk(CLK));  // open: clr
  Register #(.width(5)) register_15 (.D(multiplexer_10_out), .en(not_1_out), .Q(ShammtO), .clk(CLK));  // open: clr
  Register #(.width(5)) register_16 (.D(multiplexer_11_out), .en(not_1_out), .Q(rdO), .clk(CLK));  // open: clr
  Register #(.width(5)) register_17 (.D(multiplexer_12_out), .en(not_1_out), .Q(rtO), .clk(CLK));  // open: clr
  Register #(.width(17)) register_18 (.D(multiplexer_13_out), .en(not_1_out), .Q(ControlO), .clk(CLK));  // open: clr
  Register #(.width(32)) u_PC (.D(multiplexer_14_out), .en(not_1_out), .Q(PCO), .clk(CLK));  // open: clr
  Register #(.width(32)) register_19 (.D(multiplexer_15_out), .en(not_1_out), .Q(reg1O), .clk(CLK));  // open: clr
  Register #(.width(32)) register_20 (.D(multiplexer_16_out), .en(not_1_out), .Q(reg2O), .clk(CLK));  // open: clr
  Register #(.width(32)) register_21 (.D(multiplexer_17_out), .en(not_1_out), .Q(ImmO), .clk(CLK));  // open: clr

  // Other names for the same wires on the sheet: INS2_2 = INS1_3; INS3_2 = INS1_4; IRO[31:0] = IR_2;
  //   PC_4O[31:0] = PCO; PCO_t[31:0] = PCO_2; rb2[4:0] = rt2; rb2O[4:0] = rd2O

  // Notes on the sheet:
  //   ra2
  //   rb2
  //   shammt
  //   rs
  //   rt
  //   control
  //   reg1
  //   reg2
  //   IMM
endmodule

module EX_MEM (
  input  CLK,
  input  RST,
  input  Halt,
  input  [16:0] Control,
  input  [31:0] PC,
  input  [31:0] reg2,
  input  [31:0] Alu,
  input  [4:0] rd,
  input  [4:0] rt,
  input  [31:0] IR,
  input  [31:0] Reg1_3,
  input  [31:0] Reg2_3,
  input  [31:0] EX_PC,
  output [4:0] rdO,
  output [4:0] rtO,
  output [16:0] ControlO,
  output [31:0] PCO,
  output [31:0] reg2O,
  output [31:0] AluO,
  output [31:0] IR_2,
  output [31:0] Reg1_O,
  output [31:0] Reg2_O,
  output [31:0] EX_PCO
);

  wire not_1_out;

  not not_1 (not_1_out, Halt);
  Register #(.width(32)) register_1 (.D(EX_PC), .en(not_1_out), .Q(EX_PCO), .clk(CLK), .clr(RST));
  Register #(.width(32)) register_2 (.D(Reg2_3), .en(not_1_out), .Q(Reg2_O), .clk(CLK), .clr(RST));
  Register #(.width(32)) register_3 (.D(Reg1_3), .en(not_1_out), .Q(Reg1_O), .clk(CLK), .clr(RST));
  Register #(.width(32)) register_4 (.D(IR), .en(not_1_out), .Q(IR_2), .clk(CLK), .clr(RST));
  Register #(.width(5)) register_5 (.D(rd), .en(not_1_out), .Q(rdO), .clk(CLK), .clr(RST));
  Register #(.width(5)) register_6 (.D(rt), .en(not_1_out), .Q(rtO), .clk(CLK), .clr(RST));
  Register #(.width(17)) register_7 (.D(Control), .en(not_1_out), .Q(ControlO), .clk(CLK), .clr(RST));
  Register #(.width(32)) u_PC (.D(PC), .en(not_1_out), .Q(PCO), .clk(CLK), .clr(RST));
  Register #(.width(32)) register_8 (.D(reg2), .en(not_1_out), .Q(reg2O), .clk(CLK), .clr(RST));
  Register #(.width(32)) register_9 (.D(Alu), .en(not_1_out), .Q(AluO), .clk(CLK), .clr(RST));

  // Other names for the same wires on the sheet: IRO[31:0] = IR_2

  // Notes on the sheet:
  //   rs
  //   rt
  //   control
  //   reg2
  //   alu
endmodule

module MEM_WB (
  input  CLK,
  input  RST,
  input  Halt,
  input  [16:0] Control,
  input  [31:0] Alu,
  input  [31:0] PC,
  input  [31:0] DMout,
  input  [4:0] rd,
  input  [4:0] rt,
  input  [31:0] IR,
  input  [31:0] Reg1_3,
  input  [31:0] Reg2_3,
  input  [31:0] MEM_PC,
  output [4:0] rdO,
  output [4:0] rtO,
  output [16:0] ControlO,
  output [31:0] PCO,
  output [31:0] DMoutO,
  output [31:0] AluO,
  output [31:0] IR_2,
  output [31:0] Reg1_O,
  output [31:0] Reg2_O,
  output [31:0] MEM_PCO
);

  wire not_1_out;

  not not_1 (not_1_out, Halt);
  Register #(.width(32)) register_1 (.D(MEM_PC), .en(not_1_out), .Q(MEM_PCO), .clk(CLK), .clr(RST));
  Register #(.width(32)) register_2 (.D(Reg2_3), .en(not_1_out), .Q(Reg2_O), .clk(CLK), .clr(RST));
  Register #(.width(32)) register_3 (.D(Reg1_3), .en(not_1_out), .Q(Reg1_O), .clk(CLK), .clr(RST));
  Register #(.width(32)) register_4 (.D(IR), .en(not_1_out), .Q(IR_2), .clk(CLK), .clr(RST));
  Register #(.width(5)) register_5 (.D(rd), .en(not_1_out), .Q(rdO), .clk(CLK), .clr(RST));
  Register #(.width(5)) register_6 (.D(rt), .en(not_1_out), .Q(rtO), .clk(CLK), .clr(RST));
  Register #(.width(17)) register_7 (.D(Control), .en(not_1_out), .Q(ControlO), .clk(CLK), .clr(RST));
  Register #(.width(32)) u_PC (.D(PC), .en(not_1_out), .Q(PCO), .clk(CLK), .clr(RST));
  Register #(.width(32)) register_8 (.D(DMout), .en(not_1_out), .Q(DMoutO), .clk(CLK), .clr(RST));
  Register #(.width(32)) register_9 (.D(Alu), .en(not_1_out), .Q(AluO), .clk(CLK), .clr(RST));

  // Other names for the same wires on the sheet: IRO[31:0] = IR_2

  // Notes on the sheet:
  //   rs
  //   rt
  //   Control
  //   DMout
  //   alu
endmodule

module \分支相关  (
  input  j,
  input  jr,
  input  jal,
  input  branch,
  output j_rst
);

  or or_1 (j_rst, j, jal, jr, branch);
endmodule

module \数据相关  (
  input  [4:0] rw3,
  input  [4:0] rw4,
  input  [4:0] ra2,
  input  [4:0] rb2,
  input  RegWrite3,
  input  RegWrite4,
  input  INS1,
  input  INS2,
  input  INS3,
  output pop
);

  wire and_1_out, and_2_out, and_3_out, and_4_out, and_5_out, and_6_out, comparator_1_eq, comparator_2_eq,
       comparator_3_eq, comparator_4_eq, comparator_5_eq, comparator_6_eq, comparator_7_eq, comparator_8_eq,
       not_1_out, not_2_out, not_3_out, not_4_out, or_3_out, or_4_out, rs_r, rt_r;

  or or_1 (rs_r, INS1, INS2);
  or or_2 (rt_r, INS1, INS3);
  Comparator #(.width(5), .mode("unsigned")) comparator_1 (.a(rw3), .b(ra2), .eq(comparator_1_eq));  // open: gt, lt
  Comparator #(.width(5), .mode("unsigned")) comparator_2 (
    .a(rw3), .b({5{1'b0}}), .eq(comparator_2_eq));  // open: gt, lt
  Comparator #(.width(5), .mode("unsigned")) comparator_3 (.a(rw3), .b(rb2), .eq(comparator_3_eq));  // open: gt, lt
  Comparator #(.width(5), .mode("unsigned")) comparator_4 (
    .a(rw3), .b({5{1'b0}}), .eq(comparator_4_eq));  // open: gt, lt
  Comparator #(.width(5), .mode("unsigned")) comparator_5 (.a(rw4), .b(ra2), .eq(comparator_5_eq));  // open: gt, lt
  Comparator #(.width(5), .mode("unsigned")) comparator_6 (
    .a(rw4), .b({5{1'b0}}), .eq(comparator_6_eq));  // open: gt, lt
  Comparator #(.width(5), .mode("unsigned")) comparator_7 (.a(rw4), .b(rb2), .eq(comparator_7_eq));  // open: gt, lt
  Comparator #(.width(5), .mode("unsigned")) comparator_8 (
    .a(rw4), .b({5{1'b0}}), .eq(comparator_8_eq));  // open: gt, lt
  not not_1 (not_1_out, comparator_2_eq);
  not not_2 (not_2_out, comparator_4_eq);
  not not_3 (not_3_out, comparator_6_eq);
  not not_4 (not_4_out, comparator_8_eq);
  and and_1 (and_1_out, rs_r, comparator_1_eq, not_1_out);
  and and_2 (and_2_out, rt_r, comparator_3_eq, not_2_out);
  and and_3 (and_3_out, rs_r, comparator_5_eq, not_3_out);
  and and_4 (and_4_out, rt_r, comparator_7_eq, not_4_out);
  or or_3 (or_3_out, and_1_out, and_2_out);
  or or_4 (or_4_out, and_3_out, and_4_out);
  and and_5 (and_5_out, or_3_out, RegWrite3);
  and and_6 (and_6_out, RegWrite4, or_4_out);
  or or_5 (pop, and_5_out, and_6_out);
endmodule

module \重定向  (
  input  INS1,
  input  INS2,
  input  INS3,
  input  RegWrite4,
  input  RegWrite5,
  input  [4:0] ra3,
  input  [4:0] rb3,
  input  [4:0] rw4,
  input  [4:0] rw5,
  output sel1,
  output sel2,
  output sel3,
  output sel4
);

  wire comparator_1_eq, comparator_2_eq, comparator_3_eq, comparator_4_eq, rs_r, rt_r;

  or or_1 (rs_r, INS1, INS2);
  or or_2 (rt_r, INS1, INS3);
  Comparator #(.width(5), .mode("unsigned")) comparator_1 (.a(rw4), .b(ra3), .eq(comparator_1_eq));  // open: gt, lt
  Comparator #(.width(5), .mode("unsigned")) comparator_2 (.a(rw4), .b(rb3), .eq(comparator_2_eq));  // open: gt, lt
  Comparator #(.width(5), .mode("unsigned")) comparator_3 (.a(rw5), .b(ra3), .eq(comparator_3_eq));  // open: gt, lt
  Comparator #(.width(5), .mode("unsigned")) comparator_4 (.a(rw5), .b(rb3), .eq(comparator_4_eq));  // open: gt, lt
  and and_1 (sel1, rs_r, comparator_1_eq, RegWrite4);
  and and_2 (sel2, RegWrite4, comparator_2_eq, rt_r);
  and and_3 (sel3, rs_r, comparator_3_eq, RegWrite5);
  and and_4 (sel4, RegWrite5, comparator_4_eq, rt_r);
endmodule

module counter (
  input  rst,
  input  clk,
  input  jmp,
  input  jr,
  input  branch,
  input  halt,
  input  pop,
  output [15:0] \总周期数 ,
  output [15:0] \条件分支成功数 ,
  output [15:0] \无条件分支数 ,
  output [15:0] \气泡数 
);

  wire and_1_out, not_1_out, or_1_out;

  Counter #(.width(16), .max('hffff)) counter_1 (
    .count(not_1_out), .Q(\总周期数 ), .clk(clk), .clr(rst));  // open: load, D, carry
  not not_1 (not_1_out, halt);
  Counter #(.width(16), .max('hffff)) counter_2 (
    .count(branch), .Q(\条件分支成功数 ), .clk(clk), .clr(rst));  // open: load, D, carry
  Counter #(.width(16), .max('hffff)) counter_3 (
    .count(or_1_out), .Q(\无条件分支数 ), .clk(clk), .clr(rst));  // open: load, D, carry
  or or_1 (or_1_out, jr, jmp);
  Counter #(.width(16), .max('hffff)) counter_4 (
    .count(and_1_out), .Q(\气泡数 ), .clk(clk), .clr(rst));  // open: load, D, carry
  and and_1 (and_1_out, pop, ~halt);  // AND_Gate
endmodule

module PCout (
  input  [31:0] PC_4,
  input  [25:0] Imm26,
  input  [31:0] Imm32,
  input  [31:0] Reg1,
  input  JMP,
  input  JR,
  input  JAL,
  input  Branch,
  input  [31:0] PC_4_3,
  output [31:0] out_10
);

  wire [31:0] adder_1_out, bit_extender_1_out, multiplexer_1_out, multiplexer_3_out, shifter_1_out,
       shifter_2_out;

  Shifter #(.width(32)) shifter_1 (.in(Imm32), .\dist (5'b00010), .out(shifter_1_out));
  assign bit_extender_1_out = {{6{1'b0}}, Imm26};  // Bit_Extender bit_extender_1
  Multiplexer #(.width(32), .enable("false")) multiplexer_1 (
    .in0(PC_4), .in1(adder_1_out), .out(multiplexer_1_out), .sel(Branch));
  Adder #(.width(32)) adder_1 (.a(PC_4_3), .b(shifter_1_out), .out(adder_1_out));  // open: cin, cout
  Shifter #(.width(32)) shifter_2 (.in(bit_extender_1_out), .\dist (5'b00010), .out(shifter_2_out));
  Multiplexer #(.width(32), .enable("false")) multiplexer_2 (
    .in0(multiplexer_1_out), .in1(multiplexer_3_out), .out(out_10), .sel(JMP));
  Multiplexer #(.select(2), .width(32), .enable("false")) multiplexer_3 (
    .in0({PC_4_3[31:28], shifter_2_out[27:0]}), .in1(Reg1), .in2({PC_4_3[31:28], shifter_2_out[27:0]}),
    .out(multiplexer_3_out), .sel({JAL, JR}));  // open: in3

  // Other names for the same wires on the sheet: PCout[31:0] = out_10
endmodule

module Load_Use (
  input  INS1,
  input  INS2,
  input  INS3,
  input  RegDin3,
  input  [4:0] ra,
  input  [4:0] rb,
  input  [4:0] rw3,
  output stall
);

  wire and_1_out, and_2_out, comparator_1_eq, comparator_2_eq, or_3_out, rs_r, rt_r;

  or or_1 (rs_r, INS1, INS2);
  or or_2 (rt_r, INS1, INS3);
  Comparator #(.width(5)) comparator_1 (.a(ra), .b(rw3), .eq(comparator_1_eq));  // open: gt, lt
  Comparator #(.width(5)) comparator_2 (.a(rw3), .b(rb), .eq(comparator_2_eq));  // open: gt, lt
  and and_1 (and_1_out, rs_r, comparator_1_eq);
  and and_2 (and_2_out, rt_r, comparator_2_eq);
  or or_3 (or_3_out, and_1_out, and_2_out);
  and and_3 (stall, or_3_out, RegDin3);
endmodule

module \多级中断信号产生电路  (
);

  wire CLK, comparator_1_eq, comparator_2_eq, comparator_3_eq, comparator_4_eq, comparator_5_eq, IRa, IRb,
       IRc, or_1_out, or_2_out;
  wire [15:0] \总周期数 ;

  Comparator #(.width(16)) comparator_1 (.a(16'h258), .b(\总周期数 ), .eq(comparator_1_eq));  // open: gt, lt
  Comparator #(.width(16)) comparator_2 (.a(\总周期数 ), .b(16'h1), .eq(comparator_2_eq));  // open: gt, lt
  Comparator #(.width(16)) comparator_3 (.a(\总周期数 ), .b(16'h4), .eq(comparator_3_eq));  // open: gt, lt
  Comparator #(.width(16)) comparator_4 (.a(\总周期数 ), .b(16'h7), .eq(comparator_4_eq));  // open: gt, lt
  Comparator #(.width(16)) comparator_5 (.a(\总周期数 ), .b(16'h241), .eq(comparator_5_eq));  // open: gt, lt
  or or_1 (or_1_out, comparator_1_eq, comparator_2_eq);
  assign IRa = or_1_out ? ~CLK : 1'bz;  // Controlled_Inverter controlled_inverter_1
  assign IRb = comparator_3_eq ? ~CLK : 1'bz;  // Controlled_Inverter controlled_inverter_2
  or or_2 (or_2_out, comparator_4_eq, comparator_5_eq);
  assign IRc = or_2_out ? ~CLK : 1'bz;  // Controlled_Inverter controlled_inverter_3
  Pull_Resistor pull_resistor_1 (.node(IRa));
  Pull_Resistor pull_resistor_2 (.node(IRb));
  Pull_Resistor pull_resistor_3 (.node(IRc));
endmodule
module BHT (
  input  CLK,
  input  RST,
  input  [31:0] PC,
  input  [31:0] PC_3,
  input  [31:0] dest_attr,
  input  [2:0] hit_pos_3,
  input  jb_3,
  input  hit_3,
  input  jump_suc_3,
  output hit,
  output jump_att,
  output [31:0] pc_att,
  output [2:0] hit_pos
);

  wire and_17_out, and_18_out, and_19_out, and_20_out, and_21_out, and_22_out, and_23_out, and_24_out,
       decoder_1_out0, decoder_1_out1, decoder_1_out2, decoder_1_out3, decoder_1_out4, decoder_1_out5,
       decoder_1_out6, decoder_1_out7, e1, e2, e3, e4, e5, e6, e7, e8, empty, en0, en0addr, en1, en1addr,
       en2, en2addr, en3, en3addr, en4, en4addr, en5, en5addr, en6, en6addr, en7, en7addr, nhit_3, not_2_out,
       not_3_out, not_4_out, not_5_out, not_6_out, not_7_out, not_8_out, not_9_out, priority_encoder_2_gs,
       v1, v2, v3, v4, v5, v6, v7, v8;
  wire [0:0] multiplexer_5_out;
  wire [1:0] s1, s2, s3, s4, s5, s6, s7, s8, \状态机_1_next , \状态机_2_next , \状态机_3_next , \状态机_4_next ,
       \状态机_5_next , \状态机_6_next , \状态机_7_next , \状态机_8_next ;
  wire [2:0] cur_pos, invalid, MAX_index, multiplexer_1_out, multiplexer_3_out;
  wire [31:0] adder_1_out, adder_2_out, adder_3_out, adder_4_out, adder_5_out, adder_6_out, adder_7_out,
       adder_8_out, LRU_MAX, multiplexer_6_out, multiplexer_7_out, multiplexer_8_out, multiplexer_9_out,
       multiplexer_10_out, multiplexer_11_out, multiplexer_12_out, multiplexer_13_out, register_9_q,
       register_10_q, register_11_q, register_12_q, register_13_q, register_14_q, register_15_q,
       register_16_q, register_33_q, register_34_q, register_35_q, register_36_q, register_37_q,
       register_38_q, register_39_q, register_40_q, t1, t2, t3, t4, t5, t6, t7, t8;

  not not_1 (nhit_3, hit_3);
  Multiplexer #(.width(3), .enable("false")) multiplexer_1 (
    .in0(MAX_index), .in1(invalid), .out(multiplexer_1_out), .sel(empty));
  Multiplexer #(.width(3), .enable("false")) multiplexer_2 (
    .in0(multiplexer_1_out), .in1(hit_pos_3), .out(cur_pos), .sel(hit_3));
  Decoder #(.select(3), .enable("false")) decoder_1 (
    .out0(decoder_1_out0), .out1(decoder_1_out1), .out2(decoder_1_out2), .out3(decoder_1_out3),
    .out4(decoder_1_out4), .out5(decoder_1_out5), .out6(decoder_1_out6), .out7(decoder_1_out7), .sel(cur_pos));
  and and_1 (en0, jb_3, decoder_1_out0);
  and and_2 (en1, decoder_1_out1, jb_3);
  and and_3 (en2, decoder_1_out2, jb_3);
  and and_4 (en3, decoder_1_out3, jb_3);
  and and_5 (en4, decoder_1_out4, jb_3);
  and and_6 (en5, decoder_1_out5, jb_3);
  and and_7 (en6, decoder_1_out6, jb_3);
  and and_8 (en7, decoder_1_out7, jb_3);
  not not_2 (not_2_out, v1);
  not not_3 (not_3_out, v2);
  not not_4 (not_4_out, v3);
  Priority_Encoder priority_encoder_1 (
    .in0(not_2_out), .in1(not_3_out), .in2(not_4_out), .in3(not_5_out), .in4(not_6_out), .in5(not_7_out),
    .in6(not_8_out), .in7(not_9_out), .out(invalid), .gs(empty));  // open: en_in, en_out
  not not_5 (not_5_out, v4);
  not not_6 (not_6_out, v5);
  not not_7 (not_7_out, v6);
  not not_8 (not_8_out, v7);
  not not_9 (not_9_out, v8);
  Register #(.width(1)) register_1 (.D(1'b1), .en(en0), .Q(v1), .clk(CLK), .clr(RST));
  Register #(.width(1)) register_2 (.D(1'b1), .en(en1), .Q(v2), .clk(CLK), .clr(RST));
  Register #(.width(1)) register_3 (.D(1'b1), .en(en2), .Q(v3), .clk(CLK), .clr(RST));
  Register #(.width(1)) register_4 (.D(1'b1), .en(en3), .Q(v4), .clk(CLK), .clr(RST));
  Register #(.width(1)) register_5 (.D(1'b1), .en(en4), .Q(v5), .clk(CLK), .clr(RST));
  Register #(.width(1)) register_6 (.D(1'b1), .en(en5), .Q(v6), .clk(CLK), .clr(RST));
  Register #(.width(1)) register_7 (.D(1'b1), .en(en6), .Q(v7), .clk(CLK), .clr(RST));
  Register #(.width(1)) register_8 (.D(1'b1), .en(en7), .Q(v8), .clk(CLK), .clr(RST));
  and and_9 (en0addr, nhit_3, en0);
  and and_10 (en1addr, nhit_3, en1);
  and and_11 (en2addr, nhit_3, en2);
  and and_12 (en3addr, nhit_3, en3);
  and and_13 (en4addr, nhit_3, en4);
  and and_14 (en5addr, nhit_3, en5);
  and and_15 (en6addr, nhit_3, en6);
  and and_16 (en7addr, nhit_3, en7);
  and and_17 (and_17_out, v1, e1);
  and and_18 (and_18_out, v2, e2);
  and and_19 (and_19_out, v3, e3);
  and and_20 (and_20_out, v4, e4);
  and and_21 (and_21_out, v5, e5);
  and and_22 (and_22_out, v6, e6);
  and and_23 (and_23_out, v7, e7);
  and and_24 (and_24_out, v8, e8);
  Register #(.width(32)) register_9 (.D(PC_3), .en(en0addr), .Q(register_9_q), .clk(CLK), .clr(RST));
  Register #(.width(32)) register_10 (.D(PC_3), .en(en1addr), .Q(register_10_q), .clk(CLK), .clr(RST));
  Register #(.width(32)) register_11 (.D(PC_3), .en(en2addr), .Q(register_11_q), .clk(CLK), .clr(RST));
  Register #(.width(32)) register_12 (.D(PC_3), .en(en3addr), .Q(register_12_q), .clk(CLK), .clr(RST));
  Register #(.width(32)) register_13 (.D(PC_3), .en(en4addr), .Q(register_13_q), .clk(CLK), .clr(RST));
  Register #(.width(32)) register_14 (.D(PC_3), .en(en5addr), .Q(register_14_q), .clk(CLK), .clr(RST));
  Register #(.width(32)) register_15 (.D(PC_3), .en(en6addr), .Q(register_15_q), .clk(CLK), .clr(RST));
  Register #(.width(32)) register_16 (.D(PC_3), .en(en7addr), .Q(register_16_q), .clk(CLK), .clr(RST));
  Comparator #(.width(32), .mode("unsigned")) comparator_1 (.a(PC), .b(register_9_q), .eq(e1));  // open: gt, lt
  Comparator #(.width(32), .mode("unsigned")) comparator_2 (.a(PC), .b(register_10_q), .eq(e2));  // open: gt, lt
  Comparator #(.width(32), .mode("unsigned")) comparator_3 (.a(PC), .b(register_11_q), .eq(e3));  // open: gt, lt
  Comparator #(.width(32), .mode("unsigned")) comparator_4 (.a(PC), .b(register_12_q), .eq(e4));  // open: gt, lt
  Comparator #(.width(32), .mode("unsigned")) comparator_5 (.a(PC), .b(register_13_q), .eq(e5));  // open: gt, lt
  Comparator #(.width(32), .mode("unsigned")) comparator_6 (.a(PC), .b(register_14_q), .eq(e6));  // open: gt, lt
  Comparator #(.width(32), .mode("unsigned")) comparator_7 (.a(PC), .b(register_15_q), .eq(e7));  // open: gt, lt
  Comparator #(.width(32), .mode("unsigned")) comparator_8 (.a(PC), .b(register_16_q), .eq(e8));  // open: gt, lt
  or or_1 (hit, and_17_out, and_18_out, and_19_out, and_20_out, and_21_out, and_22_out, and_23_out, and_24_out);
  Priority_Encoder priority_encoder_2 (
    .in0(and_17_out), .in1(and_18_out), .in2(and_19_out), .in3(and_20_out), .in4(and_21_out),
    .in5(and_22_out), .in6(and_23_out), .in7(and_24_out), .out(hit_pos), .gs(priority_encoder_2_gs));  // open: en_in, en_out
  Multiplexer #(.width(3), .enable("false")) multiplexer_3 (
    .in0(3'b000), .in1(hit_pos), .out(multiplexer_3_out), .sel(priority_encoder_2_gs));
  Multiplexer #(.select(3), .width(32), .enable("false")) multiplexer_4 (
    .in0(t1), .in1(t2), .in2(t3), .in3(t4), .in4(t5), .in5(t6), .in6(t7), .in7(t8), .out(pc_att),
    .sel(multiplexer_3_out));
  Register #(.width(32)) register_17 (.D(dest_attr), .en(en0addr), .Q(t1), .clk(CLK), .clr(RST));
  Register #(.width(32)) register_18 (.D(dest_attr), .en(en1addr), .Q(t2), .clk(CLK), .clr(RST));
  Register #(.width(32)) register_19 (.D(dest_attr), .en(en2addr), .Q(t3), .clk(CLK), .clr(RST));
  Register #(.width(32)) register_20 (.D(dest_attr), .en(en3addr), .Q(t4), .clk(CLK), .clr(RST));
  Register #(.width(32)) register_21 (.D(dest_attr), .en(en4addr), .Q(t5), .clk(CLK), .clr(RST));
  Register #(.width(32)) register_22 (.D(dest_attr), .en(en5addr), .Q(t6), .clk(CLK), .clr(RST));
  Register #(.width(32)) register_23 (.D(dest_attr), .en(en6addr), .Q(t7), .clk(CLK), .clr(RST));
  Register #(.width(32)) register_24 (.D(dest_attr), .en(en7addr), .Q(t8), .clk(CLK), .clr(RST));
  Multiplexer #(.select(3), .width(2), .enable("false")) multiplexer_5 (
    .in0(s1), .in1(s2), .in2(s3), .in3(s4), .in4(s5), .in5(s6), .in6(s7), .in7(s8),
    .out({jump_att, multiplexer_5_out[0]}), .sel(multiplexer_3_out));
  \状态机  \u_状态机_1  (.status(s1), .next(\状态机_1_next ), .hit_jump({hit_3, jump_suc_3}));
  \状态机  \u_状态机_2  (.status(s2), .next(\状态机_2_next ), .hit_jump({hit_3, jump_suc_3}));
  \状态机  \u_状态机_3  (.status(s3), .next(\状态机_3_next ), .hit_jump({hit_3, jump_suc_3}));
  \状态机  \u_状态机_4  (.status(s4), .next(\状态机_4_next ), .hit_jump({hit_3, jump_suc_3}));
  \状态机  \u_状态机_5  (.status(s5), .next(\状态机_5_next ), .hit_jump({hit_3, jump_suc_3}));
  \状态机  \u_状态机_6  (.status(s6), .next(\状态机_6_next ), .hit_jump({hit_3, jump_suc_3}));
  \状态机  \u_状态机_7  (.status(s7), .next(\状态机_7_next ), .hit_jump({hit_3, jump_suc_3}));
  \状态机  \u_状态机_8  (.status(s8), .next(\状态机_8_next ), .hit_jump({hit_3, jump_suc_3}));
  Register #(.width(2)) register_25 (.D(\状态机_1_next ), .en(en0), .Q(s1), .clk(CLK), .clr(RST));
  Register #(.width(2)) register_26 (.D(\状态机_2_next ), .en(en1), .Q(s2), .clk(CLK), .clr(RST));
  Register #(.width(2)) register_27 (.D(\状态机_3_next ), .en(en2), .Q(s3), .clk(CLK), .clr(RST));
  Register #(.width(2)) register_28 (.D(\状态机_4_next ), .en(en3), .Q(s4), .clk(CLK), .clr(RST));
  Register #(.width(2)) register_29 (.D(\状态机_5_next ), .en(en4), .Q(s5), .clk(CLK), .clr(RST));
  Register #(.width(2)) register_30 (.D(\状态机_6_next ), .en(en5), .Q(s6), .clk(CLK), .clr(RST));
  Register #(.width(2)) register_31 (.D(\状态机_7_next ), .en(en6), .Q(s7), .clk(CLK), .clr(RST));
  Register #(.width(2)) register_32 (.D(\状态机_8_next ), .en(en7), .Q(s8), .clk(CLK), .clr(RST));
  Multiplexer #(.width(32), .enable("false")) multiplexer_6 (
    .in0(adder_1_out), .in1({32{1'b0}}), .out(multiplexer_6_out), .sel(en0));
  Multiplexer #(.width(32), .enable("false")) multiplexer_7 (
    .in0(adder_2_out), .in1({32{1'b0}}), .out(multiplexer_7_out), .sel(en1));
  Multiplexer #(.width(32), .enable("false")) multiplexer_8 (
    .in0(adder_3_out), .in1({32{1'b0}}), .out(multiplexer_8_out), .sel(en2));
  Multiplexer #(.width(32), .enable("false")) multiplexer_9 (
    .in0(adder_4_out), .in1({32{1'b0}}), .out(multiplexer_9_out), .sel(en3));
  Multiplexer #(.width(32), .enable("false")) multiplexer_10 (
    .in0(adder_5_out), .in1({32{1'b0}}), .out(multiplexer_10_out), .sel(en4));
  Multiplexer #(.width(32), .enable("false")) multiplexer_11 (
    .in0(adder_6_out), .in1({32{1'b0}}), .out(multiplexer_11_out), .sel(en5));
  Multiplexer #(.width(32), .enable("false")) multiplexer_12 (
    .in0(adder_7_out), .in1({32{1'b0}}), .out(multiplexer_12_out), .sel(en6));
  Multiplexer #(.width(32), .enable("false")) multiplexer_13 (
    .in0(adder_8_out), .in1({32{1'b0}}), .out(multiplexer_13_out), .sel(en7));
  Register #(.width(32)) register_33 (.D(multiplexer_6_out), .en(jb_3), .Q(register_33_q), .clk(CLK), .clr(RST));
  Register #(.width(32)) register_34 (.D(multiplexer_7_out), .en(jb_3), .Q(register_34_q), .clk(CLK), .clr(RST));
  Register #(.width(32)) register_35 (.D(multiplexer_8_out), .en(jb_3), .Q(register_35_q), .clk(CLK), .clr(RST));
  Register #(.width(32)) register_36 (.D(multiplexer_9_out), .en(jb_3), .Q(register_36_q), .clk(CLK), .clr(RST));
  Register #(.width(32)) register_37 (.D(multiplexer_10_out), .en(jb_3), .Q(register_37_q), .clk(CLK), .clr(RST));
  Register #(.width(32)) register_38 (.D(multiplexer_11_out), .en(jb_3), .Q(register_38_q), .clk(CLK), .clr(RST));
  Register #(.width(32)) register_39 (.D(multiplexer_12_out), .en(jb_3), .Q(register_39_q), .clk(CLK), .clr(RST));
  Register #(.width(32)) register_40 (.D(multiplexer_13_out), .en(jb_3), .Q(register_40_q), .clk(CLK), .clr(RST));
  Adder #(.width(32)) adder_1 (.a(32'h1), .b(register_33_q), .out(adder_1_out));  // open: cin, cout
  Adder #(.width(32)) adder_2 (.a(32'h1), .b(register_34_q), .out(adder_2_out));  // open: cin, cout
  Adder #(.width(32)) adder_3 (.a(32'h1), .b(register_35_q), .out(adder_3_out));  // open: cin, cout
  Adder #(.width(32)) adder_4 (.a(32'h1), .b(register_36_q), .out(adder_4_out));  // open: cin, cout
  Adder #(.width(32)) adder_5 (.a(32'h1), .b(register_37_q), .out(adder_5_out));  // open: cin, cout
  Adder #(.width(32)) adder_6 (.a(32'h1), .b(register_38_q), .out(adder_6_out));  // open: cin, cout
  Adder #(.width(32)) adder_7 (.a(32'h1), .b(register_39_q), .out(adder_7_out));  // open: cin, cout
  Adder #(.width(32)) adder_8 (.a(32'h1), .b(register_40_q), .out(adder_8_out));  // open: cin, cout
  MAX max_1 (
    ._000(register_33_q), ._001(register_34_q), ._010(register_35_q), ._011(register_36_q),
    ._100(register_37_q), ._101(register_38_q), ._110(register_39_q), ._111(register_40_q), .\最大数 (LRU_MAX),
    .\最大编号 (MAX_index));

  // Notes on the sheet:
  //   valid
  //   指令addr
  //   目标addr
  //   预测历史
  //   LRU
endmodule

module MAX (
  input  [31:0] _000,
  input  [31:0] _001,
  input  [31:0] _010,
  input  [31:0] _011,
  input  [31:0] _100,
  input  [31:0] _101,
  input  [31:0] _110,
  input  [31:0] _111,
  output [31:0] \最大数 ,
  output [2:0] \最大编号 
);

  wire comparator_1_lt, comparator_2_lt, comparator_3_lt, comparator_4_lt, comparator_5_lt, comparator_6_lt,
       comparator_7_lt;
  wire [2:0] multiplexer_2_out, multiplexer_4_out, multiplexer_6_out, multiplexer_8_out, multiplexer_10_out,
       multiplexer_12_out;
  wire [31:0] multiplexer_1_out, multiplexer_3_out, multiplexer_5_out, multiplexer_7_out, multiplexer_9_out,
       multiplexer_11_out;

  Comparator #(.width(32)) comparator_1 (.a(_000), .b(_001), .lt(comparator_1_lt));  // open: gt, eq
  Comparator #(.width(32)) comparator_2 (.a(_010), .b(_011), .lt(comparator_2_lt));  // open: gt, eq
  Comparator #(.width(32)) comparator_3 (.a(_100), .b(_101), .lt(comparator_3_lt));  // open: gt, eq
  Comparator #(.width(32)) comparator_4 (.a(_110), .b(_111), .lt(comparator_4_lt));  // open: gt, eq
  Multiplexer #(.width(32), .enable("false")) multiplexer_1 (
    .in0(_000), .in1(_001), .out(multiplexer_1_out), .sel(comparator_1_lt));
  Multiplexer #(.width(3), .enable("false")) multiplexer_2 (
    .in0(3'b000), .in1(3'b001), .out(multiplexer_2_out), .sel(comparator_1_lt));
  Multiplexer #(.width(32), .enable("false")) multiplexer_3 (
    .in0(_010), .in1(_011), .out(multiplexer_3_out), .sel(comparator_2_lt));
  Multiplexer #(.width(3), .enable("false")) multiplexer_4 (
    .in0(3'b010), .in1(3'b011), .out(multiplexer_4_out), .sel(comparator_2_lt));
  Multiplexer #(.width(32), .enable("false")) multiplexer_5 (
    .in0(_100), .in1(_101), .out(multiplexer_5_out), .sel(comparator_3_lt));
  Multiplexer #(.width(3), .enable("false")) multiplexer_6 (
    .in0(3'b100), .in1(3'b101), .out(multiplexer_6_out), .sel(comparator_3_lt));
  Multiplexer #(.width(32), .enable("false")) multiplexer_7 (
    .in0(_110), .in1(_111), .out(multiplexer_7_out), .sel(comparator_4_lt));
  Multiplexer #(.width(3), .enable("false")) multiplexer_8 (
    .in0(3'b110), .in1(3'b111), .out(multiplexer_8_out), .sel(comparator_4_lt));
  Comparator #(.width(32)) comparator_5 (
    .a(multiplexer_1_out), .b(multiplexer_3_out), .lt(comparator_5_lt));  // open: gt, eq
  Comparator #(.width(32)) comparator_6 (
    .a(multiplexer_5_out), .b(multiplexer_7_out), .lt(comparator_6_lt));  // open: gt, eq
  Multiplexer #(.width(32), .enable("false")) multiplexer_9 (
    .in0(multiplexer_1_out), .in1(multiplexer_3_out), .out(multiplexer_9_out), .sel(comparator_5_lt));
  Multiplexer #(.width(3), .enable("false")) multiplexer_10 (
    .in0(multiplexer_2_out), .in1(multiplexer_4_out), .out(multiplexer_10_out), .sel(comparator_5_lt));
  Multiplexer #(.width(32), .enable("false")) multiplexer_11 (
    .in0(multiplexer_5_out), .in1(multiplexer_7_out), .out(multiplexer_11_out), .sel(comparator_6_lt));
  Multiplexer #(.width(3), .enable("false")) multiplexer_12 (
    .in0(multiplexer_6_out), .in1(multiplexer_8_out), .out(multiplexer_12_out), .sel(comparator_6_lt));
  Comparator #(.width(32)) comparator_7 (
    .a(multiplexer_9_out), .b(multiplexer_11_out), .lt(comparator_7_lt));  // open: gt, eq
  Multiplexer #(.width(32), .enable("false")) multiplexer_13 (
    .in0(multiplexer_9_out), .in1(multiplexer_11_out), .out(\最大数 ), .sel(comparator_7_lt));
  Multiplexer #(.width(3), .enable("false")) multiplexer_14 (
    .in0(multiplexer_10_out), .in1(multiplexer_12_out), .out(\最大编号 ), .sel(comparator_7_lt));
endmodule

module branch_jump (
  input  [31:0] Reg1_3,
  input  Beq_3,
  input  Bne_3,
  input  Bgtz_3,
  input  equal,
  input  j_3,
  output Branch,
  output jump_suc,
  output jb_3
);

  wire and_1_out, and_2_out, and_3_out, comparator_1_gt, or_4_out;

  Comparator #(.width(32)) comparator_1 (.a(Reg1_3), .b({32{1'b0}}), .gt(comparator_1_gt));  // open: eq, lt
  and and_1 (and_1_out, comparator_1_gt, Bgtz_3);
  and and_2 (and_2_out, Beq_3, equal);
  and and_3 (and_3_out, Bne_3, ~equal);  // AND_Gate
  or or_1 (jump_suc, j_3, Branch);
  or or_2 (jb_3, j_3, Beq_3, Bne_3, Bgtz_3);
  or or_3 (Branch, and_1_out, or_4_out);
  or or_4 (or_4_out, and_2_out, and_3_out);
endmodule

module status (
  input  [1:0] status,
  input  jump,
  output [1:0] next_status
);

  wire and_1_out, and_2_out, and_3_out;

  and and_1 (and_1_out, status[0], jump);
  and and_2 (and_2_out, status[1], jump);
  and and_3 (and_3_out, status[1], status[0]);
  or or_1 (next_status[1], and_1_out, and_2_out, and_3_out);

  assign next_status[0] = jump;
endmodule

module \状态机  (
  input  [1:0] status,
  input  [1:0] hit_jump,
  output [1:0] next
);

  wire [1:0] status_1_next_status, status_2_next_status;

  status status_1 (.status(status), .jump(1'b0), .next_status(status_1_next_status));
  status status_2 (.status(status), .jump(1'b1), .next_status(status_2_next_status));
  Multiplexer #(.select(2), .width(2), .enable("false")) multiplexer_1 (
    .in0(2'b01), .in1(2'b10), .in2(status_1_next_status), .in3(status_2_next_status), .out(next),
    .sel(hit_jump));
endmodule

module \分支预测PCout  (
  input  [31:0] PC_4,
  input  [25:0] Imm26,
  input  [31:0] Imm32,
  input  [31:0] Reg1,
  input  JMP,
  input  JR,
  input  JAL,
  input  Branch,
  input  [31:0] PC_4_3,
  input  jump_suc,
  input  jb_3,
  input  hit_3,
  input  hit,
  input  [31:0] pc_att,
  input  jump_att,
  input  jump_att_3,
  output [31:0] PCout,
  output att_fail,
  output att_suc,
  output [31:0] dest_attr
);

  wire and_2_out, and_3_out, and_4_out, comparator_1_eq, not_1_out, not_2_out;
  wire [31:0] adder_1_out, bit_extender_1_out, multiplexer_1_out, multiplexer_3_out, multiplexer_4_out,
       multiplexer_5_out, shifter_1_out, shifter_2_out;

  Comparator #(.width(1)) comparator_1 (.a(jump_att_3), .b(jump_suc), .eq(comparator_1_eq));  // open: gt, lt
  and and_1 (att_suc, comparator_1_eq, hit_3);
  assign bit_extender_1_out = {{6{1'b0}}, Imm26};  // Bit_Extender bit_extender_1
  not not_1 (not_1_out, comparator_1_eq);
  Shifter #(.width(32)) shifter_1 (.in(Imm32), .\dist (5'b00010), .out(shifter_1_out));
  Shifter #(.width(32)) shifter_2 (.in(bit_extender_1_out), .\dist (5'b00010), .out(shifter_2_out));
  and and_2 (and_2_out, hit_3, not_1_out);
  not not_2 (not_2_out, hit_3);
  Adder #(.width(32)) adder_1 (.a(PC_4_3), .b(shifter_1_out), .out(adder_1_out));  // open: cin, cout
  or or_1 (att_fail, and_2_out, and_3_out);
  and and_3 (and_3_out, jump_suc, not_2_out);
  Multiplexer #(.width(32), .enable("false")) multiplexer_1 (
    .in0(PC_4), .in1(adder_1_out), .out(multiplexer_1_out), .sel(Branch));
  Multiplexer #(.width(32), .enable("false")) multiplexer_2 (
    .in0(multiplexer_1_out), .in1(multiplexer_3_out), .out(dest_attr), .sel(JMP));
  Multiplexer #(.select(2), .width(32), .enable("false")) multiplexer_3 (
    .in0({PC_4_3[31:28], shifter_2_out[27:0]}), .in1(Reg1), .in2({PC_4_3[31:28], shifter_2_out[27:0]}),
    .out(multiplexer_3_out), .sel({JAL, JR}));  // open: in3
  Multiplexer #(.width(32), .enable("false")) multiplexer_4 (
    .in0(PC_4_3), .in1(dest_attr), .out(multiplexer_4_out), .sel(jump_suc));
  and and_4 (and_4_out, hit, jump_att);
  Multiplexer #(.width(32), .enable("false")) multiplexer_5 (
    .in0(PC_4), .in1(pc_att), .out(multiplexer_5_out), .sel(and_4_out));
  Multiplexer #(.width(32), .enable("false")) multiplexer_6 (
    .in0(multiplexer_5_out), .in1(multiplexer_4_out), .out(PCout), .sel(att_fail));
endmodule
